// Logisim project ComplementadorDeSinal.circ as structural Verilog: 1 circuit, main circuit ComplementadorSinal
module ComplementadorSinal (
  input  ZeroExtend,
  input  [15:0] address16,
  output [31:0] address32ext
);

  wire [31:0] bit_extender_1_out, bit_extender_2_out;

  assign bit_extender_1_out = {{16{address16[15]}}, address16};  // Bit_Extender bit_extender_1
  assign bit_extender_2_out = {{16{1'b0}}, address16};  // Bit_Extender bit_extender_2
  Multiplexer #(.width(32)) multiplexer_1 (
    .in0(bit_extender_1_out), .in1(bit_extender_2_out), .out(address32ext), .sel(ZeroExtend));
endmodule
