// Logisim project Contadores.circ as structural Verilog: 2 circuits, main circuit Contador
module Contador (
  input  clkSignal,
  input  reset,
  output [31:0] NumeroDeCiclos
);

  wire [31:0] adder_1_out;

  Register #(.width(32)) register_1 (.D(adder_1_out), .en(clkSignal), .clk(clkSignal), .Q(NumeroDeCiclos), .clr(reset));
  Adder #(.width(32)) adder_1 (.a(NumeroDeCiclos), .b(32'h1), .out(adder_1_out));  // open: cin, cout
endmodule

module Contador_Condicional (
  input  enable,
  input  clkSignalCond,
  input  resetCond,
  output [31:0] NumeroDeCiclosCond
);

  wire [31:0] adder_1_out;

  Register #(.width(32)) register_1 (
    .D(adder_1_out), .en(enable), .clk(clkSignalCond), .Q(NumeroDeCiclosCond), .clr(resetCond));
  Adder #(.width(32)) adder_1 (.a(NumeroDeCiclosCond), .b(32'h1), .out(adder_1_out));  // open: cin, cout
endmodule
