// Logisim project HazardAndForwarding.circ as structural Verilog: 3 circuits, main circuit HazardForwardingUnit
module HazardForwardingUnit (
  input  IsToBranchOrJump,
  input  clk,
  input  ReadRs,
  input  ReadRt,
  input  isRegWriteEX,
  input  isRegWriteMEM,
  input  [4:0] RS,
  input  [4:0] RT,
  input  IsLW,
  input  [4:0] WriteRegEX,
  input  [4:0] WriteRegMEM,
  output FlushIF,
  output [1:0] RsOutput,
  output FlushID,
  output StallIF,
  output StallID,
  output [1:0] RtOutput
);

  wire d_ff_1_q, d_ff_2_q, detectordehazard_1_hazard, detectordehazard_2_hazard, detectordehazard_3_hazard,
       detectordehazard_4_hazard, not_1_out, or_1_out;
  wire [1:0] multiplexer_1_out, multiplexer_2_out;

  // Probe on RsOutput
  // Probe on RtOutput
  // Probe on StallID
  // Probe on StallID
  // Probe on FlushIF
  // Probe on FlushID
  DetectorDeHazard detectordehazard_1 (
    .regEscrito(WriteRegMEM), .regAcessado(RS), .Read(ReadRs), .RegWrite(isRegWriteMEM),
    .Hazard(detectordehazard_1_hazard));
  DetectorDeHazard detectordehazard_2 (
    .regEscrito(WriteRegEX), .regAcessado(RS), .Read(ReadRs), .RegWrite(isRegWriteEX),
    .Hazard(detectordehazard_2_hazard));
  DetectorDeHazard detectordehazard_3 (
    .regEscrito(WriteRegMEM), .regAcessado(RT), .Read(ReadRt), .RegWrite(isRegWriteMEM),
    .Hazard(detectordehazard_3_hazard));
  DetectorDeHazard detectordehazard_4 (
    .regEscrito(WriteRegEX), .regAcessado(RT), .Read(ReadRt), .RegWrite(isRegWriteEX),
    .Hazard(detectordehazard_4_hazard));
  Multiplexer #(.disabled("Z"), .width(2)) multiplexer_1 (
    .in0(2'b00), .in1(2'b10), .out(multiplexer_1_out), .sel(detectordehazard_1_hazard));
  Multiplexer #(.disabled("Z"), .width(2)) multiplexer_2 (
    .in0(2'b00), .in1(2'b10), .out(multiplexer_2_out), .sel(detectordehazard_3_hazard));
  Multiplexer #(.width(2)) multiplexer_3 (
    .in0(multiplexer_1_out), .in1(2'b01), .out(RsOutput), .sel(detectordehazard_2_hazard));
  Multiplexer #(.width(2)) multiplexer_4 (
    .in0(multiplexer_2_out), .in1(2'b01), .out(RtOutput), .sel(detectordehazard_4_hazard));
  or or_1 (or_1_out, detectordehazard_2_hazard, detectordehazard_4_hazard);
  and and_1 (StallID, IsLW, or_1_out);
  not not_1 (not_1_out, clk);
  D_Flip_Flop #(.trigger("falling")) d_ff_1 (.D(IsToBranchOrJump), .clk(clk), .Q(d_ff_1_q));  // open: Qn, preset, reset
  D_Flip_Flop #(.trigger("falling")) d_ff_2 (.D(StallID), .clk(clk), .Q(d_ff_2_q));  // open: Qn, preset, reset
  and and_2 (FlushIF, not_1_out, d_ff_1_q);
  and and_3 (FlushID, clk, d_ff_2_q);

  assign StallIF = StallID;

  // Other names for the same wires on the sheet: Tclk = clk; TFlushID = FlushID; TFlushIF = FlushIF;
  //   TisRegWriteEX = isRegWriteEX; TisRegWriteMEM = isRegWriteMEM; TReadRs = ReadRs; TReadRt = ReadRt; TRS[4:0] = RS;
  //   TRsOutput[1:0] = RsOutput; TRT[4:0] = RT; TRtOutput[1:0] = RtOutput; TStallID = StallID; TStallIF = StallID;
  //   TWriteRegEX[4:0] = WriteRegEX; TWriteRegMEM[4:0] = WriteRegMEM

  // Notes on the sheet:
  //   Rs Hazard in MEM
  //   Rs Hazard in EX
  //   Rt Hazard in MEM
  //   Rt Hazard in EX
  //   hasHazard
endmodule

module DetectorDeHazard (
  input  Read,
  input  RegWrite,
  input  [4:0] regEscrito,
  input  [4:0] regAcessado,
  output Hazard
);

  wire comparator_1_eq, comparator_2_eq, not_1_out;

  Comparator #(.width(5)) comparator_1 (.a({5{1'b0}}), .b(regEscrito), .eq(comparator_1_eq));  // open: gt, lt
  Comparator #(.width(5)) comparator_2 (.a(regEscrito), .b(regAcessado), .eq(comparator_2_eq));  // open: gt, lt
  not not_1 (not_1_out, comparator_1_eq);
  and and_1 (Hazard, Read, RegWrite, not_1_out, comparator_2_eq);
endmodule

module HazardUnit (
  input  clk_hazard,
  input  isToBranchOrJump_hazard,
  input  readRs_hazard,
  input  readRt_hazard,
  input  isRegWriteMEM_hazard,
  input  [4:0] RT_hazard,
  input  [4:0] RS_hazard,
  input  [4:0] WriteRegMEM_hazard,
  input  isRegWriteEX_hazard,
  input  [4:0] WirteRegEX_hazard,
  output FlushIF_hazard,
  output FlushID_hazard,
  output StallIF_hazard,
  output StallID_hazard
);

  wire and_1_out, and_2_out, and_3_out, and_4_out, and_5_out, and_6_out, and_7_out, and_8_out,
       comparator_1_eq, comparator_2_eq, comparator_3_eq, comparator_4_eq, comparator_5_eq, comparator_6_eq,
       d_ff_1_q, d_ff_2_q, not_1_out, not_2_out, not_3_out, or_1_out, or_2_out;

  Comparator #(.width(5)) comparator_1 (.a({5{1'b0}}), .b(WriteRegMEM_hazard), .eq(comparator_1_eq));  // open: gt, lt
  Comparator #(.width(5)) comparator_2 (.a(WriteRegMEM_hazard), .b(RT_hazard), .eq(comparator_2_eq));  // open: gt, lt
  Comparator #(.width(5)) comparator_3 (.a(WriteRegMEM_hazard), .b(RS_hazard), .eq(comparator_3_eq));  // open: gt, lt
  Comparator #(.width(5)) comparator_4 (.a({5{1'b0}}), .b(WirteRegEX_hazard), .eq(comparator_4_eq));  // open: gt, lt
  Comparator #(.width(5)) comparator_5 (.a(WirteRegEX_hazard), .b(RT_hazard), .eq(comparator_5_eq));  // open: gt, lt
  Comparator #(.width(5)) comparator_6 (.a(WirteRegEX_hazard), .b(RS_hazard), .eq(comparator_6_eq));  // open: gt, lt
  not not_1 (not_1_out, comparator_1_eq);
  not not_2 (not_2_out, comparator_4_eq);
  and and_1 (and_1_out, comparator_2_eq, readRt_hazard);
  and and_2 (and_2_out, comparator_3_eq, readRs_hazard);
  and and_3 (and_3_out, comparator_5_eq, readRt_hazard);
  and and_4 (and_4_out, comparator_6_eq, readRs_hazard);
  or or_1 (or_1_out, and_1_out, and_2_out);
  or or_2 (or_2_out, and_3_out, and_4_out);
  and and_5 (and_5_out, not_1_out, or_1_out);
  and and_6 (and_6_out, not_2_out, or_2_out);
  and and_7 (and_7_out, isRegWriteMEM_hazard, and_5_out);
  and and_8 (and_8_out, isRegWriteEX_hazard, and_6_out);
  or or_3 (StallID_hazard, and_7_out, and_8_out);
  D_Flip_Flop #(.trigger("falling")) d_ff_1 (
    .D(isToBranchOrJump_hazard), .clk(clk_hazard), .Q(d_ff_1_q));  // open: Qn, preset, reset
  not not_3 (not_3_out, clk_hazard);
  D_Flip_Flop #(.trigger("falling")) d_ff_2 (
    .D(StallID_hazard), .clk(clk_hazard), .Q(d_ff_2_q));  // open: Qn, preset, reset
  and and_9 (FlushIF_hazard, not_3_out, d_ff_1_q);
  and and_10 (FlushID_hazard, clk_hazard, d_ff_2_q);

  assign StallIF_hazard = StallID_hazard;

  // Other names for the same wires on the sheet: Tclk_hazard = clk_hazard
endmodule
