// Logisim project InstDecoder.circ as structural Verilog: 1 circuit, main circuit InstructionDecoder
module InstructionDecoder (
  input  [31:0] Instruction,
  output [5:0] op,
  output [4:0] rs,
  output [4:0] rt,
  output [4:0] rd,
  output [4:0] shamt,
  output [5:0] funct,
  output [15:0] immediate,
  output [25:0] adderess
);


  assign adderess = Instruction[25:0];
  assign funct = Instruction[5:0];
  assign immediate = Instruction[15:0];
  assign op = Instruction[31:26];
  assign rd = Instruction[15:11];
  assign rs = Instruction[25:21];
  assign rt = Instruction[20:16];
  assign shamt = Instruction[10:6];

  // Notes on the sheet:
  //   R-Type
  //   I-Type
  //   J-Type
  //   OP
  //   OP
  //   OP
  //   RS
  //   RS
  //   J-Type
  //   RT
  //   RT
  //   I-Type
  //   RD
  //   Target Address
  //   R-Type
  //   Shamt
  //   Address/Immediate
  //   Funct
endmodule
