// Logisim project InterStageRegisters.circ as structural Verilog: 4 circuits, main circuit IF_ID
module ID_EX (
  input  clk_ID_EX,
  input  clr_ID_EX,
  input  [31:0] Imm_ID,
  input  [31:0] Sham_ID,
  input  isSham_ID,
  input  ALUSrc_ID,
  input  Branch_ID,
  input  isJAL_ID,
  input  MemToReg_ID,
  input  MemRead_ID,
  input  is_JR_ID,
  input  [31:0] R1_ID,
  input  [31:0] JumpAddr_ID,
  input  RegWrite_ID,
  input  MemWrite_ID,
  input  [3:0] ALUOp_ID,
  input  [31:0] R2_ID,
  input  [31:0] PCPlus4_ID,
  input  BneOrBeq_ID,
  input  isJump_ID,
  input  [4:0] WriteReg_ID,
  input  enable_id_ex,
  output [31:0] Imm_EX,
  output [31:0] Sham_EX,
  output isSham_EX,
  output ALUSrc_EX,
  output Branch_EX,
  output isJAL_EX,
  output MemToReg_EX,
  output MemRead_EX,
  output isJR_EX,
  output [31:0] R1_EX,
  output [31:0] JumpAddr_EX,
  output RegWrite_EX,
  output MemWrite_EX,
  output [3:0] ALUOp_EX,
  output [31:0] R2_EX,
  output [31:0] PCPus4_EX,
  output BneOrBeq_EX,
  output isJump_EX,
  output [4:0] WriteReg_EX
);

  Register #(.width(32)) regImm_ID_EX (.D(Imm_ID), .en(enable_id_ex), .clk(clk_ID_EX), .Q(Imm_EX), .clr(clr_ID_EX));
  Register #(.width(32)) regR1_ID_EX (.D(R1_ID), .en(enable_id_ex), .clk(clk_ID_EX), .Q(R1_EX), .clr(clr_ID_EX));
  Register #(.width(32)) regR2_ID_EX (.D(R2_ID), .en(enable_id_ex), .clk(clk_ID_EX), .Q(R2_EX), .clr(clr_ID_EX));
  Register #(.width(32)) regSham_ID_EX (.D(Sham_ID), .en(enable_id_ex), .clk(clk_ID_EX), .Q(Sham_EX), .clr(clr_ID_EX));
  Register #(.width(32)) regJump_ID_EX (
    .D(JumpAddr_ID), .en(enable_id_ex), .clk(clk_ID_EX), .Q(JumpAddr_EX), .clr(clr_ID_EX));
  Register #(.width(32)) regPCPlus4_ID_EX (
    .D(PCPlus4_ID), .en(enable_id_ex), .clk(clk_ID_EX), .Q(PCPus4_EX), .clr(clr_ID_EX));
  Register #(.width(1)) regIsSham_ID_EX (
    .D(isSham_ID), .en(enable_id_ex), .clk(clk_ID_EX), .Q(isSham_EX), .clr(clr_ID_EX));
  Register #(.width(1)) regMemToReg_ID_EX (
    .D(MemToReg_ID), .en(enable_id_ex), .clk(clk_ID_EX), .Q(MemToReg_EX), .clr(clr_ID_EX));
  Register #(.width(1)) regRegWrite_ID_EX (
    .D(RegWrite_ID), .en(enable_id_ex), .clk(clk_ID_EX), .Q(RegWrite_EX), .clr(clr_ID_EX));
  Register #(.width(1)) regBneOrBeq_ID_EX (
    .D(BneOrBeq_ID), .en(enable_id_ex), .clk(clk_ID_EX), .Q(BneOrBeq_EX), .clr(clr_ID_EX));
  Register #(.width(1)) regALUSrc_ID_EX (
    .D(ALUSrc_ID), .en(enable_id_ex), .clk(clk_ID_EX), .Q(ALUSrc_EX), .clr(clr_ID_EX));
  Register #(.width(1)) regMemRead_ID_EX (
    .D(MemRead_ID), .en(enable_id_ex), .clk(clk_ID_EX), .Q(MemRead_EX), .clr(clr_ID_EX));
  Register #(.width(1)) regMemWrite_ID_EX (
    .D(MemWrite_ID), .en(enable_id_ex), .clk(clk_ID_EX), .Q(MemWrite_EX), .clr(clr_ID_EX));
  Register #(.width(1)) regIsJump_ID_EX (
    .D(isJump_ID), .en(enable_id_ex), .clk(clk_ID_EX), .Q(isJump_EX), .clr(clr_ID_EX));
  Register #(.width(1)) regBranch_ID_EX (
    .D(Branch_ID), .en(enable_id_ex), .clk(clk_ID_EX), .Q(Branch_EX), .clr(clr_ID_EX));
  Register #(.width(1)) regIsJR_ID_EX (.D(is_JR_ID), .en(enable_id_ex), .clk(clk_ID_EX), .Q(isJR_EX), .clr(clr_ID_EX));
  Register #(.width(4)) regALUOp_ID_EX (
    .D(ALUOp_ID), .en(enable_id_ex), .clk(clk_ID_EX), .Q(ALUOp_EX), .clr(clr_ID_EX));
  Register #(.width(5)) regWriteReg_ID_EX (
    .D(WriteReg_ID), .en(enable_id_ex), .clk(clk_ID_EX), .Q(WriteReg_EX), .clr(clr_ID_EX));
  Register #(.width(1)) regIsJAL_ID_EX (
    .D(isJAL_ID), .en(enable_id_ex), .clk(clk_ID_EX), .Q(isJAL_EX), .clr(clr_ID_EX));

  // Notes on the sheet:
  //   CLR
  //   CLK
endmodule

module IF_ID (
  input  clk_if_id,
  input  clr_if_id,
  input  [31:0] Instruction_IF,
  input  [31:0] PCPlus4_IF,
  input  Enable_if_id,
  output [31:0] Instruction_ID,
  output [31:0] PCPus4_ID
);

  Register #(.width(32)) regInst_ID_IF (
    .D(Instruction_IF), .en(Enable_if_id), .clk(clk_if_id), .Q(Instruction_ID), .clr(clr_if_id));
  Register #(.width(32)) regPC_ID_IF (
    .D(PCPlus4_IF), .en(Enable_if_id), .clk(clk_if_id), .Q(PCPus4_ID), .clr(clr_if_id));
endmodule

module EX_MEM (
  input  clk_EX_MEM,
  input  clr_EX_MEM,
  input  MemToReg_Ex,
  input  [31:0] ALU_Result_EX,
  input  RegWrite_Ex,
  input  [31:0] WriteData_EX,
  input  MemRead_Ex,
  input  [31:0] JumpAddr_EX,
  input  MemWrite_EX,
  input  isJAL_EX,
  input  [4:0] WriteReg_EX,
  input  Enable_EX_MEM,
  output MemToReg_MEM,
  output [31:0] ALUResult_MEM,
  output RegWrite_MEM,
  output [31:0] WriteData_MEM,
  output MemRead_MEM,
  output [31:0] JumpAddr_MEM,
  output MemWrite_MEM,
  output isJAL_MEM,
  output [4:0] WriteReg_MEM
);

  Register #(.width(1)) regMemToReg_EX_MEM (
    .D(MemToReg_Ex), .en(Enable_EX_MEM), .clk(clk_EX_MEM), .Q(MemToReg_MEM), .clr(clr_EX_MEM));
  Register #(.width(1)) regRegWrite_EX_MEM (
    .D(RegWrite_Ex), .en(Enable_EX_MEM), .clk(clk_EX_MEM), .Q(RegWrite_MEM), .clr(clr_EX_MEM));
  Register #(.width(1)) MemRead_EX_MEM (
    .D(MemRead_Ex), .en(Enable_EX_MEM), .clk(clk_EX_MEM), .Q(MemRead_MEM), .clr(clr_EX_MEM));
  Register #(.width(1)) MemWrite_EX_MEM (
    .D(MemWrite_EX), .en(Enable_EX_MEM), .clk(clk_EX_MEM), .Q(MemWrite_MEM), .clr(clr_EX_MEM));
  Register #(.width(5)) WriteReg_EX_MEM (
    .D(WriteReg_EX), .en(Enable_EX_MEM), .clk(clk_EX_MEM), .Q(WriteReg_MEM), .clr(clr_EX_MEM));
  Register #(.width(32)) regALUResult (
    .D(ALU_Result_EX), .en(Enable_EX_MEM), .clk(clk_EX_MEM), .Q(ALUResult_MEM), .clr(clr_EX_MEM));
  Register #(.width(32)) regWriteData (
    .D(WriteData_EX), .en(Enable_EX_MEM), .clk(clk_EX_MEM), .Q(WriteData_MEM), .clr(clr_EX_MEM));
  Register #(.width(32)) regJumpAddr (
    .D(JumpAddr_EX), .en(Enable_EX_MEM), .clk(clk_EX_MEM), .Q(JumpAddr_MEM), .clr(clr_EX_MEM));
  Register #(.width(1)) TisJAL_EX_MEM (
    .D(isJAL_EX), .en(Enable_EX_MEM), .clk(clk_EX_MEM), .Q(isJAL_MEM), .clr(clr_EX_MEM));
endmodule

module MEM_WB (
  input  clk_mem_wb,
  input  clr_mem_wb,
  input  [31:0] ALUResult_mem,
  input  memToReg_mem,
  input  regWrite_mem,
  input  [31:0] ReadData_mem,
  input  [4:0] writeReg_mem,
  input  [31:0] JumpAddr_MEM,
  input  isJALMEM,
  input  enable_mem_wb,
  output [31:0] ALUResult_wb,
  output memToReg_wb,
  output regWrite_wb,
  output [31:0] ReadData_wb,
  output [4:0] writeReg_wb,
  output [31:0] JumpAddr_wb,
  output isJALWB
);

  Register #(.width(1)) regMemToReg (
    .D(memToReg_mem), .en(enable_mem_wb), .clk(clk_mem_wb), .Q(memToReg_wb), .clr(clr_mem_wb));
  Register #(.width(1)) regRegWrite (
    .D(regWrite_mem), .en(enable_mem_wb), .clk(clk_mem_wb), .Q(regWrite_wb), .clr(clr_mem_wb));
  Register #(.width(5)) regWriteReg (
    .D(writeReg_mem), .en(enable_mem_wb), .clk(clk_mem_wb), .Q(writeReg_wb), .clr(clr_mem_wb));
  Register #(.width(1)) register_1 (.D(isJALMEM), .en(enable_mem_wb), .clk(clk_mem_wb), .Q(isJALWB), .clr(clr_mem_wb));
  Register #(.width(32)) regALUResult (
    .D(ALUResult_mem), .en(enable_mem_wb), .clk(clk_mem_wb), .Q(ALUResult_wb), .clr(clr_mem_wb));
  Register #(.width(32)) regReadData (
    .D(ReadData_mem), .en(enable_mem_wb), .clk(clk_mem_wb), .Q(ReadData_wb), .clr(clr_mem_wb));
  Register #(.width(32)) regJumAddr (
    .D(JumpAddr_MEM), .en(enable_mem_wb), .clk(clk_mem_wb), .Q(JumpAddr_wb), .clr(clr_mem_wb));
endmodule
