// Logisim project JTB.circ as structural Verilog: 1 circuit, main circuit main
module main (
  input  update,
  input  clear,
  input  clk,
  input  [31:0] pcIn,
  input  [31:0] instruction,
  input  [31:0] newpc,
  input  [31:0] targuet,
  output [31:0] instructionOut,
  output hit,
  output needUpdate
);

  wire and_1_out, and_3_out, comparator_1_eq, comparator_2_eq, d_ff_1_q, demultiplexer_1_out0,
       demultiplexer_1_out1, demultiplexer_1_out2, demultiplexer_1_out3, demultiplexer_1_out4,
       demultiplexer_1_out5, demultiplexer_1_out6, demultiplexer_1_out7, demultiplexer_2_out0,
       demultiplexer_2_out1, demultiplexer_2_out2, demultiplexer_2_out3, demultiplexer_2_out4,
       demultiplexer_2_out5, demultiplexer_2_out6, demultiplexer_2_out7, not_1_out, not_2_out, not_3_out,
       not_4_out, not_5_out, not_6_out, not_7_out;
  wire [31:0] multiplexer_1_out, register_1_q, register_2_q, register_3_q, register_4_q, register_5_q,
       register_6_q, register_7_q, register_8_q, register_9_q, register_10_q, register_11_q, register_12_q,
       register_13_q, register_14_q, register_15_q, register_16_q;

  Register #(.width(32)) register_1 (.D(newpc), .en(demultiplexer_1_out0), .clk(clk), .Q(register_1_q), .clr(clear));
  Register #(.width(32)) register_2 (.D(targuet), .en(demultiplexer_2_out0), .clk(clk), .Q(register_2_q), .clr(clear));
  Register #(.width(32)) register_3 (.D(newpc), .en(demultiplexer_1_out1), .clk(clk), .Q(register_3_q), .clr(clear));
  Register #(.width(32)) register_4 (.D(targuet), .en(demultiplexer_2_out1), .clk(clk), .Q(register_4_q), .clr(clear));
  Register #(.width(32)) register_5 (.D(newpc), .en(demultiplexer_1_out2), .clk(clk), .Q(register_5_q), .clr(clear));
  Register #(.width(32)) register_6 (.D(targuet), .en(demultiplexer_2_out2), .clk(clk), .Q(register_6_q), .clr(clear));
  not not_1 (not_1_out, instruction[26]);
  not not_2 (not_2_out, instruction[28]);
  and and_1 (and_1_out, not_1_out, instruction[27], not_2_out, not_3_out, not_4_out, not_5_out);
  not not_3 (not_3_out, instruction[29]);
  not not_4 (not_4_out, instruction[30]);
  not not_5 (not_5_out, instruction[31]);
  Register #(.width(32)) register_7 (.D(newpc), .en(demultiplexer_1_out3), .clk(clk), .Q(register_7_q), .clr(clear));
  Multiplexer #(.select(3), .width(32)) multiplexer_1 (
    .in0(register_1_q), .in1(register_3_q), .in2(register_5_q), .in3(register_7_q), .in4(register_9_q),
    .in5(register_11_q), .in6(register_13_q), .in7(register_15_q), .out(multiplexer_1_out), .sel(pcIn[4:2]));
  Register #(.width(32)) register_8 (.D(targuet), .en(demultiplexer_2_out3), .clk(clk), .Q(register_8_q), .clr(clear));
  Multiplexer #(.select(3), .width(32)) multiplexer_2 (
    .in0(register_2_q), .in1(register_4_q), .in2(register_6_q), .in3(register_8_q), .in4(register_10_q),
    .in5(register_12_q), .in6(register_14_q), .in7(register_16_q), .out(instructionOut), .sel(pcIn[4:2]));
  Register #(.width(32)) register_9 (.D(newpc), .en(demultiplexer_1_out4), .clk(clk), .Q(register_9_q), .clr(clear));
  Comparator #(.width(32)) comparator_1 (.a({32{1'b0}}), .b(multiplexer_1_out), .eq(comparator_1_eq));  // open: gt, lt
  Comparator #(.width(32)) comparator_2 (.a(multiplexer_1_out), .b(pcIn), .eq(comparator_2_eq));  // open: gt, lt
  Register #(.width(32)) register_10 (
    .D(targuet), .en(demultiplexer_2_out4), .clk(clk), .Q(register_10_q), .clr(clear));
  Register #(.width(32)) register_11 (.D(newpc), .en(demultiplexer_1_out5), .clk(clk), .Q(register_11_q), .clr(clear));
  not not_6 (not_6_out, comparator_1_eq);
  Register #(.width(32)) register_12 (
    .D(targuet), .en(demultiplexer_2_out5), .clk(clk), .Q(register_12_q), .clr(clear));
  and and_2 (hit, not_6_out, comparator_2_eq);
  Register #(.width(32)) register_13 (.D(newpc), .en(demultiplexer_1_out6), .clk(clk), .Q(register_13_q), .clr(clear));
  Register #(.width(32)) register_14 (
    .D(targuet), .en(demultiplexer_2_out6), .clk(clk), .Q(register_14_q), .clr(clear));
  Register #(.width(32)) register_15 (.D(newpc), .en(demultiplexer_1_out7), .clk(clk), .Q(register_15_q), .clr(clear));
  Register #(.width(32)) register_16 (
    .D(targuet), .en(demultiplexer_2_out7), .clk(clk), .Q(register_16_q), .clr(clear));
  Demultiplexer #(.enable("true"), .select(3)) demultiplexer_1 (
    .out0(demultiplexer_1_out0), .out1(demultiplexer_1_out1), .out2(demultiplexer_1_out2),
    .out3(demultiplexer_1_out3), .out4(demultiplexer_1_out4), .out5(demultiplexer_1_out5),
    .out6(demultiplexer_1_out6), .out7(demultiplexer_1_out7), .in(1'b1), .sel(newpc[4:2]), .en(update));
  Demultiplexer #(.enable("true"), .select(3)) demultiplexer_2 (
    .out0(demultiplexer_2_out0), .out1(demultiplexer_2_out1), .out2(demultiplexer_2_out2),
    .out3(demultiplexer_2_out3), .out4(demultiplexer_2_out4), .out5(demultiplexer_2_out5),
    .out6(demultiplexer_2_out6), .out7(demultiplexer_2_out7), .in(1'b1), .sel(newpc[4:2]), .en(update));
  not not_7 (not_7_out, hit);
  and and_3 (and_3_out, not_7_out, and_1_out);
  D_Flip_Flop d_ff_1 (.D(and_3_out), .clk(clk), .Q(d_ff_1_q));  // open: Qn, preset, reset
  and and_4 (needUpdate, and_3_out, ~d_ff_1_q);  // AND_Gate
endmodule
