// Logisim project ULAC.circ as structural Verilog: 3 circuits, main circuit SomadorComOverflowDetection
module SomadorComOverflowDetection (
  input  [31:0] X,
  input  [31:0] Y,
  input  cin,
  output SignedOverflowSum,
  output [31:0] opResult,
  output UnsignedOverflowSum
);

  wire adder_1_cout;

  Adder #(.width(31)) adder_1 (.a(X[30:0]), .b(Y[30:0]), .out(opResult[30:0]), .cin(cin), .cout(adder_1_cout));
  Adder #(.width(1)) adder_2 (.a(X[31]), .b(Y[31]), .out(opResult[31]), .cin(adder_1_cout), .cout(UnsignedOverflowSum));
  xor xor_1 (SignedOverflowSum, adder_1_cout, UnsignedOverflowSum);

  // Other names for the same wires on the sheet: sumResult[31:0] = opResult
endmodule

module SubtratorComOverflowDetection (
  input  [31:0] X,
  input  [31:0] Y,
  input  cin,
  output SignedOverflowSub,
  output [31:0] Resultado,
  output UnsignedOverflowSub
);

  wire subtractor_1_bout;

  Subtractor #(.width(31)) subtractor_1 (
    .a(X[30:0]), .b(Y[30:0]), .out(Resultado[30:0]), .bin(cin), .bout(subtractor_1_bout));
  Subtractor #(.width(1)) subtractor_2 (
    .a(X[31]), .b(Y[31]), .out(Resultado[31]), .bin(subtractor_1_bout), .bout(UnsignedOverflowSub));
  xor xor_1 (SignedOverflowSub, subtractor_1_bout, UnsignedOverflowSub);

  // Other names for the same wires on the sheet: Resultsub[31:0] = Resultado
endmodule

module pALU (
  input  [31:0] X,
  input  [31:0] Y,
  input  [3:0] ALUOp,
  output SignedOverflow,
  output UnsignedOverflow,
  output [31:0] Result1,
  output [31:0] Result2,
  output isEqual
);

  wire comparator_1_lt, comparator_2_lt;
  wire [1:0] somadorcomoverflowdetection_1_signedoverflowsum,
       subtratorcomoverflowdetection_1_signedoverflowsub;
  wire [31:0] and_1_out, bit_extender_1_out, bit_extender_2_out, divider_1_out, divider_1_rem,
       multiplier_1_cout, multiplier_1_out, not_1_out, or_1_out, or_2_out, shifter_1_out, shifter_2_out,
       shifter_3_out, somadorcomoverflowdetection_1_opresult, subtratorcomoverflowdetection_1_resultado,
       xor_1_out;

  Shifter #(.width(32)) shifter_1 (.in(X), .\dist (Y[4:0]), .out(shifter_1_out));
  Shifter #(.shift("ar"), .width(32)) shifter_2 (.in(X), .\dist (Y[4:0]), .out(shifter_2_out));
  Shifter #(.shift("lr"), .width(32)) shifter_3 (.in(X), .\dist (Y[4:0]), .out(shifter_3_out));
  Multiplier #(.width(32)) multiplier_1 (.a(X), .b(Y), .out(multiplier_1_out), .cout(multiplier_1_cout));  // open: cin
  Divider #(.width(32)) divider_1 (.a(X), .b(Y), .out(divider_1_out), .rem(divider_1_rem));  // open: upper
  assign and_1_out = X & Y;  // AND_Gate and_1, 32 bits wide
  assign or_1_out = X | Y;  // OR_Gate or_1, 32 bits wide
  assign xor_1_out = X ^ Y;  // XOR_Gate xor_1, 32 bits wide
  assign or_2_out = X | Y;  // OR_Gate or_2, 32 bits wide
  Comparator #(.width(32)) comparator_1 (.a(X), .b(Y), .lt(comparator_1_lt));  // open: gt, eq
  Comparator #(.width(32)) comparator_2 (.a(X), .b(Y), .eq(isEqual), .lt(comparator_2_lt));  // open: gt
  assign not_1_out = ~or_2_out;  // NOT_Gate not_1, 32 bits wide
  Multiplexer #(.disabled("Z"), .select(4), .width(2)) multiplexer_1 (
    .in0(2'b00), .in1(2'b00), .in2(2'b00), .in3(2'b00), .in4(2'b00),
    .in5(somadorcomoverflowdetection_1_signedoverflowsum),
    .in6(subtratorcomoverflowdetection_1_signedoverflowsub), .in7(2'b00), .in8(2'b00), .in9(2'b00),
    .in10(2'b00), .in11(2'b00), .in12(2'b00), .in13(2'b00), .in14(2'b00), .in15(2'b00),
    .out({UnsignedOverflow, SignedOverflow}), .sel(ALUOp));
  SomadorComOverflowDetection somadorcomoverflowdetection_1 (
    .X(X), .Y(Y), .SignedOverflowSum(somadorcomoverflowdetection_1_signedoverflowsum[0]),
    .opResult(somadorcomoverflowdetection_1_opresult),
    .UnsignedOverflowSum(somadorcomoverflowdetection_1_signedoverflowsum[1]));  // open: cin
  SubtratorComOverflowDetection subtratorcomoverflowdetection_1 (
    .X(X), .Y(Y), .SignedOverflowSub(subtratorcomoverflowdetection_1_signedoverflowsub[0]),
    .Resultado(subtratorcomoverflowdetection_1_resultado),
    .UnsignedOverflowSub(subtratorcomoverflowdetection_1_signedoverflowsub[1]));  // open: cin
  Multiplexer #(.disabled("Z"), .select(4), .width(32)) multiplexer_2 (
    .in0({32{1'b0}}), .in1({32{1'b0}}), .in2({32{1'b0}}), .in3(multiplier_1_cout), .in4(divider_1_rem),
    .in5({32{1'b0}}), .in6({32{1'b0}}), .in7({32{1'b0}}), .in8({32{1'b0}}), .in9({32{1'b0}}),
    .in10({32{1'b0}}), .in11({32{1'b0}}), .in12({32{1'b0}}), .in13({32{1'b0}}), .in14({32{1'b0}}),
    .in15({32{1'b0}}), .out(Result2), .sel(ALUOp));
  assign bit_extender_1_out = {{31{1'b0}}, comparator_1_lt};  // Bit_Extender bit_extender_1
  assign bit_extender_2_out = {{31{1'b0}}, comparator_2_lt};  // Bit_Extender bit_extender_2
  Multiplexer #(.select(4), .width(32)) multiplexer_3 (
    .in0(shifter_1_out), .in1(shifter_2_out), .in2(shifter_3_out), .in3(multiplier_1_out),
    .in4(divider_1_out), .in5(somadorcomoverflowdetection_1_opresult),
    .in6(subtratorcomoverflowdetection_1_resultado), .in7(and_1_out), .in8(or_1_out), .in9(xor_1_out),
    .in10(not_1_out), .in11(bit_extender_1_out), .in12(bit_extender_2_out), .in13({32{1'b0}}),
    .in14({32{1'b0}}), .in15({32{1'b0}}), .out(Result1), .sel(ALUOp));

  // Other names for the same wires on the sheet: SigOverFlow = SignedOverflow; UsgOverflow = UnsignedOverflow;
  //   S[3:0] = ALUOp
endmodule
