// Logisim project controlUnit.circ as structural Verilog: 5 circuits, main circuit RegisterRead
module OpcodeDecoder (
  input  op0,
  input  op1,
  input  op2,
  input  op3,
  input  op4,
  input  op5,
  output MemRead,
  output MemWrite,
  output BneBeq,
  output IsJAL,
  output MemToReg,
  output RegDst,
  output ZeroExtend,
  output Jump,
  output Branch,
  output ALUSrc,
  output RegWrite
);

  wire and_3_out, and_4_out, and_5_out, and_6_out, and_7_out, and_8_out, and_9_out, and_10_out, and_11_out,
       and_12_out, and_14_out, and_15_out, and_17_out, and_18_out, and_19_out, and_20_out, and_21_out,
       and_22_out, and_23_out, and_24_out, and_25_out, and_26_out, and_29_out, and_30_out, not_1_out,
       not_2_out, not_3_out, not_4_out, not_5_out, not_6_out, not_7_out, not_8_out, not_9_out, not_10_out,
       not_11_out, not_12_out, not_13_out, not_14_out, not_15_out, not_16_out, not_17_out, not_18_out,
       not_19_out, not_20_out, not_21_out, not_22_out, not_23_out, not_24_out, not_25_out, not_26_out,
       not_27_out, not_28_out, not_29_out, not_30_out, not_31_out, not_32_out, not_33_out, not_34_out,
       not_35_out, not_36_out, not_37_out, not_38_out, not_39_out, not_40_out, not_41_out, not_42_out,
       not_43_out, not_44_out, not_45_out, not_46_out, not_47_out, not_48_out, not_49_out, not_50_out,
       not_51_out, not_52_out, not_53_out, not_54_out, not_55_out, not_56_out, not_57_out, not_58_out,
       not_59_out, not_60_out, not_61_out, not_62_out, not_63_out, not_64_out, not_65_out, not_66_out,
       not_67_out, not_68_out, not_69_out, not_70_out, not_71_out, not_72_out, not_73_out, not_74_out,
       not_75_out, not_76_out, not_77_out, not_78_out, not_79_out, not_80_out, not_81_out, not_82_out,
       not_83_out, not_84_out, not_85_out, not_86_out, not_87_out, not_88_out, not_89_out, not_90_out,
       not_91_out, not_92_out, not_93_out, not_94_out, not_95_out, not_96_out, not_97_out, not_98_out,
       not_99_out, not_100_out, not_101_out, not_102_out, not_103_out, not_104_out, not_105_out, not_106_out,
       not_107_out, not_108_out, not_109_out, not_110_out, not_111_out, not_112_out, not_113_out,
       not_114_out, not_115_out, not_116_out, not_117_out, not_118_out, not_119_out;

  not not_1 (not_1_out, op1);
  not not_2 (not_2_out, op2);
  not not_3 (not_3_out, op3);
  not not_4 (not_4_out, op1);
  and and_1 (MemRead, op0, not_1_out, not_2_out, not_3_out, op4, op5);
  not not_5 (not_5_out, op3);
  not not_6 (not_6_out, op0);
  and and_2 (MemWrite, op0, not_4_out, op2, not_5_out, op4, op5);
  not not_7 (not_7_out, op1);
  not not_8 (not_8_out, op3);
  not not_9 (not_9_out, op4);
  not not_10 (not_10_out, op5);
  and and_3 (and_3_out, not_6_out, not_7_out, op2, not_8_out, not_9_out, not_10_out);
  not not_11 (not_11_out, op1);
  not not_12 (not_12_out, op2);
  not not_13 (not_13_out, op3);
  and and_4 (and_4_out, op0, not_11_out, not_12_out, not_13_out, op4, op5);
  not not_14 (not_14_out, op1);
  not not_15 (not_15_out, op3);
  and and_5 (and_5_out, op0, not_14_out, op2, not_15_out, op4, op5);
  not not_16 (not_16_out, op0);
  not not_17 (not_17_out, op1);
  not not_18 (not_18_out, op4);
  and and_6 (and_6_out, not_16_out, not_17_out, op2, op3, not_18_out, not_19_out);
  not not_19 (not_19_out, op5);
  not not_20 (not_20_out, op0);
  not not_21 (not_21_out, op1);
  and and_7 (and_7_out, not_20_out, not_21_out, op2, op3, not_22_out, op5);
  or or_1 (ALUSrc, and_3_out, and_4_out, and_5_out, and_6_out, and_7_out, and_8_out, and_9_out, and_10_out);
  not not_22 (not_22_out, op4);
  not not_23 (not_23_out, op0);
  not not_24 (not_24_out, op1);
  and and_8 (and_8_out, not_23_out, not_24_out, op2, not_25_out, op4, not_26_out);
  not not_25 (not_25_out, op3);
  not not_26 (not_26_out, op5);
  not not_27 (not_27_out, op0);
  not not_28 (not_28_out, op1);
  not not_29 (not_29_out, op3);
  not not_30 (not_30_out, op4);
  not not_31 (not_31_out, op0);
  not not_32 (not_32_out, op1);
  and and_9 (and_9_out, not_27_out, not_28_out, op2, not_29_out, not_30_out, op5);
  not not_33 (not_33_out, op5);
  not not_34 (not_34_out, op0);
  not not_35 (not_35_out, op3);
  not not_36 (not_36_out, op4);
  and and_10 (and_10_out, not_31_out, not_32_out, op2, not_35_out, not_36_out, not_33_out);
  not not_37 (not_37_out, op1);
  not not_38 (not_38_out, op2);
  not not_39 (not_39_out, op3);
  not not_40 (not_40_out, op5);
  and and_11 (and_11_out, not_34_out, not_37_out, not_38_out, not_39_out, op4, not_40_out);
  not not_41 (not_41_out, op0);
  not not_42 (not_42_out, op1);
  not not_43 (not_43_out, op2);
  not not_44 (not_44_out, op3);
  and and_12 (and_12_out, not_41_out, not_42_out, not_43_out, not_44_out, op4, op5);
  or or_2 (Jump, and_11_out, and_12_out);
  not not_45 (not_45_out, op1);
  not not_46 (not_46_out, op2);
  not not_47 (not_47_out, op3);
  and and_13 (MemToReg, op0, not_45_out, not_46_out, not_47_out, op4, op5);
  not not_48 (not_48_out, op0);
  not not_49 (not_49_out, op1);
  not not_50 (not_50_out, op2);
  not not_51 (not_51_out, op4);
  and and_14 (and_14_out, not_48_out, not_49_out, not_50_out, op3, not_51_out, op5);
  not not_52 (not_52_out, op0);
  not not_53 (not_53_out, op1);
  not not_54 (not_54_out, op2);
  and and_15 (and_15_out, not_52_out, not_53_out, not_54_out, op3, not_55_out, not_56_out);
  or or_3 (Branch, and_14_out, and_15_out);
  not not_55 (not_55_out, op4);
  not not_56 (not_56_out, op5);
  not not_57 (not_57_out, op0);
  not not_58 (not_58_out, op1);
  not not_59 (not_59_out, op2);
  and and_16 (RegDst, not_57_out, not_58_out, not_59_out, not_60_out, not_61_out, not_62_out);
  not not_60 (not_60_out, op3);
  not not_61 (not_61_out, op4);
  not not_62 (not_62_out, op5);
  not not_63 (not_63_out, op0);
  not not_64 (not_64_out, op1);
  not not_65 (not_65_out, op2);
  not not_66 (not_66_out, op3);
  not not_67 (not_67_out, op4);
  not not_68 (not_68_out, op5);
  not not_69 (not_69_out, op0);
  not not_70 (not_70_out, op1);
  and and_17 (and_17_out, not_63_out, not_64_out, not_65_out, not_66_out, not_67_out, not_68_out);
  not not_71 (not_71_out, op3);
  not not_72 (not_72_out, op4);
  not not_73 (not_73_out, op5);
  and and_18 (and_18_out, not_69_out, not_70_out, op2, not_71_out, not_72_out, not_73_out);
  not not_74 (not_74_out, op1);
  not not_75 (not_75_out, op2);
  not not_76 (not_76_out, op3);
  and and_19 (and_19_out, op0, not_74_out, not_75_out, not_76_out, op4, op5);
  not not_77 (not_77_out, op0);
  not not_78 (not_78_out, op1);
  not not_79 (not_79_out, op4);
  not not_80 (not_80_out, op5);
  and and_20 (and_20_out, not_77_out, not_78_out, op2, op3, not_79_out, not_80_out);
  not not_81 (not_81_out, op0);
  not not_82 (not_82_out, op1);
  not not_83 (not_83_out, op4);
  and and_21 (and_21_out, not_81_out, not_82_out, op2, op3, not_83_out, op5);
  or or_4 (RegWrite, and_17_out, and_18_out, and_19_out, and_20_out, and_21_out, and_22_out, and_23_out, and_24_out, and_25_out, and_26_out);
  not not_84 (not_84_out, op0);
  not not_85 (not_85_out, op1);
  not not_86 (not_86_out, op3);
  and and_22 (and_22_out, not_84_out, not_85_out, op2, not_86_out, op4, not_87_out);
  not not_87 (not_87_out, op5);
  not not_88 (not_88_out, op0);
  not not_89 (not_89_out, op1);
  not not_90 (not_90_out, op3);
  and and_23 (and_23_out, not_88_out, not_89_out, op2, not_90_out, not_91_out, op5);
  not not_91 (not_91_out, op4);
  not not_92 (not_92_out, op0);
  not not_93 (not_93_out, op1);
  and and_24 (and_24_out, not_92_out, not_93_out, op2, not_94_out, not_95_out, not_96_out);
  not not_94 (not_94_out, op3);
  not not_95 (not_95_out, op4);
  not not_96 (not_96_out, op5);
  not not_97 (not_97_out, op0);
  not not_98 (not_98_out, op1);
  not not_99 (not_99_out, op2);
  not not_100 (not_100_out, op3);
  not not_101 (not_101_out, op0);
  and and_25 (and_25_out, not_97_out, not_98_out, not_99_out, not_100_out, op4, op5);
  not not_102 (not_102_out, op2);
  not not_103 (not_103_out, op3);
  not not_104 (not_104_out, op4);
  not not_105 (not_105_out, op5);
  not not_106 (not_106_out, op0);
  and and_26 (and_26_out, not_101_out, op1, not_102_out, not_103_out, not_104_out, not_105_out);
  not not_107 (not_107_out, op1);
  not not_108 (not_108_out, op2);
  not not_109 (not_109_out, op4);
  and and_27 (BneBeq, not_106_out, not_107_out, not_108_out, op3, not_109_out, op5);
  not not_110 (not_110_out, op0);
  not not_111 (not_111_out, op1);
  not not_112 (not_112_out, op2);
  not not_113 (not_113_out, op3);
  and and_28 (IsJAL, not_110_out, not_111_out, not_112_out, not_113_out, op4, op5);
  not not_114 (not_114_out, op0);
  not not_115 (not_115_out, op1);
  not not_116 (not_116_out, op4);
  and and_29 (and_29_out, not_114_out, not_115_out, op2, op3, not_116_out);
  not not_117 (not_117_out, op0);
  not not_118 (not_118_out, op1);
  and and_30 (and_30_out, not_117_out, not_118_out, op2, op3, op4, not_119_out);
  or or_5 (ZeroExtend, and_29_out, and_30_out);
  not not_119 (not_119_out, op5);
endmodule

module RegisterRead (
  input  op0,
  input  op1,
  input  op2,
  input  op3,
  input  op4,
  input  op5,
  input  Funct0,
  input  Funct1,
  input  Funct2,
  input  Funct3,
  input  Funct4,
  input  Funct5,
  output ReadRt,
  output ReadRs
);

  wire and_1_out, and_2_out, and_3_out, and_4_out, and_5_out, and_6_out, and_7_out, and_8_out, and_9_out,
       and_10_out, and_11_out, and_12_out, and_13_out, and_14_out, and_15_out, and_16_out, and_17_out,
       and_18_out, and_19_out, and_20_out, and_21_out, and_22_out, and_23_out, and_24_out, and_25_out,
       and_26_out, and_27_out, and_28_out, and_29_out, and_30_out, and_31_out, and_32_out, and_33_out,
       and_34_out, and_35_out, not_1_out, not_2_out, not_3_out, not_4_out, not_5_out, not_6_out, not_7_out,
       not_8_out, not_9_out, not_10_out, not_11_out, not_12_out, not_13_out, not_14_out, not_15_out,
       not_16_out, not_17_out, not_18_out, not_19_out, not_20_out, not_21_out, not_22_out, not_23_out,
       not_24_out, not_25_out, not_26_out, not_27_out, not_28_out, not_29_out, not_30_out, not_31_out,
       not_32_out, not_33_out, not_34_out, not_35_out, not_36_out, not_37_out, not_38_out, not_39_out,
       not_40_out, not_41_out, not_42_out, not_43_out, not_44_out, not_45_out, not_46_out, not_47_out,
       not_48_out, not_49_out, not_50_out, not_51_out, not_52_out, not_53_out, not_54_out, not_58_out,
       not_59_out, not_60_out, not_61_out, not_62_out, not_63_out, not_64_out, not_65_out, not_66_out,
       not_67_out, not_68_out, not_69_out, not_70_out, not_71_out, not_72_out, not_73_out, not_74_out,
       not_75_out, not_76_out, not_77_out, not_78_out, not_79_out, not_80_out, not_81_out, not_82_out,
       not_83_out, not_84_out, not_85_out, not_86_out, not_87_out, not_88_out, not_89_out, not_90_out,
       not_91_out, not_92_out, not_93_out, not_94_out, not_95_out, not_96_out, not_97_out, not_98_out,
       not_99_out, not_100_out, not_101_out, not_102_out, not_103_out, not_104_out, not_105_out, not_106_out,
       not_107_out, not_108_out, not_109_out, not_110_out, not_111_out, not_112_out, not_113_out,
       not_114_out, not_115_out, not_116_out, not_117_out, not_118_out, not_119_out, not_120_out,
       not_121_out, not_122_out, not_123_out, not_124_out, not_125_out, not_126_out, not_127_out,
       not_128_out, not_129_out, not_130_out, not_131_out, not_132_out, not_133_out, not_134_out,
       not_135_out, not_136_out, not_137_out, not_138_out, not_139_out, not_151_out, not_156_out,
       not_159_out, not_160_out, not_164_out, not_165_out, not_167_out, not_168_out, not_169_out,
       not_170_out, not_172_out, not_180_out, not_181_out, not_182_out, not_183_out, not_190_out,
       not_192_out, not_193_out, not_194_out, not_196_out, not_197_out, not_198_out, not_199_out,
       not_207_out, not_208_out, not_216_out, not_217_out, not_220_out, not_221_out, not_223_out,
       not_233_out, not_246_out, not_261_out, not_262_out, not_270_out, not_271_out, not_272_out,
       not_273_out, not_275_out, not_282_out, not_284_out, not_285_out, not_286_out, not_292_out,
       not_298_out, not_299_out, not_300_out, not_301_out, not_303_out, not_310_out, not_311_out,
       not_312_out, not_314_out, not_315_out, not_316_out, not_323_out, not_324_out, not_326_out,
       not_328_out, not_329_out, not_337_out, not_338_out, not_340_out, not_341_out, not_342_out,
       not_343_out, not_344_out, not_346_out, not_353_out, not_355_out, not_356_out, not_357_out,
       not_359_out, not_360_out, not_361_out, not_369_out, or_1_out, or_3_out;

  not not_1 (not_1_out, op0);
  not not_2 (not_2_out, op1);
  not not_3 (not_3_out, op2);
  not not_4 (not_4_out, op3);
  not not_5 (not_5_out, op4);
  not not_6 (not_6_out, op5);
  and and_1 (and_1_out, not_1_out, not_2_out, not_3_out, not_4_out, not_5_out, not_6_out, or_1_out);
  not not_7 (not_7_out, Funct1);
  not not_8 (not_8_out, Funct2);
  and and_2 (and_2_out, Funct0, not_7_out, not_8_out, not_9_out, not_10_out, not_11_out);
  not not_9 (not_9_out, Funct3);
  not not_10 (not_10_out, Funct4);
  not not_11 (not_11_out, Funct4);
  not not_12 (not_12_out, Funct1);
  not not_13 (not_13_out, Funct2);
  not not_14 (not_14_out, Funct4);
  not not_15 (not_15_out, Funct5);
  and and_3 (and_3_out, Funct0, not_12_out, not_13_out, Funct3, not_14_out, not_15_out);
  not not_16 (not_16_out, Funct1);
  not not_17 (not_17_out, Funct2);
  and and_4 (and_4_out, Funct0, not_16_out, not_17_out, not_18_out, not_19_out, Funct5);
  not not_18 (not_18_out, Funct3);
  not not_19 (not_19_out, Funct4);
  not not_20 (not_20_out, Funct1);
  not not_21 (not_21_out, Funct2);
  not not_22 (not_22_out, Funct3);
  not not_23 (not_23_out, Funct5);
  and and_5 (and_5_out, Funct0, not_20_out, not_21_out, not_22_out, Funct4, not_23_out);
  not not_24 (not_24_out, Funct1);
  not not_25 (not_25_out, Funct2);
  and and_6 (and_6_out, Funct0, not_24_out, not_25_out, Funct3, not_26_out, Funct5);
  or or_1 (or_1_out, and_2_out, and_3_out, and_4_out, and_5_out, and_6_out, and_7_out, and_8_out, and_9_out, and_10_out);
  not not_26 (not_26_out, Funct4);
  not not_27 (not_27_out, Funct1);
  not not_28 (not_28_out, Funct2);
  and and_7 (and_7_out, Funct0, not_27_out, not_28_out, Funct3, Funct4, Funct5);
  not not_29 (not_29_out, Funct1);
  and and_8 (and_8_out, Funct0, not_29_out, Funct2, not_30_out, Funct4, not_31_out);
  not not_30 (not_30_out, Funct3);
  not not_31 (not_31_out, Funct5);
  not not_32 (not_32_out, Funct1);
  not not_33 (not_33_out, Funct3);
  and and_9 (and_9_out, Funct0, not_32_out, Funct2, not_33_out, Funct4, Funct5);
  not not_34 (not_34_out, Funct0);
  not not_35 (not_35_out, Funct1);
  and and_10 (and_10_out, not_34_out, not_35_out, Funct2, not_36_out, not_37_out, not_38_out);
  not not_36 (not_36_out, Funct3);
  not not_37 (not_37_out, Funct4);
  not not_38 (not_38_out, Funct5);
  not not_39 (not_39_out, op0);
  not not_40 (not_40_out, op1);
  not not_41 (not_41_out, op3);
  not not_42 (not_42_out, op4);
  not not_43 (not_43_out, op5);
  and and_11 (and_11_out, not_39_out, not_40_out, op2, not_41_out, not_42_out, not_43_out);
  not not_44 (not_44_out, op0);
  not not_45 (not_45_out, op1);
  and and_12 (and_12_out, not_44_out, not_45_out, op2, not_46_out, not_47_out, op5);
  not not_46 (not_46_out, op3);
  not not_47 (not_47_out, op4);
  not not_48 (not_48_out, op0);
  not not_49 (not_49_out, op1);
  not not_50 (not_50_out, op4);
  not not_51 (not_51_out, op5);
  and and_13 (and_13_out, not_48_out, not_49_out, op2, op3, not_50_out, not_51_out);
  not not_52 (not_52_out, op0);
  not not_53 (not_53_out, op1);
  and and_14 (and_14_out, not_52_out, not_53_out, op2, op3, not_54_out, op5);
  not not_54 (not_54_out, op4);
  // NOT_Gate not_55 is placed but not wired
  // NOT_Gate not_56 is placed but not wired
  // NOT_Gate not_57 is placed but not wired
  not not_58 (not_58_out, op1);
  not not_59 (not_59_out, op2);
  not not_60 (not_60_out, op3);
  and and_15 (and_15_out, op0, not_58_out, not_59_out, not_60_out, op4, op5);
  or or_2 (ReadRs, and_1_out, and_11_out, and_12_out, and_13_out, and_14_out, and_15_out, and_16_out, and_17_out, and_18_out, and_19_out);
  not not_61 (not_61_out, op0);
  not not_62 (not_62_out, op1);
  not not_63 (not_63_out, op2);
  and and_16 (and_16_out, not_61_out, not_62_out, not_63_out, op3, not_64_out, not_65_out);
  not not_64 (not_64_out, op4);
  not not_65 (not_65_out, op5);
  not not_66 (not_66_out, op0);
  not not_67 (not_67_out, op1);
  not not_68 (not_68_out, op2);
  not not_69 (not_69_out, op4);
  and and_17 (and_17_out, not_66_out, not_67_out, not_68_out, op3, not_69_out, op5);
  not not_70 (not_70_out, op0);
  not not_71 (not_71_out, op1);
  and and_18 (and_18_out, not_70_out, not_71_out, op2, not_72_out, op4, not_73_out);
  not not_72 (not_72_out, op3);
  not not_73 (not_73_out, op5);
  not not_74 (not_74_out, op1);
  not not_75 (not_75_out, op3);
  and and_19 (and_19_out, op0, not_74_out, op2, not_75_out, op4, op5);
  not not_76 (not_76_out, op0);
  not not_77 (not_77_out, op1);
  not not_78 (not_78_out, op2);
  not not_79 (not_79_out, op3);
  and and_20 (and_20_out, not_76_out, not_77_out, not_78_out, not_79_out, not_80_out, not_81_out, or_3_out);
  not not_80 (not_80_out, op4);
  not not_81 (not_81_out, op5);
  not not_82 (not_82_out, Funct1);
  not not_83 (not_83_out, Funct2);
  not not_84 (not_84_out, Funct3);
  not not_85 (not_85_out, Funct4);
  not not_86 (not_86_out, Funct5);
  and and_21 (and_21_out, Funct0, not_82_out, not_83_out, not_84_out, not_85_out, not_86_out);
  not not_87 (not_87_out, Funct1);
  not not_88 (not_88_out, Funct2);
  and and_22 (and_22_out, Funct0, not_87_out, not_88_out, not_89_out, not_90_out, Funct5);
  not not_89 (not_89_out, Funct3);
  not not_90 (not_90_out, Funct4);
  not not_91 (not_91_out, Funct1);
  not not_92 (not_92_out, Funct2);
  not not_93 (not_93_out, Funct4);
  not not_94 (not_94_out, Funct5);
  and and_23 (and_23_out, Funct0, not_91_out, not_92_out, Funct3, not_93_out, not_94_out);
  not not_95 (not_95_out, Funct0);
  not not_96 (not_96_out, Funct1);
  not not_97 (not_97_out, Funct2);
  and and_24 (and_24_out, not_95_out, not_96_out, not_97_out, not_98_out, not_99_out, not_100_out);
  or or_3 (or_3_out, and_21_out, and_22_out, and_23_out, and_24_out, and_25_out, and_26_out, and_27_out, and_28_out, and_29_out, and_30_out, and_31_out);
  not not_98 (not_98_out, Funct3);
  not not_99 (not_99_out, Funct4);
  not not_100 (not_100_out, Funct5);
  not not_101 (not_101_out, Funct0);
  not not_102 (not_102_out, Funct1);
  not not_103 (not_103_out, Funct2);
  not not_104 (not_104_out, Funct3);
  and and_25 (and_25_out, not_101_out, not_102_out, not_103_out, not_104_out, Funct4, Funct5);
  not not_105 (not_105_out, Funct0);
  not not_106 (not_106_out, Funct1);
  not not_107 (not_107_out, Funct2);
  and and_26 (and_26_out, not_105_out, not_106_out, not_107_out, not_108_out, Funct4, not_109_out);
  not not_108 (not_108_out, Funct3);
  not not_109 (not_109_out, Funct5);
  not not_110 (not_110_out, Funct1);
  not not_111 (not_111_out, Funct2);
  not not_112 (not_112_out, Funct3);
  not not_113 (not_113_out, Funct5);
  and and_27 (and_27_out, Funct0, not_110_out, not_111_out, not_112_out, Funct4, not_113_out);
  not not_114 (not_114_out, Funct1);
  not not_115 (not_115_out, Funct2);
  and and_28 (and_28_out, Funct0, not_114_out, not_115_out, Funct3, not_116_out, Funct5);
  not not_116 (not_116_out, Funct4);
  not not_117 (not_117_out, Funct1);
  not not_118 (not_118_out, Funct2);
  and and_29 (and_29_out, Funct0, not_117_out, not_118_out, Funct3, Funct4, Funct5);
  not not_119 (not_119_out, Funct1);
  and and_30 (and_30_out, Funct0, not_119_out, Funct2, not_120_out, Funct4, not_121_out);
  not not_120 (not_120_out, Funct3);
  not not_121 (not_121_out, Funct5);
  not not_122 (not_122_out, Funct1);
  not not_123 (not_123_out, Funct3);
  and and_31 (and_31_out, Funct0, not_122_out, Funct2, not_123_out, Funct4, Funct5);
  not not_124 (not_124_out, op0);
  not not_125 (not_125_out, op1);
  not not_126 (not_126_out, op2);
  and and_32 (and_32_out, not_124_out, not_125_out, not_126_out, op3, not_127_out, not_128_out);
  not not_127 (not_127_out, op4);
  not not_128 (not_128_out, op5);
  not not_129 (not_129_out, op0);
  not not_130 (not_130_out, op1);
  not not_131 (not_131_out, op2);
  not not_132 (not_132_out, op4);
  and and_33 (and_33_out, not_129_out, not_130_out, not_131_out, op3, not_132_out, op5);
  or or_4 (ReadRt, and_20_out, and_32_out, and_33_out, and_34_out, and_35_out);
  not not_133 (not_133_out, op0);
  not not_134 (not_134_out, op2);
  and and_34 (and_34_out, not_133_out, op1, not_134_out, not_135_out, not_136_out, not_137_out);
  not not_135 (not_135_out, op3);
  not not_136 (not_136_out, op4);
  not not_137 (not_137_out, op5);
  not not_138 (not_138_out, op1);
  not not_139 (not_139_out, op3);
  and and_35 (and_35_out, op0, not_138_out, op2, not_139_out, op4, op5);
  // NOT_Gate not_140 is placed but not wired
  // NOT_Gate not_141 is placed but not wired
  // NOT_Gate not_142 is placed but not wired
  // NOT_Gate not_143 is placed but not wired
  // NOT_Gate not_144 is placed but not wired
  // NOT_Gate not_145 is placed but not wired
  // NOT_Gate not_146 is placed but not wired
  // AND_Gate and_36 is placed but not wired
  // NOT_Gate not_147 is placed but not wired
  // NOT_Gate not_148 is placed but not wired
  // NOT_Gate not_149 is placed but not wired
  // NOT_Gate not_150 is placed but not wired
  // NOT_Gate not_151 has open pins: in=open, out=not_151_out
  // NOT_Gate not_152 is placed but not wired
  // NOT_Gate not_153 is placed but not wired
  // NOT_Gate not_154 has open pins: in=not_151_out, out=open
  // NOT_Gate not_155 is placed but not wired
  // NOT_Gate not_156 has open pins: in=open, out=not_156_out
  // NOT_Gate not_157 has open pins: in=not_156_out, out=open
  // NOT_Gate not_158 is placed but not wired
  // NOT_Gate not_159 has open pins: in=open, out=not_159_out
  // NOT_Gate not_160 has open pins: in=open, out=not_160_out
  // NOT_Gate not_161 has open pins: in=not_159_out, out=open
  // NOT_Gate not_162 is placed but not wired
  // NOT_Gate not_163 has open pins: in=not_160_out, out=open
  // AND_Gate and_37 is placed but not wired
  // NOT_Gate not_164 has open pins: in=open, out=not_164_out
  // NOT_Gate not_165 has open pins: in=open, out=not_165_out
  // NOT_Gate not_166 is placed but not wired
  // NOT_Gate not_167 has open pins: in=open, out=not_167_out
  not not_168 (not_168_out, not_164_out);
  not not_169 (not_169_out, not_165_out);
  // NOT_Gate not_170 has open pins: in=open, out=not_170_out
  // NOT_Gate not_171 is placed but not wired
  not not_172 (not_172_out, not_167_out);
  // NOT_Gate not_173 has open pins: in=not_168_out, out=open
  // NOT_Gate not_174 has open pins: in=not_169_out, out=open
  // NOT_Gate not_175 has open pins: in=not_170_out, out=open
  // NOT_Gate not_176 is placed but not wired
  // NOT_Gate not_177 has open pins: in=not_172_out, out=open
  // NOT_Gate not_178 is placed but not wired
  // NOT_Gate not_179 is placed but not wired
  // NOT_Gate not_180 has open pins: in=open, out=not_180_out
  // NOT_Gate not_181 has open pins: in=open, out=not_181_out
  // NOT_Gate not_182 has open pins: in=open, out=not_182_out
  // NOT_Gate not_183 has open pins: in=open, out=not_183_out
  // NOT_Gate not_184 is placed but not wired
  // NOT_Gate not_185 has open pins: in=not_180_out, out=open
  // NOT_Gate not_186 has open pins: in=not_181_out, out=open
  // NOT_Gate not_187 has open pins: in=not_182_out, out=open
  // NOT_Gate not_188 has open pins: in=not_183_out, out=open
  // NOT_Gate not_189 is placed but not wired
  // AND_Gate and_38 is placed but not wired
  // NOT_Gate not_190 has open pins: in=open, out=not_190_out
  // NOT_Gate not_191 is placed but not wired
  // NOT_Gate not_192 has open pins: in=open, out=not_192_out
  // NOT_Gate not_193 has open pins: in=open, out=not_193_out
  not not_194 (not_194_out, not_190_out);
  // NOT_Gate not_195 is placed but not wired
  // NOT_Gate not_196 has open pins: in=open, out=not_196_out
  not not_197 (not_197_out, not_192_out);
  not not_198 (not_198_out, not_193_out);
  // NOT_Gate not_199 has open pins: in=open, out=not_199_out
  // NOT_Gate not_200 has open pins: in=not_194_out, out=open
  // NOT_Gate not_201 is placed but not wired
  // NOT_Gate not_202 has open pins: in=not_196_out, out=open
  // NOT_Gate not_203 has open pins: in=not_197_out, out=open
  // NOT_Gate not_204 has open pins: in=not_198_out, out=open
  // NOT_Gate not_205 has open pins: in=not_199_out, out=open
  // NOT_Gate not_206 is placed but not wired
  // NOT_Gate not_207 has open pins: in=open, out=not_207_out
  // NOT_Gate not_208 has open pins: in=open, out=not_208_out
  // NOT_Gate not_209 is placed but not wired
  // NOT_Gate not_210 has open pins: in=not_207_out, out=open
  // NOT_Gate not_211 is placed but not wired
  // NOT_Gate not_212 has open pins: in=not_208_out, out=open
  // NOT_Gate not_213 is placed but not wired
  // NOT_Gate not_214 is placed but not wired
  // NOT_Gate not_215 is placed but not wired
  // NOT_Gate not_216 has open pins: in=open, out=not_216_out
  // NOT_Gate not_217 has open pins: in=open, out=not_217_out
  // NOT_Gate not_218 is placed but not wired
  // NOT_Gate not_219 is placed but not wired
  not not_220 (not_220_out, not_216_out);
  not not_221 (not_221_out, not_217_out);
  // NOT_Gate not_222 is placed but not wired
  // NOT_Gate not_223 has open pins: in=open, out=not_223_out
  // NOT_Gate not_224 is placed but not wired
  // NOT_Gate not_225 has open pins: in=not_220_out, out=open
  // NOT_Gate not_226 is placed but not wired
  // NOT_Gate not_227 has open pins: in=not_221_out, out=open
  // NOT_Gate not_228 is placed but not wired
  // NOT_Gate not_229 has open pins: in=not_223_out, out=open
  // NOT_Gate not_230 is placed but not wired
  // NOT_Gate not_231 is placed but not wired
  // NOT_Gate not_232 is placed but not wired
  // AND_Gate and_39 is placed but not wired
  // NOT_Gate not_233 has open pins: in=open, out=not_233_out
  // NOT_Gate not_234 is placed but not wired
  // NOT_Gate not_235 is placed but not wired
  // NOT_Gate not_236 is placed but not wired
  // NOT_Gate not_237 is placed but not wired
  // NOT_Gate not_238 has open pins: in=not_233_out, out=open
  // NOT_Gate not_239 is placed but not wired
  // NOT_Gate not_240 is placed but not wired
  // AND_Gate and_40 is placed but not wired
  // NOT_Gate not_241 is placed but not wired
  // NOT_Gate not_242 is placed but not wired
  // NOT_Gate not_243 is placed but not wired
  // NOT_Gate not_244 is placed but not wired
  // NOT_Gate not_245 is placed but not wired
  // NOT_Gate not_246 has open pins: in=open, out=not_246_out
  // NOT_Gate not_247 has open pins: in=not_246_out, out=open
  // NOT_Gate not_248 is placed but not wired
  // NOT_Gate not_249 is placed but not wired
  // NOT_Gate not_250 is placed but not wired
  // NOT_Gate not_251 is placed but not wired
  // NOT_Gate not_252 is placed but not wired
  // NOT_Gate not_253 is placed but not wired
  // NOT_Gate not_254 is placed but not wired
  // NOT_Gate not_255 is placed but not wired
  // NOT_Gate not_256 is placed but not wired
  // NOT_Gate not_257 is placed but not wired
  // NOT_Gate not_258 is placed but not wired
  // AND_Gate and_41 is placed but not wired
  // NOT_Gate not_259 is placed but not wired
  // NOT_Gate not_260 is placed but not wired
  // NOT_Gate not_261 has open pins: in=open, out=not_261_out
  // NOT_Gate not_262 has open pins: in=open, out=not_262_out
  // NOT_Gate not_263 is placed but not wired
  // NOT_Gate not_264 is placed but not wired
  // NOT_Gate not_265 is placed but not wired
  // NOT_Gate not_266 has open pins: in=not_261_out, out=open
  // NOT_Gate not_267 is placed but not wired
  // NOT_Gate not_268 has open pins: in=not_262_out, out=open
  // NOT_Gate not_269 is placed but not wired
  // AND_Gate and_42 is placed but not wired
  // NOT_Gate not_270 has open pins: in=open, out=not_270_out
  // NOT_Gate not_271 has open pins: in=open, out=not_271_out
  // NOT_Gate not_272 has open pins: in=open, out=not_272_out
  // NOT_Gate not_273 has open pins: in=open, out=not_273_out
  // NOT_Gate not_274 is placed but not wired
  // NOT_Gate not_275 has open pins: in=open, out=not_275_out
  // NOT_Gate not_276 has open pins: in=not_270_out, out=open
  // NOT_Gate not_277 has open pins: in=not_271_out, out=open
  // NOT_Gate not_278 has open pins: in=not_272_out, out=open
  // NOT_Gate not_279 has open pins: in=not_273_out, out=open
  // NOT_Gate not_280 is placed but not wired
  // NOT_Gate not_281 has open pins: in=not_275_out, out=open
  // NOT_Gate not_282 has open pins: in=open, out=not_282_out
  // NOT_Gate not_283 is placed but not wired
  // NOT_Gate not_284 has open pins: in=open, out=not_284_out
  // NOT_Gate not_285 has open pins: in=open, out=not_285_out
  // NOT_Gate not_286 has open pins: in=open, out=not_286_out
  // NOT_Gate not_287 is placed but not wired
  // NOT_Gate not_288 has open pins: in=not_282_out, out=open
  // NOT_Gate not_289 has open pins: in=not_284_out, out=open
  // NOT_Gate not_290 has open pins: in=not_285_out, out=open
  // NOT_Gate not_291 has open pins: in=not_286_out, out=open
  // AND_Gate and_43 is placed but not wired
  // NOT_Gate not_292 has open pins: in=open, out=not_292_out
  // NOT_Gate not_293 has open pins: in=not_292_out, out=open
  // NOT_Gate not_294 is placed but not wired
  // NOT_Gate not_295 is placed but not wired
  // NOT_Gate not_296 is placed but not wired
  // NOT_Gate not_297 is placed but not wired
  // AND_Gate and_44 is placed but not wired
  // NOT_Gate not_298 has open pins: in=open, out=not_298_out
  // NOT_Gate not_299 has open pins: in=open, out=not_299_out
  // NOT_Gate not_300 has open pins: in=open, out=not_300_out
  // NOT_Gate not_301 has open pins: in=open, out=not_301_out
  // NOT_Gate not_302 is placed but not wired
  // NOT_Gate not_303 has open pins: in=open, out=not_303_out
  // NOT_Gate not_304 has open pins: in=not_298_out, out=open
  // NOT_Gate not_305 has open pins: in=not_299_out, out=open
  // NOT_Gate not_306 has open pins: in=not_300_out, out=open
  // NOT_Gate not_307 has open pins: in=not_301_out, out=open
  // NOT_Gate not_308 is placed but not wired
  // NOT_Gate not_309 has open pins: in=not_303_out, out=open
  // NOT_Gate not_310 has open pins: in=open, out=not_310_out
  // NOT_Gate not_311 has open pins: in=open, out=not_311_out
  // NOT_Gate not_312 has open pins: in=open, out=not_312_out
  // NOT_Gate not_313 is placed but not wired
  // NOT_Gate not_314 has open pins: in=open, out=not_314_out
  not not_315 (not_315_out, not_310_out);
  not not_316 (not_316_out, not_311_out);
  // NOT_Gate not_317 is placed but not wired
  // NOT_Gate not_318 has open pins: in=not_312_out, out=open
  // NOT_Gate not_319 has open pins: in=not_314_out, out=open
  // NOT_Gate not_320 has open pins: in=not_315_out, out=open
  // NOT_Gate not_321 has open pins: in=not_316_out, out=open
  // NOT_Gate not_322 is placed but not wired
  // NOT_Gate not_323 has open pins: in=open, out=not_323_out
  // NOT_Gate not_324 has open pins: in=open, out=not_324_out
  // NOT_Gate not_325 is placed but not wired
  // NOT_Gate not_326 has open pins: in=open, out=not_326_out
  // NOT_Gate not_327 is placed but not wired
  not not_328 (not_328_out, not_323_out);
  not not_329 (not_329_out, not_324_out);
  // NOT_Gate not_330 is placed but not wired
  // NOT_Gate not_331 has open pins: in=not_326_out, out=open
  // NOT_Gate not_332 is placed but not wired
  // NOT_Gate not_333 has open pins: in=not_328_out, out=open
  // NOT_Gate not_334 is placed but not wired
  // NOT_Gate not_335 has open pins: in=not_329_out, out=open
  // NOT_Gate not_336 is placed but not wired
  // NOT_Gate not_337 has open pins: in=open, out=not_337_out
  // NOT_Gate not_338 has open pins: in=open, out=not_338_out
  // NOT_Gate not_339 is placed but not wired
  // NOT_Gate not_340 has open pins: in=open, out=not_340_out
  // NOT_Gate not_341 has open pins: in=open, out=not_341_out
  not not_342 (not_342_out, not_337_out);
  not not_343 (not_343_out, not_338_out);
  // NOT_Gate not_344 has open pins: in=open, out=not_344_out
  // NOT_Gate not_345 is placed but not wired
  not not_346 (not_346_out, not_340_out);
  // NOT_Gate not_347 has open pins: in=not_341_out, out=open
  // NOT_Gate not_348 has open pins: in=not_342_out, out=open
  // NOT_Gate not_349 has open pins: in=not_343_out, out=open
  // NOT_Gate not_350 has open pins: in=not_344_out, out=open
  // NOT_Gate not_351 is placed but not wired
  // NOT_Gate not_352 has open pins: in=not_346_out, out=open
  // NOT_Gate not_353 has open pins: in=open, out=not_353_out
  // NOT_Gate not_354 is placed but not wired
  // NOT_Gate not_355 has open pins: in=open, out=not_355_out
  // NOT_Gate not_356 has open pins: in=open, out=not_356_out
  not not_357 (not_357_out, not_353_out);
  // NOT_Gate not_358 is placed but not wired
  // NOT_Gate not_359 has open pins: in=open, out=not_359_out
  not not_360 (not_360_out, not_355_out);
  not not_361 (not_361_out, not_356_out);
  // NOT_Gate not_362 is placed but not wired
  // NOT_Gate not_363 has open pins: in=not_357_out, out=open
  // NOT_Gate not_364 is placed but not wired
  // NOT_Gate not_365 has open pins: in=not_359_out, out=open
  // NOT_Gate not_366 has open pins: in=not_360_out, out=open
  // NOT_Gate not_367 has open pins: in=not_361_out, out=open
  // NOT_Gate not_368 is placed but not wired
  // NOT_Gate not_369 has open pins: in=open, out=not_369_out
  // NOT_Gate not_370 is placed but not wired
  // NOT_Gate not_371 is placed but not wired
  // NOT_Gate not_372 is placed but not wired
  // NOT_Gate not_373 is placed but not wired
  // NOT_Gate not_374 has open pins: in=not_369_out, out=open
  // NOT_Gate not_375 is placed but not wired
  // NOT_Gate not_376 is placed but not wired
  // NOT_Gate not_377 is placed but not wired
  // NOT_Gate not_378 is placed but not wired
  // NOT_Gate not_379 is placed but not wired
endmodule

module FunctDecoder (
  input  Funct0,
  input  Funct1,
  input  Funct2,
  input  Funct3,
  input  Funct4,
  input  Funct5,
  output ALU0,
  output ALU1,
  output ALU2,
  output ALU3,
  output IsJR,
  output IsShamt
);

  wire and_1_out, and_2_out, and_3_out, and_4_out, and_5_out, and_6_out, and_7_out, and_8_out, and_9_out,
       and_10_out, and_11_out, and_12_out, and_13_out, and_14_out, and_15_out, and_16_out, and_17_out,
       and_19_out, and_20_out, and_21_out, not_1_out, not_2_out, not_3_out, not_4_out, not_5_out, not_6_out,
       not_7_out, not_8_out, not_9_out, not_10_out, not_11_out, not_12_out, not_13_out, not_14_out,
       not_15_out, not_16_out, not_17_out, not_18_out, not_19_out, not_20_out, not_21_out, not_22_out,
       not_23_out, not_24_out, not_25_out, not_26_out, not_27_out, not_28_out, not_29_out, not_30_out,
       not_31_out, not_32_out, not_33_out, not_34_out, not_35_out, not_36_out, not_37_out, not_38_out,
       not_39_out, not_40_out, not_41_out, not_42_out, not_43_out, not_44_out, not_45_out, not_46_out,
       not_47_out, not_48_out, not_49_out, not_50_out, not_51_out, not_52_out, not_53_out, not_54_out,
       not_55_out, not_56_out, not_57_out, not_58_out, not_59_out, not_60_out, not_61_out, not_62_out,
       not_63_out, not_64_out, not_65_out, not_66_out, not_67_out, not_68_out, not_69_out, not_70_out,
       not_71_out, not_72_out, not_73_out, not_74_out, not_75_out, not_76_out, not_77_out;

  not not_1 (not_1_out, Funct1);
  not not_2 (not_2_out, Funct2);
  not not_3 (not_3_out, Funct4);
  and and_1 (and_1_out, Funct0, not_1_out, not_2_out, Funct3, not_3_out, Funct5);
  not not_4 (not_4_out, Funct1);
  not not_5 (not_5_out, Funct2);
  and and_2 (and_2_out, Funct0, not_4_out, not_5_out, Funct3, Funct4, Funct5);
  or or_1 (ALU0, and_1_out, and_2_out, and_3_out, and_4_out);
  not not_6 (not_6_out, Funct1);
  not not_7 (not_7_out, Funct3);
  not not_8 (not_8_out, Funct5);
  and and_3 (and_3_out, Funct0, not_6_out, Funct2, not_7_out, Funct4, not_8_out);
  not not_9 (not_9_out, Funct1);
  and and_4 (and_4_out, Funct0, not_9_out, Funct2, not_10_out, Funct4, Funct5);
  not not_10 (not_10_out, Funct3);
  not not_11 (not_11_out, Funct1);
  not not_12 (not_12_out, Funct2);
  not not_13 (not_13_out, Funct3);
  not not_14 (not_14_out, Funct4);
  and and_5 (and_5_out, Funct0, not_11_out, not_12_out, not_13_out, not_14_out);
  not not_15 (not_15_out, Funct1);
  not not_16 (not_16_out, Funct2);
  and and_6 (and_6_out, Funct0, not_15_out, not_16_out, not_17_out, not_18_out);
  not not_17 (not_17_out, Funct3);
  not not_18 (not_18_out, Funct5);
  or or_2 (ALU1, and_5_out, and_6_out, and_7_out, and_8_out);
  not not_19 (not_19_out, Funct4);
  not not_20 (not_20_out, Funct5);
  not not_21 (not_21_out, Funct1);
  not not_22 (not_22_out, Funct2);
  and and_7 (and_7_out, Funct0, not_21_out, not_22_out, not_19_out, not_20_out);
  not not_23 (not_23_out, Funct1);
  and and_8 (and_8_out, Funct0, not_23_out, Funct2, not_24_out, Funct4, Funct5);
  not not_24 (not_24_out, Funct3);
  not not_25 (not_25_out, Funct1);
  not not_26 (not_26_out, Funct2);
  not not_27 (not_27_out, Funct3);
  not not_28 (not_28_out, Funct5);
  and and_9 (and_9_out, Funct0, not_25_out, not_26_out, not_27_out, Funct4, not_28_out);
  not not_29 (not_29_out, Funct1);
  not not_30 (not_30_out, Funct2);
  and and_10 (and_10_out, Funct0, not_29_out, not_30_out, Funct3, not_31_out, not_32_out);
  not not_31 (not_31_out, Funct4);
  not not_32 (not_32_out, Funct5);
  not not_33 (not_33_out, Funct0);
  not not_34 (not_34_out, Funct1);
  not not_35 (not_35_out, Funct2);
  not not_36 (not_36_out, Funct3);
  not not_37 (not_37_out, Funct5);
  and and_11 (and_11_out, not_33_out, not_34_out, not_35_out, not_36_out, Funct4, not_37_out);
  or or_3 (ALU2, and_9_out, and_10_out, and_11_out, and_12_out, and_13_out);
  not not_38 (not_38_out, Funct1);
  not not_39 (not_39_out, Funct2);
  and and_12 (and_12_out, Funct0, not_38_out, not_39_out, Funct3, Funct4, Funct5);
  not not_40 (not_40_out, Funct1);
  not not_41 (not_41_out, Funct3);
  not not_42 (not_42_out, Funct5);
  and and_13 (and_13_out, Funct0, not_40_out, Funct2, not_41_out, Funct4, not_42_out);
  not not_43 (not_43_out, Funct0);
  not not_44 (not_44_out, Funct1);
  not not_45 (not_45_out, Funct2);
  and and_14 (and_14_out, not_43_out, not_44_out, not_45_out, not_46_out, Funct4, Funct5);
  not not_46 (not_46_out, Funct3);
  not not_47 (not_47_out, Funct1);
  not not_48 (not_48_out, Funct2);
  not not_49 (not_49_out, Funct3);
  not not_50 (not_50_out, Funct4);
  and and_15 (and_15_out, Funct0, not_47_out, not_48_out, not_49_out, not_50_out);
  not not_51 (not_51_out, Funct1);
  not not_52 (not_52_out, Funct2);
  and and_16 (and_16_out, Funct0, not_51_out, not_52_out, not_53_out, not_54_out);
  or or_4 (ALU3, and_14_out, and_15_out, and_16_out, and_17_out);
  not not_53 (not_53_out, Funct4);
  not not_54 (not_54_out, Funct5);
  not not_55 (not_55_out, Funct1);
  not not_56 (not_56_out, Funct3);
  not not_57 (not_57_out, Funct5);
  and and_17 (and_17_out, Funct0, not_55_out, Funct2, not_56_out, Funct4, not_57_out);
  not not_58 (not_58_out, Funct0);
  not not_59 (not_59_out, Funct1);
  and and_18 (IsJR, not_58_out, not_59_out, Funct2, not_60_out, not_61_out, not_62_out);
  not not_60 (not_60_out, Funct3);
  not not_61 (not_61_out, Funct4);
  not not_62 (not_62_out, Funct5);
  not not_63 (not_63_out, Funct0);
  not not_64 (not_64_out, Funct1);
  not not_65 (not_65_out, Funct2);
  not not_66 (not_66_out, Funct3);
  and and_19 (and_19_out, not_63_out, not_64_out, not_65_out, not_66_out, Funct4, Funct5);
  not not_67 (not_67_out, Funct0);
  not not_68 (not_68_out, Funct1);
  not not_69 (not_69_out, Funct2);
  and and_20 (and_20_out, not_67_out, not_68_out, not_69_out, not_70_out, Funct4, not_71_out);
  or or_5 (IsShamt, and_19_out, and_20_out, and_21_out);
  not not_70 (not_70_out, Funct3);
  not not_71 (not_71_out, Funct5);
  not not_72 (not_72_out, Funct0);
  not not_73 (not_73_out, Funct1);
  not not_74 (not_74_out, Funct2);
  not not_75 (not_75_out, Funct3);
  not not_76 (not_76_out, Funct4);
  not not_77 (not_77_out, Funct5);
  and and_21 (and_21_out, not_72_out, not_73_out, not_74_out, not_75_out, not_76_out, not_77_out);
endmodule

module ALUDecoder (
  input  op0,
  input  op1,
  input  op2,
  input  op3,
  input  op4,
  input  op5,
  output ALUop0,
  output ALUop1,
  output ALUop2,
  output ALUop3
);

  wire and_1_out, and_2_out, and_3_out, and_4_out, and_5_out, and_6_out, and_7_out, and_8_out, and_9_out,
       and_10_out, and_11_out, and_12_out, and_13_out, and_14_out, and_15_out, and_16_out, and_17_out,
       and_18_out, and_19_out, and_20_out, and_21_out, and_22_out, and_23_out, and_24_out, and_25_out,
       and_26_out, and_27_out, and_28_out, and_29_out, not_1_out, not_2_out, not_3_out, not_4_out, not_5_out,
       not_6_out, not_7_out, not_8_out, not_9_out, not_10_out, not_11_out, not_12_out, not_13_out,
       not_14_out, not_15_out, not_16_out, not_17_out, not_18_out, not_19_out, not_20_out, not_21_out,
       not_22_out, not_23_out, not_24_out, not_25_out, not_26_out, not_27_out, not_28_out, not_29_out,
       not_30_out, not_31_out, not_32_out, not_33_out, not_34_out, not_35_out, not_36_out, not_37_out,
       not_38_out, not_39_out, not_40_out, not_41_out, not_42_out, not_43_out, not_44_out, not_45_out,
       not_46_out, not_47_out, not_48_out, not_49_out, not_50_out, not_51_out, not_52_out, not_53_out,
       not_54_out, not_55_out, not_56_out, not_57_out, not_58_out, not_59_out, not_60_out, not_61_out,
       not_62_out, not_63_out, not_64_out, not_65_out, not_66_out, not_67_out, not_68_out, not_69_out,
       not_70_out, not_71_out, not_72_out, not_73_out, not_74_out, not_75_out, not_76_out, not_77_out,
       not_78_out, not_79_out, not_80_out, not_81_out, not_82_out, not_83_out, not_84_out, not_85_out,
       not_86_out, not_87_out, not_88_out, not_89_out, not_90_out, not_91_out, not_92_out, not_93_out,
       not_94_out, not_95_out, not_96_out, not_97_out, not_98_out, not_99_out, not_100_out, not_101_out,
       not_102_out, not_103_out, not_104_out, not_105_out, not_106_out, not_107_out, not_108_out,
       not_109_out, not_110_out, not_111_out, not_112_out, not_113_out, not_114_out, not_115_out,
       not_116_out, not_117_out, not_118_out, not_119_out, not_120_out, not_121_out, not_122_out, not_123_out;

  not not_1 (not_1_out, op0);
  not not_2 (not_2_out, op1);
  not not_3 (not_3_out, op4);
  and and_1 (and_1_out, not_1_out, not_2_out, op2, op3, not_3_out, op5);
  or or_1 (ALUop0, and_1_out, and_2_out);
  not not_4 (not_4_out, op0);
  not not_5 (not_5_out, op1);
  not not_6 (not_6_out, op3);
  and and_2 (and_2_out, not_4_out, not_5_out, op2, not_6_out, op4, not_7_out);
  not not_7 (not_7_out, op5);
  not not_8 (not_8_out, op0);
  not not_9 (not_9_out, op1);
  not not_10 (not_10_out, op2);
  not not_11 (not_11_out, op3);
  not not_12 (not_12_out, op4);
  not not_13 (not_13_out, op5);
  and and_3 (and_3_out, not_8_out, not_9_out, not_10_out, not_11_out, not_12_out, not_13_out);
  not not_14 (not_14_out, op0);
  not not_15 (not_15_out, op1);
  not not_16 (not_16_out, op3);
  not not_17 (not_17_out, op4);
  and and_4 (and_4_out, not_14_out, not_15_out, op2, not_16_out, not_17_out, not_19_out);
  not not_18 (not_18_out, op1);
  not not_19 (not_19_out, op5);
  not not_20 (not_20_out, op2);
  not not_21 (not_21_out, op3);
  and and_5 (and_5_out, op0, not_18_out, not_20_out, not_21_out, op4, op5);
  not not_22 (not_22_out, op1);
  not not_23 (not_23_out, op3);
  and and_6 (and_6_out, op0, not_22_out, op2, not_23_out, op4, op5);
  not not_24 (not_24_out, op0);
  not not_25 (not_25_out, op1);
  not not_26 (not_26_out, op2);
  not not_27 (not_27_out, op4);
  and and_7 (and_7_out, not_24_out, not_25_out, not_26_out, op3, not_27_out, op5);
  not not_28 (not_28_out, op0);
  not not_29 (not_29_out, op1);
  not not_30 (not_30_out, op2);
  not not_31 (not_31_out, op4);
  and and_8 (and_8_out, not_28_out, not_29_out, not_30_out, op3, not_31_out, not_32_out);
  or or_2 (ALUop1, and_3_out, and_4_out, and_5_out, and_6_out, and_7_out, and_8_out, and_9_out, and_10_out, and_11_out, and_12_out, and_13_out, and_14_out);
  not not_32 (not_32_out, op5);
  not not_33 (not_33_out, op0);
  not not_34 (not_34_out, op1);
  not not_35 (not_35_out, op4);
  not not_36 (not_36_out, op5);
  and and_9 (and_9_out, not_33_out, not_34_out, op2, op3, not_35_out, not_36_out);
  not not_37 (not_37_out, op0);
  not not_38 (not_38_out, op1);
  not not_39 (not_39_out, op3);
  not not_40 (not_40_out, op4);
  and and_10 (and_10_out, not_37_out, not_38_out, op2, not_39_out, not_40_out, op5);
  not not_41 (not_41_out, op0);
  not not_42 (not_42_out, op1);
  not not_43 (not_43_out, op3);
  not not_44 (not_44_out, op4);
  not not_45 (not_45_out, op5);
  and and_11 (and_11_out, not_41_out, not_42_out, op2, not_43_out, not_44_out, not_45_out);
  not not_46 (not_46_out, op0);
  not not_47 (not_47_out, op1);
  not not_48 (not_48_out, op2);
  not not_49 (not_49_out, op3);
  and and_12 (and_12_out, not_46_out, not_47_out, not_48_out, not_49_out, op4, not_50_out);
  not not_50 (not_50_out, op5);
  not not_51 (not_51_out, op0);
  not not_52 (not_52_out, op1);
  not not_53 (not_53_out, op2);
  not not_54 (not_54_out, op3);
  and and_13 (and_13_out, not_51_out, not_52_out, not_53_out, not_54_out, op4, op5);
  not not_55 (not_55_out, op0);
  not not_56 (not_56_out, op2);
  not not_57 (not_57_out, op3);
  not not_58 (not_58_out, op4);
  and and_14 (and_14_out, not_55_out, op1, not_56_out, not_57_out, not_58_out, not_59_out);
  not not_59 (not_59_out, op5);
  not not_60 (not_60_out, op0);
  not not_61 (not_61_out, op1);
  not not_62 (not_62_out, op4);
  not not_63 (not_63_out, op5);
  and and_15 (and_15_out, not_60_out, not_61_out, op2, op3, not_62_out, not_63_out);
  not not_64 (not_64_out, op0);
  not not_65 (not_65_out, op1);
  not not_66 (not_66_out, op3);
  and and_16 (and_16_out, not_64_out, not_65_out, op2, not_66_out, op4, not_67_out);
  or or_3 (ALUop2, and_15_out, and_16_out);
  not not_67 (not_67_out, op5);
  not not_68 (not_68_out, op0);
  not not_69 (not_69_out, op1);
  not not_70 (not_70_out, op2);
  not not_71 (not_71_out, op3);
  not not_72 (not_72_out, op4);
  not not_73 (not_73_out, op5);
  and and_17 (and_17_out, not_68_out, not_69_out, not_70_out, not_71_out, not_72_out, not_73_out);
  not not_74 (not_74_out, op0);
  not not_75 (not_75_out, op1);
  not not_76 (not_76_out, op3);
  not not_77 (not_77_out, op4);
  and and_18 (and_18_out, not_74_out, not_75_out, op2, not_76_out, not_77_out, not_78_out);
  not not_78 (not_78_out, op5);
  not not_79 (not_79_out, op1);
  not not_80 (not_80_out, op2);
  not not_81 (not_81_out, op3);
  and and_19 (and_19_out, op0, not_79_out, not_80_out, not_81_out, op4, op5);
  not not_82 (not_82_out, op1);
  not not_83 (not_83_out, op3);
  and and_20 (and_20_out, op0, not_82_out, op2, not_83_out, op4, op5);
  not not_84 (not_84_out, op0);
  not not_85 (not_85_out, op1);
  not not_86 (not_86_out, op2);
  not not_87 (not_87_out, op4);
  and and_21 (and_21_out, not_84_out, not_85_out, not_86_out, op3, not_87_out, op5);
  not not_88 (not_88_out, op0);
  not not_89 (not_89_out, op1);
  not not_90 (not_90_out, op2);
  not not_91 (not_91_out, op4);
  and and_22 (and_22_out, not_88_out, not_89_out, not_90_out, op3, not_91_out, not_92_out);
  not not_92 (not_92_out, op5);
  not not_93 (not_93_out, op0);
  not not_94 (not_94_out, op1);
  not not_95 (not_95_out, op4);
  not not_96 (not_96_out, op5);
  and and_23 (and_23_out, not_93_out, not_94_out, op2, op3, not_95_out, not_96_out);
  or or_4 (ALUop3, and_17_out, and_18_out, and_19_out, and_20_out, and_21_out, and_22_out, and_23_out, and_24_out, and_25_out, and_26_out, and_27_out, and_28_out, and_29_out);
  not not_97 (not_97_out, op0);
  not not_98 (not_98_out, op1);
  not not_99 (not_99_out, op3);
  not not_100 (not_100_out, op5);
  and and_24 (and_24_out, not_97_out, not_98_out, op2, not_99_out, op4, not_100_out);
  not not_101 (not_101_out, op0);
  not not_102 (not_102_out, op1);
  not not_103 (not_103_out, op3);
  not not_104 (not_104_out, op4);
  and and_25 (and_25_out, not_101_out, not_102_out, op2, not_103_out, not_104_out, op5);
  not not_105 (not_105_out, op0);
  not not_106 (not_106_out, op1);
  not not_107 (not_107_out, op3);
  not not_108 (not_108_out, op4);
  not not_109 (not_109_out, op5);
  and and_26 (and_26_out, not_105_out, not_106_out, op2, not_107_out, not_108_out, not_109_out);
  not not_110 (not_110_out, op0);
  not not_111 (not_111_out, op1);
  not not_112 (not_112_out, op2);
  not not_113 (not_113_out, op3);
  not not_114 (not_114_out, op5);
  and and_27 (and_27_out, not_110_out, not_111_out, not_112_out, not_113_out, op4, not_114_out);
  not not_115 (not_115_out, op0);
  not not_116 (not_116_out, op1);
  not not_117 (not_117_out, op2);
  not not_118 (not_118_out, op3);
  and and_28 (and_28_out, not_115_out, not_116_out, not_117_out, not_118_out, op4, op5);
  not not_119 (not_119_out, op0);
  not not_120 (not_120_out, op2);
  not not_121 (not_121_out, op3);
  not not_122 (not_122_out, op4);
  not not_123 (not_123_out, op5);
  and and_29 (and_29_out, not_119_out, op1, not_120_out, not_121_out, not_122_out, not_123_out);
endmodule

module ControlUnit (
  input  [5:0] op,
  input  [5:0] funct,
  output isShamt,
  output MemRead,
  output MemToReg,
  output MemWrite,
  output RegWrite,
  output Jump,
  output BneOrBeq,
  output Branch,
  output ALUSrc,
  output RegDst,
  output ZeroExtend,
  output isJR,
  output [3:0] ALUop,
  output ReadRs,
  output isJAL,
  output ReadRt
);

  wire functdecoder_1_isjr, functdecoder_1_isshamt, isSpecial, not_1_out, not_2_out, not_3_out, not_4_out,
       not_5_out, not_6_out, not_7_out;
  wire [3:0] aludecoder_1_aluop3, functdecoder_1_alu3;

  OpcodeDecoder opcodedecoder_1 (
    .op2(op[3]), .op3(op[2]), .op4(op[1]), .op5(op[0]), .op0(op[5]), .op1(op[4]), .Jump(Jump),
    .MemToReg(MemToReg), .Branch(Branch), .RegDst(RegDst), .MemRead(MemRead), .RegWrite(RegWrite),
    .MemWrite(MemWrite), .BneBeq(BneOrBeq), .IsJAL(isJAL), .ZeroExtend(ZeroExtend), .ALUSrc(ALUSrc));
  ALUDecoder aludecoder_1 (
    .op1(op[4]), .op2(op[3]), .op3(op[2]), .op4(op[1]), .op5(op[0]), .op0(op[5]),
    .ALUop1(aludecoder_1_aluop3[2]), .ALUop2(aludecoder_1_aluop3[1]), .ALUop3(aludecoder_1_aluop3[0]),
    .ALUop0(aludecoder_1_aluop3[3]));
  FunctDecoder functdecoder_1 (
    .Funct1(funct[4]), .Funct2(funct[3]), .Funct3(funct[2]), .Funct4(funct[1]), .Funct5(funct[0]),
    .Funct0(funct[5]), .ALU2(functdecoder_1_alu3[1]), .ALU3(functdecoder_1_alu3[0]),
    .IsJR(functdecoder_1_isjr), .IsShamt(functdecoder_1_isshamt), .ALU0(functdecoder_1_alu3[3]),
    .ALU1(functdecoder_1_alu3[2]));
  not not_1 (not_1_out, op[5]);
  not not_2 (not_2_out, op[4]);
  not not_3 (not_3_out, op[3]);
  not not_4 (not_4_out, op[2]);
  not not_5 (not_5_out, op[1]);
  not not_6 (not_6_out, op[0]);
  RegisterRead registerread_1 (
    .op2(op[3]), .op3(op[2]), .op4(op[1]), .op5(op[0]), .Funct0(funct[5]), .Funct1(funct[4]),
    .Funct2(funct[3]), .Funct3(funct[2]), .Funct4(funct[1]), .Funct5(funct[0]), .op0(op[5]), .op1(op[4]),
    .ReadRs(ReadRs), .ReadRt(ReadRt));
  and and_1 (isSpecial, not_1_out, not_2_out, not_3_out, not_4_out, not_5_out, not_6_out);
  Multiplexer multiplexer_1 (.in0(1'b0), .in1(functdecoder_1_isjr), .out(isJR), .sel(isSpecial));
  Multiplexer multiplexer_2 (.in0(1'b0), .in1(functdecoder_1_isshamt), .out(isShamt), .sel(isSpecial));
  not not_7 (not_7_out, isSpecial);
  Multiplexer #(.width(4)) multiplexer_3 (
    .in0(functdecoder_1_alu3), .in1(aludecoder_1_aluop3), .out(ALUop), .sel(not_7_out));

  // Other names for the same wires on the sheet: TisJAL = isJAL

  // Notes on the sheet:
  //   Entradas e Saidas
  //   OP Decoding Area
  //   ALU Decoding Area
endmodule
