// Logisim project jumpAddress.circ as structural Verilog: 1 circuit, main circuit JumpAddess
module JumpAddess (
  input  [25:0] Address,
  input  [31:0] PC4,
  output [31:0] JumpAddress
);


  assign JumpAddress = {PC4[31:28], Address, 2'b00};
endmodule
