// Logisim project regFile.circ as structural Verilog: 2 circuits, main circuit regFileDisplay
module regFileDisplay (
  input  [4:0] R1in,
  input  [4:0] R2in,
  input  [4:0] Rw,
  input  [31:0] inDado,
  input  WE,
  input  clk,
  input  rst,
  output [31:0] R1out,
  output [31:0] a0out,
  output [31:0] R2out,
  output [31:0] v0out,
  output [31:0] SR0,
  output [31:0] SR8,
  output [31:0] SR16,
  output [31:0] SR24,
  output [31:0] SR1,
  output [31:0] SR9,
  output [31:0] SR17,
  output [31:0] SR25,
  output [31:0] SR2,
  output [31:0] SR10,
  output [31:0] SR18,
  output [31:0] SR26,
  output [31:0] SR3,
  output [31:0] SR11,
  output [31:0] SR19,
  output [31:0] SR27,
  output [31:0] SR4,
  output [31:0] SR12,
  output [31:0] SR20,
  output [31:0] SR28,
  output [31:0] SR5,
  output [31:0] SR13,
  output [31:0] SR21,
  output [31:0] SR29,
  output [31:0] SR6,
  output [31:0] SR14,
  output [31:0] SR22,
  output [31:0] SR30,
  output [31:0] SR7,
  output [31:0] SR15,
  output [31:0] SR23,
  output [31:0] SR31
);

  wire demultiplexer_1_out0, demultiplexer_1_out1, demultiplexer_1_out2, demultiplexer_1_out3,
       demultiplexer_2_out0, demultiplexer_2_out1, demultiplexer_2_out2, demultiplexer_2_out3,
       demultiplexer_2_out4, demultiplexer_2_out5, demultiplexer_2_out6, demultiplexer_2_out7,
       demultiplexer_3_out0, demultiplexer_3_out1, demultiplexer_3_out2, demultiplexer_3_out3,
       demultiplexer_3_out4, demultiplexer_3_out5, demultiplexer_3_out6, demultiplexer_3_out7,
       demultiplexer_4_out0, demultiplexer_4_out1, demultiplexer_4_out2, demultiplexer_4_out3,
       demultiplexer_4_out4, demultiplexer_4_out5, demultiplexer_4_out6, demultiplexer_4_out7,
       demultiplexer_5_out0, demultiplexer_5_out1, demultiplexer_5_out2, demultiplexer_5_out3,
       demultiplexer_5_out4, demultiplexer_5_out5, demultiplexer_5_out6, demultiplexer_5_out7;

  Demultiplexer #(.enable("true"), .select(2)) demultiplexer_1 (
    .out0(demultiplexer_1_out0), .out1(demultiplexer_1_out1), .out2(demultiplexer_1_out2),
    .out3(demultiplexer_1_out3), .in(1'b1), .sel(Rw[4:3]), .en(WE));
  Demultiplexer #(.enable("true"), .select(3)) demultiplexer_2 (
    .out0(demultiplexer_2_out0), .out1(demultiplexer_2_out1), .out2(demultiplexer_2_out2),
    .out3(demultiplexer_2_out3), .out4(demultiplexer_2_out4), .out5(demultiplexer_2_out5),
    .out6(demultiplexer_2_out6), .out7(demultiplexer_2_out7), .in(1'b1), .sel(Rw[2:0]),
    .en(demultiplexer_1_out0));
  Demultiplexer #(.enable("true"), .select(3)) demultiplexer_3 (
    .out0(demultiplexer_3_out0), .out1(demultiplexer_3_out1), .out2(demultiplexer_3_out2),
    .out3(demultiplexer_3_out3), .out4(demultiplexer_3_out4), .out5(demultiplexer_3_out5),
    .out6(demultiplexer_3_out6), .out7(demultiplexer_3_out7), .in(1'b1), .sel(Rw[2:0]),
    .en(demultiplexer_1_out1));
  Demultiplexer #(.enable("true"), .select(3)) demultiplexer_4 (
    .out0(demultiplexer_4_out0), .out1(demultiplexer_4_out1), .out2(demultiplexer_4_out2),
    .out3(demultiplexer_4_out3), .out4(demultiplexer_4_out4), .out5(demultiplexer_4_out5),
    .out6(demultiplexer_4_out6), .out7(demultiplexer_4_out7), .in(1'b1), .sel(Rw[2:0]),
    .en(demultiplexer_1_out2));
  Demultiplexer #(.enable("true"), .select(3)) demultiplexer_5 (
    .out0(demultiplexer_5_out0), .out1(demultiplexer_5_out1), .out2(demultiplexer_5_out2),
    .out3(demultiplexer_5_out3), .out4(demultiplexer_5_out4), .out5(demultiplexer_5_out5),
    .out6(demultiplexer_5_out6), .out7(demultiplexer_5_out7), .in(1'b1), .sel(Rw[2:0]),
    .en(demultiplexer_1_out3));
  Register #(.width(32)) zero_0 (.D(inDado), .en(demultiplexer_2_out0), .Q(SR0));  // open: clk, clr
  Register #(.width(32)) t0_8 (.D(inDado), .en(demultiplexer_3_out0), .clk(clk), .Q(SR8), .clr(rst));
  Register #(.width(32)) s0_16 (.D(inDado), .en(demultiplexer_4_out0), .clk(clk), .Q(SR16), .clr(rst));
  Register #(.width(32)) t8_24 (.D(inDado), .en(demultiplexer_5_out0), .clk(clk), .Q(SR24), .clr(rst));
  Register #(.width(32)) at_1 (.D(inDado), .en(demultiplexer_2_out1), .clk(clk), .Q(SR1), .clr(rst));
  Register #(.width(32)) t1_9 (.D(inDado), .en(demultiplexer_3_out1), .clk(clk), .Q(SR9), .clr(rst));
  Register #(.width(32)) s1_17 (.D(inDado), .en(demultiplexer_4_out1), .clk(clk), .Q(SR17), .clr(rst));
  Register #(.width(32)) t9_25 (.D(inDado), .en(demultiplexer_5_out1), .clk(clk), .Q(SR25), .clr(rst));
  Register #(.width(32)) v0_2 (.D(inDado), .en(demultiplexer_2_out2), .clk(clk), .Q(SR2), .clr(rst));
  Register #(.width(32)) t2_10 (.D(inDado), .en(demultiplexer_3_out2), .clk(clk), .Q(SR10), .clr(rst));
  Register #(.width(32)) s2_18 (.D(inDado), .en(demultiplexer_4_out2), .clk(clk), .Q(SR18), .clr(rst));
  Register #(.width(32)) k0_26 (.D(inDado), .en(demultiplexer_5_out2), .clk(clk), .Q(SR26), .clr(rst));
  Register #(.width(32)) v1_3 (.D(inDado), .en(demultiplexer_2_out3), .clk(clk), .Q(SR3), .clr(rst));
  Register #(.width(32)) t3_11 (.D(inDado), .en(demultiplexer_3_out3), .clk(clk), .Q(SR11), .clr(rst));
  Register #(.width(32)) s3_19 (.D(inDado), .en(demultiplexer_4_out3), .clk(clk), .Q(SR19), .clr(rst));
  Register #(.width(32)) k1_27 (.D(inDado), .en(demultiplexer_5_out3), .clk(clk), .Q(SR27), .clr(rst));
  Register #(.width(32)) a0_4 (.D(inDado), .en(demultiplexer_2_out4), .clk(clk), .Q(a0out), .clr(rst));
  Register #(.width(32)) t4_12 (.D(inDado), .en(demultiplexer_3_out4), .clk(clk), .Q(SR12), .clr(rst));
  Register #(.width(32)) s4_20 (.D(inDado), .en(demultiplexer_4_out4), .clk(clk), .Q(SR20), .clr(rst));
  Register #(.width(32)) gp_28 (.D(inDado), .en(demultiplexer_5_out4), .clk(clk), .Q(SR28), .clr(rst));
  Register #(.width(32)) a1_5 (.D(inDado), .en(demultiplexer_2_out5), .clk(clk), .Q(SR5), .clr(rst));
  Register #(.width(32)) t5_15 (.D(inDado), .en(demultiplexer_3_out5), .clk(clk), .Q(SR13), .clr(rst));
  Register #(.width(32)) s5_21 (.D(inDado), .en(demultiplexer_4_out5), .clk(clk), .Q(SR21), .clr(rst));
  Register #(.width(32)) sp_29 (.D(inDado), .en(demultiplexer_5_out5), .clk(clk), .Q(SR29), .clr(rst));
  Register #(.width(32)) a2_6 (.D(inDado), .en(demultiplexer_2_out6), .clk(clk), .Q(SR6), .clr(rst));
  Register #(.width(32)) t6_14 (.D(inDado), .en(demultiplexer_3_out6), .clk(clk), .Q(SR14), .clr(rst));
  Register #(.width(32)) s6_22 (.D(inDado), .en(demultiplexer_4_out6), .clk(clk), .Q(SR22), .clr(rst));
  Register #(.width(32)) fp_30 (.D(inDado), .en(demultiplexer_5_out6), .clk(clk), .Q(SR30), .clr(rst));
  Register #(.width(32)) a3_7 (.D(inDado), .en(demultiplexer_2_out7), .clk(clk), .Q(SR7), .clr(rst));
  Register #(.width(32)) t7_15 (.D(inDado), .en(demultiplexer_3_out7), .clk(clk), .Q(SR15), .clr(rst));
  Register #(.width(32)) s7_23 (.D(inDado), .en(demultiplexer_4_out7), .clk(clk), .Q(SR23), .clr(rst));
  Register #(.width(32)) ra_31 (.D(inDado), .en(demultiplexer_5_out7), .clk(clk), .Q(SR31), .clr(rst));
  Multiplexer #(.disabled("Z"), .select(5), .width(32)) multiplexer_1 (
    .in0(SR0), .in1(SR1), .in2(SR2), .in3(SR3), .in4(a0out), .in5(SR5), .in6(SR6), .in7(SR7), .in8(SR8),
    .in9(SR9), .in10(SR10), .in11(SR11), .in12(SR12), .in13(SR13), .in14(SR14), .in15(SR15), .in16(SR16),
    .in17(SR17), .in18(SR18), .in19(SR19), .in20(SR20), .in21(SR21), .in22(SR22), .in23(SR23), .in24(SR24),
    .in25(SR25), .in26(SR26), .in27(SR27), .in28(SR28), .in29(SR29), .in30(SR30), .in31(SR31), .out(R1out),
    .sel(R1in));
  Multiplexer #(.disabled("Z"), .select(5), .width(32)) multiplexer_2 (
    .in0(SR0), .in1(SR1), .in2(SR2), .in3(SR3), .in4(a0out), .in5(SR5), .in6(SR6), .in7(SR7), .in8(SR8),
    .in9(SR9), .in10(SR10), .in11(SR11), .in12(SR12), .in13(SR13), .in14(SR14), .in15(SR15), .in16(SR16),
    .in17(SR17), .in18(SR18), .in19(SR19), .in20(SR20), .in21(SR21), .in22(SR22), .in23(SR23), .in24(SR24),
    .in25(SR25), .in26(SR26), .in27(SR27), .in28(SR28), .in29(SR29), .in30(SR30), .in31(SR31), .out(R2out),
    .sel(R2in));

  assign SR4 = a0out;
  assign v0out = SR2;

  // Other names for the same wires on the sheet: T0[31:0] = SR0; T1[31:0] = SR1; T3[31:0] = SR3; T5[31:0] = SR5;
  //   T6[31:0] = SR6; T7[31:0] = SR7; T8[31:0] = SR8; T9[31:0] = SR9; T10[31:0] = SR10; T11[31:0] = SR11;
  //   T12[31:0] = SR12; T13[31:0] = SR13; T14[31:0] = SR14; T15[31:0] = SR15; T16[31:0] = SR16; T17[31:0] = SR17;
  //   T18[31:0] = SR18; T19[31:0] = SR19; T20[31:0] = SR20; T21[31:0] = SR21; T22[31:0] = SR22; T23[31:0] = SR23;
  //   T24[31:0] = SR24; T25[31:0] = SR25; T26[31:0] = SR26; T27[31:0] = SR27; T28[31:0] = SR28; T29[31:0] = SR29;
  //   T30[31:0] = SR30; T4[31:0] = a0out; Ta0[31:0] = a0out; Tclk = clk; TinDado[31:0] = inDado; TR1[4:0] = R1in;
  //   TR2[4:0] = R2in; T31[31:0] = SR31; Tra[31:0] = SR31; Treg1[31:0] = R1out; Treg2[31:0] = R2out; Trst = rst;
  //   TRw[4:0] = Rw; T2[31:0] = SR2; Tv0[31:0] = SR2; TWE = WE
endmodule

module regFile (
  input  [4:0] R1in,
  input  [4:0] R2in,
  input  [4:0] Rw,
  input  [31:0] inDado,
  input  WE,
  input  clk,
  input  rst,
  output [31:0] R1out,
  output [31:0] a0out,
  output [31:0] R2out,
  output [31:0] v0out
);

  wire demultiplexer_1_out0, demultiplexer_1_out1, demultiplexer_1_out2, demultiplexer_1_out3,
       demultiplexer_2_out0, demultiplexer_2_out1, demultiplexer_2_out2, demultiplexer_2_out3,
       demultiplexer_2_out4, demultiplexer_2_out5, demultiplexer_2_out6, demultiplexer_2_out7,
       demultiplexer_3_out0, demultiplexer_3_out1, demultiplexer_3_out2, demultiplexer_3_out3,
       demultiplexer_3_out4, demultiplexer_3_out5, demultiplexer_3_out6, demultiplexer_3_out7,
       demultiplexer_4_out0, demultiplexer_4_out1, demultiplexer_4_out2, demultiplexer_4_out3,
       demultiplexer_4_out4, demultiplexer_4_out5, demultiplexer_4_out6, demultiplexer_4_out7,
       demultiplexer_5_out0, demultiplexer_5_out1, demultiplexer_5_out2, demultiplexer_5_out3,
       demultiplexer_5_out4, demultiplexer_5_out5, demultiplexer_5_out6, demultiplexer_5_out7;
  wire [31:0] a1_5_q, a2_6_q, a3_7_q, at_1_q, fp_30_q, gp_28_q, k0_26_q, k1_27_q, s0_16_q, s1_17_q, s2_18_q,
       s3_19_q, s4_20_q, s5_21_q, s6_22_q, s7_23_q, sp_29_q, t0_8_q, t1_9_q, t2_10_q, t3_11_q, t4_12_q,
       t5_15_q, t6_14_q, t7_15_q, t8_24_q, t9_25_q, Tra, v1_3_q, zero_0_q;

  Demultiplexer #(.enable("true"), .select(2)) demultiplexer_1 (
    .out0(demultiplexer_1_out0), .out1(demultiplexer_1_out1), .out2(demultiplexer_1_out2),
    .out3(demultiplexer_1_out3), .in(1'b1), .sel(Rw[4:3]), .en(WE));
  Demultiplexer #(.enable("true"), .select(3)) demultiplexer_2 (
    .out0(demultiplexer_2_out0), .out1(demultiplexer_2_out1), .out2(demultiplexer_2_out2),
    .out3(demultiplexer_2_out3), .out4(demultiplexer_2_out4), .out5(demultiplexer_2_out5),
    .out6(demultiplexer_2_out6), .out7(demultiplexer_2_out7), .in(1'b1), .sel(Rw[2:0]),
    .en(demultiplexer_1_out0));
  Demultiplexer #(.enable("true"), .select(3)) demultiplexer_3 (
    .out0(demultiplexer_3_out0), .out1(demultiplexer_3_out1), .out2(demultiplexer_3_out2),
    .out3(demultiplexer_3_out3), .out4(demultiplexer_3_out4), .out5(demultiplexer_3_out5),
    .out6(demultiplexer_3_out6), .out7(demultiplexer_3_out7), .in(1'b1), .sel(Rw[2:0]),
    .en(demultiplexer_1_out1));
  Demultiplexer #(.enable("true"), .select(3)) demultiplexer_4 (
    .out0(demultiplexer_4_out0), .out1(demultiplexer_4_out1), .out2(demultiplexer_4_out2),
    .out3(demultiplexer_4_out3), .out4(demultiplexer_4_out4), .out5(demultiplexer_4_out5),
    .out6(demultiplexer_4_out6), .out7(demultiplexer_4_out7), .in(1'b1), .sel(Rw[2:0]),
    .en(demultiplexer_1_out2));
  Demultiplexer #(.enable("true"), .select(3)) demultiplexer_5 (
    .out0(demultiplexer_5_out0), .out1(demultiplexer_5_out1), .out2(demultiplexer_5_out2),
    .out3(demultiplexer_5_out3), .out4(demultiplexer_5_out4), .out5(demultiplexer_5_out5),
    .out6(demultiplexer_5_out6), .out7(demultiplexer_5_out7), .in(1'b1), .sel(Rw[2:0]),
    .en(demultiplexer_1_out3));
  Register #(.width(32)) zero_0 (.D(inDado), .en(demultiplexer_2_out0), .Q(zero_0_q));  // open: clk, clr
  Register #(.width(32)) t0_8 (.D(inDado), .en(demultiplexer_3_out0), .clk(clk), .Q(t0_8_q), .clr(rst));
  Register #(.width(32)) s0_16 (.D(inDado), .en(demultiplexer_4_out0), .clk(clk), .Q(s0_16_q), .clr(rst));
  Register #(.width(32)) t8_24 (.D(inDado), .en(demultiplexer_5_out0), .clk(clk), .Q(t8_24_q), .clr(rst));
  Register #(.width(32)) at_1 (.D(inDado), .en(demultiplexer_2_out1), .clk(clk), .Q(at_1_q), .clr(rst));
  Register #(.width(32)) t1_9 (.D(inDado), .en(demultiplexer_3_out1), .clk(clk), .Q(t1_9_q), .clr(rst));
  Register #(.width(32)) s1_17 (.D(inDado), .en(demultiplexer_4_out1), .clk(clk), .Q(s1_17_q), .clr(rst));
  Register #(.width(32)) t9_25 (.D(inDado), .en(demultiplexer_5_out1), .clk(clk), .Q(t9_25_q), .clr(rst));
  Register #(.width(32)) v0_2 (.D(inDado), .en(demultiplexer_2_out2), .clk(clk), .Q(v0out), .clr(rst));
  Register #(.width(32)) t2_10 (.D(inDado), .en(demultiplexer_3_out2), .clk(clk), .Q(t2_10_q), .clr(rst));
  Register #(.width(32)) s2_18 (.D(inDado), .en(demultiplexer_4_out2), .clk(clk), .Q(s2_18_q), .clr(rst));
  Register #(.width(32)) k0_26 (.D(inDado), .en(demultiplexer_5_out2), .clk(clk), .Q(k0_26_q), .clr(rst));
  Register #(.width(32)) v1_3 (.D(inDado), .en(demultiplexer_2_out3), .clk(clk), .Q(v1_3_q), .clr(rst));
  Register #(.width(32)) t3_11 (.D(inDado), .en(demultiplexer_3_out3), .clk(clk), .Q(t3_11_q), .clr(rst));
  Register #(.width(32)) s3_19 (.D(inDado), .en(demultiplexer_4_out3), .clk(clk), .Q(s3_19_q), .clr(rst));
  Register #(.width(32)) k1_27 (.D(inDado), .en(demultiplexer_5_out3), .clk(clk), .Q(k1_27_q), .clr(rst));
  Register #(.width(32)) a0_4 (.D(inDado), .en(demultiplexer_2_out4), .clk(clk), .Q(a0out), .clr(rst));
  Register #(.width(32)) t4_12 (.D(inDado), .en(demultiplexer_3_out4), .clk(clk), .Q(t4_12_q), .clr(rst));
  Register #(.width(32)) s4_20 (.D(inDado), .en(demultiplexer_4_out4), .clk(clk), .Q(s4_20_q), .clr(rst));
  Register #(.width(32)) gp_28 (.D(inDado), .en(demultiplexer_5_out4), .clk(clk), .Q(gp_28_q), .clr(rst));
  Register #(.width(32)) a1_5 (.D(inDado), .en(demultiplexer_2_out5), .clk(clk), .Q(a1_5_q), .clr(rst));
  Register #(.width(32)) t5_15 (.D(inDado), .en(demultiplexer_3_out5), .clk(clk), .Q(t5_15_q), .clr(rst));
  Register #(.width(32)) s5_21 (.D(inDado), .en(demultiplexer_4_out5), .clk(clk), .Q(s5_21_q), .clr(rst));
  Register #(.width(32)) sp_29 (.D(inDado), .en(demultiplexer_5_out5), .clk(clk), .Q(sp_29_q), .clr(rst));
  Register #(.width(32)) a2_6 (.D(inDado), .en(demultiplexer_2_out6), .clk(clk), .Q(a2_6_q), .clr(rst));
  Register #(.width(32)) t6_14 (.D(inDado), .en(demultiplexer_3_out6), .clk(clk), .Q(t6_14_q), .clr(rst));
  Register #(.width(32)) s6_22 (.D(inDado), .en(demultiplexer_4_out6), .clk(clk), .Q(s6_22_q), .clr(rst));
  Register #(.width(32)) fp_30 (.D(inDado), .en(demultiplexer_5_out6), .clk(clk), .Q(fp_30_q), .clr(rst));
  Register #(.width(32)) a3_7 (.D(inDado), .en(demultiplexer_2_out7), .clk(clk), .Q(a3_7_q), .clr(rst));
  Register #(.width(32)) t7_15 (.D(inDado), .en(demultiplexer_3_out7), .clk(clk), .Q(t7_15_q), .clr(rst));
  Register #(.width(32)) s7_23 (.D(inDado), .en(demultiplexer_4_out7), .clk(clk), .Q(s7_23_q), .clr(rst));
  Register #(.width(32)) ra_31 (.D(inDado), .en(demultiplexer_5_out7), .clk(clk), .Q(Tra), .clr(rst));
  Multiplexer #(.disabled("Z"), .select(5), .width(32)) multiplexer_1 (
    .in0(zero_0_q), .in1(at_1_q), .in2(v0out), .in3(v1_3_q), .in4(a0out), .in5(a1_5_q), .in6(a2_6_q),
    .in7(a3_7_q), .in8(t0_8_q), .in9(t1_9_q), .in10(t2_10_q), .in11(t3_11_q), .in12(t4_12_q), .in13(t5_15_q),
    .in14(t6_14_q), .in15(t7_15_q), .in16(s0_16_q), .in17(s1_17_q), .in18(s2_18_q), .in19(s3_19_q),
    .in20(s4_20_q), .in21(s5_21_q), .in22(s6_22_q), .in23(s7_23_q), .in24(t8_24_q), .in25(t9_25_q),
    .in26(k0_26_q), .in27(k1_27_q), .in28(gp_28_q), .in29(sp_29_q), .in30(fp_30_q), .in31(Tra), .out(R1out),
    .sel(R1in));
  Multiplexer #(.disabled("Z"), .select(5), .width(32)) multiplexer_2 (
    .in0(zero_0_q), .in1(at_1_q), .in2(v0out), .in3(v1_3_q), .in4(a0out), .in5(a1_5_q), .in6(a2_6_q),
    .in7(a3_7_q), .in8(t0_8_q), .in9(t1_9_q), .in10(t2_10_q), .in11(t3_11_q), .in12(t4_12_q), .in13(t5_15_q),
    .in14(t6_14_q), .in15(t7_15_q), .in16(s0_16_q), .in17(s1_17_q), .in18(s2_18_q), .in19(s3_19_q),
    .in20(s4_20_q), .in21(s5_21_q), .in22(s6_22_q), .in23(s7_23_q), .in24(t8_24_q), .in25(t9_25_q),
    .in26(k0_26_q), .in27(k1_27_q), .in28(gp_28_q), .in29(sp_29_q), .in30(fp_30_q), .in31(Tra), .out(R2out),
    .sel(R2in));

  // Other names for the same wires on the sheet: Ta0[31:0] = a0out; Tclk = clk; TinDado[31:0] = inDado;
  //   TR1[4:0] = R1in; TR2[4:0] = R2in; Treg1[31:0] = R1out; Treg2[31:0] = R2out; Trst = rst; TRw[4:0] = Rw;
  //   Tv0[31:0] = v0out; TWE = WE
endmodule
