// Logisim project datapath.circ as structural Verilog: 7 circuits, main circuit main
module main (
  input  ClearPC,
  input  ClearMem,
  input  in_3
);

  wire and_1_out, clock_1_out, Controller_branch, Controller_escrevemem, Controller_escrevereg,
       Controller_jump, Controller_lemem, Controller_memparareg, Controller_origalu, Controller_regdest,
       not_1_out, registerfile_1_p7, ULA_p4, wordaddress_1_p2, wordaddress_2_p2;
  wire [1:0] Controller_opalu;
  wire [3:0] ALUCtrl_operationsaidaaluctrl;
  wire [4:0] Decoder_rd, Decoder_rs, Decoder_rt, multiplexer_1_out;
  wire [5:0] Decoder_funct, Decoder_op;
  wire [15:0] Decoder_immediate;
  wire [25:0] Decoder_adderess;
  wire [31:0] adder_1_out, branchaddr_1_branchaddress, complementadorsinal_1_address32ext, counter_1_q,
       jmpaddress_1_jumpaddress, mips_ram_1_p5, mips_ram_2_p4, multiplexer_2_out, multiplexer_3_out,
       multiplexer_4_out, registerfile_1_p1, registerfile_1_p8, ULA_p5;

  Counter #(.width(32), .max('hffffffff)) counter_1 (
    .clr(ClearPC), .load(1'b1), .clk(clock_1_out), .D(multiplexer_4_out), .Q(counter_1_q));  // open: up, count, carry
  Clock clock_1 (.out(clock_1_out));
  Adder #(.width(32)) adder_1 (.a(32'h4), .b(counter_1_q), .out(adder_1_out));  // open: cin, cout
  // WordAddress wordaddress_1: pin names not known; wires that end beside it: counter_1_q, wordaddress_1_p2, wordaddress_1_p2, 1'b0
  // MIPS_RAM mips_ram_1: pin names not known; wires that end beside it: 4'b1111, 1'b0, 1'b1, ClearMem, mips_ram_1_p5
  JmpAddress jmpaddress_1 (.Address(Decoder_adderess), .PC4(adder_1_out), .JumpAddress(jmpaddress_1_jumpaddress));
  InstructionDec Decoder (
    .Instruction(mips_ram_1_p5), .op(Decoder_op), .rs(Decoder_rs), .rt(Decoder_rt), .rd(Decoder_rd),
    .funct(Decoder_funct), .immediate(Decoder_immediate), .adderess(Decoder_adderess));  // open: shamt
  Multiplexer #(.width(5), .enable("false")) multiplexer_1 (
    .in0(Decoder_rt), .in1(Decoder_rd), .out(multiplexer_1_out), .sel(Controller_regdest));
  Control Controller (
    .op(Decoder_op), .RegDest(Controller_regdest), .Branch(Controller_branch), .LeMem(Controller_lemem),
    .MemParaReg(Controller_memparareg), .OpALU(Controller_opalu), .EscreveMem(Controller_escrevemem),
    .OrigALU(Controller_origalu), .EscreveReg(Controller_escrevereg), .Jump(Controller_jump));
  not not_1 (not_1_out, clock_1_out);
  ComplementadorSinal complementadorsinal_1 (
    .address16(Decoder_immediate), .address32ext(complementadorsinal_1_address32ext));
  // RegisterFile registerfile_1: pin names not known; wires that end beside it: registerfile_1_p1, not_1_out, Controller_escrevereg, multiplexer_1_out, Decoder_rs, Decoder_rt, registerfile_1_p7, registerfile_1_p8
  Multiplexer #(.width(32), .enable("false")) multiplexer_2 (
    .in0(registerfile_1_p8), .in1(complementadorsinal_1_address32ext), .out(multiplexer_2_out),
    .sel(Controller_origalu));
  ALUcontrol ALUCtrl (
    .functALUctrl(Decoder_funct), .OpALUctrl(Controller_opalu),
    .OperationSaidaAluCtrl(ALUCtrl_operationsaidaaluctrl));
  // ALU ULA: pin names not known; wires that end beside it: registerfile_1_p7, multiplexer_2_out, ALUCtrl_operationsaidaaluctrl, ULA_p4, ULA_p5
  BranchAddr branchaddr_1 (
    .PC4(adder_1_out), .Address(complementadorsinal_1_address32ext),
    .BranchAddress(branchaddr_1_branchaddress));
  and and_1 (and_1_out, Controller_branch, ULA_p4);
  // WordAddress wordaddress_2: pin names not known; wires that end beside it: ULA_p5, wordaddress_2_p2, wordaddress_2_p2, registerfile_1_p8, Controller_escrevemem, 4'b1111
  Multiplexer #(.width(32), .enable("false")) multiplexer_3 (
    .in0(adder_1_out), .in1(branchaddr_1_branchaddress), .out(multiplexer_3_out), .sel(and_1_out));
  Multiplexer #(.width(32), .enable("false")) multiplexer_4 (
    .in0(multiplexer_3_out), .in1(jmpaddress_1_jumpaddress), .out(multiplexer_4_out), .sel(Controller_jump));
  Multiplexer #(.width(32), .enable("false")) multiplexer_5 (
    .in0(ULA_p5), .in1(mips_ram_2_p4), .out(registerfile_1_p1), .sel(Controller_memparareg));
  // MIPS_RAM mips_ram_2: pin names not known; wires that end beside it: clock_1_out, Controller_lemem, in_3, mips_ram_2_p4

  // Notes on the sheet:
  //   aaaaaaaaaaaaaaaaaaaaaaaaaaaaaaaaa
  //   aaaaaaaaaaaaaaaaaaaaaaaaaaaaaaaaa
endmodule

module Control (
  input  [5:0] op,
  output RegDest,
  output Branch,
  output LeMem,
  output MemParaReg,
  output [1:0] OpALU,
  output EscreveMem,
  output OrigALU,
  output EscreveReg,
  output Jump
);

  wire and_6_out, not_1_out, not_2_out, not_3_out, not_4_out, not_5_out, not_6_out, not_7_out, not_8_out,
       not_9_out, not_10_out, not_11_out, not_12_out, not_13_out, not_14_out, not_15_out, not_16_out,
       not_17_out, not_18_out, not_19_out, not_20_out, not_21_out, not_22_out, not_23_out, not_24_out,
       not_25_out;

  not not_1 (not_1_out, op[1]);
  not not_2 (not_2_out, op[3]);
  not not_3 (not_3_out, op[0]);
  not not_4 (not_4_out, op[5]);
  not not_5 (not_5_out, op[4]);
  not not_6 (not_6_out, op[2]);
  and and_1 (OpALU[1], not_4_out, not_5_out, not_2_out, not_6_out, not_1_out, not_3_out);
  not not_7 (not_7_out, op[2]);
  not not_8 (not_8_out, op[3]);
  not not_9 (not_9_out, op[4]);
  and and_2 (LeMem, op[5], not_9_out, not_8_out, not_7_out, op[1], op[0]);
  not not_10 (not_10_out, op[4]);
  not not_11 (not_11_out, op[2]);
  and and_3 (EscreveMem, op[5], not_10_out, op[3], not_11_out, op[1], op[0]);
  not not_12 (not_12_out, op[5]);
  not not_13 (not_13_out, op[3]);
  not not_14 (not_14_out, op[4]);
  and and_4 (Branch, not_12_out, not_14_out, not_13_out, op[2], not_19_out, not_18_out);
  not not_15 (not_15_out, op[3]);
  not not_16 (not_16_out, op[5]);
  not not_17 (not_17_out, op[4]);
  not not_18 (not_18_out, op[0]);
  not not_19 (not_19_out, op[1]);
  and and_5 (Jump, not_16_out, not_17_out, not_15_out, op[2], not_21_out, op[0]);
  or or_1 (OrigALU, LeMem, EscreveMem);
  or or_2 (EscreveReg, OpALU[1], LeMem, and_6_out);
  not not_20 (not_20_out, op[5]);
  not not_21 (not_21_out, op[1]);
  not not_22 (not_22_out, op[4]);
  not not_23 (not_23_out, op[1]);
  not not_24 (not_24_out, op[2]);
  not not_25 (not_25_out, op[0]);
  and and_6 (and_6_out, not_20_out, not_22_out, op[3], not_24_out, not_23_out, not_25_out);

  assign MemParaReg = LeMem;
  assign OpALU[0] = Branch;
  assign RegDest = OpALU[1];

  // Notes on the sheet:
  //   R-Format
  //   lw
  //   sw
  //   beq
  //   jump
  //   addi
  //   aaaaaa
endmodule

module ALUcontrol (
  input  [1:0] OpALUctrl,
  input  [5:0] functALUctrl,
  output [3:0] OperationSaidaAluCtrl
);

  wire and_2_out, not_1_out, not_2_out, not_3_out, or_1_out;

  or or_1 (or_1_out, functALUctrl[3], functALUctrl[0]);
  and and_1 (OperationSaidaAluCtrl[0], OpALUctrl[1], or_1_out);
  not not_1 (not_1_out, OpALUctrl[0]);
  and and_2 (and_2_out, OpALUctrl[1], functALUctrl[1]);
  not not_2 (not_2_out, OpALUctrl[1]);
  not not_3 (not_3_out, functALUctrl[2]);
  and and_3 (OperationSaidaAluCtrl[3], OpALUctrl[0], not_1_out);
  or or_2 (OperationSaidaAluCtrl[2], OpALUctrl[0], and_2_out);
  or or_3 (OperationSaidaAluCtrl[1], not_2_out, not_3_out);
endmodule

module InstructionDec (
  input  [31:0] Instruction,
  output [5:0] op,
  output [4:0] rs,
  output [4:0] rt,
  output [4:0] rd,
  output [4:0] shamt,
  output [5:0] funct,
  output [15:0] immediate,
  output [25:0] adderess
);


  assign adderess = Instruction[25:0];
  assign funct = Instruction[5:0];
  assign immediate = Instruction[15:0];
  assign op = Instruction[31:26];
  assign rd = Instruction[15:11];
  assign rs = Instruction[25:21];
  assign rt = Instruction[20:16];
  assign shamt = Instruction[10:6];

  // Notes on the sheet:
  //   J-Type
  //   I-Type
  //   R-Type
endmodule

module JmpAddress (
  input  [25:0] Address,
  input  [31:0] PC4,
  output [31:0] JumpAddress
);


  assign JumpAddress = {PC4[31:28], Address, 2'b00};
endmodule

module BranchAddr (
  input  [31:0] PC4,
  input  [31:0] Address,
  output [31:0] BranchAddress
);

  Adder #(.width(32)) adder_1 (.a(PC4), .b({Address[29:0], 2'b00}), .out(BranchAddress));  // open: cin, cout
endmodule

module ComplementadorSinal (
  input  [15:0] address16,
  output [31:0] address32ext
);


  assign address32ext = {{17{address16[15]}}, address16[14:0]};
endmodule
