// Logisim project datapath.circ as structural Verilog: 20 circuits, main circuit main
module main (
  input  in_1,
  input  ClearPC,
  input  in_3,
  input  in_4,
  input  in_5,
  input  in_6,
  output out_7,
  output out_8,
  output out_9,
  output out_10
);

  wire disablePC, hazardcontrol_1_flushif_hazard, hazardcontrol_1_stallid_hazard, not_1_out, not_2_out,
       not_3_out, palu_1_isequal, TALUSrc, TALUSrcEX, TBneOrBeq, TBneOrBeqEX, TBranch, TBranch_3, TBranchEX,
       TFlushIdHazard, TisJR, TisJREX, TisJump, TisJumpEX, TisShamt, TisShamtEX, TIsToBranchOrJump, TMemRead,
       TMemReadEX, TMemReadMEM, TMemToReg, TMemToRegEX, TMemToRegMEM, TMemToRegWB, TMemWrite, TMemWriteEx,
       TMemWriteMEM, TReadRsHazard, TReadRtHazard, TRegDst, TRegWrite, TRegWriteEX, TRegWriteMEM,
       TWriteEnable, TZeroExtd, xor_1_out;
  wire [3:0] TALUOp, TALUOp_ID;
  wire [4:0] multiplexer_4_out, Trd, Trs, Trt, Tshamt, TWriteReg_5, TWriteRegEX, TWriteRegMEM;
  wire [5:0] Decoder_funct, Decoder_op;
  wire [15:0] Timmediate;
  wire [25:0] TAddress;
  wire [31:0] bit_extender_1_out, multiplexer_1_out, multiplexer_2_out, multiplexer_3_out, multiplexer_5_out,
       multiplexer_6_out, multiplexer_7_out, PCPLUS4_1, ram_1_dout, register_1_q, shifter_1_out, T_WB_DATA_5,
       TALUResultEX, TALUResultMEM, TALUResultWB, TImmediate_ID, TImmEX, Tinstruction, TinstructionIF,
       TJumpAddr_3, TJumpAddr_ID, TJumpAddrEX, TJumpAddrMEM, TJumpADDRWB, TPCPlus4EX, Tpcplus4IF, TR1_ID,
       TR1EX, TR2_ID, TReadDataWB, TShamtEX, TWriteDataEx, TWriteDataMEM;

  Multiplexer #(.width(32), .disabled("Z"), .enable("false")) multiplexer_1 (
    .in0(PCPLUS4_1), .in1(TJumpAddr_3), .out(multiplexer_1_out), .sel(TBranch_3));
  Multiplexer #(.width(32), .disabled("Z"), .enable("false")) multiplexer_2 (
    .in0(multiplexer_1_out), .in1(TJumpAddrEX), .out(multiplexer_2_out), .sel(TisJumpEX));
  Multiplexer #(.width(32), .disabled("Z"), .enable("false")) multiplexer_3 (
    .in0(multiplexer_2_out), .in1(TR1EX), .out(multiplexer_3_out), .sel(TisJREX));
  not not_1 (not_1_out, disablePC);
  Register #(.width(32)) register_1 (
    .D(multiplexer_3_out), .en(not_1_out), .clk(out_7), .Q(register_1_q), .clr(ClearPC));
  Clock clock_1 (.out(out_7));
  Adder #(.width(32)) adder_1 (.a(register_1_q), .b(32'h4), .out(PCPLUS4_1));  // open: cin, cout
  ROM #(.addrWidth(10), .dataWidth(32)) rom_1 (.addr(register_1_q[11:2]), .data(Tinstruction));
  HazardControl hazardcontrol_1 (
    .FlushIF_hazard(hazardcontrol_1_flushif_hazard), .RT_hazard(Trt), .clk_hazard(out_7),
    .RegWriteMEM_hazard(TRegWriteMEM), .WirteRegEX_hazard(TWriteRegEX), .RS_hazard(Trs),
    .isToBranchOrJump_hazard(TIsToBranchOrJump), .readRt_hazard(TReadRtHazard),
    .RegWriteEX_hazard(TRegWriteEX), .WriteRegMEM_hazard(TWriteRegMEM), .readRs_hazard(TReadRsHazard),
    .FlushID_hazard(TFlushIdHazard), .StallIF_hazard(disablePC),
    .StallID_hazard(hazardcontrol_1_stallid_hazard));
  // Probe on Tinstruction
  IF_ID if_id_1 (
    .Enable_if_id(not_2_out), .clk_if_id(out_7), .clr_if_id(hazardcontrol_1_flushif_hazard),
    .Instruction_ID(TinstructionIF), .PCPlus4_IF(PCPLUS4_1), .PCPus4_ID(Tpcplus4IF),
    .Instruction_IF(Tinstruction));
  not not_2 (not_2_out, hazardcontrol_1_stallid_hazard);
  // Probe on TinstructionIF
  // Probe on Tpcplus4IF
  JmpAddress jmpaddress_1 (.Address(TAddress), .PC4(Tpcplus4IF), .JumpAddress(TJumpAddr_ID));
  InstructionDec Decoder (
    .Instruction(TinstructionIF), .op(Decoder_op), .rs(Trs), .rt(Trt), .rd(Trd), .shamt(Tshamt),
    .funct(Decoder_funct), .immediate(Timmediate), .adderess(TAddress));
  ComplementadorSinal complementadorsinal_1 (
    .ZeroExtend(TZeroExtd), .address16(Timmediate), .address32ext(TImmediate_ID));
  ControlUnit controlunit_1 (
    .MemToReg(TMemToReg), .isShamt(TisShamt), .MemRead(TMemRead), .Branch(TBranch), .Jump(TisJump),
    .ZeroExtend(TZeroExtd), .in_1(Decoder_op), .BneOrBeq(TBneOrBeq), .RegWrite(TRegWrite),
    .MemWrite(TMemWrite), .RegDst(TRegDst), .ReadRs(TReadRsHazard), .isJR(TisJR), .ALUop(TALUOp_ID),
    .ALUSrc(TALUSrc), .ReadRt(TReadRtHazard), .in_2(Decoder_funct));
  not not_3 (not_3_out, out_7);
  // RegisterFile registerfile_1: pin names not known; wires that end beside it: T_WB_DATA_5, not_3_out, in_5, TWriteEnable, TWriteReg_5, Trs, Trt, TR1_ID, TR2_ID
  assign bit_extender_1_out = {{27{1'b0}}, Tshamt};  // Bit_Extender bit_extender_1
  Multiplexer #(.width(5), .disabled("Z"), .enable("false")) multiplexer_4 (
    .in0(Trt), .in1(Trd), .out(multiplexer_4_out), .sel(TRegDst));
  ID_EX id_ex_1 (
    .RegWrite_ID(TRegWrite), .isSham_ID(TisShamt), .WriteReg_ID(multiplexer_4_out), .enable_id_ex(1'b1),
    .ALUSrc_ID(TALUSrc), .JumpAddr_ID(TJumpAddr_ID), .MemToReg_EX(TMemToRegEX), .MemWrite_ID(TMemWrite),
    .Sham_ID(bit_extender_1_out), .isJump_ID(TisJump), .Imm_EX(TImmEX), .Branch_ID(TBranch), .R1_ID(TR1_ID),
    .Branch_EX(TBranchEX), .ALUOp_ID(TALUOp_ID), .Imm_ID(TImmediate_ID), .BneOrBeq_ID(TBneOrBeq),
    .Sham_EX(TShamtEX), .MemToReg_ID(TMemToReg), .is_JR_ID(TisJR), .ALUSrc_EX(TALUSrcEX), .R2_ID(TR2_ID),
    .clr_ID_EX(TFlushIdHazard), .PCPlus4_ID(Tpcplus4IF), .isSham_EX(TisShamtEX), .MemRead_ID(TMemRead),
    .clk_ID_EX(out_7), .MemRead_EX(TMemReadEX), .isJR_EX(TisJREX), .R1_EX(TR1EX), .JumpAddr_EX(TJumpAddrEX),
    .RegWrite_EX(TRegWriteEX), .MemWrite_EX(TMemWriteEx), .ALUOp_EX(TALUOp), .R2_EX(TWriteDataEx),
    .PCPus4_EX(TPCPlus4EX), .BneOrBeq_EX(TBneOrBeqEX), .isJump_EX(TisJumpEX), .WriteReg_EX(TWriteRegEX));
  Multiplexer #(.width(32), .disabled("Z"), .enable("false")) multiplexer_5 (
    .in0(TR1EX), .in1(TWriteDataEx), .out(multiplexer_5_out), .sel(TisShamtEX));
  Multiplexer #(.width(32), .disabled("Z"), .enable("false")) multiplexer_6 (
    .in0(TWriteDataEx), .in1(TShamtEX), .out(multiplexer_6_out), .sel(TisShamtEX));
  Multiplexer #(.width(32), .disabled("Z"), .enable("false")) multiplexer_7 (
    .in0(multiplexer_6_out), .in1(TImmEX), .out(multiplexer_7_out), .sel(TALUSrcEX));
  Shifter #(.width(32)) shifter_1 (.in(TImmEX), .\dist (5'b00010), .out(shifter_1_out));
  Adder #(.width(32)) adder_2 (.a(TPCPlus4EX), .b(shifter_1_out), .out(TJumpAddr_3));  // open: cin, cout
  or or_1 (TIsToBranchOrJump, TisJREX, TBranch_3, TisJumpEX);
  pALU palu_1 (
    .X(multiplexer_5_out), .Y(multiplexer_7_out), .ALUOp(TALUOp), .Result1(TALUResultEX),
    .isEqual(palu_1_isequal));  // open: SignedOverflow, UnsignedOverflow, Result2
  xor xor_1 (xor_1_out, palu_1_isequal, TBneOrBeqEX);
  and and_1 (TBranch_3, xor_1_out, TBranchEX);
  EX_MEM ex_mem_1 (
    .ALUResult_MEM(TALUResultMEM), .JumpAddr_EX(TPCPlus4EX), .WriteData_MEM(TWriteDataMEM),
    .RegWrite_Ex(TRegWriteEX), .RegWrite_MEM(TRegWriteMEM), .MemRead_Ex(TMemReadEX), .clr_EX_MEM(in_3),
    .WriteData_EX(TWriteDataEx), .Enable_EX_MEM(1'b1), .WriteReg_EX(TWriteRegEX), .clk_EX_MEM(out_7),
    .MemToReg_Ex(TMemToRegEX), .MemToReg_MEM(TMemToRegMEM), .MemWrite_EX(TMemWriteEx),
    .ALU_Result_EX(TALUResultEX), .MemRead_MEM(TMemReadMEM), .JumpAddr_MEM(TJumpAddrMEM),
    .MemWrite_MEM(TMemWriteMEM), .WriteReg_MEM(TWriteRegMEM));
  RAM #(.addrWidth(10), .dataWidth(32), .trigger("falling"), .databus("bibus")) ram_1 (
    .addr(TALUResultMEM[11:2]), .we(TMemWriteMEM), .oe(TMemReadMEM), .clk(out_7), .din(TWriteDataMEM),
    .dout(ram_1_dout));
  MEM_WB mem_wb_1 (
    .memToReg_wb(TMemToRegWB), .ALUResult_wb(TALUResultWB), .enable_mem_wb(1'b1), .JumpAddrMem(ram_1_dout),
    .writeReg_mem(TWriteRegMEM), .ReadData_mem(TJumpAddrMEM), .regWrite_mem(TRegWriteMEM),
    .memToReg_mem(TMemToRegMEM), .ALUResult_mem(TALUResultMEM), .clr_mem_wb(in_3), .clk_mem_wb(out_7),
    .regWrite_wb(TWriteEnable), .ReadData_wb(TReadDataWB), .writeReg_wb(TWriteReg_5),
    .JumpAddr_wb(TJumpADDRWB));
  Multiplexer #(.width(32), .enable("false")) multiplexer_8 (
    .in0(TALUResultWB), .in1(TJumpADDRWB), .out(T_WB_DATA_5), .sel(TMemToRegWB));

  assign out_8 = out_7;
  assign out_9 = out_7;
  assign out_10 = out_7;

  // Other names for the same wires on the sheet: TClearPipeline = in_3; Tclk = out_7; Tclk2 = in_4

  // Notes on the sheet:
  //   contents of rom_1 (hex, n*v repeats v):
  //   8c0a0000 8c0b0004 14b4820 ac090008 1000ffff
  //   aaaaaaaaaaaaaaaaaaaaaaaaaaaaaaaaa
  //   aaaaaaaaaaaaaaaaaaaaaaaaaaaaaaaaa
endmodule

module Control (
  input  [5:0] op,
  output RegDest,
  output Branch,
  output LeMem,
  output MemParaReg,
  output [1:0] OpALU,
  output EscreveMem,
  output OrigALU,
  output EscreveReg,
  output Jump
);

  wire and_6_out, not_1_out, not_2_out, not_3_out, not_4_out, not_5_out, not_6_out, not_7_out, not_8_out,
       not_9_out, not_10_out, not_11_out, not_12_out, not_13_out, not_14_out, not_15_out, not_16_out,
       not_17_out, not_18_out, not_19_out, not_20_out, not_21_out, not_22_out, not_23_out, not_24_out,
       not_25_out;

  not not_1 (not_1_out, op[1]);
  not not_2 (not_2_out, op[4]);
  not not_3 (not_3_out, op[5]);
  not not_4 (not_4_out, op[0]);
  not not_5 (not_5_out, op[2]);
  not not_6 (not_6_out, op[3]);
  and and_1 (OpALU[1], not_3_out, not_2_out, not_6_out, not_5_out, not_1_out, not_4_out);
  not not_7 (not_7_out, op[3]);
  not not_8 (not_8_out, op[4]);
  not not_9 (not_9_out, op[2]);
  and and_2 (LeMem, op[5], not_8_out, not_7_out, not_9_out, op[1], op[0]);
  not not_10 (not_10_out, op[4]);
  not not_11 (not_11_out, op[2]);
  and and_3 (EscreveMem, op[5], not_10_out, op[3], not_11_out, op[1], op[0]);
  not not_12 (not_12_out, op[4]);
  not not_13 (not_13_out, op[3]);
  not not_14 (not_14_out, op[5]);
  and and_4 (Branch, not_14_out, not_12_out, not_13_out, op[2], not_16_out, not_18_out);
  not not_15 (not_15_out, op[3]);
  not not_16 (not_16_out, op[1]);
  not not_17 (not_17_out, op[5]);
  not not_18 (not_18_out, op[0]);
  not not_19 (not_19_out, op[4]);
  and and_5 (Jump, not_17_out, not_19_out, not_15_out, op[2], not_22_out, op[0]);
  or or_1 (OrigALU, LeMem, EscreveMem);
  or or_2 (EscreveReg, OpALU[1], LeMem, and_6_out);
  not not_20 (not_20_out, op[4]);
  not not_21 (not_21_out, op[5]);
  not not_22 (not_22_out, op[1]);
  not not_23 (not_23_out, op[0]);
  not not_24 (not_24_out, op[2]);
  not not_25 (not_25_out, op[1]);
  and and_6 (and_6_out, not_21_out, not_20_out, op[3], not_24_out, not_25_out, not_23_out);

  assign MemParaReg = LeMem;
  assign OpALU[0] = Branch;
  assign RegDest = OpALU[1];

  // Notes on the sheet:
  //   R-Format
  //   lw
  //   sw
  //   beq
  //   jump
  //   addi
  //   aaaaaa
endmodule

module ALUcontrol (
  input  [1:0] OpALUctrl,
  input  [5:0] functALUctrl,
  output [3:0] OperationSaidaAluCtrl
);

  wire and_2_out, not_1_out, not_2_out, not_3_out, or_1_out;

  or or_1 (or_1_out, functALUctrl[3], functALUctrl[0]);
  and and_1 (OperationSaidaAluCtrl[0], OpALUctrl[1], or_1_out);
  not not_1 (not_1_out, OpALUctrl[0]);
  and and_2 (and_2_out, OpALUctrl[1], functALUctrl[1]);
  not not_2 (not_2_out, OpALUctrl[1]);
  not not_3 (not_3_out, functALUctrl[2]);
  and and_3 (OperationSaidaAluCtrl[3], OpALUctrl[0], not_1_out);
  or or_2 (OperationSaidaAluCtrl[2], OpALUctrl[0], and_2_out);
  or or_3 (OperationSaidaAluCtrl[1], not_2_out, not_3_out);
endmodule

module InstructionDec (
  input  [31:0] Instruction,
  output [5:0] op,
  output [4:0] rs,
  output [4:0] rt,
  output [4:0] rd,
  output [4:0] shamt,
  output [5:0] funct,
  output [15:0] immediate,
  output [25:0] adderess
);


  assign adderess = Instruction[25:0];
  assign funct = Instruction[5:0];
  assign immediate = Instruction[15:0];
  assign op = Instruction[31:26];
  assign rd = Instruction[15:11];
  assign rs = Instruction[25:21];
  assign rt = Instruction[20:16];
  assign shamt = Instruction[10:6];

  // Notes on the sheet:
  //   J-Type
  //   I-Type
  //   R-Type
endmodule

module JmpAddress (
  input  [25:0] Address,
  input  [31:0] PC4,
  output [31:0] JumpAddress
);


  assign JumpAddress = {PC4[31:28], Address, 2'b00};
endmodule

module BranchAddr (
  input  [31:0] PC4,
  input  [31:0] Address,
  output [31:0] BranchAddress
);

  Adder #(.width(32)) adder_1 (.a(PC4), .b({Address[29:0], 2'b00}), .out(BranchAddress));  // open: cin, cout
endmodule

module ComplementadorSinal (
  input  ZeroExtend,
  input  [15:0] address16,
  output [31:0] address32ext
);

  wire [31:0] bit_extender_1_out, bit_extender_2_out;

  assign bit_extender_1_out = {{16{address16[15]}}, address16};  // Bit_Extender bit_extender_1
  assign bit_extender_2_out = {{16{1'b0}}, address16};  // Bit_Extender bit_extender_2
  Multiplexer #(.width(32), .enable("false")) multiplexer_1 (
    .in0(bit_extender_1_out), .in1(bit_extender_2_out), .out(address32ext), .sel(ZeroExtend));
endmodule

module IF_ID (
  input  clk_if_id,
  input  clr_if_id,
  input  [31:0] Instruction_IF,
  input  [31:0] PCPlus4_IF,
  input  Enable_if_id,
  output [31:0] Instruction_ID,
  output [31:0] PCPus4_ID
);

  Register #(.width(32)) regInst_ID_IF (
    .D(Instruction_IF), .en(Enable_if_id), .clk(clk_if_id), .Q(Instruction_ID), .clr(clr_if_id));
  Register #(.width(32)) regPC_ID_IF (
    .D(PCPlus4_IF), .en(Enable_if_id), .clk(clk_if_id), .Q(PCPus4_ID), .clr(clr_if_id));
endmodule

module ID_EX (
  input  clk_ID_EX,
  input  clr_ID_EX,
  input  [31:0] Imm_ID,
  input  [31:0] Sham_ID,
  input  isSham_ID,
  input  ALUSrc_ID,
  input  Branch_ID,
  input  MemToReg_ID,
  input  MemRead_ID,
  input  is_JR_ID,
  input  [31:0] R1_ID,
  input  [31:0] JumpAddr_ID,
  input  RegWrite_ID,
  input  MemWrite_ID,
  input  [3:0] ALUOp_ID,
  input  [31:0] R2_ID,
  input  [31:0] PCPlus4_ID,
  input  BneOrBeq_ID,
  input  isJump_ID,
  input  [4:0] WriteReg_ID,
  input  enable_id_ex,
  output [31:0] Imm_EX,
  output [31:0] Sham_EX,
  output isSham_EX,
  output ALUSrc_EX,
  output Branch_EX,
  output MemToReg_EX,
  output MemRead_EX,
  output isJR_EX,
  output [31:0] R1_EX,
  output [31:0] JumpAddr_EX,
  output RegWrite_EX,
  output MemWrite_EX,
  output [3:0] ALUOp_EX,
  output [31:0] R2_EX,
  output [31:0] PCPus4_EX,
  output BneOrBeq_EX,
  output isJump_EX,
  output [4:0] WriteReg_EX
);

  Register #(.width(32)) regImm_ID_EX (.D(Imm_ID), .en(enable_id_ex), .clk(clk_ID_EX), .Q(Imm_EX), .clr(clr_ID_EX));
  Register #(.width(32)) regR1_ID_EX (.D(R1_ID), .en(enable_id_ex), .clk(clk_ID_EX), .Q(R1_EX), .clr(clr_ID_EX));
  Register #(.width(32)) regR2_ID_EX (.D(R2_ID), .en(enable_id_ex), .clk(clk_ID_EX), .Q(R2_EX), .clr(clr_ID_EX));
  Register #(.width(32)) regSham_ID_EX (.D(Sham_ID), .en(enable_id_ex), .clk(clk_ID_EX), .Q(Sham_EX), .clr(clr_ID_EX));
  Register #(.width(32)) regJump_ID_EX (
    .D(JumpAddr_ID), .en(enable_id_ex), .clk(clk_ID_EX), .Q(JumpAddr_EX), .clr(clr_ID_EX));
  Register #(.width(32)) regPC_ID_EX (
    .D(PCPlus4_ID), .en(enable_id_ex), .clk(clk_ID_EX), .Q(PCPus4_EX), .clr(clr_ID_EX));
  Register #(.width(1)) regIsSham_ID_EX (
    .D(isSham_ID), .en(enable_id_ex), .clk(clk_ID_EX), .Q(isSham_EX), .clr(clr_ID_EX));
  Register #(.width(1)) regMemToReg_ID_EX (
    .D(MemToReg_ID), .en(enable_id_ex), .clk(clk_ID_EX), .Q(MemToReg_EX), .clr(clr_ID_EX));
  Register #(.width(1)) regRegWrite_ID_EX (
    .D(RegWrite_ID), .en(enable_id_ex), .clk(clk_ID_EX), .Q(RegWrite_EX), .clr(clr_ID_EX));
  Register #(.width(1)) regBneOrBeq_ID_EX (
    .D(BneOrBeq_ID), .en(enable_id_ex), .clk(clk_ID_EX), .Q(BneOrBeq_EX), .clr(clr_ID_EX));
  Register #(.width(1)) regALUSrc_ID_EX (
    .D(ALUSrc_ID), .en(enable_id_ex), .clk(clk_ID_EX), .Q(ALUSrc_EX), .clr(clr_ID_EX));
  Register #(.width(1)) regMemRead_ID_EX (
    .D(MemRead_ID), .en(enable_id_ex), .clk(clk_ID_EX), .Q(MemRead_EX), .clr(clr_ID_EX));
  Register #(.width(1)) regMemWrite_ID_EX (
    .D(MemWrite_ID), .en(enable_id_ex), .clk(clk_ID_EX), .Q(MemWrite_EX), .clr(clr_ID_EX));
  Register #(.width(1)) regIsJump_ID_EX (
    .D(isJump_ID), .en(enable_id_ex), .clk(clk_ID_EX), .Q(isJump_EX), .clr(clr_ID_EX));
  Register #(.width(1)) regBranch_ID_EX (
    .D(Branch_ID), .en(enable_id_ex), .clk(clk_ID_EX), .Q(Branch_EX), .clr(clr_ID_EX));
  Register #(.width(1)) regIsJR_ID_EX (.D(is_JR_ID), .en(enable_id_ex), .clk(clk_ID_EX), .Q(isJR_EX), .clr(clr_ID_EX));
  Register #(.width(4)) regALUOp_ID_EX (
    .D(ALUOp_ID), .en(enable_id_ex), .clk(clk_ID_EX), .Q(ALUOp_EX), .clr(clr_ID_EX));
  Register #(.width(5)) regWriteReg_ID_EX (
    .D(WriteReg_ID), .en(enable_id_ex), .clk(clk_ID_EX), .Q(WriteReg_EX), .clr(clr_ID_EX));

  // Notes on the sheet:
  //   CLR
  //   CLK
endmodule

module MEM_WB (
  input  clk_mem_wb,
  input  clr_mem_wb,
  input  [31:0] ALUResult_mem,
  input  memToReg_mem,
  input  regWrite_mem,
  input  [31:0] ReadData_mem,
  input  [4:0] writeReg_mem,
  input  [31:0] JumpAddrMem,
  input  enable_mem_wb,
  output [31:0] ALUResult_wb,
  output memToReg_wb,
  output regWrite_wb,
  output [31:0] ReadData_wb,
  output [4:0] writeReg_wb,
  output [31:0] JumpAddr_wb
);

  Register #(.width(1)) regMemToReg (
    .D(memToReg_mem), .en(enable_mem_wb), .clk(clk_mem_wb), .Q(memToReg_wb), .clr(clr_mem_wb));
  Register #(.width(1)) regRegWrite (
    .D(regWrite_mem), .en(enable_mem_wb), .clk(clk_mem_wb), .Q(regWrite_wb), .clr(clr_mem_wb));
  Register #(.width(5)) regWriteReg (
    .D(writeReg_mem), .en(enable_mem_wb), .clk(clk_mem_wb), .Q(writeReg_wb), .clr(clr_mem_wb));
  Register #(.width(32)) regALUResult (
    .D(ALUResult_mem), .en(enable_mem_wb), .clk(clk_mem_wb), .Q(ALUResult_wb), .clr(clr_mem_wb));
  Register #(.width(32)) regReadData (
    .D(ReadData_mem), .en(enable_mem_wb), .clk(clk_mem_wb), .Q(ReadData_wb), .clr(clr_mem_wb));
  Register #(.width(32)) regJumAddr (
    .D(JumpAddrMem), .en(enable_mem_wb), .clk(clk_mem_wb), .Q(JumpAddr_wb), .clr(clr_mem_wb));
endmodule

module EX_MEM (
  input  clk_EX_MEM,
  input  clr_EX_MEM,
  input  MemToReg_Ex,
  input  [31:0] ALU_Result_EX,
  input  RegWrite_Ex,
  input  [31:0] WriteData_EX,
  input  MemRead_Ex,
  input  [31:0] JumpAddr_EX,
  input  MemWrite_EX,
  input  [4:0] WriteReg_EX,
  input  Enable_EX_MEM,
  output MemToReg_MEM,
  output [31:0] ALUResult_MEM,
  output RegWrite_MEM,
  output [31:0] WriteData_MEM,
  output MemRead_MEM,
  output [31:0] JumpAddr_MEM,
  output MemWrite_MEM,
  output [4:0] WriteReg_MEM
);

  Register #(.width(1)) regMemToReg_EX_MEM (
    .D(MemToReg_Ex), .en(Enable_EX_MEM), .clk(clk_EX_MEM), .Q(MemToReg_MEM), .clr(clr_EX_MEM));
  Register #(.width(1)) regRegWrite_EX_MEM (
    .D(RegWrite_Ex), .en(Enable_EX_MEM), .clk(clk_EX_MEM), .Q(RegWrite_MEM), .clr(clr_EX_MEM));
  Register #(.width(1)) MemRead_EX_MEM (
    .D(MemRead_Ex), .en(Enable_EX_MEM), .clk(clk_EX_MEM), .Q(MemRead_MEM), .clr(clr_EX_MEM));
  Register #(.width(1)) MemWrite_EX_MEM (
    .D(MemWrite_EX), .en(Enable_EX_MEM), .clk(clk_EX_MEM), .Q(MemWrite_MEM), .clr(clr_EX_MEM));
  Register #(.width(5)) WriteReg_EX_MEM (
    .D(WriteReg_EX), .en(Enable_EX_MEM), .clk(clk_EX_MEM), .Q(WriteReg_MEM), .clr(clr_EX_MEM));
  Register #(.width(32)) regALUResult (
    .D(ALU_Result_EX), .en(Enable_EX_MEM), .clk(clk_EX_MEM), .Q(ALUResult_MEM), .clr(clr_EX_MEM));
  Register #(.width(32)) regWriteData (
    .D(WriteData_EX), .en(Enable_EX_MEM), .clk(clk_EX_MEM), .Q(WriteData_MEM), .clr(clr_EX_MEM));
  Register #(.width(32)) regJumpAddr (
    .D(JumpAddr_EX), .en(Enable_EX_MEM), .clk(clk_EX_MEM), .Q(JumpAddr_MEM), .clr(clr_EX_MEM));
endmodule

module ControlUnit (
  input  [5:0] in_1,
  input  [5:0] in_2,
  output isShamt,
  output MemRead,
  output MemToReg,
  output MemWrite,
  output RegWrite,
  output Jump,
  output BneOrBeq,
  output Branch,
  output ALUSrc,
  output RegDst,
  output [3:0] ALUop,
  output ZeroExtend,
  output isJR,
  output ReadRs,
  output ReadRt
);

  wire functdecoder_1_isjr, functdecoder_1_isshamt, isSpecial, not_1_out, not_2_out, not_3_out, not_4_out,
       not_5_out, not_6_out, not_7_out, opcodedecoder_1_isjal;
  wire [3:0] aludecoder_1_aluop3, functdecoder_1_alu3;

  OpcodeDecoder opcodedecoder_1 (
    .op0(in_1[5]), .op1(in_1[4]), .op2(in_1[3]), .op3(in_1[2]), .op4(in_1[1]), .op5(in_1[0]),
    .MemRead(MemRead), .MemWrite(MemWrite), .BneBeq(BneOrBeq), .IsJAL(opcodedecoder_1_isjal),
    .MemToReg(MemToReg), .RegDst(RegDst), .ZeroExtend(ZeroExtend), .Jump(Jump), .Branch(Branch),
    .ALUSrc(ALUSrc), .RegWrite(RegWrite));
  ALUDecoder aludecoder_1 (
    .op0(in_1[5]), .op1(in_1[4]), .op2(in_1[3]), .op3(in_1[2]), .op4(in_1[1]), .op5(in_1[0]),
    .ALUop0(aludecoder_1_aluop3[3]), .ALUop1(aludecoder_1_aluop3[2]), .ALUop2(aludecoder_1_aluop3[1]),
    .ALUop3(aludecoder_1_aluop3[0]));
  FunctDecoder functdecoder_1 (
    .Funct0(in_2[5]), .Funct1(in_2[4]), .Funct2(in_2[3]), .Funct3(in_2[2]), .Funct4(in_2[1]),
    .Funct5(in_2[0]), .ALU0(functdecoder_1_alu3[3]), .ALU1(functdecoder_1_alu3[2]),
    .ALU2(functdecoder_1_alu3[1]), .ALU3(functdecoder_1_alu3[0]), .IsJR(functdecoder_1_isjr),
    .IsShamt(functdecoder_1_isshamt));
  not not_1 (not_1_out, isSpecial);
  RegisterRead registerread_1 (
    .op0(in_1[5]), .op1(in_1[4]), .op2(in_1[3]), .op3(in_1[2]), .op4(in_1[1]), .op5(in_1[0]),
    .Funct0(in_2[5]), .Funct1(in_2[4]), .Funct2(in_2[3]), .Funct3(in_2[2]), .Funct4(in_2[1]),
    .Funct5(in_2[0]), .ReadRt(ReadRt), .ReadRs(ReadRs));
  Multiplexer #(.width(4), .enable("false")) multiplexer_1 (
    .in0(functdecoder_1_alu3), .in1(aludecoder_1_aluop3), .out(ALUop), .sel(not_1_out));
  Multiplexer #(.enable("false")) multiplexer_2 (.in0(1'b0), .in1(functdecoder_1_isjr), .out(isJR), .sel(isSpecial));
  Multiplexer #(.enable("false")) multiplexer_3 (
    .in0(1'b0), .in1(functdecoder_1_isshamt), .out(isShamt), .sel(isSpecial));
  not not_2 (not_2_out, in_1[5]);
  not not_3 (not_3_out, in_1[4]);
  not not_4 (not_4_out, in_1[3]);
  not not_5 (not_5_out, in_1[2]);
  not not_6 (not_6_out, in_1[1]);
  not not_7 (not_7_out, in_1[0]);
  and and_1 (isSpecial, not_2_out, not_3_out, not_4_out, not_5_out, not_6_out, not_7_out);

  // Other names for the same wires on the sheet: Funct[5:0] = in_2; op[5:0] = in_1

  // Notes on the sheet:
  //   Entradas e Saidas
  //   OP Decoding Area
  //   ALU Decoding Area
endmodule

module OpcodeDecoder (
  input  op0,
  input  op1,
  input  op2,
  input  op3,
  input  op4,
  input  op5,
  output MemRead,
  output MemWrite,
  output BneBeq,
  output IsJAL,
  output MemToReg,
  output RegDst,
  output ZeroExtend,
  output Jump,
  output Branch,
  output ALUSrc,
  output RegWrite
);

  wire and_3_out, and_4_out, and_5_out, and_6_out, and_7_out, and_8_out, and_9_out, and_10_out, and_11_out,
       and_12_out, and_14_out, and_15_out, and_17_out, and_18_out, and_19_out, and_20_out, and_21_out,
       and_22_out, and_23_out, and_24_out, and_25_out, and_26_out, and_29_out, and_30_out, not_1_out,
       not_2_out, not_3_out, not_4_out, not_5_out, not_6_out, not_7_out, not_8_out, not_9_out, not_10_out,
       not_11_out, not_12_out, not_13_out, not_14_out, not_15_out, not_16_out, not_17_out, not_18_out,
       not_19_out, not_20_out, not_21_out, not_22_out, not_23_out, not_24_out, not_25_out, not_26_out,
       not_27_out, not_28_out, not_29_out, not_30_out, not_31_out, not_32_out, not_33_out, not_34_out,
       not_35_out, not_36_out, not_37_out, not_38_out, not_39_out, not_40_out, not_41_out, not_42_out,
       not_43_out, not_44_out, not_45_out, not_46_out, not_47_out, not_48_out, not_49_out, not_50_out,
       not_51_out, not_52_out, not_53_out, not_54_out, not_55_out, not_56_out, not_57_out, not_58_out,
       not_59_out, not_60_out, not_61_out, not_62_out, not_63_out, not_64_out, not_65_out, not_66_out,
       not_67_out, not_68_out, not_69_out, not_70_out, not_71_out, not_72_out, not_73_out, not_74_out,
       not_75_out, not_76_out, not_77_out, not_78_out, not_79_out, not_80_out, not_81_out, not_82_out,
       not_83_out, not_84_out, not_85_out, not_86_out, not_87_out, not_88_out, not_89_out, not_90_out,
       not_91_out, not_92_out, not_93_out, not_94_out, not_95_out, not_96_out, not_97_out, not_98_out,
       not_99_out, not_100_out, not_101_out, not_102_out, not_103_out, not_104_out, not_105_out, not_106_out,
       not_107_out, not_108_out, not_109_out, not_110_out, not_111_out, not_112_out, not_113_out,
       not_114_out, not_115_out, not_116_out, not_117_out, not_118_out, not_119_out;

  not not_1 (not_1_out, op1);
  not not_2 (not_2_out, op2);
  not not_3 (not_3_out, op1);
  not not_4 (not_4_out, op3);
  and and_1 (MemRead, op0, not_1_out, not_2_out, not_4_out, op4, op5);
  not not_5 (not_5_out, op3);
  not not_6 (not_6_out, op0);
  and and_2 (MemWrite, op0, not_3_out, op2, not_5_out, op4, op5);
  not not_7 (not_7_out, op1);
  not not_8 (not_8_out, op4);
  not not_9 (not_9_out, op5);
  not not_10 (not_10_out, op3);
  and and_3 (and_3_out, not_6_out, not_7_out, op2, not_10_out, not_8_out, not_9_out);
  not not_11 (not_11_out, op1);
  not not_12 (not_12_out, op2);
  not not_13 (not_13_out, op3);
  and and_4 (and_4_out, op0, not_11_out, not_12_out, not_13_out, op4, op5);
  not not_14 (not_14_out, op1);
  not not_15 (not_15_out, op3);
  and and_5 (and_5_out, op0, not_14_out, op2, not_15_out, op4, op5);
  not not_16 (not_16_out, op0);
  not not_17 (not_17_out, op4);
  not not_18 (not_18_out, op1);
  and and_6 (and_6_out, not_16_out, not_18_out, op2, op3, not_17_out, not_19_out);
  not not_19 (not_19_out, op5);
  not not_20 (not_20_out, op1);
  not not_21 (not_21_out, op0);
  and and_7 (and_7_out, not_21_out, not_20_out, op2, op3, not_24_out, op5);
  or or_1 (ALUSrc, and_3_out, and_4_out, and_5_out, and_6_out, and_7_out, and_8_out, and_9_out, and_10_out);
  not not_22 (not_22_out, op0);
  not not_23 (not_23_out, op1);
  not not_24 (not_24_out, op4);
  and and_8 (and_8_out, not_22_out, not_23_out, op2, not_25_out, op4, not_28_out);
  not not_25 (not_25_out, op3);
  not not_26 (not_26_out, op0);
  not not_27 (not_27_out, op1);
  not not_28 (not_28_out, op5);
  not not_29 (not_29_out, op0);
  not not_30 (not_30_out, op3);
  not not_31 (not_31_out, op4);
  not not_32 (not_32_out, op1);
  and and_9 (and_9_out, not_26_out, not_27_out, op2, not_30_out, not_31_out, op5);
  not not_33 (not_33_out, op4);
  not not_34 (not_34_out, op5);
  not not_35 (not_35_out, op0);
  not not_36 (not_36_out, op3);
  and and_10 (and_10_out, not_29_out, not_32_out, op2, not_36_out, not_33_out, not_34_out);
  not not_37 (not_37_out, op1);
  not not_38 (not_38_out, op3);
  not not_39 (not_39_out, op5);
  not not_40 (not_40_out, op2);
  and and_11 (and_11_out, not_35_out, not_37_out, not_40_out, not_38_out, op4, not_39_out);
  not not_41 (not_41_out, op3);
  not not_42 (not_42_out, op2);
  not not_43 (not_43_out, op1);
  not not_44 (not_44_out, op0);
  and and_12 (and_12_out, not_44_out, not_43_out, not_42_out, not_41_out, op4, op5);
  or or_2 (Jump, and_11_out, and_12_out);
  not not_45 (not_45_out, op1);
  not not_46 (not_46_out, op3);
  not not_47 (not_47_out, op2);
  and and_13 (MemToReg, op0, not_45_out, not_47_out, not_46_out, op4, op5);
  not not_48 (not_48_out, op1);
  not not_49 (not_49_out, op2);
  not not_50 (not_50_out, op0);
  not not_51 (not_51_out, op4);
  and and_14 (and_14_out, not_50_out, not_48_out, not_49_out, op3, not_51_out, op5);
  not not_52 (not_52_out, op0);
  not not_53 (not_53_out, op2);
  not not_54 (not_54_out, op1);
  and and_15 (and_15_out, not_52_out, not_54_out, not_53_out, op3, not_57_out, not_58_out);
  or or_3 (Branch, and_14_out, and_15_out);
  not not_55 (not_55_out, op0);
  not not_56 (not_56_out, op1);
  not not_57 (not_57_out, op4);
  not not_58 (not_58_out, op5);
  not not_59 (not_59_out, op2);
  and and_16 (RegDst, not_55_out, not_56_out, not_59_out, not_60_out, not_63_out, not_62_out);
  not not_60 (not_60_out, op3);
  not not_61 (not_61_out, op1);
  not not_62 (not_62_out, op5);
  not not_63 (not_63_out, op4);
  not not_64 (not_64_out, op0);
  not not_65 (not_65_out, op2);
  not not_66 (not_66_out, op3);
  not not_67 (not_67_out, op0);
  not not_68 (not_68_out, op4);
  not not_69 (not_69_out, op1);
  not not_70 (not_70_out, op5);
  and and_17 (and_17_out, not_64_out, not_61_out, not_65_out, not_66_out, not_68_out, not_70_out);
  not not_71 (not_71_out, op3);
  not not_72 (not_72_out, op4);
  not not_73 (not_73_out, op5);
  and and_18 (and_18_out, not_67_out, not_69_out, op2, not_71_out, not_72_out, not_73_out);
  not not_74 (not_74_out, op2);
  not not_75 (not_75_out, op1);
  not not_76 (not_76_out, op3);
  and and_19 (and_19_out, op0, not_75_out, not_74_out, not_76_out, op4, op5);
  not not_77 (not_77_out, op1);
  not not_78 (not_78_out, op4);
  not not_79 (not_79_out, op0);
  not not_80 (not_80_out, op5);
  and and_20 (and_20_out, not_79_out, not_77_out, op2, op3, not_78_out, not_80_out);
  not not_81 (not_81_out, op1);
  not not_82 (not_82_out, op0);
  not not_83 (not_83_out, op4);
  and and_21 (and_21_out, not_82_out, not_81_out, op2, op3, not_83_out, op5);
  or or_4 (RegWrite, and_17_out, and_18_out, and_19_out, and_20_out, and_21_out, and_22_out, and_23_out, and_24_out, and_25_out, and_26_out);
  not not_84 (not_84_out, op3);
  not not_85 (not_85_out, op1);
  not not_86 (not_86_out, op0);
  and and_22 (and_22_out, not_86_out, not_85_out, op2, not_84_out, op4, not_88_out);
  not not_87 (not_87_out, op1);
  not not_88 (not_88_out, op5);
  not not_89 (not_89_out, op0);
  not not_90 (not_90_out, op3);
  and and_23 (and_23_out, not_89_out, not_87_out, op2, not_90_out, not_93_out, op5);
  not not_91 (not_91_out, op0);
  not not_92 (not_92_out, op1);
  not not_93 (not_93_out, op4);
  and and_24 (and_24_out, not_91_out, not_92_out, op2, not_97_out, not_98_out, not_99_out);
  not not_94 (not_94_out, op2);
  not not_95 (not_95_out, op1);
  not not_96 (not_96_out, op0);
  not not_97 (not_97_out, op3);
  not not_98 (not_98_out, op4);
  not not_99 (not_99_out, op5);
  not not_100 (not_100_out, op0);
  not not_101 (not_101_out, op3);
  and and_25 (and_25_out, not_96_out, not_95_out, not_94_out, not_101_out, op4, op5);
  not not_102 (not_102_out, op0);
  not not_103 (not_103_out, op5);
  not not_104 (not_104_out, op4);
  not not_105 (not_105_out, op3);
  not not_106 (not_106_out, op2);
  and and_26 (and_26_out, not_100_out, op1, not_106_out, not_105_out, not_104_out, not_103_out);
  not not_107 (not_107_out, op2);
  not not_108 (not_108_out, op1);
  not not_109 (not_109_out, op4);
  and and_27 (BneBeq, not_102_out, not_108_out, not_107_out, op3, not_109_out, op5);
  not not_110 (not_110_out, op2);
  not not_111 (not_111_out, op0);
  not not_112 (not_112_out, op1);
  not not_113 (not_113_out, op3);
  and and_28 (IsJAL, not_111_out, not_112_out, not_110_out, not_113_out, op4, op5);
  not not_114 (not_114_out, op4);
  not not_115 (not_115_out, op0);
  not not_116 (not_116_out, op1);
  and and_29 (and_29_out, not_115_out, not_116_out, op2, op3, not_114_out);
  not not_117 (not_117_out, op1);
  not not_118 (not_118_out, op0);
  and and_30 (and_30_out, not_118_out, not_117_out, op2, op3, op4, not_119_out);
  or or_5 (ZeroExtend, and_29_out, and_30_out);
  not not_119 (not_119_out, op5);
endmodule

module RegisterRead (
  input  op0,
  input  op1,
  input  op2,
  input  op3,
  input  op4,
  input  op5,
  input  Funct0,
  input  Funct1,
  input  Funct2,
  input  Funct3,
  input  Funct4,
  input  Funct5,
  output ReadRt,
  output ReadRs
);

  wire and_1_out, and_2_out, and_3_out, and_4_out, and_5_out, and_6_out, and_7_out, and_8_out, and_9_out,
       and_10_out, and_11_out, and_12_out, and_13_out, and_14_out, and_15_out, and_16_out, and_17_out,
       and_18_out, and_19_out, and_20_out, and_21_out, and_22_out, and_23_out, and_24_out, and_25_out,
       and_26_out, and_27_out, and_28_out, and_29_out, and_30_out, and_31_out, and_32_out, and_33_out,
       and_34_out, and_35_out, not_1_out, not_2_out, not_3_out, not_4_out, not_5_out, not_6_out, not_7_out,
       not_8_out, not_9_out, not_10_out, not_11_out, not_12_out, not_13_out, not_14_out, not_15_out,
       not_16_out, not_17_out, not_18_out, not_19_out, not_20_out, not_21_out, not_22_out, not_23_out,
       not_24_out, not_25_out, not_26_out, not_27_out, not_28_out, not_29_out, not_30_out, not_31_out,
       not_32_out, not_33_out, not_34_out, not_35_out, not_36_out, not_37_out, not_38_out, not_39_out,
       not_40_out, not_41_out, not_42_out, not_43_out, not_44_out, not_45_out, not_46_out, not_47_out,
       not_48_out, not_49_out, not_50_out, not_51_out, not_52_out, not_53_out, not_54_out, not_58_out,
       not_59_out, not_60_out, not_61_out, not_62_out, not_63_out, not_64_out, not_65_out, not_66_out,
       not_67_out, not_68_out, not_69_out, not_70_out, not_71_out, not_72_out, not_73_out, not_74_out,
       not_75_out, not_76_out, not_77_out, not_78_out, not_79_out, not_80_out, not_81_out, not_82_out,
       not_83_out, not_84_out, not_85_out, not_86_out, not_87_out, not_88_out, not_89_out, not_90_out,
       not_91_out, not_92_out, not_93_out, not_94_out, not_95_out, not_96_out, not_97_out, not_98_out,
       not_99_out, not_100_out, not_101_out, not_102_out, not_103_out, not_104_out, not_105_out, not_106_out,
       not_107_out, not_108_out, not_109_out, not_110_out, not_111_out, not_112_out, not_113_out,
       not_114_out, not_115_out, not_116_out, not_117_out, not_118_out, not_119_out, not_120_out,
       not_121_out, not_122_out, not_123_out, not_124_out, not_125_out, not_126_out, not_127_out,
       not_128_out, not_129_out, not_130_out, not_131_out, not_132_out, not_133_out, not_134_out,
       not_135_out, not_136_out, not_137_out, not_138_out, not_139_out, not_151_out, not_155_out,
       not_158_out, not_159_out, not_164_out, not_165_out, not_166_out, not_168_out, not_169_out,
       not_170_out, not_172_out, not_179_out, not_180_out, not_181_out, not_182_out, not_190_out,
       not_192_out, not_193_out, not_194_out, not_195_out, not_196_out, not_198_out, not_199_out,
       not_208_out, not_209_out, not_215_out, not_216_out, not_219_out, not_221_out, not_222_out,
       not_233_out, not_246_out, not_262_out, not_263_out, not_271_out, not_272_out, not_273_out,
       not_274_out, not_275_out, not_282_out, not_283_out, not_285_out, not_286_out, not_292_out,
       not_298_out, not_299_out, not_301_out, not_302_out, not_303_out, not_310_out, not_311_out,
       not_312_out, not_313_out, not_314_out, not_315_out, not_322_out, not_324_out, not_326_out,
       not_327_out, not_330_out, not_337_out, not_338_out, not_339_out, not_341_out, not_342_out,
       not_343_out, not_345_out, not_346_out, not_353_out, not_354_out, not_356_out, not_357_out,
       not_358_out, not_360_out, not_361_out, not_370_out, or_1_out, or_3_out;

  not not_1 (not_1_out, op2);
  not not_2 (not_2_out, op5);
  not not_3 (not_3_out, op0);
  not not_4 (not_4_out, op4);
  not not_5 (not_5_out, op3);
  not not_6 (not_6_out, op1);
  and and_1 (and_1_out, not_3_out, not_6_out, not_1_out, not_5_out, not_4_out, not_2_out, or_1_out);
  not not_7 (not_7_out, Funct1);
  not not_8 (not_8_out, Funct2);
  and and_2 (and_2_out, Funct0, not_7_out, not_8_out, not_10_out, not_9_out, not_11_out);
  not not_9 (not_9_out, Funct4);
  not not_10 (not_10_out, Funct3);
  not not_11 (not_11_out, Funct4);
  not not_12 (not_12_out, Funct4);
  not not_13 (not_13_out, Funct1);
  not not_14 (not_14_out, Funct5);
  not not_15 (not_15_out, Funct2);
  and and_3 (and_3_out, Funct0, not_13_out, not_15_out, Funct3, not_12_out, not_14_out);
  not not_16 (not_16_out, Funct2);
  not not_17 (not_17_out, Funct1);
  and and_4 (and_4_out, Funct0, not_17_out, not_16_out, not_19_out, not_18_out, Funct5);
  not not_18 (not_18_out, Funct4);
  not not_19 (not_19_out, Funct3);
  not not_20 (not_20_out, Funct2);
  not not_21 (not_21_out, Funct1);
  not not_22 (not_22_out, Funct3);
  not not_23 (not_23_out, Funct5);
  and and_5 (and_5_out, Funct0, not_21_out, not_20_out, not_22_out, Funct4, not_23_out);
  not not_24 (not_24_out, Funct1);
  not not_25 (not_25_out, Funct2);
  and and_6 (and_6_out, Funct0, not_24_out, not_25_out, Funct3, not_26_out, Funct5);
  or or_1 (or_1_out, and_2_out, and_3_out, and_4_out, and_5_out, and_6_out, and_7_out, and_8_out, and_9_out, and_10_out);
  not not_26 (not_26_out, Funct4);
  not not_27 (not_27_out, Funct2);
  not not_28 (not_28_out, Funct1);
  and and_7 (and_7_out, Funct0, not_28_out, not_27_out, Funct3, Funct4, Funct5);
  not not_29 (not_29_out, Funct1);
  and and_8 (and_8_out, Funct0, not_29_out, Funct2, not_30_out, Funct4, not_31_out);
  not not_30 (not_30_out, Funct3);
  not not_31 (not_31_out, Funct5);
  not not_32 (not_32_out, Funct1);
  not not_33 (not_33_out, Funct3);
  and and_9 (and_9_out, Funct0, not_32_out, Funct2, not_33_out, Funct4, Funct5);
  not not_34 (not_34_out, Funct0);
  not not_35 (not_35_out, Funct1);
  and and_10 (and_10_out, not_34_out, not_35_out, Funct2, not_36_out, not_38_out, not_37_out);
  not not_36 (not_36_out, Funct3);
  not not_37 (not_37_out, Funct5);
  not not_38 (not_38_out, Funct4);
  not not_39 (not_39_out, op5);
  not not_40 (not_40_out, op4);
  not not_41 (not_41_out, op1);
  not not_42 (not_42_out, op3);
  not not_43 (not_43_out, op0);
  and and_11 (and_11_out, not_43_out, not_41_out, op2, not_42_out, not_40_out, not_39_out);
  not not_44 (not_44_out, op0);
  not not_45 (not_45_out, op1);
  and and_12 (and_12_out, not_44_out, not_45_out, op2, not_47_out, not_46_out, op5);
  not not_46 (not_46_out, op4);
  not not_47 (not_47_out, op3);
  not not_48 (not_48_out, op5);
  not not_49 (not_49_out, op0);
  not not_50 (not_50_out, op1);
  not not_51 (not_51_out, op4);
  and and_13 (and_13_out, not_49_out, not_50_out, op2, op3, not_51_out, not_48_out);
  not not_52 (not_52_out, op0);
  not not_53 (not_53_out, op1);
  and and_14 (and_14_out, not_52_out, not_53_out, op2, op3, not_54_out, op5);
  not not_54 (not_54_out, op4);
  // NOT_Gate not_55 is placed but not wired
  // NOT_Gate not_56 is placed but not wired
  // NOT_Gate not_57 is placed but not wired
  not not_58 (not_58_out, op1);
  not not_59 (not_59_out, op2);
  not not_60 (not_60_out, op3);
  and and_15 (and_15_out, op0, not_58_out, not_59_out, not_60_out, op4, op5);
  or or_2 (ReadRs, and_1_out, and_11_out, and_12_out, and_13_out, and_14_out, and_15_out, and_16_out, and_17_out, and_18_out, and_19_out);
  not not_61 (not_61_out, op0);
  not not_62 (not_62_out, op1);
  not not_63 (not_63_out, op2);
  and and_16 (and_16_out, not_61_out, not_62_out, not_63_out, op3, not_65_out, not_64_out);
  not not_64 (not_64_out, op5);
  not not_65 (not_65_out, op4);
  not not_66 (not_66_out, op4);
  not not_67 (not_67_out, op1);
  not not_68 (not_68_out, op0);
  not not_69 (not_69_out, op2);
  and and_17 (and_17_out, not_68_out, not_67_out, not_69_out, op3, not_66_out, op5);
  not not_70 (not_70_out, op0);
  not not_71 (not_71_out, op1);
  and and_18 (and_18_out, not_70_out, not_71_out, op2, not_73_out, op4, not_72_out);
  not not_72 (not_72_out, op5);
  not not_73 (not_73_out, op3);
  not not_74 (not_74_out, op3);
  not not_75 (not_75_out, op1);
  and and_19 (and_19_out, op0, not_75_out, op2, not_74_out, op4, op5);
  not not_76 (not_76_out, op2);
  not not_77 (not_77_out, op0);
  not not_78 (not_78_out, op1);
  not not_79 (not_79_out, op3);
  and and_20 (and_20_out, not_77_out, not_78_out, not_76_out, not_79_out, not_80_out, not_81_out, or_3_out);
  not not_80 (not_80_out, op4);
  not not_81 (not_81_out, op5);
  not not_82 (not_82_out, Funct5);
  not not_83 (not_83_out, Funct3);
  not not_84 (not_84_out, Funct4);
  not not_85 (not_85_out, Funct1);
  not not_86 (not_86_out, Funct2);
  and and_21 (and_21_out, Funct0, not_85_out, not_86_out, not_83_out, not_84_out, not_82_out);
  not not_87 (not_87_out, Funct1);
  not not_88 (not_88_out, Funct2);
  and and_22 (and_22_out, Funct0, not_87_out, not_88_out, not_90_out, not_89_out, Funct5);
  not not_89 (not_89_out, Funct4);
  not not_90 (not_90_out, Funct3);
  not not_91 (not_91_out, Funct4);
  not not_92 (not_92_out, Funct5);
  not not_93 (not_93_out, Funct1);
  not not_94 (not_94_out, Funct2);
  and and_23 (and_23_out, Funct0, not_93_out, not_94_out, Funct3, not_91_out, not_92_out);
  not not_95 (not_95_out, Funct0);
  not not_96 (not_96_out, Funct1);
  not not_97 (not_97_out, Funct2);
  and and_24 (and_24_out, not_95_out, not_96_out, not_97_out, not_99_out, not_98_out, not_100_out);
  or or_3 (or_3_out, and_21_out, and_22_out, and_23_out, and_24_out, and_25_out, and_26_out, and_27_out, and_28_out, and_29_out, and_30_out, and_31_out);
  not not_98 (not_98_out, Funct4);
  not not_99 (not_99_out, Funct3);
  not not_100 (not_100_out, Funct5);
  not not_101 (not_101_out, Funct3);
  not not_102 (not_102_out, Funct1);
  not not_103 (not_103_out, Funct2);
  not not_104 (not_104_out, Funct0);
  and and_25 (and_25_out, not_104_out, not_102_out, not_103_out, not_101_out, Funct4, Funct5);
  not not_105 (not_105_out, Funct0);
  not not_106 (not_106_out, Funct1);
  not not_107 (not_107_out, Funct2);
  and and_26 (and_26_out, not_105_out, not_106_out, not_107_out, not_109_out, Funct4, not_108_out);
  not not_108 (not_108_out, Funct5);
  not not_109 (not_109_out, Funct3);
  not not_110 (not_110_out, Funct1);
  not not_111 (not_111_out, Funct5);
  not not_112 (not_112_out, Funct2);
  not not_113 (not_113_out, Funct3);
  and and_27 (and_27_out, Funct0, not_110_out, not_112_out, not_113_out, Funct4, not_111_out);
  not not_114 (not_114_out, Funct2);
  not not_115 (not_115_out, Funct1);
  and and_28 (and_28_out, Funct0, not_115_out, not_114_out, Funct3, not_116_out, Funct5);
  not not_116 (not_116_out, Funct4);
  not not_117 (not_117_out, Funct2);
  not not_118 (not_118_out, Funct1);
  and and_29 (and_29_out, Funct0, not_118_out, not_117_out, Funct3, Funct4, Funct5);
  not not_119 (not_119_out, Funct1);
  and and_30 (and_30_out, Funct0, not_119_out, Funct2, not_121_out, Funct4, not_120_out);
  not not_120 (not_120_out, Funct5);
  not not_121 (not_121_out, Funct3);
  not not_122 (not_122_out, Funct3);
  not not_123 (not_123_out, Funct1);
  and and_31 (and_31_out, Funct0, not_123_out, Funct2, not_122_out, Funct4, Funct5);
  not not_124 (not_124_out, op0);
  not not_125 (not_125_out, op1);
  not not_126 (not_126_out, op2);
  and and_32 (and_32_out, not_124_out, not_125_out, not_126_out, op3, not_127_out, not_128_out);
  not not_127 (not_127_out, op4);
  not not_128 (not_128_out, op5);
  not not_129 (not_129_out, op4);
  not not_130 (not_130_out, op1);
  not not_131 (not_131_out, op0);
  not not_132 (not_132_out, op2);
  and and_33 (and_33_out, not_131_out, not_130_out, not_132_out, op3, not_129_out, op5);
  or or_4 (ReadRt, and_20_out, and_32_out, and_33_out, and_34_out, and_35_out);
  not not_133 (not_133_out, op0);
  not not_134 (not_134_out, op2);
  and and_34 (and_34_out, not_133_out, op1, not_134_out, not_135_out, not_136_out, not_137_out);
  not not_135 (not_135_out, op3);
  not not_136 (not_136_out, op4);
  not not_137 (not_137_out, op5);
  not not_138 (not_138_out, op1);
  not not_139 (not_139_out, op3);
  and and_35 (and_35_out, op0, not_138_out, op2, not_139_out, op4, op5);
  // NOT_Gate not_140 is placed but not wired
  // NOT_Gate not_141 is placed but not wired
  // NOT_Gate not_142 is placed but not wired
  // NOT_Gate not_143 is placed but not wired
  // NOT_Gate not_144 is placed but not wired
  // NOT_Gate not_145 is placed but not wired
  // NOT_Gate not_146 is placed but not wired
  // AND_Gate and_36 is placed but not wired
  // NOT_Gate not_147 is placed but not wired
  // NOT_Gate not_148 is placed but not wired
  // NOT_Gate not_149 is placed but not wired
  // NOT_Gate not_150 is placed but not wired
  // NOT_Gate not_151 has open pins: in=open, out=not_151_out
  // NOT_Gate not_152 has open pins: in=not_151_out, out=open
  // NOT_Gate not_153 is placed but not wired
  // NOT_Gate not_154 is placed but not wired
  // NOT_Gate not_155 has open pins: in=open, out=not_155_out
  // NOT_Gate not_156 is placed but not wired
  // NOT_Gate not_157 has open pins: in=not_155_out, out=open
  // NOT_Gate not_158 has open pins: in=open, out=not_158_out
  // NOT_Gate not_159 has open pins: in=open, out=not_159_out
  // NOT_Gate not_160 is placed but not wired
  // NOT_Gate not_161 is placed but not wired
  // NOT_Gate not_162 has open pins: in=not_159_out, out=open
  // NOT_Gate not_163 has open pins: in=not_158_out, out=open
  // AND_Gate and_37 is placed but not wired
  // NOT_Gate not_164 has open pins: in=open, out=not_164_out
  // NOT_Gate not_165 has open pins: in=open, out=not_165_out
  // NOT_Gate not_166 has open pins: in=open, out=not_166_out
  // NOT_Gate not_167 is placed but not wired
  not not_168 (not_168_out, not_165_out);
  // NOT_Gate not_169 has open pins: in=open, out=not_169_out
  not not_170 (not_170_out, not_166_out);
  // NOT_Gate not_171 is placed but not wired
  not not_172 (not_172_out, not_164_out);
  // NOT_Gate not_173 is placed but not wired
  // NOT_Gate not_174 has open pins: in=not_169_out, out=open
  // NOT_Gate not_175 has open pins: in=not_172_out, out=open
  // NOT_Gate not_176 is placed but not wired
  // NOT_Gate not_177 has open pins: in=not_170_out, out=open
  // NOT_Gate not_178 has open pins: in=not_168_out, out=open
  // NOT_Gate not_179 has open pins: in=open, out=not_179_out
  // NOT_Gate not_180 has open pins: in=open, out=not_180_out
  // NOT_Gate not_181 has open pins: in=open, out=not_181_out
  // NOT_Gate not_182 has open pins: in=open, out=not_182_out
  // NOT_Gate not_183 is placed but not wired
  // NOT_Gate not_184 is placed but not wired
  // NOT_Gate not_185 has open pins: in=not_181_out, out=open
  // NOT_Gate not_186 has open pins: in=not_179_out, out=open
  // NOT_Gate not_187 is placed but not wired
  // NOT_Gate not_188 has open pins: in=not_180_out, out=open
  // NOT_Gate not_189 has open pins: in=not_182_out, out=open
  // AND_Gate and_38 is placed but not wired
  // NOT_Gate not_190 has open pins: in=open, out=not_190_out
  // NOT_Gate not_191 is placed but not wired
  // NOT_Gate not_192 has open pins: in=open, out=not_192_out
  // NOT_Gate not_193 has open pins: in=open, out=not_193_out
  not not_194 (not_194_out, not_192_out);
  // NOT_Gate not_195 has open pins: in=open, out=not_195_out
  not not_196 (not_196_out, not_193_out);
  // NOT_Gate not_197 is placed but not wired
  not not_198 (not_198_out, not_190_out);
  // NOT_Gate not_199 has open pins: in=open, out=not_199_out
  // NOT_Gate not_200 has open pins: in=not_195_out, out=open
  // NOT_Gate not_201 has open pins: in=not_199_out, out=open
  // NOT_Gate not_202 has open pins: in=not_194_out, out=open
  // NOT_Gate not_203 is placed but not wired
  // NOT_Gate not_204 has open pins: in=not_196_out, out=open
  // NOT_Gate not_205 has open pins: in=not_198_out, out=open
  // NOT_Gate not_206 is placed but not wired
  // NOT_Gate not_207 is placed but not wired
  // NOT_Gate not_208 has open pins: in=open, out=not_208_out
  // NOT_Gate not_209 has open pins: in=open, out=not_209_out
  // NOT_Gate not_210 has open pins: in=not_209_out, out=open
  // NOT_Gate not_211 has open pins: in=not_208_out, out=open
  // NOT_Gate not_212 is placed but not wired
  // NOT_Gate not_213 is placed but not wired
  // NOT_Gate not_214 is placed but not wired
  // NOT_Gate not_215 has open pins: in=open, out=not_215_out
  // NOT_Gate not_216 has open pins: in=open, out=not_216_out
  // NOT_Gate not_217 is placed but not wired
  // NOT_Gate not_218 is placed but not wired
  not not_219 (not_219_out, not_215_out);
  // NOT_Gate not_220 is placed but not wired
  // NOT_Gate not_221 has open pins: in=open, out=not_221_out
  not not_222 (not_222_out, not_216_out);
  // NOT_Gate not_223 is placed but not wired
  // NOT_Gate not_224 has open pins: in=not_221_out, out=open
  // NOT_Gate not_225 is placed but not wired
  // NOT_Gate not_226 has open pins: in=not_222_out, out=open
  // NOT_Gate not_227 is placed but not wired
  // NOT_Gate not_228 has open pins: in=not_219_out, out=open
  // NOT_Gate not_229 is placed but not wired
  // NOT_Gate not_230 is placed but not wired
  // NOT_Gate not_231 is placed but not wired
  // NOT_Gate not_232 is placed but not wired
  // AND_Gate and_39 is placed but not wired
  // NOT_Gate not_233 has open pins: in=open, out=not_233_out
  // NOT_Gate not_234 is placed but not wired
  // NOT_Gate not_235 is placed but not wired
  // NOT_Gate not_236 is placed but not wired
  // NOT_Gate not_237 is placed but not wired
  // NOT_Gate not_238 has open pins: in=not_233_out, out=open
  // NOT_Gate not_239 is placed but not wired
  // NOT_Gate not_240 is placed but not wired
  // AND_Gate and_40 is placed but not wired
  // NOT_Gate not_241 is placed but not wired
  // NOT_Gate not_242 is placed but not wired
  // NOT_Gate not_243 is placed but not wired
  // NOT_Gate not_244 is placed but not wired
  // NOT_Gate not_245 is placed but not wired
  // NOT_Gate not_246 has open pins: in=open, out=not_246_out
  // NOT_Gate not_247 is placed but not wired
  // NOT_Gate not_248 is placed but not wired
  // NOT_Gate not_249 has open pins: in=not_246_out, out=open
  // NOT_Gate not_250 is placed but not wired
  // NOT_Gate not_251 is placed but not wired
  // NOT_Gate not_252 is placed but not wired
  // NOT_Gate not_253 is placed but not wired
  // NOT_Gate not_254 is placed but not wired
  // NOT_Gate not_255 is placed but not wired
  // NOT_Gate not_256 is placed but not wired
  // NOT_Gate not_257 is placed but not wired
  // NOT_Gate not_258 is placed but not wired
  // AND_Gate and_41 is placed but not wired
  // NOT_Gate not_259 is placed but not wired
  // NOT_Gate not_260 is placed but not wired
  // NOT_Gate not_261 is placed but not wired
  // NOT_Gate not_262 has open pins: in=open, out=not_262_out
  // NOT_Gate not_263 has open pins: in=open, out=not_263_out
  // NOT_Gate not_264 is placed but not wired
  // NOT_Gate not_265 is placed but not wired
  // NOT_Gate not_266 is placed but not wired
  // NOT_Gate not_267 is placed but not wired
  // NOT_Gate not_268 has open pins: in=not_263_out, out=open
  // NOT_Gate not_269 has open pins: in=not_262_out, out=open
  // AND_Gate and_42 is placed but not wired
  // NOT_Gate not_270 is placed but not wired
  // NOT_Gate not_271 has open pins: in=open, out=not_271_out
  // NOT_Gate not_272 has open pins: in=open, out=not_272_out
  // NOT_Gate not_273 has open pins: in=open, out=not_273_out
  // NOT_Gate not_274 has open pins: in=open, out=not_274_out
  // NOT_Gate not_275 has open pins: in=open, out=not_275_out
  // NOT_Gate not_276 has open pins: in=not_272_out, out=open
  // NOT_Gate not_277 has open pins: in=not_273_out, out=open
  // NOT_Gate not_278 has open pins: in=not_274_out, out=open
  // NOT_Gate not_279 is placed but not wired
  // NOT_Gate not_280 has open pins: in=not_275_out, out=open
  // NOT_Gate not_281 has open pins: in=not_271_out, out=open
  // NOT_Gate not_282 has open pins: in=open, out=not_282_out
  // NOT_Gate not_283 has open pins: in=open, out=not_283_out
  // NOT_Gate not_284 is placed but not wired
  // NOT_Gate not_285 has open pins: in=open, out=not_285_out
  // NOT_Gate not_286 has open pins: in=open, out=not_286_out
  // NOT_Gate not_287 is placed but not wired
  // NOT_Gate not_288 has open pins: in=not_286_out, out=open
  // NOT_Gate not_289 has open pins: in=not_282_out, out=open
  // NOT_Gate not_290 has open pins: in=not_283_out, out=open
  // NOT_Gate not_291 has open pins: in=not_285_out, out=open
  // AND_Gate and_43 is placed but not wired
  // NOT_Gate not_292 has open pins: in=open, out=not_292_out
  // NOT_Gate not_293 is placed but not wired
  // NOT_Gate not_294 is placed but not wired
  // NOT_Gate not_295 is placed but not wired
  // NOT_Gate not_296 is placed but not wired
  // NOT_Gate not_297 has open pins: in=not_292_out, out=open
  // AND_Gate and_44 is placed but not wired
  // NOT_Gate not_298 has open pins: in=open, out=not_298_out
  // NOT_Gate not_299 has open pins: in=open, out=not_299_out
  // NOT_Gate not_300 is placed but not wired
  // NOT_Gate not_301 has open pins: in=open, out=not_301_out
  // NOT_Gate not_302 has open pins: in=open, out=not_302_out
  // NOT_Gate not_303 has open pins: in=open, out=not_303_out
  // NOT_Gate not_304 is placed but not wired
  // NOT_Gate not_305 has open pins: in=not_303_out, out=open
  // NOT_Gate not_306 has open pins: in=not_299_out, out=open
  // NOT_Gate not_307 has open pins: in=not_298_out, out=open
  // NOT_Gate not_308 has open pins: in=not_301_out, out=open
  // NOT_Gate not_309 has open pins: in=not_302_out, out=open
  // NOT_Gate not_310 has open pins: in=open, out=not_310_out
  // NOT_Gate not_311 has open pins: in=open, out=not_311_out
  // NOT_Gate not_312 has open pins: in=open, out=not_312_out
  not not_313 (not_313_out, not_311_out);
  not not_314 (not_314_out, not_310_out);
  // NOT_Gate not_315 has open pins: in=open, out=not_315_out
  // NOT_Gate not_316 is placed but not wired
  // NOT_Gate not_317 is placed but not wired
  // NOT_Gate not_318 has open pins: in=not_312_out, out=open
  // NOT_Gate not_319 has open pins: in=not_313_out, out=open
  // NOT_Gate not_320 has open pins: in=not_314_out, out=open
  // NOT_Gate not_321 has open pins: in=not_315_out, out=open
  // NOT_Gate not_322 has open pins: in=open, out=not_322_out
  // NOT_Gate not_323 is placed but not wired
  // NOT_Gate not_324 has open pins: in=open, out=not_324_out
  // NOT_Gate not_325 is placed but not wired
  // NOT_Gate not_326 has open pins: in=open, out=not_326_out
  not not_327 (not_327_out, not_324_out);
  // NOT_Gate not_328 is placed but not wired
  // NOT_Gate not_329 is placed but not wired
  not not_330 (not_330_out, not_322_out);
  // NOT_Gate not_331 is placed but not wired
  // NOT_Gate not_332 has open pins: in=not_327_out, out=open
  // NOT_Gate not_333 has open pins: in=not_330_out, out=open
  // NOT_Gate not_334 is placed but not wired
  // NOT_Gate not_335 has open pins: in=not_326_out, out=open
  // NOT_Gate not_336 is placed but not wired
  // NOT_Gate not_337 has open pins: in=open, out=not_337_out
  // NOT_Gate not_338 has open pins: in=open, out=not_338_out
  // NOT_Gate not_339 has open pins: in=open, out=not_339_out
  // NOT_Gate not_340 is placed but not wired
  // NOT_Gate not_341 has open pins: in=open, out=not_341_out
  not not_342 (not_342_out, not_338_out);
  not not_343 (not_343_out, not_337_out);
  // NOT_Gate not_344 is placed but not wired
  // NOT_Gate not_345 has open pins: in=open, out=not_345_out
  not not_346 (not_346_out, not_339_out);
  // NOT_Gate not_347 is placed but not wired
  // NOT_Gate not_348 has open pins: in=not_341_out, out=open
  // NOT_Gate not_349 has open pins: in=not_342_out, out=open
  // NOT_Gate not_350 has open pins: in=not_346_out, out=open
  // NOT_Gate not_351 has open pins: in=not_345_out, out=open
  // NOT_Gate not_352 has open pins: in=not_343_out, out=open
  // NOT_Gate not_353 has open pins: in=open, out=not_353_out
  // NOT_Gate not_354 has open pins: in=open, out=not_354_out
  // NOT_Gate not_355 is placed but not wired
  // NOT_Gate not_356 has open pins: in=open, out=not_356_out
  not not_357 (not_357_out, not_353_out);
  // NOT_Gate not_358 has open pins: in=open, out=not_358_out
  // NOT_Gate not_359 is placed but not wired
  not not_360 (not_360_out, not_356_out);
  not not_361 (not_361_out, not_354_out);
  // NOT_Gate not_362 has open pins: in=not_360_out, out=open
  // NOT_Gate not_363 has open pins: in=not_361_out, out=open
  // NOT_Gate not_364 has open pins: in=not_357_out, out=open
  // NOT_Gate not_365 is placed but not wired
  // NOT_Gate not_366 is placed but not wired
  // NOT_Gate not_367 has open pins: in=not_358_out, out=open
  // NOT_Gate not_368 is placed but not wired
  // NOT_Gate not_369 is placed but not wired
  // NOT_Gate not_370 has open pins: in=open, out=not_370_out
  // NOT_Gate not_371 is placed but not wired
  // NOT_Gate not_372 is placed but not wired
  // NOT_Gate not_373 is placed but not wired
  // NOT_Gate not_374 has open pins: in=not_370_out, out=open
  // NOT_Gate not_375 is placed but not wired
  // NOT_Gate not_376 is placed but not wired
  // NOT_Gate not_377 is placed but not wired
  // NOT_Gate not_378 is placed but not wired
  // NOT_Gate not_379 is placed but not wired
endmodule

module FunctDecoder (
  input  Funct0,
  input  Funct1,
  input  Funct2,
  input  Funct3,
  input  Funct4,
  input  Funct5,
  output ALU0,
  output ALU1,
  output ALU2,
  output ALU3,
  output IsJR,
  output IsShamt
);

  wire and_1_out, and_2_out, and_3_out, and_4_out, and_5_out, and_6_out, and_7_out, and_8_out, and_9_out,
       and_10_out, and_11_out, and_12_out, and_13_out, and_14_out, and_15_out, and_16_out, and_17_out,
       and_19_out, and_20_out, and_21_out, not_1_out, not_2_out, not_3_out, not_4_out, not_5_out, not_6_out,
       not_7_out, not_8_out, not_9_out, not_10_out, not_11_out, not_12_out, not_13_out, not_14_out,
       not_15_out, not_16_out, not_17_out, not_18_out, not_19_out, not_20_out, not_21_out, not_22_out,
       not_23_out, not_24_out, not_25_out, not_26_out, not_27_out, not_28_out, not_29_out, not_30_out,
       not_31_out, not_32_out, not_33_out, not_34_out, not_35_out, not_36_out, not_37_out, not_38_out,
       not_39_out, not_40_out, not_41_out, not_42_out, not_43_out, not_44_out, not_45_out, not_46_out,
       not_47_out, not_48_out, not_49_out, not_50_out, not_51_out, not_52_out, not_53_out, not_54_out,
       not_55_out, not_56_out, not_57_out, not_58_out, not_59_out, not_60_out, not_61_out, not_62_out,
       not_63_out, not_64_out, not_65_out, not_66_out, not_67_out, not_68_out, not_69_out, not_70_out,
       not_71_out, not_72_out, not_73_out, not_74_out, not_75_out, not_76_out, not_77_out, not_78_out;

  not not_1 (not_1_out, Funct2);
  not not_2 (not_2_out, Funct4);
  not not_3 (not_3_out, Funct1);
  and and_1 (and_1_out, Funct0, not_3_out, not_1_out, Funct3, not_2_out, Funct5);
  not not_4 (not_4_out, Funct1);
  not not_5 (not_5_out, Funct2);
  and and_2 (and_2_out, Funct0, not_4_out, not_5_out, Funct3, Funct4, Funct5);
  or or_1 (ALU0, and_1_out, and_2_out, and_3_out, and_4_out);
  not not_6 (not_6_out, Funct5);
  not not_7 (not_7_out, Funct1);
  not not_8 (not_8_out, Funct3);
  and and_3 (and_3_out, Funct0, not_7_out, Funct2, not_8_out, Funct4, not_6_out);
  not not_9 (not_9_out, Funct1);
  and and_4 (and_4_out, Funct0, not_9_out, Funct2, not_10_out, Funct4, Funct5);
  not not_10 (not_10_out, Funct3);
  not not_11 (not_11_out, Funct2);
  not not_12 (not_12_out, Funct4);
  not not_13 (not_13_out, Funct3);
  not not_14 (not_14_out, Funct1);
  and and_5 (and_5_out, Funct0, not_14_out, not_11_out, not_13_out, not_12_out);
  not not_15 (not_15_out, Funct1);
  not not_16 (not_16_out, Funct2);
  and and_6 (and_6_out, Funct0, not_15_out, not_16_out, not_17_out, not_18_out);
  not not_17 (not_17_out, Funct3);
  not not_18 (not_18_out, Funct5);
  or or_2 (ALU1, and_5_out, and_6_out, and_7_out, and_8_out);
  not not_19 (not_19_out, Funct1);
  not not_20 (not_20_out, Funct4);
  not not_21 (not_21_out, Funct5);
  not not_22 (not_22_out, Funct2);
  and and_7 (and_7_out, Funct0, not_19_out, not_22_out, not_20_out, not_21_out);
  not not_23 (not_23_out, Funct1);
  and and_8 (and_8_out, Funct0, not_23_out, Funct2, not_24_out, Funct4, Funct5);
  not not_24 (not_24_out, Funct3);
  not not_25 (not_25_out, Funct2);
  not not_26 (not_26_out, Funct5);
  not not_27 (not_27_out, Funct3);
  not not_28 (not_28_out, Funct1);
  and and_9 (and_9_out, Funct0, not_28_out, not_25_out, not_27_out, Funct4, not_26_out);
  not not_29 (not_29_out, Funct1);
  not not_30 (not_30_out, Funct2);
  and and_10 (and_10_out, Funct0, not_29_out, not_30_out, Funct3, not_31_out, not_32_out);
  not not_31 (not_31_out, Funct4);
  not not_32 (not_32_out, Funct5);
  not not_33 (not_33_out, Funct2);
  not not_34 (not_34_out, Funct3);
  not not_35 (not_35_out, Funct1);
  not not_36 (not_36_out, Funct0);
  not not_37 (not_37_out, Funct5);
  and and_11 (and_11_out, not_36_out, not_35_out, not_33_out, not_34_out, Funct4, not_37_out);
  or or_3 (ALU2, and_9_out, and_10_out, and_11_out, and_12_out, and_13_out);
  not not_38 (not_38_out, Funct1);
  not not_39 (not_39_out, Funct2);
  and and_12 (and_12_out, Funct0, not_38_out, not_39_out, Funct3, Funct4, Funct5);
  not not_40 (not_40_out, Funct3);
  not not_41 (not_41_out, Funct5);
  not not_42 (not_42_out, Funct1);
  and and_13 (and_13_out, Funct0, not_42_out, Funct2, not_40_out, Funct4, not_41_out);
  not not_43 (not_43_out, Funct1);
  not not_44 (not_44_out, Funct0);
  not not_45 (not_45_out, Funct2);
  and and_14 (and_14_out, not_44_out, not_43_out, not_45_out, not_46_out, Funct4, Funct5);
  not not_46 (not_46_out, Funct3);
  not not_47 (not_47_out, Funct3);
  not not_48 (not_48_out, Funct2);
  not not_49 (not_49_out, Funct4);
  not not_50 (not_50_out, Funct1);
  and and_15 (and_15_out, Funct0, not_50_out, not_48_out, not_47_out, not_49_out);
  not not_51 (not_51_out, Funct2);
  not not_52 (not_52_out, Funct1);
  and and_16 (and_16_out, Funct0, not_52_out, not_51_out, not_53_out, not_55_out, not_54_out);
  or or_4 (ALU3, and_14_out, and_15_out, and_16_out, and_17_out);
  not not_53 (not_53_out, Funct3);
  not not_54 (not_54_out, Funct5);
  not not_55 (not_55_out, Funct4);
  not not_56 (not_56_out, Funct1);
  not not_57 (not_57_out, Funct5);
  not not_58 (not_58_out, Funct3);
  and and_17 (and_17_out, Funct0, not_56_out, Funct2, not_58_out, Funct4, not_57_out);
  not not_59 (not_59_out, Funct0);
  not not_60 (not_60_out, Funct1);
  and and_18 (IsJR, not_59_out, not_60_out, Funct2, not_63_out, not_61_out, not_62_out);
  not not_61 (not_61_out, Funct4);
  not not_62 (not_62_out, Funct5);
  not not_63 (not_63_out, Funct3);
  not not_64 (not_64_out, Funct2);
  not not_65 (not_65_out, Funct3);
  not not_66 (not_66_out, Funct1);
  not not_67 (not_67_out, Funct0);
  and and_19 (and_19_out, not_67_out, not_66_out, not_64_out, not_65_out, Funct4, Funct5);
  not not_68 (not_68_out, Funct0);
  not not_69 (not_69_out, Funct2);
  not not_70 (not_70_out, Funct1);
  and and_20 (and_20_out, not_68_out, not_70_out, not_69_out, not_71_out, Funct4, not_72_out);
  or or_5 (IsShamt, and_19_out, and_20_out, and_21_out);
  not not_71 (not_71_out, Funct3);
  not not_72 (not_72_out, Funct5);
  not not_73 (not_73_out, Funct2);
  not not_74 (not_74_out, Funct3);
  not not_75 (not_75_out, Funct5);
  not not_76 (not_76_out, Funct1);
  not not_77 (not_77_out, Funct0);
  not not_78 (not_78_out, Funct4);
  and and_21 (and_21_out, not_77_out, not_76_out, not_73_out, not_74_out, not_78_out, not_75_out);
endmodule

module ALUDecoder (
  input  op0,
  input  op1,
  input  op2,
  input  op3,
  input  op4,
  input  op5,
  output ALUop0,
  output ALUop1,
  output ALUop2,
  output ALUop3
);

  wire and_1_out, and_2_out, and_3_out, and_4_out, and_5_out, and_6_out, and_7_out, and_8_out, and_9_out,
       and_10_out, and_11_out, and_12_out, and_13_out, and_14_out, and_15_out, and_16_out, and_17_out,
       and_18_out, and_19_out, and_20_out, and_21_out, and_22_out, and_23_out, and_24_out, and_25_out,
       and_26_out, and_27_out, and_28_out, and_29_out, not_1_out, not_2_out, not_3_out, not_4_out, not_5_out,
       not_6_out, not_7_out, not_8_out, not_9_out, not_10_out, not_11_out, not_12_out, not_13_out,
       not_14_out, not_15_out, not_16_out, not_17_out, not_18_out, not_19_out, not_20_out, not_21_out,
       not_22_out, not_23_out, not_24_out, not_25_out, not_26_out, not_27_out, not_28_out, not_29_out,
       not_30_out, not_31_out, not_32_out, not_33_out, not_34_out, not_35_out, not_36_out, not_37_out,
       not_38_out, not_39_out, not_40_out, not_41_out, not_42_out, not_43_out, not_44_out, not_45_out,
       not_46_out, not_47_out, not_48_out, not_49_out, not_50_out, not_51_out, not_52_out, not_53_out,
       not_54_out, not_55_out, not_56_out, not_57_out, not_58_out, not_59_out, not_60_out, not_61_out,
       not_62_out, not_63_out, not_64_out, not_65_out, not_66_out, not_67_out, not_68_out, not_69_out,
       not_70_out, not_71_out, not_72_out, not_73_out, not_74_out, not_75_out, not_76_out, not_77_out,
       not_78_out, not_79_out, not_80_out, not_81_out, not_82_out, not_83_out, not_84_out, not_85_out,
       not_86_out, not_87_out, not_88_out, not_89_out, not_90_out, not_91_out, not_92_out, not_93_out,
       not_94_out, not_95_out, not_96_out, not_97_out, not_98_out, not_99_out, not_100_out, not_101_out,
       not_102_out, not_103_out, not_104_out, not_105_out, not_106_out, not_107_out, not_108_out,
       not_109_out, not_110_out, not_111_out, not_112_out, not_113_out, not_114_out, not_115_out,
       not_116_out, not_117_out, not_118_out, not_119_out, not_120_out, not_121_out, not_122_out, not_123_out;

  not not_1 (not_1_out, op1);
  not not_2 (not_2_out, op0);
  not not_3 (not_3_out, op4);
  and and_1 (and_1_out, not_2_out, not_1_out, op2, op3, not_3_out, op5);
  or or_1 (ALUop0, and_1_out, and_2_out);
  not not_4 (not_4_out, op0);
  not not_5 (not_5_out, op1);
  not not_6 (not_6_out, op3);
  and and_2 (and_2_out, not_4_out, not_5_out, op2, not_6_out, op4, not_9_out);
  not not_7 (not_7_out, op1);
  not not_8 (not_8_out, op0);
  not not_9 (not_9_out, op5);
  not not_10 (not_10_out, op3);
  not not_11 (not_11_out, op2);
  not not_12 (not_12_out, op5);
  not not_13 (not_13_out, op4);
  and and_3 (and_3_out, not_8_out, not_7_out, not_11_out, not_10_out, not_13_out, not_12_out);
  not not_14 (not_14_out, op0);
  not not_15 (not_15_out, op3);
  not not_16 (not_16_out, op4);
  not not_17 (not_17_out, op1);
  and and_4 (and_4_out, not_14_out, not_17_out, op2, not_15_out, not_16_out, not_19_out);
  not not_18 (not_18_out, op1);
  not not_19 (not_19_out, op5);
  not not_20 (not_20_out, op2);
  not not_21 (not_21_out, op3);
  and and_5 (and_5_out, op0, not_18_out, not_20_out, not_21_out, op4, op5);
  not not_22 (not_22_out, op3);
  not not_23 (not_23_out, op1);
  and and_6 (and_6_out, op0, not_23_out, op2, not_22_out, op4, op5);
  not not_24 (not_24_out, op0);
  not not_25 (not_25_out, op1);
  not not_26 (not_26_out, op4);
  not not_27 (not_27_out, op2);
  and and_7 (and_7_out, not_24_out, not_25_out, not_27_out, op3, not_26_out, op5);
  not not_28 (not_28_out, op2);
  not not_29 (not_29_out, op4);
  not not_30 (not_30_out, op0);
  not not_31 (not_31_out, op1);
  and and_8 (and_8_out, not_30_out, not_31_out, not_28_out, op3, not_29_out, not_34_out);
  or or_2 (ALUop1, and_3_out, and_4_out, and_5_out, and_6_out, and_7_out, and_8_out, and_9_out, and_10_out, and_11_out, and_12_out, and_13_out, and_14_out);
  not not_32 (not_32_out, op0);
  not not_33 (not_33_out, op1);
  not not_34 (not_34_out, op5);
  not not_35 (not_35_out, op4);
  not not_36 (not_36_out, op5);
  and and_9 (and_9_out, not_32_out, not_33_out, op2, op3, not_35_out, not_36_out);
  not not_37 (not_37_out, op4);
  not not_38 (not_38_out, op3);
  not not_39 (not_39_out, op0);
  not not_40 (not_40_out, op1);
  and and_10 (and_10_out, not_39_out, not_40_out, op2, not_38_out, not_37_out, op5);
  not not_41 (not_41_out, op0);
  not not_42 (not_42_out, op1);
  not not_43 (not_43_out, op4);
  not not_44 (not_44_out, op3);
  not not_45 (not_45_out, op5);
  and and_11 (and_11_out, not_41_out, not_42_out, op2, not_44_out, not_43_out, not_45_out);
  not not_46 (not_46_out, op3);
  not not_47 (not_47_out, op2);
  not not_48 (not_48_out, op0);
  not not_49 (not_49_out, op1);
  and and_12 (and_12_out, not_48_out, not_49_out, not_47_out, not_46_out, op4, not_50_out);
  not not_50 (not_50_out, op5);
  not not_51 (not_51_out, op1);
  not not_52 (not_52_out, op0);
  not not_53 (not_53_out, op3);
  not not_54 (not_54_out, op2);
  and and_13 (and_13_out, not_52_out, not_51_out, not_54_out, not_53_out, op4, op5);
  not not_55 (not_55_out, op3);
  not not_56 (not_56_out, op0);
  not not_57 (not_57_out, op4);
  not not_58 (not_58_out, op2);
  and and_14 (and_14_out, not_56_out, op1, not_58_out, not_55_out, not_57_out, not_60_out);
  not not_59 (not_59_out, op0);
  not not_60 (not_60_out, op5);
  not not_61 (not_61_out, op1);
  not not_62 (not_62_out, op5);
  not not_63 (not_63_out, op4);
  and and_15 (and_15_out, not_59_out, not_61_out, op2, op3, not_63_out, not_62_out);
  not not_64 (not_64_out, op3);
  not not_65 (not_65_out, op0);
  not not_66 (not_66_out, op1);
  and and_16 (and_16_out, not_65_out, not_66_out, op2, not_64_out, op4, not_68_out);
  or or_3 (ALUop2, and_15_out, and_16_out);
  not not_67 (not_67_out, op0);
  not not_68 (not_68_out, op5);
  not not_69 (not_69_out, op1);
  not not_70 (not_70_out, op5);
  not not_71 (not_71_out, op3);
  not not_72 (not_72_out, op4);
  not not_73 (not_73_out, op2);
  and and_17 (and_17_out, not_67_out, not_69_out, not_73_out, not_71_out, not_72_out, not_70_out);
  not not_74 (not_74_out, op1);
  not not_75 (not_75_out, op0);
  not not_76 (not_76_out, op3);
  not not_77 (not_77_out, op4);
  and and_18 (and_18_out, not_75_out, not_74_out, op2, not_76_out, not_77_out, not_78_out);
  not not_78 (not_78_out, op5);
  not not_79 (not_79_out, op1);
  not not_80 (not_80_out, op2);
  not not_81 (not_81_out, op3);
  and and_19 (and_19_out, op0, not_79_out, not_80_out, not_81_out, op4, op5);
  not not_82 (not_82_out, op3);
  not not_83 (not_83_out, op1);
  and and_20 (and_20_out, op0, not_83_out, op2, not_82_out, op4, op5);
  not not_84 (not_84_out, op1);
  not not_85 (not_85_out, op0);
  not not_86 (not_86_out, op4);
  not not_87 (not_87_out, op2);
  and and_21 (and_21_out, not_85_out, not_84_out, not_87_out, op3, not_86_out, op5);
  not not_88 (not_88_out, op0);
  not not_89 (not_89_out, op2);
  not not_90 (not_90_out, op4);
  not not_91 (not_91_out, op1);
  and and_22 (and_22_out, not_88_out, not_91_out, not_89_out, op3, not_90_out, not_92_out);
  not not_92 (not_92_out, op5);
  not not_93 (not_93_out, op1);
  not not_94 (not_94_out, op0);
  not not_95 (not_95_out, op4);
  not not_96 (not_96_out, op5);
  and and_23 (and_23_out, not_94_out, not_93_out, op2, op3, not_95_out, not_96_out);
  or or_4 (ALUop3, and_17_out, and_18_out, and_19_out, and_20_out, and_21_out, and_22_out, and_23_out, and_24_out, and_25_out, and_26_out, and_27_out, and_28_out, and_29_out);
  not not_97 (not_97_out, op5);
  not not_98 (not_98_out, op0);
  not not_99 (not_99_out, op1);
  not not_100 (not_100_out, op3);
  and and_24 (and_24_out, not_98_out, not_99_out, op2, not_100_out, op4, not_97_out);
  not not_101 (not_101_out, op0);
  not not_102 (not_102_out, op1);
  not not_103 (not_103_out, op3);
  not not_104 (not_104_out, op4);
  and and_25 (and_25_out, not_101_out, not_102_out, op2, not_103_out, not_104_out, op5);
  not not_105 (not_105_out, op4);
  not not_106 (not_106_out, op0);
  not not_107 (not_107_out, op1);
  not not_108 (not_108_out, op3);
  not not_109 (not_109_out, op5);
  and and_26 (and_26_out, not_106_out, not_107_out, op2, not_108_out, not_105_out, not_109_out);
  not not_110 (not_110_out, op0);
  not not_111 (not_111_out, op1);
  not not_112 (not_112_out, op2);
  not not_113 (not_113_out, op5);
  not not_114 (not_114_out, op3);
  and and_27 (and_27_out, not_110_out, not_111_out, not_112_out, not_114_out, op4, not_113_out);
  not not_115 (not_115_out, op0);
  not not_116 (not_116_out, op3);
  not not_117 (not_117_out, op2);
  not not_118 (not_118_out, op1);
  and and_28 (and_28_out, not_115_out, not_118_out, not_117_out, not_116_out, op4, op5);
  not not_119 (not_119_out, op0);
  not not_120 (not_120_out, op2);
  not not_121 (not_121_out, op4);
  not not_122 (not_122_out, op3);
  not not_123 (not_123_out, op5);
  and and_29 (and_29_out, not_119_out, op1, not_120_out, not_122_out, not_121_out, not_123_out);
endmodule

module pALU (
  input  [31:0] X,
  input  [31:0] Y,
  input  [3:0] ALUOp,
  output SignedOverflow,
  output UnsignedOverflow,
  output [31:0] Result1,
  output [31:0] Result2,
  output isEqual
);

  wire comparator_1_lt, comparator_2_lt;
  wire [1:0] somadorcomoverflowdetection_1_out_4, subtratorcomoverflowdetection_1_out_4;
  wire [31:0] and_1_out, bit_extender_1_out, bit_extender_2_out, divider_1_out, divider_1_rem,
       multiplier_1_cout, multiplier_1_out, not_1_out, or_1_out, or_2_out, shifter_1_out, shifter_2_out,
       shifter_3_out, somadorcomoverflowdetection_1_opresult, subtratorcomoverflowdetection_1_resultado,
       xor_1_out;

  Shifter #(.width(32)) shifter_1 (.in(X), .\dist (Y[4:0]), .out(shifter_1_out));
  Shifter #(.width(32), .shift("ar")) shifter_2 (.in(X), .\dist (Y[4:0]), .out(shifter_2_out));
  Shifter #(.width(32), .shift("lr")) shifter_3 (.in(X), .\dist (Y[4:0]), .out(shifter_3_out));
  Multiplier #(.width(32)) multiplier_1 (.a(X), .b(Y), .out(multiplier_1_out), .cout(multiplier_1_cout));  // open: cin
  Divider #(.width(32)) divider_1 (.a(X), .b(Y), .out(divider_1_out), .rem(divider_1_rem));  // open: upper
  assign and_1_out = X & Y;  // AND_Gate and_1, 32 bits wide
  assign or_1_out = X | Y;  // OR_Gate or_1, 32 bits wide
  assign xor_1_out = X ^ Y;  // XOR_Gate xor_1, 32 bits wide
  assign or_2_out = X | Y;  // OR_Gate or_2, 32 bits wide
  Comparator #(.width(32)) comparator_1 (.a(X), .b(Y), .lt(comparator_1_lt));  // open: gt, eq
  Comparator #(.width(32)) comparator_2 (.a(X), .b(Y), .eq(isEqual), .lt(comparator_2_lt));  // open: gt
  assign not_1_out = ~or_2_out;  // NOT_Gate not_1, 32 bits wide
  Multiplexer #(.select(4), .width(2), .disabled("Z"), .enable("false")) multiplexer_1 (
    .in0(2'b00), .in1(2'b00), .in2(2'b00), .in3(2'b00), .in4(2'b00),
    .in5(somadorcomoverflowdetection_1_out_4), .in6(subtratorcomoverflowdetection_1_out_4), .in7(2'b00),
    .in8(2'b00), .in9(2'b00), .in10(2'b00), .in11(2'b00), .in12(2'b00), .in13(2'b00), .in14(2'b00),
    .in15(2'b00), .out({UnsignedOverflow, SignedOverflow}), .sel(ALUOp));
  SomadorComOverflowDetection somadorcomoverflowdetection_1 (
    .X(X), .out_4(somadorcomoverflowdetection_1_out_4[0]), .out_6(somadorcomoverflowdetection_1_out_4[1]),
    .opResult(somadorcomoverflowdetection_1_opresult), .Y(Y));  // open: in_3
  SubtratorComOverflowDetection subtratorcomoverflowdetection_1 (
    .X(X), .out_4(subtratorcomoverflowdetection_1_out_4[0]),
    .out_6(subtratorcomoverflowdetection_1_out_4[1]), .Resultado(subtratorcomoverflowdetection_1_resultado),
    .Y(Y));  // open: in_3
  Multiplexer #(.select(4), .width(32), .disabled("Z"), .enable("false")) multiplexer_2 (
    .in0({32{1'b0}}), .in1({32{1'b0}}), .in2({32{1'b0}}), .in3(multiplier_1_cout), .in4(divider_1_rem),
    .in5({32{1'b0}}), .in6({32{1'b0}}), .in7({32{1'b0}}), .in8({32{1'b0}}), .in9({32{1'b0}}),
    .in10({32{1'b0}}), .in11({32{1'b0}}), .in12({32{1'b0}}), .in13({32{1'b0}}), .in14({32{1'b0}}),
    .in15({32{1'b0}}), .out(Result2), .sel(ALUOp));
  assign bit_extender_1_out = {{31{1'b0}}, comparator_1_lt};  // Bit_Extender bit_extender_1
  assign bit_extender_2_out = {{31{1'b0}}, comparator_2_lt};  // Bit_Extender bit_extender_2
  Multiplexer #(.select(4), .width(32), .enable("false")) multiplexer_3 (
    .in0(shifter_1_out), .in1(shifter_2_out), .in2(shifter_3_out), .in3(multiplier_1_out),
    .in4(divider_1_out), .in5(somadorcomoverflowdetection_1_opresult),
    .in6(subtratorcomoverflowdetection_1_resultado), .in7(and_1_out), .in8(or_1_out), .in9(xor_1_out),
    .in10(not_1_out), .in11(bit_extender_1_out), .in12(bit_extender_2_out), .in13({32{1'b0}}),
    .in14({32{1'b0}}), .in15({32{1'b0}}), .out(Result1), .sel(ALUOp));

  // Other names for the same wires on the sheet: SigOverFlow = SignedOverflow; UsgOverflow = UnsignedOverflow;
  //   S[3:0] = ALUOp
endmodule

module SomadorComOverflowDetection (
  input  [31:0] X,
  input  [31:0] Y,
  input  in_3,
  output out_4,
  output [31:0] opResult,
  output out_6
);

  wire adder_1_cout;

  Adder #(.width(31)) adder_1 (.a(X[30:0]), .b(Y[30:0]), .out(opResult[30:0]), .cin(in_3), .cout(adder_1_cout));
  Adder #(.width(1)) adder_2 (.a(X[31]), .b(Y[31]), .out(opResult[31]), .cin(adder_1_cout), .cout(out_4));
  xor xor_1 (out_6, adder_1_cout, out_4);

  // Other names for the same wires on the sheet: cin = in_3; SignedOverflowsum = out_4; sumResult[31:0] = opResult;
  //   UnsignedOverflowsum = out_6
endmodule

module SubtratorComOverflowDetection (
  input  [31:0] X,
  input  [31:0] Y,
  input  in_3,
  output out_4,
  output [31:0] Resultado,
  output out_6
);

  wire adder_1_cout;

  Adder #(.width(31)) adder_1 (.a(X[30:0]), .b(Y[30:0]), .out(Resultado[30:0]), .cin(in_3), .cout(adder_1_cout));
  Adder #(.width(1)) adder_2 (.a(X[31]), .b(Y[31]), .out(Resultado[31]), .cin(adder_1_cout), .cout(out_6));
  xor xor_1 (out_4, adder_1_cout, out_6);

  // Other names for the same wires on the sheet: cin = in_3; Resultsub[31:0] = Resultado; SignedOverflowsub = out_6;
  //   UnsignedOverflowsub = out_4
endmodule

module HazardControl (
  input  clk_hazard,
  input  isToBranchOrJump_hazard,
  input  readRs_hazard,
  input  readRt_hazard,
  input  RegWriteMEM_hazard,
  input  [4:0] RT_hazard,
  input  [4:0] RS_hazard,
  input  [4:0] WriteRegMEM_hazard,
  input  RegWriteEX_hazard,
  input  [4:0] WirteRegEX_hazard,
  output FlushIF_hazard,
  output FlushID_hazard,
  output StallIF_hazard,
  output StallID_hazard
);

  wire and_1_out, and_2_out, and_3_out, and_4_out, and_5_out, and_6_out, and_7_out, and_8_out,
       comparator_1_eq, comparator_2_eq, comparator_3_eq, comparator_4_eq, comparator_5_eq, comparator_6_eq,
       d_ff_1_q, d_ff_2_q, not_1_out, not_2_out, not_3_out, or_1_out, or_2_out;

  Comparator #(.width(5)) comparator_1 (.a({5{1'b0}}), .b(WriteRegMEM_hazard), .eq(comparator_1_eq));  // open: gt, lt
  Comparator #(.width(5)) comparator_2 (.a(WriteRegMEM_hazard), .b(RT_hazard), .eq(comparator_2_eq));  // open: gt, lt
  Comparator #(.width(5)) comparator_3 (.a(WriteRegMEM_hazard), .b(RS_hazard), .eq(comparator_3_eq));  // open: gt, lt
  Comparator #(.width(5)) comparator_4 (.a({5{1'b0}}), .b(WirteRegEX_hazard), .eq(comparator_4_eq));  // open: gt, lt
  Comparator #(.width(5)) comparator_5 (.a(WirteRegEX_hazard), .b(RT_hazard), .eq(comparator_5_eq));  // open: gt, lt
  Comparator #(.width(5)) comparator_6 (.a(WirteRegEX_hazard), .b(RS_hazard), .eq(comparator_6_eq));  // open: gt, lt
  not not_1 (not_1_out, comparator_1_eq);
  not not_2 (not_2_out, comparator_4_eq);
  and and_1 (and_1_out, comparator_2_eq, readRt_hazard);
  and and_2 (and_2_out, comparator_3_eq, readRs_hazard);
  and and_3 (and_3_out, comparator_5_eq, readRt_hazard);
  and and_4 (and_4_out, comparator_6_eq, readRs_hazard);
  or or_1 (or_1_out, and_1_out, and_2_out);
  or or_2 (or_2_out, and_3_out, and_4_out);
  and and_5 (and_5_out, not_1_out, or_1_out);
  and and_6 (and_6_out, not_2_out, or_2_out);
  and and_7 (and_7_out, RegWriteMEM_hazard, and_5_out);
  and and_8 (and_8_out, RegWriteEX_hazard, and_6_out);
  or or_3 (StallID_hazard, and_7_out, and_8_out);
  D_Flip_Flop #(.trigger("falling")) d_ff_1 (
    .D(isToBranchOrJump_hazard), .clk(clk_hazard), .Q(d_ff_1_q));  // open: Qn, preset, reset
  not not_3 (not_3_out, clk_hazard);
  D_Flip_Flop #(.trigger("falling")) d_ff_2 (
    .D(StallID_hazard), .clk(clk_hazard), .Q(d_ff_2_q));  // open: Qn, preset, reset
  and and_9 (FlushIF_hazard, not_3_out, d_ff_1_q);
  and and_10 (FlushID_hazard, clk_hazard, d_ff_2_q);

  assign StallIF_hazard = StallID_hazard;

  // Other names for the same wires on the sheet: Tclk_hazard = clk_hazard

  // Notes on the sheet:
  //   _______
endmodule
