// Logisim project AddressCalculator.circ as structural Verilog: 1 circuit, main circuit JumpAddress
module JumpAddress (
  input  [25:0] Address,
  input  [31:0] PCPlus4,
  output [31:0] JumpAddress
);


  assign JumpAddress = {PCPlus4[31:28], Address, 2'b00};
endmodule
