// Logisim project BranchHandler.circ as structural Verilog: 2 circuits, main circuit simpleBranchHandler
module simpleBranchHandler (
  input  isBranch,
  input  clk,
  input  clear,
  input  BranchAccepted,
  output ClearIF,
  output Halt
);

  wire and_1_out, and_2_out, d_ff_1_q, d_ff_2_q, d_ff_3_q;

  D_Flip_Flop #(.trigger("falling")) d_ff_1 (.D(isBranch), .clk(clk), .Q(d_ff_1_q), .reset(clear));  // open: Qn, preset
  D_Flip_Flop #(.trigger("falling")) d_ff_2 (.D(d_ff_1_q), .clk(clk), .Q(d_ff_2_q), .reset(clear));  // open: Qn, preset
  and and_1 (and_1_out, clk, d_ff_1_q);
  D_Flip_Flop #(.trigger("falling")) d_ff_3 (.D(d_ff_2_q), .clk(clk), .Q(d_ff_3_q), .reset(clear));  // open: Qn, preset
  and and_2 (and_2_out, clk, d_ff_3_q);
  or or_1 (Halt, and_2_out, d_ff_2_q, d_ff_1_q, isBranch);
  or or_2 (ClearIF, and_1_out, BranchAccepted);
endmodule

module BranchHandlerv2 (
  input  isBranch,
  input  clk,
  input  clear,
  input  BranchAccepted,
  output Halt
);

  wire d_ff_1_q;

  D_Flip_Flop #(.trigger("falling")) d_ff_1 (.D(isBranch), .clk(clk), .Q(d_ff_1_q), .reset(clear));  // open: Qn, preset
  and and_1 (Halt, clk, d_ff_1_q, BranchAccepted);
endmodule
