// Logisim project Decodificador.circ as structural Verilog: 2 circuits, main circuit decodificador
module decodificador (
  input  [31:0] Instruction,
  output [25:0] adderess,
  output [15:0] immediate,
  output [5:0] funct,
  output [4:0] shamt,
  output [4:0] rd,
  output [4:0] rt,
  output [4:0] rs,
  output [5:0] op
);


  assign adderess = Instruction[25:0];
  assign funct = Instruction[5:0];
  assign immediate = Instruction[15:0];
  assign op = Instruction[31:26];
  assign rd = Instruction[15:11];
  assign rs = Instruction[25:21];
  assign rt = Instruction[20:16];
  assign shamt = Instruction[10:6];

  // Notes on the sheet:
  //   R-Type
  //   I-Type
  //   J-Type
  //   J-Type
  //   OP
  //   OP
  //   OP
  //   I-Type
  //   RS
  //   RS
  //   R-Type
  //   RT
  //   RT
  //   RD
  //   Target Address
  //   Shamt
  //   Address/Immediate
  //   Funct
endmodule

module decoder_alt (
  input  [31:0] Instruction,
  output [25:0] adderess,
  output [15:0] immediate,
  output [5:0] funct,
  output [4:0] shamt,
  output [4:0] rd,
  output [4:0] rt,
  output [4:0] rs,
  output [5:0] op
);


  assign adderess = Instruction[25:0];
  assign funct = Instruction[5:0];
  assign immediate = Instruction[15:0];
  assign op = Instruction[31:26];
  assign rd = Instruction[15:11];
  assign rs = Instruction[25:21];
  assign rt = Instruction[20:16];
  assign shamt = Instruction[10:6];

  // Notes on the sheet:
  //   R-Type
  //   I-Type
  //   J-Type
  //   J-Type
  //   OP
  //   OP
  //   OP
  //   I-Type
  //   RS
  //   RS
  //   R-Type
  //   RT
  //   RT
  //   RD
  //   Target Address
  //   Shamt
  //   Address/Immediate
  //   Funct
endmodule
