// Logisim project ForwardingUnit.circ as structural Verilog: 2 circuits, main circuit Forwarding_Unit
module Forwarding_Unit (
  input  ReadRs,
  input  ReadRt,
  input  RegWriteEX,
  input  RegWriteMEM,
  input  [4:0] RS,
  input  [4:0] RT,
  input  [4:0] WriteRegEX,
  input  [4:0] WriteRegMEM,
  output [1:0] RsSource,
  output HasForwarded,
  output [1:0] RtSource
);

  wire and_1_out, and_2_out, and_3_out, and_4_out, comparator_1_eq, comparator_2_eq, comparator_3_eq,
       comparator_4_eq, comparator_5_eq, comparator_6_eq, comparator_7_eq, comparator_8_eq, not_1_out,
       not_2_out, not_3_out, not_4_out;
  wire [1:0] multiplexer_1_out, multiplexer_2_out;

  Comparator #(.width(5)) comparator_1 (.a({5{1'b0}}), .b(WriteRegMEM), .eq(comparator_1_eq));  // open: gt, lt
  Comparator #(.width(5)) comparator_2 (.a(WriteRegMEM), .b(RS), .eq(comparator_2_eq));  // open: gt, lt
  Comparator #(.width(5)) comparator_3 (.a({5{1'b0}}), .b(WriteRegEX), .eq(comparator_3_eq));  // open: gt, lt
  Comparator #(.width(5)) comparator_4 (.a(WriteRegEX), .b(RS), .eq(comparator_4_eq));  // open: gt, lt
  Comparator #(.width(5)) comparator_5 (.a({5{1'b0}}), .b(WriteRegMEM), .eq(comparator_5_eq));  // open: gt, lt
  Comparator #(.width(5)) comparator_6 (.a(WriteRegMEM), .b(RT), .eq(comparator_6_eq));  // open: gt, lt
  Comparator #(.width(5)) comparator_7 (.a({5{1'b0}}), .b(WriteRegEX), .eq(comparator_7_eq));  // open: gt, lt
  Comparator #(.width(5)) comparator_8 (.a(WriteRegEX), .b(RT), .eq(comparator_8_eq));  // open: gt, lt
  not not_1 (not_1_out, comparator_1_eq);
  not not_2 (not_2_out, comparator_3_eq);
  not not_3 (not_3_out, comparator_5_eq);
  not not_4 (not_4_out, comparator_7_eq);
  and and_1 (and_1_out, ReadRs, RegWriteMEM, not_1_out, comparator_2_eq);
  and and_2 (and_2_out, ReadRs, RegWriteEX, not_2_out, comparator_4_eq);
  and and_3 (and_3_out, ReadRt, RegWriteMEM, not_3_out, comparator_6_eq);
  and and_4 (and_4_out, ReadRt, RegWriteEX, not_4_out, comparator_8_eq);
  Multiplexer #(.disabled("Z"), .width(2)) multiplexer_1 (
    .in0(2'b00), .in1(2'b10), .out(multiplexer_1_out), .sel(and_1_out));
  Multiplexer #(.disabled("Z"), .width(2)) multiplexer_2 (
    .in0(2'b00), .in1(2'b10), .out(multiplexer_2_out), .sel(and_3_out));
  Multiplexer #(.width(2)) multiplexer_3 (.in0(multiplexer_1_out), .in1(2'b01), .out(RsSource), .sel(and_2_out));
  Multiplexer #(.width(2)) multiplexer_4 (.in0(multiplexer_2_out), .in1(2'b01), .out(RtSource), .sel(and_4_out));
  or or_1 (HasForwarded, and_2_out, and_4_out);

  // Other names for the same wires on the sheet: RegDestEX[4:0] = WriteRegEX; RegDestMEM[4:0] = WriteRegMEM

  // Notes on the sheet:
  //   Rs Hazard in MEM
  //   Rs Match in EX
  //   Rt Match in MEM
  //   Rt Match in EX
endmodule

module LW_Hazard_Handler (
  input  clk,
  input  DataForwarded,
  input  isLW,
  output FlushID,
  output StallIF,
  output StallID
);

  wire d_ff_1_q;

  and and_1 (StallID, DataForwarded, isLW);
  D_Flip_Flop #(.trigger("falling")) d_ff_1 (.D(StallID), .clk(clk), .Q(d_ff_1_q));  // open: Qn, preset, reset
  and and_2 (FlushID, clk, d_ff_1_q);

  assign StallIF = StallID;
endmodule
