// Logisim project HazardDetectionUnit.circ as structural Verilog: 1 circuit, main circuit Hazard_Detection_Unit
module Hazard_Detection_Unit (
  input  clk,
  input  ReadRs,
  input  ReadRt,
  input  RegWriteEX,
  input  RegWriteMEM,
  input  [4:0] RS,
  input  [4:0] RT,
  input  [4:0] WriteRegEX,
  input  [4:0] WriteRegMEM,
  output FlushID,
  output StallIF,
  output StallID
);

  wire and_1_out, and_2_out, and_3_out, and_4_out, and_5_out, and_6_out, and_7_out, and_8_out,
       comparator_1_eq, comparator_2_eq, comparator_3_eq, comparator_4_eq, comparator_5_eq, comparator_6_eq,
       d_ff_1_q, not_1_out, not_2_out, or_1_out, or_2_out;

  Comparator #(.width(5)) comparator_1 (.a({5{1'b0}}), .b(WriteRegMEM), .eq(comparator_1_eq));  // open: gt, lt
  Comparator #(.width(5)) comparator_2 (.a(WriteRegMEM), .b(RS), .eq(comparator_2_eq));  // open: gt, lt
  Comparator #(.width(5)) comparator_3 (.a(WriteRegMEM), .b(RT), .eq(comparator_3_eq));  // open: gt, lt
  Comparator #(.width(5)) comparator_4 (.a({5{1'b0}}), .b(WriteRegEX), .eq(comparator_4_eq));  // open: gt, lt
  Comparator #(.width(5)) comparator_5 (.a(WriteRegEX), .b(RS), .eq(comparator_5_eq));  // open: gt, lt
  Comparator #(.width(5)) comparator_6 (.a(WriteRegEX), .b(RT), .eq(comparator_6_eq));  // open: gt, lt
  not not_1 (not_1_out, comparator_1_eq);
  not not_2 (not_2_out, comparator_4_eq);
  and and_1 (and_1_out, ReadRs, comparator_2_eq);
  and and_2 (and_2_out, ReadRt, comparator_3_eq);
  and and_3 (and_3_out, ReadRs, comparator_5_eq);
  and and_4 (and_4_out, ReadRt, comparator_6_eq);
  or or_1 (or_1_out, and_1_out, and_2_out);
  or or_2 (or_2_out, and_3_out, and_4_out);
  and and_5 (and_5_out, not_1_out, or_1_out);
  and and_6 (and_6_out, not_2_out, or_2_out);
  and and_7 (and_7_out, RegWriteMEM, and_5_out);
  and and_8 (and_8_out, RegWriteEX, and_6_out);
  or or_3 (StallID, and_7_out, and_8_out);
  D_Flip_Flop #(.trigger("falling")) d_ff_1 (.D(StallID), .clk(clk), .Q(d_ff_1_q));  // open: Qn, preset, reset
  and and_9 (FlushID, clk, d_ff_1_q);

  assign StallIF = StallID;

  // Other names for the same wires on the sheet: RegDestEX[4:0] = WriteRegEX; RegDestMEM[4:0] = WriteRegMEM
endmodule
