// Logisim project Stages.circ as structural Verilog: 7 circuits, main circuit IF_ID
module IF_ID (
  input  clk_IF_ID,
  input  clr_IF_ID,
  input  [31:0] Instruction_IF,
  input  [31:0] PCPlus4_IF,
  input  enable_IF_ID,
  output [31:0] Instruction_ID,
  output [31:0] PCPus4_ID
);

  Register #(.width(32)) reg_Instruction_IF_ID (
    .D(Instruction_IF), .en(enable_IF_ID), .clk(clk_IF_ID), .Q(Instruction_ID), .clr(clr_IF_ID));
  Register #(.width(32)) reg_PCPlus4_IF_ID (
    .D(PCPlus4_IF), .en(enable_IF_ID), .clk(clk_IF_ID), .Q(PCPus4_ID), .clr(clr_IF_ID));
endmodule

module ID_EX (
  input  clk_ID_EX,
  input  clr_ID_EX,
  input  [31:0] Imm_ID,
  input  [31:0] PCPlus4_ID,
  input  isShift_ID,
  input  [3:0] ALUOp_ID,
  input  MemRead_ID,
  input  [31:0] R1_ID,
  input  MemToReg_ID,
  input  [4:0] WriteReg_ID,
  input  MemWrite_ID,
  input  [31:0] R2_ID,
  input  RegWrite_ID,
  input  isJAL_ID,
  input  isJump_ID,
  input  [31:0] Shamt_ID,
  input  Bne_ID,
  input  Branch_ID,
  input  [31:0] JumpAddr_ID,
  input  ALUSrc_ID,
  input  isJR_ID,
  input  enable_ID_EX,
  output [31:0] Imm_EX,
  output [31:0] PCPus4_EX,
  output isShift_EX,
  output [3:0] ALUOp_EX,
  output MemRead_EX,
  output [31:0] R1_EX,
  output MemToReg_EX,
  output [4:0] WriteReg_EX,
  output MemWrite_EX,
  output [31:0] R2_EX,
  output RegWrite_EX,
  output isJAL_EX,
  output isJump_EX,
  output [31:0] Shamt_EX,
  output Bne_EX,
  output Branch_EX,
  output [31:0] JumpAddr_EX,
  output ALUSrc_EX,
  output isJR_EX
);

  Register #(.width(32)) reg_Immediate_ID_EX (
    .D(Imm_ID), .en(enable_ID_EX), .clk(clk_ID_EX), .Q(Imm_EX), .clr(clr_ID_EX));
  Register #(.width(32)) reg_R1_ID_EX (.D(R1_ID), .en(enable_ID_EX), .clk(clk_ID_EX), .Q(R1_EX), .clr(clr_ID_EX));
  Register #(.width(32)) reg_R2_ID_EX (.D(R2_ID), .en(enable_ID_EX), .clk(clk_ID_EX), .Q(R2_EX), .clr(clr_ID_EX));
  Register #(.width(32)) reg_Shamt_ID_EX (
    .D(Shamt_ID), .en(enable_ID_EX), .clk(clk_ID_EX), .Q(Shamt_EX), .clr(clr_ID_EX));
  Register #(.width(32)) reg_JumpAddr_ID_EX (
    .D(JumpAddr_ID), .en(enable_ID_EX), .clk(clk_ID_EX), .Q(JumpAddr_EX), .clr(clr_ID_EX));
  Register #(.width(32)) regPC_ID_EX (
    .D(PCPlus4_ID), .en(enable_ID_EX), .clk(clk_ID_EX), .Q(PCPus4_EX), .clr(clr_ID_EX));
  Register #(.width(1)) reg_isShift_ID_EX (
    .D(isShift_ID), .en(enable_ID_EX), .clk(clk_ID_EX), .Q(isShift_EX), .clr(clr_ID_EX));
  Register #(.width(1)) reg_MemToReg_ID_EX (
    .D(MemToReg_ID), .en(enable_ID_EX), .clk(clk_ID_EX), .Q(MemToReg_EX), .clr(clr_ID_EX));
  Register #(.width(1)) reg_RegWrite_ID_EX (
    .D(RegWrite_ID), .en(enable_ID_EX), .clk(clk_ID_EX), .Q(RegWrite_EX), .clr(clr_ID_EX));
  Register #(.width(1)) reg_Bne_ID_EX (.D(Bne_ID), .en(enable_ID_EX), .clk(clk_ID_EX), .Q(Bne_EX), .clr(clr_ID_EX));
  Register #(.width(1)) reg_ALUSrc_ID_EX (
    .D(ALUSrc_ID), .en(enable_ID_EX), .clk(clk_ID_EX), .Q(ALUSrc_EX), .clr(clr_ID_EX));
  Register #(.width(1)) reg_MemRead_ID_EX (
    .D(MemRead_ID), .en(enable_ID_EX), .clk(clk_ID_EX), .Q(MemRead_EX), .clr(clr_ID_EX));
  Register #(.width(1)) reg_MemWrite_ID_EX (
    .D(MemWrite_ID), .en(enable_ID_EX), .clk(clk_ID_EX), .Q(MemWrite_EX), .clr(clr_ID_EX));
  Register #(.width(1)) reg_IsJump_ID_EX (
    .D(isJump_ID), .en(enable_ID_EX), .clk(clk_ID_EX), .Q(isJump_EX), .clr(clr_ID_EX));
  Register #(.width(1)) reg_Branch_ID_EX (
    .D(Branch_ID), .en(enable_ID_EX), .clk(clk_ID_EX), .Q(Branch_EX), .clr(clr_ID_EX));
  Register #(.width(1)) reg_isJR_ID_EX (.D(isJR_ID), .en(enable_ID_EX), .clk(clk_ID_EX), .Q(isJR_EX), .clr(clr_ID_EX));
  Register #(.width(4)) regALUOp_ID_EX (
    .D(ALUOp_ID), .en(enable_ID_EX), .clk(clk_ID_EX), .Q(ALUOp_EX), .clr(clr_ID_EX));
  Register #(.width(5)) regWriteReg_ID_EX (
    .D(WriteReg_ID), .en(enable_ID_EX), .clk(clk_ID_EX), .Q(WriteReg_EX), .clr(clr_ID_EX));
  Register #(.width(1)) reg_isJAL_ID_EX (
    .D(isJAL_ID), .en(enable_ID_EX), .clk(clk_ID_EX), .Q(isJAL_EX), .clr(clr_ID_EX));
endmodule

module EX_MEM (
  input  clr_EX_MEM,
  input  clk_EX_MEM,
  input  [31:0] ALUResult_EX,
  input  isJAL_EX,
  input  [31:0] BranchDest_EX,
  input  Bne_ID,
  input  [31:0] MemData_EX,
  input  MemToReg_EX,
  input  [31:0] JRDest_EX,
  input  isJump_ID,
  input  [4:0] WriteReg_EX,
  input  RegWrite_EX,
  input  Branch_ID,
  input  [31:0] PCPlus4_EX,
  input  MemRead_EX,
  input  isJR_ID,
  input  [31:0] JumpAddr_EX,
  input  MemWrite_EX,
  input  isEqual_EX,
  input  enable_EX_MEM,
  output [31:0] ALUResult_MEM,
  output isJAL_MEM,
  output [31:0] BranchDest_MEM,
  output Bne_EX,
  output [31:0] MemData_MEM,
  output MemToReg_MEM,
  output [31:0] JRDestMEM,
  output isJump_EX,
  output [4:0] WriteReg_MEM,
  output RegWrite_MEM,
  output Branch_EX,
  output [31:0] PCPlus4_MEM,
  output MemRead_MEM,
  output isJR_EX,
  output [31:0] JumpAddr_MEM,
  output MemWrite_MEM,
  output isEqual_MEM
);

  Register #(.width(32)) reg_ALUResult_EX_MEM (
    .D(ALUResult_EX), .en(enable_EX_MEM), .clk(clk_EX_MEM), .Q(ALUResult_MEM), .clr(clr_EX_MEM));
  Register #(.width(32)) reg_MemData_EX_MEM (
    .D(MemData_EX), .en(enable_EX_MEM), .clk(clk_EX_MEM), .Q(MemData_MEM), .clr(clr_EX_MEM));
  Register #(.width(5)) reg_WriteReg_EX_MEM (
    .D(WriteReg_EX), .en(enable_EX_MEM), .clk(clk_EX_MEM), .Q(WriteReg_MEM), .clr(clr_EX_MEM));
  Register #(.width(32)) reg_PCPlus4_EX_MEM (
    .D(PCPlus4_EX), .en(enable_EX_MEM), .clk(clk_EX_MEM), .Q(PCPlus4_MEM), .clr(clr_EX_MEM));
  Register #(.width(32)) reg_JumpAddr_EX_MEM (
    .D(JumpAddr_EX), .en(enable_EX_MEM), .clk(clk_EX_MEM), .Q(JumpAddr_MEM), .clr(clr_EX_MEM));
  Register #(.width(32)) reg_BranchDest_EX_MEM (
    .D(BranchDest_EX), .en(enable_EX_MEM), .clk(clk_EX_MEM), .Q(BranchDest_MEM), .clr(clr_EX_MEM));
  Register #(.width(32)) reg_JRDest_EX_MEM (
    .D(JRDest_EX), .en(enable_EX_MEM), .clk(clk_EX_MEM), .Q(JRDestMEM), .clr(clr_EX_MEM));
  Register #(.width(1)) reg_isJAL_EX_MEM (
    .D(isJAL_EX), .en(enable_EX_MEM), .clk(clk_EX_MEM), .Q(isJAL_MEM), .clr(clr_EX_MEM));
  Register #(.width(1)) reg_MemToReg_EX_MEM (
    .D(MemToReg_EX), .en(enable_EX_MEM), .clk(clk_EX_MEM), .Q(MemToReg_MEM), .clr(clr_EX_MEM));
  Register #(.width(1)) reg_RegWrite_EX_MEM (
    .D(RegWrite_EX), .en(enable_EX_MEM), .clk(clk_EX_MEM), .Q(RegWrite_MEM), .clr(clr_EX_MEM));
  Register #(.width(1)) reg_MemRead_EX_MEM (
    .D(MemRead_EX), .en(enable_EX_MEM), .clk(clk_EX_MEM), .Q(MemRead_MEM), .clr(clr_EX_MEM));
  Register #(.width(1)) reg_MemWrite_EX_MEM (
    .D(MemWrite_EX), .en(enable_EX_MEM), .clk(clk_EX_MEM), .Q(MemWrite_MEM), .clr(clr_EX_MEM));
  Register #(.width(1)) reg_Bne_ID_EX (.D(Bne_ID), .en(enable_EX_MEM), .clk(clk_EX_MEM), .Q(Bne_EX), .clr(clr_EX_MEM));
  Register #(.width(1)) reg_IsJump_ID_EX (
    .D(isJump_ID), .en(enable_EX_MEM), .clk(clk_EX_MEM), .Q(isJump_EX), .clr(clr_EX_MEM));
  Register #(.width(1)) reg_Branch_ID_EX (
    .D(Branch_ID), .en(enable_EX_MEM), .clk(clk_EX_MEM), .Q(Branch_EX), .clr(clr_EX_MEM));
  Register #(.width(1)) reg_isJR_ID_EX (
    .D(isJR_ID), .en(enable_EX_MEM), .clk(clk_EX_MEM), .Q(isJR_EX), .clr(clr_EX_MEM));
  Register #(.width(1)) reg_isEqual_EX_MEM (
    .D(isEqual_EX), .en(enable_EX_MEM), .clk(clk_EX_MEM), .Q(isEqual_MEM), .clr(clr_EX_MEM));
endmodule

module MEM_WB (
  input  clr_MEM_WB,
  input  clk_MEM_WB,
  input  [31:0] ALUResult_MEM,
  input  isJAL_MEM,
  input  [31:0] DataFromMem_MEM,
  input  MemToReg_MEM,
  input  [4:0] WriteReg_MEM,
  input  RegWrite_MEM,
  input  [31:0] PCPlus4_MEM,
  input  enable_MEM_WB,
  output [31:0] ALUResult_WB,
  output isJAL_WB,
  output [31:0] DataFromMem_WB,
  output MemToReg_WB,
  output [4:0] WriteReg_WB,
  output RegWrite_WB,
  output [31:0] PCPlus4_WB
);

  Register #(.width(32)) reg_ALUResult_MEM_WB (
    .D(ALUResult_MEM), .en(enable_MEM_WB), .clk(clk_MEM_WB), .Q(ALUResult_WB), .clr(clr_MEM_WB));
  Register #(.width(32)) reg_DataFromMem_MEM_WB (
    .D(DataFromMem_MEM), .en(enable_MEM_WB), .clk(clk_MEM_WB), .Q(DataFromMem_WB), .clr(clr_MEM_WB));
  Register #(.width(5)) reg_WriteReg_MEM_WB (
    .D(WriteReg_MEM), .en(enable_MEM_WB), .clk(clk_MEM_WB), .Q(WriteReg_WB), .clr(clr_MEM_WB));
  Register #(.width(32)) reg_PCPlus4_MEM_WB (
    .D(PCPlus4_MEM), .en(enable_MEM_WB), .clk(clk_MEM_WB), .Q(PCPlus4_WB), .clr(clr_MEM_WB));
  Register #(.width(1)) reg_isJAL_MEM_WB (
    .D(isJAL_MEM), .en(enable_MEM_WB), .clk(clk_MEM_WB), .Q(isJAL_WB), .clr(clr_MEM_WB));
  Register #(.width(1)) reg_MemToReg_MEM_WB (
    .D(MemToReg_MEM), .en(enable_MEM_WB), .clk(clk_MEM_WB), .Q(MemToReg_WB), .clr(clr_MEM_WB));
  Register #(.width(1)) reg_RegWrite_MEM_WB (
    .D(RegWrite_MEM), .en(enable_MEM_WB), .clk(clk_MEM_WB), .Q(RegWrite_WB), .clr(clr_MEM_WB));
endmodule

module ID_EXv2 (
  input  clk_ID_EX,
  input  clr_ID_EX,
  input  [31:0] Imm_ID,
  input  [31:0] PCPlus4_ID,
  input  isShift_ID,
  input  MemWrite_ID,
  input  [31:0] R1_ID,
  input  MemToReg_ID,
  input  [3:0] ALUOp_ID,
  input  [31:0] R2_ID,
  input  RegWrite_ID,
  input  [4:0] WriteReg_ID,
  input  [31:0] Shamt_ID,
  input  ALUSrc_ID,
  input  isJAL_ID,
  input  [31:0] JumpAddr_ID,
  input  MemRead_ID,
  input  enable_ID_EX,
  output [31:0] Imm_EX,
  output [31:0] PCPus4_EX,
  output isShift_EX,
  output MemWrite_EX,
  output [31:0] R1_EX,
  output MemToReg_EX,
  output [3:0] ALUOp_EX,
  output [31:0] R2_EX,
  output RegWrite_EX,
  output [4:0] WriteReg_EX,
  output [31:0] Shamt_EX,
  output ALUSrc_EX,
  output isJAL_EX,
  output [31:0] JumpAddr_EX,
  output MemRead_EX
);

  Register #(.width(32)) reg_Immediate_ID_EX (
    .D(Imm_ID), .en(enable_ID_EX), .clk(clk_ID_EX), .Q(Imm_EX), .clr(clr_ID_EX));
  Register #(.width(32)) reg_R1_ID_EX (.D(R1_ID), .en(enable_ID_EX), .clk(clk_ID_EX), .Q(R1_EX), .clr(clr_ID_EX));
  Register #(.width(32)) reg_R2_ID_EX (.D(R2_ID), .en(enable_ID_EX), .clk(clk_ID_EX), .Q(R2_EX), .clr(clr_ID_EX));
  Register #(.width(32)) reg_Shamt_ID_EX (
    .D(Shamt_ID), .en(enable_ID_EX), .clk(clk_ID_EX), .Q(Shamt_EX), .clr(clr_ID_EX));
  Register #(.width(32)) reg_JumpAddr_ID_EX (
    .D(JumpAddr_ID), .en(enable_ID_EX), .clk(clk_ID_EX), .Q(JumpAddr_EX), .clr(clr_ID_EX));
  Register #(.width(32)) regPC_ID_EX (
    .D(PCPlus4_ID), .en(enable_ID_EX), .clk(clk_ID_EX), .Q(PCPus4_EX), .clr(clr_ID_EX));
  Register #(.width(1)) reg_isShift_ID_EX (
    .D(isShift_ID), .en(enable_ID_EX), .clk(clk_ID_EX), .Q(isShift_EX), .clr(clr_ID_EX));
  Register #(.width(1)) reg_MemToReg_ID_EX (
    .D(MemToReg_ID), .en(enable_ID_EX), .clk(clk_ID_EX), .Q(MemToReg_EX), .clr(clr_ID_EX));
  Register #(.width(1)) reg_RegWrite_ID_EX (
    .D(RegWrite_ID), .en(enable_ID_EX), .clk(clk_ID_EX), .Q(RegWrite_EX), .clr(clr_ID_EX));
  Register #(.width(1)) reg_ALUSrc_ID_EX (
    .D(ALUSrc_ID), .en(enable_ID_EX), .clk(clk_ID_EX), .Q(ALUSrc_EX), .clr(clr_ID_EX));
  Register #(.width(1)) reg_MemRead_ID_EX (
    .D(MemRead_ID), .en(enable_ID_EX), .clk(clk_ID_EX), .Q(MemRead_EX), .clr(clr_ID_EX));
  Register #(.width(1)) reg_MemWrite_ID_EX (
    .D(MemWrite_ID), .en(enable_ID_EX), .clk(clk_ID_EX), .Q(MemWrite_EX), .clr(clr_ID_EX));
  Register #(.width(4)) regALUOp_ID_EX (
    .D(ALUOp_ID), .en(enable_ID_EX), .clk(clk_ID_EX), .Q(ALUOp_EX), .clr(clr_ID_EX));
  Register #(.width(5)) regWriteReg_ID_EX (
    .D(WriteReg_ID), .en(enable_ID_EX), .clk(clk_ID_EX), .Q(WriteReg_EX), .clr(clr_ID_EX));
  Register #(.width(1)) reg_isJAL_ID_EX (
    .D(isJAL_ID), .en(enable_ID_EX), .clk(clk_ID_EX), .Q(isJAL_EX), .clr(clr_ID_EX));
endmodule

module EX_MEMv2 (
  input  clr_EX_MEM,
  input  clk_EX_MEM,
  input  [31:0] ALUResult_EX,
  input  isJAL_EX,
  input  [31:0] MemData_EX,
  input  MemToReg_EX,
  input  [4:0] WriteReg_EX,
  input  RegWrite_EX,
  input  [31:0] PCPlus4_EX,
  input  MemRead_EX,
  input  MemWrite_EX,
  input  enable_EX_MEM,
  output [31:0] ALUResult_MEM,
  output isJAL_MEM,
  output [31:0] MemData_MEM,
  output MemToReg_MEM,
  output [4:0] WriteReg_MEM,
  output RegWrite_MEM,
  output [31:0] PCPlus4_MEM,
  output MemRead_MEM,
  output MemWrite_MEM
);

  Register #(.width(32)) reg_ALUResult_EX_MEM (
    .D(ALUResult_EX), .en(enable_EX_MEM), .clk(clk_EX_MEM), .Q(ALUResult_MEM), .clr(clr_EX_MEM));
  Register #(.width(32)) reg_MemData_EX_MEM (
    .D(MemData_EX), .en(enable_EX_MEM), .clk(clk_EX_MEM), .Q(MemData_MEM), .clr(clr_EX_MEM));
  Register #(.width(5)) reg_WriteReg_EX_MEM (
    .D(WriteReg_EX), .en(enable_EX_MEM), .clk(clk_EX_MEM), .Q(WriteReg_MEM), .clr(clr_EX_MEM));
  Register #(.width(32)) reg_PCPlus4_EX_MEM (
    .D(PCPlus4_EX), .en(enable_EX_MEM), .clk(clk_EX_MEM), .Q(PCPlus4_MEM), .clr(clr_EX_MEM));
  Register #(.width(1)) reg_isJAL_EX_MEM (
    .D(isJAL_EX), .en(enable_EX_MEM), .clk(clk_EX_MEM), .Q(isJAL_MEM), .clr(clr_EX_MEM));
  Register #(.width(1)) reg_MemToReg_EX_MEM (
    .D(MemToReg_EX), .en(enable_EX_MEM), .clk(clk_EX_MEM), .Q(MemToReg_MEM), .clr(clr_EX_MEM));
  Register #(.width(1)) reg_RegWrite_EX_MEM (
    .D(RegWrite_EX), .en(enable_EX_MEM), .clk(clk_EX_MEM), .Q(RegWrite_MEM), .clr(clr_EX_MEM));
  Register #(.width(1)) reg_MemRead_EX_MEM (
    .D(MemRead_EX), .en(enable_EX_MEM), .clk(clk_EX_MEM), .Q(MemRead_MEM), .clr(clr_EX_MEM));
  Register #(.width(1)) reg_MemWrite_EX_MEM (
    .D(MemWrite_EX), .en(enable_EX_MEM), .clk(clk_EX_MEM), .Q(MemWrite_MEM), .clr(clr_EX_MEM));
endmodule

module IF_ID_JTB (
  input  clk_IF_ID,
  input  clr_IF_ID,
  input  [31:0] Instruction_IF,
  input  [31:0] PCPlus4_IF,
  input  updateJTB_IF,
  input  enable_IF_ID,
  output [31:0] Instruction_ID,
  output [31:0] PCPus4_ID,
  output updateJTB_ID
);

  Register #(.width(32)) reg_Instruction_IF_ID (
    .D(Instruction_IF), .en(enable_IF_ID), .clk(clk_IF_ID), .Q(Instruction_ID), .clr(clr_IF_ID));
  Register #(.width(32)) reg_PCPlus4_IF_ID (
    .D(PCPlus4_IF), .en(enable_IF_ID), .clk(clk_IF_ID), .Q(PCPus4_ID), .clr(clr_IF_ID));
  Register #(.width(1)) register_1 (
    .D(updateJTB_IF), .en(enable_IF_ID), .clk(clk_IF_ID), .Q(updateJTB_ID), .clr(clr_IF_ID));
endmodule
