// Logisim project UnidadeDeControle.circ as structural Verilog: 6 circuits, main circuit ControlUnit
module ControlUnit (
  input  [5:0] opcode,
  input  [5:0] funct,
  output BNE,
  output [3:0] ALUop,
  output Branch,
  output isJAL,
  output isJump,
  output MemToReg,
  output ZeroExtend,
  output MemRead,
  output ALUSrc,
  output MemWrite,
  output RegWrite,
  output RegDest,
  output ReadingRs,
  output isJR,
  output ReadingRt,
  output isShift
);

  wire and_1_out, functtoaluoperation_1_isjr, functtoaluoperation_1_shiftoperation, not_1_out, not_2_out,
       not_3_out, not_4_out, not_5_out, not_6_out;
  wire [3:0] functtoaluoperation_1_aluop0, instructiontoaluoperation_1_aluop0;

  FlagsDecoder flagsdecoder_1 (
    .op1(opcode[1]), .op2(opcode[2]), .op3(opcode[3]), .op4(opcode[4]), .op5(opcode[5]), .op0(opcode[0]),
    .MemWrite(MemWrite), .RegDest(RegDest), .Bne(BNE), .Branch(Branch), .Jump(isJump), .isJal(isJAL),
    .ZeroExtnd(ZeroExtend), .ALUSrc(ALUSrc), .RegWrite(RegWrite), .MemToReg(MemToReg), .MemRead(MemRead));
  not not_1 (not_1_out, opcode[5]);
  not not_2 (not_2_out, opcode[4]);
  not not_3 (not_3_out, opcode[3]);
  not not_4 (not_4_out, opcode[2]);
  not not_5 (not_5_out, opcode[1]);
  not not_6 (not_6_out, opcode[0]);
  and and_1 (and_1_out, not_1_out, not_2_out, not_3_out, not_4_out, not_5_out, not_6_out);
  RegisterReadDetector registerreaddetector_1 (
    .f2(funct[2]), .f3(funct[3]), .f4(funct[4]), .f5(funct[5]), .f0(funct[0]), .isRType(and_1_out),
    .op1(opcode[1]), .op2(opcode[2]), .op3(opcode[3]), .op4(opcode[4]), .op5(opcode[5]), .op0(opcode[0]),
    .f1(funct[1]), .ReadRt(ReadingRt), .ReadRs(ReadingRs));
  InstructionToALUOperation instructiontoaluoperation_1 (
    .op1(opcode[1]), .op2(opcode[2]), .op3(opcode[3]), .op4(opcode[4]), .op5(opcode[5]), .op0(opcode[0]),
    .ALUop1(instructiontoaluoperation_1_aluop0[1]), .ALUop2(instructiontoaluoperation_1_aluop0[2]),
    .ALUop3(instructiontoaluoperation_1_aluop0[3]), .ALUop0(instructiontoaluoperation_1_aluop0[0]));
  FunctToALUOperation functtoaluoperation_1 (
    .f1(funct[1]), .f2(funct[2]), .f3(funct[3]), .f4(funct[4]), .f5(funct[5]), .f0(funct[0]),
    .ALUop1(functtoaluoperation_1_aluop0[1]), .ALUop2(functtoaluoperation_1_aluop0[2]),
    .ALUop3(functtoaluoperation_1_aluop0[3]), .shiftOperation(functtoaluoperation_1_shiftoperation),
    .ALUop0(functtoaluoperation_1_aluop0[0]), .isJR(functtoaluoperation_1_isjr));
  Multiplexer #(.width(4)) multiplexer_1 (
    .in0(instructiontoaluoperation_1_aluop0), .in1(functtoaluoperation_1_aluop0), .out(ALUop), .sel(and_1_out));
  and and_2 (isJR, and_1_out, functtoaluoperation_1_isjr);
  and and_3 (isShift, and_1_out, functtoaluoperation_1_shiftoperation);

  // Other names for the same wires on the sheet: Jump = isJump; ReadRs = ReadingRs; ReadRt = ReadingRt

  // Notes on the sheet:
  //   Input and Output
  //   Control Flags Decoding
  //   isRType?
  //   ALU Operation Decoding
endmodule

module InstructionToALUOperation (
  input  op0,
  input  op1,
  input  op2,
  input  op3,
  input  op4,
  input  op5,
  output ALUop0,
  output ALUop1,
  output ALUop2,
  output ALUop3
);

  wire and_1_out, and_2_out, and_3_out, and_4_out, and_5_out, and_6_out, and_7_out, and_8_out, not_1_out,
       not_2_out, not_3_out, not_4_out, not_5_out, not_6_out, not_7_out, not_8_out, not_9_out, not_10_out,
       not_11_out, not_12_out, not_13_out, not_14_out, not_15_out, not_16_out, not_17_out, not_18_out,
       not_19_out, not_20_out, not_21_out, not_22_out, not_23_out, not_24_out, not_25_out, not_26_out,
       not_27_out, not_28_out, not_29_out, not_30_out, not_31_out, not_32_out;

  not not_1 (not_1_out, op5);
  not not_2 (not_2_out, op4);
  not not_3 (not_3_out, op1);
  and and_1 (and_1_out, not_1_out, not_2_out, op3, op2, not_3_out, op0);
  not not_4 (not_4_out, op5);
  not not_5 (not_5_out, op4);
  not not_6 (not_6_out, op3);
  not not_7 (not_7_out, op1);
  not not_8 (not_8_out, op0);
  and and_2 (and_2_out, not_4_out, not_5_out, not_6_out, op2, not_7_out, not_8_out);
  or or_1 (ALUop0, and_1_out, and_2_out, and_3_out);
  not not_9 (not_9_out, op5);
  not not_10 (not_10_out, op4);
  not not_11 (not_11_out, op3);
  not not_12 (not_12_out, op1);
  and and_3 (and_3_out, not_9_out, not_10_out, not_11_out, op2, not_12_out, op0);
  not not_13 (not_13_out, op1);
  not not_14 (not_14_out, op0);
  not not_15 (not_15_out, op5);
  not not_16 (not_16_out, op4);
  and and_4 (and_4_out, not_15_out, not_16_out, op3, op2, not_13_out, not_14_out);
  not not_17 (not_17_out, op5);
  not not_18 (not_18_out, op4);
  and and_5 (and_5_out, not_17_out, not_18_out, op3, op2, not_19_out, op0);
  or or_2 (ALUop1, and_4_out, and_5_out);
  not not_19 (not_19_out, op1);
  not not_20 (not_20_out, op5);
  not not_21 (not_21_out, op4);
  not not_22 (not_22_out, op3);
  not not_23 (not_23_out, op1);
  and and_6 (and_6_out, not_20_out, not_21_out, not_22_out, op2, not_23_out, not_24_out);
  not not_24 (not_24_out, op0);
  not not_25 (not_25_out, op5);
  not not_26 (not_26_out, op4);
  not not_27 (not_27_out, op3);
  not not_28 (not_28_out, op1);
  and and_7 (and_7_out, not_25_out, not_26_out, not_27_out, op2, not_28_out, op0);
  or or_3 (ALUop3, and_6_out, and_7_out, and_8_out);
  not not_29 (not_29_out, op5);
  not not_30 (not_30_out, op4);
  not not_31 (not_31_out, op2);
  not not_32 (not_32_out, op0);
  and and_8 (and_8_out, not_29_out, not_30_out, op3, not_31_out, op1, not_32_out);

  assign ALUop2 = 1'b0;

  // Notes on the sheet:
  //   PRI
  //   BEQ
  //   BNE
  //   ANDI
  //   ORI
  //   BEQ
  //   BNE
  //   SLTI
endmodule

module FunctToALUOperation (
  input  f0,
  input  f1,
  input  f2,
  input  f3,
  input  f4,
  input  f5,
  output ALUop1,
  output ALUop2,
  output ALUop3,
  output shiftOperation,
  output isJR,
  output ALUop0
);

  wire and_1_out, and_2_out, and_3_out, and_4_out, and_5_out, and_6_out, and_7_out, and_8_out, and_9_out,
       and_10_out, and_11_out, and_12_out, and_14_out, and_15_out, not_1_out, not_2_out, not_3_out,
       not_4_out, not_5_out, not_6_out, not_7_out, not_8_out, not_9_out, not_10_out, not_11_out, not_12_out,
       not_13_out, not_14_out, not_15_out, not_16_out, not_17_out, not_18_out, not_19_out, not_20_out,
       not_21_out, not_22_out, not_23_out, not_24_out, not_25_out, not_26_out, not_27_out, not_28_out,
       not_29_out, not_30_out, not_31_out, not_32_out, not_33_out, not_34_out, not_35_out, not_36_out,
       not_37_out, not_38_out, not_39_out, not_40_out, not_41_out, not_42_out, not_43_out, not_44_out,
       not_45_out, not_46_out, not_47_out, not_48_out, not_49_out, not_50_out, not_51_out, not_52_out,
       not_53_out, not_54_out, not_55_out, not_56_out, not_57_out, not_58_out, not_59_out, not_60_out,
       not_61_out, not_62_out, not_63_out, not_64_out, not_65_out, not_66_out, not_67_out;

  not not_1 (not_1_out, f5);
  not not_2 (not_2_out, f4);
  not not_3 (not_3_out, f3);
  not not_4 (not_4_out, f2);
  and and_1 (and_1_out, not_1_out, not_2_out, not_3_out, not_4_out, f1, not_5_out);
  not not_5 (not_5_out, f0);
  not not_6 (not_6_out, f4);
  not not_7 (not_7_out, f3);
  not not_8 (not_8_out, f2);
  not not_9 (not_9_out, f0);
  and and_2 (and_2_out, f5, not_6_out, not_7_out, not_8_out, f1, not_9_out);
  or or_1 (ALUop0, and_1_out, and_2_out, and_3_out, and_4_out);
  not not_10 (not_10_out, f4);
  not not_11 (not_11_out, f3);
  not not_12 (not_12_out, f1);
  and and_3 (and_3_out, f5, not_10_out, not_11_out, f2, not_12_out, f0);
  not not_13 (not_13_out, f4);
  not not_14 (not_14_out, f3);
  and and_4 (and_4_out, f5, not_13_out, not_14_out, f2, f1, f0);
  not not_15 (not_15_out, f4);
  not not_16 (not_16_out, f0);
  not not_17 (not_17_out, f3);
  not not_18 (not_18_out, f1);
  and and_5 (and_5_out, f5, not_15_out, not_17_out, f2, not_18_out, not_16_out);
  not not_19 (not_19_out, f5);
  not not_20 (not_20_out, f4);
  not not_21 (not_21_out, f3);
  not not_22 (not_22_out, f2);
  not not_23 (not_23_out, f1);
  and and_6 (and_6_out, not_19_out, not_20_out, not_21_out, not_22_out, not_23_out, not_24_out);
  not not_24 (not_24_out, f0);
  not not_25 (not_25_out, f5);
  not not_26 (not_26_out, f4);
  or or_2 (ALUop1, and_5_out, and_6_out, and_7_out, and_8_out);
  not not_27 (not_27_out, f3);
  not not_28 (not_28_out, f2);
  not not_29 (not_29_out, f0);
  and and_7 (and_7_out, not_25_out, not_26_out, not_27_out, not_28_out, f1, not_29_out);
  not not_30 (not_30_out, f4);
  not not_31 (not_31_out, f3);
  not not_32 (not_32_out, f1);
  and and_8 (and_8_out, f5, not_30_out, not_31_out, f2, not_32_out, f0);
  not not_33 (not_33_out, f5);
  not not_34 (not_34_out, f4);
  not not_35 (not_35_out, f3);
  and and_9 (and_9_out, not_33_out, not_34_out, not_35_out, not_36_out, not_37_out, not_38_out);
  not not_36 (not_36_out, f2);
  not not_37 (not_37_out, f1);
  not not_38 (not_38_out, f0);
  not not_39 (not_39_out, f5);
  not not_40 (not_40_out, f4);
  not not_41 (not_41_out, f3);
  not not_42 (not_42_out, f2);
  not not_43 (not_43_out, f0);
  and and_10 (and_10_out, not_39_out, not_40_out, not_41_out, not_42_out, f1, not_43_out);
  not not_44 (not_44_out, f4);
  not not_45 (not_45_out, f3);
  and and_11 (and_11_out, f5, not_44_out, not_45_out, f2, f1, not_46_out);
  or or_3 (ALUop2, and_9_out, and_10_out, and_11_out, and_12_out);
  not not_46 (not_46_out, f0);
  not not_47 (not_47_out, f4);
  not not_48 (not_48_out, f3);
  and and_12 (and_12_out, f5, not_47_out, not_48_out, f2, f1, f0);
  not not_49 (not_49_out, f4);
  not not_50 (not_50_out, f2);
  not not_51 (not_51_out, f0);
  and and_13 (ALUop3, f5, not_49_out, f3, not_50_out, f1, not_51_out);
  not not_52 (not_52_out, f5);
  not not_53 (not_53_out, f4);
  not not_54 (not_54_out, f3);
  and and_14 (and_14_out, not_52_out, not_53_out, not_54_out, not_55_out, not_56_out, not_57_out);
  not not_55 (not_55_out, f2);
  not not_56 (not_56_out, f1);
  not not_57 (not_57_out, f0);
  or or_4 (shiftOperation, and_14_out, and_15_out);
  not not_58 (not_58_out, f5);
  not not_59 (not_59_out, f4);
  not not_60 (not_60_out, f3);
  not not_61 (not_61_out, f2);
  not not_62 (not_62_out, f0);
  and and_15 (and_15_out, not_58_out, not_59_out, not_60_out, not_61_out, f1, not_62_out);
  not not_63 (not_63_out, f5);
  not not_64 (not_64_out, f4);
  not not_65 (not_65_out, f2);
  and and_16 (isJR, not_63_out, not_64_out, f3, not_65_out, not_66_out, not_67_out);
  not not_66 (not_66_out, f1);
  not not_67 (not_67_out, f0);

  // Notes on the sheet:
  //   SRL
  //   SUB
  //   OR
  //   NOR
  //   AND
  //   SLL
  //   SRL
  //   OR
  //   SLL
  //   SRL
  //   XOR
  //   NOR
  //   SLT
  //   SLL
  //   SRL
  //   JR
endmodule

module FlagsDecoder (
  input  op0,
  input  op1,
  input  op2,
  input  op3,
  input  op4,
  input  op5,
  output isJal,
  output MemToReg,
  output MemRead,
  output MemWrite,
  output RegDest,
  output Bne,
  output Branch,
  output Jump,
  output ZeroExtnd,
  output ALUSrc,
  output RegWrite
);

  wire and_7_out, and_8_out, and_9_out, and_10_out, and_11_out, and_12_out, and_13_out, and_14_out,
       and_15_out, and_16_out, and_17_out, and_18_out, and_19_out, and_20_out, and_21_out, and_22_out,
       and_23_out, and_24_out, and_25_out, not_1_out, not_2_out, not_3_out, not_4_out, not_5_out, not_6_out,
       not_7_out, not_8_out, not_9_out, not_10_out, not_11_out, not_12_out, not_13_out, not_14_out,
       not_15_out, not_16_out, not_17_out, not_18_out, not_19_out, not_20_out, not_21_out, not_22_out,
       not_23_out, not_24_out, not_25_out, not_26_out, not_27_out, not_28_out, not_29_out, not_30_out,
       not_31_out, not_32_out, not_33_out, not_34_out, not_35_out, not_36_out, not_37_out, not_38_out,
       not_39_out, not_40_out, not_41_out, not_42_out, not_43_out, not_44_out, not_45_out, not_46_out,
       not_47_out, not_48_out, not_49_out, not_50_out, not_51_out, not_52_out, not_53_out, not_54_out,
       not_55_out, not_56_out, not_57_out, not_58_out, not_59_out, not_60_out, not_61_out, not_62_out,
       not_63_out, not_64_out, not_65_out, not_66_out, not_67_out, not_68_out, not_69_out, not_70_out,
       not_71_out, not_72_out, not_73_out, not_74_out, not_75_out, not_76_out, not_77_out, not_78_out,
       not_79_out, not_80_out, not_81_out, not_82_out, not_83_out, not_84_out, not_85_out, not_86_out,
       not_87_out, not_88_out, not_89_out, not_90_out, not_91_out, not_92_out, not_93_out, not_94_out,
       not_95_out, not_96_out, not_97_out;

  not not_1 (not_1_out, op5);
  not not_2 (not_2_out, op4);
  not not_3 (not_3_out, op3);
  not not_4 (not_4_out, op2);
  and and_1 (isJal, not_1_out, not_2_out, not_3_out, not_4_out, op1, op0);
  not not_5 (not_5_out, op4);
  not not_6 (not_6_out, op3);
  not not_7 (not_7_out, op2);
  and and_2 (MemToReg, op5, not_5_out, not_6_out, not_7_out, op1, op0);
  not not_8 (not_8_out, op4);
  not not_9 (not_9_out, op3);
  not not_10 (not_10_out, op2);
  and and_3 (MemRead, op5, not_8_out, not_9_out, not_10_out, op1, op0);
  not not_11 (not_11_out, op4);
  not not_12 (not_12_out, op2);
  and and_4 (MemWrite, op5, not_11_out, op3, not_12_out, op1, op0);
  not not_13 (not_13_out, op5);
  not not_14 (not_14_out, op4);
  not not_15 (not_15_out, op3);
  and and_5 (RegDest, not_13_out, not_14_out, not_15_out, not_16_out, not_17_out, not_18_out);
  not not_16 (not_16_out, op2);
  not not_17 (not_17_out, op1);
  not not_18 (not_18_out, op0);
  not not_19 (not_19_out, op5);
  not not_20 (not_20_out, op4);
  not not_21 (not_21_out, op3);
  not not_22 (not_22_out, op1);
  and and_6 (Bne, not_19_out, not_20_out, not_21_out, op2, not_22_out, op0);
  not not_23 (not_23_out, op5);
  not not_24 (not_24_out, op4);
  not not_25 (not_25_out, op3);
  not not_26 (not_26_out, op1);
  and and_7 (and_7_out, not_23_out, not_24_out, not_25_out, op2, not_26_out, not_27_out);
  not not_27 (not_27_out, op0);
  not not_28 (not_28_out, op5);
  not not_29 (not_29_out, op4);
  or or_1 (Branch, and_7_out, and_8_out);
  not not_30 (not_30_out, op3);
  not not_31 (not_31_out, op1);
  and and_8 (and_8_out, not_28_out, not_29_out, not_30_out, op2, not_31_out, op0);
  not not_32 (not_32_out, op5);
  not not_33 (not_33_out, op4);
  not not_34 (not_34_out, op3);
  not not_35 (not_35_out, op2);
  not not_36 (not_36_out, op0);
  and and_9 (and_9_out, not_32_out, not_33_out, not_34_out, not_35_out, op1, not_36_out);
  not not_37 (not_37_out, op5);
  not not_38 (not_38_out, op4);
  not not_39 (not_39_out, op3);
  or or_2 (Jump, and_9_out, and_10_out);
  not not_40 (not_40_out, op2);
  and and_10 (and_10_out, not_37_out, not_38_out, not_39_out, not_40_out, op1, op0);
  not not_41 (not_41_out, op5);
  not not_42 (not_42_out, op4);
  not not_43 (not_43_out, op1);
  not not_44 (not_44_out, op0);
  and and_11 (and_11_out, not_41_out, not_42_out, op3, op2, not_43_out, not_44_out);
  not not_45 (not_45_out, op5);
  not not_46 (not_46_out, op4);
  and and_12 (and_12_out, not_45_out, not_46_out, op3, op2, not_47_out, op0);
  or or_3 (ZeroExtnd, and_11_out, and_12_out);
  not not_47 (not_47_out, op1);
  not not_48 (not_48_out, op5);
  not not_49 (not_49_out, op4);
  not not_50 (not_50_out, op2);
  not not_51 (not_51_out, op1);
  not not_52 (not_52_out, op0);
  and and_13 (and_13_out, not_48_out, not_49_out, op3, not_50_out, not_51_out, not_52_out);
  not not_53 (not_53_out, op5);
  not not_54 (not_54_out, op4);
  and and_14 (and_14_out, not_53_out, not_54_out, op3, op2, not_55_out, not_56_out);
  not not_55 (not_55_out, op1);
  not not_56 (not_56_out, op0);
  not not_57 (not_57_out, op5);
  not not_58 (not_58_out, op4);
  not not_59 (not_59_out, op1);
  and and_15 (and_15_out, not_57_out, not_58_out, op3, op2, not_59_out, op0);
  not not_60 (not_60_out, op4);
  not not_61 (not_61_out, op3);
  not not_62 (not_62_out, op2);
  and and_16 (and_16_out, op5, not_60_out, not_61_out, not_62_out, op1, op0);
  or or_4 (ALUSrc, and_13_out, and_14_out, and_15_out, and_16_out, and_17_out, and_18_out);
  not not_63 (not_63_out, op4);
  not not_64 (not_64_out, op2);
  and and_17 (and_17_out, op5, not_63_out, op3, not_64_out, op1, op0);
  not not_65 (not_65_out, op5);
  not not_66 (not_66_out, op4);
  not not_67 (not_67_out, op2);
  and and_18 (and_18_out, not_65_out, not_66_out, op3, not_67_out, op1, not_68_out);
  not not_68 (not_68_out, op0);
  not not_69 (not_69_out, op5);
  not not_70 (not_70_out, op4);
  not not_71 (not_71_out, op3);
  not not_72 (not_72_out, op2);
  not not_73 (not_73_out, op1);
  not not_74 (not_74_out, op0);
  and and_19 (and_19_out, not_69_out, not_70_out, not_71_out, not_72_out, not_73_out, not_74_out);
  not not_75 (not_75_out, op5);
  not not_76 (not_76_out, op4);
  not not_77 (not_77_out, op2);
  not not_78 (not_78_out, op1);
  and and_20 (and_20_out, not_75_out, not_76_out, op3, not_77_out, not_78_out, not_79_out);
  not not_79 (not_79_out, op0);
  not not_80 (not_80_out, op5);
  not not_81 (not_81_out, op4);
  not not_82 (not_82_out, op1);
  not not_83 (not_83_out, op0);
  and and_21 (and_21_out, not_80_out, not_81_out, op3, op2, not_82_out, not_83_out);
  not not_84 (not_84_out, op5);
  not not_85 (not_85_out, op4);
  not not_86 (not_86_out, op1);
  and and_22 (and_22_out, not_84_out, not_85_out, op3, op2, not_86_out, op0);
  or or_5 (RegWrite, and_19_out, and_20_out, and_21_out, and_22_out, and_23_out, and_24_out, and_25_out);
  not not_87 (not_87_out, op4);
  not not_88 (not_88_out, op3);
  not not_89 (not_89_out, op2);
  and and_23 (and_23_out, op5, not_87_out, not_88_out, not_89_out, op1, op0);
  not not_90 (not_90_out, op5);
  not not_91 (not_91_out, op4);
  not not_92 (not_92_out, op2);
  and and_24 (and_24_out, not_90_out, not_91_out, op3, not_92_out, op1, not_93_out);
  not not_93 (not_93_out, op0);
  not not_94 (not_94_out, op5);
  not not_95 (not_95_out, op4);
  not not_96 (not_96_out, op3);
  not not_97 (not_97_out, op2);
  and and_25 (and_25_out, not_94_out, not_95_out, not_96_out, not_97_out, op1, op0);

  // Notes on the sheet:
  //   JAL
  //   LW
  //   LW
  //   SW
  //   (R-Type)
  //   ADD
  //   AND
  //   SLL
  //   SRL
  //   SUB
  //   OR
  //   SLT
  //   BNE
  //   BEQ
  //   BNE
  //   J
  //   JAL
  //   ANDI
  //   ORI
  //   ADDI
  //   ANDI
  //   ORI
  //   LW
  //   SW
  //   SLTI
  //   (R-Type)
  //   ADD
  //   AND
  //   SLL
  //   SRL
  //   SUB
  //   OR
  //   SLT
  //   ADDI
  //   ANDI
  //   ORI
  //   LW
  //   SLTI
  //   JAL
endmodule

module RegisterReadDetector (
  input  op0,
  input  op1,
  input  op2,
  input  op3,
  input  op4,
  input  op5,
  input  isRType,
  input  f0,
  input  f1,
  input  f2,
  input  f3,
  input  f4,
  input  f5,
  output ReadRs,
  output ReadRt
);

  wire and_1_out, and_2_out, and_3_out, and_4_out, and_5_out, and_6_out, and_7_out, and_8_out, and_9_out,
       and_10_out, and_11_out, and_12_out, and_13_out, and_14_out, and_15_out, and_16_out, and_17_out,
       and_18_out, and_19_out, and_20_out, and_21_out, and_22_out, and_23_out, and_24_out, and_25_out,
       and_26_out, not_1_out, not_2_out, not_3_out, not_4_out, not_5_out, not_6_out, not_7_out, not_8_out,
       not_9_out, not_10_out, not_11_out, not_12_out, not_13_out, not_14_out, not_15_out, not_16_out,
       not_17_out, not_18_out, not_19_out, not_20_out, not_21_out, not_22_out, not_23_out, not_24_out,
       not_25_out, not_26_out, not_27_out, not_28_out, not_29_out, not_30_out, not_31_out, not_32_out,
       not_33_out, not_34_out, not_35_out, not_36_out, not_37_out, not_38_out, not_39_out, not_40_out,
       not_41_out, not_42_out, not_43_out, not_44_out, not_45_out, not_46_out, not_47_out, not_48_out,
       not_49_out, not_50_out, not_51_out, not_52_out, not_53_out, not_54_out, not_55_out, not_56_out,
       not_57_out, not_58_out, not_59_out, not_60_out, not_61_out, not_62_out, not_63_out, not_64_out,
       not_65_out, not_66_out, not_67_out, not_68_out, not_69_out, not_70_out, not_71_out, not_72_out,
       not_73_out, not_74_out, not_75_out, not_76_out, not_77_out, not_78_out, not_79_out, not_80_out,
       not_81_out, not_82_out, not_83_out, not_84_out, not_85_out, not_86_out, not_87_out, not_88_out,
       not_89_out, not_90_out, not_91_out, not_92_out, not_93_out, not_94_out, not_95_out, or_1_out,
       or_2_out, or_4_out, or_6_out;

  not not_1 (not_1_out, f4);
  not not_2 (not_2_out, f3);
  not not_3 (not_3_out, f2);
  not not_4 (not_4_out, f1);
  not not_5 (not_5_out, f0);
  not not_6 (not_6_out, f4);
  not not_7 (not_7_out, f3);
  not not_8 (not_8_out, f1);
  not not_9 (not_9_out, f0);
  not not_10 (not_10_out, f4);
  not not_11 (not_11_out, f3);
  not not_12 (not_12_out, f2);
  not not_13 (not_13_out, f0);
  not not_14 (not_14_out, f4);
  not not_15 (not_15_out, f3);
  not not_16 (not_16_out, f1);
  not not_17 (not_17_out, f4);
  not not_18 (not_18_out, f2);
  not not_19 (not_19_out, f0);
  not not_20 (not_20_out, f5);
  not not_21 (not_21_out, f4);
  not not_22 (not_22_out, f2);
  not not_23 (not_23_out, f1);
  not not_24 (not_24_out, f0);
  not not_25 (not_25_out, f4);
  not not_26 (not_26_out, f3);
  not not_27 (not_27_out, f2);
  not not_28 (not_28_out, f1);
  not not_29 (not_29_out, f0);
  not not_30 (not_30_out, f4);
  not not_31 (not_31_out, f3);
  not not_32 (not_32_out, f1);
  not not_33 (not_33_out, f0);
  not not_34 (not_34_out, f5);
  not not_35 (not_35_out, f4);
  not not_36 (not_36_out, f3);
  not not_37 (not_37_out, f2);
  not not_38 (not_38_out, f1);
  not not_39 (not_39_out, f0);
  not not_40 (not_40_out, f5);
  not not_41 (not_41_out, f4);
  not not_42 (not_42_out, f3);
  not not_43 (not_43_out, f2);
  not not_44 (not_44_out, f0);
  not not_45 (not_45_out, f4);
  not not_46 (not_46_out, f3);
  not not_47 (not_47_out, f2);
  not not_48 (not_48_out, f0);
  not not_49 (not_49_out, f4);
  not not_50 (not_50_out, f3);
  not not_51 (not_51_out, f1);
  not not_52 (not_52_out, f4);
  not not_53 (not_53_out, f2);
  not not_54 (not_54_out, f0);
  and and_1 (and_1_out, f5, not_1_out, not_2_out, not_3_out, not_4_out, not_5_out);
  and and_2 (and_2_out, f5, not_6_out, not_7_out, f2, not_8_out, not_9_out);
  and and_3 (and_3_out, f5, not_10_out, not_11_out, not_12_out, f1, not_13_out);
  and and_4 (and_4_out, f5, not_14_out, not_15_out, f2, not_16_out, f0);
  and and_5 (and_5_out, f5, not_17_out, f3, not_18_out, f1, not_19_out);
  and and_6 (and_6_out, not_20_out, not_21_out, f3, not_22_out, not_23_out, not_24_out);
  and and_7 (and_7_out, f5, not_25_out, not_26_out, not_27_out, not_28_out, not_29_out);
  and and_8 (and_8_out, f5, not_30_out, not_31_out, f2, not_32_out, not_33_out);
  and and_9 (and_9_out, not_34_out, not_35_out, not_36_out, not_37_out, not_38_out, not_39_out);
  and and_10 (and_10_out, not_40_out, not_41_out, not_42_out, not_43_out, f1, not_44_out);
  and and_11 (and_11_out, f5, not_45_out, not_46_out, not_47_out, f1, not_48_out);
  and and_12 (and_12_out, f5, not_49_out, not_50_out, f2, not_51_out, f0);
  and and_13 (and_13_out, f5, not_52_out, f3, not_53_out, f1, not_54_out);
  or or_1 (or_1_out, and_1_out, and_2_out, and_3_out, and_4_out, and_5_out, and_6_out);
  or or_2 (or_2_out, and_7_out, and_8_out, and_9_out, and_10_out, and_11_out, and_12_out, and_13_out);
  and and_14 (and_14_out, isRType, or_1_out);
  and and_15 (and_15_out, isRType, or_2_out);
  not not_55 (not_55_out, op5);
  not not_56 (not_56_out, op4);
  not not_57 (not_57_out, op2);
  not not_58 (not_58_out, op1);
  and and_16 (and_16_out, not_55_out, not_56_out, op3, not_57_out, not_58_out, not_59_out);
  not not_59 (not_59_out, op0);
  not not_60 (not_60_out, op5);
  not not_61 (not_61_out, op4);
  not not_62 (not_62_out, op1);
  and and_17 (and_17_out, not_60_out, not_61_out, op3, op2, not_62_out, not_63_out);
  not not_63 (not_63_out, op0);
  not not_64 (not_64_out, op5);
  not not_65 (not_65_out, op4);
  not not_66 (not_66_out, op1);
  and and_18 (and_18_out, not_64_out, not_65_out, op3, op2, not_66_out, op0);
  not not_67 (not_67_out, op3);
  not not_68 (not_68_out, op2);
  not not_69 (not_69_out, op4);
  and and_19 (and_19_out, op5, not_69_out, not_67_out, not_68_out, op1, op0);
  or or_3 (ReadRs, and_14_out, or_4_out);
  not not_70 (not_70_out, op4);
  not not_71 (not_71_out, op2);
  and and_20 (and_20_out, op5, not_70_out, op3, not_71_out, op1, op0);
  or or_4 (or_4_out, and_16_out, and_17_out, and_18_out, and_19_out, and_20_out, and_21_out, and_22_out, and_23_out);
  not not_72 (not_72_out, op5);
  not not_73 (not_73_out, op4);
  not not_74 (not_74_out, op3);
  not not_75 (not_75_out, op1);
  and and_21 (and_21_out, not_72_out, not_73_out, not_74_out, op2, not_75_out, not_76_out);
  not not_76 (not_76_out, op0);
  not not_77 (not_77_out, op5);
  not not_78 (not_78_out, op4);
  not not_79 (not_79_out, op3);
  not not_80 (not_80_out, op1);
  and and_22 (and_22_out, not_77_out, not_78_out, not_79_out, op2, not_80_out, op0);
  not not_81 (not_81_out, op5);
  not not_82 (not_82_out, op4);
  not not_83 (not_83_out, op2);
  and and_23 (and_23_out, not_81_out, not_82_out, op3, not_83_out, op1, not_84_out);
  not not_84 (not_84_out, op0);
  not not_85 (not_85_out, op4);
  or or_5 (ReadRt, and_15_out, or_6_out);
  not not_86 (not_86_out, op2);
  not not_87 (not_87_out, op5);
  not not_88 (not_88_out, op4);
  not not_89 (not_89_out, op3);
  and and_24 (and_24_out, op5, not_85_out, op3, not_86_out, op1, op0);
  not not_90 (not_90_out, op1);
  not not_91 (not_91_out, op0);
  not not_92 (not_92_out, op5);
  not not_93 (not_93_out, op4);
  not not_94 (not_94_out, op3);
  and and_25 (and_25_out, not_87_out, not_88_out, not_89_out, op2, not_90_out, not_91_out);
  or or_6 (or_6_out, and_24_out, and_25_out, and_26_out);
  not not_95 (not_95_out, op1);
  and and_26 (and_26_out, not_92_out, not_93_out, not_94_out, op2, not_95_out, op0);

  // Notes on the sheet:
  //   ADD
  //   AND
  //   SUB
  //   OR
  //   SLT
  //   JR
  //   ADD
  //   AND
  //   SLL
  //   SRL
  //   SUB
  //   OR
  //   SLT
  //   ADDI
  //   ANDI
  //   ORI
  //   LW
  //   SW
  //   BEQ
  //   BNE
  //   SLTI
  //   SW
  //   BEQ
  //   BNE
endmodule

module ControlUnit_alt (
  input  [5:0] opcode,
  input  [5:0] funct,
  output BNE,
  output [3:0] ALUop,
  output Branch,
  output isJAL,
  output Jump,
  output MemToReg,
  output ZeroExtend,
  output MemRead,
  output ALUSrc,
  output MemWrite,
  output RegWrite,
  output RegDest,
  output ReadingRs,
  output isJR,
  output ReadingRt,
  output isShift
);

  wire and_1_out, functtoaluoperation_1_isjr, functtoaluoperation_1_shiftoperation, not_1_out, not_2_out,
       not_3_out, not_4_out, not_5_out, not_6_out;
  wire [3:0] functtoaluoperation_1_aluop0, instructiontoaluoperation_1_aluop0;

  FlagsDecoder flagsdecoder_1 (
    .op1(opcode[1]), .op2(opcode[2]), .op3(opcode[3]), .op4(opcode[4]), .op5(opcode[5]), .op0(opcode[0]),
    .MemWrite(MemWrite), .RegDest(RegDest), .Bne(BNE), .Branch(Branch), .Jump(Jump), .isJal(isJAL),
    .ZeroExtnd(ZeroExtend), .ALUSrc(ALUSrc), .RegWrite(RegWrite), .MemToReg(MemToReg), .MemRead(MemRead));
  not not_1 (not_1_out, opcode[5]);
  not not_2 (not_2_out, opcode[4]);
  not not_3 (not_3_out, opcode[3]);
  not not_4 (not_4_out, opcode[2]);
  not not_5 (not_5_out, opcode[1]);
  not not_6 (not_6_out, opcode[0]);
  and and_1 (and_1_out, not_1_out, not_2_out, not_3_out, not_4_out, not_5_out, not_6_out);
  RegisterReadDetector registerreaddetector_1 (
    .f2(funct[2]), .f3(funct[3]), .f4(funct[4]), .f5(funct[5]), .f0(funct[0]), .isRType(and_1_out),
    .op1(opcode[1]), .op2(opcode[2]), .op3(opcode[3]), .op4(opcode[4]), .op5(opcode[5]), .op0(opcode[0]),
    .f1(funct[1]), .ReadRt(ReadingRt), .ReadRs(ReadingRs));
  InstructionToALUOperation instructiontoaluoperation_1 (
    .op1(opcode[1]), .op2(opcode[2]), .op3(opcode[3]), .op4(opcode[4]), .op5(opcode[5]), .op0(opcode[0]),
    .ALUop1(instructiontoaluoperation_1_aluop0[1]), .ALUop2(instructiontoaluoperation_1_aluop0[2]),
    .ALUop3(instructiontoaluoperation_1_aluop0[3]), .ALUop0(instructiontoaluoperation_1_aluop0[0]));
  FunctToALUOperation functtoaluoperation_1 (
    .f1(funct[1]), .f2(funct[2]), .f3(funct[3]), .f4(funct[4]), .f5(funct[5]), .f0(funct[0]),
    .ALUop1(functtoaluoperation_1_aluop0[1]), .ALUop2(functtoaluoperation_1_aluop0[2]),
    .ALUop3(functtoaluoperation_1_aluop0[3]), .shiftOperation(functtoaluoperation_1_shiftoperation),
    .ALUop0(functtoaluoperation_1_aluop0[0]), .isJR(functtoaluoperation_1_isjr));
  Multiplexer #(.width(4)) multiplexer_1 (
    .in0(instructiontoaluoperation_1_aluop0), .in1(functtoaluoperation_1_aluop0), .out(ALUop), .sel(and_1_out));
  and and_2 (isJR, and_1_out, functtoaluoperation_1_isjr);
  and and_3 (isShift, and_1_out, functtoaluoperation_1_shiftoperation);

  // Other names for the same wires on the sheet: ReadRs = ReadingRs; ReadRt = ReadingRt

  // Notes on the sheet:
  //   Input and Output
  //   Control Flags Decoding
  //   isRType?
  //   ALU Operation Decoding
endmodule
