// Logisim project aritmetica.circ as structural Verilog: 22 circuits, main circuit meio_somador
module meio_somador (
  input  B1,
  input  A1,
  input  Carry_in,
  input  B1_2,
  input  A1_2,
  input  Carry_in_2,
  input  B1_3,
  input  A1_3,
  output out_9,
  output Soma,
  output out_11,
  output Soma_2,
  output out_13,
  output Soma_3
);

  wire and_1_out, and_3_out, and_4_out, and_5_out, xor_3_out, xor_4_out;

  and and_1 (and_1_out, B1_3, A1_3);
  or or_1 (out_13, and_1_out, and_3_out);
  and and_2 (out_9, A1, B1);
  and and_3 (and_3_out, Carry_in_2, xor_3_out);
  xor xor_1 (Soma_3, Carry_in_2, xor_3_out);
  xor xor_2 (Soma, B1, A1);
  and and_4 (and_4_out, A1_2, B1_2);
  and and_5 (and_5_out, xor_4_out, Carry_in);
  or or_2 (out_11, and_4_out, and_5_out);
  xor xor_3 (xor_3_out, B1_3, A1_3);
  xor xor_4 (xor_4_out, B1_2, A1_2);
  xor xor_5 (Soma_2, Carry_in, xor_4_out);

  // Notes on the sheet:
  //   Carry_out
  //   *Organizando o circuito
  //   Carry_out
  //   Meio Somador (half adder)
  //   Somador Completo (full adder)
  //   Carry_out
  //   A
  //   0
  //   0
  //   1
  //   1
  //   A
  //   0
  //   0
  //   0
  //   0
  //   1
  //   1
  //   1
  //   1
  //   B
  //   0
  //   1
  //   0
  //   1
  //   B
  //   C_in
  //   0
  //   0
  //   0
  //   1
  //   1
  //   0
  //   1
  //   1
  //   0
  //   0
  //   0
  //   1
  //   1
  //   0
  //   1
  //   1
  //   Carry_out
  //   Soma
  //   0
  //   0
  //   0
  //   1
  //   0
  //   1
  //   1
  //   0
  //   Soma
  //   0
  //   1
  //   1
  //   0
  //   1
  //   0
  //   0
  //   1
  //   Carry_out
  //   0
  //   0
  //   0
  //   1
  //   0
  //   1
  //   1
  //   1
endmodule

module somador_4bits (
  input  B4,
  input  B3,
  input  A2,
  input  B1,
  input  in_5,
  input  in_6,
  input  B2,
  input  Carry_in,
  input  in_9
);

  wire and_1_out, and_2_out, and_3_out, and_4_out, and_5_out, and_6_out, and_7_out, and_8_out, or_1_out,
       or_2_out, or_3_out, or_4_out, xor_1_out, xor_2_out, xor_4_out, xor_6_out, xor_8_out;
  wire [3:0] xor_9_out;

  and and_1 (and_1_out, in_5, B4);
  or or_1 (or_1_out, and_1_out, and_2_out);
  xor xor_1 (xor_1_out, or_2_out, or_1_out);
  and and_2 (and_2_out, or_2_out, xor_2_out);
  xor xor_2 (xor_2_out, in_5, B4);
  xor xor_3 (xor_9_out[3], or_2_out, xor_2_out);
  and and_3 (and_3_out, in_6, B3);
  or or_2 (or_2_out, and_3_out, and_4_out);
  and and_4 (and_4_out, or_3_out, xor_4_out);
  xor xor_4 (xor_4_out, in_6, B3);
  xor xor_5 (xor_9_out[2], or_3_out, xor_4_out);
  and and_5 (and_5_out, B2, A2);
  or or_3 (or_3_out, and_5_out, and_6_out);
  and and_6 (and_6_out, or_4_out, xor_6_out);
  // Probe on xor_9_out
  // Probe on xor_9_out
  // Probe on xor_9_out
  // Probe on xor_1_out
  // Probe on or_1_out
  xor xor_6 (xor_6_out, B2, A2);
  xor xor_7 (xor_9_out[1], or_4_out, xor_6_out);
  and and_7 (and_7_out, in_9, B1);
  or or_4 (or_4_out, and_7_out, and_8_out);
  and and_8 (and_8_out, Carry_in, xor_8_out);
  xor xor_8 (xor_8_out, in_9, B1);
  xor xor_9 (xor_9_out[0], Carry_in, xor_8_out);

  // Notes on the sheet:
  //   8
  //   A4
  //   4
  //   A3
  //   2
  //   Decimal sem sinal
  //   Decimal com sinal
  //   Binário
  //   Overflow
  //   Unsigned Overflow
  //   1
  //   A1
endmodule

module somador_8bits (
  input  B8,
  input  B7,
  input  B6,
  input  B5,
  input  B4,
  input  B3,
  input  B2,
  input  B1,
  input  in_9,
  input  in_10,
  input  in_11,
  input  in_12,
  input  in_13,
  input  in_14,
  input  in_15,
  input  Carry_in,
  input  in_17
);

  wire and_1_out, and_2_out, and_3_out, and_4_out, and_5_out, and_6_out, and_7_out, and_8_out, and_9_out,
       and_10_out, and_11_out, and_12_out, and_13_out, and_14_out, and_15_out, and_16_out, or_1_out,
       or_2_out, or_3_out, or_4_out, or_5_out, or_6_out, or_7_out, or_8_out, xor_1_out, xor_3_out, xor_5_out,
       xor_7_out, xor_9_out, xor_11_out, xor_13_out, xor_15_out, xor_17_out;
  wire [7:0] xor_16_out;

  and and_1 (and_1_out, in_9, B8);
  or or_1 (or_1_out, and_1_out, and_2_out);
  xor xor_1 (xor_1_out, or_2_out, or_1_out);
  and and_2 (and_2_out, or_2_out, xor_3_out);
  xor xor_2 (xor_16_out[7], or_2_out, xor_3_out);
  xor xor_3 (xor_3_out, in_9, B8);
  and and_3 (and_3_out, in_10, B7);
  or or_2 (or_2_out, and_3_out, and_4_out);
  and and_4 (and_4_out, or_3_out, xor_5_out);
  xor xor_4 (xor_16_out[6], or_3_out, xor_5_out);
  xor xor_5 (xor_5_out, in_10, B7);
  and and_5 (and_5_out, in_11, B6);
  or or_3 (or_3_out, and_5_out, and_6_out);
  and and_6 (and_6_out, or_4_out, xor_7_out);
  xor xor_6 (xor_16_out[5], or_4_out, xor_7_out);
  xor xor_7 (xor_7_out, in_11, B6);
  and and_7 (and_7_out, in_12, B5);
  or or_4 (or_4_out, and_7_out, and_8_out);
  and and_8 (and_8_out, or_5_out, xor_9_out);
  xor xor_8 (xor_16_out[4], or_5_out, xor_9_out);
  xor xor_9 (xor_9_out, in_12, B5);
  and and_9 (and_9_out, in_13, B4);
  or or_5 (or_5_out, and_9_out, and_10_out);
  and and_10 (and_10_out, or_6_out, xor_11_out);
  xor xor_10 (xor_16_out[3], or_6_out, xor_11_out);
  // Probe on xor_16_out
  // Probe on xor_16_out
  // Probe on xor_16_out
  // Probe on xor_1_out
  // Probe on or_1_out
  xor xor_11 (xor_11_out, in_13, B4);
  and and_11 (and_11_out, in_14, B3);
  or or_6 (or_6_out, and_11_out, and_12_out);
  and and_12 (and_12_out, or_7_out, xor_13_out);
  xor xor_12 (xor_16_out[2], or_7_out, xor_13_out);
  xor xor_13 (xor_13_out, in_14, B3);
  and and_13 (and_13_out, in_15, B2);
  or or_7 (or_7_out, and_13_out, and_14_out);
  and and_14 (and_14_out, or_8_out, xor_15_out);
  xor xor_14 (xor_16_out[1], or_8_out, xor_15_out);
  xor xor_15 (xor_15_out, in_15, B2);
  and and_15 (and_15_out, in_17, B1);
  or or_8 (or_8_out, and_15_out, and_16_out);
  and and_16 (and_16_out, Carry_in, xor_17_out);
  xor xor_16 (xor_16_out[0], Carry_in, xor_17_out);
  xor xor_17 (xor_17_out, in_17, B1);

  // Notes on the sheet:
  //   128
  //   A8
  //   64
  //   A7
  //   32
  //   A6
  //   16
  //   A5
  //   8
  //   A4
  //   Decimal sem sinal
  //   Decimal com sinal
  //   Binário
  //   Overflow
  //   Unsigned Overflow
  //   4
  //   A3
  //   2
  //   A2
  //   1
  //   A1
endmodule

module somador_32bits (
  input  [31:0] in_1,
  input  Carry_in,
  input  [31:0] in_3
);

  wire and_1_out, and_2_out, and_3_out, and_4_out, and_5_out, and_6_out, and_7_out, and_8_out, and_9_out,
       and_10_out, and_11_out, and_12_out, and_13_out, and_14_out, and_15_out, and_16_out, and_17_out,
       and_18_out, and_19_out, and_20_out, and_21_out, and_22_out, and_23_out, and_24_out, and_25_out,
       and_26_out, and_27_out, and_28_out, and_29_out, and_30_out, and_31_out, and_32_out, and_33_out,
       and_34_out, and_35_out, and_36_out, and_37_out, and_38_out, and_39_out, and_40_out, and_41_out,
       and_42_out, and_43_out, and_44_out, and_45_out, and_46_out, and_47_out, and_48_out, and_49_out,
       and_50_out, and_51_out, and_52_out, and_53_out, and_54_out, and_55_out, and_56_out, and_57_out,
       and_58_out, and_59_out, and_60_out, and_61_out, and_62_out, and_63_out, and_64_out, or_1_out,
       or_2_out, or_3_out, or_4_out, or_5_out, or_6_out, or_7_out, or_8_out, or_9_out, or_10_out, or_11_out,
       or_12_out, or_13_out, or_14_out, or_15_out, or_16_out, or_17_out, or_18_out, or_19_out, or_20_out,
       or_21_out, or_22_out, or_23_out, or_24_out, or_25_out, or_26_out, or_27_out, or_28_out, or_29_out,
       or_30_out, or_31_out, or_32_out, xor_1_out, xor_2_out, xor_4_out, xor_6_out, xor_8_out, xor_12_out,
       xor_13_out, xor_14_out, xor_16_out, xor_18_out, xor_20_out, xor_22_out, xor_24_out, xor_26_out,
       xor_28_out, xor_30_out, xor_32_out, xor_34_out, xor_36_out, xor_38_out, xor_40_out, xor_44_out,
       xor_45_out, xor_46_out, xor_48_out, xor_50_out, xor_52_out, xor_54_out, xor_56_out, xor_58_out,
       xor_60_out, xor_62_out, xor_64_out;
  wire [31:0] xor_63_out;

  and and_1 (and_1_out, in_3[15], in_1[15]);
  or or_1 (or_1_out, and_1_out, and_3_out);
  and and_2 (and_2_out, in_3[31], in_1[31]);
  or or_2 (or_2_out, and_2_out, and_4_out);
  xor xor_1 (xor_1_out, or_4_out, or_2_out);
  xor xor_2 (xor_2_out, in_3[15], in_1[15]);
  and and_3 (and_3_out, or_3_out, xor_2_out);
  xor xor_3 (xor_63_out[15], or_3_out, xor_2_out);
  xor xor_4 (xor_4_out, in_3[31], in_1[31]);
  and and_4 (and_4_out, or_4_out, xor_4_out);
  xor xor_5 (xor_63_out[31], or_4_out, xor_4_out);
  and and_5 (and_5_out, in_3[14], in_1[14]);
  and and_6 (and_6_out, or_5_out, xor_6_out);
  or or_3 (or_3_out, and_5_out, and_6_out);
  and and_7 (and_7_out, in_3[30], in_1[30]);
  and and_8 (and_8_out, or_6_out, xor_8_out);
  or or_4 (or_4_out, and_7_out, and_8_out);
  xor xor_6 (xor_6_out, in_3[14], in_1[14]);
  and and_9 (and_9_out, in_3[13], in_1[13]);
  xor xor_7 (xor_63_out[14], or_5_out, xor_6_out);
  xor xor_8 (xor_8_out, in_3[30], in_1[30]);
  and and_10 (and_10_out, in_3[29], in_1[29]);
  xor xor_9 (xor_63_out[30], or_6_out, xor_8_out);
  and and_11 (and_11_out, or_7_out, xor_12_out);
  xor xor_10 (xor_63_out[13], or_7_out, xor_12_out);
  or or_5 (or_5_out, and_9_out, and_11_out);
  and and_12 (and_12_out, or_8_out, xor_13_out);
  xor xor_11 (xor_63_out[29], or_8_out, xor_13_out);
  or or_6 (or_6_out, and_10_out, and_12_out);
  xor xor_12 (xor_12_out, in_3[13], in_1[13]);
  and and_13 (and_13_out, in_3[12], in_1[12]);
  or or_7 (or_7_out, and_13_out, and_15_out);
  xor xor_13 (xor_13_out, in_3[29], in_1[29]);
  and and_14 (and_14_out, in_3[28], in_1[28]);
  or or_8 (or_8_out, and_14_out, and_16_out);
  xor xor_14 (xor_14_out, in_3[12], in_1[12]);
  and and_15 (and_15_out, or_9_out, xor_14_out);
  xor xor_15 (xor_63_out[12], or_9_out, xor_14_out);
  xor xor_16 (xor_16_out, in_3[28], in_1[28]);
  and and_16 (and_16_out, or_10_out, xor_16_out);
  xor xor_17 (xor_63_out[28], or_10_out, xor_16_out);
  and and_17 (and_17_out, in_3[11], in_1[11]);
  and and_18 (and_18_out, or_11_out, xor_18_out);
  or or_9 (or_9_out, and_17_out, and_18_out);
  and and_19 (and_19_out, in_3[27], in_1[27]);
  and and_20 (and_20_out, or_12_out, xor_20_out);
  or or_10 (or_10_out, and_19_out, and_20_out);
  xor xor_18 (xor_18_out, in_3[11], in_1[11]);
  and and_21 (and_21_out, in_3[10], in_1[10]);
  xor xor_19 (xor_63_out[11], or_11_out, xor_18_out);
  xor xor_20 (xor_20_out, in_3[27], in_1[27]);
  and and_22 (and_22_out, in_3[26], in_1[26]);
  xor xor_21 (xor_63_out[27], or_12_out, xor_20_out);
  xor xor_22 (xor_22_out, in_3[10], in_1[10]);
  and and_23 (and_23_out, or_13_out, xor_22_out);
  xor xor_23 (xor_63_out[10], or_13_out, xor_22_out);
  or or_11 (or_11_out, and_21_out, and_23_out);
  xor xor_24 (xor_24_out, in_3[26], in_1[26]);
  and and_24 (and_24_out, or_14_out, xor_24_out);
  xor xor_25 (xor_63_out[26], or_14_out, xor_24_out);
  or or_12 (or_12_out, and_22_out, and_24_out);
  and and_25 (and_25_out, in_3[9], in_1[9]);
  and and_26 (and_26_out, or_15_out, xor_26_out);
  or or_13 (or_13_out, and_25_out, and_26_out);
  and and_27 (and_27_out, in_3[25], in_1[25]);
  and and_28 (and_28_out, or_16_out, xor_28_out);
  or or_14 (or_14_out, and_27_out, and_28_out);
  xor xor_26 (xor_26_out, in_3[9], in_1[9]);
  xor xor_27 (xor_63_out[9], or_15_out, xor_26_out);
  xor xor_28 (xor_28_out, in_3[25], in_1[25]);
  xor xor_29 (xor_63_out[25], or_16_out, xor_28_out);
  // Probe on or_2_out
  and and_29 (and_29_out, in_3[8], in_1[8]);
  and and_30 (and_30_out, or_17_out, xor_30_out);
  or or_15 (or_15_out, and_29_out, and_30_out);
  and and_31 (and_31_out, in_3[24], in_1[24]);
  and and_32 (and_32_out, or_18_out, xor_32_out);
  or or_16 (or_16_out, and_31_out, and_32_out);
  xor xor_30 (xor_30_out, in_3[8], in_1[8]);
  and and_33 (and_33_out, in_3[7], in_1[7]);
  xor xor_31 (xor_63_out[8], or_17_out, xor_30_out);
  or or_17 (or_17_out, and_33_out, and_35_out);
  xor xor_32 (xor_32_out, in_3[24], in_1[24]);
  and and_34 (and_34_out, in_3[23], in_1[23]);
  xor xor_33 (xor_63_out[24], or_18_out, xor_32_out);
  or or_18 (or_18_out, and_34_out, and_36_out);
  // Probe on in_1
  // Probe on in_3
  // Probe on xor_63_out
  xor xor_34 (xor_34_out, in_3[7], in_1[7]);
  and and_35 (and_35_out, or_19_out, xor_34_out);
  xor xor_35 (xor_63_out[7], or_19_out, xor_34_out);
  xor xor_36 (xor_36_out, in_3[23], in_1[23]);
  and and_36 (and_36_out, or_20_out, xor_36_out);
  xor xor_37 (xor_63_out[23], or_20_out, xor_36_out);
  // Probe on xor_1_out
  and and_37 (and_37_out, in_3[6], in_1[6]);
  and and_38 (and_38_out, or_21_out, xor_38_out);
  or or_19 (or_19_out, and_37_out, and_38_out);
  and and_39 (and_39_out, in_3[22], in_1[22]);
  and and_40 (and_40_out, or_22_out, xor_40_out);
  or or_20 (or_20_out, and_39_out, and_40_out);
  xor xor_38 (xor_38_out, in_3[6], in_1[6]);
  and and_41 (and_41_out, in_3[5], in_1[5]);
  xor xor_39 (xor_63_out[6], or_21_out, xor_38_out);
  xor xor_40 (xor_40_out, in_3[22], in_1[22]);
  and and_42 (and_42_out, in_3[21], in_1[21]);
  xor xor_41 (xor_63_out[22], or_22_out, xor_40_out);
  // Probe on in_1
  // Probe on in_3
  // Probe on xor_63_out
  and and_43 (and_43_out, or_23_out, xor_44_out);
  xor xor_42 (xor_63_out[5], or_23_out, xor_44_out);
  or or_21 (or_21_out, and_41_out, and_43_out);
  and and_44 (and_44_out, or_24_out, xor_45_out);
  xor xor_43 (xor_63_out[21], or_24_out, xor_45_out);
  or or_22 (or_22_out, and_42_out, and_44_out);
  xor xor_44 (xor_44_out, in_3[5], in_1[5]);
  and and_45 (and_45_out, in_3[4], in_1[4]);
  or or_23 (or_23_out, and_45_out, and_47_out);
  xor xor_45 (xor_45_out, in_3[21], in_1[21]);
  and and_46 (and_46_out, in_3[20], in_1[20]);
  or or_24 (or_24_out, and_46_out, and_48_out);
  xor xor_46 (xor_46_out, in_3[4], in_1[4]);
  and and_47 (and_47_out, or_25_out, xor_46_out);
  xor xor_47 (xor_63_out[4], or_25_out, xor_46_out);
  xor xor_48 (xor_48_out, in_3[20], in_1[20]);
  and and_48 (and_48_out, or_26_out, xor_48_out);
  xor xor_49 (xor_63_out[20], or_26_out, xor_48_out);
  and and_49 (and_49_out, in_3[3], in_1[3]);
  and and_50 (and_50_out, or_27_out, xor_50_out);
  or or_25 (or_25_out, and_49_out, and_50_out);
  and and_51 (and_51_out, in_3[19], in_1[19]);
  and and_52 (and_52_out, or_28_out, xor_52_out);
  or or_26 (or_26_out, and_51_out, and_52_out);
  xor xor_50 (xor_50_out, in_3[3], in_1[3]);
  and and_53 (and_53_out, in_3[2], in_1[2]);
  xor xor_51 (xor_63_out[3], or_27_out, xor_50_out);
  xor xor_52 (xor_52_out, in_3[19], in_1[19]);
  and and_54 (and_54_out, in_3[18], in_1[18]);
  xor xor_53 (xor_63_out[19], or_28_out, xor_52_out);
  xor xor_54 (xor_54_out, in_3[2], in_1[2]);
  and and_55 (and_55_out, or_29_out, xor_54_out);
  xor xor_55 (xor_63_out[2], or_29_out, xor_54_out);
  or or_27 (or_27_out, and_53_out, and_55_out);
  xor xor_56 (xor_56_out, in_3[18], in_1[18]);
  and and_56 (and_56_out, or_30_out, xor_56_out);
  xor xor_57 (xor_63_out[18], or_30_out, xor_56_out);
  or or_28 (or_28_out, and_54_out, and_56_out);
  and and_57 (and_57_out, in_3[1], in_1[1]);
  and and_58 (and_58_out, or_31_out, xor_58_out);
  or or_29 (or_29_out, and_57_out, and_58_out);
  and and_59 (and_59_out, in_3[17], in_1[17]);
  and and_60 (and_60_out, or_32_out, xor_60_out);
  or or_30 (or_30_out, and_59_out, and_60_out);
  xor xor_58 (xor_58_out, in_3[1], in_1[1]);
  xor xor_59 (xor_63_out[1], or_31_out, xor_58_out);
  xor xor_60 (xor_60_out, in_3[17], in_1[17]);
  xor xor_61 (xor_63_out[17], or_32_out, xor_60_out);
  and and_61 (and_61_out, in_3[0], in_1[0]);
  and and_62 (and_62_out, Carry_in, xor_62_out);
  or or_31 (or_31_out, and_61_out, and_62_out);
  and and_63 (and_63_out, in_3[16], in_1[16]);
  and and_64 (and_64_out, or_1_out, xor_64_out);
  or or_32 (or_32_out, and_63_out, and_64_out);
  xor xor_62 (xor_62_out, in_3[0], in_1[0]);
  xor xor_63 (xor_63_out[0], Carry_in, xor_62_out);
  xor xor_64 (xor_64_out, in_3[16], in_1[16]);
  xor xor_65 (xor_63_out[16], or_1_out, xor_64_out);

  // Notes on the sheet:
  //   Unsigned Overflow
  //   Soma sem sinal
  //   +
  //   =
  //   Overflow
  //   Soma com sinal
  //   +
  //   =
  //   A
  //   B
endmodule

module somador_subtrator_4bits (
  input  B4,
  input  B3,
  input  B2,
  input  B1,
  input  in_5,
  input  in_6,
  input  in_7,
  input  in_8,
  input  Controle
);

  wire and_1_out, and_2_out, and_3_out, and_4_out, and_5_out, and_6_out, and_7_out, and_8_out, or_1_out,
       or_2_out, or_3_out, or_4_out, xor_1_out, xor_2_out, xor_4_out, xor_5_out, xor_7_out, xor_8_out,
       xor_10_out, xor_11_out, xor_13_out;
  wire [3:0] xor_12_out;

  and and_1 (and_1_out, xor_2_out, B4);
  or or_1 (or_1_out, and_1_out, and_2_out);
  xor xor_1 (xor_1_out, or_2_out, or_1_out);
  xor xor_2 (xor_2_out, Controle, in_5);
  and and_2 (and_2_out, or_2_out, xor_4_out);
  xor xor_3 (xor_12_out[3], or_2_out, xor_4_out);
  xor xor_4 (xor_4_out, xor_2_out, B4);
  and and_3 (and_3_out, xor_5_out, B3);
  or or_2 (or_2_out, and_3_out, and_4_out);
  xor xor_5 (xor_5_out, Controle, in_6);
  and and_4 (and_4_out, or_3_out, xor_7_out);
  xor xor_6 (xor_12_out[2], or_3_out, xor_7_out);
  xor xor_7 (xor_7_out, xor_5_out, B3);
  and and_5 (and_5_out, xor_8_out, B2);
  or or_3 (or_3_out, and_5_out, and_6_out);
  xor xor_8 (xor_8_out, Controle, in_7);
  and and_6 (and_6_out, or_4_out, xor_10_out);
  xor xor_9 (xor_12_out[1], or_4_out, xor_10_out);
  // Probe on xor_12_out
  // Probe on xor_12_out
  // Probe on xor_12_out
  // Probe on xor_1_out
  // Probe on or_1_out
  xor xor_10 (xor_10_out, xor_8_out, B2);
  and and_7 (and_7_out, xor_11_out, B1);
  or or_4 (or_4_out, and_7_out, and_8_out);
  xor xor_11 (xor_11_out, Controle, in_8);
  and and_8 (and_8_out, Controle, xor_13_out);
  xor xor_12 (xor_12_out[0], Controle, xor_13_out);
  xor xor_13 (xor_13_out, xor_11_out, B1);

  // Notes on the sheet:
  //   8
  //   A4
  //   4
  //   A3
  //   2
  //   A2
  //   Binário
  //   Overflow
  //   1
  //   Decimal sem sinal
  //   Decimal com sinal
  //   Unsigned Overflow
  //   A1
endmodule

module somador_subtrator_8bits (
  input  B8,
  input  B7,
  input  B6,
  input  B5,
  input  B4,
  input  B3,
  input  B2,
  input  B1,
  input  in_9,
  input  in_10,
  input  in_11,
  input  in_12,
  input  in_13,
  input  in_14,
  input  in_15,
  input  in_16,
  input  Controle
);

  wire and_1_out, and_2_out, and_3_out, and_4_out, and_5_out, and_6_out, and_7_out, and_8_out, and_9_out,
       and_10_out, and_11_out, and_12_out, and_13_out, and_14_out, and_15_out, and_16_out, or_1_out,
       or_2_out, or_3_out, or_4_out, or_5_out, or_6_out, or_7_out, or_8_out, xor_1_out, xor_2_out, xor_3_out,
       xor_5_out, xor_6_out, xor_8_out, xor_9_out, xor_11_out, xor_12_out, xor_14_out, xor_15_out,
       xor_17_out, xor_18_out, xor_20_out, xor_21_out, xor_23_out, xor_24_out;
  wire [7:0] xor_25_out;

  and and_1 (and_1_out, or_2_out, xor_3_out);
  and and_2 (and_2_out, xor_2_out, B8);
  or or_1 (or_1_out, and_2_out, and_1_out);
  xor xor_1 (xor_1_out, or_2_out, or_1_out);
  xor xor_2 (xor_2_out, Controle, in_9);
  xor xor_3 (xor_3_out, xor_2_out, B8);
  xor xor_4 (xor_25_out[7], or_2_out, xor_3_out);
  and and_3 (and_3_out, xor_5_out, B7);
  and and_4 (and_4_out, or_3_out, xor_6_out);
  or or_2 (or_2_out, and_3_out, and_4_out);
  xor xor_5 (xor_5_out, Controle, in_10);
  xor xor_6 (xor_6_out, xor_5_out, B7);
  xor xor_7 (xor_25_out[6], or_3_out, xor_6_out);
  and and_5 (and_5_out, xor_8_out, B6);
  and and_6 (and_6_out, or_4_out, xor_9_out);
  or or_3 (or_3_out, and_5_out, and_6_out);
  xor xor_8 (xor_8_out, Controle, in_11);
  xor xor_9 (xor_9_out, xor_8_out, B6);
  xor xor_10 (xor_25_out[5], or_4_out, xor_9_out);
  and and_7 (and_7_out, xor_11_out, B5);
  and and_8 (and_8_out, or_5_out, xor_12_out);
  or or_4 (or_4_out, and_7_out, and_8_out);
  xor xor_11 (xor_11_out, Controle, in_12);
  xor xor_12 (xor_12_out, xor_11_out, B5);
  xor xor_13 (xor_25_out[4], or_5_out, xor_12_out);
  and and_9 (and_9_out, xor_14_out, B4);
  and and_10 (and_10_out, or_6_out, xor_15_out);
  or or_5 (or_5_out, and_9_out, and_10_out);
  xor xor_14 (xor_14_out, Controle, in_13);
  xor xor_15 (xor_15_out, xor_14_out, B4);
  xor xor_16 (xor_25_out[3], or_6_out, xor_15_out);
  // Probe on xor_25_out
  // Probe on xor_25_out
  // Probe on xor_25_out
  // Probe on xor_1_out
  // Probe on or_1_out
  and and_11 (and_11_out, xor_17_out, B3);
  and and_12 (and_12_out, or_7_out, xor_18_out);
  or or_6 (or_6_out, and_11_out, and_12_out);
  xor xor_17 (xor_17_out, Controle, in_14);
  xor xor_18 (xor_18_out, xor_17_out, B3);
  xor xor_19 (xor_25_out[2], or_7_out, xor_18_out);
  and and_13 (and_13_out, xor_20_out, B2);
  and and_14 (and_14_out, or_8_out, xor_21_out);
  or or_7 (or_7_out, and_13_out, and_14_out);
  xor xor_20 (xor_20_out, Controle, in_15);
  xor xor_21 (xor_21_out, xor_20_out, B2);
  xor xor_22 (xor_25_out[1], or_8_out, xor_21_out);
  and and_15 (and_15_out, xor_23_out, B1);
  and and_16 (and_16_out, Controle, xor_24_out);
  or or_8 (or_8_out, and_15_out, and_16_out);
  xor xor_23 (xor_23_out, Controle, in_16);
  xor xor_24 (xor_24_out, xor_23_out, B1);
  xor xor_25 (xor_25_out[0], Controle, xor_24_out);

  // Notes on the sheet:
  //   128
  //   A8
  //   64
  //   A7
  //   32
  //   A6
  //   16
  //   A5
  //   8
  //   A4
  //   4
  //   Binário
  //   Overflow
  //   Decimal sem sinal
  //   Decimal com sinal
  //   Unsigned Overflow
  //   A3
  //   2
  //   A2
  //   1
  //   A1
endmodule

module somador_4bits_lookahead (
  input  B4,
  input  B3,
  input  B2,
  input  B1,
  input  Carry_in,
  input  in_6,
  input  in_7,
  input  in_8,
  input  in_9
);

  wire and_1_out, and_2_out, and_3_out, and_4_out, and_5_out, and_6_out, and_7_out, and_8_out, and_9_out,
       and_10_out, and_11_out, and_12_out, and_13_out, and_14_out, or_1_out, or_2_out, or_3_out, or_4_out,
       xor_1_out, xor_2_out, xor_4_out, xor_6_out, xor_8_out;
  wire [3:0] xor_9_out;

  and and_1 (and_1_out, xor_2_out, and_9_out);
  and and_2 (and_2_out, xor_2_out, xor_4_out, and_12_out);
  or or_1 (or_1_out, and_5_out, and_1_out, and_2_out, and_3_out, and_4_out);
  and and_3 (and_3_out, xor_2_out, xor_4_out, xor_6_out, and_14_out);
  and and_4 (and_4_out, xor_2_out, xor_4_out, xor_6_out, xor_8_out, Carry_in);
  xor xor_1 (xor_1_out, or_1_out, or_2_out);
  and and_5 (and_5_out, in_6, B4);
  xor xor_2 (xor_2_out, in_6, B4);
  and and_6 (and_6_out, xor_4_out, and_12_out);
  or or_2 (or_2_out, and_9_out, and_6_out, and_7_out, and_8_out);
  xor xor_3 (xor_9_out[3], xor_2_out, or_2_out);
  and and_7 (and_7_out, xor_4_out, xor_6_out, and_14_out);
  and and_8 (and_8_out, xor_4_out, xor_6_out, xor_8_out, Carry_in);
  and and_9 (and_9_out, in_7, B3);
  xor xor_4 (xor_4_out, in_7, B3);
  or or_3 (or_3_out, and_12_out, and_10_out, and_11_out);
  xor xor_5 (xor_9_out[2], xor_4_out, or_3_out);
  and and_10 (and_10_out, xor_6_out, and_14_out);
  and and_11 (and_11_out, xor_6_out, xor_8_out, Carry_in);
  and and_12 (and_12_out, in_8, B2);
  xor xor_6 (xor_6_out, in_8, B2);
  // Probe on xor_9_out
  // Probe on xor_9_out
  // Probe on xor_9_out
  // Probe on xor_1_out
  // Probe on or_1_out
  and and_13 (and_13_out, xor_8_out, Carry_in);
  or or_4 (or_4_out, and_14_out, and_13_out);
  xor xor_7 (xor_9_out[1], xor_6_out, or_4_out);
  and and_14 (and_14_out, in_9, B1);
  xor xor_8 (xor_8_out, in_9, B1);
  xor xor_9 (xor_9_out[0], xor_8_out, Carry_in);

  // Notes on the sheet:
  //   8
  //   A4
  //   4
  //   A3
  //   2
  //   A2
  //   1
  //   Binário
  //   Overflow
  //   A1
  //   Decimal sem sinal
  //   Decimal com sinal
  //   Unsigned Overflow
endmodule

module somador_8bits_lookahead (
  input  B8,
  input  B7,
  input  B6,
  input  B5,
  input  B4,
  input  B3,
  input  B2,
  input  B1,
  input  in_9,
  input  in_10,
  input  in_11,
  input  in_12,
  input  in_13,
  input  in_14,
  input  in_15,
  input  in_16,
  input  in_17
);

  wire and_1_out, and_2_out, and_3_out, and_4_out, and_5_out, and_6_out, and_7_out, and_8_out, and_9_out,
       and_10_out, and_11_out, and_12_out, and_13_out, and_14_out, and_15_out, and_16_out, and_17_out,
       and_18_out, and_19_out, and_20_out, and_21_out, and_22_out, and_23_out, and_24_out, and_25_out,
       and_26_out, and_27_out, and_28_out, and_29_out, and_30_out, and_31_out, and_32_out, and_33_out,
       and_34_out, and_35_out, and_36_out, and_37_out, and_38_out, and_39_out, and_40_out, and_41_out,
       and_42_out, and_43_out, and_44_out, or_1_out, or_2_out, or_3_out, or_4_out, or_5_out, or_6_out,
       or_7_out, or_8_out, xor_1_out, xor_2_out, xor_4_out, xor_6_out, xor_8_out, xor_10_out, xor_12_out,
       xor_14_out, xor_16_out;
  wire [7:0] xor_17_out;

  and and_1 (and_1_out, xor_2_out, xor_4_out, and_24_out);
  and and_2 (and_2_out, xor_2_out, and_17_out);
  or or_1 (or_1_out, and_9_out, and_2_out, and_1_out, and_3_out, and_4_out, and_5_out, and_6_out, and_7_out, and_8_out);
  and and_3 (and_3_out, xor_2_out, xor_4_out, xor_6_out, and_30_out);
  and and_4 (and_4_out, xor_2_out, xor_4_out, xor_6_out, xor_8_out, and_35_out);
  and and_5 (and_5_out, xor_2_out, xor_4_out, xor_6_out, xor_8_out, xor_10_out, and_39_out);
  and and_6 (and_6_out, xor_2_out, xor_4_out, xor_6_out, xor_8_out, xor_10_out, xor_12_out, and_42_out);
  and and_7 (and_7_out, xor_2_out, xor_4_out, xor_6_out, xor_8_out, xor_10_out, xor_12_out, xor_14_out, and_44_out);
  xor xor_1 (xor_1_out, or_1_out, or_2_out);
  and and_8 (and_8_out, xor_2_out, xor_4_out, xor_6_out, xor_8_out, xor_10_out, xor_12_out, xor_14_out, xor_16_out, in_9);
  and and_9 (and_9_out, in_10, B8);
  xor xor_2 (xor_2_out, in_10, B8);
  and and_10 (and_10_out, xor_4_out, and_24_out);
  xor xor_3 (xor_17_out[7], xor_2_out, or_2_out);
  and and_11 (and_11_out, xor_4_out, xor_6_out, and_30_out);
  and and_12 (and_12_out, xor_4_out, xor_6_out, xor_8_out, and_35_out);
  or or_2 (or_2_out, and_17_out, and_10_out, and_11_out, and_12_out, and_13_out, and_14_out, and_15_out, and_16_out);
  and and_13 (and_13_out, xor_4_out, xor_6_out, xor_8_out, xor_10_out, and_39_out);
  and and_14 (and_14_out, xor_4_out, xor_6_out, xor_8_out, xor_10_out, xor_12_out, and_42_out);
  and and_15 (and_15_out, xor_4_out, xor_6_out, xor_8_out, xor_10_out, xor_12_out, xor_14_out, and_44_out);
  and and_16 (and_16_out, xor_4_out, xor_6_out, xor_8_out, xor_10_out, xor_12_out, xor_14_out, xor_16_out, in_9);
  and and_17 (and_17_out, in_11, B7);
  xor xor_4 (xor_4_out, in_11, B7);
  xor xor_5 (xor_17_out[6], xor_4_out, or_3_out);
  and and_18 (and_18_out, xor_6_out, and_30_out);
  and and_19 (and_19_out, xor_6_out, xor_8_out, and_35_out);
  or or_3 (or_3_out, and_24_out, and_18_out, and_19_out, and_20_out, and_21_out, and_22_out, and_23_out);
  and and_20 (and_20_out, xor_6_out, xor_8_out, xor_10_out, and_39_out);
  and and_21 (and_21_out, xor_6_out, xor_8_out, xor_10_out, xor_12_out, and_42_out);
  and and_22 (and_22_out, xor_6_out, xor_8_out, xor_10_out, xor_12_out, xor_14_out, and_44_out);
  and and_23 (and_23_out, xor_6_out, xor_8_out, xor_10_out, xor_12_out, xor_14_out, xor_16_out, in_9);
  and and_24 (and_24_out, in_12, B6);
  xor xor_6 (xor_6_out, in_12, B6);
  and and_25 (and_25_out, xor_8_out, and_35_out);
  or or_4 (or_4_out, and_30_out, and_25_out, and_26_out, and_27_out, and_28_out, and_29_out);
  xor xor_7 (xor_17_out[5], xor_6_out, or_4_out);
  and and_26 (and_26_out, xor_8_out, xor_10_out, and_39_out);
  and and_27 (and_27_out, xor_8_out, xor_10_out, xor_12_out, and_42_out);
  and and_28 (and_28_out, xor_8_out, xor_10_out, xor_12_out, xor_14_out, and_44_out);
  and and_29 (and_29_out, xor_8_out, xor_10_out, xor_12_out, xor_14_out, xor_16_out, in_9);
  and and_30 (and_30_out, in_13, B5);
  xor xor_8 (xor_8_out, in_13, B5);
  xor xor_9 (xor_17_out[4], xor_8_out, or_5_out);
  and and_31 (and_31_out, xor_10_out, and_39_out);
  and and_32 (and_32_out, xor_10_out, xor_12_out, and_42_out);
  or or_5 (or_5_out, and_35_out, and_31_out, and_32_out, and_33_out, and_34_out);
  and and_33 (and_33_out, xor_10_out, xor_12_out, xor_14_out, and_44_out);
  and and_34 (and_34_out, xor_10_out, xor_12_out, xor_14_out, xor_16_out, in_9);
  and and_35 (and_35_out, in_14, B4);
  // Probe on xor_17_out
  // Probe on xor_17_out
  // Probe on xor_17_out
  // Probe on xor_1_out
  // Probe on or_1_out
  xor xor_10 (xor_10_out, in_14, B4);
  and and_36 (and_36_out, xor_12_out, and_42_out);
  or or_6 (or_6_out, and_39_out, and_36_out, and_37_out, and_38_out);
  xor xor_11 (xor_17_out[3], xor_10_out, or_6_out);
  and and_37 (and_37_out, xor_12_out, xor_14_out, and_44_out);
  and and_38 (and_38_out, xor_12_out, xor_14_out, xor_16_out, in_9);
  and and_39 (and_39_out, in_15, B3);
  xor xor_12 (xor_12_out, in_15, B3);
  and and_40 (and_40_out, xor_14_out, and_44_out);
  or or_7 (or_7_out, and_42_out, and_40_out, and_41_out);
  xor xor_13 (xor_17_out[2], xor_12_out, or_7_out);
  and and_41 (and_41_out, xor_14_out, xor_16_out, in_9);
  and and_42 (and_42_out, in_16, B2);
  xor xor_14 (xor_14_out, in_16, B2);
  xor xor_15 (xor_17_out[1], xor_14_out, or_8_out);
  and and_43 (and_43_out, xor_16_out, in_9);
  or or_8 (or_8_out, and_44_out, and_43_out);
  and and_44 (and_44_out, in_17, B1);
  xor xor_16 (xor_16_out, in_17, B1);
  xor xor_17 (xor_17_out[0], xor_16_out, in_9);

  // Notes on the sheet:
  //   128
  //   A8
  //   64
  //   A7
  //   32
  //   A6
  //   16
  //   A5
  //   8
  //   A4
  //   Binário
  //   Overflow
  //   4
  //   Decimal sem sinal
  //   Decimal com sinal
  //   Unsigned Overflow
  //   A3
  //   2
  //   A2
  //   1
  //   A1
endmodule

module somador_subtrator_4bits_lookahead (
  input  B4,
  input  B3,
  input  B2,
  input  A1,
  input  in_5,
  input  in_6,
  input  in_7,
  input  B1,
  input  Controle
);

  wire and_1_out, and_2_out, and_3_out, and_4_out, and_5_out, and_6_out, and_7_out, and_8_out, and_9_out,
       and_10_out, and_11_out, and_12_out, and_13_out, and_14_out, or_1_out, or_2_out, or_3_out, or_4_out,
       xor_1_out, xor_2_out, xor_3_out, xor_5_out, xor_6_out, xor_8_out, xor_9_out, xor_11_out, xor_12_out;
  wire [3:0] xor_13_out;

  and and_1 (and_1_out, xor_3_out, and_9_out);
  or or_1 (or_1_out, and_5_out, and_1_out, and_2_out, and_3_out, and_4_out);
  and and_2 (and_2_out, xor_3_out, xor_6_out, and_12_out);
  and and_3 (and_3_out, xor_3_out, xor_6_out, xor_9_out, and_14_out);
  and and_4 (and_4_out, xor_3_out, xor_6_out, xor_9_out, xor_12_out, Controle);
  xor xor_1 (xor_1_out, or_1_out, or_2_out);
  xor xor_2 (xor_2_out, Controle, in_5);
  and and_5 (and_5_out, xor_2_out, B4);
  xor xor_3 (xor_3_out, xor_2_out, B4);
  and and_6 (and_6_out, xor_6_out, and_12_out);
  and and_7 (and_7_out, xor_6_out, xor_9_out, and_14_out);
  or or_2 (or_2_out, and_9_out, and_6_out, and_7_out, and_8_out);
  xor xor_4 (xor_13_out[3], xor_3_out, or_2_out);
  and and_8 (and_8_out, xor_6_out, xor_9_out, xor_12_out, Controle);
  xor xor_5 (xor_5_out, Controle, in_6);
  and and_9 (and_9_out, xor_5_out, B3);
  xor xor_6 (xor_6_out, xor_5_out, B3);
  and and_10 (and_10_out, xor_9_out, and_14_out);
  and and_11 (and_11_out, xor_9_out, xor_12_out, Controle);
  or or_3 (or_3_out, and_12_out, and_10_out, and_11_out);
  xor xor_7 (xor_13_out[2], xor_6_out, or_3_out);
  and and_12 (and_12_out, xor_8_out, B2);
  xor xor_8 (xor_8_out, Controle, in_7);
  xor xor_9 (xor_9_out, xor_8_out, B2);
  and and_13 (and_13_out, xor_12_out, Controle);
  or or_4 (or_4_out, and_14_out, and_13_out);
  xor xor_10 (xor_13_out[1], xor_9_out, or_4_out);
  // Probe on xor_13_out
  // Probe on xor_13_out
  // Probe on xor_13_out
  // Probe on xor_1_out
  // Probe on or_1_out
  and and_14 (and_14_out, xor_11_out, A1);
  xor xor_11 (xor_11_out, Controle, B1);
  xor xor_12 (xor_12_out, xor_11_out, A1);
  xor xor_13 (xor_13_out[0], xor_12_out, Controle);

  // Notes on the sheet:
  //   8
  //   A4
  //   4
  //   A3
  //   2
  //   A2
  //   1
  //   Binário
  //   Overflow
  //   Decimal sem sinal
  //   Decimal com sinal
  //   Unsigned Overflow
endmodule

module somador_subtrator_8bits_lookahead (
  input  B8,
  input  B7,
  input  B6,
  input  B5,
  input  B4,
  input  B3,
  input  B2,
  input  B1,
  input  in_9,
  input  in_10,
  input  in_11,
  input  in_12,
  input  in_13,
  input  in_14,
  input  in_15,
  input  in_16,
  input  Controle
);

  wire and_1_out, and_2_out, and_3_out, and_4_out, and_5_out, and_6_out, and_7_out, and_8_out, and_9_out,
       and_10_out, and_11_out, and_12_out, and_13_out, and_14_out, and_15_out, and_16_out, and_17_out,
       and_18_out, and_19_out, and_20_out, and_21_out, and_22_out, and_23_out, and_24_out, and_25_out,
       and_26_out, and_27_out, and_28_out, and_29_out, and_30_out, and_31_out, and_32_out, and_33_out,
       and_34_out, and_35_out, and_36_out, and_37_out, and_38_out, and_39_out, and_40_out, and_41_out,
       and_42_out, and_43_out, and_44_out, or_1_out, or_2_out, or_3_out, or_4_out, or_5_out, or_6_out,
       or_7_out, or_8_out, xor_1_out, xor_2_out, xor_3_out, xor_5_out, xor_6_out, xor_8_out, xor_9_out,
       xor_11_out, xor_12_out, xor_14_out, xor_15_out, xor_17_out, xor_18_out, xor_20_out, xor_21_out,
       xor_23_out, xor_24_out;
  wire [7:0] xor_25_out;

  and and_1 (and_1_out, xor_3_out, and_17_out);
  and and_2 (and_2_out, xor_3_out, xor_6_out, and_24_out);
  or or_1 (or_1_out, and_9_out, and_1_out, and_2_out, and_3_out, and_4_out, and_5_out, and_6_out, and_7_out, and_8_out);
  and and_3 (and_3_out, xor_3_out, xor_6_out, xor_9_out, and_30_out);
  and and_4 (and_4_out, xor_3_out, xor_6_out, xor_9_out, xor_12_out, and_35_out);
  and and_5 (and_5_out, xor_3_out, xor_6_out, xor_9_out, xor_12_out, xor_15_out, and_39_out);
  and and_6 (and_6_out, xor_3_out, xor_6_out, xor_9_out, xor_12_out, xor_15_out, xor_18_out, and_42_out);
  and and_7 (and_7_out, xor_3_out, xor_6_out, xor_9_out, xor_12_out, xor_15_out, xor_18_out, xor_21_out, and_44_out);
  xor xor_1 (xor_1_out, or_1_out, or_2_out);
  and and_8 (and_8_out, xor_3_out, xor_6_out, xor_9_out, xor_12_out, xor_15_out, xor_18_out, xor_21_out, xor_24_out, Controle);
  xor xor_2 (xor_2_out, Controle, in_9);
  and and_9 (and_9_out, xor_2_out, B8);
  xor xor_3 (xor_3_out, xor_2_out, B8);
  xor xor_4 (xor_25_out[7], xor_3_out, or_2_out);
  and and_10 (and_10_out, xor_6_out, and_24_out);
  and and_11 (and_11_out, xor_6_out, xor_9_out, and_30_out);
  or or_2 (or_2_out, and_17_out, and_10_out, and_11_out, and_12_out, and_13_out, and_14_out, and_15_out, and_16_out);
  and and_12 (and_12_out, xor_6_out, xor_9_out, xor_12_out, and_35_out);
  and and_13 (and_13_out, xor_6_out, xor_9_out, xor_12_out, xor_15_out, and_39_out);
  and and_14 (and_14_out, xor_6_out, xor_9_out, xor_12_out, xor_15_out, xor_18_out, and_42_out);
  and and_15 (and_15_out, xor_6_out, xor_9_out, xor_12_out, xor_15_out, xor_18_out, xor_21_out, and_44_out);
  and and_16 (and_16_out, xor_6_out, xor_9_out, xor_12_out, xor_15_out, xor_18_out, xor_21_out, xor_24_out, Controle);
  xor xor_5 (xor_5_out, Controle, in_10);
  and and_17 (and_17_out, xor_5_out, B7);
  xor xor_6 (xor_6_out, xor_5_out, B7);
  and and_18 (and_18_out, xor_9_out, and_30_out);
  or or_3 (or_3_out, and_24_out, and_18_out, and_19_out, and_20_out, and_21_out, and_22_out, and_23_out);
  xor xor_7 (xor_25_out[6], xor_6_out, or_3_out);
  and and_19 (and_19_out, xor_9_out, xor_12_out, and_35_out);
  and and_20 (and_20_out, xor_9_out, xor_12_out, xor_15_out, and_39_out);
  and and_21 (and_21_out, xor_9_out, xor_12_out, xor_15_out, xor_18_out, and_42_out);
  and and_22 (and_22_out, xor_9_out, xor_12_out, xor_15_out, xor_18_out, xor_21_out, and_44_out);
  and and_23 (and_23_out, xor_9_out, xor_12_out, xor_15_out, xor_18_out, xor_21_out, xor_24_out, Controle);
  and and_24 (and_24_out, xor_8_out, B6);
  xor xor_8 (xor_8_out, Controle, in_11);
  xor xor_9 (xor_9_out, xor_8_out, B6);
  xor xor_10 (xor_25_out[5], xor_9_out, or_4_out);
  and and_25 (and_25_out, xor_12_out, and_35_out);
  and and_26 (and_26_out, xor_12_out, xor_15_out, and_39_out);
  and and_27 (and_27_out, xor_12_out, xor_15_out, xor_18_out, and_42_out);
  or or_4 (or_4_out, and_30_out, and_25_out, and_26_out, and_27_out, and_28_out, and_29_out);
  and and_28 (and_28_out, xor_12_out, xor_15_out, xor_18_out, xor_21_out, and_44_out);
  and and_29 (and_29_out, xor_12_out, xor_15_out, xor_18_out, xor_21_out, xor_24_out, Controle);
  xor xor_11 (xor_11_out, Controle, in_12);
  and and_30 (and_30_out, xor_11_out, B5);
  xor xor_12 (xor_12_out, xor_11_out, B5);
  and and_31 (and_31_out, xor_15_out, and_39_out);
  and and_32 (and_32_out, xor_15_out, xor_18_out, and_42_out);
  or or_5 (or_5_out, and_35_out, and_31_out, and_32_out, and_33_out, and_34_out);
  xor xor_13 (xor_25_out[4], xor_12_out, or_5_out);
  and and_33 (and_33_out, xor_15_out, xor_18_out, xor_21_out, and_44_out);
  and and_34 (and_34_out, xor_15_out, xor_18_out, xor_21_out, xor_24_out, Controle);
  xor xor_14 (xor_14_out, Controle, in_13);
  and and_35 (and_35_out, xor_14_out, B4);
  xor xor_15 (xor_15_out, xor_14_out, B4);
  xor xor_16 (xor_25_out[3], xor_15_out, or_6_out);
  // Probe on xor_25_out
  // Probe on xor_25_out
  // Probe on xor_25_out
  // Probe on xor_1_out
  // Probe on or_1_out
  and and_36 (and_36_out, xor_18_out, and_42_out);
  and and_37 (and_37_out, xor_18_out, xor_21_out, and_44_out);
  or or_6 (or_6_out, and_39_out, and_36_out, and_37_out, and_38_out);
  and and_38 (and_38_out, xor_18_out, xor_21_out, xor_24_out, Controle);
  xor xor_17 (xor_17_out, Controle, in_14);
  and and_39 (and_39_out, xor_17_out, B3);
  xor xor_18 (xor_18_out, xor_17_out, B3);
  xor xor_19 (xor_25_out[2], xor_18_out, or_7_out);
  and and_40 (and_40_out, xor_21_out, and_44_out);
  and and_41 (and_41_out, xor_21_out, xor_24_out, Controle);
  or or_7 (or_7_out, and_42_out, and_40_out, and_41_out);
  xor xor_20 (xor_20_out, Controle, in_15);
  and and_42 (and_42_out, xor_20_out, B2);
  xor xor_21 (xor_21_out, xor_20_out, B2);
  and and_43 (and_43_out, xor_24_out, Controle);
  or or_8 (or_8_out, and_44_out, and_43_out);
  xor xor_22 (xor_25_out[1], xor_21_out, or_8_out);
  xor xor_23 (xor_23_out, Controle, in_16);
  and and_44 (and_44_out, xor_23_out, B1);
  xor xor_24 (xor_24_out, xor_23_out, B1);
  xor xor_25 (xor_25_out[0], xor_24_out, Controle);

  // Notes on the sheet:
  //   128
  //   A8
  //   64
  //   A7
  //   32
  //   A6
  //   16
  //   A5
  //   8
  //   A4
  //   4
  //   Binário
  //   Overflow
  //   A3
  //   Decimal sem sinal
  //   Decimal com sinal
  //   Unsigned Overflow
  //   2
  //   A2
  //   1
  //   A1
endmodule

module multiplicador_array_4bits (
  input  B0,
  input  A3,
  input  A2,
  input  A1,
  input  A0,
  input  B1,
  input  B2,
  input  B3
);

  wire and_1_out, and_2_out, and_3_out, and_4_out, and_5_out, and_6_out, and_7_out, and_8_out, and_9_out,
       and_10_out, and_11_out, and_12_out, and_13_out, and_14_out, and_15_out,
       meio_somador_do_multiplicador_1_c_out, meio_somador_do_multiplicador_1_s,
       meio_somador_do_multiplicador_2_c_out, meio_somador_do_multiplicador_3_c_out,
       meio_somador_do_multiplicador_4_c_out, somador_do_multiplicador_2_c_out, somador_do_multiplicador_2_s,
       somador_do_multiplicador_3_c_out, somador_do_multiplicador_4_c_out, somador_do_multiplicador_4_s,
       somador_do_multiplicador_5_c_out, somador_do_multiplicador_6_c_out, somador_do_multiplicador_6_s,
       somador_do_multiplicador_7_c_out, somador_do_multiplicador_7_s, somador_do_multiplicador_8_c_out,
       somador_do_multiplicador_8_s;
  wire [7:0] and_16_out;

  LED led_1 (.in(and_16_out[7]));
  and and_1 (and_1_out, B3, A3);
  somador_do_multiplicador somador_do_multiplicador_1 (
    .C_in(somador_do_multiplicador_3_c_out), .B(and_1_out), .A(somador_do_multiplicador_2_c_out),
    .C_out(and_16_out[7]), .S(and_16_out[6]));
  LED led_2 (.in(and_16_out[6]));
  and and_2 (and_2_out, B2, A3);
  and and_3 (and_3_out, B3, A2);
  LED led_3 (.in(and_16_out[5]));
  and and_4 (and_4_out, B1, A3);
  and and_5 (and_5_out, B2, A2);
  somador_do_multiplicador somador_do_multiplicador_2 (
    .C_in(somador_do_multiplicador_4_c_out), .B(and_2_out), .A(meio_somador_do_multiplicador_1_c_out),
    .C_out(somador_do_multiplicador_2_c_out), .S(somador_do_multiplicador_2_s));
  and and_6 (and_6_out, B3, A1);
  somador_do_multiplicador somador_do_multiplicador_3 (
    .C_in(somador_do_multiplicador_5_c_out), .B(and_3_out), .A(somador_do_multiplicador_2_s),
    .C_out(somador_do_multiplicador_3_c_out), .S(and_16_out[5]));
  and and_7 (and_7_out, B1, A2);
  meio_somador_do_multiplicador meio_somador_do_multiplicador_1 (
    .B(and_4_out), .A(somador_do_multiplicador_6_c_out), .C_out(meio_somador_do_multiplicador_1_c_out),
    .S(meio_somador_do_multiplicador_1_s));
  and and_8 (and_8_out, B2, A1);
  somador_do_multiplicador somador_do_multiplicador_4 (
    .C_in(somador_do_multiplicador_7_c_out), .B(and_5_out), .A(meio_somador_do_multiplicador_1_s),
    .C_out(somador_do_multiplicador_4_c_out), .S(somador_do_multiplicador_4_s));
  and and_9 (and_9_out, B3, A0);
  somador_do_multiplicador somador_do_multiplicador_5 (
    .C_in(meio_somador_do_multiplicador_2_c_out), .B(and_6_out), .A(somador_do_multiplicador_4_s),
    .C_out(somador_do_multiplicador_5_c_out), .S(and_16_out[4]));
  LED led_4 (.in(and_16_out[4]));
  and and_10 (and_10_out, B0, A3);
  somador_do_multiplicador somador_do_multiplicador_6 (
    .C_in(somador_do_multiplicador_8_c_out), .B(and_7_out), .A(and_10_out),
    .C_out(somador_do_multiplicador_6_c_out), .S(somador_do_multiplicador_6_s));
  somador_do_multiplicador somador_do_multiplicador_7 (
    .C_in(meio_somador_do_multiplicador_3_c_out), .B(and_8_out), .A(somador_do_multiplicador_6_s),
    .C_out(somador_do_multiplicador_7_c_out), .S(somador_do_multiplicador_7_s));
  meio_somador_do_multiplicador meio_somador_do_multiplicador_2 (
    .B(and_9_out), .A(somador_do_multiplicador_7_s), .C_out(meio_somador_do_multiplicador_2_c_out),
    .S(and_16_out[3]));
  LED led_5 (.in(and_16_out[3]));
  and and_11 (and_11_out, B0, A2);
  and and_12 (and_12_out, B1, A1);
  somador_do_multiplicador somador_do_multiplicador_8 (
    .C_in(meio_somador_do_multiplicador_4_c_out), .B(and_12_out), .A(and_11_out),
    .C_out(somador_do_multiplicador_8_c_out), .S(somador_do_multiplicador_8_s));
  and and_13 (and_13_out, B2, A0);
  meio_somador_do_multiplicador meio_somador_do_multiplicador_3 (
    .B(and_13_out), .A(somador_do_multiplicador_8_s), .C_out(meio_somador_do_multiplicador_3_c_out),
    .S(and_16_out[2]));
  LED led_6 (.in(and_16_out[2]));
  and and_14 (and_14_out, B0, A1);
  and and_15 (and_15_out, B1, A0);
  LED led_7 (.in(and_16_out[1]));
  meio_somador_do_multiplicador meio_somador_do_multiplicador_4 (
    .B(and_15_out), .A(and_14_out), .C_out(meio_somador_do_multiplicador_4_c_out), .S(and_16_out[1]));
  and and_16 (and_16_out[0], B0, A0);
  LED led_8 (.in(and_16_out[0]));
  // Probe on {A3, A2, A1, A0}
  // Probe on {B3, B2, B1, B0}
  // Probe on and_16_out

  // Notes on the sheet:
  //   128
  //   64
  //   32
  //   16
  //   8
  //   8
  //   4
  //   4
  //   2
  //   2
  //   1
  //   1
  //   1
  //   2
  //   4
  //   8
  //   X
  //   =
endmodule

module multiplicador_array_8bits (
  input  B0,
  input  B1,
  input  B2,
  input  B3,
  input  B4,
  input  B5,
  input  B6,
  input  B7,
  input  A7,
  input  A6,
  input  A5,
  input  A4,
  input  A3,
  input  A2,
  input  A1,
  input  A0
);

  wire and_1_out, and_2_out, and_3_out, and_4_out, and_5_out, and_6_out, and_7_out, and_8_out, and_9_out,
       and_10_out, and_11_out, and_12_out, and_13_out, and_14_out, and_15_out, and_16_out, and_17_out,
       and_18_out, and_19_out, and_20_out, and_21_out, and_22_out, and_23_out, and_24_out, and_25_out,
       and_26_out, and_27_out, and_28_out, and_29_out, and_30_out, and_31_out, and_32_out, and_33_out,
       and_34_out, and_35_out, and_36_out, and_37_out, and_38_out, and_39_out, and_40_out, and_41_out,
       and_42_out, and_43_out, and_44_out, and_45_out, and_46_out, and_47_out, and_48_out, and_49_out,
       and_50_out, and_51_out, and_52_out, and_53_out, and_54_out, and_55_out, and_56_out, and_57_out,
       and_58_out, and_59_out, and_60_out, and_61_out, and_62_out, and_63_out,
       meio_somador_do_multiplicador_1_c_out, meio_somador_do_multiplicador_1_s,
       meio_somador_do_multiplicador_2_c_out, meio_somador_do_multiplicador_3_c_out,
       meio_somador_do_multiplicador_4_c_out, meio_somador_do_multiplicador_5_c_out,
       meio_somador_do_multiplicador_6_c_out, meio_somador_do_multiplicador_7_c_out,
       meio_somador_do_multiplicador_8_c_out, somador_do_multiplicador_2_c_out, somador_do_multiplicador_2_s,
       somador_do_multiplicador_3_c_out, somador_do_multiplicador_4_c_out, somador_do_multiplicador_4_s,
       somador_do_multiplicador_5_c_out, somador_do_multiplicador_5_s, somador_do_multiplicador_6_c_out,
       somador_do_multiplicador_7_c_out, somador_do_multiplicador_7_s, somador_do_multiplicador_8_c_out,
       somador_do_multiplicador_8_s, somador_do_multiplicador_9_c_out, somador_do_multiplicador_9_s,
       somador_do_multiplicador_10_c_out, somador_do_multiplicador_11_c_out, somador_do_multiplicador_11_s,
       somador_do_multiplicador_12_c_out, somador_do_multiplicador_12_s, somador_do_multiplicador_13_c_out,
       somador_do_multiplicador_13_s, somador_do_multiplicador_14_c_out, somador_do_multiplicador_14_s,
       somador_do_multiplicador_15_c_out, somador_do_multiplicador_16_c_out, somador_do_multiplicador_16_s,
       somador_do_multiplicador_17_c_out, somador_do_multiplicador_17_s, somador_do_multiplicador_18_c_out,
       somador_do_multiplicador_18_s, somador_do_multiplicador_19_c_out, somador_do_multiplicador_19_s,
       somador_do_multiplicador_20_c_out, somador_do_multiplicador_20_s, somador_do_multiplicador_21_c_out,
       somador_do_multiplicador_22_c_out, somador_do_multiplicador_22_s, somador_do_multiplicador_23_c_out,
       somador_do_multiplicador_23_s, somador_do_multiplicador_24_c_out, somador_do_multiplicador_24_s,
       somador_do_multiplicador_25_c_out, somador_do_multiplicador_25_s, somador_do_multiplicador_26_c_out,
       somador_do_multiplicador_26_s, somador_do_multiplicador_27_c_out, somador_do_multiplicador_28_c_out,
       somador_do_multiplicador_28_s, somador_do_multiplicador_29_c_out, somador_do_multiplicador_29_s,
       somador_do_multiplicador_30_c_out, somador_do_multiplicador_30_s, somador_do_multiplicador_31_c_out,
       somador_do_multiplicador_31_s, somador_do_multiplicador_32_c_out, somador_do_multiplicador_32_s,
       somador_do_multiplicador_33_c_out, somador_do_multiplicador_33_s, somador_do_multiplicador_34_c_out,
       somador_do_multiplicador_34_s, somador_do_multiplicador_35_c_out, somador_do_multiplicador_35_s,
       somador_do_multiplicador_36_c_out, somador_do_multiplicador_36_s, somador_do_multiplicador_37_c_out,
       somador_do_multiplicador_37_s, somador_do_multiplicador_38_c_out, somador_do_multiplicador_38_s,
       somador_do_multiplicador_39_c_out, somador_do_multiplicador_39_s, somador_do_multiplicador_40_c_out,
       somador_do_multiplicador_40_s, somador_do_multiplicador_41_c_out, somador_do_multiplicador_41_s,
       somador_do_multiplicador_42_c_out, somador_do_multiplicador_42_s, somador_do_multiplicador_43_c_out,
       somador_do_multiplicador_43_s, somador_do_multiplicador_44_c_out, somador_do_multiplicador_44_s,
       somador_do_multiplicador_45_c_out, somador_do_multiplicador_45_s, somador_do_multiplicador_46_c_out,
       somador_do_multiplicador_46_s, somador_do_multiplicador_47_c_out, somador_do_multiplicador_47_s,
       somador_do_multiplicador_48_c_out, somador_do_multiplicador_48_s;
  wire [15:0] S;

  LED led_1 (.in(S[15]));
  and and_1 (and_1_out, B7, A7);
  somador_do_multiplicador somador_do_multiplicador_1 (
    .C_in(somador_do_multiplicador_3_c_out), .B(and_1_out), .A(somador_do_multiplicador_2_c_out),
    .C_out(S[15]), .S(S[14]));
  LED led_2 (.in(S[14]));
  and and_2 (and_2_out, B6, A7);
  and and_3 (and_3_out, B7, A6);
  LED led_3 (.in(S[13]));
  // Probe on {A7, A6, A5, A4, A3, A2, A1, A0}
  // Probe on {B7, B6, B5, B4, B3, B2, B1, B0}
  // Probe on S
  and and_4 (and_4_out, B5, A7);
  and and_5 (and_5_out, B6, A6);
  somador_do_multiplicador somador_do_multiplicador_2 (
    .C_in(somador_do_multiplicador_5_c_out), .B(and_2_out), .A(somador_do_multiplicador_4_c_out),
    .C_out(somador_do_multiplicador_2_c_out), .S(somador_do_multiplicador_2_s));
  and and_6 (and_6_out, B7, A5);
  somador_do_multiplicador somador_do_multiplicador_3 (
    .C_in(somador_do_multiplicador_6_c_out), .B(and_3_out), .A(somador_do_multiplicador_2_s),
    .C_out(somador_do_multiplicador_3_c_out), .S(S[13]));
  and and_7 (and_7_out, B4, A7);
  and and_8 (and_8_out, B5, A6);
  somador_do_multiplicador somador_do_multiplicador_4 (
    .C_in(somador_do_multiplicador_8_c_out), .B(and_4_out), .A(somador_do_multiplicador_7_c_out),
    .C_out(somador_do_multiplicador_4_c_out), .S(somador_do_multiplicador_4_s));
  and and_9 (and_9_out, B6, A5);
  somador_do_multiplicador somador_do_multiplicador_5 (
    .C_in(somador_do_multiplicador_9_c_out), .B(and_5_out), .A(somador_do_multiplicador_4_s),
    .C_out(somador_do_multiplicador_5_c_out), .S(somador_do_multiplicador_5_s));
  and and_10 (and_10_out, B7, A4);
  somador_do_multiplicador somador_do_multiplicador_6 (
    .C_in(somador_do_multiplicador_10_c_out), .B(and_6_out), .A(somador_do_multiplicador_5_s),
    .C_out(somador_do_multiplicador_6_c_out), .S(S[12]));
  LED led_4 (.in(S[12]));
  somador_do_multiplicador somador_do_multiplicador_7 (
    .C_in(somador_do_multiplicador_12_c_out), .B(and_7_out), .A(somador_do_multiplicador_11_c_out),
    .C_out(somador_do_multiplicador_7_c_out), .S(somador_do_multiplicador_7_s));
  somador_do_multiplicador somador_do_multiplicador_8 (
    .C_in(somador_do_multiplicador_13_c_out), .B(and_8_out), .A(somador_do_multiplicador_7_s),
    .C_out(somador_do_multiplicador_8_c_out), .S(somador_do_multiplicador_8_s));
  somador_do_multiplicador somador_do_multiplicador_9 (
    .C_in(somador_do_multiplicador_14_c_out), .B(and_9_out), .A(somador_do_multiplicador_8_s),
    .C_out(somador_do_multiplicador_9_c_out), .S(somador_do_multiplicador_9_s));
  somador_do_multiplicador somador_do_multiplicador_10 (
    .C_in(somador_do_multiplicador_15_c_out), .B(and_10_out), .A(somador_do_multiplicador_9_s),
    .C_out(somador_do_multiplicador_10_c_out), .S(S[11]));
  LED led_5 (.in(S[11]));
  and and_11 (and_11_out, B3, A7);
  somador_do_multiplicador somador_do_multiplicador_11 (
    .C_in(somador_do_multiplicador_17_c_out), .B(and_11_out), .A(somador_do_multiplicador_16_c_out),
    .C_out(somador_do_multiplicador_11_c_out), .S(somador_do_multiplicador_11_s));
  and and_12 (and_12_out, B4, A6);
  somador_do_multiplicador somador_do_multiplicador_12 (
    .C_in(somador_do_multiplicador_18_c_out), .B(and_12_out), .A(somador_do_multiplicador_11_s),
    .C_out(somador_do_multiplicador_12_c_out), .S(somador_do_multiplicador_12_s));
  and and_13 (and_13_out, B5, A5);
  somador_do_multiplicador somador_do_multiplicador_13 (
    .C_in(somador_do_multiplicador_19_c_out), .B(and_13_out), .A(somador_do_multiplicador_12_s),
    .C_out(somador_do_multiplicador_13_c_out), .S(somador_do_multiplicador_13_s));
  and and_14 (and_14_out, B6, A4);
  somador_do_multiplicador somador_do_multiplicador_14 (
    .C_in(somador_do_multiplicador_20_c_out), .B(and_14_out), .A(somador_do_multiplicador_13_s),
    .C_out(somador_do_multiplicador_14_c_out), .S(somador_do_multiplicador_14_s));
  and and_15 (and_15_out, B7, A3);
  somador_do_multiplicador somador_do_multiplicador_15 (
    .C_in(somador_do_multiplicador_21_c_out), .B(and_15_out), .A(somador_do_multiplicador_14_s),
    .C_out(somador_do_multiplicador_15_c_out), .S(S[10]));
  LED led_6 (.in(S[10]));
  and and_16 (and_16_out, B2, A7);
  and and_17 (and_17_out, B3, A6);
  and and_18 (and_18_out, B4, A5);
  and and_19 (and_19_out, B5, A4);
  and and_20 (and_20_out, B6, A3);
  and and_21 (and_21_out, B7, A2);
  LED led_7 (.in(S[9]));
  and and_22 (and_22_out, B1, A7);
  and and_23 (and_23_out, B2, A6);
  somador_do_multiplicador somador_do_multiplicador_16 (
    .C_in(somador_do_multiplicador_22_c_out), .B(and_16_out), .A(meio_somador_do_multiplicador_1_c_out),
    .C_out(somador_do_multiplicador_16_c_out), .S(somador_do_multiplicador_16_s));
  and and_24 (and_24_out, B3, A5);
  somador_do_multiplicador somador_do_multiplicador_17 (
    .C_in(somador_do_multiplicador_23_c_out), .B(and_17_out), .A(somador_do_multiplicador_16_s),
    .C_out(somador_do_multiplicador_17_c_out), .S(somador_do_multiplicador_17_s));
  and and_25 (and_25_out, B4, A4);
  somador_do_multiplicador somador_do_multiplicador_18 (
    .C_in(somador_do_multiplicador_24_c_out), .B(and_18_out), .A(somador_do_multiplicador_17_s),
    .C_out(somador_do_multiplicador_18_c_out), .S(somador_do_multiplicador_18_s));
  and and_26 (and_26_out, B5, A3);
  somador_do_multiplicador somador_do_multiplicador_19 (
    .C_in(somador_do_multiplicador_25_c_out), .B(and_19_out), .A(somador_do_multiplicador_18_s),
    .C_out(somador_do_multiplicador_19_c_out), .S(somador_do_multiplicador_19_s));
  and and_27 (and_27_out, B6, A2);
  somador_do_multiplicador somador_do_multiplicador_20 (
    .C_in(somador_do_multiplicador_26_c_out), .B(and_20_out), .A(somador_do_multiplicador_19_s),
    .C_out(somador_do_multiplicador_20_c_out), .S(somador_do_multiplicador_20_s));
  and and_28 (and_28_out, B7, A1);
  somador_do_multiplicador somador_do_multiplicador_21 (
    .C_in(somador_do_multiplicador_27_c_out), .B(and_21_out), .A(somador_do_multiplicador_20_s),
    .C_out(somador_do_multiplicador_21_c_out), .S(S[9]));
  and and_29 (and_29_out, B1, A6);
  meio_somador_do_multiplicador meio_somador_do_multiplicador_1 (
    .B(and_22_out), .A(somador_do_multiplicador_28_c_out), .C_out(meio_somador_do_multiplicador_1_c_out),
    .S(meio_somador_do_multiplicador_1_s));
  and and_30 (and_30_out, B2, A5);
  somador_do_multiplicador somador_do_multiplicador_22 (
    .C_in(somador_do_multiplicador_29_c_out), .B(and_23_out), .A(meio_somador_do_multiplicador_1_s),
    .C_out(somador_do_multiplicador_22_c_out), .S(somador_do_multiplicador_22_s));
  and and_31 (and_31_out, B3, A4);
  somador_do_multiplicador somador_do_multiplicador_23 (
    .C_in(somador_do_multiplicador_30_c_out), .B(and_24_out), .A(somador_do_multiplicador_22_s),
    .C_out(somador_do_multiplicador_23_c_out), .S(somador_do_multiplicador_23_s));
  and and_32 (and_32_out, B4, A3);
  somador_do_multiplicador somador_do_multiplicador_24 (
    .C_in(somador_do_multiplicador_31_c_out), .B(and_25_out), .A(somador_do_multiplicador_23_s),
    .C_out(somador_do_multiplicador_24_c_out), .S(somador_do_multiplicador_24_s));
  and and_33 (and_33_out, B5, A2);
  somador_do_multiplicador somador_do_multiplicador_25 (
    .C_in(somador_do_multiplicador_32_c_out), .B(and_26_out), .A(somador_do_multiplicador_24_s),
    .C_out(somador_do_multiplicador_25_c_out), .S(somador_do_multiplicador_25_s));
  and and_34 (and_34_out, B6, A1);
  somador_do_multiplicador somador_do_multiplicador_26 (
    .C_in(somador_do_multiplicador_33_c_out), .B(and_27_out), .A(somador_do_multiplicador_25_s),
    .C_out(somador_do_multiplicador_26_c_out), .S(somador_do_multiplicador_26_s));
  and and_35 (and_35_out, B7, A0);
  somador_do_multiplicador somador_do_multiplicador_27 (
    .C_in(meio_somador_do_multiplicador_2_c_out), .B(and_28_out), .A(somador_do_multiplicador_26_s),
    .C_out(somador_do_multiplicador_27_c_out), .S(S[8]));
  LED led_8 (.in(S[8]));
  and and_36 (and_36_out, B0, A7);
  somador_do_multiplicador somador_do_multiplicador_28 (
    .C_in(somador_do_multiplicador_34_c_out), .B(and_29_out), .A(and_36_out),
    .C_out(somador_do_multiplicador_28_c_out), .S(somador_do_multiplicador_28_s));
  somador_do_multiplicador somador_do_multiplicador_29 (
    .C_in(somador_do_multiplicador_35_c_out), .B(and_30_out), .A(somador_do_multiplicador_28_s),
    .C_out(somador_do_multiplicador_29_c_out), .S(somador_do_multiplicador_29_s));
  somador_do_multiplicador somador_do_multiplicador_30 (
    .C_in(somador_do_multiplicador_36_c_out), .B(and_31_out), .A(somador_do_multiplicador_29_s),
    .C_out(somador_do_multiplicador_30_c_out), .S(somador_do_multiplicador_30_s));
  somador_do_multiplicador somador_do_multiplicador_31 (
    .C_in(somador_do_multiplicador_37_c_out), .B(and_32_out), .A(somador_do_multiplicador_30_s),
    .C_out(somador_do_multiplicador_31_c_out), .S(somador_do_multiplicador_31_s));
  somador_do_multiplicador somador_do_multiplicador_32 (
    .C_in(somador_do_multiplicador_38_c_out), .B(and_33_out), .A(somador_do_multiplicador_31_s),
    .C_out(somador_do_multiplicador_32_c_out), .S(somador_do_multiplicador_32_s));
  somador_do_multiplicador somador_do_multiplicador_33 (
    .C_in(meio_somador_do_multiplicador_3_c_out), .B(and_34_out), .A(somador_do_multiplicador_32_s),
    .C_out(somador_do_multiplicador_33_c_out), .S(somador_do_multiplicador_33_s));
  meio_somador_do_multiplicador meio_somador_do_multiplicador_2 (
    .B(and_35_out), .A(somador_do_multiplicador_33_s), .C_out(meio_somador_do_multiplicador_2_c_out), .S(S[7]));
  LED led_9 (.in(S[7]));
  and and_37 (and_37_out, B0, A6);
  and and_38 (and_38_out, B1, A5);
  somador_do_multiplicador somador_do_multiplicador_34 (
    .C_in(somador_do_multiplicador_39_c_out), .B(and_38_out), .A(and_37_out),
    .C_out(somador_do_multiplicador_34_c_out), .S(somador_do_multiplicador_34_s));
  and and_39 (and_39_out, B2, A4);
  somador_do_multiplicador somador_do_multiplicador_35 (
    .C_in(somador_do_multiplicador_40_c_out), .B(and_39_out), .A(somador_do_multiplicador_34_s),
    .C_out(somador_do_multiplicador_35_c_out), .S(somador_do_multiplicador_35_s));
  and and_40 (and_40_out, B3, A3);
  somador_do_multiplicador somador_do_multiplicador_36 (
    .C_in(somador_do_multiplicador_41_c_out), .B(and_40_out), .A(somador_do_multiplicador_35_s),
    .C_out(somador_do_multiplicador_36_c_out), .S(somador_do_multiplicador_36_s));
  and and_41 (and_41_out, B4, A2);
  somador_do_multiplicador somador_do_multiplicador_37 (
    .C_in(somador_do_multiplicador_42_c_out), .B(and_41_out), .A(somador_do_multiplicador_36_s),
    .C_out(somador_do_multiplicador_37_c_out), .S(somador_do_multiplicador_37_s));
  and and_42 (and_42_out, B5, A1);
  somador_do_multiplicador somador_do_multiplicador_38 (
    .C_in(meio_somador_do_multiplicador_4_c_out), .B(and_42_out), .A(somador_do_multiplicador_37_s),
    .C_out(somador_do_multiplicador_38_c_out), .S(somador_do_multiplicador_38_s));
  and and_43 (and_43_out, B6, A0);
  meio_somador_do_multiplicador meio_somador_do_multiplicador_3 (
    .B(and_43_out), .A(somador_do_multiplicador_38_s), .C_out(meio_somador_do_multiplicador_3_c_out), .S(S[6]));
  LED led_10 (.in(S[6]));
  and and_44 (and_44_out, B0, A5);
  and and_45 (and_45_out, B1, A4);
  and and_46 (and_46_out, B2, A3);
  and and_47 (and_47_out, B3, A2);
  and and_48 (and_48_out, B4, A1);
  and and_49 (and_49_out, B5, A0);
  LED led_11 (.in(S[5]));
  and and_50 (and_50_out, B1, A3);
  somador_do_multiplicador somador_do_multiplicador_39 (
    .C_in(somador_do_multiplicador_43_c_out), .B(and_45_out), .A(and_44_out),
    .C_out(somador_do_multiplicador_39_c_out), .S(somador_do_multiplicador_39_s));
  and and_51 (and_51_out, B2, A2);
  somador_do_multiplicador somador_do_multiplicador_40 (
    .C_in(somador_do_multiplicador_44_c_out), .B(and_46_out), .A(somador_do_multiplicador_39_s),
    .C_out(somador_do_multiplicador_40_c_out), .S(somador_do_multiplicador_40_s));
  and and_52 (and_52_out, B3, A1);
  somador_do_multiplicador somador_do_multiplicador_41 (
    .C_in(somador_do_multiplicador_45_c_out), .B(and_47_out), .A(somador_do_multiplicador_40_s),
    .C_out(somador_do_multiplicador_41_c_out), .S(somador_do_multiplicador_41_s));
  and and_53 (and_53_out, B4, A0);
  somador_do_multiplicador somador_do_multiplicador_42 (
    .C_in(meio_somador_do_multiplicador_5_c_out), .B(and_48_out), .A(somador_do_multiplicador_41_s),
    .C_out(somador_do_multiplicador_42_c_out), .S(somador_do_multiplicador_42_s));
  meio_somador_do_multiplicador meio_somador_do_multiplicador_4 (
    .B(and_49_out), .A(somador_do_multiplicador_42_s), .C_out(meio_somador_do_multiplicador_4_c_out), .S(S[5]));
  and and_54 (and_54_out, B0, A4);
  and and_55 (and_55_out, B1, A2);
  somador_do_multiplicador somador_do_multiplicador_43 (
    .C_in(somador_do_multiplicador_46_c_out), .B(and_50_out), .A(and_54_out),
    .C_out(somador_do_multiplicador_43_c_out), .S(somador_do_multiplicador_43_s));
  and and_56 (and_56_out, B2, A1);
  somador_do_multiplicador somador_do_multiplicador_44 (
    .C_in(somador_do_multiplicador_47_c_out), .B(and_51_out), .A(somador_do_multiplicador_43_s),
    .C_out(somador_do_multiplicador_44_c_out), .S(somador_do_multiplicador_44_s));
  and and_57 (and_57_out, B3, A0);
  somador_do_multiplicador somador_do_multiplicador_45 (
    .C_in(meio_somador_do_multiplicador_6_c_out), .B(and_52_out), .A(somador_do_multiplicador_44_s),
    .C_out(somador_do_multiplicador_45_c_out), .S(somador_do_multiplicador_45_s));
  meio_somador_do_multiplicador meio_somador_do_multiplicador_5 (
    .B(and_53_out), .A(somador_do_multiplicador_45_s), .C_out(meio_somador_do_multiplicador_5_c_out), .S(S[4]));
  LED led_12 (.in(S[4]));
  and and_58 (and_58_out, B0, A3);
  somador_do_multiplicador somador_do_multiplicador_46 (
    .C_in(somador_do_multiplicador_48_c_out), .B(and_55_out), .A(and_58_out),
    .C_out(somador_do_multiplicador_46_c_out), .S(somador_do_multiplicador_46_s));
  somador_do_multiplicador somador_do_multiplicador_47 (
    .C_in(meio_somador_do_multiplicador_7_c_out), .B(and_56_out), .A(somador_do_multiplicador_46_s),
    .C_out(somador_do_multiplicador_47_c_out), .S(somador_do_multiplicador_47_s));
  meio_somador_do_multiplicador meio_somador_do_multiplicador_6 (
    .B(and_57_out), .A(somador_do_multiplicador_47_s), .C_out(meio_somador_do_multiplicador_6_c_out), .S(S[3]));
  LED led_13 (.in(S[3]));
  and and_59 (and_59_out, B0, A2);
  and and_60 (and_60_out, B1, A1);
  somador_do_multiplicador somador_do_multiplicador_48 (
    .C_in(meio_somador_do_multiplicador_8_c_out), .B(and_60_out), .A(and_59_out),
    .C_out(somador_do_multiplicador_48_c_out), .S(somador_do_multiplicador_48_s));
  and and_61 (and_61_out, B2, A0);
  meio_somador_do_multiplicador meio_somador_do_multiplicador_7 (
    .B(and_61_out), .A(somador_do_multiplicador_48_s), .C_out(meio_somador_do_multiplicador_7_c_out), .S(S[2]));
  LED led_14 (.in(S[2]));
  and and_62 (and_62_out, B0, A1);
  and and_63 (and_63_out, B1, A0);
  LED led_15 (.in(S[1]));
  meio_somador_do_multiplicador meio_somador_do_multiplicador_8 (
    .B(and_63_out), .A(and_62_out), .C_out(meio_somador_do_multiplicador_8_c_out), .S(S[1]));
  and and_64 (S[0], B0, A0);
  LED led_16 (.in(S[0]));

  // Notes on the sheet:
  //   32768
  //   16384
  //   X
  //   =
  //   8192
  //   4096
  //   2048
  //   1024
  //   512
  //   256
  //   128
  //   128
  //   64
  //   64
  //   32
  //   32
  //   16
  //   16
  //   8
  //   8
  //   4
  //   4
  //   2
  //   2
  //   1
  //   1
  //   1
  //   2
  //   4
  //   8
  //   16
  //   32
  //   64
  //   128
endmodule

module multiplicador_array_8bits_SA (
  input  B0,
  input  B1,
  input  B2,
  input  B3,
  input  B4,
  input  B5,
  input  B6,
  input  B7,
  input  A7,
  input  A6,
  input  A5,
  input  A4,
  input  A3,
  input  A2,
  input  A1,
  input  A0
);

  wire and_1_out, and_2_out, and_3_out, and_4_out, and_5_out, and_6_out, and_7_out, and_8_out, and_9_out,
       and_10_out, and_11_out, and_12_out, and_13_out, and_14_out, and_15_out, and_16_out, and_17_out,
       and_18_out, and_19_out, and_20_out, and_21_out, and_22_out, and_23_out, and_24_out, and_25_out,
       and_26_out, and_27_out, and_28_out, and_29_out, and_30_out, and_31_out, and_32_out, and_33_out,
       and_34_out, and_35_out, and_36_out, and_37_out, and_38_out, and_39_out, and_40_out, and_41_out,
       and_42_out, and_43_out, and_44_out, and_45_out, and_46_out, and_47_out, and_48_out, and_49_out,
       and_50_out, and_51_out, and_52_out, and_53_out, and_54_out, and_55_out, and_56_out, and_57_out,
       and_58_out, and_59_out, and_60_out, and_61_out, and_62_out, and_63_out, and_64_out, and_65_out,
       and_66_out, and_67_out, and_68_out, and_69_out, and_70_out, and_71_out, and_72_out, and_73_out,
       and_74_out, and_75_out, and_76_out, and_77_out, and_78_out, and_79_out, and_80_out, and_81_out,
       and_82_out, and_83_out, and_84_out, and_85_out, and_86_out, and_87_out, and_88_out, and_89_out,
       and_90_out, and_91_out, and_92_out, and_93_out, and_94_out, and_95_out, and_96_out, and_97_out,
       and_98_out, and_99_out, and_100_out, and_101_out, and_102_out, and_103_out, and_104_out, and_105_out,
       and_106_out, and_107_out, and_108_out, and_109_out, and_110_out, and_111_out, and_112_out,
       and_113_out, and_114_out, and_115_out, and_116_out, and_117_out, and_118_out, and_119_out,
       and_120_out, and_121_out, and_122_out, and_123_out, and_124_out, and_125_out, and_126_out,
       and_127_out, and_128_out, and_129_out, and_130_out, and_131_out, and_132_out, and_133_out,
       and_134_out, and_135_out, and_136_out, and_137_out, and_138_out, and_139_out, and_140_out,
       and_141_out, and_142_out, and_143_out, and_144_out, and_145_out, and_146_out, and_147_out,
       and_148_out, and_149_out, and_150_out, and_151_out, and_152_out, and_153_out, and_154_out,
       and_155_out, and_156_out, and_157_out, and_158_out, and_159_out, and_160_out, and_161_out,
       and_162_out, and_163_out, and_164_out, and_165_out, and_166_out, and_167_out, or_2_out, or_3_out,
       or_4_out, or_5_out, or_6_out, or_7_out, or_8_out, or_9_out, or_10_out, or_11_out, or_12_out,
       or_13_out, or_14_out, or_15_out, or_16_out, or_17_out, or_18_out, or_19_out, or_20_out, or_21_out,
       or_22_out, or_23_out, or_24_out, or_25_out, or_26_out, or_27_out, or_28_out, or_29_out, or_30_out,
       or_31_out, or_32_out, or_33_out, or_34_out, or_35_out, or_36_out, or_37_out, or_38_out, or_39_out,
       or_40_out, or_41_out, or_42_out, or_43_out, or_44_out, or_45_out, or_46_out, or_47_out, or_48_out,
       xor_1_out, xor_4_out, xor_5_out, xor_6_out, xor_7_out, xor_9_out, xor_10_out, xor_11_out, xor_12_out,
       xor_13_out, xor_14_out, xor_15_out, xor_17_out, xor_18_out, xor_19_out, xor_20_out, xor_21_out,
       xor_22_out, xor_23_out, xor_24_out, xor_26_out, xor_27_out, xor_28_out, xor_29_out, xor_30_out,
       xor_32_out, xor_33_out, xor_34_out, xor_35_out, xor_36_out, xor_37_out, xor_38_out, xor_39_out,
       xor_40_out, xor_41_out, xor_42_out, xor_43_out, xor_45_out, xor_46_out, xor_47_out, xor_48_out,
       xor_49_out, xor_50_out, xor_51_out, xor_52_out, xor_53_out, xor_54_out, xor_55_out, xor_56_out,
       xor_57_out, xor_59_out, xor_60_out, xor_61_out, xor_62_out, xor_63_out, xor_64_out, xor_65_out,
       xor_66_out, xor_67_out, xor_68_out, xor_69_out, xor_71_out, xor_72_out, xor_73_out, xor_74_out,
       xor_75_out, xor_76_out, xor_77_out, xor_78_out, xor_79_out, xor_81_out, xor_82_out, xor_83_out,
       xor_84_out, xor_85_out, xor_86_out, xor_87_out, xor_88_out, xor_90_out, xor_91_out, xor_92_out,
       xor_93_out, xor_94_out, xor_95_out, xor_96_out, xor_97_out, xor_98_out, xor_99_out, xor_101_out,
       xor_102_out;
  wire [15:0] S;

  and and_1 (and_1_out, or_3_out, xor_1_out);
  and and_2 (and_2_out, or_2_out, and_3_out);
  or or_1 (S[15], and_2_out, and_1_out);
  LED led_1 (.in(S[15]));
  and and_3 (and_3_out, B7, A7);
  xor xor_1 (xor_1_out, and_3_out, or_2_out);
  and and_4 (and_4_out, xor_5_out, and_7_out);
  xor xor_2 (S[14], or_3_out, xor_1_out);
  LED led_2 (.in(S[14]));
  and and_5 (and_5_out, or_5_out, and_9_out);
  and and_6 (and_6_out, or_6_out, xor_4_out);
  or or_2 (or_2_out, and_5_out, and_6_out);
  and and_7 (and_7_out, B7, A6);
  and and_8 (and_8_out, or_4_out, xor_6_out);
  xor xor_3 (S[13], or_4_out, xor_6_out);
  or or_3 (or_3_out, and_4_out, and_8_out);
  LED led_3 (.in(S[13]));
  and and_9 (and_9_out, B6, A7);
  xor xor_4 (xor_4_out, and_9_out, or_5_out);
  xor xor_5 (xor_5_out, or_6_out, xor_4_out);
  xor xor_6 (xor_6_out, and_7_out, xor_5_out);
  and and_10 (and_10_out, xor_12_out, and_16_out);
  or or_4 (or_4_out, and_10_out, and_17_out);
  and and_11 (and_11_out, or_8_out, and_18_out);
  and and_12 (and_12_out, or_9_out, xor_9_out);
  or or_5 (or_5_out, and_11_out, and_12_out);
  and and_13 (and_13_out, B6, A6);
  and and_14 (and_14_out, xor_10_out, and_13_out);
  and and_15 (and_15_out, or_10_out, xor_11_out);
  or or_6 (or_6_out, and_14_out, and_15_out);
  and and_16 (and_16_out, B7, A5);
  xor xor_7 (xor_7_out, and_16_out, xor_12_out);
  and and_17 (and_17_out, or_7_out, xor_7_out);
  xor xor_8 (S[12], or_7_out, xor_7_out);
  LED led_4 (.in(S[12]));
  and and_18 (and_18_out, B5, A7);
  xor xor_9 (xor_9_out, and_18_out, or_8_out);
  xor xor_10 (xor_10_out, or_9_out, xor_9_out);
  xor xor_11 (xor_11_out, and_13_out, xor_10_out);
  and and_19 (and_19_out, xor_20_out, and_25_out);
  xor xor_12 (xor_12_out, or_10_out, xor_11_out);
  and and_20 (and_20_out, xor_14_out, and_27_out);
  and and_21 (and_21_out, or_12_out, xor_15_out);
  or or_7 (or_7_out, and_20_out, and_21_out);
  and and_22 (and_22_out, or_13_out, and_28_out);
  or or_8 (or_8_out, and_22_out, and_29_out);
  and and_23 (and_23_out, xor_18_out, and_30_out);
  and and_24 (and_24_out, or_15_out, xor_19_out);
  or or_9 (or_9_out, and_23_out, and_24_out);
  and and_25 (and_25_out, B6, A5);
  xor xor_13 (xor_13_out, and_25_out, xor_20_out);
  and and_26 (and_26_out, or_11_out, xor_13_out);
  xor xor_14 (xor_14_out, or_11_out, xor_13_out);
  or or_10 (or_10_out, and_19_out, and_26_out);
  and and_27 (and_27_out, B7, A4);
  xor xor_15 (xor_15_out, and_27_out, xor_14_out);
  xor xor_16 (S[11], or_12_out, xor_15_out);
  LED led_5 (.in(S[11]));
  and and_28 (and_28_out, B4, A7);
  xor xor_17 (xor_17_out, and_28_out, or_13_out);
  and and_29 (and_29_out, or_14_out, xor_17_out);
  xor xor_18 (xor_18_out, or_14_out, xor_17_out);
  and and_30 (and_30_out, B5, A6);
  xor xor_19 (xor_19_out, and_30_out, xor_18_out);
  and and_31 (and_31_out, xor_29_out, and_38_out);
  xor xor_20 (xor_20_out, or_15_out, xor_19_out);
  and and_32 (and_32_out, xor_21_out, and_40_out);
  or or_11 (or_11_out, and_32_out, and_41_out);
  and and_33 (and_33_out, xor_23_out, and_42_out);
  and and_34 (and_34_out, or_18_out, xor_24_out);
  or or_12 (or_12_out, and_33_out, and_34_out);
  // Probe on {A7, A6, A5, A4, A3, A2, A1, A0}
  // Probe on {B7, B6, B5, B4, B3, B2, B1, B0}
  // Probe on S
  and and_35 (and_35_out, or_22_out, and_44_out);
  or or_13 (or_13_out, and_35_out, and_45_out);
  and and_36 (and_36_out, xor_27_out, and_46_out);
  and and_37 (and_37_out, or_20_out, xor_28_out);
  or or_14 (or_14_out, and_36_out, and_37_out);
  and and_38 (and_38_out, B5, A5);
  and and_39 (and_39_out, or_16_out, xor_30_out);
  xor xor_21 (xor_21_out, or_16_out, xor_30_out);
  or or_15 (or_15_out, and_31_out, and_39_out);
  and and_40 (and_40_out, B6, A4);
  xor xor_22 (xor_22_out, and_40_out, xor_21_out);
  and and_41 (and_41_out, or_17_out, xor_22_out);
  xor xor_23 (xor_23_out, or_17_out, xor_22_out);
  and and_42 (and_42_out, B7, A3);
  xor xor_24 (xor_24_out, and_42_out, xor_23_out);
  and and_43 (and_43_out, xor_35_out, and_50_out);
  xor xor_25 (S[10], or_18_out, xor_24_out);
  LED led_6 (.in(S[10]));
  and and_44 (and_44_out, B3, A7);
  xor xor_26 (xor_26_out, and_44_out, or_22_out);
  and and_45 (and_45_out, or_19_out, xor_26_out);
  xor xor_27 (xor_27_out, or_19_out, xor_26_out);
  and and_46 (and_46_out, B4, A6);
  xor xor_28 (xor_28_out, and_46_out, xor_27_out);
  xor xor_29 (xor_29_out, or_20_out, xor_28_out);
  xor xor_30 (xor_30_out, and_38_out, xor_29_out);
  and and_47 (and_47_out, xor_42_out, and_58_out);
  or or_16 (or_16_out, and_47_out, and_59_out);
  and and_48 (and_48_out, xor_33_out, and_60_out);
  and and_49 (and_49_out, or_24_out, xor_34_out);
  or or_17 (or_17_out, and_48_out, and_49_out);
  and and_50 (and_50_out, B7, A2);
  and and_51 (and_51_out, or_21_out, xor_36_out);
  xor xor_31 (S[9], or_21_out, xor_36_out);
  or or_18 (or_18_out, and_43_out, and_51_out);
  LED led_7 (.in(S[9]));
  and and_52 (and_52_out, and_82_out, and_62_out);
  and and_53 (and_53_out, xor_38_out, and_64_out);
  and and_54 (and_54_out, or_26_out, xor_39_out);
  or or_19 (or_19_out, and_53_out, and_54_out);
  and and_55 (and_55_out, B4, A5);
  and and_56 (and_56_out, xor_40_out, and_55_out);
  and and_57 (and_57_out, or_27_out, xor_41_out);
  or or_20 (or_20_out, and_56_out, and_57_out);
  and and_58 (and_58_out, B5, A4);
  xor xor_32 (xor_32_out, and_58_out, xor_42_out);
  and and_59 (and_59_out, or_23_out, xor_32_out);
  xor xor_33 (xor_33_out, or_23_out, xor_32_out);
  and and_60 (and_60_out, B6, A3);
  xor xor_34 (xor_34_out, and_60_out, xor_33_out);
  xor xor_35 (xor_35_out, or_24_out, xor_34_out);
  xor xor_36 (xor_36_out, and_50_out, xor_35_out);
  and and_61 (and_61_out, xor_50_out, and_71_out);
  or or_21 (or_21_out, and_61_out, and_72_out);
  and and_62 (and_62_out, B2, A7);
  xor xor_37 (xor_37_out, and_62_out, and_82_out);
  and and_63 (and_63_out, or_25_out, xor_37_out);
  xor xor_38 (xor_38_out, or_25_out, xor_37_out);
  or or_22 (or_22_out, and_52_out, and_63_out);
  and and_64 (and_64_out, B3, A6);
  xor xor_39 (xor_39_out, and_64_out, xor_38_out);
  xor xor_40 (xor_40_out, or_26_out, xor_39_out);
  xor xor_41 (xor_41_out, and_55_out, xor_40_out);
  and and_65 (and_65_out, xor_55_out, and_76_out);
  xor xor_42 (xor_42_out, or_27_out, xor_41_out);
  and and_66 (and_66_out, or_29_out, xor_47_out);
  and and_67 (and_67_out, xor_46_out, and_78_out);
  or or_23 (or_23_out, and_67_out, and_66_out);
  and and_68 (and_68_out, B6, A2);
  and and_69 (and_69_out, or_30_out, xor_49_out);
  and and_70 (and_70_out, xor_48_out, and_68_out);
  or or_24 (or_24_out, and_70_out, and_69_out);
  and and_71 (and_71_out, B7, A1);
  xor xor_43 (xor_43_out, and_71_out, xor_50_out);
  and and_72 (and_72_out, and_80_out, xor_43_out);
  xor xor_44 (S[8], and_80_out, xor_43_out);
  LED led_8 (.in(S[8]));
  and and_73 (and_73_out, xor_51_out, and_83_out);
  or or_25 (or_25_out, and_73_out, and_84_out);
  and and_74 (and_74_out, xor_53_out, and_85_out);
  and and_75 (and_75_out, or_33_out, xor_54_out);
  or or_26 (or_26_out, and_74_out, and_75_out);
  and and_76 (and_76_out, B4, A4);
  xor xor_45 (xor_45_out, and_76_out, xor_55_out);
  and and_77 (and_77_out, or_28_out, xor_45_out);
  xor xor_46 (xor_46_out, or_28_out, xor_45_out);
  or or_27 (or_27_out, and_65_out, and_77_out);
  and and_78 (and_78_out, B5, A3);
  xor xor_47 (xor_47_out, and_78_out, xor_46_out);
  xor xor_48 (xor_48_out, or_29_out, xor_47_out);
  xor xor_49 (xor_49_out, and_68_out, xor_48_out);
  and and_79 (and_79_out, xor_63_out, and_90_out);
  xor xor_50 (xor_50_out, or_30_out, xor_49_out);
  and and_80 (and_80_out, and_92_out, xor_57_out);
  and and_81 (and_81_out, B1, A7);
  and and_82 (and_82_out, and_81_out, or_31_out);
  xor xor_51 (xor_51_out, and_81_out, or_31_out);
  and and_83 (and_83_out, B2, A6);
  xor xor_52 (xor_52_out, and_83_out, xor_51_out);
  and and_84 (and_84_out, or_32_out, xor_52_out);
  xor xor_53 (xor_53_out, or_32_out, xor_52_out);
  and and_85 (and_85_out, B3, A5);
  xor xor_54 (xor_54_out, and_85_out, xor_53_out);
  and and_86 (and_86_out, xor_67_out, and_96_out);
  xor xor_55 (xor_55_out, or_33_out, xor_54_out);
  and and_87 (and_87_out, xor_59_out, and_98_out);
  or or_28 (or_28_out, and_87_out, and_99_out);
  and and_88 (and_88_out, xor_61_out, and_100_out);
  and and_89 (and_89_out, or_36_out, xor_62_out);
  or or_29 (or_29_out, and_88_out, and_89_out);
  and and_90 (and_90_out, B6, A1);
  xor xor_56 (xor_56_out, and_90_out, xor_63_out);
  and and_91 (and_91_out, and_111_out, xor_56_out);
  xor xor_57 (xor_57_out, and_111_out, xor_56_out);
  or or_30 (or_30_out, and_79_out, and_91_out);
  and and_92 (and_92_out, B7, A0);
  xor xor_58 (S[7], and_92_out, xor_57_out);
  LED led_9 (.in(S[7]));
  and and_93 (and_93_out, and_112_out, and_102_out);
  or or_31 (or_31_out, and_93_out, and_103_out);
  and and_94 (and_94_out, xor_65_out, and_104_out);
  and and_95 (and_95_out, or_38_out, xor_66_out);
  or or_32 (or_32_out, and_94_out, and_95_out);
  and and_96 (and_96_out, B3, A4);
  and and_97 (and_97_out, or_34_out, xor_68_out);
  xor xor_59 (xor_59_out, or_34_out, xor_68_out);
  or or_33 (or_33_out, and_86_out, and_97_out);
  and and_98 (and_98_out, B4, A3);
  xor xor_60 (xor_60_out, and_98_out, xor_59_out);
  and and_99 (and_99_out, or_35_out, xor_60_out);
  xor xor_61 (xor_61_out, or_35_out, xor_60_out);
  and and_100 (and_100_out, B5, A2);
  xor xor_62 (xor_62_out, and_100_out, xor_61_out);
  and and_101 (and_101_out, xor_74_out, and_108_out);
  xor xor_63 (xor_63_out, or_36_out, xor_62_out);
  and and_102 (and_102_out, B1, A6);
  xor xor_64 (xor_64_out, and_102_out, and_112_out);
  and and_103 (and_103_out, or_37_out, xor_64_out);
  xor xor_65 (xor_65_out, or_37_out, xor_64_out);
  and and_104 (and_104_out, B2, A5);
  xor xor_66 (xor_66_out, and_104_out, xor_65_out);
  xor xor_67 (xor_67_out, or_38_out, xor_66_out);
  xor xor_68 (xor_68_out, and_96_out, xor_67_out);
  and and_105 (and_105_out, xor_79_out, and_118_out);
  or or_34 (or_34_out, and_105_out, and_119_out);
  and and_106 (and_106_out, xor_72_out, and_120_out);
  and and_107 (and_107_out, or_40_out, xor_73_out);
  or or_35 (or_35_out, and_106_out, and_107_out);
  and and_108 (and_108_out, B5, A1);
  and and_109 (and_109_out, and_130_out, xor_75_out);
  xor xor_69 (xor_69_out, and_130_out, xor_75_out);
  or or_36 (or_36_out, and_101_out, and_109_out);
  and and_110 (and_110_out, B6, A0);
  and and_111 (and_111_out, and_110_out, xor_69_out);
  xor xor_70 (S[6], and_110_out, xor_69_out);
  LED led_10 (.in(S[6]));
  and and_112 (and_112_out, B0, A7);
  and and_113 (and_113_out, and_121_out, and_122_out);
  and and_114 (and_114_out, or_41_out, xor_76_out);
  or or_37 (or_37_out, and_113_out, and_114_out);
  and and_115 (and_115_out, B2, A4);
  and and_116 (and_116_out, xor_77_out, and_115_out);
  and and_117 (and_117_out, or_42_out, xor_78_out);
  or or_38 (or_38_out, and_116_out, and_117_out);
  and and_118 (and_118_out, B3, A3);
  xor xor_71 (xor_71_out, and_118_out, xor_79_out);
  and and_119 (and_119_out, or_39_out, xor_71_out);
  xor xor_72 (xor_72_out, or_39_out, xor_71_out);
  and and_120 (and_120_out, B4, A2);
  xor xor_73 (xor_73_out, and_120_out, xor_72_out);
  xor xor_74 (xor_74_out, or_40_out, xor_73_out);
  xor xor_75 (xor_75_out, and_108_out, xor_74_out);
  and and_121 (and_121_out, B0, A6);
  and and_122 (and_122_out, B1, A5);
  xor xor_76 (xor_76_out, and_122_out, and_121_out);
  xor xor_77 (xor_77_out, or_41_out, xor_76_out);
  xor xor_78 (xor_78_out, and_115_out, xor_77_out);
  and and_123 (and_123_out, xor_88_out, and_133_out);
  xor xor_79 (xor_79_out, or_42_out, xor_78_out);
  and and_124 (and_124_out, xor_82_out, and_135_out);
  and and_125 (and_125_out, or_44_out, xor_83_out);
  or or_39 (or_39_out, and_124_out, and_125_out);
  and and_126 (and_126_out, B4, A1);
  and and_127 (and_127_out, xor_84_out, and_126_out);
  and and_128 (and_128_out, and_143_out, xor_85_out);
  or or_40 (or_40_out, and_127_out, and_128_out);
  and and_129 (and_129_out, B5, A0);
  and and_130 (and_130_out, and_129_out, xor_86_out);
  xor xor_80 (S[5], and_129_out, xor_86_out);
  LED led_11 (.in(S[5]));
  and and_131 (and_131_out, and_136_out, and_137_out);
  and and_132 (and_132_out, or_45_out, xor_87_out);
  or or_41 (or_41_out, and_131_out, and_132_out);
  and and_133 (and_133_out, B2, A3);
  xor xor_81 (xor_81_out, and_133_out, xor_88_out);
  and and_134 (and_134_out, or_43_out, xor_81_out);
  xor xor_82 (xor_82_out, or_43_out, xor_81_out);
  or or_42 (or_42_out, and_123_out, and_134_out);
  and and_135 (and_135_out, B3, A2);
  xor xor_83 (xor_83_out, and_135_out, xor_82_out);
  xor xor_84 (xor_84_out, or_44_out, xor_83_out);
  xor xor_85 (xor_85_out, and_126_out, xor_84_out);
  xor xor_86 (xor_86_out, and_143_out, xor_85_out);
  and and_136 (and_136_out, B0, A5);
  and and_137 (and_137_out, B1, A4);
  xor xor_87 (xor_87_out, and_137_out, and_136_out);
  and and_138 (and_138_out, and_149_out, and_144_out);
  xor xor_88 (xor_88_out, or_45_out, xor_87_out);
  and and_139 (and_139_out, xor_90_out, and_146_out);
  or or_43 (or_43_out, and_139_out, and_147_out);
  and and_140 (and_140_out, xor_92_out, and_148_out);
  and and_141 (and_141_out, and_154_out, xor_93_out);
  or or_44 (or_44_out, and_140_out, and_141_out);
  and and_142 (and_142_out, B4, A0);
  and and_143 (and_143_out, and_142_out, xor_94_out);
  xor xor_89 (S[4], and_142_out, xor_94_out);
  LED led_12 (.in(S[4]));
  and and_144 (and_144_out, B1, A3);
  and and_145 (and_145_out, or_46_out, xor_95_out);
  xor xor_90 (xor_90_out, or_46_out, xor_95_out);
  or or_45 (or_45_out, and_138_out, and_145_out);
  and and_146 (and_146_out, B2, A2);
  xor xor_91 (xor_91_out, and_146_out, xor_90_out);
  and and_147 (and_147_out, or_47_out, xor_91_out);
  xor xor_92 (xor_92_out, or_47_out, xor_91_out);
  and and_148 (and_148_out, B3, A1);
  xor xor_93 (xor_93_out, and_148_out, xor_92_out);
  xor xor_94 (xor_94_out, and_154_out, xor_93_out);
  and and_149 (and_149_out, B0, A4);
  xor xor_95 (xor_95_out, and_144_out, and_149_out);
  and and_150 (and_150_out, and_158_out, and_155_out);
  or or_46 (or_46_out, and_150_out, and_156_out);
  and and_151 (and_151_out, xor_97_out, and_157_out);
  and and_152 (and_152_out, and_162_out, xor_98_out);
  or or_47 (or_47_out, and_151_out, and_152_out);
  and and_153 (and_153_out, B3, A0);
  and and_154 (and_154_out, and_153_out, xor_99_out);
  and and_155 (and_155_out, B1, A2);
  xor xor_96 (xor_96_out, and_155_out, and_158_out);
  and and_156 (and_156_out, or_48_out, xor_96_out);
  xor xor_97 (xor_97_out, or_48_out, xor_96_out);
  and and_157 (and_157_out, B2, A1);
  xor xor_98 (xor_98_out, and_157_out, xor_97_out);
  xor xor_99 (xor_99_out, and_162_out, xor_98_out);
  xor xor_100 (S[3], and_153_out, xor_99_out);
  LED led_13 (.in(S[3]));
  and and_158 (and_158_out, B0, A3);
  and and_159 (and_159_out, and_163_out, and_164_out);
  and and_160 (and_160_out, and_166_out, xor_101_out);
  or or_48 (or_48_out, and_159_out, and_160_out);
  and and_161 (and_161_out, B2, A0);
  and and_162 (and_162_out, and_161_out, xor_102_out);
  and and_163 (and_163_out, B0, A2);
  and and_164 (and_164_out, B1, A1);
  xor xor_101 (xor_101_out, and_164_out, and_163_out);
  xor xor_102 (xor_102_out, and_166_out, xor_101_out);
  xor xor_103 (S[2], and_161_out, xor_102_out);
  LED led_14 (.in(S[2]));
  and and_165 (and_165_out, B1, A0);
  and and_166 (and_166_out, and_165_out, and_167_out);
  xor xor_104 (S[1], and_165_out, and_167_out);
  LED led_15 (.in(S[1]));
  and and_167 (and_167_out, B0, A1);
  and and_168 (S[0], B0, A0);
  LED led_16 (.in(S[0]));

  // Notes on the sheet:
  //   32768
  //   16384
  //   8192
  //   4096
  //   2048
  //   X
  //   =
  //   1024
  //   512
  //   256
  //   128
  //   64
  //   128
  //   32
  //   64
  //   16
  //   32
  //   16
  //   8
  //   8
  //   4
  //   4
  //   2
  //   2
  //   1
  //   1
  //   1
  //   2
  //   4
  //   8
  //   16
  //   32
  //   64
  //   128
endmodule

module multiplicador_8bits_sequencial (
  input  Carregar_Valores
);

  wire and_1_out, clock_1_out, comparator_1_eq, not_1_out, or_1_out, undriven, undriven_2, undriven_3,
       undriven_4;
  wire [3:0] multiplexer_3_out, register_4_q, subtractor_1_out;
  wire [7:0] multiplexer_2_out, register_3_q, shifter_2_out;
  wire [15:0] multiplexer_1_out, register_1_q, S, shifter_1_out, ula16add_1_c;

  Register #(.width(16)) register_1 (.D(multiplexer_1_out), .en(1'b1), .clk(and_1_out), .Q(register_1_q));  // open: clr
  Multiplexer #(.width(16)) multiplexer_1 (
    .in0(shifter_1_out), .in1(16'h2), .out(multiplexer_1_out), .sel(Carregar_Valores));
  // NoConnect on undriven
  // NoConnect on undriven_2
  // Probe on register_1_q
  Register #(.width(16)) register_2 (
    .D(ula16add_1_c), .en(register_3_q[0]), .clk(and_1_out), .Q(S), .clr(Carregar_Valores));
  Shifter #(.width(16)) shifter_1 (.in(register_1_q), .\dist (4'b0001), .out(shifter_1_out));
  ula16add ula16add_1 (.A(S), .B(register_1_q), .C(ula16add_1_c));
  Multiplexer #(.width(8)) multiplexer_2 (
    .in0(shifter_2_out), .in1(8'h12), .out(multiplexer_2_out), .sel(Carregar_Valores));
  // NoConnect on undriven_3
  // Probe on register_3_q
  Register register_3 (.D(multiplexer_2_out), .en(1'b1), .clk(and_1_out), .Q(register_3_q));  // open: clr
  Shifter #(.shift("lr")) shifter_2 (.in(register_3_q), .\dist (3'b001), .out(shifter_2_out));
  Multiplexer #(.width(4)) multiplexer_3 (
    .in0(subtractor_1_out), .in1(4'b1000), .out(multiplexer_3_out), .sel(Carregar_Valores));
  Register #(.width(4)) register_4 (.D(multiplexer_3_out), .en(1'b1), .clk(and_1_out), .Q(register_4_q));  // open: clr
  and and_1 (and_1_out, or_1_out, clock_1_out);
  // NoConnect on undriven_4
  // Probe on 16'h2
  // Probe on 8'h12
  // Probe on S
  or or_1 (or_1_out, not_1_out, Carregar_Valores);
  Clock clock_1 (.out(clock_1_out));
  Subtractor #(.width(4)) subtractor_1 (.a(register_4_q), .b(4'b0001), .out(subtractor_1_out));  // open: bin, bout
  not not_1 (not_1_out, comparator_1_eq);
  Comparator #(.width(4)) comparator_1 (.a(register_4_q), .b(4'b0000), .eq(comparator_1_eq));  // open: gt, lt

  // Notes on the sheet:
  //   Carregar valores: 
  //   1: Defina os valores nas constantes multiplicando e multiplicador
  //   2: Ative o sinal "carregar valores"
  //   3: De um pulso de "Clock"
  //   4: Desative o sinal "carregar valores"
  //   Para calcular o valor, de vários pulsos de clock até o sinal de controle virar 0
  //   INSTRUÇÕES
  //   Multiplicando
  //   Produto
  //   Multiplicador
  //   X
  //   =
  //   Clock
  //   Produto
  //   Controle
  //   Multiplicando
  //   Multiplicador
endmodule

module divisor_array_4bits (
  input  _1,
  input  in_2,
  input  D1,
  input  D0,
  input  in_5,
  input  d0_2
);

  wire multiplexer_2_out, multiplexer_4_out, multiplexer_5_out, multiplexer_7_out, multiplexer_8_out,
       multiplexer_10_out, subtrator_do_divisor_1_c_out, subtrator_do_divisor_1_s,
       subtrator_do_divisor_2_c_out, subtrator_do_divisor_2_s, subtrator_do_divisor_3_c_out,
       subtrator_do_divisor_3_s, subtrator_do_divisor_4_c_out, subtrator_do_divisor_4_s,
       subtrator_do_divisor_5_c_out, subtrator_do_divisor_5_s, subtrator_do_divisor_6_c_out,
       subtrator_do_divisor_6_s, subtrator_do_divisor_7_c_out, subtrator_do_divisor_7_s,
       subtrator_do_divisor_8_c_out, subtrator_do_divisor_8_s, subtrator_do_divisor_9_c_out,
       subtrator_do_divisor_9_s, subtrator_do_divisor_10_c_out, subtrator_do_divisor_10_s,
       subtrator_do_divisor_11_c_out, subtrator_do_divisor_11_s, subtrator_do_divisor_12_c_out,
       subtrator_do_divisor_12_s;
  wire [2:0] R;
  wire [3:0] S;

  not not_1 (S[3], subtrator_do_divisor_1_c_out);
  LED led_1 (.in(S[3]));
  subtrator_do_divisor subtrator_do_divisor_1 (
    .C_in(subtrator_do_divisor_2_c_out), .B(1'b0), .A(1'b0), .C_out(subtrator_do_divisor_1_c_out),
    .S(subtrator_do_divisor_1_s));
  Multiplexer multiplexer_1 (
    .in0(subtrator_do_divisor_1_s), .in1(1'b0), .sel(subtrator_do_divisor_1_c_out));  // open: out
  not not_2 (S[2], subtrator_do_divisor_3_c_out);
  LED led_2 (.in(S[2]));
  subtrator_do_divisor subtrator_do_divisor_2 (
    .C_in(subtrator_do_divisor_4_c_out), .B(in_5), .A(1'b0), .C_out(subtrator_do_divisor_2_c_out),
    .S(subtrator_do_divisor_2_s));
  Multiplexer multiplexer_2 (
    .in0(subtrator_do_divisor_2_s), .in1(1'b0), .out(multiplexer_2_out), .sel(subtrator_do_divisor_1_c_out));
  subtrator_do_divisor subtrator_do_divisor_3 (
    .C_in(subtrator_do_divisor_5_c_out), .B(1'b0), .A(multiplexer_2_out),
    .C_out(subtrator_do_divisor_3_c_out), .S(subtrator_do_divisor_3_s));
  Multiplexer multiplexer_3 (
    .in0(subtrator_do_divisor_3_s), .in1(multiplexer_2_out), .sel(subtrator_do_divisor_3_c_out));  // open: out
  not not_3 (S[1], subtrator_do_divisor_6_c_out);
  LED led_3 (.in(S[1]));
  subtrator_do_divisor subtrator_do_divisor_4 (
    .C_in(1'b0), .B(d0_2), .A(_1), .C_out(subtrator_do_divisor_4_c_out), .S(subtrator_do_divisor_4_s));
  Multiplexer multiplexer_4 (
    .in0(subtrator_do_divisor_4_s), .in1(_1), .out(multiplexer_4_out), .sel(subtrator_do_divisor_1_c_out));
  subtrator_do_divisor subtrator_do_divisor_5 (
    .C_in(subtrator_do_divisor_7_c_out), .B(in_5), .A(multiplexer_4_out),
    .C_out(subtrator_do_divisor_5_c_out), .S(subtrator_do_divisor_5_s));
  Multiplexer multiplexer_5 (
    .in0(subtrator_do_divisor_5_s), .in1(multiplexer_4_out), .out(multiplexer_5_out),
    .sel(subtrator_do_divisor_3_c_out));
  subtrator_do_divisor subtrator_do_divisor_6 (
    .C_in(subtrator_do_divisor_8_c_out), .B(1'b0), .A(multiplexer_5_out),
    .C_out(subtrator_do_divisor_6_c_out), .S(subtrator_do_divisor_6_s));
  Multiplexer multiplexer_6 (
    .in0(subtrator_do_divisor_6_s), .in1(multiplexer_5_out), .sel(subtrator_do_divisor_6_c_out));  // open: out
  subtrator_do_divisor subtrator_do_divisor_7 (
    .C_in(1'b0), .B(d0_2), .A(in_2), .C_out(subtrator_do_divisor_7_c_out), .S(subtrator_do_divisor_7_s));
  Multiplexer multiplexer_7 (
    .in0(subtrator_do_divisor_7_s), .in1(in_2), .out(multiplexer_7_out), .sel(subtrator_do_divisor_3_c_out));
  not not_4 (S[0], subtrator_do_divisor_9_c_out);
  LED led_4 (.in(S[0]));
  subtrator_do_divisor subtrator_do_divisor_8 (
    .C_in(subtrator_do_divisor_10_c_out), .B(in_5), .A(multiplexer_7_out),
    .C_out(subtrator_do_divisor_8_c_out), .S(subtrator_do_divisor_8_s));
  Multiplexer multiplexer_8 (
    .in0(subtrator_do_divisor_8_s), .in1(multiplexer_7_out), .out(multiplexer_8_out),
    .sel(subtrator_do_divisor_6_c_out));
  subtrator_do_divisor subtrator_do_divisor_9 (
    .C_in(subtrator_do_divisor_11_c_out), .B(1'b0), .A(multiplexer_8_out),
    .C_out(subtrator_do_divisor_9_c_out), .S(subtrator_do_divisor_9_s));
  Multiplexer multiplexer_9 (
    .in0(subtrator_do_divisor_9_s), .in1(multiplexer_8_out), .out(R[2]), .sel(subtrator_do_divisor_9_c_out));
  LED led_5 (.in(R[2]));
  subtrator_do_divisor subtrator_do_divisor_10 (
    .C_in(1'b0), .B(d0_2), .A(D1), .C_out(subtrator_do_divisor_10_c_out), .S(subtrator_do_divisor_10_s));
  Multiplexer multiplexer_10 (
    .in0(subtrator_do_divisor_10_s), .in1(D1), .out(multiplexer_10_out), .sel(subtrator_do_divisor_6_c_out));
  subtrator_do_divisor subtrator_do_divisor_11 (
    .C_in(subtrator_do_divisor_12_c_out), .B(in_5), .A(multiplexer_10_out),
    .C_out(subtrator_do_divisor_11_c_out), .S(subtrator_do_divisor_11_s));
  Multiplexer multiplexer_11 (
    .in0(subtrator_do_divisor_11_s), .in1(multiplexer_10_out), .out(R[1]), .sel(subtrator_do_divisor_9_c_out));
  LED led_6 (.in(R[1]));
  subtrator_do_divisor subtrator_do_divisor_12 (
    .C_in(1'b0), .B(d0_2), .A(D0), .C_out(subtrator_do_divisor_12_c_out), .S(subtrator_do_divisor_12_s));
  Multiplexer multiplexer_12 (
    .in0(subtrator_do_divisor_12_s), .in1(D0), .out(R[0]), .sel(subtrator_do_divisor_9_c_out));
  LED led_7 (.in(R[0]));
  // Probe on {_1, in_2, D1, D0}
  // Probe on {in_5, d0_2}
  // Probe on S
  // Probe on R

  // Other names for the same wires on the sheet: D2 = in_2; D3 = _1; d0_t = d0_2; d1_t = in_5

  // Notes on the sheet:
  //   2
  //   d1
  //   8
  //   D3
  //   4
  //   D2
  //   2
  //   1
  //   /
  //   %
  //   =
endmodule
module divisor_array_8bits (
  input  _1,
  input  D6,
  input  D5,
  input  D4,
  input  D3,
  input  D2,
  input  D1,
  input  D0,
  input  d3_2,
  input  in_10,
  input  d1_2,
  input  d0_2
);

  wire multiplexer_2_out, multiplexer_4_out, multiplexer_5_out, multiplexer_7_out, multiplexer_8_out,
       multiplexer_9_out, multiplexer_11_out, multiplexer_12_out, multiplexer_13_out, multiplexer_14_out,
       multiplexer_16_out, multiplexer_17_out, multiplexer_18_out, multiplexer_19_out, multiplexer_21_out,
       multiplexer_22_out, multiplexer_23_out, multiplexer_24_out, multiplexer_26_out, multiplexer_27_out,
       multiplexer_28_out, multiplexer_29_out, multiplexer_31_out, multiplexer_32_out, multiplexer_33_out,
       multiplexer_35_out, multiplexer_36_out, multiplexer_38_out, subtrator_do_divisor_1_c_out,
       subtrator_do_divisor_1_s, subtrator_do_divisor_2_c_out, subtrator_do_divisor_2_s,
       subtrator_do_divisor_3_c_out, subtrator_do_divisor_3_s, subtrator_do_divisor_4_c_out,
       subtrator_do_divisor_4_s, subtrator_do_divisor_5_c_out, subtrator_do_divisor_5_s,
       subtrator_do_divisor_6_c_out, subtrator_do_divisor_6_s, subtrator_do_divisor_7_c_out,
       subtrator_do_divisor_7_s, subtrator_do_divisor_8_c_out, subtrator_do_divisor_8_s,
       subtrator_do_divisor_9_c_out, subtrator_do_divisor_9_s, subtrator_do_divisor_10_c_out,
       subtrator_do_divisor_10_s, subtrator_do_divisor_11_c_out, subtrator_do_divisor_11_s,
       subtrator_do_divisor_12_c_out, subtrator_do_divisor_12_s, subtrator_do_divisor_13_c_out,
       subtrator_do_divisor_13_s, subtrator_do_divisor_14_c_out, subtrator_do_divisor_14_s,
       subtrator_do_divisor_15_c_out, subtrator_do_divisor_15_s, subtrator_do_divisor_16_c_out,
       subtrator_do_divisor_16_s, subtrator_do_divisor_17_c_out, subtrator_do_divisor_17_s,
       subtrator_do_divisor_18_c_out, subtrator_do_divisor_18_s, subtrator_do_divisor_19_c_out,
       subtrator_do_divisor_19_s, subtrator_do_divisor_20_c_out, subtrator_do_divisor_20_s,
       subtrator_do_divisor_21_c_out, subtrator_do_divisor_21_s, subtrator_do_divisor_22_c_out,
       subtrator_do_divisor_22_s, subtrator_do_divisor_23_c_out, subtrator_do_divisor_23_s,
       subtrator_do_divisor_24_c_out, subtrator_do_divisor_24_s, subtrator_do_divisor_25_c_out,
       subtrator_do_divisor_25_s, subtrator_do_divisor_26_c_out, subtrator_do_divisor_26_s,
       subtrator_do_divisor_27_c_out, subtrator_do_divisor_27_s, subtrator_do_divisor_28_c_out,
       subtrator_do_divisor_28_s, subtrator_do_divisor_29_c_out, subtrator_do_divisor_29_s,
       subtrator_do_divisor_30_c_out, subtrator_do_divisor_30_s, subtrator_do_divisor_31_c_out,
       subtrator_do_divisor_31_s, subtrator_do_divisor_32_c_out, subtrator_do_divisor_32_s,
       subtrator_do_divisor_33_c_out, subtrator_do_divisor_33_s, subtrator_do_divisor_34_c_out,
       subtrator_do_divisor_34_s, subtrator_do_divisor_35_c_out, subtrator_do_divisor_35_s,
       subtrator_do_divisor_36_c_out, subtrator_do_divisor_36_s, subtrator_do_divisor_37_c_out,
       subtrator_do_divisor_37_s, subtrator_do_divisor_38_c_out, subtrator_do_divisor_38_s,
       subtrator_do_divisor_39_c_out, subtrator_do_divisor_39_s, subtrator_do_divisor_40_c_out,
       subtrator_do_divisor_40_s;
  wire [4:0] R;
  wire [7:0] S;

  not not_1 (S[7], subtrator_do_divisor_1_c_out);
  LED led_1 (.in(S[7]));
  subtrator_do_divisor subtrator_do_divisor_1 (
    .C_in(subtrator_do_divisor_2_c_out), .B(1'b0), .A(1'b0), .C_out(subtrator_do_divisor_1_c_out),
    .S(subtrator_do_divisor_1_s));
  Multiplexer multiplexer_1 (
    .in0(subtrator_do_divisor_1_s), .in1(1'b0), .sel(subtrator_do_divisor_1_c_out));  // open: out
  subtrator_do_divisor subtrator_do_divisor_2 (
    .C_in(subtrator_do_divisor_4_c_out), .B(d3_2), .A(1'b0), .C_out(subtrator_do_divisor_2_c_out),
    .S(subtrator_do_divisor_2_s));
  Multiplexer multiplexer_2 (
    .in0(subtrator_do_divisor_2_s), .in1(1'b0), .out(multiplexer_2_out), .sel(subtrator_do_divisor_1_c_out));
  not not_2 (S[6], subtrator_do_divisor_3_c_out);
  LED led_2 (.in(S[6]));
  subtrator_do_divisor subtrator_do_divisor_3 (
    .C_in(subtrator_do_divisor_5_c_out), .B(1'b0), .A(multiplexer_2_out),
    .C_out(subtrator_do_divisor_3_c_out), .S(subtrator_do_divisor_3_s));
  Multiplexer multiplexer_3 (
    .in0(subtrator_do_divisor_3_s), .in1(multiplexer_2_out), .sel(subtrator_do_divisor_3_c_out));  // open: out
  not not_3 (S[5], subtrator_do_divisor_6_c_out);
  LED led_3 (.in(S[5]));
  subtrator_do_divisor subtrator_do_divisor_4 (
    .C_in(subtrator_do_divisor_7_c_out), .B(in_10), .A(1'b0), .C_out(subtrator_do_divisor_4_c_out),
    .S(subtrator_do_divisor_4_s));
  Multiplexer multiplexer_4 (
    .in0(subtrator_do_divisor_4_s), .in1(1'b0), .out(multiplexer_4_out), .sel(subtrator_do_divisor_1_c_out));
  subtrator_do_divisor subtrator_do_divisor_5 (
    .C_in(subtrator_do_divisor_8_c_out), .B(d3_2), .A(multiplexer_4_out),
    .C_out(subtrator_do_divisor_5_c_out), .S(subtrator_do_divisor_5_s));
  Multiplexer multiplexer_5 (
    .in0(subtrator_do_divisor_5_s), .in1(multiplexer_4_out), .out(multiplexer_5_out),
    .sel(subtrator_do_divisor_3_c_out));
  subtrator_do_divisor subtrator_do_divisor_6 (
    .C_in(subtrator_do_divisor_9_c_out), .B(1'b0), .A(multiplexer_5_out),
    .C_out(subtrator_do_divisor_6_c_out), .S(subtrator_do_divisor_6_s));
  Multiplexer multiplexer_6 (
    .in0(subtrator_do_divisor_6_s), .in1(multiplexer_5_out), .sel(subtrator_do_divisor_6_c_out));  // open: out
  not not_4 (S[4], subtrator_do_divisor_10_c_out);
  LED led_4 (.in(S[4]));
  subtrator_do_divisor subtrator_do_divisor_7 (
    .C_in(subtrator_do_divisor_11_c_out), .B(d1_2), .A(1'b0), .C_out(subtrator_do_divisor_7_c_out),
    .S(subtrator_do_divisor_7_s));
  Multiplexer multiplexer_7 (
    .in0(subtrator_do_divisor_7_s), .in1(1'b0), .out(multiplexer_7_out), .sel(subtrator_do_divisor_1_c_out));
  subtrator_do_divisor subtrator_do_divisor_8 (
    .C_in(subtrator_do_divisor_12_c_out), .B(in_10), .A(multiplexer_7_out),
    .C_out(subtrator_do_divisor_8_c_out), .S(subtrator_do_divisor_8_s));
  Multiplexer multiplexer_8 (
    .in0(subtrator_do_divisor_8_s), .in1(multiplexer_7_out), .out(multiplexer_8_out),
    .sel(subtrator_do_divisor_3_c_out));
  subtrator_do_divisor subtrator_do_divisor_9 (
    .C_in(subtrator_do_divisor_13_c_out), .B(d3_2), .A(multiplexer_8_out),
    .C_out(subtrator_do_divisor_9_c_out), .S(subtrator_do_divisor_9_s));
  Multiplexer multiplexer_9 (
    .in0(subtrator_do_divisor_9_s), .in1(multiplexer_8_out), .out(multiplexer_9_out),
    .sel(subtrator_do_divisor_6_c_out));
  subtrator_do_divisor subtrator_do_divisor_10 (
    .C_in(subtrator_do_divisor_14_c_out), .B(1'b0), .A(multiplexer_9_out),
    .C_out(subtrator_do_divisor_10_c_out), .S(subtrator_do_divisor_10_s));
  Multiplexer multiplexer_10 (
    .in0(subtrator_do_divisor_10_s), .in1(multiplexer_9_out), .sel(subtrator_do_divisor_10_c_out));  // open: out
  subtrator_do_divisor subtrator_do_divisor_11 (
    .C_in(1'b0), .B(d0_2), .A(_1), .C_out(subtrator_do_divisor_11_c_out), .S(subtrator_do_divisor_11_s));
  Multiplexer multiplexer_11 (
    .in0(subtrator_do_divisor_11_s), .in1(_1), .out(multiplexer_11_out), .sel(subtrator_do_divisor_1_c_out));
  subtrator_do_divisor subtrator_do_divisor_12 (
    .C_in(subtrator_do_divisor_16_c_out), .B(d1_2), .A(multiplexer_11_out),
    .C_out(subtrator_do_divisor_12_c_out), .S(subtrator_do_divisor_12_s));
  Multiplexer multiplexer_12 (
    .in0(subtrator_do_divisor_12_s), .in1(multiplexer_11_out), .out(multiplexer_12_out),
    .sel(subtrator_do_divisor_3_c_out));
  not not_5 (S[3], subtrator_do_divisor_15_c_out);
  LED led_5 (.in(S[3]));
  subtrator_do_divisor subtrator_do_divisor_13 (
    .C_in(subtrator_do_divisor_17_c_out), .B(in_10), .A(multiplexer_12_out),
    .C_out(subtrator_do_divisor_13_c_out), .S(subtrator_do_divisor_13_s));
  Multiplexer multiplexer_13 (
    .in0(subtrator_do_divisor_13_s), .in1(multiplexer_12_out), .out(multiplexer_13_out),
    .sel(subtrator_do_divisor_6_c_out));
  subtrator_do_divisor subtrator_do_divisor_14 (
    .C_in(subtrator_do_divisor_18_c_out), .B(d3_2), .A(multiplexer_13_out),
    .C_out(subtrator_do_divisor_14_c_out), .S(subtrator_do_divisor_14_s));
  Multiplexer multiplexer_14 (
    .in0(subtrator_do_divisor_14_s), .in1(multiplexer_13_out), .out(multiplexer_14_out),
    .sel(subtrator_do_divisor_10_c_out));
  subtrator_do_divisor subtrator_do_divisor_15 (
    .C_in(subtrator_do_divisor_19_c_out), .B(1'b0), .A(multiplexer_14_out),
    .C_out(subtrator_do_divisor_15_c_out), .S(subtrator_do_divisor_15_s));
  Multiplexer multiplexer_15 (
    .in0(subtrator_do_divisor_15_s), .in1(multiplexer_14_out), .sel(subtrator_do_divisor_15_c_out));  // open: out
  subtrator_do_divisor subtrator_do_divisor_16 (
    .C_in(1'b0), .B(d0_2), .A(D6), .C_out(subtrator_do_divisor_16_c_out), .S(subtrator_do_divisor_16_s));
  Multiplexer multiplexer_16 (
    .in0(subtrator_do_divisor_16_s), .in1(D6), .out(multiplexer_16_out), .sel(subtrator_do_divisor_3_c_out));
  subtrator_do_divisor subtrator_do_divisor_17 (
    .C_in(subtrator_do_divisor_21_c_out), .B(d1_2), .A(multiplexer_16_out),
    .C_out(subtrator_do_divisor_17_c_out), .S(subtrator_do_divisor_17_s));
  Multiplexer multiplexer_17 (
    .in0(subtrator_do_divisor_17_s), .in1(multiplexer_16_out), .out(multiplexer_17_out),
    .sel(subtrator_do_divisor_6_c_out));
  subtrator_do_divisor subtrator_do_divisor_18 (
    .C_in(subtrator_do_divisor_22_c_out), .B(in_10), .A(multiplexer_17_out),
    .C_out(subtrator_do_divisor_18_c_out), .S(subtrator_do_divisor_18_s));
  Multiplexer multiplexer_18 (
    .in0(subtrator_do_divisor_18_s), .in1(multiplexer_17_out), .out(multiplexer_18_out),
    .sel(subtrator_do_divisor_10_c_out));
  subtrator_do_divisor subtrator_do_divisor_19 (
    .C_in(subtrator_do_divisor_23_c_out), .B(d3_2), .A(multiplexer_18_out),
    .C_out(subtrator_do_divisor_19_c_out), .S(subtrator_do_divisor_19_s));
  Multiplexer multiplexer_19 (
    .in0(subtrator_do_divisor_19_s), .in1(multiplexer_18_out), .out(multiplexer_19_out),
    .sel(subtrator_do_divisor_15_c_out));
  not not_6 (S[2], subtrator_do_divisor_20_c_out);
  LED led_6 (.in(S[2]));
  subtrator_do_divisor subtrator_do_divisor_20 (
    .C_in(subtrator_do_divisor_24_c_out), .B(1'b0), .A(multiplexer_19_out),
    .C_out(subtrator_do_divisor_20_c_out), .S(subtrator_do_divisor_20_s));
  Multiplexer multiplexer_20 (
    .in0(subtrator_do_divisor_20_s), .in1(multiplexer_19_out), .sel(subtrator_do_divisor_20_c_out));  // open: out
  not not_7 (S[1], subtrator_do_divisor_25_c_out);
  LED led_7 (.in(S[1]));
  subtrator_do_divisor subtrator_do_divisor_21 (
    .C_in(1'b0), .B(d0_2), .A(D5), .C_out(subtrator_do_divisor_21_c_out), .S(subtrator_do_divisor_21_s));
  Multiplexer multiplexer_21 (
    .in0(subtrator_do_divisor_21_s), .in1(D5), .out(multiplexer_21_out), .sel(subtrator_do_divisor_6_c_out));
  subtrator_do_divisor subtrator_do_divisor_22 (
    .C_in(subtrator_do_divisor_26_c_out), .B(d1_2), .A(multiplexer_21_out),
    .C_out(subtrator_do_divisor_22_c_out), .S(subtrator_do_divisor_22_s));
  Multiplexer multiplexer_22 (
    .in0(subtrator_do_divisor_22_s), .in1(multiplexer_21_out), .out(multiplexer_22_out),
    .sel(subtrator_do_divisor_10_c_out));
  subtrator_do_divisor subtrator_do_divisor_23 (
    .C_in(subtrator_do_divisor_27_c_out), .B(in_10), .A(multiplexer_22_out),
    .C_out(subtrator_do_divisor_23_c_out), .S(subtrator_do_divisor_23_s));
  Multiplexer multiplexer_23 (
    .in0(subtrator_do_divisor_23_s), .in1(multiplexer_22_out), .out(multiplexer_23_out),
    .sel(subtrator_do_divisor_15_c_out));
  subtrator_do_divisor subtrator_do_divisor_24 (
    .C_in(subtrator_do_divisor_28_c_out), .B(d3_2), .A(multiplexer_23_out),
    .C_out(subtrator_do_divisor_24_c_out), .S(subtrator_do_divisor_24_s));
  Multiplexer multiplexer_24 (
    .in0(subtrator_do_divisor_24_s), .in1(multiplexer_23_out), .out(multiplexer_24_out),
    .sel(subtrator_do_divisor_20_c_out));
  subtrator_do_divisor subtrator_do_divisor_25 (
    .C_in(subtrator_do_divisor_29_c_out), .B(1'b0), .A(multiplexer_24_out),
    .C_out(subtrator_do_divisor_25_c_out), .S(subtrator_do_divisor_25_s));
  Multiplexer multiplexer_25 (
    .in0(subtrator_do_divisor_25_s), .in1(multiplexer_24_out), .sel(subtrator_do_divisor_25_c_out));  // open: out
  not not_8 (S[0], subtrator_do_divisor_30_c_out);
  LED led_8 (.in(S[0]));
  subtrator_do_divisor subtrator_do_divisor_26 (
    .C_in(1'b0), .B(d0_2), .A(D4), .C_out(subtrator_do_divisor_26_c_out), .S(subtrator_do_divisor_26_s));
  Multiplexer multiplexer_26 (
    .in0(subtrator_do_divisor_26_s), .in1(D4), .out(multiplexer_26_out), .sel(subtrator_do_divisor_10_c_out));
  subtrator_do_divisor subtrator_do_divisor_27 (
    .C_in(subtrator_do_divisor_31_c_out), .B(d1_2), .A(multiplexer_26_out),
    .C_out(subtrator_do_divisor_27_c_out), .S(subtrator_do_divisor_27_s));
  Multiplexer multiplexer_27 (
    .in0(subtrator_do_divisor_27_s), .in1(multiplexer_26_out), .out(multiplexer_27_out),
    .sel(subtrator_do_divisor_15_c_out));
  subtrator_do_divisor subtrator_do_divisor_28 (
    .C_in(subtrator_do_divisor_32_c_out), .B(in_10), .A(multiplexer_27_out),
    .C_out(subtrator_do_divisor_28_c_out), .S(subtrator_do_divisor_28_s));
  Multiplexer multiplexer_28 (
    .in0(subtrator_do_divisor_28_s), .in1(multiplexer_27_out), .out(multiplexer_28_out),
    .sel(subtrator_do_divisor_20_c_out));
  subtrator_do_divisor subtrator_do_divisor_29 (
    .C_in(subtrator_do_divisor_33_c_out), .B(d3_2), .A(multiplexer_28_out),
    .C_out(subtrator_do_divisor_29_c_out), .S(subtrator_do_divisor_29_s));
  Multiplexer multiplexer_29 (
    .in0(subtrator_do_divisor_29_s), .in1(multiplexer_28_out), .out(multiplexer_29_out),
    .sel(subtrator_do_divisor_25_c_out));
  subtrator_do_divisor subtrator_do_divisor_30 (
    .C_in(subtrator_do_divisor_34_c_out), .B(1'b0), .A(multiplexer_29_out),
    .C_out(subtrator_do_divisor_30_c_out), .S(subtrator_do_divisor_30_s));
  Multiplexer multiplexer_30 (
    .in0(subtrator_do_divisor_30_s), .in1(multiplexer_29_out), .out(R[4]), .sel(subtrator_do_divisor_30_c_out));
  LED led_9 (.in(R[4]));
  subtrator_do_divisor subtrator_do_divisor_31 (
    .C_in(1'b0), .B(d0_2), .A(D3), .C_out(subtrator_do_divisor_31_c_out), .S(subtrator_do_divisor_31_s));
  Multiplexer multiplexer_31 (
    .in0(subtrator_do_divisor_31_s), .in1(D3), .out(multiplexer_31_out), .sel(subtrator_do_divisor_15_c_out));
  subtrator_do_divisor subtrator_do_divisor_32 (
    .C_in(subtrator_do_divisor_35_c_out), .B(d1_2), .A(multiplexer_31_out),
    .C_out(subtrator_do_divisor_32_c_out), .S(subtrator_do_divisor_32_s));
  Multiplexer multiplexer_32 (
    .in0(subtrator_do_divisor_32_s), .in1(multiplexer_31_out), .out(multiplexer_32_out),
    .sel(subtrator_do_divisor_20_c_out));
  subtrator_do_divisor subtrator_do_divisor_33 (
    .C_in(subtrator_do_divisor_36_c_out), .B(in_10), .A(multiplexer_32_out),
    .C_out(subtrator_do_divisor_33_c_out), .S(subtrator_do_divisor_33_s));
  Multiplexer multiplexer_33 (
    .in0(subtrator_do_divisor_33_s), .in1(multiplexer_32_out), .out(multiplexer_33_out),
    .sel(subtrator_do_divisor_25_c_out));
  subtrator_do_divisor subtrator_do_divisor_34 (
    .C_in(subtrator_do_divisor_37_c_out), .B(d3_2), .A(multiplexer_33_out),
    .C_out(subtrator_do_divisor_34_c_out), .S(subtrator_do_divisor_34_s));
  Multiplexer multiplexer_34 (
    .in0(subtrator_do_divisor_34_s), .in1(multiplexer_33_out), .out(R[3]), .sel(subtrator_do_divisor_30_c_out));
  LED led_10 (.in(R[3]));
  subtrator_do_divisor subtrator_do_divisor_35 (
    .C_in(1'b0), .B(d0_2), .A(D2), .C_out(subtrator_do_divisor_35_c_out), .S(subtrator_do_divisor_35_s));
  Multiplexer multiplexer_35 (
    .in0(subtrator_do_divisor_35_s), .in1(D2), .out(multiplexer_35_out), .sel(subtrator_do_divisor_20_c_out));
  subtrator_do_divisor subtrator_do_divisor_36 (
    .C_in(subtrator_do_divisor_38_c_out), .B(d1_2), .A(multiplexer_35_out),
    .C_out(subtrator_do_divisor_36_c_out), .S(subtrator_do_divisor_36_s));
  Multiplexer multiplexer_36 (
    .in0(subtrator_do_divisor_36_s), .in1(multiplexer_35_out), .out(multiplexer_36_out),
    .sel(subtrator_do_divisor_25_c_out));
  subtrator_do_divisor subtrator_do_divisor_37 (
    .C_in(subtrator_do_divisor_39_c_out), .B(in_10), .A(multiplexer_36_out),
    .C_out(subtrator_do_divisor_37_c_out), .S(subtrator_do_divisor_37_s));
  Multiplexer multiplexer_37 (
    .in0(subtrator_do_divisor_37_s), .in1(multiplexer_36_out), .out(R[2]), .sel(subtrator_do_divisor_30_c_out));
  LED led_11 (.in(R[2]));
  subtrator_do_divisor subtrator_do_divisor_38 (
    .C_in(1'b0), .B(d0_2), .A(D1), .C_out(subtrator_do_divisor_38_c_out), .S(subtrator_do_divisor_38_s));
  Multiplexer multiplexer_38 (
    .in0(subtrator_do_divisor_38_s), .in1(D1), .out(multiplexer_38_out), .sel(subtrator_do_divisor_25_c_out));
  subtrator_do_divisor subtrator_do_divisor_39 (
    .C_in(subtrator_do_divisor_40_c_out), .B(d1_2), .A(multiplexer_38_out),
    .C_out(subtrator_do_divisor_39_c_out), .S(subtrator_do_divisor_39_s));
  Multiplexer multiplexer_39 (
    .in0(subtrator_do_divisor_39_s), .in1(multiplexer_38_out), .out(R[1]), .sel(subtrator_do_divisor_30_c_out));
  LED led_12 (.in(R[1]));
  subtrator_do_divisor subtrator_do_divisor_40 (
    .C_in(1'b0), .B(d0_2), .A(D0), .C_out(subtrator_do_divisor_40_c_out), .S(subtrator_do_divisor_40_s));
  Multiplexer multiplexer_40 (
    .in0(subtrator_do_divisor_40_s), .in1(D0), .out(R[0]), .sel(subtrator_do_divisor_30_c_out));
  LED led_13 (.in(R[0]));
  // Probe on {_1, D6, D5, D4, D3, D2, D1, D0}
  // Probe on {d3_2, in_10, d1_2, d0_2}
  // Probe on S
  // Probe on R

  // Other names for the same wires on the sheet: D7 = _1; d0_t = d0_2; d1_t = d1_2; d2_t = in_10; d3_t = d3_2

  // Notes on the sheet:
  //   128
  //   64
  //   8
  //   4
  //   d2
  //   32
  //   2
  //   16
  //   128
  //   D7
  //   8
  //   4
  //   64
  //   2
  //   32
  //   16
  //   1
  //   8
  //   4
  //   2
  //   1
  //   =
  //   X
  //   %
endmodule

module meio_somador_do_multiplicador (
  input  B,
  input  A,
  output C_out,
  output S
);

  and and_1 (C_out, A, B);
  xor xor_1 (S, B, A);

  // Notes on the sheet:
  //   *Componente criado apenas para simplificar a construção do multiplicador array
endmodule

module somador_do_multiplicador (
  input  C_in,
  input  B,
  input  A,
  output C_out,
  output S
);

  wire and_1_out, and_2_out, xor_1_out;

  and and_1 (and_1_out, B, A);
  and and_2 (and_2_out, C_in, xor_1_out);
  or or_1 (C_out, and_1_out, and_2_out);
  xor xor_1 (xor_1_out, B, A);
  xor xor_2 (S, C_in, xor_1_out);

  // Notes on the sheet:
  //   *Componente criado apenas para simplificar a construção do multiplicador array
endmodule

module subtrator_do_divisor (
  input  C_in,
  input  B,
  input  A,
  output C_out,
  output S
);

  wire and_1_out, and_2_out, not_1_out, not_2_out, xor_1_out;

  not not_1 (not_1_out, A);
  and and_1 (and_1_out, B, not_1_out);
  and and_2 (and_2_out, C_in, not_2_out);
  or or_1 (C_out, and_1_out, and_2_out);
  xor xor_1 (xor_1_out, B, A);
  not not_2 (not_2_out, xor_1_out);
  xor xor_2 (S, C_in, xor_1_out);

  // Notes on the sheet:
  //   *Componente criado apenas para simplificar a construção do divisor array
endmodule

module ula16add (
  input  [15:0] A,
  input  [15:0] B,
  output [15:0] C
);

  Adder #(.width(16)) adder_1 (.a(A), .b(B), .out(C));  // open: cin, cout

  // Notes on the sheet:
  //   *Componente criado apenas para simplificar a construção do multiplicador sequencial
endmodule

module teste (
  input  in_1,
  input  d0,
  input  in_3,
  input  in_4,
  input  in_5,
  input  in_6,
  input  in_7
);

  wire and_1_out, and_2_out, and_3_out, clock_1_out, multiplexer_5_out, multiplexer_7_out, multiplexer_8_out,
       multiplexer_10_out, multiplexer_11_out, multiplexer_12_out, multiplexer_13_out, multiplexer_14_out,
       multiplexer_15_out, not_1_out, not_2_out, not_3_out, not_4_out, not_5_out,
       subtrator_do_divisor_1_c_out, subtrator_do_divisor_1_s, subtrator_do_divisor_2_c_out,
       subtrator_do_divisor_2_s, subtrator_do_divisor_3_c_out, subtrator_do_divisor_3_s,
       subtrator_do_divisor_4_c_out, subtrator_do_divisor_4_s, subtrator_do_divisor_5_c_out,
       subtrator_do_divisor_5_s, subtrator_do_divisor_6_c_out, subtrator_do_divisor_6_s,
       subtrator_do_divisor_7_c_out, subtrator_do_divisor_7_s, subtrator_do_divisor_8_c_out,
       subtrator_do_divisor_8_s, subtrator_do_divisor_9_c_out, subtrator_do_divisor_9_s,
       subtrator_do_divisor_10_c_out, subtrator_do_divisor_10_s, subtrator_do_divisor_11_c_out,
       subtrator_do_divisor_11_s, subtrator_do_divisor_12_c_out, subtrator_do_divisor_12_s;
  wire [0:0] shifter_2_out;
  wire [7:0] register_3_q;
  wire [7:1] shifter_2_out_2;
  wire [15:0] adder_1_out, multiplexer_1_out, multiplexer_3_out, multiplexer_4_out, register_1_q,
       register_2_q, shifter_1_out, ula16sub_1_csub;

  Multiplexer #(.width(16)) multiplexer_1 (.in0(shifter_1_out), .in1(16'h20), .out(multiplexer_1_out), .sel(in_1));
  not not_1 (not_1_out, subtrator_do_divisor_1_c_out);
  and and_1 (and_1_out, register_2_q[15], 1'b1);
  subtrator_do_divisor subtrator_do_divisor_1 (
    .C_in(subtrator_do_divisor_2_c_out), .B(1'b0), .A(1'b0), .C_out(subtrator_do_divisor_1_c_out),
    .S(subtrator_do_divisor_1_s));
  Multiplexer multiplexer_2 (
    .in0(subtrator_do_divisor_1_s), .in1(1'b0), .sel(subtrator_do_divisor_1_c_out));  // open: out
  Register #(.width(16)) register_1 (
    .D(multiplexer_1_out), .en(and_1_out), .clk(clock_1_out), .Q(register_1_q));  // open: clr
  Multiplexer #(.width(16)) multiplexer_3 (
    .in0(ula16sub_1_csub), .in1(adder_1_out), .out(multiplexer_3_out), .sel(not_4_out));
  Multiplexer #(.width(16)) multiplexer_4 (.in0(multiplexer_3_out), .in1(16'h7), .out(multiplexer_4_out), .sel(in_1));
  not not_2 (not_2_out, subtrator_do_divisor_3_c_out);
  ula16sub ula16sub_1 (.A(register_2_q), .B(register_1_q), .Csub(ula16sub_1_csub));  // open: Cadd
  Register #(.width(16)) register_2 (
    .D(multiplexer_4_out), .en(and_2_out), .clk(clock_1_out), .Q(register_2_q));  // open: clr
  buf and_2 (and_2_out, 1'b1);  // AND_Gate
  subtrator_do_divisor subtrator_do_divisor_2 (
    .C_in(subtrator_do_divisor_4_c_out), .B(in_6), .A(1'b0), .C_out(subtrator_do_divisor_2_c_out),
    .S(subtrator_do_divisor_2_s));
  Multiplexer multiplexer_5 (
    .in0(subtrator_do_divisor_2_s), .in1(1'b0), .out(multiplexer_5_out), .sel(subtrator_do_divisor_1_c_out));
  subtrator_do_divisor subtrator_do_divisor_3 (
    .C_in(subtrator_do_divisor_5_c_out), .B(1'b0), .A(multiplexer_5_out),
    .C_out(subtrator_do_divisor_3_c_out), .S(subtrator_do_divisor_3_s));
  Multiplexer multiplexer_6 (
    .in0(subtrator_do_divisor_3_s), .in1(multiplexer_5_out), .sel(subtrator_do_divisor_3_c_out));  // open: out
  Adder #(.width(16)) adder_1 (.a(register_2_q), .b(register_1_q), .out(adder_1_out));  // open: cin, cout
  subtrator_do_divisor subtrator_do_divisor_4 (
    .C_in(1'b0), .B(in_7), .A(d0), .C_out(subtrator_do_divisor_4_c_out), .S(subtrator_do_divisor_4_s));
  Multiplexer multiplexer_7 (
    .in0(subtrator_do_divisor_4_s), .in1(d0), .out(multiplexer_7_out), .sel(subtrator_do_divisor_1_c_out));
  subtrator_do_divisor subtrator_do_divisor_5 (
    .C_in(subtrator_do_divisor_7_c_out), .B(in_6), .A(multiplexer_7_out),
    .C_out(subtrator_do_divisor_5_c_out), .S(subtrator_do_divisor_5_s));
  Multiplexer multiplexer_8 (
    .in0(subtrator_do_divisor_5_s), .in1(multiplexer_7_out), .out(multiplexer_8_out),
    .sel(subtrator_do_divisor_3_c_out));
  not not_3 (not_3_out, subtrator_do_divisor_6_c_out);
  Shifter #(.shift("lr"), .width(16)) shifter_1 (.in(register_1_q), .\dist (4'b0001), .out(shifter_1_out));
  not not_4 (not_4_out, register_2_q[15]);
  subtrator_do_divisor subtrator_do_divisor_6 (
    .C_in(subtrator_do_divisor_8_c_out), .B(1'b0), .A(multiplexer_8_out),
    .C_out(subtrator_do_divisor_6_c_out), .S(subtrator_do_divisor_6_s));
  Multiplexer multiplexer_9 (
    .in0(subtrator_do_divisor_6_s), .in1(multiplexer_8_out), .sel(subtrator_do_divisor_6_c_out));  // open: out
  not not_5 (not_5_out, subtrator_do_divisor_9_c_out);
  subtrator_do_divisor subtrator_do_divisor_7 (
    .C_in(1'b0), .B(in_7), .A(in_3), .C_out(subtrator_do_divisor_7_c_out), .S(subtrator_do_divisor_7_s));
  Multiplexer multiplexer_10 (
    .in0(subtrator_do_divisor_7_s), .in1(in_3), .out(multiplexer_10_out), .sel(subtrator_do_divisor_3_c_out));
  subtrator_do_divisor subtrator_do_divisor_8 (
    .C_in(subtrator_do_divisor_10_c_out), .B(in_6), .A(multiplexer_10_out),
    .C_out(subtrator_do_divisor_8_c_out), .S(subtrator_do_divisor_8_s));
  Multiplexer multiplexer_11 (
    .in0(subtrator_do_divisor_8_s), .in1(multiplexer_10_out), .out(multiplexer_11_out),
    .sel(subtrator_do_divisor_6_c_out));
  subtrator_do_divisor subtrator_do_divisor_9 (
    .C_in(subtrator_do_divisor_11_c_out), .B(1'b0), .A(multiplexer_11_out),
    .C_out(subtrator_do_divisor_9_c_out), .S(subtrator_do_divisor_9_s));
  Multiplexer multiplexer_12 (
    .in0(subtrator_do_divisor_9_s), .in1(multiplexer_11_out), .out(multiplexer_12_out),
    .sel(subtrator_do_divisor_9_c_out));
  Clock clock_1 (.out(clock_1_out));
  Register register_3 (.D({shifter_2_out_2, 1'b1}), .en(and_3_out), .clk(clock_1_out), .Q(register_3_q));  // open: clr
  buf and_3 (and_3_out, 1'b1);  // AND_Gate
  subtrator_do_divisor subtrator_do_divisor_10 (
    .C_in(1'b0), .B(in_7), .A(in_4), .C_out(subtrator_do_divisor_10_c_out), .S(subtrator_do_divisor_10_s));
  Multiplexer multiplexer_13 (
    .in0(subtrator_do_divisor_10_s), .in1(in_4), .out(multiplexer_13_out), .sel(subtrator_do_divisor_6_c_out));
  subtrator_do_divisor subtrator_do_divisor_11 (
    .C_in(subtrator_do_divisor_12_c_out), .B(in_6), .A(multiplexer_13_out),
    .C_out(subtrator_do_divisor_11_c_out), .S(subtrator_do_divisor_11_s));
  Multiplexer multiplexer_14 (
    .in0(subtrator_do_divisor_11_s), .in1(multiplexer_13_out), .out(multiplexer_14_out),
    .sel(subtrator_do_divisor_9_c_out));
  subtrator_do_divisor subtrator_do_divisor_12 (
    .C_in(1'b0), .B(in_7), .A(in_5), .C_out(subtrator_do_divisor_12_c_out), .S(subtrator_do_divisor_12_s));
  Multiplexer multiplexer_15 (
    .in0(subtrator_do_divisor_12_s), .in1(in_5), .out(multiplexer_15_out), .sel(subtrator_do_divisor_9_c_out));
  Shifter shifter_2 (.in(register_3_q), .\dist (3'b001), .out({shifter_2_out_2, shifter_2_out[0]}));

  // Notes on the sheet:
  //   d1
  //   D3
  //   D2
  //   D1
  //   D0
endmodule

module ula16sub (
  input  [15:0] A,
  input  [15:0] B,
  output [15:0] Csub,
  output [15:0] Cadd
);

  Subtractor #(.width(16)) subtractor_1 (.a(A), .b(B), .out(Csub));  // open: bin, bout
  Adder #(.width(16)) adder_1 (.a(A), .b(B), .out(Cadd));  // open: cin, cout

  // Notes on the sheet:
  //   *Componente criado apenas para simplificar a construção do multiplicador sequencial
endmodule
