// Logisim project encoders.circ as structural Verilog: 3 circuits, main circuit decodificador
module decodificador (
  input  _2,
  input  _1,
  input  _8,
  input  _4,
  input  _2_2,
  input  _1_2,
  input  _8_2,
  input  _4_2,
  input  _2_3,
  input  _1_3,
  input  _8_3,
  input  _4_3,
  input  _2_4,
  input  _1_4
);

  wire and_1_out, and_2_out, and_3_out, and_4_out, and_5_out, and_6_out, and_7_out, and_8_out, and_9_out,
       and_10_out, and_11_out, and_12_out, and_13_out, and_14_out, and_15_out, and_16_out, and_17_out,
       and_18_out, and_19_out, and_20_out, and_21_out, and_22_out, and_23_out, and_24_out, and_25_out,
       and_26_out, and_27_out, and_28_out, and_29_out, and_30_out, and_31_out, and_32_out, and_33_out,
       and_34_out, and_35_out, and_36_out, and_37_out, and_38_out, and_39_out, and_40_out, and_41_out,
       and_42_out, and_43_out, and_44_out, and_45_out, and_46_out, and_47_out, and_48_out, and_49_out,
       and_50_out, and_51_out, and_52_out, and_53_out, and_54_out, and_55_out, and_56_out, and_57_out,
       and_58_out, and_59_out, and_60_out, and_61_out, and_62_out, and_63_out, and_64_out, and_65_out,
       and_66_out, and_67_out, and_68_out, and_69_out, and_70_out, and_71_out, and_72_out, and_73_out,
       not_1_out, not_2_out, not_3_out, not_4_out, not_5_out, not_6_out, not_7_out, not_8_out, not_9_out,
       not_10_out, not_11_out, not_12_out, not_13_out, not_14_out, or_1_out, or_2_out, or_3_out, or_4_out,
       or_5_out, or_6_out, or_7_out, or_8_out, or_9_out, or_10_out, or_11_out, or_12_out, or_13_out,
       or_14_out, or_15_out, or_16_out, or_17_out, or_18_out, or_19_out;

  not not_1 (not_1_out, _8_3);
  not not_2 (not_2_out, _4_3);
  not not_3 (not_3_out, _2);
  not not_4 (not_4_out, _1);
  not not_5 (not_5_out, _8);
  not not_6 (not_6_out, _4);
  not not_7 (not_7_out, _2_2);
  not not_8 (not_8_out, _8_2);
  not not_9 (not_9_out, _4_2);
  not not_10 (not_10_out, _2_3);
  not not_11 (not_11_out, _2_4);
  not not_12 (not_12_out, _1_4);
  and and_1 (and_1_out, not_4_out, not_3_out);
  and and_2 (and_2_out, _1, not_3_out);
  and and_3 (and_3_out, not_4_out, _2);
  and and_4 (and_4_out, _1, _2);
  not not_13 (not_13_out, _1_2);
  not not_14 (not_14_out, _1_3);
  or or_1 (or_1_out, _8_3, _2_4);
  or or_2 (or_2_out, or_1_out, and_5_out);
  and and_5 (and_5_out, _4_3, _1_4);
  and and_6 (and_6_out, not_2_out, not_12_out);
  or or_3 (or_3_out, not_2_out, and_7_out);
  and and_7 (and_7_out, not_11_out, not_12_out);
  and and_8 (and_8_out, _2_4, _1_4);
  or or_4 (or_4_out, _4_3, not_11_out);
  or or_5 (or_5_out, or_4_out, _1_4);
  or or_6 (or_6_out, _8_3, and_9_out);
  and and_9 (and_9_out, not_2_out, not_12_out);
  and and_10 (and_10_out, not_2_out, _2_4);
  and and_11 (and_11_out, _2_4, not_12_out);
  and and_12 (and_12_out, _4_3, not_11_out);
  and and_13 (and_13_out, and_12_out, _1_4);
  and and_14 (and_14_out, not_2_out, not_12_out);
  or or_7 (or_7_out, and_14_out, and_15_out);
  and and_15 (and_15_out, _2_4, not_12_out);
  or or_8 (or_8_out, _8_3, and_16_out);
  and and_16 (and_16_out, not_11_out, not_12_out);
  and and_17 (and_17_out, _4_3, not_11_out);
  and and_18 (and_18_out, _4_3, not_12_out);
  or or_9 (or_9_out, _8_3, and_19_out);
  and and_19 (and_19_out, _4_3, not_11_out);
  and and_20 (and_20_out, not_2_out, _2_4);
  and and_21 (and_21_out, _2_4, not_12_out);
  LED led_1 (.in(and_1_out));
  LED led_2 (.in(and_2_out));
  LED led_3 (.in(and_3_out));
  LED led_4 (.in(and_4_out));
  and and_22 (and_22_out, not_13_out, not_7_out);
  and and_23 (and_23_out, and_22_out, and_24_out);
  and and_24 (and_24_out, not_6_out, not_5_out);
  and and_25 (and_25_out, _1_2, not_7_out);
  and and_26 (and_26_out, and_25_out, and_27_out);
  and and_27 (and_27_out, not_6_out, not_5_out);
  and and_28 (and_28_out, not_13_out, _2_2);
  and and_29 (and_29_out, and_28_out, not_6_out);
  and and_30 (and_30_out, _1_2, _2_2);
  and and_31 (and_31_out, and_30_out, not_6_out);
  and and_32 (and_32_out, not_13_out, not_7_out);
  and and_33 (and_33_out, and_32_out, _4);
  and and_34 (and_34_out, _1_2, not_7_out);
  and and_35 (and_35_out, and_34_out, _4);
  and and_36 (and_36_out, not_13_out, _2_2);
  and and_37 (and_37_out, and_36_out, _4);
  and and_38 (and_38_out, _1_2, _2_2);
  and and_39 (and_39_out, and_38_out, _4);
  and and_40 (and_40_out, not_13_out, _8);
  and and_41 (and_41_out, _1_2, _8);
  and and_42 (and_42_out, not_14_out, not_10_out);
  and and_43 (and_43_out, and_42_out, and_44_out);
  and and_44 (and_44_out, not_9_out, not_8_out);
  and and_45 (and_45_out, _1_3, not_10_out);
  and and_46 (and_46_out, and_45_out, and_47_out);
  and and_47 (and_47_out, not_9_out, not_8_out);
  and and_48 (and_48_out, not_14_out, _2_3);
  and and_49 (and_49_out, and_48_out, and_50_out);
  and and_50 (and_50_out, not_9_out, not_8_out);
  and and_51 (and_51_out, _1_3, _2_3);
  and and_52 (and_52_out, and_51_out, and_53_out);
  and and_53 (and_53_out, not_9_out, not_8_out);
  and and_54 (and_54_out, not_14_out, not_10_out);
  and and_55 (and_55_out, and_54_out, and_56_out);
  and and_56 (and_56_out, _4_2, not_8_out);
  and and_57 (and_57_out, _1_3, not_10_out);
  and and_58 (and_58_out, and_57_out, and_59_out);
  and and_59 (and_59_out, _4_2, not_8_out);
  and and_60 (and_60_out, not_14_out, _2_3);
  and and_61 (and_61_out, and_60_out, and_62_out);
  and and_62 (and_62_out, _4_2, not_8_out);
  and and_63 (and_63_out, _1_3, _2_3);
  and and_64 (and_64_out, and_63_out, and_65_out);
  and and_65 (and_65_out, _4_2, not_8_out);
  and and_66 (and_66_out, not_14_out, not_10_out);
  and and_67 (and_67_out, and_66_out, and_68_out);
  and and_68 (and_68_out, not_9_out, _8_2);
  and and_69 (and_69_out, _1_3, not_10_out);
  and and_70 (and_70_out, and_69_out, and_71_out);
  and and_71 (and_71_out, not_9_out, _8_2);
  and and_72 (and_72_out, _8_2, _2_3);
  or or_10 (or_10_out, and_72_out, and_73_out);
  and and_73 (and_73_out, _8_2, _4_2);
  or or_11 (or_11_out, or_2_out, and_6_out);
  or or_12 (or_12_out, or_3_out, and_8_out);
  or or_13 (or_13_out, or_6_out, and_10_out);
  or or_14 (or_14_out, or_13_out, and_11_out);
  or or_15 (or_15_out, or_8_out, and_17_out);
  or or_16 (or_16_out, or_15_out, and_18_out);
  or or_17 (or_17_out, or_9_out, and_20_out);
  or or_18 (or_18_out, or_17_out, and_21_out);
  or or_19 (or_19_out, or_14_out, and_13_out);
  LED led_5 (.in(and_23_out));
  LED led_6 (.in(and_26_out));
  LED led_7 (.in(and_29_out));
  LED led_8 (.in(and_31_out));
  LED led_9 (.in(and_33_out));
  LED led_10 (.in(and_35_out));
  LED led_11 (.in(and_37_out));
  LED led_12 (.in(and_39_out));
  LED led_13 (.in(and_40_out));
  LED led_14 (.in(and_41_out));
  LED led_15 (.in(and_43_out));
  LED led_16 (.in(and_46_out));
  LED led_17 (.in(and_49_out));
  LED led_18 (.in(and_52_out));
  LED led_19 (.in(and_55_out));
  LED led_20 (.in(and_58_out));
  LED led_21 (.in(and_61_out));
  LED led_22 (.in(and_64_out));
  LED led_23 (.in(and_67_out));
  LED led_24 (.in(and_70_out));
  LED led_25 (.in(or_10_out));
  _7_Segment_Display u_7_segment_display_1 (
    .g(or_18_out), .f(or_16_out), .a(or_11_out), .b(or_12_out), .e(or_7_out), .d(or_19_out), .c(or_5_out));  // open: dp

  // Notes on the sheet:
  //   Decodificador 2/4
  //   Decodificador BCD
  //   Decodificador BCD com pino de erro
  //   Decodificador para display de 7 segmentos
  //   0
  //   1
  //   2
  //   3
  //   A
  //   B
  //   C
  //   D
  //   E
  //   F
  //   G
  //   0
  //   1
  //   2
  //   3
  //   4
  //   5
  //   6
  //   7
  //   8
  //   9
  //   0
  //   1
  //   2
  //   3
  //   4
  //   5
  //   6
  //   7
  //   8
  //   9
  //   Erro
endmodule

module codificador (
  input  _0,
  input  _1,
  input  _2,
  input  _3,
  input  _1_2,
  input  _2_2,
  input  _3_2,
  input  _4,
  input  _5,
  input  _6,
  input  _7,
  input  _8,
  input  _9
);

  wire or_1_out, or_2_out, or_3_out, or_4_out, or_5_out, or_6_out, or_7_out, or_8_out, or_9_out, or_10_out,
       or_11_out, or_12_out, or_13_out;

  or or_1 (or_1_out, _1, _3);
  or or_2 (or_2_out, _2, _3);
  LED led_1 (.in(or_1_out));
  LED led_2 (.in(or_2_out));
  or or_3 (or_3_out, _1_2, _3_2);
  or or_4 (or_4_out, _2_2, _3_2);
  or or_5 (or_5_out, _6, _7);
  or or_6 (or_6_out, _4, _5);
  or or_7 (or_7_out, _6, _7);
  or or_8 (or_8_out, _8, _9);
  or or_9 (or_9_out, or_3_out, _5);
  or or_10 (or_10_out, _7, _9);
  or or_11 (or_11_out, or_4_out, or_5_out);
  or or_12 (or_12_out, or_6_out, or_7_out);
  or or_13 (or_13_out, or_9_out, or_10_out);
  LED led_3 (.in(or_13_out));
  LED led_4 (.in(or_11_out));
  LED led_5 (.in(or_12_out));
  LED led_6 (.in(or_8_out));

  // Notes on the sheet:
  //   Codificador 4/2
  //   Codificador BCD
  //   1
  //   2
  //   1
  //   2
  //   4
  //   8
endmodule

module codificador_decodificador (
  input  _1,
  input  _2,
  input  _3,
  input  _4,
  input  _5,
  input  _6,
  input  _7,
  input  _8,
  input  _9
);

  wire and_1_out, and_2_out, and_3_out, and_4_out, and_5_out, and_6_out, and_7_out, and_8_out, and_9_out,
       and_10_out, and_11_out, and_12_out, and_13_out, and_14_out, and_15_out, and_16_out, and_17_out,
       not_1_out, not_2_out, not_3_out, not_4_out, or_1_out, or_2_out, or_3_out, or_4_out, or_5_out,
       or_6_out, or_7_out, or_8_out, or_9_out, or_10_out, or_11_out, or_12_out, or_13_out, or_14_out,
       or_15_out, or_16_out, or_17_out, or_18_out, or_19_out, or_20_out, or_21_out, or_22_out, or_23_out,
       or_24_out, or_25_out, or_26_out, or_27_out, or_28_out, or_29_out;

  or or_1 (or_1_out, _1, _3);
  or or_2 (or_2_out, or_1_out, _5);
  or or_3 (or_3_out, _7, _9);
  or or_4 (or_4_out, _2, _3);
  or or_5 (or_5_out, or_4_out, or_6_out);
  or or_6 (or_6_out, _6, _7);
  or or_7 (or_7_out, _4, _5);
  or or_8 (or_8_out, or_7_out, or_9_out);
  or or_9 (or_9_out, _6, _7);
  or or_10 (or_10_out, _8, _9);
  or or_11 (or_11_out, or_2_out, or_3_out);
  LED led_1 (.in(or_10_out));
  LED led_2 (.in(or_8_out));
  LED led_3 (.in(or_5_out));
  not not_1 (not_1_out, or_10_out);
  LED led_4 (.in(or_11_out));
  not not_2 (not_2_out, or_8_out);
  not not_3 (not_3_out, or_5_out);
  not not_4 (not_4_out, or_11_out);
  or or_12 (or_12_out, or_10_out, or_5_out);
  and and_1 (and_1_out, or_8_out, or_11_out);
  and and_2 (and_2_out, not_2_out, not_4_out);
  and and_3 (and_3_out, not_3_out, not_4_out);
  and and_4 (and_4_out, or_5_out, or_11_out);
  or or_13 (or_13_out, or_8_out, not_3_out);
  and and_5 (and_5_out, not_2_out, not_4_out);
  and and_6 (and_6_out, not_2_out, or_5_out);
  and and_7 (and_7_out, or_5_out, not_4_out);
  and and_8 (and_8_out, or_8_out, not_3_out);
  and and_9 (and_9_out, not_2_out, not_4_out);
  and and_10 (and_10_out, or_5_out, not_4_out);
  and and_11 (and_11_out, not_3_out, not_4_out);
  and and_12 (and_12_out, or_8_out, not_3_out);
  and and_13 (and_13_out, or_8_out, not_4_out);
  and and_14 (and_14_out, or_8_out, not_3_out);
  and and_15 (and_15_out, not_2_out, or_5_out);
  and and_16 (and_16_out, or_5_out, not_4_out);
  or or_14 (or_14_out, or_12_out, and_1_out);
  or or_15 (or_15_out, or_14_out, and_2_out);
  or or_16 (or_16_out, not_2_out, and_3_out);
  or or_17 (or_17_out, or_16_out, and_4_out);
  or or_18 (or_18_out, or_13_out, or_11_out);
  or or_19 (or_19_out, or_10_out, and_5_out);
  or or_20 (or_20_out, or_19_out, and_6_out);
  and and_17 (and_17_out, and_8_out, or_11_out);
  or or_21 (or_21_out, and_9_out, and_10_out);
  or or_22 (or_22_out, or_10_out, and_11_out);
  or or_23 (or_23_out, or_22_out, and_12_out);
  or or_24 (or_24_out, or_10_out, and_14_out);
  or or_25 (or_25_out, or_24_out, and_15_out);
  or or_26 (or_26_out, or_20_out, and_7_out);
  or or_27 (or_27_out, or_26_out, and_17_out);
  or or_28 (or_28_out, or_23_out, and_13_out);
  or or_29 (or_29_out, or_25_out, and_16_out);
  _7_Segment_Display u_7_segment_display_1 (
    .g(or_29_out), .f(or_28_out), .a(or_15_out), .b(or_17_out), .e(or_21_out), .d(or_27_out), .c(or_18_out));  // open: dp

  // Notes on the sheet:
  //   8
  //   4
  //   2
  //   1
  //   Pin_A = (~bit3⋅~bit1)+bit2+(bit3⋅bit1)+bit4
  //   Pin_B = ~bit3+(~bit2⋅~bit1)+(bit2⋅bit1)
  //   Pin_C = ~bit2+bit1+bit3
  //   Pin_D = (~bit3⋅~bit1)+(~bit3⋅bit2)+(bit3⋅~bit2⋅bit1)+(bit2⋅~bit1)+bit4
  //   Pin_E = (~bit3⋅~bit1)+(bit2⋅~bit1)
  //   Pin_F = (~bit2⋅~bit1)+(bit3⋅~bit2)+(bit3⋅~bit1)+bit4
  //   Pin_G = (~bit3⋅bit2)+(bit3⋅~bit2)+bit4+(bit2⋅~bit1)
  //   A
  //   B
  //   C
  //   D
  //   E
  //   F
  //   G
endmodule
