// Logisim project equivalencias_NAND_NOR.circ as structural Verilog: 2 circuits, main circuit Quadro_NAND
module Quadro_NAND (
  input  in_1,
  input  in_2,
  input  in_3,
  input  in_4,
  input  in_5,
  input  in_6,
  input  in_7,
  input  in_8,
  input  in_9,
  input  in_10,
  input  in_11,
  input  in_12,
  input  in_13,
  input  in_14,
  input  in_15,
  input  in_16,
  input  in_17,
  input  in_18,
  input  in_19,
  input  in_20,
  input  in_21,
  input  in_22,
  input  in_23,
  input  in_24,
  input  in_25,
  input  in_26,
  input  in_27,
  input  in_28,
  input  in_29,
  input  in_30
);

  wire and_1_out, nand_1_out, nand_2_out, nand_3_out, nand_4_out, nand_5_out, nand_6_out, nand_7_out,
       nand_8_out, nand_9_out, nand_10_out, nand_11_out, nand_12_out, nand_13_out, nand_14_out, nand_15_out,
       nand_16_out, nand_17_out, nand_18_out, nand_19_out, nand_20_out, nand_21_out, nand_22_out,
       nand_23_out, nand_24_out, nand_25_out, nand_26_out, nand_27_out, nand_28_out, nand_29_out,
       nand_30_out, nor_1_out, nor_2_out, not_1_out, not_2_out, not_3_out, not_4_out, or_1_out, xnor_1_out,
       xor_1_out;

  not not_1 (not_1_out, in_6);
  LED led_1 (.in(not_1_out));
  nand nand_1 (nand_1_out, in_8, in_8);
  LED led_2 (.in(nand_1_out));
  or or_1 (or_1_out, in_11, in_13);
  LED led_3 (.in(or_1_out));
  nand nand_2 (nand_2_out, in_15, in_15);
  nand nand_3 (nand_3_out, in_17, in_17);
  xor xor_1 (xor_1_out, in_19, in_21);
  nand nand_4 (nand_4_out, in_23, in_25);
  nand nand_5 (nand_5_out, in_30, in_30);
  nand nand_6 (nand_6_out, in_28, in_28);
  nand nand_7 (nand_7_out, nand_2_out, nand_3_out);
  LED led_4 (.in(nand_7_out));
  LED led_5 (.in(xor_1_out));
  nand nand_8 (nand_8_out, in_23, nand_4_out);
  nand nand_9 (nand_9_out, nand_4_out, in_25);
  nand nand_10 (nand_10_out, in_28, nand_5_out);
  nand nand_11 (nand_11_out, nand_6_out, in_30);
  nand nand_12 (nand_12_out, nand_8_out, nand_9_out);
  LED led_6 (.in(nand_12_out));
  nand nand_13 (nand_13_out, nand_10_out, nand_11_out);
  LED led_7 (.in(nand_13_out));
  not not_2 (not_2_out, in_3);
  not not_3 (not_3_out, in_4);
  nand nand_14 (nand_14_out, in_1, in_2);
  nor nor_1 (nor_1_out, not_2_out, not_3_out);
  LED led_8 (.in(nand_14_out));
  not not_4 (not_4_out, nor_1_out);
  LED led_9 (.in(not_4_out));
  xnor xnor_1 (xnor_1_out, in_20, in_22);
  nand nand_15 (nand_15_out, in_24, in_26);
  and and_1 (and_1_out, in_5, in_7);
  LED led_10 (.in(and_1_out));
  nand nand_16 (nand_16_out, in_9, in_10);
  nor nor_2 (nor_2_out, in_12, in_14);
  LED led_11 (.in(nor_2_out));
  nand nand_17 (nand_17_out, in_16, in_16);
  nand nand_18 (nand_18_out, in_18, in_18);
  nand nand_19 (nand_19_out, in_24, nand_15_out);
  nand nand_20 (nand_20_out, nand_15_out, in_26);
  nand nand_21 (nand_21_out, in_27, in_27);
  nand nand_22 (nand_22_out, in_29, in_29);
  nand nand_23 (nand_23_out, in_27, in_29);
  nand nand_24 (nand_24_out, nand_16_out, nand_16_out);
  LED led_12 (.in(nand_24_out));
  nand nand_25 (nand_25_out, nand_17_out, nand_18_out);
  LED led_13 (.in(xnor_1_out));
  nand nand_26 (nand_26_out, nand_19_out, nand_20_out);
  nand nand_27 (nand_27_out, nand_21_out, nand_22_out);
  nand nand_28 (nand_28_out, nand_25_out, nand_25_out);
  LED led_14 (.in(nand_28_out));
  nand nand_29 (nand_29_out, nand_26_out, nand_26_out);
  LED led_15 (.in(nand_29_out));
  nand nand_30 (nand_30_out, nand_27_out, nand_23_out);
  LED led_16 (.in(nand_30_out));

  // Notes on the sheet:
  //   NOT
  //   OR
  //   XOR -> (A^(~B)) v ((~A)^B)
  //   A
  //   0
  //   0
  //   1
  //   1
  //   A
  //   0
  //   0
  //   1
  //   1
  //   NAND a partir da NOR
  //   A
  //   1
  //   0
  //   B
  //   0
  //   1
  //   0
  //   1
  //   B
  //   0
  //   1
  //   0
  //   1
  //   ~A
  //   0
  //   1
  //   AvB
  //   0
  //   1
  //   1
  //   1
  //   A⊕B
  //   0
  //   1
  //   1
  //   0
  //   Portas lógicas contruídas a partir da NAND
  //   NAND
  //   A
  //   0
  //   0
  //   1
  //   1
  //   B
  //   0
  //   1
  //   0
  //   1
  //   ~(A^B)
  //   1
  //   1
  //   1
  //   0
  //   AND
  //   NOR
  //   XNOR -> ((~A)^(~B)) v (A^B)
  //   A
  //   0
  //   0
  //   1
  //   1
  //   A
  //   0
  //   0
  //   1
  //   1
  //   A
  //   0
  //   0
  //   1
  //   1
  //   B
  //   0
  //   1
  //   0
  //   1
  //   B
  //   0
  //   1
  //   0
  //   1
  //   B
  //   0
  //   1
  //   0
  //   1
  //   A^B
  //   0
  //   0
  //   0
  //   1
  //   ~(AvB)
  //   1
  //   0
  //   0
  //   0
  //   ~(AvB)
  //   1
  //   0
  //   0
  //   0
endmodule

module Quadro_NOR (
  input  in_1,
  input  in_2,
  input  in_3,
  input  in_4,
  input  in_5,
  input  in_6,
  input  in_7,
  input  in_8,
  input  in_9,
  input  in_10,
  input  in_11,
  input  in_12,
  input  in_13,
  input  in_14,
  input  in_15,
  input  in_16,
  input  in_17,
  input  in_18,
  input  in_19,
  input  in_20,
  input  in_21,
  input  in_22,
  input  in_23,
  input  in_24,
  input  in_25,
  input  in_26,
  input  in_27,
  input  in_28,
  input  in_29,
  input  in_30
);

  wire and_1_out, nand_1_out, nand_2_out, nor_1_out, nor_2_out, nor_3_out, nor_4_out, nor_5_out, nor_6_out,
       nor_7_out, nor_8_out, nor_9_out, nor_10_out, nor_11_out, nor_12_out, nor_13_out, nor_14_out,
       nor_15_out, nor_16_out, nor_17_out, nor_18_out, nor_19_out, nor_20_out, nor_21_out, nor_22_out,
       nor_23_out, nor_24_out, nor_25_out, nor_26_out, nor_27_out, nor_28_out, nor_29_out, nor_30_out,
       not_1_out, not_2_out, not_3_out, not_4_out, or_1_out, xnor_1_out, xor_1_out;

  xor xor_1 (xor_1_out, in_19, in_21);
  nor nor_1 (nor_1_out, in_24, in_26);
  not not_1 (not_1_out, in_6);
  LED led_1 (.in(not_1_out));
  nor nor_2 (nor_2_out, in_8, in_8);
  LED led_2 (.in(nor_2_out));
  or or_1 (or_1_out, in_11, in_13);
  LED led_3 (.in(or_1_out));
  nor nor_3 (nor_3_out, in_16, in_17);
  nor nor_4 (nor_4_out, in_24, nor_1_out);
  nor nor_5 (nor_5_out, nor_1_out, in_26);
  nor nor_6 (nor_6_out, in_27, in_27);
  nor nor_7 (nor_7_out, in_29, in_29);
  nor nor_8 (nor_8_out, in_27, in_29);
  nor nor_9 (nor_9_out, nor_3_out, nor_3_out);
  LED led_4 (.in(nor_9_out));
  LED led_5 (.in(xor_1_out));
  nor nor_10 (nor_10_out, nor_4_out, nor_5_out);
  nor nor_11 (nor_11_out, nor_6_out, nor_7_out);
  nor nor_12 (nor_12_out, nor_10_out, nor_10_out);
  nor nor_13 (nor_13_out, nor_11_out, nor_8_out);
  LED led_6 (.in(nor_13_out));
  LED led_7 (.in(nor_12_out));
  not not_2 (not_2_out, in_3);
  not not_3 (not_3_out, in_4);
  nor nor_14 (nor_14_out, in_1, in_2);
  nand nand_1 (nand_1_out, not_2_out, not_3_out);
  LED led_8 (.in(nor_14_out));
  not not_4 (not_4_out, nand_1_out);
  LED led_9 (.in(not_4_out));
  xnor xnor_1 (xnor_1_out, in_20, in_22);
  nor nor_15 (nor_15_out, in_23, in_25);
  nor nor_16 (nor_16_out, in_30, in_30);
  nor nor_17 (nor_17_out, in_28, in_28);
  and and_1 (and_1_out, in_5, in_7);
  LED led_10 (.in(and_1_out));
  nor nor_18 (nor_18_out, in_9, in_9);
  nor nor_19 (nor_19_out, in_10, in_10);
  nand nand_2 (nand_2_out, in_12, in_14);
  LED led_11 (.in(nand_2_out));
  nor nor_20 (nor_20_out, in_15, in_15);
  nor nor_21 (nor_21_out, in_18, in_18);
  nor nor_22 (nor_22_out, in_23, nor_15_out);
  nor nor_23 (nor_23_out, nor_15_out, in_25);
  nor nor_24 (nor_24_out, in_28, nor_16_out);
  nor nor_25 (nor_25_out, nor_17_out, in_30);
  nor nor_26 (nor_26_out, nor_18_out, nor_19_out);
  LED led_12 (.in(nor_26_out));
  nor nor_27 (nor_27_out, nor_20_out, nor_21_out);
  LED led_13 (.in(xnor_1_out));
  nor nor_28 (nor_28_out, nor_22_out, nor_23_out);
  nor nor_29 (nor_29_out, nor_24_out, nor_25_out);
  nor nor_30 (nor_30_out, nor_27_out, nor_27_out);
  LED led_14 (.in(nor_30_out));
  LED led_15 (.in(nor_28_out));
  LED led_16 (.in(nor_29_out));

  // Notes on the sheet:
  //   NOT
  //   OR
  //   XOR -> (A^(~B)) v ((~A)^B)
  //   A
  //   0
  //   0
  //   1
  //   1
  //   A
  //   0
  //   0
  //   1
  //   1
  //   NOR a partir da NAND
  //   A
  //   1
  //   0
  //   B
  //   0
  //   1
  //   0
  //   1
  //   B
  //   0
  //   1
  //   0
  //   1
  //   ~A
  //   0
  //   1
  //   AvB
  //   0
  //   1
  //   1
  //   1
  //   A⊕B
  //   0
  //   1
  //   1
  //   0
  //   Portas lógicas contruídas a partir da NOR
  //   NOR
  //   A
  //   0
  //   0
  //   1
  //   1
  //   B
  //   0
  //   1
  //   0
  //   1
  //   ~(AvB)
  //   1
  //   0
  //   0
  //   0
  //   AND
  //   NAND
  //   XNOR -> ((~A)^(~B)) v (A^B)
  //   A
  //   0
  //   0
  //   1
  //   1
  //   A
  //   0
  //   0
  //   1
  //   1
  //   A
  //   0
  //   0
  //   1
  //   1
  //   B
  //   0
  //   1
  //   0
  //   1
  //   B
  //   0
  //   1
  //   0
  //   1
  //   B
  //   0
  //   1
  //   0
  //   1
  //   A^B
  //   0
  //   0
  //   0
  //   1
  //   ~(A^B)
  //   1
  //   1
  //   1
  //   0
  //   ~(AvB)
  //   1
  //   0
  //   0
  //   0
endmodule
