// Logisim project flipflops.circ as structural Verilog: 2 circuits, main circuit main
module main (
  input  S,
  input  S_2,
  input  S_3,
  input  R,
  input  S_4,
  input  Enable,
  input  R_2,
  input  S_5,
  input  Enable_2,
  input  R_3,
  input  S_6,
  input  Enable_3,
  input  R_4,
  input  Preset_input,
  input  Enable_4,
  input  K,
  input  Preset_input_2,
  input  Enable_5,
  input  D,
  input  Enable_6,
  input  D_2,
  input  Enable_7
);

  wire and_1_out, and_2_out, and_3_out, and_4_out, and_5_out, and_6_out, buffer_1_out, buffer_2_out,
       buffer_3_out, buffer_4_out, buffer_5_out, buffer_6_out, buffer_7_out, buffer_8_out, buffer_9_out,
       button_1_out, button_2_out, button_3_out, button_4_out, button_5_out, button_6_out, button_7_out,
       button_8_out, nand_1_out, nand_2_out, nand_3_out, nand_4_out, nand_5_out, nand_6_out, nand_7_out,
       nand_8_out, nand_9_out, nand_10_out, nand_11_out, nand_12_out, nand_13_out, nand_14_out, nand_15_out,
       nand_16_out, nand_17_out, nand_18_out, nand_19_out, nand_20_out, nand_21_out, nand_22_out,
       nand_23_out, nand_24_out, nand_25_out, nand_26_out, nand_27_out, nand_28_out, nand_29_out,
       nand_30_out, nand_31_out, nand_32_out, nand_33_out, nand_34_out, nand_35_out, nand_36_out,
       nand_37_out, nand_38_out, nand_39_out, nand_40_out, nand_41_out, nand_42_out, nand_43_out,
       nand_44_out, nand_45_out, nand_46_out, not_1_out, not_2_out, not_3_out, not_4_out, not_5_out,
       not_6_out, not_7_out, not_8_out, not_9_out, not_10_out, not_11_out, not_12_out, not_13_out,
       not_14_out, not_15_out, not_16_out, not_17_out, not_18_out, not_19_out, not_20_out, or_1_out,
       poweror_1_out_2, poweror_2_out_2, poweror_3_out_2, poweror_4_out_2, switch_1_p1, switch_1_p2;

  // Switch switch_1: pin names not known; wires that end beside it: switch_1_p1, switch_1_p2
  Pull_Resistor pull_resistor_1 (.node(switch_1_p2));
  or or_1 (or_1_out, S, or_1_out);
  or or_2 (switch_1_p1, S_2, switch_1_p2);
  not not_1 (not_1_out, S_5);
  and and_1 (and_1_out, not_1_out, R_3);
  buf buffer_1 (buffer_1_out, Enable_3);
  buf buffer_2 (buffer_2_out, buffer_1_out);
  buf buffer_3 (buffer_3_out, Enable_4);
  buf buffer_4 (buffer_4_out, buffer_3_out);
  buf buffer_5 (buffer_5_out, Enable_5);
  buf buffer_6 (buffer_6_out, buffer_5_out);
  not not_2 (not_2_out, D);
  Button button_1 (.out(button_1_out));
  Button button_2 (.out(button_2_out));
  nand nand_1 (nand_1_out, S_3, nand_2_out);
  nand nand_2 (nand_2_out, nand_1_out, R);
  nand nand_3 (nand_3_out, S_4, Enable);
  nand nand_4 (nand_4_out, Enable, R_2);
  nand nand_5 (nand_5_out, S_5, Enable_2);
  nand nand_6 (nand_6_out, Enable_2, and_1_out);
  Button button_3 (.out(button_3_out));
  PowerOR poweror_1 (.in_1(button_3_out), .out_2(poweror_1_out_2));
  and and_2 (and_2_out, S_6, Enable_3);
  buf buffer_7 (buffer_7_out, buffer_2_out);
  not not_3 (not_3_out, buffer_7_out);
  and and_3 (and_3_out, Enable_3, R_4);
  Button button_4 (.out(button_4_out));
  Button button_5 (.out(button_5_out));
  PowerOR poweror_2 (.in_1(button_5_out), .out_2(poweror_2_out_2));
  and and_4 (and_4_out, Preset_input, Enable_4);
  buf buffer_8 (buffer_8_out, buffer_4_out);
  not not_4 (not_4_out, buffer_8_out);
  and and_5 (and_5_out, Enable_4, K);
  Button button_6 (.out(button_6_out));
  Button button_7 (.out(button_7_out));
  PowerOR poweror_3 (.in_1(button_7_out), .out_2(poweror_3_out_2));
  and and_6 (and_6_out, Preset_input_2, Enable_5);
  buf buffer_9 (buffer_9_out, buffer_6_out);
  not not_5 (not_5_out, buffer_9_out);
  Button button_8 (.out(button_8_out));
  nand nand_7 (nand_7_out, D, Enable_6);
  nand nand_8 (nand_8_out, Enable_6, not_2_out);
  PowerOR poweror_4 (.in_1(button_1_out), .out_2(poweror_4_out_2));
  not not_6 (not_6_out, Enable_7);
  not not_7 (not_7_out, D_2);
  LED led_1 (.in(nand_1_out));
  LED led_2 (.in(nand_2_out));
  nand nand_9 (nand_9_out, nand_3_out, nand_10_out);
  nand nand_10 (nand_10_out, nand_9_out, nand_4_out);
  nand nand_11 (nand_11_out, nand_5_out, nand_12_out);
  nand nand_12 (nand_12_out, nand_11_out, nand_6_out);
  not not_8 (not_8_out, poweror_1_out_2);
  nand nand_13 (nand_13_out, and_2_out, not_3_out);
  nand nand_14 (nand_14_out, not_3_out, and_3_out);
  not not_9 (not_9_out, button_4_out);
  not not_10 (not_10_out, poweror_2_out_2);
  nand nand_15 (nand_15_out, nand_44_out, and_4_out, not_4_out);
  nand nand_16 (nand_16_out, not_4_out, and_5_out, nand_43_out);
  not not_11 (not_11_out, button_6_out);
  not not_12 (not_12_out, poweror_4_out_2);
  nand nand_17 (nand_17_out, D_2, not_6_out);
  nand nand_18 (nand_18_out, not_6_out, not_7_out);
  not not_13 (not_13_out, button_2_out);
  LED led_3 (.in(nand_9_out));
  LED led_4 (.in(nand_10_out));
  LED led_5 (.in(nand_11_out));
  LED led_6 (.in(nand_12_out));
  not not_14 (not_14_out, poweror_3_out_2);
  nand nand_19 (nand_19_out, nand_46_out, and_6_out, not_5_out);
  nand nand_20 (nand_20_out, not_5_out, and_6_out, nand_45_out);
  not not_15 (not_15_out, button_8_out);
  nand nand_21 (nand_21_out, nand_7_out, nand_22_out);
  LED led_7 (.in(nand_21_out));
  nand nand_22 (nand_22_out, nand_21_out, nand_8_out);
  LED led_8 (.in(nand_22_out));
  nand nand_23 (nand_23_out, not_12_out, nand_17_out, nand_24_out);
  nand nand_24 (nand_24_out, nand_23_out, nand_18_out, not_13_out);
  nand nand_25 (nand_25_out, not_8_out, nand_13_out, nand_26_out);
  nand nand_26 (nand_26_out, nand_25_out, nand_14_out, not_9_out);
  nand nand_27 (nand_27_out, not_10_out, nand_15_out, nand_28_out);
  nand nand_28 (nand_28_out, nand_27_out, nand_16_out, not_11_out);
  nand nand_29 (nand_29_out, not_14_out, nand_19_out, nand_30_out);
  nand nand_30 (nand_30_out, nand_29_out, nand_20_out, not_15_out);
  not not_16 (not_16_out, not_6_out);
  not not_17 (not_17_out, nand_23_out);
  not not_18 (not_18_out, not_3_out);
  not not_19 (not_19_out, not_4_out);
  not not_20 (not_20_out, not_5_out);
  nand nand_31 (nand_31_out, nand_23_out, not_16_out);
  nand nand_32 (nand_32_out, not_16_out, not_17_out);
  nand nand_33 (nand_33_out, not_9_out, nand_25_out, not_18_out);
  nand nand_34 (nand_34_out, not_18_out, nand_26_out, not_8_out);
  nand nand_35 (nand_35_out, not_11_out, nand_27_out, not_19_out);
  nand nand_36 (nand_36_out, not_19_out, nand_28_out, not_10_out);
  nand nand_37 (nand_37_out, not_15_out, nand_29_out, not_20_out);
  nand nand_38 (nand_38_out, not_20_out, nand_30_out, not_14_out);
  nand nand_39 (nand_39_out, not_12_out, nand_31_out, nand_40_out);
  nand nand_40 (nand_40_out, nand_39_out, nand_32_out, not_13_out);
  nand nand_41 (nand_41_out, not_8_out, nand_33_out, nand_42_out);
  nand nand_42 (nand_42_out, nand_41_out, nand_34_out, not_9_out);
  nand nand_43 (nand_43_out, not_10_out, nand_35_out, nand_44_out);
  nand nand_44 (nand_44_out, nand_43_out, nand_36_out, not_11_out);
  nand nand_45 (nand_45_out, not_14_out, nand_37_out, nand_46_out);
  nand nand_46 (nand_46_out, nand_45_out, nand_38_out, not_15_out);
  LED led_9 (.in(nand_39_out));
  LED led_10 (.in(nand_40_out));
  LED led_11 (.in(nand_41_out));
  LED led_12 (.in(nand_42_out));
  LED led_13 (.in(nand_43_out));
  LED led_14 (.in(nand_44_out));
  LED led_15 (.in(nand_45_out));
  LED led_16 (.in(nand_46_out));

  // Notes on the sheet:
  //   S_4: initial=0x1
  //   S_5: initial=0x1
  //   Enable: initial=0x1
  //   S_6: initial=0x1
  //   D: initial=0x1
  //   Enable_6: initial=0x1
  //   Enable_2: initial=0x1
  //   Aqui é introduzido o conceito de circuitos sequenciais. Nos circuitos combinacionais, as saídas são definidas apenas pelos seus valores de entrada, duas entradas '1' em
  //   uma XOR sempre terá uma saída '0', independente de onde ou quando isso for feito.
  //   Circuitos que usam Latches ou Flip-Flops são chamados circuitos sequenciais, que diferentemente dos circuitos combinacionais, que só dependem das entradas do
  //   momento, circuitos sequenciais também dependem de estados passados para definirem seu estado atual.
  //   Esse comportamento adiciona de certa forma o conceito de "memória" aos circuitos.
  //   "S" Latch
  //   Esse Latch tem pouca utilidade prática, mas apresenta bem a ideia de um "loop" no circuito, causando uma "trava" (latch) do seu estado.
  //   Ele possúi apenas dois estados "estáveis", quando a entrada 'S' é 0, então sua saída 'A' fica em 0, e quando sua entrada 'S' é setada para 1, sua saída 'A' trava em 1.
  //   Ele parece estar em desacordo com a idéia de acrescentar o conceito de memória aos circuitos, visto que após ser setado para um  uma vez, não tem uma forma de
  //    retornar seu estado incial, entretanto, na verdade esse latch tem a capacidade de "lembrar" se a sua entrada 'S' foi setada para 1 em algum momento do passado.
  //   Por conta de algumas limitações do motor de simulação do Logisim, podemos encontrar erros quando tentamos simular  circuitos com "Latches", portanto é comum
  //   o Logisim apresentar fios vermelhos sinalizando erro, as vezes precisamos fazer alguams modificações para contornar essas limitações.
  //   Para facilitar a interação com esse Latch, foi feito a versão abaixo com um interruptor para "cortar" o fio para que o estado da trava seja resetado, e um resistor de
  //   ajuste para corrigir o estado indefinido do interruptor quando ele está desligado evitando a saída com erro.
  //   Latch SR NAND
  //   Esse Latch demonstra a sua capacidade de "lembrar" quando ele tem suas duas entradas, 'S' e 'R'  maracadas como 1, mantendo armazenado o estado anterior.
  //   Latch SR com enable
  //   Esse Latch tem comportamento similar ao SR normal, mas adiciona um sinal de controle. Esse sinal de controle serve para  controlar quando uma mudança pode
  //    acontecer nas saidas do Latch, se o sinal de controle estiver desativado, nenhuma mudança ocorre nas saidas, independente das entradas S e R. As saídas ficam
  //   travadas/memorizadas enquanto o sinal de 'Enable' estiver baixo.
  //   Caso voce acione o estado inválido e a simulação travar, basta alterar as entradas para um estádo válido, ir no menu do  logisim "simular", "desabilitar simulação" e
  //    "habilitar simulação".
  //   Latch SR com enable e correção da oscilação
  //   Aqui foi acrescentada uma porta AND que impede das entradas S e R estarem ativadas ao mesmo tempo.
  //   Flip-flop SR
  //   A principal diferença de Latches e Flip-flops é que os Flip-flops são sensíveis a borda, enquanto os Latches são sensíveis a nível.
  //   Ou seja, enquanto os Latches SR mudam sua saida ENQUANTO o sinal de enable está ativo, os Flip-flops anteral suas saídas  apenas na borda de subída do enable.
  //   Caso voce acione o estado inválido e a simulação travar, basta alterar as entradas para um estádo válido, ir no menu do
  //    logisim "simular", "desabilitar simulação" e "habilitar simulação".
  //   Um exemplo de uso do Flip-flop SR é em circuitos de controle simples, mantendo o estado de ativação de um sistema, como o controle de portas automáticas
  //   Flip-Flop JK
  //   O Flip-flop JK resolver o problema do estado indeterminado do Flip-flop SR.
  //   Aqui, caso as entradas J e K estiverem ativas no momento da subida de borda do enable, o estado das saídas do Flip-flop se invertem.
  //   Um exemplo de uso do Flip-flop JK é como registradores de controle, usado em sistemas onde o estado precisa alternar ou ser forçado a um valor específico.
  //   Flip-Flop T
  //   O comportamento do Flip-flop T é de quando sua entrada estiver ativa, ele se comporta como o Flip-flop JK quando suas duas entradas estão ativas.
  //   Um exemplo de uso do Flip-flop T é como um divisor de frequência para um relógio digital, onde cada flip-flop T divide a frequência do clock de entrada por 2.
  //   Latch D
  //   O comportamento desse latch é travar as saídas como estiverem no momento em que o o sinal de enable se torna baixo, aqui o comportamento de "trava" fica bem evidente.
  //   Flip-flop D
  //   Tem o mesmo comportamento do Latch D, mas a mudança das saídas ocorre na borda de subída do enable.
  //   Um uso muito comum para os Flip-flops D é como buffers de dados.
  //    (aberta ou fechada).
  //   J
  //   T
  //   Preset input
  //   Clear input
  //   A
  //   Q
  //   A
  //   Q
  //   Preset input
  //   Clear input
  //   Clear input
  //   Clear input
  //   Latches e Flip-Flops
  //   Q
  //   ~Q
  //   S
  //   0
  //   0
  //   1
  //   1
  //   R
  //   0
  //   1
  //   0
  //   1
  //   Q
  //   0
  //   ~Q
  //   Q
  //   ~Q
  //   Q
  //   ~Q
  //   Q
  //   1
  //   1
  //   0
  //   Mantém o
  //   estado anterior
  //   Enable
  //   S
  //   X
  //   1
  //   0
  //   1
  //   0
  //   1
  //   1
  //   1
  //   1
  //   Enable
  //   S
  //   0
  //   X
  //   1
  //   0
  //   1
  //   0
  //   1
  //   1
  //   1
  //   1
  //   Enable
  //   0
  //   0
  //   1
  //   1
  //   ~Q
  //   1
  //   0
  //   1
  //   Mantém o
  //   estado anterior
  //   R
  //   X
  //   0
  //   1
  //   0
  //   1
  //   R
  //   X
  //   0
  //   1
  //   0
  //   1
  //   S
  //   0
  //   1
  //   0
  //   1
  //   Q
  //   Mantém o
  //   estado anterior
  //   Mantém o
  //   estado anterior
  //   0
  //   1
  //   Inválido
  //   Q
  //   Mantém o
  //   estado anterior
  //   Mantém o
  //   estado anterior
  //   0
  //   1
  //   1
  //   Q
  //   Mantém o
  //   estado anterior
  //   Mantém o
  //   estado anterior
  //   Armazena 0
  //   Armazena 1
  //   ~Q
  //   Mantém o
  //   estado anterior
  //   Mantém o
  //   estado anterior
  //   1
  //   0
  //   Inválido
  //   ~Q
  //   Mantém o
  //   estado anterior
  //   Mantém o
  //   estado anterior
  //   1
  //   0
  //   0
  //   ~Q
  //   Mantém o
  //   estado anterior
  //   Mantém o
  //   estado anterior
  //   Armazena 1
  //   Armazena 0
  //   Q
  //   ~Q
  //   Q
  //   ~Q
  //   Q
  //   ~Q
  //   Q
  //   ~Q
  //   Enable
  //   0
  //   ↑
  //   ↑
  //   ↑
  //   ↑
  //   Enable
  //   0
  //   ↑
  //   ↑
  //   ↑
  //   ↑
  //   S
  //   R
  //   X
  //   X
  //   0
  //   0
  //   0
  //   1
  //   1
  //   0
  //   1
  //   1
  //   J
  //   K
  //   X
  //   X
  //   0
  //   0
  //   0
  //   1
  //   1
  //   0
  //   1
  //   1
  //   Enable
  //   T
  //   0
  //   X
  //   ↑
  //   0
  //   ↑
  //   1
  //   Enable
  //   D
  //   0
  //   X
  //   ↑
  //   0
  //   ↑
  //   1
  //   Q
  //   Mantém o
  //   estado anterior
  //   Mantém o
  //   estado anterior
  //   0
  //   1
  //   Inválido
  //   Q
  //   Mantém o
  //   estado anterior
  //   Mantém o
  //   estado anterior
  //   0
  //   1
  //   Inverte o
  //   estado anterior
  //   Q
  //   Mantém o
  //   estado anterior
  //   Mantém o
  //   estado anterior
  //   Inverte o
  //   estado anterior
  //   Q
  //   Mantém o
  //   estado anterior
  //   0
  //   1
  //   ~Q
  //   Mantém o
  //   estado anterior
  //   Mantém o
  //   estado anterior
  //   1
  //   0
  //   Inválido
  //   ~Q
  //   Mantém o
  //   estado anterior
  //   Mantém o
  //   estado anterior
  //   1
  //   0
  //   Inverte o
  //   estado anterior
  //   ~Q
  //   Mantém o
  //   estado anterior
  //   Mantém o
  //   estado anterior
  //   Inverte o
  //   estado anterior
  //   ~Q
  //   Mantém o
  //   estado anterior
  //   1
  //   0
endmodule

module PowerOR (
  input  in_1,
  output out_2
);

  wire por_1_out;

  POR #(.PorHighDuration(1)) por_1 (.out(por_1_out));
  or or_1 (out_2, por_1_out, in_1);
endmodule
