// Logisim project logic_gates.circ as structural Verilog: 3 circuits, main circuit portas_logicas
module transistor_P (
  input  Source,
  input  Gate,
  output Drain
);

  wire not_1_out, pull_resistor_1_node, pull_resistor_3_node, transistor_2_out;

  Pull_Resistor pull_resistor_1 (.node(pull_resistor_1_node));
  not not_1 (not_1_out, Gate);
  Transistor transistor_1 (.in(Source), .out(pull_resistor_1_node), .gate(not_1_out));
  Transistor #(.\type ("n")) transistor_2 (.in(1'b0), .out(transistor_2_out), .gate(Source));
  Pull_Resistor #(.pull(1)) pull_resistor_2 (.node(transistor_2_out));
  assign Drain = pull_resistor_3_node ? pull_resistor_1_node : 1'bz;  // Controlled_Buffer controlled_buffer_1
  Pull_Resistor pull_resistor_3 (.node(pull_resistor_3_node));
  Transistor transistor_3 (.in(Gate), .out(pull_resistor_3_node), .gate(transistor_2_out));
endmodule

module portas_logicas (
  input  A,
  input  A_2,
  input  A_3,
  input  A_4,
  input  A_5,
  input  A_6,
  input  B,
  input  B_2,
  input  B_3,
  input  B_4,
  input  A_7,
  input  A_8,
  input  A_9,
  input  A_10,
  input  A_11,
  input  A_12,
  input  B_5,
  input  B_6,
  input  B_7,
  input  B_8,
  input  B_9,
  input  B_10,
  input  A_13,
  input  A_14,
  input  A_15,
  input  A_16,
  input  B_11,
  input  B_12,
  input  B_13,
  input  B_14
);

  wire pull_resistor_11_node, pull_resistor_12_node, pull_resistor_14_node, pull_resistor_16_node,
       pull_resistor_17_node, pull_resistor_18_node, pull_resistor_19_node, pull_resistor_25_node,
       pull_resistor_27_node, pull_resistor_28_node, pull_resistor_30_node, pull_resistor_32_node,
       transistor_1_out, transistor_3_out, transistor_4_out, transistor_7_out, transistor_9_out,
       transistor_13_out, transistor_17_out, transistor_19_out, transistor_22_out, transistor_24_out,
       transistor_27_out, transistor_28_out, transistor_29_out, transistor_31_out, transistor_n_1_drain,
       transistor_n_2_drain, transistor_n_3_drain, transistor_n_4_drain, transistor_n_7_drain,
       transistor_n_11_drain, transistor_p_1_drain, transistor_p_2_drain, transistor_p_5_drain,
       transistor_p_6_drain, transistor_p_7_drain, transistor_p_8_drain, transistor_p_9_drain,
       transistor_p_11_drain, transistor_p_12_drain, transistor_p_13_drain, transistor_p_14_drain,
       transistor_p_15_drain, transistor_p_16_drain, transistor_p_17_drain, transistor_p_19_drain,
       transistor_p_20_drain;

  transistor_P transistor_p_1 (.Source(1'b1), .Gate(A_3), .Drain(transistor_p_1_drain));
  transistor_P transistor_p_2 (.Source(1'b1), .Gate(A_11), .Drain(transistor_p_2_drain));
  transistor_N transistor_n_1 (.Gate(B_12), .Source(1'b0), .Drain(transistor_n_1_drain));
  Pull_Resistor pull_resistor_1 (.node(transistor_p_1_drain));
  LED led_1 (.in(transistor_p_1_drain));
  transistor_P transistor_p_3 (.Source(1'b1), .Gate(B_5), .Drain(transistor_p_2_drain));
  Pull_Resistor pull_resistor_2 (.node(transistor_p_2_drain));
  transistor_N transistor_n_2 (.Gate(transistor_p_2_drain), .Source(1'b0), .Drain(transistor_n_2_drain));
  Pull_Resistor #(.pull(1)) pull_resistor_3 (.node(transistor_n_1_drain));
  transistor_N transistor_n_3 (.Gate(A_13), .Source(1'b0), .Drain(transistor_n_3_drain));
  Pull_Resistor #(.pull(1)) pull_resistor_4 (.node(transistor_n_3_drain));
  transistor_P transistor_p_4 (.Source(1'b1), .Gate(B), .Drain(transistor_p_1_drain));
  Pull_Resistor #(.pull(1)) pull_resistor_5 (.node(transistor_n_2_drain));
  LED led_2 (.in(transistor_n_2_drain));
  transistor_P transistor_p_5 (.Source(1'b1), .Gate(A_13), .Drain(transistor_p_5_drain));
  transistor_P transistor_p_6 (
    .Source(transistor_p_5_drain), .Gate(transistor_n_1_drain), .Drain(transistor_p_6_drain));
  transistor_P transistor_p_7 (.Source(1'b1), .Gate(transistor_n_3_drain), .Drain(transistor_p_7_drain));
  transistor_P transistor_p_8 (.Source(transistor_p_7_drain), .Gate(B_12), .Drain(transistor_p_8_drain));
  transistor_P transistor_p_9 (.Source(1'b1), .Gate(transistor_p_6_drain), .Drain(transistor_p_9_drain));
  Pull_Resistor pull_resistor_6 (.node(transistor_p_6_drain));
  transistor_P transistor_p_10 (.Source(1'b1), .Gate(transistor_p_8_drain), .Drain(transistor_p_9_drain));
  Pull_Resistor pull_resistor_7 (.node(transistor_p_9_drain));
  Pull_Resistor pull_resistor_8 (.node(transistor_p_8_drain));
  Transistor #(.\type ("n")) transistor_1 (.in(1'b0), .out(transistor_1_out), .gate(A_4));
  Pull_Resistor #(.pull(1)) pull_resistor_9 (.node(transistor_1_out));
  Transistor #(.\type ("n")) transistor_2 (.in(1'b0), .out(transistor_1_out), .gate(B_2));
  Transistor transistor_3 (.in(1'b1), .out(transistor_3_out), .gate(transistor_1_out));
  LED led_3 (.in(transistor_3_out));
  transistor_N transistor_n_4 (.Gate(A_7), .Source(1'b0), .Drain(transistor_n_4_drain));
  transistor_N transistor_n_5 (.Gate(B_7), .Source(1'b0), .Drain(transistor_n_4_drain));
  LED led_4 (.in(transistor_p_9_drain));
  LED led_5 (.in(transistor_n_4_drain));
  Pull_Resistor #(.pull(1)) pull_resistor_10 (.node(transistor_n_4_drain));
  Pull_Resistor #(.pull(1)) pull_resistor_11 (.node(pull_resistor_11_node));
  Transistor transistor_4 (.in(1'b1), .out(transistor_4_out), .gate(B_13));
  Transistor #(.\type ("n")) transistor_5 (.in(1'b0), .out(transistor_4_out), .gate(B_13));
  Pull_Resistor #(.pull(1)) pull_resistor_12 (.node(pull_resistor_12_node));
  Transistor #(.\type ("n")) transistor_6 (.in(1'b0), .out(pull_resistor_12_node), .gate(transistor_7_out));
  Transistor transistor_7 (.in(1'b1), .out(transistor_7_out), .gate(A_15));
  Transistor #(.\type ("n")) transistor_8 (.in(1'b0), .out(transistor_7_out), .gate(A_15));
  Transistor #(.\type ("n")) transistor_9 (.in(1'b0), .out(transistor_9_out), .gate(B_6));
  Transistor #(.\type ("n")) transistor_10 (.in(1'b0), .out(transistor_9_out), .gate(A_12));
  Pull_Resistor #(.pull(1)) pull_resistor_13 (.node(transistor_9_out));
  Transistor #(.\type ("n")) transistor_11 (.in(1'b0), .out(pull_resistor_11_node), .gate(A_15));
  Pull_Resistor pull_resistor_14 (.node(pull_resistor_14_node));
  Transistor transistor_12 (.in(transistor_4_out), .out(pull_resistor_14_node), .gate(pull_resistor_11_node));
  Transistor #(.\type ("n")) transistor_13 (.in(1'b0), .out(transistor_13_out), .gate(pull_resistor_14_node));
  Pull_Resistor #(.pull(1)) pull_resistor_15 (.node(transistor_13_out));
  Transistor #(.\type ("n")) transistor_14 (.in(1'b0), .out(transistor_13_out), .gate(pull_resistor_16_node));
  Pull_Resistor pull_resistor_16 (.node(pull_resistor_16_node));
  Pull_Resistor pull_resistor_17 (.node(pull_resistor_17_node));
  Transistor transistor_15 (.in(B_13), .out(pull_resistor_16_node), .gate(pull_resistor_12_node));
  LED led_6 (.in(transistor_9_out));
  Transistor transistor_16 (.in(1'b1), .out(pull_resistor_17_node), .gate(transistor_13_out));
  LED led_7 (.in(pull_resistor_17_node));
  LED led_8 (.in(pull_resistor_18_node));
  Pull_Resistor #(.pull(1)) pull_resistor_18 (.node(pull_resistor_18_node));
  transistor_N transistor_n_6 (.Gate(A_5), .Source(1'b0), .Drain(pull_resistor_18_node));
  Transistor transistor_17 (.in(1'b1), .out(transistor_17_out), .gate(A_6));
  Transistor #(.\type ("n")) transistor_18 (.in(1'b0), .out(transistor_17_out), .gate(A_6));
  LED led_9 (.in(transistor_17_out));
  transistor_P transistor_p_11 (.Source(1'b1), .Gate(A_8), .Drain(transistor_p_11_drain));
  transistor_P transistor_p_12 (.Source(transistor_p_11_drain), .Gate(B_8), .Drain(transistor_p_12_drain));
  transistor_N transistor_n_7 (.Gate(A_14), .Source(1'b0), .Drain(transistor_n_7_drain));
  transistor_N transistor_n_8 (.Gate(B_11), .Source(1'b0), .Drain(transistor_n_7_drain));
  LED led_10 (.in(pull_resistor_19_node));
  Pull_Resistor #(.pull(1)) pull_resistor_19 (.node(pull_resistor_19_node));
  transistor_N transistor_n_9 (.Gate(transistor_p_12_drain), .Source(1'b0), .Drain(pull_resistor_19_node));
  Pull_Resistor pull_resistor_20 (.node(transistor_p_12_drain));
  transistor_P transistor_p_13 (.Source(1'b1), .Gate(transistor_n_7_drain), .Drain(transistor_p_13_drain));
  Pull_Resistor #(.pull(1)) pull_resistor_21 (.node(transistor_n_7_drain));
  transistor_P transistor_p_14 (
    .Source(transistor_p_13_drain), .Gate(transistor_n_7_drain), .Drain(transistor_p_14_drain));
  Pull_Resistor pull_resistor_22 (.node(transistor_p_14_drain));
  transistor_P transistor_p_15 (.Source(1'b1), .Gate(A_14), .Drain(transistor_p_15_drain));
  transistor_P transistor_p_16 (.Source(transistor_p_15_drain), .Gate(B_11), .Drain(transistor_p_16_drain));
  Pull_Resistor pull_resistor_23 (.node(transistor_p_16_drain));
  transistor_P transistor_p_17 (.Source(1'b1), .Gate(transistor_p_14_drain), .Drain(transistor_p_17_drain));
  transistor_P transistor_p_18 (.Source(1'b1), .Gate(transistor_p_16_drain), .Drain(transistor_p_17_drain));
  Pull_Resistor pull_resistor_24 (.node(transistor_p_17_drain));
  LED led_11 (.in(transistor_p_17_drain));
  transistor_P transistor_p_19 (.Source(1'b1), .Gate(A), .Drain(transistor_p_19_drain));
  transistor_P transistor_p_20 (.Source(transistor_p_19_drain), .Gate(B_3), .Drain(transistor_p_20_drain));
  Pull_Resistor #(.pull(1)) pull_resistor_25 (.node(pull_resistor_25_node));
  transistor_N transistor_n_10 (.Gate(A_9), .Source(transistor_n_11_drain), .Drain(pull_resistor_25_node));
  transistor_N transistor_n_11 (.Gate(B_9), .Source(1'b0), .Drain(transistor_n_11_drain));
  Pull_Resistor pull_resistor_26 (.node(transistor_p_20_drain));
  LED led_12 (.in(transistor_p_20_drain));
  LED led_13 (.in(pull_resistor_25_node));
  Transistor transistor_19 (.in(1'b1), .out(transistor_19_out), .gate(B_14));
  Transistor #(.\type ("n")) transistor_20 (.in(1'b0), .out(transistor_19_out), .gate(B_14));
  Pull_Resistor #(.pull(1)) pull_resistor_27 (.node(pull_resistor_27_node));
  Transistor #(.\type ("n")) transistor_21 (.in(1'b0), .out(pull_resistor_27_node), .gate(A_16));
  Pull_Resistor #(.pull(1)) pull_resistor_28 (.node(pull_resistor_28_node));
  Transistor transistor_22 (.in(1'b1), .out(transistor_22_out), .gate(A_16));
  Transistor #(.\type ("n")) transistor_23 (.in(1'b0), .out(transistor_22_out), .gate(A_16));
  Transistor #(.\type ("n")) transistor_24 (.in(1'b0), .out(transistor_24_out), .gate(transistor_22_out));
  Pull_Resistor #(.pull(1)) pull_resistor_29 (.node(transistor_24_out));
  Pull_Resistor pull_resistor_30 (.node(pull_resistor_30_node));
  Transistor transistor_25 (.in(B_14), .out(pull_resistor_30_node), .gate(pull_resistor_27_node));
  Transistor #(.\type ("n")) transistor_26 (.in(1'b0), .out(pull_resistor_28_node), .gate(A_2));
  Transistor transistor_27 (.in(B_4), .out(transistor_27_out), .gate(pull_resistor_28_node));
  LED led_14 (.in(transistor_27_out));
  Transistor #(.\type ("n")) transistor_28 (.in(transistor_29_out), .out(transistor_28_out), .gate(A_10));
  LED led_15 (.in(transistor_28_out));
  Transistor #(.\type ("n")) transistor_29 (.in(1'b0), .out(transistor_29_out), .gate(B_10));
  Transistor transistor_30 (.in(transistor_19_out), .out(pull_resistor_30_node), .gate(transistor_24_out));
  Transistor #(.\type ("n")) transistor_31 (.in(1'b0), .out(transistor_31_out), .gate(pull_resistor_30_node));
  Pull_Resistor #(.pull(1)) pull_resistor_31 (.node(transistor_31_out));
  Transistor #(.\type ("n")) transistor_32 (.in(1'b0), .out(transistor_31_out), .gate(pull_resistor_30_node));
  Pull_Resistor pull_resistor_32 (.node(pull_resistor_32_node));
  Pull_Resistor #(.pull(1)) pull_resistor_33 (.node(transistor_28_out));
  Transistor transistor_33 (.in(1'b1), .out(pull_resistor_32_node), .gate(transistor_31_out));
  LED led_16 (.in(pull_resistor_32_node));

  // Notes on the sheet:
  //   AvB
  //   NOR -> OR + NOT
  //   OR
  //   AvB
  //   A⊕B
  //   NOR
  //   A
  //   B
  //   0
  //   0
  //   0
  //   1
  //   1
  //   0
  //   1
  //   1
  //   XOR -> (A^(~B)) v ((~A)^B)
  //   AvB
  //   0
  //   1
  //   1
  //   1
  //   A⊕B
  //   A
  //   B
  //   0
  //   0
  //   0
  //   1
  //   1
  //   0
  //   1
  //   1
  //   A
  //   B
  //   0
  //   0
  //   0
  //   1
  //   1
  //   0
  //   1
  //   1
  //   ~(AvB)
  //   1
  //   0
  //   0
  //   0
  //   A⊕B
  //   0
  //   1
  //   1
  //   0
  //   ~A
  //   NOT
  //   ~A
  //   A
  //   ~A
  //   1
  //   0
  //   0
  //   1
  //   NAND -> AND + NOT
  //   ~(A^B)
  //   A⊙B
  //   A^B
  //   ~(A^B)
  //   NAND
  //   XNOR -> ((~A)^(~B)) v (A^B)
  //   AND
  //   ~(A^B)
  //   A
  //   0
  //   0
  //   1
  //   1
  //   A^B
  //   A
  //   0
  //   0
  //   1
  //   1
  //   A
  //   0
  //   0
  //   1
  //   1
  //   A⊙B
  //   B
  //   0
  //   1
  //   0
  //   1
  //   B
  //   0
  //   1
  //   0
  //   1
  //   B
  //   0
  //   1
  //   0
  //   1
  //   A^B
  //   0
  //   0
  //   0
  //   1
  //   ~(A^B)
  //   1
  //   1
  //   1
  //   0
  //   A⊙B
  //   1
  //   0
  //   0
  //   1
endmodule

module transistor_N (
  input  Gate,
  input  Source,
  output Drain
);

  Transistor #(.\type ("n")) transistor_1 (.in(Source), .out(Drain), .gate(Gate));
endmodule
