// Logisim project muxes.circ as structural Verilog: 2 circuits, main circuit main
module main (
  input  Seletor,
  input  Entrada_0,
  input  Entrada_1,
  input  [1:0] Seletor_2,
  input  Entrada_0_2,
  input  Entrada_1_2,
  input  Entrada_2,
  input  Entrada_3,
  input  [1:0] Seletor_3,
  input  Entrada_0_3,
  input  Entrada_1_3,
  input  Entrada_2_2,
  input  Entrada_3_2,
  input  [2:0] in_14,
  input  Entrada_0_4,
  input  Entrada_1_4,
  input  Entrada_2_3,
  input  Entrada_3_3,
  input  Entrada_4,
  input  Entrada_5,
  input  Entrada_6,
  input  Entrada_7,
  input  Seletor_4,
  input  [1:0] in_24,
  input  [1:0] in_25,
  input  [1:0] in_26,
  input  [1:0] in_27,
  input  Seletor_5,
  input  [1:0] in_29,
  input  [1:0] in_30,
  input  [1:0] in_31,
  input  [1:0] in_32,
  input  [1:0] in_33,
  input  [1:0] in_34,
  input  [1:0] in_35,
  input  [1:0] in_36,
  input  [1:0] in_37,
  input  [1:0] in_38,
  output \Saída ,
  output \Saída_2 ,
  output \Saída_3 ,
  output \Saída_4 ,
  output [1:0] \Saída_5 ,
  output [1:0] \Saída_6 ,
  output [1:0] \Saída_7 ,
  output [1:0] \Saída_8 
);

  wire and_1_out, and_2_out, and_3_out, and_4_out, and_5_out, and_6_out, and_7_out, and_8_out, and_9_out,
       and_10_out, and_11_out, and_12_out, and_13_out, and_14_out, and_17_out, and_18_out, and_19_out,
       and_20_out, and_21_out, and_22_out, and_23_out, and_24_out, and_25_out, and_26_out, and_27_out,
       and_28_out, and_29_out, and_30_out, and_31_out, and_32_out, and_33_out, and_34_out, and_35_out,
       and_36_out, and_37_out, and_38_out, and_39_out, and_40_out, and_41_out, and_42_out, and_43_out,
       and_44_out, and_45_out, and_46_out, and_47_out, and_48_out, not_1_out, not_2_out, not_3_out,
       not_4_out, not_5_out, not_6_out, not_7_out, not_8_out, not_9_out, not_10_out, not_11_out, not_12_out,
       not_13_out, not_14_out, or_1_out, or_2_out, or_3_out, or_4_out, or_7_out, or_8_out, or_9_out,
       or_10_out, or_11_out, or_12_out, or_13_out, or_14_out, or_15_out, or_16_out, or_17_out, or_18_out,
       or_19_out, or_20_out, or_21_out, or_22_out;

  not not_1 (not_1_out, Seletor);
  not not_2 (not_2_out, Seletor_2[0]);
  not not_3 (not_3_out, Seletor_2[1]);
  not not_4 (not_4_out, Seletor_3[0]);
  not not_5 (not_5_out, Seletor_3[1]);
  not not_6 (not_6_out, in_14[0]);
  and and_1 (and_1_out, not_1_out, Entrada_0);
  and and_2 (and_2_out, Seletor, Entrada_1);
  not not_7 (not_7_out, in_14[1]);
  not not_8 (not_8_out, in_14[2]);
  not not_9 (not_9_out, Seletor_5);
  not not_10 (not_10_out, Seletor_4);
  or or_1 (or_1_out, Seletor_5, in_27[1]);
  or or_2 (or_2_out, not_9_out, in_26[1]);
  or or_3 (or_3_out, Seletor_5, in_27[0]);
  or or_4 (or_4_out, not_9_out, in_26[0]);
  not not_11 (not_11_out, in_38[1]);
  not not_12 (not_12_out, in_38[0]);
  and and_3 (and_3_out, not_2_out, not_3_out);
  and and_4 (and_4_out, not_3_out, Seletor_2[0]);
  and and_5 (and_5_out, Seletor_2[1], not_2_out);
  and and_6 (and_6_out, Seletor_2[1], Seletor_2[0]);
  and and_7 (and_7_out, not_5_out, not_4_out, Entrada_0_3);
  and and_8 (and_8_out, not_5_out, Seletor_3[0], Entrada_1_3);
  and and_9 (and_9_out, Seletor_3[1], Seletor_3[0], Entrada_2_2);
  and and_10 (and_10_out, Seletor_3[1], Seletor_3[0], Entrada_3_2);
  and and_11 (and_11_out, not_10_out, in_24[0]);
  and and_12 (and_12_out, Seletor_4, in_25[0]);
  and and_13 (and_13_out, not_10_out, in_24[1]);
  and and_14 (and_14_out, Seletor_4, in_25[1]);
  and and_15 (\Saída_6 [1], or_1_out, or_2_out);
  and and_16 (\Saída_6 [0], or_3_out, or_4_out);
  not not_13 (not_13_out, in_29[0]);
  not not_14 (not_14_out, in_29[1]);
  and and_17 (and_17_out, and_3_out, Entrada_0_2);
  and and_18 (and_18_out, and_4_out, Entrada_1_2);
  and and_19 (and_19_out, and_5_out, Entrada_2);
  and and_20 (and_20_out, and_6_out, Entrada_3);
  or or_5 (\Saída_5 [0], and_11_out, and_12_out);
  or or_6 (\Saída_5 [1], and_13_out, and_14_out);
  or or_7 (or_7_out, in_38[1], in_38[0]);
  or or_8 (or_8_out, in_38[1], not_12_out);
  or or_9 (or_9_out, not_11_out, in_38[0]);
  or or_10 (or_10_out, not_11_out, not_12_out);
  or or_11 (or_11_out, in_38[1], in_38[0]);
  or or_12 (or_12_out, in_38[1], not_12_out);
  or or_13 (or_13_out, not_11_out, in_38[0]);
  or or_14 (or_14_out, not_11_out, not_12_out);
  and and_21 (and_21_out, not_13_out, not_14_out);
  and and_22 (and_22_out, not_14_out, in_29[0]);
  and and_23 (and_23_out, in_29[1], not_13_out);
  and and_24 (and_24_out, in_29[1], in_29[0]);
  and and_25 (and_25_out, not_13_out, not_14_out);
  and and_26 (and_26_out, not_14_out, in_29[0]);
  and and_27 (and_27_out, in_29[1], not_13_out);
  and and_28 (and_28_out, in_29[1], in_29[0]);
  or or_15 (or_15_out, or_7_out, in_37[1]);
  or or_16 (or_16_out, or_8_out, in_36[1]);
  or or_17 (or_17_out, or_9_out, in_35[1]);
  or or_18 (or_18_out, or_10_out, in_34[1]);
  or or_19 (or_19_out, or_11_out, in_37[0]);
  or or_20 (or_20_out, or_12_out, in_36[0]);
  or or_21 (or_21_out, or_13_out, in_35[0]);
  or or_22 (or_22_out, or_14_out, in_34[0]);
  or or_23 (\Saída , and_1_out, and_2_out);
  or or_24 (\Saída_2 , and_17_out, and_18_out, and_19_out, and_20_out);
  or or_25 (\Saída_3 , and_7_out, and_8_out, and_9_out, and_10_out);
  and and_29 (and_29_out, not_8_out, not_7_out, not_6_out, Entrada_0_4);
  and and_30 (and_30_out, not_8_out, not_7_out, in_14[0], Entrada_1_4);
  and and_31 (and_31_out, not_8_out, in_14[1], not_6_out, Entrada_2_3);
  and and_32 (and_32_out, not_8_out, in_14[1], in_14[0], Entrada_3_3);
  and and_33 (and_33_out, in_14[2], not_7_out, not_6_out, Entrada_4);
  and and_34 (and_34_out, in_14[2], not_7_out, in_14[0], Entrada_5);
  and and_35 (and_35_out, in_14[2], in_14[1], not_6_out, Entrada_6);
  and and_36 (and_36_out, in_14[2], in_14[1], in_14[0], Entrada_7);
  and and_37 (and_37_out, and_21_out, in_30[0]);
  and and_38 (and_38_out, and_22_out, in_31[0]);
  and and_39 (and_39_out, and_23_out, in_32[0]);
  and and_40 (and_40_out, and_24_out, in_33[0]);
  and and_41 (and_41_out, and_25_out, in_30[1]);
  and and_42 (and_42_out, and_26_out, in_31[1]);
  and and_43 (and_43_out, and_27_out, in_32[1]);
  and and_44 (and_44_out, and_28_out, in_33[1]);
  and and_45 (and_45_out, or_15_out, or_16_out);
  and and_46 (and_46_out, or_17_out, or_18_out);
  and and_47 (and_47_out, or_19_out, or_20_out);
  and and_48 (and_48_out, or_21_out, or_22_out);
  or or_26 (\Saída_4 , and_29_out, and_30_out, and_31_out, and_32_out, and_33_out, and_34_out, and_35_out, and_36_out);
  or or_27 (\Saída_7 [0], and_37_out, and_38_out, and_39_out, and_40_out);
  or or_28 (\Saída_7 [1], and_41_out, and_42_out, and_43_out, and_44_out);
  and and_49 (\Saída_8 [1], and_45_out, and_46_out);
  and and_50 (\Saída_8 [0], and_47_out, and_48_out);

  // Notes on the sheet:
  //   Opção 1
  //   Opção 2
  //   Seletor
  //   Entrada 0
  //   Entrada 1
  //   Entrada 0
  //   Entrada 1
  //   Entrada 0
  //   Entrada 1
  //   Entrada 2
  //   Entrada 3
  //   Entrada 3
  //   Entrada 2
  //   Entrada 1
  //   Entrada 0
  //   Seletor
  //   MUX para duas entradas
  //   MUX para quatro entradas
  //   MUX para oito entradas
  //   MUX para duas entradas de 2 bits
  //   MUX para quatro entradas de 2 bits
  //   Entrada 0 bit 0
  //   Entrada 1 bit 0
  //   Entrada 0 bit 1
  //   Entrada 1 bit 1
  //   Seletor
  //   Entrada 0 bit 0
  //   Entrada 1 bit 0
  //   Entrada 2 bit 0
  //   Entrada 3 bit 0
  //   Entrada 0 bit 1
  //   Entrada 1 bit 1
  //   Entrada 2 bit 1
  //   Entrada 3 bit 1
  //   MUX para duas entradas de 2 bits na forma de produto das somas
  //   MUX para quatro entradas de 2 bits na forma de produto das somas
  //   Saída bit 0
  //   Saída bit 1
  //   bit 0 -> (Sel+e0[1])^(~Sel+e1[1])
  //   bit 1 -> (Sel+e0[0])^(~Sel+e1[0])
  //   bit 0 -> (~sel^e0[0])+(sel^e1[0])
  //   bit 1 -> (~sel^e0[1])+(sel^e1[1])
  //   Saída bit 0
  //   Saída bit 1
endmodule

module demux (
  input  Seletor,
  input  Dado,
  input  [1:0] in_3,
  input  Dado_2,
  input  [1:0] in_5,
  input  in_6,
  input  [2:0] in_7,
  input  in_8,
  input  Seletor_2,
  input  [1:0] Dado_3,
  input  [1:0] Dado_4,
  input  [1:0] in_12,
  output \Saída_0 ,
  output \Saída_1 ,
  output \Saída_0_2 ,
  output \Saída_1_2 ,
  output \Saída_2 ,
  output \Saída_3 ,
  output \Saída_0_3 ,
  output \Saída_1_3 ,
  output \Saída_2_2 ,
  output \Saída_3_2 ,
  output \Saída_0_4 ,
  output \Saída_1_4 ,
  output \Saída_2_3 ,
  output \Saída_3_3 ,
  output \Saída_4 ,
  output \Saída_5 ,
  output \Saída_6 ,
  output \Saída_7 ,
  output [1:0] \Saída_0_5 ,
  output [1:0] \Saída_1_5 ,
  output [1:0] out_33,
  output [1:0] out_34,
  output [1:0] out_35,
  output [1:0] out_36
);

  wire and_3_out, and_4_out, and_5_out, and_6_out, and_27_out, and_28_out, and_29_out, and_30_out,
       and_31_out, and_32_out, and_33_out, and_34_out, not_1_out, not_2_out, not_3_out, not_4_out, not_5_out,
       not_6_out, not_7_out, not_8_out, not_9_out, not_10_out, not_11_out;

  not not_1 (not_1_out, Seletor);
  not not_2 (not_2_out, in_3[0]);
  not not_3 (not_3_out, in_5[0]);
  not not_4 (not_4_out, in_7[0]);
  not not_5 (not_5_out, Seletor_2);
  not not_6 (not_6_out, in_12[0]);
  and and_1 (\Saída_0 , not_1_out, Dado);
  and and_2 (\Saída_1 , Seletor, Dado);
  not not_7 (not_7_out, in_3[1]);
  not not_8 (not_8_out, in_5[1]);
  not not_9 (not_9_out, in_7[1]);
  not not_10 (not_10_out, in_7[2]);
  not not_11 (not_11_out, in_12[1]);
  and and_3 (and_3_out, not_7_out, not_2_out);
  and and_4 (and_4_out, in_3[0], not_7_out);
  and and_5 (and_5_out, not_2_out, in_3[1]);
  and and_6 (and_6_out, in_3[0], in_3[1]);
  and and_7 (\Saída_0_3 , not_8_out, not_3_out, in_6);
  and and_8 (\Saída_1_3 , not_8_out, in_5[0], in_6);
  and and_9 (\Saída_2_2 , not_3_out, in_5[1], in_6);
  and and_10 (\Saída_3_2 , in_5[1], in_5[0], in_6);
  and and_11 (\Saída_0_4 , not_4_out, not_9_out, not_10_out, in_8);
  and and_12 (\Saída_1_4 , in_7[0], not_9_out, not_10_out, in_8);
  and and_13 (\Saída_2_3 , not_4_out, in_7[1], not_10_out, in_8);
  and and_14 (\Saída_3_3 , in_7[0], in_7[1], not_10_out, in_8);
  and and_15 (\Saída_4 , not_4_out, not_9_out, in_7[2], in_8);
  and and_16 (\Saída_5 , in_7[0], not_9_out, in_7[2], in_8);
  and and_17 (\Saída_6 , not_4_out, in_7[1], in_7[2], in_8);
  and and_18 (\Saída_7 , in_7[2], in_7[1], in_7[0], in_8);
  and and_19 (\Saída_0_5 [0], not_5_out, Dado_3[0]);
  and and_20 (\Saída_1_5 [0], Seletor_2, Dado_3[0]);
  and and_21 (\Saída_0_5 [1], not_5_out, Dado_3[1]);
  and and_22 (\Saída_1_5 [1], Seletor_2, Dado_3[1]);
  and and_23 (\Saída_0_2 , and_3_out, Dado_2);
  and and_24 (\Saída_1_2 , and_4_out, Dado_2);
  and and_25 (\Saída_2 , and_5_out, Dado_2);
  and and_26 (\Saída_3 , and_6_out, Dado_2);
  and and_27 (and_27_out, not_6_out, not_11_out);
  and and_28 (and_28_out, in_12[0], not_11_out);
  and and_29 (and_29_out, in_12[1], not_6_out);
  and and_30 (and_30_out, in_12[1], in_12[0]);
  and and_31 (and_31_out, not_6_out, not_11_out);
  and and_32 (and_32_out, in_12[0], not_11_out);
  and and_33 (and_33_out, in_12[1], not_6_out);
  and and_34 (and_34_out, in_12[1], in_12[0]);
  and and_35 (out_33[0], and_27_out, Dado_4[0]);
  and and_36 (out_34[0], and_28_out, Dado_4[0]);
  and and_37 (out_35[0], and_29_out, Dado_4[0]);
  and and_38 (out_36[0], and_30_out, Dado_4[0]);
  and and_39 (out_33[1], and_31_out, Dado_4[1]);
  and and_40 (out_34[1], and_32_out, Dado_4[1]);
  and and_41 (out_35[1], and_33_out, Dado_4[1]);
  and and_42 (out_36[1], and_34_out, Dado_4[1]);

  // Notes on the sheet:
  //   Seletor
  //   Seletor
  //   Seletor
  //   Seletor
  //   Opção 1
  //   Opção 2
  //   DEMUX para duas entradas
  //   DEMUX para quatro entradas
  //   DEMUX para oito entradas
  //   DEMUX para duas saídas de 2 bits
  //   DEMUX para quatro saídas de 2 bits
  //   Dado
  //   Dado
  //   Saída 0
  //   Saída 1
  //   Saída 2
  //   Saída 3
endmodule
