// Logisim project registradores.circ as structural Verilog: 7 circuits, main circuit registrador_PIPO_8bits
module registrador_PIPO_8bits (
  input  in_1,
  input  in_2,
  input  in_3,
  input  in_4,
  input  in_5,
  input  in_6,
  input  in_7,
  input  in_8,
  output out_9,
  output out_10,
  output out_11,
  output out_12,
  output out_13,
  output out_14,
  output out_15,
  output out_16
);

  wire clock_1_out;

  D_Flip_Flop d_ff_1 (.D(in_8), .clk(clock_1_out), .Q(out_16));  // open: Qn, preset, reset
  Clock clock_1 (.out(clock_1_out));
  D_Flip_Flop d_ff_2 (.D(in_7), .clk(clock_1_out), .Q(out_15));  // open: Qn, preset, reset
  // Probe on {in_8, in_7, in_6, in_5, in_4, in_3, in_2, in_1}
  D_Flip_Flop d_ff_3 (.D(in_6), .clk(clock_1_out), .Q(out_14));  // open: Qn, preset, reset
  // Probe on {out_16, out_15, out_14, out_13, out_12, out_11, out_10, out_9}
  D_Flip_Flop d_ff_4 (.D(in_5), .clk(clock_1_out), .Q(out_13));  // open: Qn, preset, reset
  D_Flip_Flop d_ff_5 (.D(in_4), .clk(clock_1_out), .Q(out_12));  // open: Qn, preset, reset
  D_Flip_Flop d_ff_6 (.D(in_3), .clk(clock_1_out), .Q(out_11));  // open: Qn, preset, reset
  D_Flip_Flop d_ff_7 (.D(in_2), .clk(clock_1_out), .Q(out_10));  // open: Qn, preset, reset
  D_Flip_Flop d_ff_8 (.D(in_1), .clk(clock_1_out), .Q(out_9));  // open: Qn, preset, reset

  // Notes on the sheet:
  //   CLOCK
  //   Exemplo de uso: Buffer de dados
  //   Registrador Parallel In, Parallel Out (PIPO)
endmodule

module registrador_PIPO_32bits (
  input  in_1,
  input  in_2,
  input  in_3,
  input  in_4,
  input  in_5,
  input  in_6,
  input  in_7,
  input  in_8,
  input  in_9,
  input  in_10,
  input  in_11,
  input  in_12,
  input  in_13,
  input  in_14,
  input  in_15,
  input  in_16,
  input  in_17,
  input  in_18,
  input  in_19,
  input  in_20,
  input  in_21,
  input  in_22,
  input  in_23,
  input  in_24,
  input  in_25,
  input  in_26,
  input  in_27,
  input  in_28,
  input  in_29,
  input  in_30,
  input  in_31,
  input  in_32
);

  wire clock_1_out;
  wire [7:0] d_ff_29_q, d_ff_30_q, d_ff_31_q, d_ff_32_q;

  Clock clock_1 (.out(clock_1_out));
  D_Flip_Flop d_ff_1 (.D(in_1), .clk(clock_1_out), .Q(d_ff_29_q[7]));  // open: Qn, preset, reset
  D_Flip_Flop d_ff_2 (.D(in_9), .clk(clock_1_out), .Q(d_ff_30_q[7]));  // open: Qn, preset, reset
  D_Flip_Flop d_ff_3 (.D(in_17), .clk(clock_1_out), .Q(d_ff_31_q[7]));  // open: Qn, preset, reset
  D_Flip_Flop d_ff_4 (.D(in_25), .clk(clock_1_out), .Q(d_ff_32_q[7]));  // open: Qn, preset, reset
  D_Flip_Flop d_ff_5 (.D(in_2), .clk(clock_1_out), .Q(d_ff_29_q[6]));  // open: Qn, preset, reset
  D_Flip_Flop d_ff_6 (.D(in_10), .clk(clock_1_out), .Q(d_ff_30_q[6]));  // open: Qn, preset, reset
  D_Flip_Flop d_ff_7 (.D(in_18), .clk(clock_1_out), .Q(d_ff_31_q[6]));  // open: Qn, preset, reset
  D_Flip_Flop d_ff_8 (.D(in_26), .clk(clock_1_out), .Q(d_ff_32_q[6]));  // open: Qn, preset, reset
  D_Flip_Flop d_ff_9 (.D(in_3), .clk(clock_1_out), .Q(d_ff_29_q[5]));  // open: Qn, preset, reset
  D_Flip_Flop d_ff_10 (.D(in_11), .clk(clock_1_out), .Q(d_ff_30_q[5]));  // open: Qn, preset, reset
  D_Flip_Flop d_ff_11 (.D(in_19), .clk(clock_1_out), .Q(d_ff_31_q[5]));  // open: Qn, preset, reset
  D_Flip_Flop d_ff_12 (.D(in_27), .clk(clock_1_out), .Q(d_ff_32_q[5]));  // open: Qn, preset, reset
  D_Flip_Flop d_ff_13 (.D(in_4), .clk(clock_1_out), .Q(d_ff_29_q[4]));  // open: Qn, preset, reset
  D_Flip_Flop d_ff_14 (.D(in_12), .clk(clock_1_out), .Q(d_ff_30_q[4]));  // open: Qn, preset, reset
  D_Flip_Flop d_ff_15 (.D(in_20), .clk(clock_1_out), .Q(d_ff_31_q[4]));  // open: Qn, preset, reset
  D_Flip_Flop d_ff_16 (.D(in_28), .clk(clock_1_out), .Q(d_ff_32_q[4]));  // open: Qn, preset, reset
  D_Flip_Flop d_ff_17 (.D(in_5), .clk(clock_1_out), .Q(d_ff_29_q[3]));  // open: Qn, preset, reset
  D_Flip_Flop d_ff_18 (.D(in_13), .clk(clock_1_out), .Q(d_ff_30_q[3]));  // open: Qn, preset, reset
  D_Flip_Flop d_ff_19 (.D(in_21), .clk(clock_1_out), .Q(d_ff_31_q[3]));  // open: Qn, preset, reset
  D_Flip_Flop d_ff_20 (.D(in_29), .clk(clock_1_out), .Q(d_ff_32_q[3]));  // open: Qn, preset, reset
  D_Flip_Flop d_ff_21 (.D(in_6), .clk(clock_1_out), .Q(d_ff_29_q[2]));  // open: Qn, preset, reset
  D_Flip_Flop d_ff_22 (.D(in_14), .clk(clock_1_out), .Q(d_ff_30_q[2]));  // open: Qn, preset, reset
  D_Flip_Flop d_ff_23 (.D(in_22), .clk(clock_1_out), .Q(d_ff_31_q[2]));  // open: Qn, preset, reset
  D_Flip_Flop d_ff_24 (.D(in_30), .clk(clock_1_out), .Q(d_ff_32_q[2]));  // open: Qn, preset, reset
  D_Flip_Flop d_ff_25 (.D(in_7), .clk(clock_1_out), .Q(d_ff_29_q[1]));  // open: Qn, preset, reset
  D_Flip_Flop d_ff_26 (.D(in_15), .clk(clock_1_out), .Q(d_ff_30_q[1]));  // open: Qn, preset, reset
  D_Flip_Flop d_ff_27 (.D(in_23), .clk(clock_1_out), .Q(d_ff_31_q[1]));  // open: Qn, preset, reset
  D_Flip_Flop d_ff_28 (.D(in_31), .clk(clock_1_out), .Q(d_ff_32_q[1]));  // open: Qn, preset, reset
  D_Flip_Flop d_ff_29 (.D(in_8), .clk(clock_1_out), .Q(d_ff_29_q[0]));  // open: Qn, preset, reset
  D_Flip_Flop d_ff_30 (.D(in_16), .clk(clock_1_out), .Q(d_ff_30_q[0]));  // open: Qn, preset, reset
  D_Flip_Flop d_ff_31 (.D(in_24), .clk(clock_1_out), .Q(d_ff_31_q[0]));  // open: Qn, preset, reset
  D_Flip_Flop d_ff_32 (.D(in_32), .clk(clock_1_out), .Q(d_ff_32_q[0]));  // open: Qn, preset, reset
  LED led_1 (.in(d_ff_29_q[7]));
  LED led_2 (.in(d_ff_29_q[6]));
  LED led_3 (.in(d_ff_30_q[7]));
  LED led_4 (.in(d_ff_30_q[6]));
  LED led_5 (.in(d_ff_31_q[7]));
  LED led_6 (.in(d_ff_31_q[6]));
  LED led_7 (.in(d_ff_32_q[7]));
  LED led_8 (.in(d_ff_32_q[6]));
  LED led_9 (.in(d_ff_29_q[5]));
  LED led_10 (.in(d_ff_29_q[4]));
  LED led_11 (.in(d_ff_29_q[3]));
  LED led_12 (.in(d_ff_30_q[5]));
  LED led_13 (.in(d_ff_30_q[4]));
  LED led_14 (.in(d_ff_30_q[3]));
  LED led_15 (.in(d_ff_31_q[5]));
  LED led_16 (.in(d_ff_31_q[4]));
  LED led_17 (.in(d_ff_31_q[3]));
  LED led_18 (.in(d_ff_32_q[5]));
  LED led_19 (.in(d_ff_32_q[4]));
  LED led_20 (.in(d_ff_32_q[3]));
  LED led_21 (.in(d_ff_29_q[2]));
  LED led_22 (.in(d_ff_29_q[1]));
  LED led_23 (.in(d_ff_30_q[2]));
  LED led_24 (.in(d_ff_30_q[1]));
  LED led_25 (.in(d_ff_31_q[2]));
  LED led_26 (.in(d_ff_31_q[1]));
  LED led_27 (.in(d_ff_32_q[2]));
  LED led_28 (.in(d_ff_32_q[1]));
  LED led_29 (.in(d_ff_29_q[0]));
  LED led_30 (.in(d_ff_30_q[0]));
  LED led_31 (.in(d_ff_31_q[0]));
  LED led_32 (.in(d_ff_32_q[0]));

  // Notes on the sheet:
  //   Registrador Parallel In, Parallel Out (PIPO)
  //   Exemplo de uso: Buffer de dados
  //   CLOCK
endmodule

module registrador_PISO (
  input  in_1,
  input  in_2,
  input  in_3,
  input  in_4,
  input  in_5,
  input  in_6,
  input  in_7,
  input  in_8,
  input  in_9,
  input  CLEAR,
  output out_11,
  output out_12,
  output out_13,
  output out_14,
  output out_15,
  output out_16,
  output out_17,
  output out_18
);

  wire and_1_out, and_2_out, and_3_out, and_4_out, and_5_out, and_6_out, and_7_out, and_8_out, and_9_out,
       and_10_out, and_11_out, and_12_out, and_13_out, and_14_out, and_15_out, clock_1_out, d_ff_1_q,
       d_ff_2_q, d_ff_3_q, d_ff_4_q, d_ff_5_q, d_ff_6_q, d_ff_7_q, d_ff_8_q, not_1_out, or_1_out, or_2_out,
       or_3_out, or_4_out, or_5_out, or_6_out, or_7_out;

  Clock clock_1 (.out(clock_1_out));
  not not_1 (not_1_out, in_9);
  and and_1 (and_1_out, in_1, not_1_out);
  // Probe on {in_1, in_2, in_3, in_4, in_5, in_6, in_7, in_8}
  D_Flip_Flop d_ff_1 (.D(and_1_out), .clk(clock_1_out), .Q(d_ff_1_q));  // open: Qn, preset, reset
  and and_2 (and_2_out, d_ff_1_q, in_9);
  and and_3 (and_3_out, in_2, not_1_out);
  or or_1 (or_1_out, and_2_out, and_3_out);
  D_Flip_Flop d_ff_2 (.D(or_1_out), .clk(clock_1_out), .Q(d_ff_2_q));  // open: Qn, preset, reset
  // Probe on {out_11, out_12, out_13, out_14, out_15, out_16, out_17, out_18}
  and and_4 (and_4_out, d_ff_2_q, in_9);
  and and_5 (and_5_out, in_3, not_1_out);
  or or_2 (or_2_out, and_4_out, and_5_out);
  D_Flip_Flop d_ff_3 (.D(or_2_out), .clk(clock_1_out), .Q(d_ff_3_q));  // open: Qn, preset, reset
  and and_6 (and_6_out, d_ff_3_q, in_9);
  and and_7 (and_7_out, in_4, not_1_out);
  or or_3 (or_3_out, and_6_out, and_7_out);
  D_Flip_Flop d_ff_4 (.D(or_3_out), .clk(clock_1_out), .Q(d_ff_4_q));  // open: Qn, preset, reset
  and and_8 (and_8_out, d_ff_4_q, in_9);
  and and_9 (and_9_out, in_5, not_1_out);
  or or_4 (or_4_out, and_8_out, and_9_out);
  D_Flip_Flop d_ff_5 (.D(or_4_out), .clk(clock_1_out), .Q(d_ff_5_q));  // open: Qn, preset, reset
  and and_10 (and_10_out, d_ff_5_q, in_9);
  or or_5 (or_5_out, and_10_out, and_11_out);
  and and_11 (and_11_out, in_6, not_1_out);
  D_Flip_Flop d_ff_6 (.D(or_5_out), .clk(clock_1_out), .Q(d_ff_6_q));  // open: Qn, preset, reset
  and and_12 (and_12_out, d_ff_6_q, in_9);
  and and_13 (and_13_out, in_7, not_1_out);
  or or_6 (or_6_out, and_12_out, and_13_out);
  D_Flip_Flop d_ff_7 (.D(or_6_out), .clk(clock_1_out), .Q(d_ff_7_q));  // open: Qn, preset, reset
  and and_14 (and_14_out, d_ff_7_q, in_9);
  and and_15 (and_15_out, in_8, not_1_out);
  or or_7 (or_7_out, and_14_out, and_15_out);
  D_Flip_Flop d_ff_8 (.D(or_7_out), .clk(clock_1_out), .Q(d_ff_8_q));  // open: Qn, preset, reset
  leitor_serial leitor_serial_1 (
    .inactive(not_1_out), .clk(clock_1_out), .clear(CLEAR), .value_in(d_ff_8_q),
    .data_out({out_11, out_12, out_13, out_14, out_15, out_16, out_17, out_18}));

  // Notes on the sheet:
  //   Registrador Parallel In, Serial Out
  //   Exemplo de uso: Conversão de dados paralelos para comunicação serial
  //   SHIFT / ~LOAD
  //   CLOCK
  //   Receptor
endmodule

module registrador_SIPO (
  input  in_1,
  input  in_2,
  input  in_3,
  input  in_4,
  input  in_5,
  input  in_6,
  input  in_7,
  input  in_8,
  input  ENABLE,
  output out_10,
  output out_11,
  output out_12,
  output out_13,
  output out_14,
  output out_15,
  output out_16,
  output out_17
);

  wire alimentador_serial_1_value_out, button_1_out, clock_1_out;

  Clock clock_1 (.out(clock_1_out));
  Button button_1 (.out(button_1_out));
  D_Flip_Flop d_ff_1 (
    .D(alimentador_serial_1_value_out), .clk(clock_1_out), .Q(out_17), .reset(button_1_out));  // open: Qn, preset
  // Probe on {in_8, in_7, in_6, in_5, in_4, in_3, in_2, in_1}
  D_Flip_Flop d_ff_2 (.D(out_17), .clk(clock_1_out), .Q(out_16), .reset(button_1_out));  // open: Qn, preset
  alimentador_serial alimentador_serial_1 (
    .clk(clock_1_out), .clear(button_1_out), .data_in({in_8, in_7, in_6, in_5, in_4, in_3, in_2, in_1}),
    .enable(ENABLE), .value_out(alimentador_serial_1_value_out));
  D_Flip_Flop d_ff_3 (.D(out_16), .clk(clock_1_out), .Q(out_15), .reset(button_1_out));  // open: Qn, preset
  // Probe on {out_17, out_16, out_15, out_14, out_13, out_12, out_11, out_10}
  D_Flip_Flop d_ff_4 (.D(out_15), .clk(clock_1_out), .Q(out_14), .reset(button_1_out));  // open: Qn, preset
  D_Flip_Flop d_ff_5 (.D(out_14), .clk(clock_1_out), .Q(out_13), .reset(button_1_out));  // open: Qn, preset
  D_Flip_Flop d_ff_6 (.D(out_13), .clk(clock_1_out), .Q(out_12), .reset(button_1_out));  // open: Qn, preset
  D_Flip_Flop d_ff_7 (.D(out_12), .clk(clock_1_out), .Q(out_11), .reset(button_1_out));  // open: Qn, preset
  D_Flip_Flop d_ff_8 (.D(out_11), .clk(clock_1_out), .Q(out_10), .reset(button_1_out));  // open: Qn, preset

  // Notes on the sheet:
  //   Registrador Serial In, Parallel Out
  //   Exemplo de uso: Conversão de dados seriais em formato paralelo
  //   CLOCK
  //   CLEAR
endmodule

module registrador_SISO (
  input  in_1,
  input  in_2,
  input  in_3,
  input  in_4,
  input  in_5,
  input  in_6,
  input  in_7,
  input  in_8,
  input  LOAD,
  output out_10,
  output out_11,
  output out_12,
  output out_13,
  output out_14,
  output out_15,
  output out_16,
  output out_17
);

  wire alimentador_serial_1_value_out, button_1_out, clock_1_out, d_ff_1_q, d_ff_2_q, d_ff_3_q, d_ff_4_q,
       d_ff_5_q, d_ff_6_q, d_ff_7_q, d_ff_8_q;

  Clock clock_1 (.out(clock_1_out));
  Button button_1 (.out(button_1_out));
  D_Flip_Flop d_ff_1 (
    .D(alimentador_serial_1_value_out), .clk(clock_1_out), .Q(d_ff_1_q), .reset(button_1_out));  // open: Qn, preset
  // Probe on {in_8, in_7, in_6, in_5, in_4, in_3, in_2, in_1}
  alimentador_serial alimentador_serial_1 (
    .clk(clock_1_out), .clear(button_1_out), .data_in({in_8, in_7, in_6, in_5, in_4, in_3, in_2, in_1}),
    .enable(LOAD), .value_out(alimentador_serial_1_value_out));
  D_Flip_Flop d_ff_2 (.D(d_ff_1_q), .clk(clock_1_out), .Q(d_ff_2_q), .reset(button_1_out));  // open: Qn, preset
  D_Flip_Flop d_ff_3 (.D(d_ff_2_q), .clk(clock_1_out), .Q(d_ff_3_q), .reset(button_1_out));  // open: Qn, preset
  // Probe on {out_17, out_16, out_15, out_14, out_13, out_12, out_11, out_10}
  D_Flip_Flop d_ff_4 (.D(d_ff_3_q), .clk(clock_1_out), .Q(d_ff_4_q), .reset(button_1_out));  // open: Qn, preset
  D_Flip_Flop d_ff_5 (.D(d_ff_4_q), .clk(clock_1_out), .Q(d_ff_5_q), .reset(button_1_out));  // open: Qn, preset
  D_Flip_Flop d_ff_6 (.D(d_ff_5_q), .clk(clock_1_out), .Q(d_ff_6_q), .reset(button_1_out));  // open: Qn, preset
  D_Flip_Flop d_ff_7 (.D(d_ff_6_q), .clk(clock_1_out), .Q(d_ff_7_q), .reset(button_1_out));  // open: Qn, preset
  D_Flip_Flop d_ff_8 (.D(d_ff_7_q), .clk(clock_1_out), .Q(d_ff_8_q), .reset(button_1_out));  // open: Qn, preset
  leitor_serial leitor_serial_1 (
    .inactive(LOAD), .clk(clock_1_out), .clear(button_1_out), .value_in(d_ff_8_q),
    .data_out({out_17, out_16, out_15, out_14, out_13, out_12, out_11, out_10}));

  // Notes on the sheet:
  //   Registrador Serial In, Serial Out
  //   Exemplo de uso: Transmissão de dados por uma linha única, como comunicação UART
  //   CLOCK
  //   CLEAR
  //   Receptor
endmodule

module alimentador_serial (
  input  enable,
  input  [7:0] data_in,
  input  clk,
  input  clear,
  output value_out
);

  wire [2:0] counter_1_q;
  wire [7:0] shifter_1_out;

  Counter #(.max('h7), .width(3)) counter_1 (
    .Q(counter_1_q), .up(1'b1), .clk(clk), .clr(clear));  // open: load, D, count, carry
  Shifter #(.shift("lr")) shifter_1 (.in(data_in), .\dist (counter_1_q), .out(shifter_1_out));
  and and_1 (value_out, enable, shifter_1_out[0]);

  // Notes on the sheet:
  //   *Componente criado apenas para simplificar o processor de entrada de dados seriais
endmodule

module leitor_serial (
  input  clk,
  input  clear,
  input  inactive,
  input  value_in,
  output [7:0] data_out
);

  wire and_1_out, and_2_out, and_3_out, and_4_out, and_5_out, and_6_out, and_7_out, and_8_out, and_9_out,
       not_1_out;
  wire [2:0] counter_1_q;
  wire [7:0] or_8_out, shifter_1_out;

  not not_1 (not_1_out, inactive);
  Register register_1 (.D(or_8_out), .en(1'b1), .Q(data_out), .clk(clk), .clr(clear));
  and and_1 (and_1_out, clk, not_1_out);
  Counter #(.max('h7), .width(3)) counter_1 (
    .Q(counter_1_q), .up(1'b1), .clk(and_1_out), .clr(clear));  // open: load, D, count, carry
  Shifter shifter_1 (.in(8'h1), .\dist (counter_1_q), .out(shifter_1_out));
  and and_2 (and_2_out, shifter_1_out[7], value_in);
  and and_3 (and_3_out, shifter_1_out[6], value_in);
  or or_1 (or_8_out[7], data_out[7], and_2_out);
  or or_2 (or_8_out[6], data_out[6], and_3_out);
  and and_4 (and_4_out, shifter_1_out[5], value_in);
  and and_5 (and_5_out, shifter_1_out[4], value_in);
  or or_3 (or_8_out[5], data_out[5], and_4_out);
  or or_4 (or_8_out[4], data_out[4], and_5_out);
  and and_6 (and_6_out, shifter_1_out[3], value_in);
  and and_7 (and_7_out, shifter_1_out[2], value_in);
  or or_5 (or_8_out[3], data_out[3], and_6_out);
  or or_6 (or_8_out[2], data_out[2], and_7_out);
  and and_8 (and_8_out, shifter_1_out[1], value_in);
  and and_9 (and_9_out, shifter_1_out[0], value_in);
  or or_7 (or_8_out[1], data_out[1], and_8_out);
  or or_8 (or_8_out[0], data_out[0], and_9_out);

  // Notes on the sheet:
  //   *Componente criado apenas para simplificar o processor de leitura de dados seriais
endmodule
