// Logisim project monociclo_1.circ as structural Verilog: 1 circuit, main circuit main
module main (
  input  in_1,
  input  in_2
);

  wire and_1_out, CLK, controlunit_alt_1_alusrc, controlunit_alt_1_bne, controlunit_alt_1_branch,
       controlunit_alt_1_isjal, controlunit_alt_1_isjr, controlunit_alt_1_isshift, controlunit_alt_1_jump,
       controlunit_alt_1_memread, controlunit_alt_1_memtoreg, controlunit_alt_1_memwrite,
       controlunit_alt_1_regdest, controlunit_alt_1_regwrite, controlunit_alt_1_zeroextend, ula_1_isequal,
       xor_1_out;
  wire [3:0] controlunit_alt_1_aluop;
  wire [4:0] decoder_alt_1_rd, decoder_alt_1_rs, decoder_alt_1_rt, decoder_alt_1_shamt, multiplexer_1_out,
       multiplexer_2_out;
  wire [5:0] decoder_alt_1_funct, decoder_alt_1_op;
  wire [15:0] decoder_alt_1_immediate;
  wire [25:0] decoder_alt_1_adderess;
  wire [31:0] adder_1_out, adder_2_out, bit_extender_1_out, immediatecomplement_1_extendedimmediate,
       jumpaddress_1_jumpaddress, multiplexer_3_out, multiplexer_4_out, multiplexer_5_out, multiplexer_6_out,
       multiplexer_7_out, multiplexer_8_out, multiplexer_9_out, multiplexer_10_out, multiplexer_11_out,
       ram_1_dout, register_1_q, registerfile_1_r1out, registerfile_1_r2out, rom_1_data, shifter_1_out,
       ula_1_result, undriven;

  Register #(.width(32)) register_1 (.D(multiplexer_8_out), .en(1'b1), .clk(CLK), .Q(register_1_q), .clr(in_1));
  Clock clock_1 (.out(CLK));
  ROM #(.addrWidth(10), .dataWidth(32)) rom_1 (.addr(register_1_q[11:2]), .data(rom_1_data));
  decoder_alt decoder_alt_1 (
    .Instruction(rom_1_data), .adderess(decoder_alt_1_adderess), .immediate(decoder_alt_1_immediate),
    .funct(decoder_alt_1_funct), .op(decoder_alt_1_op), .shamt(decoder_alt_1_shamt), .rd(decoder_alt_1_rd),
    .rt(decoder_alt_1_rt), .rs(decoder_alt_1_rs));
  Adder #(.width(32)) adder_1 (.a(register_1_q), .b(32'h4), .out(adder_1_out));  // open: cin, cout
  ControlUnit_alt controlunit_alt_1 (
    .opcode(decoder_alt_1_op), .funct(decoder_alt_1_funct), .BNE(controlunit_alt_1_bne),
    .Branch(controlunit_alt_1_branch), .Jump(controlunit_alt_1_jump),
    .ZeroExtend(controlunit_alt_1_zeroextend), .ALUSrc(controlunit_alt_1_alusrc),
    .RegWrite(controlunit_alt_1_regwrite), .ALUop(controlunit_alt_1_aluop), .isJAL(controlunit_alt_1_isjal),
    .MemToReg(controlunit_alt_1_memtoreg), .MemRead(controlunit_alt_1_memread),
    .MemWrite(controlunit_alt_1_memwrite), .RegDest(controlunit_alt_1_regdest),
    .isJR(controlunit_alt_1_isjr), .isShift(controlunit_alt_1_isshift));  // open: ReadingRs, ReadingRt
  Multiplexer #(.width(5)) multiplexer_1 (
    .in0(decoder_alt_1_rt), .in1(decoder_alt_1_rd), .out(multiplexer_1_out), .sel(controlunit_alt_1_regdest));
  assign bit_extender_1_out = {{27{1'b0}}, decoder_alt_1_shamt};  // Bit_Extender bit_extender_1
  immediateComplement immediatecomplement_1 (
    .Immediate(decoder_alt_1_immediate), .ZeroExtend(controlunit_alt_1_zeroextend),
    .extendedImmediate(immediatecomplement_1_extendedimmediate));
  JumpAddress jumpaddress_1 (
    .Address(decoder_alt_1_adderess), .PCPlus4(adder_1_out), .JumpAddress(jumpaddress_1_jumpaddress));
  Multiplexer #(.width(5)) multiplexer_2 (
    .in0(multiplexer_1_out), .in1({5{1'b1}}), .out(multiplexer_2_out), .sel(controlunit_alt_1_isjal));
  Shifter #(.width(32)) shifter_1 (
    .in(immediatecomplement_1_extendedimmediate), .\dist (5'b00010), .out(shifter_1_out));
  Adder #(.width(32)) adder_2 (.a(adder_1_out), .b(shifter_1_out), .out(adder_2_out));  // open: cin, cout
  RegisterFile registerfile_1 (
    .RwIn(multiplexer_2_out), .inData(multiplexer_11_out), .WriteEnable(controlunit_alt_1_regwrite),
    .clk(CLK), .rst(in_2), .R1In(decoder_alt_1_rs), .R2In(decoder_alt_1_rt), .R1Out(registerfile_1_r1out),
    .R2Out(registerfile_1_r2out));
  Multiplexer #(.width(32)) multiplexer_3 (
    .in0(adder_1_out), .in1(adder_2_out), .out(multiplexer_3_out), .sel(and_1_out));
  and and_1 (and_1_out, xor_1_out, controlunit_alt_1_branch);
  xor xor_1 (xor_1_out, ula_1_isequal, controlunit_alt_1_bne);
  Multiplexer #(.width(32)) multiplexer_4 (
    .in0(registerfile_1_r1out), .in1(registerfile_1_r2out), .out(multiplexer_4_out),
    .sel(controlunit_alt_1_isshift));
  Multiplexer #(.width(32)) multiplexer_5 (
    .in0(registerfile_1_r2out), .in1(immediatecomplement_1_extendedimmediate), .out(multiplexer_5_out),
    .sel(controlunit_alt_1_alusrc));
  Multiplexer #(.width(32)) multiplexer_6 (
    .in0(multiplexer_5_out), .in1(bit_extender_1_out), .out(multiplexer_6_out),
    .sel(controlunit_alt_1_isshift));
  Multiplexer #(.width(32)) multiplexer_7 (
    .in0(multiplexer_3_out), .in1(jumpaddress_1_jumpaddress), .out(multiplexer_7_out),
    .sel(controlunit_alt_1_jump));
  Multiplexer #(.width(32)) multiplexer_8 (
    .in0(multiplexer_7_out), .in1(registerfile_1_r1out), .out(multiplexer_8_out), .sel(controlunit_alt_1_isjr));
  ULA ula_1 (
    .A(multiplexer_4_out), .B(multiplexer_6_out), .ALUOp(controlunit_alt_1_aluop), .isEqual(ula_1_isequal),
    .Result(ula_1_result));  // open: SignedOverflow, UnsignedOverflow
  RAM #(.addrWidth(10), .dataWidth(32), .enables("line")) ram_1 (
    .addr(ula_1_result[11:2]), .we(controlunit_alt_1_memwrite), .clk(CLK), .din(registerfile_1_r2out),
    .dout(ram_1_dout));
  // NoConnect on undriven
  Multiplexer #(.width(32)) multiplexer_9 (
    .in0(undriven), .in1(ram_1_dout), .out(multiplexer_9_out), .sel(controlunit_alt_1_memread));
  Multiplexer #(.width(32)) multiplexer_10 (
    .in0(ula_1_result), .in1(multiplexer_9_out), .out(multiplexer_10_out), .sel(controlunit_alt_1_memtoreg));
  Multiplexer #(.width(32)) multiplexer_11 (
    .in0(multiplexer_10_out), .in1(adder_1_out), .out(multiplexer_11_out), .sel(controlunit_alt_1_isjal));
endmodule
