// Logisim project Complementador.circ as structural Verilog: 1 circuit, main circuit immediateComplement
module immediateComplement (
  input  [15:0] Immediate,
  input  ZeroExtend,
  output [31:0] extendedImmediate
);

  Multiplexer #(.width(32)) multiplexer_1 (
    .in0({{17{Immediate[15]}}, Immediate[14:0]}), .in1({{16{1'b0}}, Immediate}), .out(extendedImmediate),
    .sel(ZeroExtend));
endmodule
