// Logisim project RegistradoresPrincipais.circ as structural Verilog: 2 circuits, main circuit RegisterFile
module RegisterFile (
  input  [4:0] R1In,
  input  [4:0] R2In,
  input  [4:0] RwIn,
  input  [31:0] inData,
  input  WriteEnable,
  input  clk,
  input  rst,
  output [31:0] R1Out,
  output [31:0] R2Out
);

  wire demultiplexer_1_out0, demultiplexer_1_out1, demultiplexer_1_out2, demultiplexer_1_out3,
       demultiplexer_2_out0, demultiplexer_2_out1, demultiplexer_2_out2, demultiplexer_2_out3,
       demultiplexer_2_out4, demultiplexer_2_out5, demultiplexer_2_out6, demultiplexer_2_out7,
       demultiplexer_3_out0, demultiplexer_3_out1, demultiplexer_3_out2, demultiplexer_3_out3,
       demultiplexer_3_out4, demultiplexer_3_out5, demultiplexer_3_out6, demultiplexer_3_out7,
       demultiplexer_4_out0, demultiplexer_4_out1, demultiplexer_4_out2, demultiplexer_4_out3,
       demultiplexer_4_out4, demultiplexer_4_out5, demultiplexer_4_out6, demultiplexer_4_out7,
       demultiplexer_5_out0, demultiplexer_5_out1, demultiplexer_5_out2, demultiplexer_5_out3,
       demultiplexer_5_out4, demultiplexer_5_out5, demultiplexer_5_out6, demultiplexer_5_out7;
  wire [31:0] a0_4_q, a1_5_q, a2_6_q, a3_7_q, at_1_q, fp_30_q, gp_28_q, k0_26_q, k1_27_q, ra_31_q, s3_19_q,
       s4_20_q, s5_21_q, s6_22_q, s7_23_q, sp_29_q, t0_8_q, t1_9_q, t2_10_q, t3_11_q, t4_12_q, t5_15_q,
       t6_14_q, t7_15_q, t8_24_q, t9_25_q, Ts0, Ts1, Ts2, v0_2_q, v1_3_q, zero_0_q;

  Demultiplexer #(.enable("true"), .select(2)) demultiplexer_1 (
    .out0(demultiplexer_1_out0), .out1(demultiplexer_1_out1), .out2(demultiplexer_1_out2),
    .out3(demultiplexer_1_out3), .in(1'b1), .sel(RwIn[4:3]), .en(WriteEnable));
  Demultiplexer #(.enable("true"), .select(3)) demultiplexer_2 (
    .out0(demultiplexer_2_out0), .out1(demultiplexer_2_out1), .out2(demultiplexer_2_out2),
    .out3(demultiplexer_2_out3), .out4(demultiplexer_2_out4), .out5(demultiplexer_2_out5),
    .out6(demultiplexer_2_out6), .out7(demultiplexer_2_out7), .in(1'b1), .sel(RwIn[2:0]),
    .en(demultiplexer_1_out0));
  Demultiplexer #(.enable("true"), .select(3)) demultiplexer_3 (
    .out0(demultiplexer_3_out0), .out1(demultiplexer_3_out1), .out2(demultiplexer_3_out2),
    .out3(demultiplexer_3_out3), .out4(demultiplexer_3_out4), .out5(demultiplexer_3_out5),
    .out6(demultiplexer_3_out6), .out7(demultiplexer_3_out7), .in(1'b1), .sel(RwIn[2:0]),
    .en(demultiplexer_1_out1));
  Demultiplexer #(.enable("true"), .select(3)) demultiplexer_4 (
    .out0(demultiplexer_4_out0), .out1(demultiplexer_4_out1), .out2(demultiplexer_4_out2),
    .out3(demultiplexer_4_out3), .out4(demultiplexer_4_out4), .out5(demultiplexer_4_out5),
    .out6(demultiplexer_4_out6), .out7(demultiplexer_4_out7), .in(1'b1), .sel(RwIn[2:0]),
    .en(demultiplexer_1_out2));
  Demultiplexer #(.enable("true"), .select(3)) demultiplexer_5 (
    .out0(demultiplexer_5_out0), .out1(demultiplexer_5_out1), .out2(demultiplexer_5_out2),
    .out3(demultiplexer_5_out3), .out4(demultiplexer_5_out4), .out5(demultiplexer_5_out5),
    .out6(demultiplexer_5_out6), .out7(demultiplexer_5_out7), .in(1'b1), .sel(RwIn[2:0]),
    .en(demultiplexer_1_out3));
  Register #(.width(32)) zero_0 (.D(inData), .en(demultiplexer_2_out0), .Q(zero_0_q), .clr(rst));  // open: clk
  Register #(.width(32)) t0_8 (.D(inData), .en(demultiplexer_3_out0), .clk(clk), .Q(t0_8_q), .clr(rst));
  Register #(.width(32)) s0_16 (.D(inData), .en(demultiplexer_4_out0), .clk(clk), .Q(Ts0), .clr(rst));
  Register #(.width(32)) t8_24 (.D(inData), .en(demultiplexer_5_out0), .clk(clk), .Q(t8_24_q), .clr(rst));
  Register #(.width(32)) at_1 (.D(inData), .en(demultiplexer_2_out1), .clk(clk), .Q(at_1_q), .clr(rst));
  Register #(.width(32)) t1_9 (.D(inData), .en(demultiplexer_3_out1), .clk(clk), .Q(t1_9_q), .clr(rst));
  Register #(.width(32)) s1_17 (.D(inData), .en(demultiplexer_4_out1), .clk(clk), .Q(Ts1), .clr(rst));
  Register #(.width(32)) t9_25 (.D(inData), .en(demultiplexer_5_out1), .clk(clk), .Q(t9_25_q), .clr(rst));
  Register #(.width(32)) v0_2 (.D(inData), .en(demultiplexer_2_out2), .clk(clk), .Q(v0_2_q), .clr(rst));
  Register #(.width(32)) t2_10 (.D(inData), .en(demultiplexer_3_out2), .clk(clk), .Q(t2_10_q), .clr(rst));
  Register #(.width(32)) s2_18 (.D(inData), .en(demultiplexer_4_out2), .clk(clk), .Q(Ts2), .clr(rst));
  Register #(.width(32)) k0_26 (.D(inData), .en(demultiplexer_5_out2), .clk(clk), .Q(k0_26_q), .clr(rst));
  Register #(.width(32)) v1_3 (.D(inData), .en(demultiplexer_2_out3), .clk(clk), .Q(v1_3_q), .clr(rst));
  Register #(.width(32)) t3_11 (.D(inData), .en(demultiplexer_3_out3), .clk(clk), .Q(t3_11_q), .clr(rst));
  Register #(.width(32)) s3_19 (.D(inData), .en(demultiplexer_4_out3), .clk(clk), .Q(s3_19_q), .clr(rst));
  Register #(.width(32)) k1_27 (.D(inData), .en(demultiplexer_5_out3), .clk(clk), .Q(k1_27_q), .clr(rst));
  Register #(.width(32)) a0_4 (.D(inData), .en(demultiplexer_2_out4), .clk(clk), .Q(a0_4_q), .clr(rst));
  Register #(.width(32)) t4_12 (.D(inData), .en(demultiplexer_3_out4), .clk(clk), .Q(t4_12_q), .clr(rst));
  Register #(.width(32)) s4_20 (.D(inData), .en(demultiplexer_4_out4), .clk(clk), .Q(s4_20_q), .clr(rst));
  Register #(.width(32)) gp_28 (.D(inData), .en(demultiplexer_5_out4), .clk(clk), .Q(gp_28_q), .clr(rst));
  Register #(.width(32)) a1_5 (.D(inData), .en(demultiplexer_2_out5), .clk(clk), .Q(a1_5_q), .clr(rst));
  Register #(.width(32)) t5_15 (.D(inData), .en(demultiplexer_3_out5), .clk(clk), .Q(t5_15_q), .clr(rst));
  Register #(.width(32)) s5_21 (.D(inData), .en(demultiplexer_4_out5), .clk(clk), .Q(s5_21_q), .clr(rst));
  Register #(.width(32)) sp_29 (.D(inData), .en(demultiplexer_5_out5), .clk(clk), .Q(sp_29_q), .clr(rst));
  Register #(.width(32)) a2_6 (.D(inData), .en(demultiplexer_2_out6), .clk(clk), .Q(a2_6_q), .clr(rst));
  Register #(.width(32)) t6_14 (.D(inData), .en(demultiplexer_3_out6), .clk(clk), .Q(t6_14_q), .clr(rst));
  Register #(.width(32)) s6_22 (.D(inData), .en(demultiplexer_4_out6), .clk(clk), .Q(s6_22_q), .clr(rst));
  Register #(.width(32)) fp_30 (.D(inData), .en(demultiplexer_5_out6), .clk(clk), .Q(fp_30_q), .clr(rst));
  Register #(.width(32)) a3_7 (.D(inData), .en(demultiplexer_2_out7), .clk(clk), .Q(a3_7_q), .clr(rst));
  Register #(.width(32)) t7_15 (.D(inData), .en(demultiplexer_3_out7), .clk(clk), .Q(t7_15_q), .clr(rst));
  Register #(.width(32)) s7_23 (.D(inData), .en(demultiplexer_4_out7), .clk(clk), .Q(s7_23_q), .clr(rst));
  Register #(.width(32)) ra_31 (.D(inData), .en(demultiplexer_5_out7), .clk(clk), .Q(ra_31_q), .clr(rst));
  Multiplexer #(.disabled("Z"), .select(5), .width(32)) multiplexer_1 (
    .in0(zero_0_q), .in1(at_1_q), .in2(v0_2_q), .in3(v1_3_q), .in4(a0_4_q), .in5(a1_5_q), .in6(a2_6_q),
    .in7(a3_7_q), .in8(t0_8_q), .in9(t1_9_q), .in10(t2_10_q), .in11(t3_11_q), .in12(t4_12_q), .in13(t5_15_q),
    .in14(t6_14_q), .in15(t7_15_q), .in16(Ts0), .in17(Ts1), .in18(Ts2), .in19(s3_19_q), .in20(s4_20_q),
    .in21(s5_21_q), .in22(s6_22_q), .in23(s7_23_q), .in24(t8_24_q), .in25(t9_25_q), .in26(k0_26_q),
    .in27(k1_27_q), .in28(gp_28_q), .in29(sp_29_q), .in30(fp_30_q), .in31(ra_31_q), .out(R1Out), .sel(R1In));
  Multiplexer #(.disabled("Z"), .select(5), .width(32)) multiplexer_2 (
    .in0(zero_0_q), .in1(at_1_q), .in2(v0_2_q), .in3(v1_3_q), .in4(a0_4_q), .in5(a1_5_q), .in6(a2_6_q),
    .in7(a3_7_q), .in8(t0_8_q), .in9(t1_9_q), .in10(t2_10_q), .in11(t3_11_q), .in12(t4_12_q), .in13(t5_15_q),
    .in14(t6_14_q), .in15(t7_15_q), .in16(Ts0), .in17(Ts1), .in18(Ts2), .in19(s3_19_q), .in20(s4_20_q),
    .in21(s5_21_q), .in22(s6_22_q), .in23(s7_23_q), .in24(t8_24_q), .in25(t9_25_q), .in26(k0_26_q),
    .in27(k1_27_q), .in28(gp_28_q), .in29(sp_29_q), .in30(fp_30_q), .in31(ra_31_q), .out(R2Out), .sel(R2In));

  // Other names for the same wires on the sheet: Tclk = clk; TinDado[31:0] = inData; TR1[4:0] = R1In; TR2[4:0] = R2In;
  //   Treg1[31:0] = R1Out; Treg2[31:0] = R2Out; Trst = rst; TRw[4:0] = RwIn; TWE = WriteEnable
endmodule

module RegisterFIle_1_Const (
  input  [4:0] R1In,
  input  [4:0] R2In,
  input  [4:0] RwIn,
  input  [31:0] inData,
  input  WriteEnable,
  input  clk,
  input  rst,
  output [31:0] R1Out,
  output [31:0] R2Out
);

  wire demultiplexer_1_out0, demultiplexer_1_out1, demultiplexer_1_out2, demultiplexer_1_out3,
       demultiplexer_2_out1, demultiplexer_2_out2, demultiplexer_2_out3, demultiplexer_2_out4,
       demultiplexer_2_out5, demultiplexer_2_out6, demultiplexer_2_out7, demultiplexer_3_out0,
       demultiplexer_3_out1, demultiplexer_3_out2, demultiplexer_3_out3, demultiplexer_3_out4,
       demultiplexer_3_out5, demultiplexer_3_out6, demultiplexer_3_out7, demultiplexer_4_out0,
       demultiplexer_4_out1, demultiplexer_4_out2, demultiplexer_4_out3, demultiplexer_4_out4,
       demultiplexer_4_out5, demultiplexer_4_out6, demultiplexer_4_out7, demultiplexer_5_out0,
       demultiplexer_5_out1, demultiplexer_5_out2, demultiplexer_5_out3, demultiplexer_5_out4,
       demultiplexer_5_out5, demultiplexer_5_out6, demultiplexer_5_out7;
  wire [31:0] a0_4_q, a1_5_q, a2_6_q, a3_7_q, at_1_q, fp_30_q, gp_28_q, k0_26_q, k1_27_q, ra_31_q, s3_19_q,
       s4_20_q, s5_21_q, s6_22_q, s7_23_q, sp_29_q, t0_8_q, t1_9_q, t2_10_q, t3_11_q, t4_12_q, t5_15_q,
       t6_14_q, t7_15_q, t8_24_q, t9_25_q, Ts0, Ts1, Ts2, v0_2_q, v1_3_q, zero_0_q;

  Demultiplexer #(.enable("true"), .select(2)) demultiplexer_1 (
    .out0(demultiplexer_1_out0), .out1(demultiplexer_1_out1), .out2(demultiplexer_1_out2),
    .out3(demultiplexer_1_out3), .in(1'b1), .sel(RwIn[4:3]), .en(WriteEnable));
  Demultiplexer #(.enable("true"), .select(3)) demultiplexer_2 (
    .out1(demultiplexer_2_out1), .out2(demultiplexer_2_out2), .out3(demultiplexer_2_out3),
    .out4(demultiplexer_2_out4), .out5(demultiplexer_2_out5), .out6(demultiplexer_2_out6),
    .out7(demultiplexer_2_out7), .in(1'b1), .sel(RwIn[2:0]), .en(demultiplexer_1_out0));  // open: out0
  Demultiplexer #(.enable("true"), .select(3)) demultiplexer_3 (
    .out0(demultiplexer_3_out0), .out1(demultiplexer_3_out1), .out2(demultiplexer_3_out2),
    .out3(demultiplexer_3_out3), .out4(demultiplexer_3_out4), .out5(demultiplexer_3_out5),
    .out6(demultiplexer_3_out6), .out7(demultiplexer_3_out7), .in(1'b1), .sel(RwIn[2:0]),
    .en(demultiplexer_1_out1));
  Demultiplexer #(.enable("true"), .select(3)) demultiplexer_4 (
    .out0(demultiplexer_4_out0), .out1(demultiplexer_4_out1), .out2(demultiplexer_4_out2),
    .out3(demultiplexer_4_out3), .out4(demultiplexer_4_out4), .out5(demultiplexer_4_out5),
    .out6(demultiplexer_4_out6), .out7(demultiplexer_4_out7), .in(1'b1), .sel(RwIn[2:0]),
    .en(demultiplexer_1_out2));
  Demultiplexer #(.enable("true"), .select(3)) demultiplexer_5 (
    .out0(demultiplexer_5_out0), .out1(demultiplexer_5_out1), .out2(demultiplexer_5_out2),
    .out3(demultiplexer_5_out3), .out4(demultiplexer_5_out4), .out5(demultiplexer_5_out5),
    .out6(demultiplexer_5_out6), .out7(demultiplexer_5_out7), .in(1'b1), .sel(RwIn[2:0]),
    .en(demultiplexer_1_out3));
  Register #(.trigger("high"), .width(32)) zero_0 (.D(32'h1), .en(1'b1), .clk(1'b1), .Q(zero_0_q));  // open: clr
  Register #(.width(32)) t0_8 (.D(inData), .en(demultiplexer_3_out0), .clk(clk), .Q(t0_8_q), .clr(rst));
  Register #(.width(32)) s0_16 (.D(inData), .en(demultiplexer_4_out0), .clk(clk), .Q(Ts0), .clr(rst));
  Register #(.width(32)) t8_24 (.D(inData), .en(demultiplexer_5_out0), .clk(clk), .Q(t8_24_q), .clr(rst));
  Register #(.width(32)) at_1 (.D(inData), .en(demultiplexer_2_out1), .clk(clk), .Q(at_1_q), .clr(rst));
  Register #(.width(32)) t1_9 (.D(inData), .en(demultiplexer_3_out1), .clk(clk), .Q(t1_9_q), .clr(rst));
  Register #(.width(32)) s1_17 (.D(inData), .en(demultiplexer_4_out1), .clk(clk), .Q(Ts1), .clr(rst));
  Register #(.width(32)) t9_25 (.D(inData), .en(demultiplexer_5_out1), .clk(clk), .Q(t9_25_q), .clr(rst));
  Register #(.width(32)) v0_2 (.D(inData), .en(demultiplexer_2_out2), .clk(clk), .Q(v0_2_q), .clr(rst));
  Register #(.width(32)) t2_10 (.D(inData), .en(demultiplexer_3_out2), .clk(clk), .Q(t2_10_q), .clr(rst));
  Register #(.width(32)) s2_18 (.D(inData), .en(demultiplexer_4_out2), .clk(clk), .Q(Ts2), .clr(rst));
  Register #(.width(32)) k0_26 (.D(inData), .en(demultiplexer_5_out2), .clk(clk), .Q(k0_26_q), .clr(rst));
  Register #(.width(32)) v1_3 (.D(inData), .en(demultiplexer_2_out3), .clk(clk), .Q(v1_3_q), .clr(rst));
  Register #(.width(32)) t3_11 (.D(inData), .en(demultiplexer_3_out3), .clk(clk), .Q(t3_11_q), .clr(rst));
  Register #(.width(32)) s3_19 (.D(inData), .en(demultiplexer_4_out3), .clk(clk), .Q(s3_19_q), .clr(rst));
  Register #(.width(32)) k1_27 (.D(inData), .en(demultiplexer_5_out3), .clk(clk), .Q(k1_27_q), .clr(rst));
  Register #(.width(32)) a0_4 (.D(inData), .en(demultiplexer_2_out4), .clk(clk), .Q(a0_4_q), .clr(rst));
  Register #(.width(32)) t4_12 (.D(inData), .en(demultiplexer_3_out4), .clk(clk), .Q(t4_12_q), .clr(rst));
  Register #(.width(32)) s4_20 (.D(inData), .en(demultiplexer_4_out4), .clk(clk), .Q(s4_20_q), .clr(rst));
  Register #(.width(32)) gp_28 (.D(inData), .en(demultiplexer_5_out4), .clk(clk), .Q(gp_28_q), .clr(rst));
  Register #(.width(32)) a1_5 (.D(inData), .en(demultiplexer_2_out5), .clk(clk), .Q(a1_5_q), .clr(rst));
  Register #(.width(32)) t5_15 (.D(inData), .en(demultiplexer_3_out5), .clk(clk), .Q(t5_15_q), .clr(rst));
  Register #(.width(32)) s5_21 (.D(inData), .en(demultiplexer_4_out5), .clk(clk), .Q(s5_21_q), .clr(rst));
  Register #(.width(32)) sp_29 (.D(inData), .en(demultiplexer_5_out5), .clk(clk), .Q(sp_29_q), .clr(rst));
  Register #(.width(32)) a2_6 (.D(inData), .en(demultiplexer_2_out6), .clk(clk), .Q(a2_6_q), .clr(rst));
  Register #(.width(32)) t6_14 (.D(inData), .en(demultiplexer_3_out6), .clk(clk), .Q(t6_14_q), .clr(rst));
  Register #(.width(32)) s6_22 (.D(inData), .en(demultiplexer_4_out6), .clk(clk), .Q(s6_22_q), .clr(rst));
  Register #(.width(32)) fp_30 (.D(inData), .en(demultiplexer_5_out6), .clk(clk), .Q(fp_30_q), .clr(rst));
  Register #(.width(32)) a3_7 (.D(inData), .en(demultiplexer_2_out7), .clk(clk), .Q(a3_7_q), .clr(rst));
  Register #(.width(32)) t7_15 (.D(inData), .en(demultiplexer_3_out7), .clk(clk), .Q(t7_15_q), .clr(rst));
  Register #(.width(32)) s7_23 (.D(inData), .en(demultiplexer_4_out7), .clk(clk), .Q(s7_23_q), .clr(rst));
  Register #(.width(32)) ra_31 (.D(inData), .en(demultiplexer_5_out7), .clk(clk), .Q(ra_31_q), .clr(rst));
  Multiplexer #(.disabled("Z"), .select(5), .width(32)) multiplexer_1 (
    .in0(zero_0_q), .in1(at_1_q), .in2(v0_2_q), .in3(v1_3_q), .in4(a0_4_q), .in5(a1_5_q), .in6(a2_6_q),
    .in7(a3_7_q), .in8(t0_8_q), .in9(t1_9_q), .in10(t2_10_q), .in11(t3_11_q), .in12(t4_12_q), .in13(t5_15_q),
    .in14(t6_14_q), .in15(t7_15_q), .in16(Ts0), .in17(Ts1), .in18(Ts2), .in19(s3_19_q), .in20(s4_20_q),
    .in21(s5_21_q), .in22(s6_22_q), .in23(s7_23_q), .in24(t8_24_q), .in25(t9_25_q), .in26(k0_26_q),
    .in27(k1_27_q), .in28(gp_28_q), .in29(sp_29_q), .in30(fp_30_q), .in31(ra_31_q), .out(R1Out), .sel(R1In));
  Multiplexer #(.disabled("Z"), .select(5), .width(32)) multiplexer_2 (
    .in0(zero_0_q), .in1(at_1_q), .in2(v0_2_q), .in3(v1_3_q), .in4(a0_4_q), .in5(a1_5_q), .in6(a2_6_q),
    .in7(a3_7_q), .in8(t0_8_q), .in9(t1_9_q), .in10(t2_10_q), .in11(t3_11_q), .in12(t4_12_q), .in13(t5_15_q),
    .in14(t6_14_q), .in15(t7_15_q), .in16(Ts0), .in17(Ts1), .in18(Ts2), .in19(s3_19_q), .in20(s4_20_q),
    .in21(s5_21_q), .in22(s6_22_q), .in23(s7_23_q), .in24(t8_24_q), .in25(t9_25_q), .in26(k0_26_q),
    .in27(k1_27_q), .in28(gp_28_q), .in29(sp_29_q), .in30(fp_30_q), .in31(ra_31_q), .out(R2Out), .sel(R2In));

  // Other names for the same wires on the sheet: Tclk = clk; TinDado[31:0] = inData; TR1[4:0] = R1In; TR2[4:0] = R2In;
  //   Treg1[31:0] = R1Out; Treg2[31:0] = R2Out; Trst = rst; TRw[4:0] = RwIn; TWE = WriteEnable
endmodule
