// Logisim project ULA.circ as structural Verilog: 3 circuits, main circuit ULA
module ULA (
  input  [31:0] A,
  input  [31:0] B,
  input  [3:0] ALUOp,
  output SignedOverflow,
  output UnsignedOverflow,
  output [31:0] Result,
  output isEqual
);

  wire comparator_1_lt;
  wire [1:0] modifiedadder_1_signedoverflow, modifiedsubtractor_1_signedoverflow;
  wire [31:0] and_1_out, bit_extender_1_out, modifiedadder_1_sum, modifiedsubtractor_1_subtraction,
       nor_1_out, or_1_out, shifter_1_out, shifter_2_out, xor_1_out;

  ModifiedAdder modifiedadder_1 (
    .A(A), .B(B), .Sum(modifiedadder_1_sum), .UnsignedOverflow(modifiedadder_1_signedoverflow[1]),
    .SignedOverflow(modifiedadder_1_signedoverflow[0]));
  ModifiedSubtractor modifiedsubtractor_1 (
    .A(A), .B(B), .Subtraction(modifiedsubtractor_1_subtraction),
    .UnsignedOverflow(modifiedsubtractor_1_signedoverflow[1]),
    .SignedOverflow(modifiedsubtractor_1_signedoverflow[0]));
  assign and_1_out = A & B;  // AND_Gate and_1, 32 bits wide
  assign or_1_out = A | B;  // OR_Gate or_1, 32 bits wide
  assign xor_1_out = A ^ B;  // XOR_Gate xor_1, 32 bits wide
  assign nor_1_out = ~(A | B);  // NOR_Gate nor_1, 32 bits wide
  Shifter #(.width(32)) shifter_1 (.in(A), .\dist (B[4:0]), .out(shifter_1_out));
  Shifter #(.shift("lr"), .width(32)) shifter_2 (.in(A), .\dist (B[4:0]), .out(shifter_2_out));
  Comparator #(.width(32)) comparator_1 (.a(A), .b(B), .lt(comparator_1_lt));  // open: gt, eq
  Comparator #(.width(32)) comparator_2 (.a(A), .b(B), .eq(isEqual));  // open: gt, lt
  assign bit_extender_1_out = {{31{1'b0}}, comparator_1_lt};  // Bit_Extender bit_extender_1
  Multiplexer #(.select(4), .width(2)) multiplexer_1 (
    .in0(modifiedsubtractor_1_signedoverflow), .in1(modifiedadder_1_signedoverflow), .in2(2'b00),
    .in3(2'b00), .in4(2'b00), .in5(2'b00), .in6(2'b00), .in7(2'b00), .in8(2'b00), .in9(2'b00), .in10(2'b00),
    .in11(2'b00), .in12(2'b00), .in13(2'b00), .in14(2'b00), .in15(2'b00),
    .out({UnsignedOverflow, SignedOverflow}), .sel(ALUOp));
  Multiplexer #(.select(4), .width(32)) multiplexer_2 (
    .in0(modifiedadder_1_sum), .in1(modifiedsubtractor_1_subtraction), .in2(and_1_out), .in3(or_1_out),
    .in4(xor_1_out), .in5(nor_1_out), .in6(shifter_1_out), .in7(shifter_2_out), .in8(bit_extender_1_out),
    .in9({32{1'b0}}), .in10({32{1'b0}}), .in11({32{1'b0}}), .in12({32{1'b0}}), .in13({32{1'b0}}),
    .in14({32{1'b0}}), .in15({32{1'b0}}), .out(Result), .sel(ALUOp));

  // Other names for the same wires on the sheet: SigOverFlow = SignedOverflow; UsgOverflow = UnsignedOverflow;
  //   Operation[3:0] = ALUOp
endmodule

module ModifiedAdder (
  input  [31:0] A,
  input  [31:0] B,
  output SignedOverflow,
  output UnsignedOverflow,
  output [31:0] Sum
);

  wire adder_1_cout;

  Adder #(.width(31)) adder_1 (.a(A[30:0]), .b(B[30:0]), .out(Sum[30:0]), .cout(adder_1_cout));  // open: cin
  Adder #(.width(1)) adder_2 (.a(A[31]), .b(B[31]), .out(Sum[31]), .cin(adder_1_cout), .cout(UnsignedOverflow));
  xor xor_1 (SignedOverflow, adder_1_cout, UnsignedOverflow);

  // Other names for the same wires on the sheet: SignedOverflowsum = SignedOverflow; sumResult[31:0] = Sum;
  //   UnsignedOverflowsum = UnsignedOverflow; X[31:0] = A; Y[31:0] = B
endmodule

module ModifiedSubtractor (
  input  [31:0] A,
  input  [31:0] B,
  output SignedOverflow,
  output UnsignedOverflow,
  output [31:0] Subtraction
);

  wire subtractor_1_bout;

  Subtractor #(.width(31)) subtractor_1 (
    .a(A[30:0]), .b(B[30:0]), .out(Subtraction[30:0]), .bout(subtractor_1_bout));  // open: bin
  Subtractor #(.width(1)) subtractor_2 (
    .a(A[31]), .b(B[31]), .out(Subtraction[31]), .bin(subtractor_1_bout), .bout(UnsignedOverflow));
  xor xor_1 (SignedOverflow, subtractor_1_bout, UnsignedOverflow);

  // Other names for the same wires on the sheet: Resultsub[31:0] = Subtraction; SignedOverflowsub = SignedOverflow;
  //   UnsignedOverflowsub = UnsignedOverflow; X[31:0] = A; Y[31:0] = B
endmodule
