// Logisim project desenhos.circ as structural Verilog: 2 circuits, main circuit circulo
module circulo (
  input  in_1,
  output out_2
);


  assign out_2 = in_1;
endmodule

module quadrado (
  input  in_1,
  output out_2
);


  assign out_2 = in_1;
endmodule
