// Logisim project datapath_add.circ as structural Verilog: 1 circuit, main circuit main
module main (
);

  wire buffer_1_out, buffer_2_out, circulo_1_out_2, Clear_out, clock_1_out, quadrado_1_out_2, Reset_PC_out;
  wire [4:0] decoder_alt_1_rd, decoder_alt_1_rs, decoder_alt_1_rt;
  wire [31:0] adder_1_out, register_1_q, registerfile_1_const_1_r1out, registerfile_1_const_1_r2out,
       rom_1_data, ula_1_result;

  Register #(.width(32)) register_1 (
    .D(adder_1_out), .en(1'b1), .clk(clock_1_out), .Q(register_1_q), .clr(Reset_PC_out));
  Button Reset_PC (.out(Reset_PC_out));
  quadrado quadrado_1 (.in_1(buffer_1_out), .out_2(quadrado_1_out_2));
  buf buffer_1 (buffer_1_out, circulo_1_out_2);
  Adder #(.width(32)) adder_1 (.a(register_1_q), .b(32'h4), .out(adder_1_out));  // open: cin, cout
  ROM #(.addrWidth(10), .dataWidth(32)) rom_1 (.addr(register_1_q[11:2]), .data(rom_1_data));
  decoder_alt decoder_alt_1 (
    .Instruction(rom_1_data), .rd(decoder_alt_1_rd), .rt(decoder_alt_1_rt), .rs(decoder_alt_1_rs));  // open: adderess, immediate, funct, op, shamt
  Clock clock_1 (.out(clock_1_out));
  buf buffer_2 (buffer_2_out, quadrado_1_out_2);
  Button Clear (.out(Clear_out));
  circulo circulo_1 (.in_1(buffer_2_out), .out_2(circulo_1_out_2));
  RegisterFIle_1_Const registerfile_1_const_1 (
    .RwIn(decoder_alt_1_rd), .inData(ula_1_result), .WriteEnable(1'b1), .clk(clock_1_out), .rst(Clear_out),
    .R1In(decoder_alt_1_rs), .R2In(decoder_alt_1_rt), .R1Out(registerfile_1_const_1_r1out),
    .R2Out(registerfile_1_const_1_r2out));
  ULA ula_1 (
    .A(registerfile_1_const_1_r1out), .B(registerfile_1_const_1_r2out), .ALUOp(4'b0000), .Result(ula_1_result));  // open: SignedOverflow, UnsignedOverflow, isEqual

  // Notes on the sheet:
  //   contents of rom_1 (hex, n*v repeats v):
  //   1005020 14a5020 10a5820 1686020 18c6820 10a6820 16a7020 14a5020 10a5820
endmodule
