// Logisim project datapath_addi.circ as structural Verilog: 1 circuit, main circuit main
module main (
);

  wire buffer_1_out, buffer_2_out, circulo_1_out_2, Clear_out, clock_1_out, quadrado_1_out_2, Reset_PC_out;
  wire [4:0] decoder_alt_1_rs, decoder_alt_1_rt;
  wire [15:0] decoder_alt_1_immediate;
  wire [31:0] adder_1_out, immediatecomplement_1_extendedimmediate, register_1_q, registerfile_1_r1out,
       rom_1_data, ula_1_result;

  Register #(.width(32)) register_1 (
    .D(adder_1_out), .en(1'b1), .clk(clock_1_out), .Q(register_1_q), .clr(Reset_PC_out));
  Button Reset_PC (.out(Reset_PC_out));
  quadrado quadrado_1 (.in_1(buffer_1_out), .out_2(quadrado_1_out_2));
  buf buffer_1 (buffer_1_out, circulo_1_out_2);
  Adder #(.width(32)) adder_1 (.a(register_1_q), .b(32'h4), .out(adder_1_out));  // open: cin, cout
  ROM #(.addrWidth(10), .dataWidth(32)) rom_1 (.addr(register_1_q[11:2]), .data(rom_1_data));
  decoder_alt decoder_alt_1 (
    .Instruction(rom_1_data), .immediate(decoder_alt_1_immediate), .rt(decoder_alt_1_rt),
    .rs(decoder_alt_1_rs));  // open: adderess, funct, op, shamt, rd
  immediateComplement immediatecomplement_1 (
    .Immediate(decoder_alt_1_immediate), .ZeroExtend(1'b0),
    .extendedImmediate(immediatecomplement_1_extendedimmediate));
  Clock clock_1 (.out(clock_1_out));
  buf buffer_2 (buffer_2_out, quadrado_1_out_2);
  Button Clear (.out(Clear_out));
  circulo circulo_1 (.in_1(buffer_2_out), .out_2(circulo_1_out_2));
  RegisterFile registerfile_1 (
    .RwIn(decoder_alt_1_rt), .inData(ula_1_result), .WriteEnable(1'b1), .clk(clock_1_out), .rst(Clear_out),
    .R1In(decoder_alt_1_rs), .R1Out(registerfile_1_r1out));  // open: R2In, R2Out
  ULA ula_1 (
    .A(registerfile_1_r1out), .B(immediatecomplement_1_extendedimmediate), .ALUOp(4'b0000),
    .Result(ula_1_result));  // open: SignedOverflow, UnsignedOverflow, isEqual

  // Notes on the sheet:
  //   contents of rom_1 (hex, n*v repeats v):
  //   20080d08 20090d09 200a0d0a 200b0d0b 200c0d0c 200d0d0d 200e0d0e 200f0d0f 20100d10 20110d11 20120d12
  //   20130d13 20140d14 20150d15 20160d16 20170d17 20180d18 20190d19
endmodule
