// Logisim project datapath_beq.circ as structural Verilog: 1 circuit, main circuit main
module main (
);

  wire and_1_out, and_2_out, buffer_2_out, Clear_out, clock_1_out, not_1_out, not_2_out, not_3_out,
       not_4_out, not_5_out, Reset_PC_out, ula_1_isequal, undriven, undriven_2;
  wire [4:0] decoder_alt_1_rs, decoder_alt_1_rt;
  wire [5:0] decoder_alt_1_op;
  wire [15:0] decoder_alt_1_immediate;
  wire [31:0] adder_1_out, adder_2_out, immediatecomplement_1_extendedimmediate, multiplexer_1_out,
       register_1_q, registerfile_1_const_1_r1out, registerfile_1_const_1_r2out, rom_1_data, shifter_1_out;

  Register #(.width(32)) register_1 (
    .D(multiplexer_1_out), .en(1'b1), .clk(clock_1_out), .Q(register_1_q), .clr(Reset_PC_out));
  Button Reset_PC (.out(Reset_PC_out));
  // Buffer buffer_1 has open pins: in=undriven, out=open
  Adder #(.width(32)) adder_1 (.a(register_1_q), .b(32'h4), .out(adder_1_out));  // open: cin, cout
  ROM #(.addrWidth(10), .dataWidth(32)) rom_1 (.addr(register_1_q[11:2]), .data(rom_1_data));
  decoder_alt decoder_alt_1 (
    .Instruction(rom_1_data), .immediate(decoder_alt_1_immediate), .op(decoder_alt_1_op),
    .rt(decoder_alt_1_rt), .rs(decoder_alt_1_rs));  // open: adderess, funct, shamt, rd
  Clock clock_1 (.out(clock_1_out));
  buf buffer_2 (buffer_2_out, undriven_2);
  immediateComplement immediatecomplement_1 (
    .Immediate(decoder_alt_1_immediate), .ZeroExtend(1'b0),
    .extendedImmediate(immediatecomplement_1_extendedimmediate));
  Button Clear (.out(Clear_out));
  not not_1 (not_1_out, decoder_alt_1_op[0]);
  not not_2 (not_2_out, decoder_alt_1_op[1]);
  not not_3 (not_3_out, decoder_alt_1_op[3]);
  not not_4 (not_4_out, decoder_alt_1_op[4]);
  not not_5 (not_5_out, decoder_alt_1_op[5]);
  Shifter #(.width(32)) shifter_1 (
    .in(immediatecomplement_1_extendedimmediate), .\dist (5'b00010), .out(shifter_1_out));
  and and_1 (and_1_out, not_1_out, not_2_out, decoder_alt_1_op[2], not_3_out, not_4_out, not_5_out);
  Multiplexer #(.width(32)) multiplexer_1 (
    .in0(adder_1_out), .in1(adder_2_out), .out(multiplexer_1_out), .sel(and_2_out));
  Adder #(.width(32)) adder_2 (.a(adder_1_out), .b(shifter_1_out), .out(adder_2_out));  // open: cin, cout
  and and_2 (and_2_out, and_1_out, ula_1_isequal);
  RegisterFIle_1_Const registerfile_1_const_1 (
    .WriteEnable(1'b1), .clk(clock_1_out), .rst(Clear_out), .R1In(decoder_alt_1_rs), .R2In(decoder_alt_1_rt),
    .R1Out(registerfile_1_const_1_r1out), .R2Out(registerfile_1_const_1_r2out));  // open: RwIn, inData
  ULA ula_1 (
    .A(registerfile_1_const_1_r1out), .B(registerfile_1_const_1_r2out), .ALUOp(4'b0000),
    .isEqual(ula_1_isequal));  // open: SignedOverflow, UnsignedOverflow, Result

  // Notes on the sheet:
  //   contents of rom_1 (hex, n*v repeats v):
  //   10090005 100a0002 10100003 11090002 100a0002 10100003 10090005 1211fffa 10100003 10100003
endmodule
