// Logisim project datapath_j.circ as structural Verilog: 1 circuit, main circuit main
module main (
);

  wire and_1_out, buffer_2_out, clock_1_out, not_1_out, not_2_out, not_3_out, not_4_out, not_5_out,
       Reset_PC_out, undriven, undriven_2;
  wire [5:0] decoder_alt_1_op;
  wire [25:0] decoder_alt_1_adderess;
  wire [31:0] adder_1_out, jumpaddress_1_jumpaddress, multiplexer_1_out, register_1_q, rom_1_data;

  Register #(.width(32)) register_1 (
    .D(multiplexer_1_out), .en(1'b1), .clk(clock_1_out), .Q(register_1_q), .clr(Reset_PC_out));
  Button Reset_PC (.out(Reset_PC_out));
  // Buffer buffer_1 has open pins: in=undriven, out=open
  Adder #(.width(32)) adder_1 (.a(register_1_q), .b(32'h4), .out(adder_1_out));  // open: cin, cout
  ROM #(.addrWidth(10), .dataWidth(32)) rom_1 (.addr(register_1_q[11:2]), .data(rom_1_data));
  decoder_alt decoder_alt_1 (
    .Instruction(rom_1_data), .adderess(decoder_alt_1_adderess), .op(decoder_alt_1_op));  // open: immediate, funct, shamt, rd, rt, rs
  Clock clock_1 (.out(clock_1_out));
  buf buffer_2 (buffer_2_out, undriven_2);
  Multiplexer #(.width(32)) multiplexer_1 (
    .in0(adder_1_out), .in1(jumpaddress_1_jumpaddress), .out(multiplexer_1_out), .sel(and_1_out));
  not not_1 (not_1_out, decoder_alt_1_op[0]);
  not not_2 (not_2_out, decoder_alt_1_op[2]);
  not not_3 (not_3_out, decoder_alt_1_op[3]);
  not not_4 (not_4_out, decoder_alt_1_op[4]);
  not not_5 (not_5_out, decoder_alt_1_op[5]);
  JumpAddress jumpaddress_1 (
    .Address(decoder_alt_1_adderess), .PCPlus4(adder_1_out), .JumpAddress(jumpaddress_1_jumpaddress));
  and and_1 (and_1_out, not_1_out, decoder_alt_1_op[1], not_2_out, not_3_out, not_4_out, not_5_out);

  // Notes on the sheet:
  //   contents of rom_1 (hex, n*v repeats v):
  //   0 0 0 8000005 0 0 0 8000002 8000010 8000020
endmodule
