// Logisim project datapath_sw.circ as structural Verilog: 1 circuit, main circuit main
module main (
  input  Clear_Memory
);

  wire buffer_1_out, buffer_2_out, circulo_1_out_2, Clear_out, clock_1_out, quadrado_1_out_2, Reset_PC_out;
  wire [4:0] decoder_alt_1_rs, decoder_alt_1_rt;
  wire [15:0] decoder_alt_1_immediate;
  wire [31:0] adder_1_out, immediatecomplement_1_extendedimmediate, register_1_q,
       registerfile_1_const_1_r1out, registerfile_1_const_1_r2out, rom_1_data, ula_1_result;

  Register #(.width(32)) register_1 (
    .D(adder_1_out), .en(1'b1), .clk(clock_1_out), .Q(register_1_q), .clr(Reset_PC_out));
  Button Reset_PC (.out(Reset_PC_out));
  quadrado quadrado_1 (.in_1(buffer_1_out), .out_2(quadrado_1_out_2));
  buf buffer_1 (buffer_1_out, circulo_1_out_2);
  Adder #(.width(32)) adder_1 (.a(register_1_q), .b(32'h4), .out(adder_1_out));  // open: cin, cout
  ROM #(.addrWidth(10), .dataWidth(32)) rom_1 (.addr(register_1_q[11:2]), .data(rom_1_data));
  decoder_alt decoder_alt_1 (
    .Instruction(rom_1_data), .immediate(decoder_alt_1_immediate), .rt(decoder_alt_1_rt),
    .rs(decoder_alt_1_rs));  // open: adderess, funct, op, shamt, rd
  immediateComplement immediatecomplement_1 (
    .Immediate(decoder_alt_1_immediate), .ZeroExtend(1'b0),
    .extendedImmediate(immediatecomplement_1_extendedimmediate));
  Clock clock_1 (.out(clock_1_out));
  buf buffer_2 (buffer_2_out, quadrado_1_out_2);
  Button Clear (.out(Clear_out));
  circulo circulo_1 (.in_1(buffer_2_out), .out_2(circulo_1_out_2));
  RegisterFIle_1_Const registerfile_1_const_1 (
    .WriteEnable(1'b1), .clk(clock_1_out), .rst(Clear_out), .R1In(decoder_alt_1_rs), .R2In(decoder_alt_1_rt),
    .R1Out(registerfile_1_const_1_r1out), .R2Out(registerfile_1_const_1_r2out));  // open: RwIn, inData
  ULA ula_1 (
    .A(registerfile_1_const_1_r1out), .B(immediatecomplement_1_extendedimmediate), .ALUOp(4'b0000),
    .Result(ula_1_result));  // open: SignedOverflow, UnsignedOverflow, isEqual
  RAM #(.addrWidth(10), .asyncread("true"), .clearpin("true"), .dataWidth(32)) ram_1 (
    .addr(ula_1_result[11:2]), .we(1'b1), .oe(1'b0), .clk(clock_1_out), .din(registerfile_1_const_1_r2out),
    .clr(Clear_Memory));  // open: dout

  // Notes on the sheet:
  //   contents of rom_1 (hex, n*v repeats v):
  //   ac000000 ac000004 ac000008 ac00000c ac000010 ac000014
endmodule
