// Logisim project partial_datapaths.circ as structural Verilog: 8 circuits, main circuit datapath_add
module datapath_add (
);

  wire buffer_1_out, buffer_2_out, circulo_1_out_2, Clear_out, clock_1_out, quadrado_1_out_2, Reset_PC_out;
  wire [4:0] decoder_alt_1_rd, decoder_alt_1_rs, decoder_alt_1_rt;
  wire [31:0] adder_1_out, register_1_q, registerfile_1_const_1_r1out, registerfile_1_const_1_r2out,
       rom_1_data, ula_1_result;

  Register #(.width(32)) register_1 (
    .D(adder_1_out), .en(1'b1), .clk(clock_1_out), .Q(register_1_q), .clr(Reset_PC_out));
  Button Reset_PC (.out(Reset_PC_out));
  quadrado quadrado_1 (.in_1(buffer_1_out), .out_2(quadrado_1_out_2));
  buf buffer_1 (buffer_1_out, circulo_1_out_2);
  Adder #(.width(32)) adder_1 (.a(register_1_q), .b(32'h4), .out(adder_1_out));  // open: cin, cout
  ROM #(.addrWidth(10), .dataWidth(32)) rom_1 (.addr(register_1_q[11:2]), .data(rom_1_data));
  decoder_alt decoder_alt_1 (
    .Instruction(rom_1_data), .rd(decoder_alt_1_rd), .rt(decoder_alt_1_rt), .rs(decoder_alt_1_rs));  // open: adderess, immediate, funct, op, shamt
  Clock clock_1 (.out(clock_1_out));
  buf buffer_2 (buffer_2_out, quadrado_1_out_2);
  Button Clear (.out(Clear_out));
  circulo circulo_1 (.in_1(buffer_2_out), .out_2(circulo_1_out_2));
  RegisterFIle_1_Const registerfile_1_const_1 (
    .RwIn(decoder_alt_1_rd), .inData(ula_1_result), .WriteEnable(1'b1), .clk(clock_1_out), .rst(Clear_out),
    .R1In(decoder_alt_1_rs), .R2In(decoder_alt_1_rt), .R1Out(registerfile_1_const_1_r1out),
    .R2Out(registerfile_1_const_1_r2out));
  ULA ula_1 (
    .A(registerfile_1_const_1_r1out), .B(registerfile_1_const_1_r2out), .ALUOp(4'b0000), .Result(ula_1_result));  // open: SignedOverflow, UnsignedOverflow, isEqual

  // Notes on the sheet:
  //   contents of rom_1 (hex, n*v repeats v):
  //   1005020 14a5020 10a5820 1686020 18c6820 10a6820 16a7020 14a5020 10a5820
endmodule

module datapath_addi (
);

  wire buffer_1_out, buffer_2_out, circulo_1_out_2, Clear_out, clock_1_out, quadrado_1_out_2, Reset_PC_out;
  wire [4:0] decoder_alt_1_rs, decoder_alt_1_rt;
  wire [15:0] decoder_alt_1_immediate;
  wire [31:0] adder_1_out, immediatecomplement_1_extendedimmediate, register_1_q, registerfile_1_r1out,
       rom_1_data, ula_1_result;

  Register #(.width(32)) register_1 (
    .D(adder_1_out), .en(1'b1), .clk(clock_1_out), .Q(register_1_q), .clr(Reset_PC_out));
  Button Reset_PC (.out(Reset_PC_out));
  quadrado quadrado_1 (.in_1(buffer_1_out), .out_2(quadrado_1_out_2));
  buf buffer_1 (buffer_1_out, circulo_1_out_2);
  Adder #(.width(32)) adder_1 (.a(register_1_q), .b(32'h4), .out(adder_1_out));  // open: cin, cout
  ROM #(.addrWidth(10), .dataWidth(32)) rom_1 (.addr(register_1_q[11:2]), .data(rom_1_data));
  decoder_alt decoder_alt_1 (
    .Instruction(rom_1_data), .immediate(decoder_alt_1_immediate), .rt(decoder_alt_1_rt),
    .rs(decoder_alt_1_rs));  // open: adderess, funct, op, shamt, rd
  immediateComplement immediatecomplement_1 (
    .Immediate(decoder_alt_1_immediate), .ZeroExtend(1'b0),
    .extendedImmediate(immediatecomplement_1_extendedimmediate));
  Clock clock_1 (.out(clock_1_out));
  buf buffer_2 (buffer_2_out, quadrado_1_out_2);
  Button Clear (.out(Clear_out));
  circulo circulo_1 (.in_1(buffer_2_out), .out_2(circulo_1_out_2));
  RegisterFile registerfile_1 (
    .RwIn(decoder_alt_1_rt), .inData(ula_1_result), .WriteEnable(1'b1), .clk(clock_1_out), .rst(Clear_out),
    .R1In(decoder_alt_1_rs), .R1Out(registerfile_1_r1out));  // open: R2In, R2Out
  ULA ula_1 (
    .A(registerfile_1_r1out), .B(immediatecomplement_1_extendedimmediate), .ALUOp(4'b0000),
    .Result(ula_1_result));  // open: SignedOverflow, UnsignedOverflow, isEqual

  // Notes on the sheet:
  //   contents of rom_1 (hex, n*v repeats v):
  //   20080d08 20090d09 200a0d0a 200b0d0b 200c0d0c 200d0d0d 200e0d0e 200f0d0f 20100d10 20110d11 20120d12
  //   20130d13 20140d14 20150d15 20160d16 20170d17 20180d18 20190d19
endmodule

module datapath_beq (
);

  wire and_1_out, and_2_out, buffer_1_out, buffer_2_out, circulo_1_out_2, Clear_out, clock_1_out, not_1_out,
       not_2_out, not_3_out, not_4_out, not_5_out, quadrado_1_out_2, Reset_PC_out, ula_1_isequal;
  wire [4:0] decoder_alt_1_rs, decoder_alt_1_rt;
  wire [5:0] decoder_alt_1_op;
  wire [15:0] decoder_alt_1_immediate;
  wire [31:0] adder_1_out, adder_2_out, immediatecomplement_1_extendedimmediate, multiplexer_1_out,
       register_1_q, registerfile_1_const_1_r1out, registerfile_1_const_1_r2out, rom_1_data, shifter_1_out;

  Register #(.width(32)) register_1 (
    .D(multiplexer_1_out), .en(1'b1), .clk(clock_1_out), .Q(register_1_q), .clr(Reset_PC_out));
  Button Reset_PC (.out(Reset_PC_out));
  quadrado quadrado_1 (.in_1(buffer_1_out), .out_2(quadrado_1_out_2));
  buf buffer_1 (buffer_1_out, circulo_1_out_2);
  Adder #(.width(32)) adder_1 (.a(register_1_q), .b(32'h4), .out(adder_1_out));  // open: cin, cout
  ROM #(.addrWidth(10), .dataWidth(32)) rom_1 (.addr(register_1_q[11:2]), .data(rom_1_data));
  decoder_alt decoder_alt_1 (
    .Instruction(rom_1_data), .immediate(decoder_alt_1_immediate), .op(decoder_alt_1_op),
    .rt(decoder_alt_1_rt), .rs(decoder_alt_1_rs));  // open: adderess, funct, shamt, rd
  Clock clock_1 (.out(clock_1_out));
  buf buffer_2 (buffer_2_out, quadrado_1_out_2);
  immediateComplement immediatecomplement_1 (
    .Immediate(decoder_alt_1_immediate), .ZeroExtend(1'b0),
    .extendedImmediate(immediatecomplement_1_extendedimmediate));
  Button Clear (.out(Clear_out));
  not not_1 (not_1_out, decoder_alt_1_op[0]);
  not not_2 (not_2_out, decoder_alt_1_op[1]);
  not not_3 (not_3_out, decoder_alt_1_op[3]);
  not not_4 (not_4_out, decoder_alt_1_op[4]);
  not not_5 (not_5_out, decoder_alt_1_op[5]);
  circulo circulo_1 (.in_1(buffer_2_out), .out_2(circulo_1_out_2));
  Shifter #(.width(32)) shifter_1 (
    .in(immediatecomplement_1_extendedimmediate), .\dist (5'b00010), .out(shifter_1_out));
  and and_1 (and_1_out, not_1_out, not_2_out, decoder_alt_1_op[2], not_3_out, not_4_out, not_5_out);
  Multiplexer #(.width(32)) multiplexer_1 (
    .in0(adder_1_out), .in1(adder_2_out), .out(multiplexer_1_out), .sel(and_2_out));
  Adder #(.width(32)) adder_2 (.a(adder_1_out), .b(shifter_1_out), .out(adder_2_out));  // open: cin, cout
  and and_2 (and_2_out, and_1_out, ula_1_isequal);
  RegisterFIle_1_Const registerfile_1_const_1 (
    .WriteEnable(1'b1), .clk(clock_1_out), .rst(Clear_out), .R1In(decoder_alt_1_rs), .R2In(decoder_alt_1_rt),
    .R1Out(registerfile_1_const_1_r1out), .R2Out(registerfile_1_const_1_r2out));  // open: RwIn, inData
  ULA ula_1 (
    .A(registerfile_1_const_1_r1out), .B(registerfile_1_const_1_r2out), .ALUOp(4'b0000),
    .isEqual(ula_1_isequal));  // open: SignedOverflow, UnsignedOverflow, Result

  // Notes on the sheet:
  //   contents of rom_1 (hex, n*v repeats v):
  //   10090005 100a0002 10100003 11090002 100a0002 10100003 10090005 1211fffa 10100003 10100003
endmodule

module datapath_j (
);

  wire and_1_out, buffer_1_out, buffer_2_out, circulo_1_out_2, clock_1_out, not_1_out, not_2_out, not_3_out,
       not_4_out, not_5_out, quadrado_1_out_2, Reset_PC_out;
  wire [5:0] decoder_alt_1_op;
  wire [25:0] decoder_alt_1_adderess;
  wire [31:0] adder_1_out, jumpaddress_1_jumpaddress, multiplexer_1_out, register_1_q, rom_1_data;

  Register #(.width(32)) register_1 (
    .D(multiplexer_1_out), .en(1'b1), .clk(clock_1_out), .Q(register_1_q), .clr(Reset_PC_out));
  Button Reset_PC (.out(Reset_PC_out));
  quadrado quadrado_1 (.in_1(buffer_1_out), .out_2(quadrado_1_out_2));
  buf buffer_1 (buffer_1_out, circulo_1_out_2);
  Adder #(.width(32)) adder_1 (.a(register_1_q), .b(32'h4), .out(adder_1_out));  // open: cin, cout
  ROM #(.addrWidth(10), .dataWidth(32)) rom_1 (.addr(register_1_q[11:2]), .data(rom_1_data));
  decoder_alt decoder_alt_1 (
    .Instruction(rom_1_data), .adderess(decoder_alt_1_adderess), .op(decoder_alt_1_op));  // open: immediate, funct, shamt, rd, rt, rs
  Clock clock_1 (.out(clock_1_out));
  buf buffer_2 (buffer_2_out, quadrado_1_out_2);
  Multiplexer #(.width(32)) multiplexer_1 (
    .in0(adder_1_out), .in1(jumpaddress_1_jumpaddress), .out(multiplexer_1_out), .sel(and_1_out));
  not not_1 (not_1_out, decoder_alt_1_op[0]);
  not not_2 (not_2_out, decoder_alt_1_op[2]);
  not not_3 (not_3_out, decoder_alt_1_op[3]);
  not not_4 (not_4_out, decoder_alt_1_op[4]);
  not not_5 (not_5_out, decoder_alt_1_op[5]);
  JumpAddress jumpaddress_1 (
    .Address(decoder_alt_1_adderess), .PCPlus4(adder_1_out), .JumpAddress(jumpaddress_1_jumpaddress));
  and and_1 (and_1_out, not_1_out, decoder_alt_1_op[1], not_2_out, not_3_out, not_4_out, not_5_out);
  circulo circulo_1 (.in_1(buffer_2_out), .out_2(circulo_1_out_2));

  // Notes on the sheet:
  //   contents of rom_1 (hex, n*v repeats v):
  //   0 0 0 8000005 0 0 0 8000002 8000010 8000020
endmodule

module datapath_lw (
  input  Clear_Memory
);

  wire buffer_1_out, buffer_2_out, circulo_1_out_2, Clear_out, clock_1_out, quadrado_1_out_2, Reset_PC_out;
  wire [4:0] decoder_alt_1_rs, decoder_alt_1_rt;
  wire [15:0] decoder_alt_1_immediate;
  wire [31:0] adder_1_out, immediatecomplement_1_extendedimmediate, ram_1_dout, register_1_q,
       registerfile_1_r1out, rom_1_data, ula_1_result;

  Register #(.width(32)) register_1 (
    .D(adder_1_out), .en(1'b1), .clk(clock_1_out), .Q(register_1_q), .clr(Reset_PC_out));
  Button Reset_PC (.out(Reset_PC_out));
  quadrado quadrado_1 (.in_1(buffer_1_out), .out_2(quadrado_1_out_2));
  buf buffer_1 (buffer_1_out, circulo_1_out_2);
  Adder #(.width(32)) adder_1 (.a(register_1_q), .b(32'h4), .out(adder_1_out));  // open: cin, cout
  ROM #(.addrWidth(10), .dataWidth(32)) rom_1 (.addr(register_1_q[11:2]), .data(rom_1_data));
  decoder_alt decoder_alt_1 (
    .Instruction(rom_1_data), .immediate(decoder_alt_1_immediate), .rt(decoder_alt_1_rt),
    .rs(decoder_alt_1_rs));  // open: adderess, funct, op, shamt, rd
  immediateComplement immediatecomplement_1 (
    .Immediate(decoder_alt_1_immediate), .ZeroExtend(1'b0),
    .extendedImmediate(immediatecomplement_1_extendedimmediate));
  Clock clock_1 (.out(clock_1_out));
  buf buffer_2 (buffer_2_out, quadrado_1_out_2);
  Button Clear (.out(Clear_out));
  circulo circulo_1 (.in_1(buffer_2_out), .out_2(circulo_1_out_2));
  RegisterFile registerfile_1 (
    .RwIn(decoder_alt_1_rt), .inData(ram_1_dout), .WriteEnable(1'b1), .clk(clock_1_out), .rst(Clear_out),
    .R1In(decoder_alt_1_rs), .R1Out(registerfile_1_r1out));  // open: R2In, R2Out
  ULA ula_1 (
    .A(registerfile_1_r1out), .B(immediatecomplement_1_extendedimmediate), .ALUOp(4'b0000),
    .Result(ula_1_result));  // open: SignedOverflow, UnsignedOverflow, isEqual
  RAM #(.addrWidth(10), .asyncread("true"), .clearpin("true"), .dataWidth(32)) ram_1 (
    .addr(ula_1_result[11:2]), .we(1'b0), .oe(1'b1), .clk(clock_1_out), .dout(ram_1_dout), .clr(Clear_Memory));  // open: din

  // Notes on the sheet:
  //   contents of rom_1 (hex, n*v repeats v):
  //   ac100000 ac110004 ac120008 ac13000c ac140010 ac150014
endmodule

module datapath_sw (
  input  Clear_Memory
);

  wire buffer_1_out, buffer_2_out, circulo_1_out_2, Clear_out, clock_1_out, quadrado_1_out_2, Reset_PC_out;
  wire [4:0] decoder_alt_1_rs, decoder_alt_1_rt;
  wire [15:0] decoder_alt_1_immediate;
  wire [31:0] adder_1_out, immediatecomplement_1_extendedimmediate, register_1_q,
       registerfile_1_const_1_r1out, registerfile_1_const_1_r2out, rom_1_data, ula_1_result;

  Register #(.width(32)) register_1 (
    .D(adder_1_out), .en(1'b1), .clk(clock_1_out), .Q(register_1_q), .clr(Reset_PC_out));
  Button Reset_PC (.out(Reset_PC_out));
  quadrado quadrado_1 (.in_1(buffer_1_out), .out_2(quadrado_1_out_2));
  buf buffer_1 (buffer_1_out, circulo_1_out_2);
  Adder #(.width(32)) adder_1 (.a(register_1_q), .b(32'h4), .out(adder_1_out));  // open: cin, cout
  ROM #(.addrWidth(10), .dataWidth(32)) rom_1 (.addr(register_1_q[11:2]), .data(rom_1_data));
  decoder_alt decoder_alt_1 (
    .Instruction(rom_1_data), .immediate(decoder_alt_1_immediate), .rt(decoder_alt_1_rt),
    .rs(decoder_alt_1_rs));  // open: adderess, funct, op, shamt, rd
  immediateComplement immediatecomplement_1 (
    .Immediate(decoder_alt_1_immediate), .ZeroExtend(1'b0),
    .extendedImmediate(immediatecomplement_1_extendedimmediate));
  Clock clock_1 (.out(clock_1_out));
  buf buffer_2 (buffer_2_out, quadrado_1_out_2);
  Button Clear (.out(Clear_out));
  circulo circulo_1 (.in_1(buffer_2_out), .out_2(circulo_1_out_2));
  RegisterFIle_1_Const registerfile_1_const_1 (
    .WriteEnable(1'b1), .clk(clock_1_out), .rst(Clear_out), .R1In(decoder_alt_1_rs), .R2In(decoder_alt_1_rt),
    .R1Out(registerfile_1_const_1_r1out), .R2Out(registerfile_1_const_1_r2out));  // open: RwIn, inData
  ULA ula_1 (
    .A(registerfile_1_const_1_r1out), .B(immediatecomplement_1_extendedimmediate), .ALUOp(4'b0000),
    .Result(ula_1_result));  // open: SignedOverflow, UnsignedOverflow, isEqual
  RAM #(.addrWidth(10), .asyncread("true"), .clearpin("true"), .dataWidth(32)) ram_1 (
    .addr(ula_1_result[11:2]), .we(1'b1), .oe(1'b0), .clk(clock_1_out), .din(registerfile_1_const_1_r2out),
    .clr(Clear_Memory));  // open: dout

  // Notes on the sheet:
  //   contents of rom_1 (hex, n*v repeats v):
  //   ac000000 ac000004 ac000008 ac00000c ac000010 ac000014
endmodule

module compared_datapaths (
  input  Clock,
  input  Clock_2,
  input  Clock_3,
  input  Clear_Memory,
  input  in_5,
  input  Clock_4,
  input  Clock_5,
  input  Clear_Memory_2
);

  wire and_1_out, and_2_out, and_3_out, button_1_out, button_2_out, button_3_out, button_4_out, button_5_out,
       button_6_out, button_7_out, button_8_out, button_9_out, button_10_out, button_11_out, not_1_out,
       not_2_out, not_3_out, not_4_out, not_5_out, not_6_out, not_7_out, not_8_out, not_9_out, not_10_out,
       ula_3_isequal;
  wire [4:0] decoder_alt_1_rd, decoder_alt_1_rs, decoder_alt_1_rt, decoder_alt_2_rs, decoder_alt_2_rt,
       decoder_alt_3_rs, decoder_alt_3_rt, decoder_alt_5_rs, decoder_alt_5_rt, decoder_alt_6_rs,
       decoder_alt_6_rt;
  wire [5:0] decoder_alt_3_op, decoder_alt_4_op;
  wire [15:0] decoder_alt_2_immediate, decoder_alt_3_immediate, decoder_alt_5_immediate,
       decoder_alt_6_immediate;
  wire [25:0] decoder_alt_4_adderess;
  wire [31:0] adder_1_out, adder_2_out, adder_3_out, adder_4_out, adder_5_out, adder_6_out, adder_7_out,
       immediatecomplement_1_extendedimmediate, immediatecomplement_2_extendedimmediate,
       immediatecomplement_3_extendedimmediate, immediatecomplement_4_extendedimmediate,
       jumpaddress_1_jumpaddress, multiplexer_1_out, multiplexer_2_out, ram_1_dout, register_1_q,
       register_2_q, register_3_q, register_4_q, register_5_q, register_6_q, registerfile_1_const_1_r1out,
       registerfile_1_const_1_r2out, registerfile_1_const_2_r1out, registerfile_1_const_2_r2out,
       registerfile_1_const_3_r1out, registerfile_1_const_3_r2out, registerfile_1_r1out,
       registerfile_2_r1out, rom_1_data, rom_2_data, rom_3_data, rom_4_data, rom_5_data, rom_6_data,
       shifter_1_out, ula_1_result, ula_2_result, ula_4_result, ula_5_result;

  Register #(.width(32)) register_1 (.D(adder_1_out), .en(1'b1), .clk(Clock_2), .Q(register_1_q), .clr(button_1_out));
  Register #(.width(32)) register_2 (.D(adder_2_out), .en(1'b1), .clk(in_5), .Q(register_2_q), .clr(button_2_out));
  Button button_1 (.out(button_1_out));
  Button button_2 (.out(button_2_out));
  Adder #(.width(32)) adder_1 (.a(register_1_q), .b(32'h4), .out(adder_1_out));  // open: cin, cout
  ROM #(.addrWidth(10), .dataWidth(32)) rom_1 (.addr(register_1_q[11:2]), .data(rom_1_data));
  Adder #(.width(32)) adder_2 (.a(register_2_q), .b(32'h4), .out(adder_2_out));  // open: cin, cout
  ROM #(.addrWidth(10), .dataWidth(32)) rom_2 (.addr(register_2_q[11:2]), .data(rom_2_data));
  decoder_alt decoder_alt_1 (
    .Instruction(rom_1_data), .rd(decoder_alt_1_rd), .rt(decoder_alt_1_rt), .rs(decoder_alt_1_rs));  // open: adderess, immediate, funct, op, shamt
  Button button_3 (.out(button_3_out));
  decoder_alt decoder_alt_2 (
    .Instruction(rom_2_data), .immediate(decoder_alt_2_immediate), .rt(decoder_alt_2_rt),
    .rs(decoder_alt_2_rs));  // open: adderess, funct, op, shamt, rd
  immediateComplement immediatecomplement_1 (
    .Immediate(decoder_alt_2_immediate), .ZeroExtend(1'b0),
    .extendedImmediate(immediatecomplement_1_extendedimmediate));
  Button button_4 (.out(button_4_out));
  RegisterFIle_1_Const registerfile_1_const_1 (
    .RwIn(decoder_alt_1_rd), .inData(ula_1_result), .WriteEnable(1'b1), .clk(Clock_2), .rst(button_3_out),
    .R1In(decoder_alt_1_rs), .R2In(decoder_alt_1_rt), .R1Out(registerfile_1_const_1_r1out),
    .R2Out(registerfile_1_const_1_r2out));
  RegisterFile registerfile_1 (
    .RwIn(decoder_alt_2_rt), .inData(ula_2_result), .WriteEnable(1'b1), .clk(in_5), .rst(button_4_out),
    .R1In(decoder_alt_2_rs), .R1Out(registerfile_1_r1out));  // open: R2In, R2Out
  ULA ula_1 (
    .A(registerfile_1_const_1_r1out), .B(registerfile_1_const_1_r2out), .ALUOp(4'b0000), .Result(ula_1_result));  // open: SignedOverflow, UnsignedOverflow, isEqual
  ULA ula_2 (
    .A(registerfile_1_r1out), .B(immediatecomplement_1_extendedimmediate), .ALUOp(4'b0000),
    .Result(ula_2_result));  // open: SignedOverflow, UnsignedOverflow, isEqual
  Register #(.width(32)) register_3 (
    .D(multiplexer_2_out), .en(1'b1), .clk(Clock_3), .Q(register_3_q), .clr(button_5_out));
  Register #(.width(32)) register_4 (
    .D(multiplexer_1_out), .en(1'b1), .clk(Clock_5), .Q(register_4_q), .clr(button_6_out));
  Button button_5 (.out(button_5_out));
  Button button_6 (.out(button_6_out));
  Adder #(.width(32)) adder_3 (.a(register_3_q), .b(32'h4), .out(adder_3_out));  // open: cin, cout
  ROM #(.addrWidth(10), .dataWidth(32)) rom_3 (.addr(register_3_q[11:2]), .data(rom_3_data));
  Adder #(.width(32)) adder_4 (.a(register_4_q), .b(32'h4), .out(adder_4_out));  // open: cin, cout
  ROM #(.addrWidth(10), .dataWidth(32)) rom_4 (.addr(register_4_q[11:2]), .data(rom_4_data));
  decoder_alt decoder_alt_3 (
    .Instruction(rom_3_data), .immediate(decoder_alt_3_immediate), .op(decoder_alt_3_op),
    .rt(decoder_alt_3_rt), .rs(decoder_alt_3_rs));  // open: adderess, funct, shamt, rd
  Button button_7 (.out(button_7_out));
  decoder_alt decoder_alt_4 (
    .Instruction(rom_4_data), .adderess(decoder_alt_4_adderess), .op(decoder_alt_4_op));  // open: immediate, funct, shamt, rd, rt, rs
  immediateComplement immediatecomplement_2 (
    .Immediate(decoder_alt_3_immediate), .ZeroExtend(1'b0),
    .extendedImmediate(immediatecomplement_2_extendedimmediate));
  Multiplexer #(.width(32)) multiplexer_1 (
    .in0(adder_4_out), .in1(jumpaddress_1_jumpaddress), .out(multiplexer_1_out), .sel(and_1_out));
  not not_1 (not_1_out, decoder_alt_4_op[0]);
  not not_2 (not_2_out, decoder_alt_4_op[2]);
  not not_3 (not_3_out, decoder_alt_4_op[3]);
  not not_4 (not_4_out, decoder_alt_4_op[4]);
  not not_5 (not_5_out, decoder_alt_4_op[5]);
  JumpAddress jumpaddress_1 (
    .Address(decoder_alt_4_adderess), .PCPlus4(adder_4_out), .JumpAddress(jumpaddress_1_jumpaddress));
  not not_6 (not_6_out, decoder_alt_3_op[0]);
  not not_7 (not_7_out, decoder_alt_3_op[1]);
  not not_8 (not_8_out, decoder_alt_3_op[3]);
  not not_9 (not_9_out, decoder_alt_3_op[4]);
  not not_10 (not_10_out, decoder_alt_3_op[5]);
  and and_1 (and_1_out, not_1_out, decoder_alt_4_op[1], not_2_out, not_4_out, not_5_out);
  Shifter #(.width(32)) shifter_1 (
    .in(immediatecomplement_2_extendedimmediate), .\dist (5'b00010), .out(shifter_1_out));
  and and_2 (and_2_out, not_6_out, not_7_out, decoder_alt_3_op[2], not_8_out, not_9_out, not_10_out);
  Multiplexer #(.width(32)) multiplexer_2 (
    .in0(adder_3_out), .in1(adder_5_out), .out(multiplexer_2_out), .sel(and_3_out));
  Adder #(.width(32)) adder_5 (.a(adder_3_out), .b(shifter_1_out), .out(adder_5_out));  // open: cin, cout
  and and_3 (and_3_out, and_2_out, ula_3_isequal);
  RegisterFIle_1_Const registerfile_1_const_2 (
    .WriteEnable(1'b1), .clk(Clock_3), .rst(button_7_out), .R1In(decoder_alt_3_rs), .R2In(decoder_alt_3_rt),
    .R1Out(registerfile_1_const_2_r1out), .R2Out(registerfile_1_const_2_r2out));  // open: RwIn, inData
  ULA ula_3 (
    .A(registerfile_1_const_2_r1out), .B(registerfile_1_const_2_r2out), .ALUOp(4'b0000),
    .isEqual(ula_3_isequal));  // open: SignedOverflow, UnsignedOverflow, Result
  Register #(.width(32)) register_5 (.D(adder_6_out), .en(1'b1), .clk(Clock), .Q(register_5_q), .clr(button_8_out));
  Button button_8 (.out(button_8_out));
  Register #(.width(32)) register_6 (.D(adder_7_out), .en(1'b1), .clk(Clock_4), .Q(register_6_q), .clr(button_9_out));
  Button button_9 (.out(button_9_out));
  ROM #(.addrWidth(10), .dataWidth(32)) rom_5 (.addr(register_5_q[11:2]), .data(rom_5_data));
  ROM #(.addrWidth(10), .dataWidth(32)) rom_6 (.addr(register_6_q[11:2]), .data(rom_6_data));
  Adder #(.width(32)) adder_6 (.a(register_5_q), .b(32'h4), .out(adder_6_out));  // open: cin, cout
  Adder #(.width(32)) adder_7 (.a(register_6_q), .b(32'h4), .out(adder_7_out));  // open: cin, cout
  decoder_alt decoder_alt_5 (
    .Instruction(rom_5_data), .immediate(decoder_alt_5_immediate), .rt(decoder_alt_5_rt),
    .rs(decoder_alt_5_rs));  // open: adderess, funct, op, shamt, rd
  immediateComplement immediatecomplement_3 (
    .Immediate(decoder_alt_5_immediate), .ZeroExtend(1'b0),
    .extendedImmediate(immediatecomplement_3_extendedimmediate));
  decoder_alt decoder_alt_6 (
    .Instruction(rom_6_data), .immediate(decoder_alt_6_immediate), .rt(decoder_alt_6_rt),
    .rs(decoder_alt_6_rs));  // open: adderess, funct, op, shamt, rd
  immediateComplement immediatecomplement_4 (
    .Immediate(decoder_alt_6_immediate), .ZeroExtend(1'b0),
    .extendedImmediate(immediatecomplement_4_extendedimmediate));
  Button button_10 (.out(button_10_out));
  Button button_11 (.out(button_11_out));
  RegisterFile registerfile_2 (
    .RwIn(decoder_alt_5_rt), .inData(ram_1_dout), .WriteEnable(1'b1), .clk(Clock), .rst(button_10_out),
    .R1In(decoder_alt_5_rs), .R1Out(registerfile_2_r1out));  // open: R2In, R2Out
  RegisterFIle_1_Const registerfile_1_const_3 (
    .WriteEnable(1'b1), .clk(Clock_4), .rst(button_11_out), .R1In(decoder_alt_6_rs), .R2In(decoder_alt_6_rt),
    .R1Out(registerfile_1_const_3_r1out), .R2Out(registerfile_1_const_3_r2out));  // open: RwIn, inData
  ULA ula_4 (
    .A(registerfile_2_r1out), .B(immediatecomplement_3_extendedimmediate), .ALUOp(4'b0000),
    .Result(ula_4_result));  // open: SignedOverflow, UnsignedOverflow, isEqual
  ULA ula_5 (
    .A(registerfile_1_const_3_r1out), .B(immediatecomplement_4_extendedimmediate), .ALUOp(4'b0000),
    .Result(ula_5_result));  // open: SignedOverflow, UnsignedOverflow, isEqual
  RAM #(.addrWidth(10), .asyncread("true"), .clearpin("true"), .dataWidth(32)) ram_1 (
    .addr(ula_4_result[11:2]), .we(1'b0), .oe(1'b1), .clk(Clock), .dout(ram_1_dout), .clr(Clear_Memory));  // open: din
  RAM #(.addrWidth(10), .asyncread("true"), .clearpin("true"), .dataWidth(32)) ram_2 (
    .addr(ula_5_result[11:2]), .we(1'b1), .oe(1'b0), .clk(Clock_4), .din(registerfile_1_const_3_r2out),
    .clr(Clear_Memory_2));  // open: dout

  // Notes on the sheet:
  //   Reset_PC
  //   Reset_PC
  //   contents of rom_1 (hex, n*v repeats v):
  //   1005020 14a5020 10a5820 1686020 18c6820 10a6820 16a7020 14a5020 10a5820
  //   contents of rom_2 (hex, n*v repeats v):
  //   20080d08 20090d09 200a0d0a 200b0d0b 200c0d0c 200d0d0d 200e0d0e 200f0d0f 20100d10 20110d11 20120d12
  //   20130d13 20140d14 20150d15 20160d16 20170d17 20180d18 20190d19
  //   ADD
  //   Clear
  //   ADDI
  //   Clear
  //   Reset_PC
  //   Reset_PC
  //   contents of rom_3 (hex, n*v repeats v):
  //   10090005 100a0002 10100003 11090002 100a0002 10100003 10090005 1211fffa 10100003 10100003
  //   contents of rom_4 (hex, n*v repeats v):
  //   0 0 0 8000005 0 0 0 8000002 8000010 8000020
  //   BEQ
  //   Clear
  //   J
  //   Reset_PC
  //   Reset_PC
  //   contents of rom_5 (hex, n*v repeats v):
  //   ac100000 ac110004 ac120008 ac13000c ac140010 ac150014
  //   contents of rom_6 (hex, n*v repeats v):
  //   ac000000 ac000004 ac000008 ac00000c ac000010 ac000014
  //   Clear
  //   Clear
  //   LW
  //   SW
endmodule

module manual_datapath (
  input  Clear,
  input  Reset_Pc,
  input  in_3,
  input  RegDest,
  input  RegWrite,
  input  Branch,
  input  Jump,
  input  ALUSrc,
  input  MEMWrite,
  input  MEMRead,
  input  MEMToReg
);

  wire and_1_out, CLK, ula_1_isequal;
  wire [4:0] decoder_alt_1_rd, decoder_alt_1_rs, decoder_alt_1_rt, multiplexer_1_out;
  wire [5:0] decoder_alt_1_funct, decoder_alt_1_op;
  wire [15:0] decoder_alt_1_immediate;
  wire [25:0] decoder_alt_1_adderess;
  wire [31:0] adder_1_out, adder_2_out, immediatecomplement_1_extendedimmediate, jumpaddress_1_jumpaddress,
       multiplexer_2_out, multiplexer_3_out, multiplexer_4_out, multiplexer_5_out, ram_1_dout, register_1_q,
       registerfile_1_r1out, registerfile_1_r2out, rom_1_data, shifter_1_out, ula_1_result;

  Register #(.width(32)) register_1 (.D(multiplexer_3_out), .en(1'b1), .clk(CLK), .Q(register_1_q), .clr(Reset_Pc));
  ROM #(.addrWidth(10), .dataWidth(32)) rom_1 (.addr(register_1_q[11:2]), .data(rom_1_data));
  decoder_alt decoder_alt_1 (
    .Instruction(rom_1_data), .adderess(decoder_alt_1_adderess), .immediate(decoder_alt_1_immediate),
    .funct(decoder_alt_1_funct), .op(decoder_alt_1_op), .rd(decoder_alt_1_rd), .rt(decoder_alt_1_rt),
    .rs(decoder_alt_1_rs));  // open: shamt
  // Probe on decoder_alt_1_op
  // Probe on decoder_alt_1_funct
  Adder #(.width(32)) adder_1 (.a(register_1_q), .b(32'h4), .out(adder_1_out));  // open: cin, cout
  Clock clock_1 (.out(CLK));
  Multiplexer #(.width(5)) multiplexer_1 (
    .in0(decoder_alt_1_rt), .in1(decoder_alt_1_rd), .out(multiplexer_1_out), .sel(RegDest));
  immediateComplement immediatecomplement_1 (
    .Immediate(decoder_alt_1_immediate), .ZeroExtend(1'b0),
    .extendedImmediate(immediatecomplement_1_extendedimmediate));
  JumpAddress jumpaddress_1 (
    .Address(decoder_alt_1_adderess), .PCPlus4(adder_1_out), .JumpAddress(jumpaddress_1_jumpaddress));
  Shifter #(.width(32)) shifter_1 (
    .in(immediatecomplement_1_extendedimmediate), .\dist (5'b00010), .out(shifter_1_out));
  Adder #(.width(32)) adder_2 (.a(adder_1_out), .b(shifter_1_out), .out(adder_2_out));  // open: cin, cout
  RegisterFile registerfile_1 (
    .RwIn(multiplexer_1_out), .inData(multiplexer_5_out), .WriteEnable(RegWrite), .clk(CLK), .rst(in_3),
    .R1In(decoder_alt_1_rs), .R2In(decoder_alt_1_rt), .R1Out(registerfile_1_r1out),
    .R2Out(registerfile_1_r2out));
  Multiplexer #(.width(32)) multiplexer_2 (
    .in0(adder_1_out), .in1(adder_2_out), .out(multiplexer_2_out), .sel(and_1_out));
  and and_1 (and_1_out, Branch, ula_1_isequal);
  Multiplexer #(.width(32)) multiplexer_3 (
    .in0(multiplexer_2_out), .in1(jumpaddress_1_jumpaddress), .out(multiplexer_3_out), .sel(Jump));
  Multiplexer #(.width(32)) multiplexer_4 (
    .in0(registerfile_1_r2out), .in1(immediatecomplement_1_extendedimmediate), .out(multiplexer_4_out),
    .sel(ALUSrc));
  ULA ula_1 (
    .A(registerfile_1_r1out), .B(multiplexer_4_out), .ALUOp(4'b0000), .isEqual(ula_1_isequal),
    .Result(ula_1_result));  // open: SignedOverflow, UnsignedOverflow
  RAM #(.addrWidth(10), .asyncread("true"), .clearpin("true"), .dataWidth(32)) ram_1 (
    .addr(ula_1_result[11:2]), .we(MEMWrite), .oe(MEMRead), .clk(CLK), .din(registerfile_1_r2out),
    .dout(ram_1_dout), .clr(Clear));
  Multiplexer #(.width(32)) multiplexer_5 (
    .in0(ula_1_result), .in1(ram_1_dout), .out(multiplexer_5_out), .sel(MEMToReg));

  // Notes on the sheet:
  //   Instruction
  //   Type
  //   add
  //   R
  //   addi
  //   I
  //   beq
  //   I
  //   j
  //   j
  //   lw
  //   I
  //   sw
  //   I
  //   Format
  //   rd=rs+rt
  //   rt=rs+imm
  //   if(rs==rt) pc+=offset*4
  //   pc=pc_upper|(target<<2)
  //   R[rt] = M[R[Rs]+SignExtImm]
  //   M[R[rs]+SignExtImm] = R[rt]
  //   Opcode
  //   000000
  //   001000
  //   000100
  //   000010
  //   100011
  //   101011
  //   Funct
  //   100000
  //   N/A
  //   N/A
  //   N/A
  //   N/A
  //   N/A
  //   Control Signals
  //   RegWrite
  //   1
  //   1
  //   0
  //   0
  //   1
  //   0
  //   RegDest
  //   1
  //   0
  //   0
  //   0
  //   0
  //   0
  //   ALUSrc
  //   0
  //   1
  //   0
  //   0
  //   1
  //   1
  //   Branch
  //   0
  //   0
  //   1
  //   0
  //   0
  //   0
  //   Jump
  //   0
  //   0
  //   0
  //   1
  //   0
  //   0
  //   Branch
  //   0
  //   0
  //   1
  //   0
  //   0
  //   0
  //   MemRead
  //   0
  //   0
  //   0
  //   0
  //   1
  //   0
  //   MemWrite
  //   0
  //   0
  //   0
  //   0
  //   0
  //   1
  //   MemToReg
  //   0
  //   0
  //   0
  //   0
  //   0
  //   1
endmodule
