// Logisim project pipeline_2_bubble.circ as structural Verilog: 1 circuit, main circuit main
module main (
  input  Clear_Pipeline,
  input  in_2,
  input  Clear_Memory,
  input  in_4,
  input  in_5
);

  wire and_1_out, and_2_out, CLK, controlunit_1_alusrc, controlunit_1_bne, controlunit_1_branch,
       controlunit_1_isjal, controlunit_1_isjr, controlunit_1_isjump, controlunit_1_isshift,
       controlunit_1_memread, controlunit_1_memtoreg, controlunit_1_memwrite, controlunit_1_readingrs,
       controlunit_1_readingrt, controlunit_1_regdest, controlunit_1_regwrite, controlunit_1_zeroextend,
       ex_mem_1_bne_ex, ex_mem_1_branch_ex, ex_mem_1_isequal_mem, ex_mem_1_isjal_mem, ex_mem_1_isjr_ex,
       ex_mem_1_isjump_ex, ex_mem_1_memread_mem, ex_mem_1_memtoreg_mem, ex_mem_1_memwrite_mem,
       ex_mem_1_regwrite_mem, halt, hazard_detection_unit_1_flushid, hazard_detection_unit_1_stallid,
       hazard_detection_unit_1_stallif, id_ex_1_alusrc_ex, id_ex_1_bne_ex, id_ex_1_branch_ex,
       id_ex_1_isjal_ex, id_ex_1_isjr_ex, id_ex_1_isjump_ex, id_ex_1_isshift_ex, id_ex_1_memread_ex,
       id_ex_1_memtoreg_ex, id_ex_1_memwrite_ex, id_ex_1_regwrite_ex, mem_wb_1_isjal_wb,
       mem_wb_1_memtoreg_wb, mem_wb_1_regwrite_wb, multiplexer_2_out, not_1_out, not_2_out, not_3_out,
       not_4_out, or_1_out, or_2_out, or_3_out, or_4_out, or_5_out, simplebranchhandler_1_clearif,
       ula_1_isequal, xor_1_out;
  wire [3:0] controlunit_1_aluop, id_ex_1_aluop_ex;
  wire [4:0] decoder_alt_1_rd, decoder_alt_1_rs, decoder_alt_1_rt, decoder_alt_1_shamt,
       ex_mem_1_writereg_mem, id_ex_1_writereg_ex, mem_wb_1_writereg_wb, multiplexer_3_out, multiplexer_4_out;
  wire [5:0] decoder_alt_1_funct, decoder_alt_1_op;
  wire [15:0] decoder_alt_1_immediate;
  wire [25:0] decoder_alt_1_adderess;
  wire [31:0] adder_1_out, adder_2_out, bit_extender_1_out, contador_1_numerodeciclos,
       ex_mem_1_aluresult_mem, ex_mem_1_branchdest_mem, ex_mem_1_jrdestmem, ex_mem_1_jumpaddr_mem,
       ex_mem_1_memdata_mem, ex_mem_1_pcplus4_mem, id_ex_1_imm_ex, id_ex_1_jumpaddr_ex, id_ex_1_pcpus4_ex,
       id_ex_1_r1_ex, id_ex_1_r2_ex, id_ex_1_shamt_ex, if_id_1_instruction_id, if_id_1_pcpus4_id,
       immediatecomplement_1_extendedimmediate, jumpaddress_1_jumpaddress, mem_wb_1_aluresult_wb,
       mem_wb_1_datafrommem_wb, mem_wb_1_pcplus4_wb, multiplexer_1_out, multiplexer_5_out, multiplexer_6_out,
       multiplexer_7_out, multiplexer_8_out, multiplexer_9_out, multiplexer_10_out, multiplexer_11_out,
       ram_1_dout, register_1_q, registerfile_1_r1out, registerfile_1_r2out, rom_1_data, shifter_1_out,
       ula_1_result;

  Multiplexer #(.width(32)) multiplexer_1 (
    .in0(adder_1_out), .in1(multiplexer_9_out), .out(multiplexer_1_out), .sel(or_5_out));
  Register #(.width(32)) register_1 (
    .D(multiplexer_1_out), .en(not_1_out), .clk(multiplexer_2_out), .Q(register_1_q), .clr(in_5));
  not not_1 (not_1_out, hazard_detection_unit_1_stallif);
  Multiplexer multiplexer_2 (.in0(CLK), .in1(1'b1), .out(multiplexer_2_out), .sel(halt));
  Clock clock_1 (.out(CLK));
  // Probe on contador_1_numerodeciclos
  Adder #(.width(32)) adder_1 (.a(register_1_q), .b(32'h4), .out(adder_1_out));  // open: cin, cout
  ROM #(.addrWidth(10), .dataWidth(32)) rom_1 (.addr(register_1_q[11:2]), .data(rom_1_data));
  Contador contador_1 (.clkSignal(CLK), .reset(in_2), .NumeroDeCiclos(contador_1_numerodeciclos));
  or or_1 (or_1_out, halt, hazard_detection_unit_1_stallid);
  IF_ID if_id_1 (
    .clk_IF_ID(CLK), .Instruction_IF(rom_1_data), .PCPlus4_IF(adder_1_out), .enable_IF_ID(not_2_out),
    .clr_IF_ID(or_2_out), .Instruction_ID(if_id_1_instruction_id), .PCPus4_ID(if_id_1_pcpus4_id));
  not not_2 (not_2_out, or_1_out);
  or or_2 (or_2_out, Clear_Pipeline, simplebranchhandler_1_clearif);
  decoder_alt decoder_alt_1 (
    .Instruction(if_id_1_instruction_id), .adderess(decoder_alt_1_adderess),
    .immediate(decoder_alt_1_immediate), .funct(decoder_alt_1_funct), .op(decoder_alt_1_op),
    .shamt(decoder_alt_1_shamt), .rd(decoder_alt_1_rd), .rt(decoder_alt_1_rt), .rs(decoder_alt_1_rs));
  immediateComplement immediatecomplement_1 (
    .Immediate(decoder_alt_1_immediate), .ZeroExtend(controlunit_1_zeroextend),
    .extendedImmediate(immediatecomplement_1_extendedimmediate));
  assign bit_extender_1_out = {{27{1'b0}}, decoder_alt_1_shamt};  // Bit_Extender bit_extender_1
  ControlUnit controlunit_1 (
    .opcode(decoder_alt_1_op), .funct(decoder_alt_1_funct), .BNE(controlunit_1_bne),
    .Branch(controlunit_1_branch), .isJump(controlunit_1_isjump), .ZeroExtend(controlunit_1_zeroextend),
    .ALUSrc(controlunit_1_alusrc), .RegWrite(controlunit_1_regwrite), .ReadingRs(controlunit_1_readingrs),
    .ReadingRt(controlunit_1_readingrt), .ALUop(controlunit_1_aluop), .isJAL(controlunit_1_isjal),
    .MemToReg(controlunit_1_memtoreg), .MemRead(controlunit_1_memread), .MemWrite(controlunit_1_memwrite),
    .RegDest(controlunit_1_regdest), .isJR(controlunit_1_isjr), .isShift(controlunit_1_isshift));
  Multiplexer #(.width(5)) multiplexer_3 (
    .in0(decoder_alt_1_rt), .in1(decoder_alt_1_rd), .out(multiplexer_3_out), .sel(controlunit_1_regdest));
  Multiplexer #(.width(5)) multiplexer_4 (
    .in0(multiplexer_3_out), .in1({5{1'b1}}), .out(multiplexer_4_out), .sel(controlunit_1_isjal));
  JumpAddress jumpaddress_1 (
    .Address(decoder_alt_1_adderess), .PCPlus4(if_id_1_pcpus4_id), .JumpAddress(jumpaddress_1_jumpaddress));
  or or_3 (or_3_out, controlunit_1_branch, controlunit_1_isjump, controlunit_1_isjr);
  and and_1 (and_1_out, or_3_out, not_3_out);
  not not_3 (not_3_out, hazard_detection_unit_1_stallif);
  not not_4 (not_4_out, CLK);
  Hazard_Detection_Unit hazard_detection_unit_1 (
    .clk(CLK), .ReadRs(controlunit_1_readingrs), .ReadRt(controlunit_1_readingrt),
    .RegWriteEX(id_ex_1_regwrite_ex), .RegWriteMEM(ex_mem_1_regwrite_mem), .RS(decoder_alt_1_rs),
    .RT(decoder_alt_1_rt), .WriteRegEX(id_ex_1_writereg_ex), .WriteRegMEM(ex_mem_1_writereg_mem),
    .StallIF(hazard_detection_unit_1_stallif), .StallID(hazard_detection_unit_1_stallid),
    .FlushID(hazard_detection_unit_1_flushid));
  simpleBranchHandler simplebranchhandler_1 (
    .isBranch(and_1_out), .clk(CLK), .clear(Clear_Pipeline), .BranchAccepted(or_5_out), .Halt(halt),
    .ClearIF(simplebranchhandler_1_clearif));
  RegisterFile registerfile_1 (
    .RwIn(mem_wb_1_writereg_wb), .inData(multiplexer_11_out), .WriteEnable(mem_wb_1_regwrite_wb),
    .clk(not_4_out), .rst(in_4), .R1In(decoder_alt_1_rs), .R2In(decoder_alt_1_rt),
    .R1Out(registerfile_1_r1out), .R2Out(registerfile_1_r2out));
  ID_EX id_ex_1 (
    .isShift_ID(controlunit_1_isshift), .MemToReg_ID(controlunit_1_memtoreg),
    .RegWrite_ID(controlunit_1_regwrite), .Bne_ID(controlunit_1_bne), .ALUSrc_ID(controlunit_1_alusrc),
    .MemRead_ID(controlunit_1_memread), .MemWrite_ID(controlunit_1_memwrite),
    .isJump_ID(controlunit_1_isjump), .Branch_ID(controlunit_1_branch), .isJR_ID(controlunit_1_isjr),
    .clr_ID_EX(or_4_out), .ALUOp_ID(controlunit_1_aluop), .WriteReg_ID(multiplexer_4_out),
    .isJAL_ID(controlunit_1_isjal), .Imm_ID(immediatecomplement_1_extendedimmediate),
    .R1_ID(registerfile_1_r1out), .R2_ID(registerfile_1_r2out), .Shamt_ID(bit_extender_1_out),
    .JumpAddr_ID(jumpaddress_1_jumpaddress), .enable_ID_EX(1'b1), .clk_ID_EX(CLK),
    .PCPlus4_ID(if_id_1_pcpus4_id), .isShift_EX(id_ex_1_isshift_ex), .MemToReg_EX(id_ex_1_memtoreg_ex),
    .RegWrite_EX(id_ex_1_regwrite_ex), .Bne_EX(id_ex_1_bne_ex), .ALUSrc_EX(id_ex_1_alusrc_ex),
    .MemRead_EX(id_ex_1_memread_ex), .MemWrite_EX(id_ex_1_memwrite_ex), .isJump_EX(id_ex_1_isjump_ex),
    .Branch_EX(id_ex_1_branch_ex), .isJR_EX(id_ex_1_isjr_ex), .ALUOp_EX(id_ex_1_aluop_ex),
    .WriteReg_EX(id_ex_1_writereg_ex), .isJAL_EX(id_ex_1_isjal_ex), .Imm_EX(id_ex_1_imm_ex),
    .R1_EX(id_ex_1_r1_ex), .R2_EX(id_ex_1_r2_ex), .Shamt_EX(id_ex_1_shamt_ex),
    .JumpAddr_EX(id_ex_1_jumpaddr_ex), .PCPus4_EX(id_ex_1_pcpus4_ex));
  or or_4 (or_4_out, hazard_detection_unit_1_flushid, Clear_Pipeline);
  Shifter #(.width(32)) shifter_1 (.in(id_ex_1_imm_ex), .\dist (5'b00010), .out(shifter_1_out));
  Multiplexer #(.width(32)) multiplexer_5 (
    .in0(id_ex_1_r2_ex), .in1(id_ex_1_imm_ex), .out(multiplexer_5_out), .sel(id_ex_1_alusrc_ex));
  Adder #(.width(32)) adder_2 (.a(id_ex_1_pcpus4_ex), .b(shifter_1_out), .out(adder_2_out));  // open: cin, cout
  Multiplexer #(.width(32)) multiplexer_6 (
    .in0(id_ex_1_r1_ex), .in1(id_ex_1_r2_ex), .out(multiplexer_6_out), .sel(id_ex_1_isshift_ex));
  Multiplexer #(.width(32)) multiplexer_7 (
    .in0(multiplexer_5_out), .in1(id_ex_1_shamt_ex), .out(multiplexer_7_out), .sel(id_ex_1_isshift_ex));
  ULA ula_1 (
    .A(multiplexer_6_out), .B(multiplexer_7_out), .ALUOp(id_ex_1_aluop_ex), .isEqual(ula_1_isequal),
    .Result(ula_1_result));  // open: SignedOverflow, UnsignedOverflow
  EX_MEM ex_mem_1 (
    .isJAL_EX(id_ex_1_isjal_ex), .MemToReg_EX(id_ex_1_memtoreg_ex), .RegWrite_EX(id_ex_1_regwrite_ex),
    .MemRead_EX(id_ex_1_memread_ex), .MemWrite_EX(id_ex_1_memwrite_ex), .Bne_ID(id_ex_1_bne_ex),
    .isJump_ID(id_ex_1_isjump_ex), .Branch_ID(id_ex_1_branch_ex), .isJR_ID(id_ex_1_isjr_ex),
    .isEqual_EX(ula_1_isequal), .clr_EX_MEM(Clear_Pipeline), .ALUResult_EX(ula_1_result),
    .MemData_EX(id_ex_1_r2_ex), .WriteReg_EX(id_ex_1_writereg_ex), .PCPlus4_EX(id_ex_1_pcpus4_ex),
    .JumpAddr_EX(id_ex_1_jumpaddr_ex), .enable_EX_MEM(1'b1), .clk_EX_MEM(CLK), .BranchDest_EX(adder_2_out),
    .JRDest_EX(id_ex_1_r1_ex), .isJAL_MEM(ex_mem_1_isjal_mem), .MemToReg_MEM(ex_mem_1_memtoreg_mem),
    .RegWrite_MEM(ex_mem_1_regwrite_mem), .MemRead_MEM(ex_mem_1_memread_mem),
    .MemWrite_MEM(ex_mem_1_memwrite_mem), .Bne_EX(ex_mem_1_bne_ex), .isJump_EX(ex_mem_1_isjump_ex),
    .Branch_EX(ex_mem_1_branch_ex), .isJR_EX(ex_mem_1_isjr_ex), .isEqual_MEM(ex_mem_1_isequal_mem),
    .ALUResult_MEM(ex_mem_1_aluresult_mem), .MemData_MEM(ex_mem_1_memdata_mem),
    .WriteReg_MEM(ex_mem_1_writereg_mem), .PCPlus4_MEM(ex_mem_1_pcplus4_mem),
    .JumpAddr_MEM(ex_mem_1_jumpaddr_mem), .BranchDest_MEM(ex_mem_1_branchdest_mem),
    .JRDestMEM(ex_mem_1_jrdestmem));
  xor xor_1 (xor_1_out, ex_mem_1_bne_ex, ex_mem_1_isequal_mem);
  and and_2 (and_2_out, xor_1_out, ex_mem_1_branch_ex);
  RAM #(.addrWidth(10), .asyncread("true"), .clearpin("true"), .dataWidth(32)) ram_1 (
    .addr(ex_mem_1_aluresult_mem[11:2]), .we(ex_mem_1_memwrite_mem), .oe(ex_mem_1_memread_mem), .clk(CLK),
    .din(ex_mem_1_memdata_mem), .dout(ram_1_dout), .clr(Clear_Memory));
  Multiplexer #(.width(32)) multiplexer_8 (
    .in0(ex_mem_1_branchdest_mem), .in1(ex_mem_1_jumpaddr_mem), .out(multiplexer_8_out),
    .sel(ex_mem_1_isjump_ex));
  or or_5 (or_5_out, and_2_out, ex_mem_1_isjump_ex, ex_mem_1_isjr_ex);
  Multiplexer #(.width(32)) multiplexer_9 (
    .in0(multiplexer_8_out), .in1(ex_mem_1_jrdestmem), .out(multiplexer_9_out), .sel(ex_mem_1_isjr_ex));
  MEM_WB mem_wb_1 (
    .clr_MEM_WB(Clear_Pipeline), .ALUResult_MEM(ex_mem_1_aluresult_mem), .DataFromMem_MEM(ram_1_dout),
    .WriteReg_MEM(ex_mem_1_writereg_mem), .PCPlus4_MEM(ex_mem_1_pcplus4_mem), .enable_MEM_WB(1'b1),
    .clk_MEM_WB(CLK), .isJAL_MEM(ex_mem_1_isjal_mem), .MemToReg_MEM(ex_mem_1_memtoreg_mem),
    .RegWrite_MEM(ex_mem_1_regwrite_mem), .ALUResult_WB(mem_wb_1_aluresult_wb),
    .DataFromMem_WB(mem_wb_1_datafrommem_wb), .WriteReg_WB(mem_wb_1_writereg_wb),
    .PCPlus4_WB(mem_wb_1_pcplus4_wb), .isJAL_WB(mem_wb_1_isjal_wb), .MemToReg_WB(mem_wb_1_memtoreg_wb),
    .RegWrite_WB(mem_wb_1_regwrite_wb));
  Multiplexer #(.width(32)) multiplexer_10 (
    .in0(mem_wb_1_aluresult_wb), .in1(mem_wb_1_datafrommem_wb), .out(multiplexer_10_out),
    .sel(mem_wb_1_memtoreg_wb));
  Multiplexer #(.width(32)) multiplexer_11 (
    .in0(multiplexer_10_out), .in1(mem_wb_1_pcplus4_wb), .out(multiplexer_11_out), .sel(mem_wb_1_isjal_wb));

  // Other names for the same wires on the sheet: Clear = Clear_Pipeline

  // Notes on the sheet:
  //   Clear PC
  //   contents of rom_1 (hex, n*v repeats v):
  //   8d0a0000 21080004 20a8020 8d0a0000 21080004 20a8020 8d0a0000 21080004 20a8020 8d0a0000 21080004
  //   20a8020 8d0a0000 21080004 20a8020 8d0a0000 21080004 20a8020 8d0a0000 21080004 20a8020 8d0a0000
  //   21080004 20a8020 8d0a0000 21080004 20a8020 8d0a0000 21080004 20a8020 800001e
endmodule
