// Logisim project pipeline_2_v2_fw.circ as structural Verilog: 1 circuit, main circuit main
module main (
  input  Clear_Pipeline,
  input  Clear_Memory,
  input  in_3,
  input  in_4
);

  wire and_1_out, and_2_out, branchhandlerv2_1_halt, CLK, comparator_1_eq, controlunit_1_alusrc,
       controlunit_1_bne, controlunit_1_branch, controlunit_1_isjal, controlunit_1_isjr,
       controlunit_1_isjump, controlunit_1_isshift, controlunit_1_memread, controlunit_1_memtoreg,
       controlunit_1_memwrite, controlunit_1_readingrs, controlunit_1_readingrt, controlunit_1_regdest,
       controlunit_1_regwrite, controlunit_1_zeroextend, ex_memv2_1_isjal_mem, ex_memv2_1_memread_mem,
       ex_memv2_1_memtoreg_mem, ex_memv2_1_memwrite_mem, ex_memv2_1_regwrite_mem,
       forwarding_unit_1_hasforwarded, id_exv2_1_alusrc_ex, id_exv2_1_isjal_ex, id_exv2_1_isshift_ex,
       id_exv2_1_memread_ex, id_exv2_1_memtoreg_ex, id_exv2_1_memwrite_ex, id_exv2_1_regwrite_ex,
       lw_hazard_handler_1_flushid, lw_hazard_handler_1_stallid, lw_hazard_handler_1_stallif,
       mem_wb_1_isjal_wb, mem_wb_1_memtoreg_wb, mem_wb_1_regwrite_wb, not_1_out, not_2_out, not_3_out,
       not_4_out, or_1_out, or_2_out, or_3_out, or_4_out, xor_1_out;
  wire [1:0] forwarding_unit_1_rssource, forwarding_unit_1_rtsource;
  wire [3:0] controlunit_1_aluop, id_exv2_1_aluop_ex;
  wire [4:0] decoder_alt_1_rd, decoder_alt_1_rs, decoder_alt_1_rt, decoder_alt_1_shamt,
       ex_memv2_1_writereg_mem, id_exv2_1_writereg_ex, mem_wb_1_writereg_wb, multiplexer_2_out,
       multiplexer_3_out;
  wire [5:0] decoder_alt_1_funct, decoder_alt_1_op;
  wire [15:0] decoder_alt_1_immediate;
  wire [25:0] decoder_alt_1_adderess;
  wire [31:0] adder_1_out, adder_2_out, bit_extender_1_out, ex_memv2_1_aluresult_mem, ex_memv2_1_memdata_mem,
       ex_memv2_1_pcplus4_mem, id_exv2_1_imm_ex, id_exv2_1_pcpus4_ex, id_exv2_1_r1_ex, id_exv2_1_r2_ex,
       id_exv2_1_shamt_ex, if_id_1_instruction_id, if_id_1_pcpus4_id,
       immediatecomplement_1_extendedimmediate, jumpaddress_1_jumpaddress, mem_wb_1_aluresult_wb,
       mem_wb_1_datafrommem_wb, mem_wb_1_pcplus4_wb, multiplexer_1_out, multiplexer_4_out, multiplexer_5_out,
       multiplexer_6_out, multiplexer_7_out, multiplexer_8_out, multiplexer_9_out, multiplexer_10_out,
       multiplexer_11_out, multiplexer_12_out, multiplexer_13_out, multiplexer_14_out, ram_1_dout,
       register_1_q, registerfile_1_r1out, registerfile_1_r2out, rom_1_data, shifter_1_out, ula_1_result;

  Multiplexer #(.width(32)) multiplexer_1 (
    .in0(adder_1_out), .in1(multiplexer_6_out), .out(multiplexer_1_out), .sel(or_3_out));
  Register #(.width(32)) register_1 (.D(multiplexer_1_out), .en(not_1_out), .clk(CLK), .Q(register_1_q), .clr(in_4));
  not not_1 (not_1_out, lw_hazard_handler_1_stallif);
  Clock clock_1 (.out(CLK));
  Adder #(.width(32)) adder_1 (.a(register_1_q), .b(32'h4), .out(adder_1_out));  // open: cin, cout
  ROM #(.addrWidth(10), .dataWidth(32)) rom_1 (.addr(register_1_q[11:2]), .data(rom_1_data));
  IF_ID if_id_1 (
    .clk_IF_ID(CLK), .Instruction_IF(rom_1_data), .PCPlus4_IF(adder_1_out), .enable_IF_ID(not_2_out),
    .clr_IF_ID(or_1_out), .Instruction_ID(if_id_1_instruction_id), .PCPus4_ID(if_id_1_pcpus4_id));
  not not_2 (not_2_out, lw_hazard_handler_1_stallid);
  or or_1 (or_1_out, Clear_Pipeline, branchhandlerv2_1_halt);
  decoder_alt decoder_alt_1 (
    .Instruction(if_id_1_instruction_id), .adderess(decoder_alt_1_adderess),
    .immediate(decoder_alt_1_immediate), .funct(decoder_alt_1_funct), .op(decoder_alt_1_op),
    .shamt(decoder_alt_1_shamt), .rd(decoder_alt_1_rd), .rt(decoder_alt_1_rt), .rs(decoder_alt_1_rs));
  or or_2 (or_2_out, controlunit_1_branch, controlunit_1_isjump, controlunit_1_isjr);
  immediateComplement immediatecomplement_1 (
    .Immediate(decoder_alt_1_immediate), .ZeroExtend(controlunit_1_zeroextend),
    .extendedImmediate(immediatecomplement_1_extendedimmediate));
  assign bit_extender_1_out = {{27{1'b0}}, decoder_alt_1_shamt};  // Bit_Extender bit_extender_1
  not not_3 (not_3_out, lw_hazard_handler_1_stallif);
  and and_1 (and_1_out, not_3_out, or_2_out);
  ControlUnit controlunit_1 (
    .opcode(decoder_alt_1_op), .funct(decoder_alt_1_funct), .BNE(controlunit_1_bne),
    .Branch(controlunit_1_branch), .isJump(controlunit_1_isjump), .ZeroExtend(controlunit_1_zeroextend),
    .ALUSrc(controlunit_1_alusrc), .RegWrite(controlunit_1_regwrite), .ReadingRs(controlunit_1_readingrs),
    .ReadingRt(controlunit_1_readingrt), .ALUop(controlunit_1_aluop), .isJAL(controlunit_1_isjal),
    .MemToReg(controlunit_1_memtoreg), .MemRead(controlunit_1_memread), .MemWrite(controlunit_1_memwrite),
    .RegDest(controlunit_1_regdest), .isJR(controlunit_1_isjr), .isShift(controlunit_1_isshift));
  Multiplexer #(.width(5)) multiplexer_2 (
    .in0(decoder_alt_1_rt), .in1(decoder_alt_1_rd), .out(multiplexer_2_out), .sel(controlunit_1_regdest));
  BranchHandlerv2 branchhandlerv2_1 (
    .isBranch(and_1_out), .clk(CLK), .clear(Clear_Pipeline), .BranchAccepted(or_3_out),
    .Halt(branchhandlerv2_1_halt));
  Multiplexer #(.width(5)) multiplexer_3 (
    .in0(multiplexer_2_out), .in1({5{1'b1}}), .out(multiplexer_3_out), .sel(controlunit_1_isjal));
  JumpAddress jumpaddress_1 (
    .Address(decoder_alt_1_adderess), .PCPlus4(if_id_1_pcpus4_id), .JumpAddress(jumpaddress_1_jumpaddress));
  not not_4 (not_4_out, CLK);
  Shifter #(.width(32)) shifter_1 (
    .in(immediatecomplement_1_extendedimmediate), .\dist (5'b00010), .out(shifter_1_out));
  Comparator #(.width(32)) comparator_1 (
    .a(multiplexer_8_out), .b(multiplexer_7_out), .eq(comparator_1_eq));  // open: gt, lt
  and and_2 (and_2_out, controlunit_1_branch, xor_1_out);
  xor xor_1 (xor_1_out, comparator_1_eq, controlunit_1_bne);
  Adder #(.width(32)) adder_2 (.a(if_id_1_pcpus4_id), .b(shifter_1_out), .out(adder_2_out));  // open: cin, cout
  LW_Hazard_Handler lw_hazard_handler_1 (
    .clk(CLK), .DataForwarded(forwarding_unit_1_hasforwarded), .isLW(id_exv2_1_memread_ex),
    .StallIF(lw_hazard_handler_1_stallif), .StallID(lw_hazard_handler_1_stallid),
    .FlushID(lw_hazard_handler_1_flushid));
  Multiplexer #(.width(32)) multiplexer_4 (
    .in0(if_id_1_pcpus4_id), .in1(adder_2_out), .out(multiplexer_4_out), .sel(and_2_out));
  Multiplexer #(.width(32)) multiplexer_5 (
    .in0(multiplexer_4_out), .in1(jumpaddress_1_jumpaddress), .out(multiplexer_5_out),
    .sel(controlunit_1_isjump));
  RegisterFile registerfile_1 (
    .RwIn(mem_wb_1_writereg_wb), .inData(multiplexer_14_out), .WriteEnable(mem_wb_1_regwrite_wb),
    .clk(not_4_out), .rst(in_3), .R1In(decoder_alt_1_rs), .R2In(decoder_alt_1_rt),
    .R1Out(registerfile_1_r1out), .R2Out(registerfile_1_r2out));
  or or_3 (or_3_out, and_2_out, controlunit_1_isjr, controlunit_1_isjump);
  Multiplexer #(.width(32)) multiplexer_6 (
    .in0(multiplexer_5_out), .in1(multiplexer_7_out), .out(multiplexer_6_out), .sel(controlunit_1_isjr));
  Forwarding_Unit forwarding_unit_1 (
    .ReadRs(controlunit_1_readingrs), .ReadRt(controlunit_1_readingrt), .RegWriteEX(id_exv2_1_regwrite_ex),
    .RegWriteMEM(ex_memv2_1_regwrite_mem), .RS(decoder_alt_1_rs), .RT(decoder_alt_1_rt),
    .WriteRegEX(id_exv2_1_writereg_ex), .WriteRegMEM(ex_memv2_1_writereg_mem),
    .RsSource(forwarding_unit_1_rssource), .RtSource(forwarding_unit_1_rtsource),
    .HasForwarded(forwarding_unit_1_hasforwarded));
  Multiplexer #(.select(2), .width(32)) multiplexer_7 (
    .in0(registerfile_1_r1out), .in1(ula_1_result), .in2(multiplexer_12_out), .out(multiplexer_7_out),
    .sel(forwarding_unit_1_rssource));  // open: in3
  Multiplexer #(.select(2), .width(32)) multiplexer_8 (
    .in0(registerfile_1_r2out), .in1(ula_1_result), .in2(multiplexer_12_out), .out(multiplexer_8_out),
    .sel(forwarding_unit_1_rtsource));  // open: in3
  ID_EXv2 id_exv2_1 (
    .isShift_ID(controlunit_1_isshift), .MemToReg_ID(controlunit_1_memtoreg),
    .RegWrite_ID(controlunit_1_regwrite), .ALUSrc_ID(controlunit_1_alusrc),
    .MemRead_ID(controlunit_1_memread), .MemWrite_ID(controlunit_1_memwrite), .ALUOp_ID(controlunit_1_aluop),
    .WriteReg_ID(multiplexer_3_out), .isJAL_ID(controlunit_1_isjal), .clr_ID_EX(or_4_out),
    .Imm_ID(immediatecomplement_1_extendedimmediate), .R1_ID(multiplexer_7_out), .R2_ID(multiplexer_8_out),
    .Shamt_ID(bit_extender_1_out), .enable_ID_EX(1'b1), .clk_ID_EX(CLK), .PCPlus4_ID(if_id_1_pcpus4_id),
    .isShift_EX(id_exv2_1_isshift_ex), .MemToReg_EX(id_exv2_1_memtoreg_ex),
    .RegWrite_EX(id_exv2_1_regwrite_ex), .ALUSrc_EX(id_exv2_1_alusrc_ex), .MemRead_EX(id_exv2_1_memread_ex),
    .MemWrite_EX(id_exv2_1_memwrite_ex), .ALUOp_EX(id_exv2_1_aluop_ex), .WriteReg_EX(id_exv2_1_writereg_ex),
    .isJAL_EX(id_exv2_1_isjal_ex), .Imm_EX(id_exv2_1_imm_ex), .R1_EX(id_exv2_1_r1_ex),
    .R2_EX(id_exv2_1_r2_ex), .Shamt_EX(id_exv2_1_shamt_ex), .PCPus4_EX(id_exv2_1_pcpus4_ex));  // open: JumpAddr_ID, JumpAddr_EX
  or or_4 (or_4_out, lw_hazard_handler_1_flushid, Clear_Pipeline);
  Multiplexer #(.width(32)) multiplexer_9 (
    .in0(id_exv2_1_r2_ex), .in1(id_exv2_1_imm_ex), .out(multiplexer_9_out), .sel(id_exv2_1_alusrc_ex));
  Multiplexer #(.width(32)) multiplexer_10 (
    .in0(id_exv2_1_r1_ex), .in1(id_exv2_1_r2_ex), .out(multiplexer_10_out), .sel(id_exv2_1_isshift_ex));
  Multiplexer #(.width(32)) multiplexer_11 (
    .in0(multiplexer_9_out), .in1(id_exv2_1_shamt_ex), .out(multiplexer_11_out), .sel(id_exv2_1_isshift_ex));
  ULA ula_1 (
    .A(multiplexer_10_out), .B(multiplexer_11_out), .ALUOp(id_exv2_1_aluop_ex), .Result(ula_1_result));  // open: SignedOverflow, UnsignedOverflow, isEqual
  EX_MEMv2 ex_memv2_1 (
    .clr_EX_MEM(Clear_Pipeline), .ALUResult_EX(ula_1_result), .MemData_EX(id_exv2_1_r2_ex),
    .WriteReg_EX(id_exv2_1_writereg_ex), .PCPlus4_EX(id_exv2_1_pcpus4_ex), .enable_EX_MEM(1'b1),
    .clk_EX_MEM(CLK), .isJAL_EX(id_exv2_1_isjal_ex), .MemToReg_EX(id_exv2_1_memtoreg_ex),
    .RegWrite_EX(id_exv2_1_regwrite_ex), .MemRead_EX(id_exv2_1_memread_ex),
    .MemWrite_EX(id_exv2_1_memwrite_ex), .ALUResult_MEM(ex_memv2_1_aluresult_mem),
    .MemData_MEM(ex_memv2_1_memdata_mem), .WriteReg_MEM(ex_memv2_1_writereg_mem),
    .PCPlus4_MEM(ex_memv2_1_pcplus4_mem), .isJAL_MEM(ex_memv2_1_isjal_mem),
    .MemToReg_MEM(ex_memv2_1_memtoreg_mem), .RegWrite_MEM(ex_memv2_1_regwrite_mem),
    .MemRead_MEM(ex_memv2_1_memread_mem), .MemWrite_MEM(ex_memv2_1_memwrite_mem));
  RAM #(.addrWidth(10), .asyncread("true"), .clearpin("true"), .dataWidth(32)) ram_1 (
    .addr(ex_memv2_1_aluresult_mem[11:2]), .we(ex_memv2_1_memwrite_mem), .oe(ex_memv2_1_memread_mem),
    .clk(CLK), .din(ex_memv2_1_memdata_mem), .dout(ram_1_dout), .clr(Clear_Memory));
  Multiplexer #(.width(32)) multiplexer_12 (
    .in0(ex_memv2_1_aluresult_mem), .in1(ram_1_dout), .out(multiplexer_12_out), .sel(ex_memv2_1_memtoreg_mem));
  MEM_WB mem_wb_1 (
    .clr_MEM_WB(Clear_Pipeline), .ALUResult_MEM(ex_memv2_1_aluresult_mem), .DataFromMem_MEM(ram_1_dout),
    .WriteReg_MEM(ex_memv2_1_writereg_mem), .PCPlus4_MEM(ex_memv2_1_pcplus4_mem), .enable_MEM_WB(1'b1),
    .clk_MEM_WB(CLK), .isJAL_MEM(ex_memv2_1_isjal_mem), .MemToReg_MEM(ex_memv2_1_memtoreg_mem),
    .RegWrite_MEM(ex_memv2_1_regwrite_mem), .ALUResult_WB(mem_wb_1_aluresult_wb),
    .DataFromMem_WB(mem_wb_1_datafrommem_wb), .WriteReg_WB(mem_wb_1_writereg_wb),
    .PCPlus4_WB(mem_wb_1_pcplus4_wb), .isJAL_WB(mem_wb_1_isjal_wb), .MemToReg_WB(mem_wb_1_memtoreg_wb),
    .RegWrite_WB(mem_wb_1_regwrite_wb));
  Multiplexer #(.width(32)) multiplexer_13 (
    .in0(mem_wb_1_aluresult_wb), .in1(mem_wb_1_datafrommem_wb), .out(multiplexer_13_out),
    .sel(mem_wb_1_memtoreg_wb));
  Multiplexer #(.width(32)) multiplexer_14 (
    .in0(multiplexer_13_out), .in1(mem_wb_1_pcplus4_wb), .out(multiplexer_14_out), .sel(mem_wb_1_isjal_wb));

  // Other names for the same wires on the sheet: Clear = Clear_Pipeline

  // Notes on the sheet:
  //   Clear PC
endmodule
