// Logisim project pipeline_2_v2_fw_JTB.circ as structural Verilog: 4 circuits, main circuit main
module main (
  input  Clear_Pipeline,
  input  Clear_Memory,
  input  in_3,
  input  in_4,
  input  Clear
);

  wire and_1_out, and_2_out, branchhandlerv2_1_halt, CLK, comparator_1_eq, controlunit_1_alusrc,
       controlunit_1_bne, controlunit_1_branch, controlunit_1_isjal, controlunit_1_isjr,
       controlunit_1_isjump, controlunit_1_isshift, controlunit_1_memread, controlunit_1_memtoreg,
       controlunit_1_memwrite, controlunit_1_readingrs, controlunit_1_readingrt, controlunit_1_regdest,
       controlunit_1_regwrite, controlunit_1_zeroextend, ex_memv2_1_isjal_mem, ex_memv2_1_memread_mem,
       ex_memv2_1_memtoreg_mem, ex_memv2_1_memwrite_mem, ex_memv2_1_regwrite_mem,
       forwarding_unit_1_hasforwarded, id_exv2_1_alusrc_ex, id_exv2_1_isjal_ex, id_exv2_1_isshift_ex,
       id_exv2_1_memread_ex, id_exv2_1_memtoreg_ex, id_exv2_1_memwrite_ex, id_exv2_1_regwrite_ex,
       if_id_jtb_1_updatejtb_id, jtb_1_hit, jtb_1_needupdate, lw_hazard_handler_1_flushid,
       lw_hazard_handler_1_stallid, lw_hazard_handler_1_stallif, mem_wb_1_isjal_wb, mem_wb_1_memtoreg_wb,
       mem_wb_1_regwrite_wb, not_1_out, not_2_out, not_3_out, not_4_out, or_1_out, or_2_out, or_3_out,
       or_4_out, xor_1_out;
  wire [1:0] forwarding_unit_1_rssource, forwarding_unit_1_rtsource;
  wire [3:0] controlunit_1_aluop, id_exv2_1_aluop_ex;
  wire [4:0] decoder_alt_1_rd, decoder_alt_1_rs, decoder_alt_1_rt, decoder_alt_1_shamt,
       ex_memv2_1_writereg_mem, id_exv2_1_writereg_ex, mem_wb_1_writereg_wb, multiplexer_5_out,
       multiplexer_6_out;
  wire [5:0] decoder_alt_1_funct, decoder_alt_1_op;
  wire [15:0] decoder_alt_1_immediate;
  wire [25:0] decoder_alt_1_adderess;
  wire [31:0] adder_1_out, adder_2_out, adder_3_out, bit_extender_1_out, ex_memv2_1_aluresult_mem,
       ex_memv2_1_memdata_mem, ex_memv2_1_pcplus4_mem, id_exv2_1_imm_ex, id_exv2_1_pcpus4_ex,
       id_exv2_1_r1_ex, id_exv2_1_r2_ex, id_exv2_1_shamt_ex, if_id_jtb_1_instruction_id,
       immediatecomplement_1_extendedimmediate, jtb_1_instructionout, jumpaddress_1_jumpaddress,
       mem_wb_1_aluresult_wb, mem_wb_1_datafrommem_wb, mem_wb_1_pcplus4_wb, multiplexer_1_out,
       multiplexer_2_out, multiplexer_3_out, multiplexer_4_out, multiplexer_7_out, multiplexer_8_out,
       multiplexer_9_out, multiplexer_10_out, multiplexer_11_out, multiplexer_12_out, multiplexer_13_out,
       multiplexer_14_out, multiplexer_15_out, multiplexer_16_out, multiplexer_17_out, ram_1_dout,
       register_1_q, registerfile_1_r1out, registerfile_1_r2out, rom_1_data, shifter_1_out, TPCPlus4EX,
       ula_1_result;

  Adder #(.width(32)) adder_1 (.a(register_1_q), .b(32'h4), .out(adder_1_out));  // open: cin, cout
  jtb jtb_1 (
    .newpc(TPCPlus4EX), .update(if_id_jtb_1_updatejtb_id), .target(jumpaddress_1_jumpaddress), .clear(Clear),
    .pcIn(adder_1_out), .instruction(rom_1_data), .clk(CLK), .hit(jtb_1_hit),
    .instructionOut(jtb_1_instructionout), .needUpdate(jtb_1_needupdate));
  Multiplexer #(.width(32)) multiplexer_1 (
    .in0(multiplexer_3_out), .in1(multiplexer_9_out), .out(multiplexer_1_out), .sel(or_3_out));
  Register #(.width(32)) register_1 (.D(multiplexer_2_out), .en(not_1_out), .clk(CLK), .Q(register_1_q), .clr(in_4));
  not not_1 (not_1_out, lw_hazard_handler_1_stallif);
  Multiplexer #(.width(32)) multiplexer_2 (
    .in0(multiplexer_1_out), .in1(multiplexer_3_out), .out(multiplexer_2_out), .sel(jtb_1_hit));
  Multiplexer #(.width(32)) multiplexer_3 (
    .in0(adder_1_out), .in1(adder_2_out), .out(multiplexer_3_out), .sel(jtb_1_hit));
  Adder #(.width(32)) adder_2 (.a(jtb_1_instructionout), .b(32'h4), .out(adder_2_out));  // open: cin, cout
  Multiplexer #(.width(32)) multiplexer_4 (
    .in0(register_1_q), .in1(jtb_1_instructionout), .out(multiplexer_4_out), .sel(jtb_1_hit));
  ROM #(.addrWidth(10), .dataWidth(32)) rom_1 (.addr(multiplexer_4_out[11:2]), .data(rom_1_data));
  Clock clock_1 (.out(CLK));
  not not_2 (not_2_out, lw_hazard_handler_1_stallid);
  IF_ID_JTB if_id_jtb_1 (
    .clk_IF_ID(CLK), .Instruction_IF(rom_1_data), .PCPlus4_IF(multiplexer_3_out),
    .updateJTB_IF(jtb_1_needupdate), .enable_IF_ID(not_2_out), .clr_IF_ID(or_1_out),
    .Instruction_ID(if_id_jtb_1_instruction_id), .PCPus4_ID(TPCPlus4EX),
    .updateJTB_ID(if_id_jtb_1_updatejtb_id));
  or or_1 (or_1_out, Clear_Pipeline, branchhandlerv2_1_halt);
  // Probe on if_id_jtb_1_instruction_id
  decoder_alt decoder_alt_1 (
    .Instruction(if_id_jtb_1_instruction_id), .adderess(decoder_alt_1_adderess),
    .immediate(decoder_alt_1_immediate), .funct(decoder_alt_1_funct), .op(decoder_alt_1_op),
    .shamt(decoder_alt_1_shamt), .rd(decoder_alt_1_rd), .rt(decoder_alt_1_rt), .rs(decoder_alt_1_rs));
  not not_3 (not_3_out, lw_hazard_handler_1_stallif);
  or or_2 (or_2_out, controlunit_1_branch, controlunit_1_isjump, controlunit_1_isjr);
  immediateComplement immediatecomplement_1 (
    .Immediate(decoder_alt_1_immediate), .ZeroExtend(controlunit_1_zeroextend),
    .extendedImmediate(immediatecomplement_1_extendedimmediate));
  assign bit_extender_1_out = {{27{1'b0}}, decoder_alt_1_shamt};  // Bit_Extender bit_extender_1
  and and_1 (and_1_out, not_3_out, or_2_out);
  ControlUnit controlunit_1 (
    .opcode(decoder_alt_1_op), .funct(decoder_alt_1_funct), .BNE(controlunit_1_bne),
    .Branch(controlunit_1_branch), .isJump(controlunit_1_isjump), .ZeroExtend(controlunit_1_zeroextend),
    .ALUSrc(controlunit_1_alusrc), .RegWrite(controlunit_1_regwrite), .ReadingRs(controlunit_1_readingrs),
    .ReadingRt(controlunit_1_readingrt), .ALUop(controlunit_1_aluop), .isJAL(controlunit_1_isjal),
    .MemToReg(controlunit_1_memtoreg), .MemRead(controlunit_1_memread), .MemWrite(controlunit_1_memwrite),
    .RegDest(controlunit_1_regdest), .isJR(controlunit_1_isjr), .isShift(controlunit_1_isshift));
  Multiplexer #(.width(5)) multiplexer_5 (
    .in0(decoder_alt_1_rt), .in1(decoder_alt_1_rd), .out(multiplexer_5_out), .sel(controlunit_1_regdest));
  JumpAddress jumpaddress_1 (
    .Address(decoder_alt_1_adderess), .PCPlus4(TPCPlus4EX), .JumpAddress(jumpaddress_1_jumpaddress));
  BranchHandlerv2 branchhandlerv2_1 (
    .isBranch(and_1_out), .clk(CLK), .clear(Clear_Pipeline), .BranchAccepted(or_3_out),
    .Halt(branchhandlerv2_1_halt));
  Multiplexer #(.width(5)) multiplexer_6 (
    .in0(multiplexer_5_out), .in1({5{1'b1}}), .out(multiplexer_6_out), .sel(controlunit_1_isjal));
  not not_4 (not_4_out, CLK);
  Comparator #(.width(32)) comparator_1 (
    .a(multiplexer_11_out), .b(multiplexer_10_out), .eq(comparator_1_eq));  // open: gt, lt
  and and_2 (and_2_out, controlunit_1_branch, xor_1_out);
  Shifter #(.width(32)) shifter_1 (
    .in(immediatecomplement_1_extendedimmediate), .\dist (5'b00010), .out(shifter_1_out));
  LW_Hazard_Handler lw_hazard_handler_1 (
    .clk(CLK), .DataForwarded(forwarding_unit_1_hasforwarded), .isLW(id_exv2_1_memread_ex),
    .StallIF(lw_hazard_handler_1_stallif), .StallID(lw_hazard_handler_1_stallid),
    .FlushID(lw_hazard_handler_1_flushid));
  xor xor_1 (xor_1_out, comparator_1_eq, controlunit_1_bne);
  Multiplexer #(.width(32)) multiplexer_7 (
    .in0(TPCPlus4EX), .in1(adder_3_out), .out(multiplexer_7_out), .sel(and_2_out));
  Adder #(.width(32)) adder_3 (.a(TPCPlus4EX), .b(shifter_1_out), .out(adder_3_out));  // open: cin, cout
  RegisterFile registerfile_1 (
    .RwIn(mem_wb_1_writereg_wb), .inData(multiplexer_17_out), .WriteEnable(mem_wb_1_regwrite_wb),
    .clk(not_4_out), .rst(in_3), .R1In(decoder_alt_1_rs), .R2In(decoder_alt_1_rt),
    .R1Out(registerfile_1_r1out), .R2Out(registerfile_1_r2out));
  Multiplexer #(.width(32)) multiplexer_8 (
    .in0(multiplexer_7_out), .in1(jumpaddress_1_jumpaddress), .out(multiplexer_8_out),
    .sel(controlunit_1_isjump));
  Multiplexer #(.width(32)) multiplexer_9 (
    .in0(multiplexer_8_out), .in1(multiplexer_10_out), .out(multiplexer_9_out), .sel(controlunit_1_isjr));
  or or_3 (or_3_out, and_2_out, controlunit_1_isjr, controlunit_1_isjump);
  Forwarding_Unit forwarding_unit_1 (
    .ReadRs(controlunit_1_readingrs), .ReadRt(controlunit_1_readingrt), .RegWriteEX(id_exv2_1_regwrite_ex),
    .RegWriteMEM(ex_memv2_1_regwrite_mem), .RS(decoder_alt_1_rs), .RT(decoder_alt_1_rt),
    .WriteRegEX(id_exv2_1_writereg_ex), .WriteRegMEM(ex_memv2_1_writereg_mem),
    .RsSource(forwarding_unit_1_rssource), .RtSource(forwarding_unit_1_rtsource),
    .HasForwarded(forwarding_unit_1_hasforwarded));
  Multiplexer #(.select(2), .width(32)) multiplexer_10 (
    .in0(registerfile_1_r1out), .in1(ula_1_result), .in2(multiplexer_15_out), .out(multiplexer_10_out),
    .sel(forwarding_unit_1_rssource));  // open: in3
  Multiplexer #(.select(2), .width(32)) multiplexer_11 (
    .in0(registerfile_1_r2out), .in1(ula_1_result), .in2(multiplexer_15_out), .out(multiplexer_11_out),
    .sel(forwarding_unit_1_rtsource));  // open: in3
  ID_EXv2 id_exv2_1 (
    .isShift_ID(controlunit_1_isshift), .MemToReg_ID(controlunit_1_memtoreg),
    .RegWrite_ID(controlunit_1_regwrite), .ALUSrc_ID(controlunit_1_alusrc),
    .MemRead_ID(controlunit_1_memread), .MemWrite_ID(controlunit_1_memwrite), .ALUOp_ID(controlunit_1_aluop),
    .WriteReg_ID(multiplexer_6_out), .isJAL_ID(controlunit_1_isjal), .clr_ID_EX(or_4_out),
    .Imm_ID(immediatecomplement_1_extendedimmediate), .R1_ID(multiplexer_10_out), .R2_ID(multiplexer_11_out),
    .Shamt_ID(bit_extender_1_out), .enable_ID_EX(1'b1), .clk_ID_EX(CLK), .PCPlus4_ID(TPCPlus4EX),
    .isShift_EX(id_exv2_1_isshift_ex), .MemToReg_EX(id_exv2_1_memtoreg_ex),
    .RegWrite_EX(id_exv2_1_regwrite_ex), .ALUSrc_EX(id_exv2_1_alusrc_ex), .MemRead_EX(id_exv2_1_memread_ex),
    .MemWrite_EX(id_exv2_1_memwrite_ex), .ALUOp_EX(id_exv2_1_aluop_ex), .WriteReg_EX(id_exv2_1_writereg_ex),
    .isJAL_EX(id_exv2_1_isjal_ex), .Imm_EX(id_exv2_1_imm_ex), .R1_EX(id_exv2_1_r1_ex),
    .R2_EX(id_exv2_1_r2_ex), .Shamt_EX(id_exv2_1_shamt_ex), .PCPus4_EX(id_exv2_1_pcpus4_ex));  // open: JumpAddr_ID, JumpAddr_EX
  or or_4 (or_4_out, lw_hazard_handler_1_flushid, Clear_Pipeline);
  Multiplexer #(.width(32)) multiplexer_12 (
    .in0(id_exv2_1_r2_ex), .in1(id_exv2_1_imm_ex), .out(multiplexer_12_out), .sel(id_exv2_1_alusrc_ex));
  Multiplexer #(.width(32)) multiplexer_13 (
    .in0(id_exv2_1_r1_ex), .in1(id_exv2_1_r2_ex), .out(multiplexer_13_out), .sel(id_exv2_1_isshift_ex));
  Multiplexer #(.width(32)) multiplexer_14 (
    .in0(multiplexer_12_out), .in1(id_exv2_1_shamt_ex), .out(multiplexer_14_out), .sel(id_exv2_1_isshift_ex));
  ULA ula_1 (
    .A(multiplexer_13_out), .B(multiplexer_14_out), .ALUOp(id_exv2_1_aluop_ex), .Result(ula_1_result));  // open: SignedOverflow, UnsignedOverflow, isEqual
  EX_MEMv2 ex_memv2_1 (
    .clr_EX_MEM(Clear_Pipeline), .ALUResult_EX(ula_1_result), .MemData_EX(id_exv2_1_r2_ex),
    .WriteReg_EX(id_exv2_1_writereg_ex), .PCPlus4_EX(id_exv2_1_pcpus4_ex), .enable_EX_MEM(1'b1),
    .clk_EX_MEM(CLK), .isJAL_EX(id_exv2_1_isjal_ex), .MemToReg_EX(id_exv2_1_memtoreg_ex),
    .RegWrite_EX(id_exv2_1_regwrite_ex), .MemRead_EX(id_exv2_1_memread_ex),
    .MemWrite_EX(id_exv2_1_memwrite_ex), .ALUResult_MEM(ex_memv2_1_aluresult_mem),
    .MemData_MEM(ex_memv2_1_memdata_mem), .WriteReg_MEM(ex_memv2_1_writereg_mem),
    .PCPlus4_MEM(ex_memv2_1_pcplus4_mem), .isJAL_MEM(ex_memv2_1_isjal_mem),
    .MemToReg_MEM(ex_memv2_1_memtoreg_mem), .RegWrite_MEM(ex_memv2_1_regwrite_mem),
    .MemRead_MEM(ex_memv2_1_memread_mem), .MemWrite_MEM(ex_memv2_1_memwrite_mem));
  RAM #(.addrWidth(10), .asyncread("true"), .clearpin("true"), .dataWidth(32)) ram_1 (
    .addr(ex_memv2_1_aluresult_mem[11:2]), .we(ex_memv2_1_memwrite_mem), .oe(ex_memv2_1_memread_mem),
    .clk(CLK), .din(ex_memv2_1_memdata_mem), .dout(ram_1_dout), .clr(Clear_Memory));
  Multiplexer #(.width(32)) multiplexer_15 (
    .in0(ex_memv2_1_aluresult_mem), .in1(ram_1_dout), .out(multiplexer_15_out), .sel(ex_memv2_1_memtoreg_mem));
  MEM_WB mem_wb_1 (
    .clr_MEM_WB(Clear_Pipeline), .ALUResult_MEM(ex_memv2_1_aluresult_mem), .DataFromMem_MEM(ram_1_dout),
    .WriteReg_MEM(ex_memv2_1_writereg_mem), .PCPlus4_MEM(ex_memv2_1_pcplus4_mem), .enable_MEM_WB(1'b1),
    .clk_MEM_WB(CLK), .isJAL_MEM(ex_memv2_1_isjal_mem), .MemToReg_MEM(ex_memv2_1_memtoreg_mem),
    .RegWrite_MEM(ex_memv2_1_regwrite_mem), .ALUResult_WB(mem_wb_1_aluresult_wb),
    .DataFromMem_WB(mem_wb_1_datafrommem_wb), .WriteReg_WB(mem_wb_1_writereg_wb),
    .PCPlus4_WB(mem_wb_1_pcplus4_wb), .isJAL_WB(mem_wb_1_isjal_wb), .MemToReg_WB(mem_wb_1_memtoreg_wb),
    .RegWrite_WB(mem_wb_1_regwrite_wb));
  Multiplexer #(.width(32)) multiplexer_16 (
    .in0(mem_wb_1_aluresult_wb), .in1(mem_wb_1_datafrommem_wb), .out(multiplexer_16_out),
    .sel(mem_wb_1_memtoreg_wb));
  Multiplexer #(.width(32)) multiplexer_17 (
    .in0(multiplexer_16_out), .in1(mem_wb_1_pcplus4_wb), .out(multiplexer_17_out), .sel(mem_wb_1_isjal_wb));

  // Other names for the same wires on the sheet: Clear_t = Clear_Pipeline

  // Notes on the sheet:
  //   Clear PC
  //   contents of rom_1 (hex, n*v repeats v):
  //   2009000a 4020 5020 1120000c 8d0b0000 21080004 2129ffff 14b5020 8000003 8000009
endmodule

module jtbteste (
  input  update,
  input  clear,
  input  clk,
  input  [31:0] pcIn,
  input  [31:0] instruction,
  input  [31:0] newpc,
  input  [31:0] targuet,
  output [31:0] instructionOut,
  output hit,
  output needUpdate
);

  wire and_1_out, and_3_out, comparator_1_eq, comparator_2_eq, d_ff_1_q, demultiplexer_1_out0,
       demultiplexer_1_out1, demultiplexer_1_out2, demultiplexer_1_out3, demultiplexer_1_out4,
       demultiplexer_1_out5, demultiplexer_1_out6, demultiplexer_1_out7, demultiplexer_2_out0,
       demultiplexer_2_out1, demultiplexer_2_out2, demultiplexer_2_out3, demultiplexer_2_out4,
       demultiplexer_2_out5, demultiplexer_2_out6, demultiplexer_2_out7, not_1_out, not_2_out, not_3_out,
       not_4_out, not_5_out, not_6_out, not_7_out;
  wire [31:0] multiplexer_1_out, register_1_q, register_2_q, register_3_q, register_4_q, register_5_q,
       register_6_q, register_7_q, register_8_q, register_9_q, register_10_q, register_11_q, register_12_q,
       register_13_q, register_14_q, register_15_q, register_16_q;

  Register #(.width(32)) register_1 (.D(newpc), .en(demultiplexer_1_out0), .clk(clk), .Q(register_1_q), .clr(clear));
  Register #(.width(32)) register_2 (.D(targuet), .en(demultiplexer_2_out0), .clk(clk), .Q(register_2_q), .clr(clear));
  Register #(.width(32)) register_3 (.D(newpc), .en(demultiplexer_1_out1), .clk(clk), .Q(register_3_q), .clr(clear));
  Register #(.width(32)) register_4 (.D(targuet), .en(demultiplexer_2_out1), .clk(clk), .Q(register_4_q), .clr(clear));
  Register #(.width(32)) register_5 (.D(newpc), .en(demultiplexer_1_out2), .clk(clk), .Q(register_5_q), .clr(clear));
  Register #(.width(32)) register_6 (.D(targuet), .en(demultiplexer_2_out2), .clk(clk), .Q(register_6_q), .clr(clear));
  not not_1 (not_1_out, instruction[26]);
  not not_2 (not_2_out, instruction[28]);
  and and_1 (and_1_out, not_1_out, instruction[27], not_2_out, not_3_out, not_4_out, not_5_out);
  not not_3 (not_3_out, instruction[29]);
  not not_4 (not_4_out, instruction[30]);
  not not_5 (not_5_out, instruction[31]);
  Register #(.width(32)) register_7 (.D(newpc), .en(demultiplexer_1_out3), .clk(clk), .Q(register_7_q), .clr(clear));
  Multiplexer #(.select(3), .width(32)) multiplexer_1 (
    .in0(register_1_q), .in1(register_3_q), .in2(register_5_q), .in3(register_7_q), .in4(register_9_q),
    .in5(register_11_q), .in6(register_13_q), .in7(register_15_q), .out(multiplexer_1_out), .sel(pcIn[4:2]));
  Register #(.width(32)) register_8 (.D(targuet), .en(demultiplexer_2_out3), .clk(clk), .Q(register_8_q), .clr(clear));
  Multiplexer #(.select(3), .width(32)) multiplexer_2 (
    .in0(register_2_q), .in1(register_4_q), .in2(register_6_q), .in3(register_8_q), .in4(register_10_q),
    .in5(register_12_q), .in6(register_14_q), .in7(register_16_q), .out(instructionOut), .sel(pcIn[4:2]));
  Register #(.width(32)) register_9 (.D(newpc), .en(demultiplexer_1_out4), .clk(clk), .Q(register_9_q), .clr(clear));
  Comparator #(.width(32)) comparator_1 (.a({32{1'b0}}), .b(multiplexer_1_out), .eq(comparator_1_eq));  // open: gt, lt
  Comparator #(.width(32)) comparator_2 (.a(multiplexer_1_out), .b(pcIn), .eq(comparator_2_eq));  // open: gt, lt
  Register #(.width(32)) register_10 (
    .D(targuet), .en(demultiplexer_2_out4), .clk(clk), .Q(register_10_q), .clr(clear));
  Register #(.width(32)) register_11 (.D(newpc), .en(demultiplexer_1_out5), .clk(clk), .Q(register_11_q), .clr(clear));
  not not_6 (not_6_out, comparator_1_eq);
  Register #(.width(32)) register_12 (
    .D(targuet), .en(demultiplexer_2_out5), .clk(clk), .Q(register_12_q), .clr(clear));
  and and_2 (hit, not_6_out, comparator_2_eq);
  Register #(.width(32)) register_13 (.D(newpc), .en(demultiplexer_1_out6), .clk(clk), .Q(register_13_q), .clr(clear));
  Register #(.width(32)) register_14 (
    .D(targuet), .en(demultiplexer_2_out6), .clk(clk), .Q(register_14_q), .clr(clear));
  Register #(.width(32)) register_15 (.D(newpc), .en(demultiplexer_1_out7), .clk(clk), .Q(register_15_q), .clr(clear));
  Register #(.width(32)) register_16 (
    .D(targuet), .en(demultiplexer_2_out7), .clk(clk), .Q(register_16_q), .clr(clear));
  Demultiplexer #(.enable("true"), .select(3)) demultiplexer_1 (
    .out0(demultiplexer_1_out0), .out1(demultiplexer_1_out1), .out2(demultiplexer_1_out2),
    .out3(demultiplexer_1_out3), .out4(demultiplexer_1_out4), .out5(demultiplexer_1_out5),
    .out6(demultiplexer_1_out6), .out7(demultiplexer_1_out7), .in(1'b1), .sel(newpc[4:2]), .en(update));
  Demultiplexer #(.enable("true"), .select(3)) demultiplexer_2 (
    .out0(demultiplexer_2_out0), .out1(demultiplexer_2_out1), .out2(demultiplexer_2_out2),
    .out3(demultiplexer_2_out3), .out4(demultiplexer_2_out4), .out5(demultiplexer_2_out5),
    .out6(demultiplexer_2_out6), .out7(demultiplexer_2_out7), .in(1'b1), .sel(newpc[4:2]), .en(update));
  // Probe on instructionOut
  not not_7 (not_7_out, hit);
  and and_3 (and_3_out, not_7_out, and_1_out);
  D_Flip_Flop d_ff_1 (.D(and_3_out), .clk(clk), .Q(d_ff_1_q));  // open: Qn, preset, reset
  and and_4 (needUpdate, and_3_out, ~d_ff_1_q);  // AND_Gate
endmodule

module IF_ID2 (
  input  clk_IF_ID,
  input  clr_IF_ID,
  input  [31:0] Instruction_IF,
  input  [31:0] PCPlus4_IF,
  input  updateJTB_IF,
  input  enable_IF_ID,
  output [31:0] Instruction_ID,
  output [31:0] PCPus4_ID,
  output updateJTB_ID
);

  Register #(.width(32)) reg_Instruction_IF_ID (
    .D(Instruction_IF), .en(enable_IF_ID), .clk(clk_IF_ID), .Q(Instruction_ID), .clr(clr_IF_ID));
  Register #(.width(32)) reg_PCPlus4_IF_ID (
    .D(PCPlus4_IF), .en(enable_IF_ID), .clk(clk_IF_ID), .Q(PCPus4_ID), .clr(clr_IF_ID));
  Register #(.width(1)) register_1 (
    .D(updateJTB_IF), .en(enable_IF_ID), .clk(clk_IF_ID), .Q(updateJTB_ID), .clr(clr_IF_ID));
endmodule

module jtbteste2 (
  input  update,
  input  clear,
  input  clk,
  input  [31:0] pcIn,
  input  [31:0] instruction,
  input  [31:0] newpc,
  input  [31:0] targuet,
  output [31:0] instructionOut,
  output hit,
  output needUpdate
);

  wire and_1_out, and_3_out, comparator_1_eq, comparator_2_eq, d_ff_1_q, demultiplexer_1_out0,
       demultiplexer_1_out1, demultiplexer_1_out2, demultiplexer_1_out3, demultiplexer_1_out4,
       demultiplexer_1_out5, demultiplexer_1_out6, demultiplexer_1_out7, demultiplexer_2_out0,
       demultiplexer_2_out1, demultiplexer_2_out2, demultiplexer_2_out3, demultiplexer_2_out4,
       demultiplexer_2_out5, demultiplexer_2_out6, demultiplexer_2_out7, not_1_out, not_2_out, not_3_out,
       not_4_out, not_5_out, not_6_out, not_7_out;
  wire [31:0] multiplexer_1_out, register_1_q, register_2_q, register_3_q, register_4_q, register_5_q,
       register_6_q, register_7_q, register_8_q, register_9_q, register_10_q, register_11_q, register_12_q,
       register_13_q, register_14_q, register_15_q, register_16_q;

  Register #(.width(32)) register_1 (.D(newpc), .en(demultiplexer_1_out0), .clk(clk), .Q(register_1_q), .clr(clear));
  Register #(.width(32)) register_2 (.D(targuet), .en(demultiplexer_2_out0), .clk(clk), .Q(register_2_q), .clr(clear));
  Register #(.width(32)) register_3 (.D(newpc), .en(demultiplexer_1_out1), .clk(clk), .Q(register_3_q), .clr(clear));
  Register #(.width(32)) register_4 (.D(targuet), .en(demultiplexer_2_out1), .clk(clk), .Q(register_4_q), .clr(clear));
  Register #(.width(32)) register_5 (.D(newpc), .en(demultiplexer_1_out2), .clk(clk), .Q(register_5_q), .clr(clear));
  Register #(.width(32)) register_6 (.D(targuet), .en(demultiplexer_2_out2), .clk(clk), .Q(register_6_q), .clr(clear));
  not not_1 (not_1_out, instruction[26]);
  not not_2 (not_2_out, instruction[28]);
  and and_1 (and_1_out, not_1_out, instruction[27], not_2_out, not_3_out, not_4_out, not_5_out);
  not not_3 (not_3_out, instruction[29]);
  not not_4 (not_4_out, instruction[30]);
  not not_5 (not_5_out, instruction[31]);
  Register #(.width(32)) register_7 (.D(newpc), .en(demultiplexer_1_out3), .clk(clk), .Q(register_7_q), .clr(clear));
  Multiplexer #(.select(3), .width(32)) multiplexer_1 (
    .in0(register_1_q), .in1(register_3_q), .in2(register_5_q), .in3(register_7_q), .in4(register_9_q),
    .in5(register_11_q), .in6(register_13_q), .in7(register_15_q), .out(multiplexer_1_out), .sel(pcIn[4:2]));
  Register #(.width(32)) register_8 (.D(targuet), .en(demultiplexer_2_out3), .clk(clk), .Q(register_8_q), .clr(clear));
  Multiplexer #(.select(3), .width(32)) multiplexer_2 (
    .in0(register_2_q), .in1(register_4_q), .in2(register_6_q), .in3(register_8_q), .in4(register_10_q),
    .in5(register_12_q), .in6(register_14_q), .in7(register_16_q), .out(instructionOut), .sel(pcIn[4:2]));
  Register #(.width(32)) register_9 (.D(newpc), .en(demultiplexer_1_out4), .clk(clk), .Q(register_9_q), .clr(clear));
  Comparator #(.width(32)) comparator_1 (.a({32{1'b0}}), .b(multiplexer_1_out), .eq(comparator_1_eq));  // open: gt, lt
  Comparator #(.width(32)) comparator_2 (.a(multiplexer_1_out), .b(pcIn), .eq(comparator_2_eq));  // open: gt, lt
  Register #(.width(32)) register_10 (
    .D(targuet), .en(demultiplexer_2_out4), .clk(clk), .Q(register_10_q), .clr(clear));
  Register #(.width(32)) register_11 (.D(newpc), .en(demultiplexer_1_out5), .clk(clk), .Q(register_11_q), .clr(clear));
  not not_6 (not_6_out, comparator_1_eq);
  Register #(.width(32)) register_12 (
    .D(targuet), .en(demultiplexer_2_out5), .clk(clk), .Q(register_12_q), .clr(clear));
  and and_2 (hit, not_6_out, comparator_2_eq);
  Register #(.width(32)) register_13 (.D(newpc), .en(demultiplexer_1_out6), .clk(clk), .Q(register_13_q), .clr(clear));
  Register #(.width(32)) register_14 (
    .D(targuet), .en(demultiplexer_2_out6), .clk(clk), .Q(register_14_q), .clr(clear));
  Register #(.width(32)) register_15 (.D(newpc), .en(demultiplexer_1_out7), .clk(clk), .Q(register_15_q), .clr(clear));
  Register #(.width(32)) register_16 (
    .D(targuet), .en(demultiplexer_2_out7), .clk(clk), .Q(register_16_q), .clr(clear));
  Demultiplexer #(.enable("true"), .select(3)) demultiplexer_1 (
    .out0(demultiplexer_1_out0), .out1(demultiplexer_1_out1), .out2(demultiplexer_1_out2),
    .out3(demultiplexer_1_out3), .out4(demultiplexer_1_out4), .out5(demultiplexer_1_out5),
    .out6(demultiplexer_1_out6), .out7(demultiplexer_1_out7), .in(1'b1), .sel(newpc[4:2]), .en(update));
  Demultiplexer #(.enable("true"), .select(3)) demultiplexer_2 (
    .out0(demultiplexer_2_out0), .out1(demultiplexer_2_out1), .out2(demultiplexer_2_out2),
    .out3(demultiplexer_2_out3), .out4(demultiplexer_2_out4), .out5(demultiplexer_2_out5),
    .out6(demultiplexer_2_out6), .out7(demultiplexer_2_out7), .in(1'b1), .sel(newpc[4:2]), .en(update));
  // Probe on instructionOut
  not not_7 (not_7_out, hit);
  and and_3 (and_3_out, not_7_out, and_1_out);
  D_Flip_Flop d_ff_1 (.D(and_3_out), .clk(clk), .Q(d_ff_1_q));  // open: Qn, preset, reset
  and and_4 (needUpdate, and_3_out, ~d_ff_1_q);  // AND_Gate
endmodule
