// Logisim project pipeline_JTB_5.circ as structural Verilog: 26 circuits, main circuit main
module main (
  input  in_1,
  input  ClearPC,
  input  in_3,
  input  in_4,
  input  in_5,
  input  in_6,
  input  in_7,
  output out_8,
  output out_9,
  output out_10,
  output out_11
);

  wire disablePC, jtb_1_hit, not_1_out, not_2_out, not_3_out, palu_1_isequal, TALUSrc, TALUSrcEX, TBneOrBeq,
       TBneOrBeqEX, TBranch, TBranch_3, TBranchEX, TFlushIdHazard, TFlushIF, TisJR, TisJREX, TisJump,
       TisJumpEX, TisShamt, TisShamtEX, TIsToBranchOrJump, TMemRead, TMemReadEX, TMemReadMEM, TMemToReg,
       TMemToRegEX, TMemToRegMEM, TMemToRegWB, TMemWrite, TMemWriteEx, TMemWriteMEM, TReadRsHazard,
       TReadRtHazard, TRegDst, TRegWrite, TRegWriteEX, TRegWriteMEM, TStallID, TUpdateJTB, TUpdateJTB_EX,
       TUpdateJTB_ID, TWriteEnable, TZeroExtd, xor_1_out;
  wire [1:0] TRsOutput, TRtOutput;
  wire [3:0] TALUOp, TALUOp_ID;
  wire [4:0] multiplexer_7_out, Trd, Trs, Trt, Tshamt, TWriteReg_5, TWriteRegEX, TWriteRegMEM;
  wire [5:0] Decoder_funct, Decoder_op;
  wire [15:0] Timmediate;
  wire [25:0] TAddress;
  wire [31:0] adder_1_out, adder_2_out, bit_extender_1_out, contador_1_numerociclos, jtb_1_instructionout,
       multiplexer_1_out, multiplexer_2_out, multiplexer_3_out, multiplexer_4_out, multiplexer_5_out,
       multiplexer_10_out, multiplexer_11_out, multiplexer_12_out, PCPLUS4_1, register_1_q,
       registerfilepmostradores_1_sr0, registerfilepmostradores_1_sr1, registerfilepmostradores_1_sr2,
       registerfilepmostradores_1_sr3, registerfilepmostradores_1_sr4, registerfilepmostradores_1_sr5,
       registerfilepmostradores_1_sr6, registerfilepmostradores_1_sr7, registerfilepmostradores_1_sr8,
       registerfilepmostradores_1_sr9, registerfilepmostradores_1_sr10, registerfilepmostradores_1_sr11,
       registerfilepmostradores_1_sr12, registerfilepmostradores_1_sr13, registerfilepmostradores_1_sr14,
       registerfilepmostradores_1_sr15, registerfilepmostradores_1_sr16, registerfilepmostradores_1_sr17,
       registerfilepmostradores_1_sr18, registerfilepmostradores_1_sr19, registerfilepmostradores_1_sr20,
       registerfilepmostradores_1_sr21, registerfilepmostradores_1_sr22, registerfilepmostradores_1_sr23,
       registerfilepmostradores_1_sr24, registerfilepmostradores_1_sr25, registerfilepmostradores_1_sr26,
       registerfilepmostradores_1_sr27, registerfilepmostradores_1_sr28, registerfilepmostradores_1_sr29,
       registerfilepmostradores_1_sr30, registerfilepmostradores_1_sr31, shifter_1_out, T_WB_DATA_5,
       TALUResultEX, TALUResultMEM, TALUResultWB, TDataFromMEM, TImmediate_ID, TImmEX, Tinstruction,
       TinstructionIF, TJumpAddr_3, TJumpAddr_ID, TJumpAddrEX, TJumpAddrMEM, TJumpADDRWB, TOutputFromMEM,
       TPCPlus4EX, Tpcplus4IF, TR1_ID, TR1EX, TR1FromReg, TR2_ID, TR2FromReg, TReadDataWB, TShamtEX,
       TWriteDataEx, TWriteDataMEM;

  Multiplexer #(.disabled("Z"), .width(32)) multiplexer_1 (
    .in0(PCPLUS4_1), .in1(TJumpAddr_3), .out(multiplexer_1_out), .sel(TBranch_3));
  Multiplexer #(.disabled("Z"), .width(32)) multiplexer_2 (
    .in0(multiplexer_1_out), .in1(TJumpAddrEX), .out(multiplexer_2_out), .sel(TisJumpEX));
  Multiplexer #(.disabled("Z"), .width(32)) multiplexer_3 (
    .in0(multiplexer_2_out), .in1(TR1EX), .out(multiplexer_3_out), .sel(TisJREX));
  Adder #(.width(32)) adder_1 (.a(jtb_1_instructionout), .b(32'h4), .out(adder_1_out));  // open: cin, cout
  Multiplexer #(.disabled("Z"), .width(32)) multiplexer_4 (
    .in0(multiplexer_3_out), .in1(adder_1_out), .out(multiplexer_4_out), .sel(jtb_1_hit));
  not not_1 (not_1_out, disablePC);
  Register #(.width(32)) register_1 (
    .D(multiplexer_4_out), .en(not_1_out), .clk(out_8), .Q(register_1_q), .clr(ClearPC));
  JTB jtb_1 (
    .newpc(TPCPlus4EX), .update(TUpdateJTB_EX), .targuet(TJumpAddrEX), .clear(in_6), .pcIn(adder_2_out),
    .instruction(Tinstruction), .clk(out_8), .hit(jtb_1_hit), .instructionOut(jtb_1_instructionout),
    .needUpdate(TUpdateJTB));
  Clock clock_1 (.out(out_8));
  Adder #(.width(32)) adder_2 (.a(register_1_q), .b(32'h4), .out(adder_2_out));  // open: cin, cout
  // Probe on contador_1_numerociclos
  Multiplexer #(.width(32)) multiplexer_5 (
    .in0(register_1_q), .in1(jtb_1_instructionout), .out(multiplexer_5_out), .sel(jtb_1_hit));
  Multiplexer #(.width(32)) multiplexer_6 (.in0(adder_2_out), .in1(adder_1_out), .out(PCPLUS4_1), .sel(jtb_1_hit));
  Contador contador_1 (.clkSignal(out_8), .zerarContador(in_3), .NumeroCiclos(contador_1_numerociclos));
  ROM #(.addrWidth(10), .dataWidth(32)) rom_1 (.addr(multiplexer_5_out[11:2]), .data(Tinstruction));
  // Probe on Tinstruction
  // Probe on PCPLUS4_1
  IF_ID if_id_1 (
    .clk_if_id(out_8), .Instruction_IF(Tinstruction), .PCPlus4_IF(PCPLUS4_1), .updateJTB_IF(TUpdateJTB),
    .Enable_if_id(not_2_out), .clr_if_id(TFlushIF), .Instruction_ID(TinstructionIF), .PCPus4_ID(Tpcplus4IF),
    .updateJTB_ID(TUpdateJTB_ID));
  not not_2 (not_2_out, TStallID);
  // Probe on TinstructionIF
  // Probe on Tpcplus4IF
  JmpAddress jmpaddress_1 (.Address(TAddress), .PC4(Tpcplus4IF), .JumpAddress(TJumpAddr_ID));
  InstructionDec Decoder (
    .Instruction(TinstructionIF), .op(Decoder_op), .rs(Trs), .rt(Trt), .rd(Trd), .shamt(Tshamt),
    .funct(Decoder_funct), .immediate(Timmediate), .adderess(TAddress));
  ComplementadorSinal complementadorsinal_1 (
    .ZeroExtend(TZeroExtd), .address16(Timmediate), .address32ext(TImmediate_ID));
  ControlUnit controlunit_1 (
    .in_1(Decoder_op), .in_2(Decoder_funct), .ALUop(TALUOp_ID), .isShamt(TisShamt), .MemToReg(TMemToReg),
    .RegWrite(TRegWrite), .BneOrBeq(TBneOrBeq), .ALUSrc(TALUSrc), .ZeroExtend(TZeroExtd),
    .ReadRs(TReadRsHazard), .MemRead(TMemRead), .MemWrite(TMemWrite), .Jump(TisJump), .Branch(TBranch),
    .RegDst(TRegDst), .isJR(TisJR), .ReadRt(TReadRtHazard));
  not not_3 (not_3_out, out_8);
  // Probe on registerfilepmostradores_1_sr0
  // Probe on registerfilepmostradores_1_sr1
  // Probe on registerfilepmostradores_1_sr2
  // Probe on registerfilepmostradores_1_sr3
  // Probe on registerfilepmostradores_1_sr4
  // Probe on registerfilepmostradores_1_sr5
  // Probe on registerfilepmostradores_1_sr6
  // Probe on registerfilepmostradores_1_sr7
  // Probe on registerfilepmostradores_1_sr8
  // Probe on registerfilepmostradores_1_sr9
  // Probe on registerfilepmostradores_1_sr10
  // Probe on registerfilepmostradores_1_sr11
  // Probe on registerfilepmostradores_1_sr12
  // Probe on registerfilepmostradores_1_sr13
  // Probe on registerfilepmostradores_1_sr14
  // Probe on registerfilepmostradores_1_sr15
  // Probe on registerfilepmostradores_1_sr16
  // Probe on registerfilepmostradores_1_sr17
  // Probe on registerfilepmostradores_1_sr18
  // Probe on registerfilepmostradores_1_sr19
  // Probe on registerfilepmostradores_1_sr20
  // Probe on registerfilepmostradores_1_sr21
  // Probe on registerfilepmostradores_1_sr22
  // Probe on registerfilepmostradores_1_sr23
  // Probe on registerfilepmostradores_1_sr24
  // Probe on registerfilepmostradores_1_sr25
  // Probe on registerfilepmostradores_1_sr26
  // Probe on registerfilepmostradores_1_sr27
  // Probe on registerfilepmostradores_1_sr28
  // Probe on registerfilepmostradores_1_sr29
  // Probe on registerfilepmostradores_1_sr30
  // Probe on registerfilepmostradores_1_sr31
  registerFilePMostradores registerfilepmostradores_1 (
    .Rw(TWriteReg_5), .inDado(T_WB_DATA_5), .WE(TWriteEnable), .clk(not_3_out), .rst(in_7), .R1in(Trs),
    .R2in(Trt), .SR15(registerfilepmostradores_1_sr15), .SR8(registerfilepmostradores_1_sr8),
    .SR9(registerfilepmostradores_1_sr9), .SR10(registerfilepmostradores_1_sr10),
    .SR11(registerfilepmostradores_1_sr11), .SR12(registerfilepmostradores_1_sr12),
    .SR13(registerfilepmostradores_1_sr13), .SR14(registerfilepmostradores_1_sr14), .R1out(TR1FromReg),
    .SR23(registerfilepmostradores_1_sr23), .R2out(TR2FromReg), .SR16(registerfilepmostradores_1_sr16),
    .SR17(registerfilepmostradores_1_sr17), .SR18(registerfilepmostradores_1_sr18),
    .SR19(registerfilepmostradores_1_sr19), .SR20(registerfilepmostradores_1_sr20),
    .SR21(registerfilepmostradores_1_sr21), .SR22(registerfilepmostradores_1_sr22),
    .SR31(registerfilepmostradores_1_sr31), .SR24(registerfilepmostradores_1_sr24),
    .SR25(registerfilepmostradores_1_sr25), .SR26(registerfilepmostradores_1_sr26),
    .SR27(registerfilepmostradores_1_sr27), .SR28(registerfilepmostradores_1_sr28),
    .SR29(registerfilepmostradores_1_sr29), .SR30(registerfilepmostradores_1_sr30),
    .SR7(registerfilepmostradores_1_sr7), .SR0(registerfilepmostradores_1_sr0),
    .SR1(registerfilepmostradores_1_sr1), .SR2(registerfilepmostradores_1_sr2),
    .SR3(registerfilepmostradores_1_sr3), .SR4(registerfilepmostradores_1_sr4),
    .SR5(registerfilepmostradores_1_sr5), .SR6(registerfilepmostradores_1_sr6));  // open: a0out, v0out
  FHazardUnit fhazardunit_1 (
    .IsToBranchOrJump(TIsToBranchOrJump), .clk(out_8), .ReadRs(TReadRsHazard), .ReadRt(TReadRtHazard),
    .RegWriteEX(TRegWriteEX), .RegWriteMEM(TRegWriteMEM), .RS(Trs), .RT(Trt), .IsLW(TMemReadEX),
    .WriteRegEX(TWriteRegEX), .WriteRegMEM(TWriteRegMEM), .FlushIF(TFlushIF), .RsOutput(TRsOutput),
    .FlushID(TFlushIdHazard), .StallIF(disablePC), .StallID(TStallID), .RtOutput(TRtOutput));
  assign bit_extender_1_out = {{27{1'b0}}, Tshamt};  // Bit_Extender bit_extender_1
  Multiplexer #(.disabled("Z"), .width(5)) multiplexer_7 (.in0(Trt), .in1(Trd), .out(multiplexer_7_out), .sel(TRegDst));
  Multiplexer #(.disabled("Z"), .select(2), .width(32)) multiplexer_8 (
    .in0(TR1FromReg), .in1(TALUResultEX), .in2(TDataFromMEM), .out(TR1_ID), .sel(TRsOutput));  // open: in3
  Multiplexer #(.disabled("Z"), .select(2), .width(32)) multiplexer_9 (
    .in0(TR2FromReg), .in1(TALUResultEX), .in2(TDataFromMEM), .out(TR2_ID), .sel(TRtOutput));  // open: in3
  ID_EX id_ex_1 (
    .isSham_ID(TisShamt), .MemToReg_ID(TMemToReg), .RegWrite_ID(TRegWrite), .BneOrBeq_ID(TBneOrBeq),
    .clr_ID_EX(TFlushIdHazard), .ALUSrc_ID(TALUSrc), .MemRead_ID(TMemRead), .MemWrite_ID(TMemWrite),
    .isJump_ID(TisJump), .Branch_ID(TBranch), .is_JR_ID(TisJR), .ALUOp_ID(TALUOp_ID),
    .WriteReg_ID(multiplexer_7_out), .updateJTB_ID(TUpdateJTB_ID), .Imm_ID(TImmediate_ID), .R1_ID(TR1_ID),
    .R2_ID(TR2_ID), .enable_id_ex(1'b1), .Sham_ID(bit_extender_1_out), .JumpAddr_ID(TJumpAddr_ID),
    .PCPlus4_ID(Tpcplus4IF), .clk_ID_EX(out_8), .isSham_EX(TisShamtEX), .MemToReg_EX(TMemToRegEX),
    .RegWrite_EX(TRegWriteEX), .BneOrBeq_EX(TBneOrBeqEX), .ALUSrc_EX(TALUSrcEX), .MemRead_EX(TMemReadEX),
    .MemWrite_EX(TMemWriteEx), .isJump_EX(TisJumpEX), .Branch_EX(TBranchEX), .isJR_EX(TisJREX),
    .ALUOp_EX(TALUOp), .WriteReg_EX(TWriteRegEX), .updateJTB_EX(TUpdateJTB_EX), .Imm_EX(TImmEX),
    .R1_EX(TR1EX), .R2_EX(TWriteDataEx), .Sham_EX(TShamtEX), .JumpAddr_EX(TJumpAddrEX), .PCPus4_EX(TPCPlus4EX));
  Multiplexer #(.disabled("Z"), .width(32)) multiplexer_10 (
    .in0(TR1EX), .in1(TWriteDataEx), .out(multiplexer_10_out), .sel(TisShamtEX));
  Multiplexer #(.disabled("Z"), .width(32)) multiplexer_11 (
    .in0(TWriteDataEx), .in1(TShamtEX), .out(multiplexer_11_out), .sel(TisShamtEX));
  Multiplexer #(.disabled("Z"), .width(32)) multiplexer_12 (
    .in0(multiplexer_11_out), .in1(TImmEX), .out(multiplexer_12_out), .sel(TALUSrcEX));
  Shifter #(.width(32)) shifter_1 (.in(TImmEX), .\dist (5'b00010), .out(shifter_1_out));
  // Probe on TALUOp
  // Probe on multiplexer_12_out
  // Probe on multiplexer_10_out
  Adder #(.width(32)) adder_3 (.a(TPCPlus4EX), .b(shifter_1_out), .out(TJumpAddr_3));  // open: cin, cout
  or or_1 (TIsToBranchOrJump, TisJREX, TBranch_3, TisJumpEX);
  // Probe on TALUResultEX
  pALU palu_1 (
    .X(multiplexer_10_out), .Y(multiplexer_12_out), .ALUOp(TALUOp), .Result1(TALUResultEX),
    .isEqual(palu_1_isequal));  // open: SignedOverflow, UnsignedOverflow, Result2
  xor xor_1 (xor_1_out, palu_1_isequal, TBneOrBeqEX);
  and and_1 (TBranch_3, xor_1_out, TBranchEX);
  EX_MEM ex_mem_1 (
    .clk_EX_MEM(out_8), .clr_EX_MEM(in_4), .MemToReg_Ex(TMemToRegEX), .RegWrite_Ex(TRegWriteEX),
    .MemRead_Ex(TMemReadEX), .MemWrite_EX(TMemWriteEx), .WriteReg_EX(TWriteRegEX), .Enable_EX_MEM(1'b1),
    .ALU_Result_EX(TALUResultEX), .WriteData_EX(TWriteDataEx), .JumpAddr_EX(TPCPlus4EX),
    .ALUResult_MEM(TALUResultMEM), .WriteData_MEM(TWriteDataMEM), .JumpAddr_MEM(TJumpAddrMEM),
    .MemToReg_MEM(TMemToRegMEM), .RegWrite_MEM(TRegWriteMEM), .MemRead_MEM(TMemReadMEM),
    .MemWrite_MEM(TMemWriteMEM), .WriteReg_MEM(TWriteRegMEM));
  Multiplexer #(.width(32)) multiplexer_13 (
    .in0(TALUResultMEM), .in1(TOutputFromMEM), .out(TDataFromMEM), .sel(TMemToRegMEM));
  RAM #(.addrWidth(10), .dataWidth(32), .trigger("falling")) ram_1 (
    .addr(TALUResultMEM[11:2]), .we(TMemWriteMEM), .oe(TMemReadMEM), .clk(out_8), .din(TWriteDataMEM),
    .dout(TOutputFromMEM));
  MEM_WB mem_wb_1 (
    .clk_mem_wb(out_8), .memToReg_mem(TMemToRegMEM), .regWrite_mem(TRegWriteMEM),
    .writeReg_mem(TWriteRegMEM), .enable_mem_wb(1'b1), .clr_mem_wb(in_4), .ALUResult_mem(TALUResultMEM),
    .ReadData_mem(TJumpAddrMEM), .JumpAddrMem(TOutputFromMEM), .ALUResult_wb(TALUResultWB),
    .ReadData_wb(TReadDataWB), .JumpAddr_wb(TJumpADDRWB), .memToReg_wb(TMemToRegWB),
    .regWrite_wb(TWriteEnable), .writeReg_wb(TWriteReg_5));
  Multiplexer #(.width(32)) multiplexer_14 (
    .in0(TALUResultWB), .in1(TJumpADDRWB), .out(T_WB_DATA_5), .sel(TMemToRegWB));

  assign out_9 = out_8;
  assign out_10 = out_8;
  assign out_11 = out_8;

  // Other names for the same wires on the sheet: TClearPipeline = in_4; Tclk = out_8; Tclk2 = in_5

  // Notes on the sheet:
  //   contents of rom_1 (hex, n*v repeats v):
  //   4020 2009000a 5020 11200005 8d0b0000 21080004 14b5020 2129ffff 8000003 8000009
  //   aaaaaaaaaaaaaaaaaaaaaaaaaaaaaaaaa
  //   aaaaaaaaaaaaaaaaaaaaaaaaaaaaaaaaa
endmodule

module Control (
  input  [5:0] op,
  output RegDest,
  output Branch,
  output LeMem,
  output MemParaReg,
  output [1:0] OpALU,
  output EscreveMem,
  output OrigALU,
  output EscreveReg,
  output Jump
);

  wire and_6_out, not_1_out, not_2_out, not_3_out, not_4_out, not_5_out, not_6_out, not_7_out, not_8_out,
       not_9_out, not_10_out, not_11_out, not_12_out, not_13_out, not_14_out, not_15_out, not_16_out,
       not_17_out, not_18_out, not_19_out, not_20_out, not_21_out, not_22_out, not_23_out, not_24_out,
       not_25_out;

  not not_1 (not_1_out, op[5]);
  not not_2 (not_2_out, op[4]);
  not not_3 (not_3_out, op[3]);
  not not_4 (not_4_out, op[2]);
  not not_5 (not_5_out, op[1]);
  not not_6 (not_6_out, op[0]);
  and and_1 (OpALU[1], not_1_out, not_2_out, not_3_out, not_4_out, not_5_out, not_6_out);
  not not_7 (not_7_out, op[4]);
  not not_8 (not_8_out, op[3]);
  not not_9 (not_9_out, op[2]);
  and and_2 (LeMem, op[5], not_7_out, not_8_out, not_9_out, op[1], op[0]);
  not not_10 (not_10_out, op[4]);
  not not_11 (not_11_out, op[2]);
  and and_3 (EscreveMem, op[5], not_10_out, op[3], not_11_out, op[1], op[0]);
  not not_12 (not_12_out, op[5]);
  not not_13 (not_13_out, op[4]);
  not not_14 (not_14_out, op[3]);
  and and_4 (Branch, not_12_out, not_13_out, not_14_out, op[2], not_15_out, not_16_out);
  not not_15 (not_15_out, op[1]);
  not not_16 (not_16_out, op[0]);
  not not_17 (not_17_out, op[5]);
  not not_18 (not_18_out, op[4]);
  not not_19 (not_19_out, op[3]);
  and and_5 (Jump, not_17_out, not_18_out, not_19_out, op[2], not_20_out, op[0]);
  or or_1 (OrigALU, LeMem, EscreveMem);
  or or_2 (EscreveReg, OpALU[1], LeMem, and_6_out);
  not not_20 (not_20_out, op[1]);
  not not_21 (not_21_out, op[5]);
  not not_22 (not_22_out, op[4]);
  not not_23 (not_23_out, op[2]);
  not not_24 (not_24_out, op[1]);
  not not_25 (not_25_out, op[0]);
  and and_6 (and_6_out, not_21_out, not_22_out, op[3], not_23_out, not_24_out, not_25_out);

  assign MemParaReg = LeMem;
  assign OpALU[0] = Branch;
  assign RegDest = OpALU[1];

  // Notes on the sheet:
  //   R-Format
  //   lw
  //   sw
  //   beq
  //   jump
  //   addi
  //   aaaaaa
endmodule

module ALUcontrol (
  input  [1:0] OpALUctrl,
  input  [5:0] functALUctrl,
  output [3:0] OperationSaidaAluCtrl
);

  wire and_2_out, not_1_out, not_2_out, not_3_out, or_1_out;

  or or_1 (or_1_out, functALUctrl[3], functALUctrl[0]);
  and and_1 (OperationSaidaAluCtrl[0], OpALUctrl[1], or_1_out);
  not not_1 (not_1_out, OpALUctrl[0]);
  and and_2 (and_2_out, OpALUctrl[1], functALUctrl[1]);
  not not_2 (not_2_out, OpALUctrl[1]);
  not not_3 (not_3_out, functALUctrl[2]);
  and and_3 (OperationSaidaAluCtrl[3], OpALUctrl[0], not_1_out);
  or or_2 (OperationSaidaAluCtrl[2], OpALUctrl[0], and_2_out);
  or or_3 (OperationSaidaAluCtrl[1], not_2_out, not_3_out);
endmodule

module InstructionDec (
  input  [31:0] Instruction,
  output [5:0] op,
  output [4:0] rs,
  output [4:0] rt,
  output [4:0] rd,
  output [4:0] shamt,
  output [5:0] funct,
  output [15:0] immediate,
  output [25:0] adderess
);


  assign adderess = Instruction[25:0];
  assign funct = Instruction[5:0];
  assign immediate = Instruction[15:0];
  assign op = Instruction[31:26];
  assign rd = Instruction[15:11];
  assign rs = Instruction[25:21];
  assign rt = Instruction[20:16];
  assign shamt = Instruction[10:6];

  // Notes on the sheet:
  //   J-Type
  //   I-Type
  //   R-Type
endmodule

module JmpAddress (
  input  [25:0] Address,
  input  [31:0] PC4,
  output [31:0] JumpAddress
);


  assign JumpAddress = {PC4[31:28], Address, 2'b00};
endmodule

module BranchAddr (
  input  [31:0] PC4,
  input  [31:0] Address,
  output [31:0] BranchAddress
);

  Adder #(.width(32)) adder_1 (.a(PC4), .b({Address[29:0], 2'b00}), .out(BranchAddress));  // open: cin, cout
endmodule

module ComplementadorSinal (
  input  ZeroExtend,
  input  [15:0] address16,
  output [31:0] address32ext
);

  wire [31:0] bit_extender_1_out, bit_extender_2_out;

  assign bit_extender_1_out = {{16{address16[15]}}, address16};  // Bit_Extender bit_extender_1
  assign bit_extender_2_out = {{16{1'b0}}, address16};  // Bit_Extender bit_extender_2
  Multiplexer #(.width(32)) multiplexer_1 (
    .in0(bit_extender_1_out), .in1(bit_extender_2_out), .out(address32ext), .sel(ZeroExtend));
endmodule

module IF_ID (
  input  clk_if_id,
  input  clr_if_id,
  input  [31:0] Instruction_IF,
  input  [31:0] PCPlus4_IF,
  input  updateJTB_IF,
  input  Enable_if_id,
  output [31:0] Instruction_ID,
  output [31:0] PCPus4_ID,
  output updateJTB_ID
);

  Register #(.width(32)) regInst_ID_IF (
    .D(Instruction_IF), .en(Enable_if_id), .clk(clk_if_id), .Q(Instruction_ID), .clr(clr_if_id));
  Register #(.width(32)) regPC_ID_IF (
    .D(PCPlus4_IF), .en(Enable_if_id), .clk(clk_if_id), .Q(PCPus4_ID), .clr(clr_if_id));
  Register #(.width(1)) regUpdateJTB_IF_ID (
    .D(updateJTB_IF), .en(Enable_if_id), .clk(clk_if_id), .Q(updateJTB_ID), .clr(clr_if_id));
endmodule

module ID_EX (
  input  clk_ID_EX,
  input  clr_ID_EX,
  input  [31:0] Imm_ID,
  input  [31:0] Sham_ID,
  input  isSham_ID,
  input  ALUSrc_ID,
  input  Branch_ID,
  input  updateJTB_ID,
  input  MemToReg_ID,
  input  MemRead_ID,
  input  is_JR_ID,
  input  [31:0] R1_ID,
  input  [31:0] JumpAddr_ID,
  input  RegWrite_ID,
  input  MemWrite_ID,
  input  [3:0] ALUOp_ID,
  input  [31:0] R2_ID,
  input  [31:0] PCPlus4_ID,
  input  BneOrBeq_ID,
  input  isJump_ID,
  input  [4:0] WriteReg_ID,
  input  enable_id_ex,
  output [31:0] Imm_EX,
  output [31:0] Sham_EX,
  output isSham_EX,
  output ALUSrc_EX,
  output Branch_EX,
  output updateJTB_EX,
  output MemToReg_EX,
  output MemRead_EX,
  output isJR_EX,
  output [31:0] R1_EX,
  output [31:0] JumpAddr_EX,
  output RegWrite_EX,
  output MemWrite_EX,
  output [3:0] ALUOp_EX,
  output [31:0] R2_EX,
  output [31:0] PCPus4_EX,
  output BneOrBeq_EX,
  output isJump_EX,
  output [4:0] WriteReg_EX
);

  Register #(.width(32)) regImm_ID_EX (.D(Imm_ID), .en(enable_id_ex), .clk(clk_ID_EX), .Q(Imm_EX), .clr(clr_ID_EX));
  Register #(.width(32)) regR1_ID_EX (.D(R1_ID), .en(enable_id_ex), .clk(clk_ID_EX), .Q(R1_EX), .clr(clr_ID_EX));
  Register #(.width(32)) regR2_ID_EX (.D(R2_ID), .en(enable_id_ex), .clk(clk_ID_EX), .Q(R2_EX), .clr(clr_ID_EX));
  Register #(.width(32)) regSham_ID_EX (.D(Sham_ID), .en(enable_id_ex), .clk(clk_ID_EX), .Q(Sham_EX), .clr(clr_ID_EX));
  Register #(.width(32)) regJump_ID_EX (
    .D(JumpAddr_ID), .en(enable_id_ex), .clk(clk_ID_EX), .Q(JumpAddr_EX), .clr(clr_ID_EX));
  Register #(.width(32)) regPC_ID_EX (
    .D(PCPlus4_ID), .en(enable_id_ex), .clk(clk_ID_EX), .Q(PCPus4_EX), .clr(clr_ID_EX));
  Register #(.width(1)) regIsSham_ID_EX (
    .D(isSham_ID), .en(enable_id_ex), .clk(clk_ID_EX), .Q(isSham_EX), .clr(clr_ID_EX));
  Register #(.width(1)) regMemToReg_ID_EX (
    .D(MemToReg_ID), .en(enable_id_ex), .clk(clk_ID_EX), .Q(MemToReg_EX), .clr(clr_ID_EX));
  Register #(.width(1)) regRegWrite_ID_EX (
    .D(RegWrite_ID), .en(enable_id_ex), .clk(clk_ID_EX), .Q(RegWrite_EX), .clr(clr_ID_EX));
  Register #(.width(1)) regBneOrBeq_ID_EX (
    .D(BneOrBeq_ID), .en(enable_id_ex), .clk(clk_ID_EX), .Q(BneOrBeq_EX), .clr(clr_ID_EX));
  Register #(.width(1)) regALUSrc_ID_EX (
    .D(ALUSrc_ID), .en(enable_id_ex), .clk(clk_ID_EX), .Q(ALUSrc_EX), .clr(clr_ID_EX));
  Register #(.width(1)) regMemRead_ID_EX (
    .D(MemRead_ID), .en(enable_id_ex), .clk(clk_ID_EX), .Q(MemRead_EX), .clr(clr_ID_EX));
  Register #(.width(1)) regMemWrite_ID_EX (
    .D(MemWrite_ID), .en(enable_id_ex), .clk(clk_ID_EX), .Q(MemWrite_EX), .clr(clr_ID_EX));
  Register #(.width(1)) regIsJump_ID_EX (
    .D(isJump_ID), .en(enable_id_ex), .clk(clk_ID_EX), .Q(isJump_EX), .clr(clr_ID_EX));
  Register #(.width(1)) regBranch_ID_EX (
    .D(Branch_ID), .en(enable_id_ex), .clk(clk_ID_EX), .Q(Branch_EX), .clr(clr_ID_EX));
  Register #(.width(1)) regIsJR_ID_EX (.D(is_JR_ID), .en(enable_id_ex), .clk(clk_ID_EX), .Q(isJR_EX), .clr(clr_ID_EX));
  Register #(.width(4)) regALUOp_ID_EX (
    .D(ALUOp_ID), .en(enable_id_ex), .clk(clk_ID_EX), .Q(ALUOp_EX), .clr(clr_ID_EX));
  Register #(.width(5)) regWriteReg_ID_EX (
    .D(WriteReg_ID), .en(enable_id_ex), .clk(clk_ID_EX), .Q(WriteReg_EX), .clr(clr_ID_EX));
  Register #(.width(1)) regUpdateJTB_ID_EX (
    .D(updateJTB_ID), .en(enable_id_ex), .clk(clk_ID_EX), .Q(updateJTB_EX), .clr(clr_ID_EX));

  // Notes on the sheet:
  //   CLR
  //   CLK
endmodule

module MEM_WB (
  input  clk_mem_wb,
  input  clr_mem_wb,
  input  [31:0] ALUResult_mem,
  input  memToReg_mem,
  input  regWrite_mem,
  input  [31:0] ReadData_mem,
  input  [4:0] writeReg_mem,
  input  [31:0] JumpAddrMem,
  input  enable_mem_wb,
  output [31:0] ALUResult_wb,
  output memToReg_wb,
  output regWrite_wb,
  output [31:0] ReadData_wb,
  output [4:0] writeReg_wb,
  output [31:0] JumpAddr_wb
);

  Register #(.width(1)) regMemToReg (
    .D(memToReg_mem), .en(enable_mem_wb), .clk(clk_mem_wb), .Q(memToReg_wb), .clr(clr_mem_wb));
  Register #(.width(1)) regRegWrite (
    .D(regWrite_mem), .en(enable_mem_wb), .clk(clk_mem_wb), .Q(regWrite_wb), .clr(clr_mem_wb));
  Register #(.width(5)) regWriteReg (
    .D(writeReg_mem), .en(enable_mem_wb), .clk(clk_mem_wb), .Q(writeReg_wb), .clr(clr_mem_wb));
  Register #(.width(32)) regALUResult (
    .D(ALUResult_mem), .en(enable_mem_wb), .clk(clk_mem_wb), .Q(ALUResult_wb), .clr(clr_mem_wb));
  Register #(.width(32)) regReadData (
    .D(ReadData_mem), .en(enable_mem_wb), .clk(clk_mem_wb), .Q(ReadData_wb), .clr(clr_mem_wb));
  Register #(.width(32)) regJumAddr (
    .D(JumpAddrMem), .en(enable_mem_wb), .clk(clk_mem_wb), .Q(JumpAddr_wb), .clr(clr_mem_wb));
endmodule

module EX_MEM (
  input  clk_EX_MEM,
  input  clr_EX_MEM,
  input  MemToReg_Ex,
  input  [31:0] ALU_Result_EX,
  input  RegWrite_Ex,
  input  [31:0] WriteData_EX,
  input  MemRead_Ex,
  input  [31:0] JumpAddr_EX,
  input  MemWrite_EX,
  input  [4:0] WriteReg_EX,
  input  Enable_EX_MEM,
  output MemToReg_MEM,
  output [31:0] ALUResult_MEM,
  output RegWrite_MEM,
  output [31:0] WriteData_MEM,
  output MemRead_MEM,
  output [31:0] JumpAddr_MEM,
  output MemWrite_MEM,
  output [4:0] WriteReg_MEM
);

  Register #(.width(1)) regMemToReg_EX_MEM (
    .D(MemToReg_Ex), .en(Enable_EX_MEM), .clk(clk_EX_MEM), .Q(MemToReg_MEM), .clr(clr_EX_MEM));
  Register #(.width(1)) regRegWrite_EX_MEM (
    .D(RegWrite_Ex), .en(Enable_EX_MEM), .clk(clk_EX_MEM), .Q(RegWrite_MEM), .clr(clr_EX_MEM));
  Register #(.width(1)) MemRead_EX_MEM (
    .D(MemRead_Ex), .en(Enable_EX_MEM), .clk(clk_EX_MEM), .Q(MemRead_MEM), .clr(clr_EX_MEM));
  Register #(.width(1)) MemWrite_EX_MEM (
    .D(MemWrite_EX), .en(Enable_EX_MEM), .clk(clk_EX_MEM), .Q(MemWrite_MEM), .clr(clr_EX_MEM));
  Register #(.width(5)) WriteReg_EX_MEM (
    .D(WriteReg_EX), .en(Enable_EX_MEM), .clk(clk_EX_MEM), .Q(WriteReg_MEM), .clr(clr_EX_MEM));
  Register #(.width(32)) regALUResult (
    .D(ALU_Result_EX), .en(Enable_EX_MEM), .clk(clk_EX_MEM), .Q(ALUResult_MEM), .clr(clr_EX_MEM));
  Register #(.width(32)) regWriteData (
    .D(WriteData_EX), .en(Enable_EX_MEM), .clk(clk_EX_MEM), .Q(WriteData_MEM), .clr(clr_EX_MEM));
  Register #(.width(32)) regJumpAddr (
    .D(JumpAddr_EX), .en(Enable_EX_MEM), .clk(clk_EX_MEM), .Q(JumpAddr_MEM), .clr(clr_EX_MEM));
endmodule

module ControlUnit (
  input  [5:0] in_1,
  input  [5:0] in_2,
  output isShamt,
  output MemRead,
  output MemToReg,
  output MemWrite,
  output RegWrite,
  output Jump,
  output BneOrBeq,
  output Branch,
  output ALUSrc,
  output RegDst,
  output [3:0] ALUop,
  output ZeroExtend,
  output isJR,
  output ReadRs,
  output ReadRt
);

  wire functdecoder_1_isjr, functdecoder_1_isshamt, isSpecial, not_1_out, not_2_out, not_3_out, not_4_out,
       not_5_out, not_6_out, not_7_out, opcodedecoder_1_isjal;
  wire [3:0] aludecoder_1_aluop3, functdecoder_1_alu3;

  OpcodeDecoder opcodedecoder_1 (
    .op0(in_1[5]), .op1(in_1[4]), .op2(in_1[3]), .op3(in_1[2]), .op4(in_1[1]), .op5(in_1[0]),
    .MemRead(MemRead), .MemWrite(MemWrite), .BneBeq(BneOrBeq), .IsJAL(opcodedecoder_1_isjal),
    .MemToReg(MemToReg), .RegDst(RegDst), .ZeroExtend(ZeroExtend), .Jump(Jump), .Branch(Branch),
    .ALUSrc(ALUSrc), .RegWrite(RegWrite));
  ALUDecoder aludecoder_1 (
    .op0(in_1[5]), .op1(in_1[4]), .op2(in_1[3]), .op3(in_1[2]), .op4(in_1[1]), .op5(in_1[0]),
    .ALUop0(aludecoder_1_aluop3[3]), .ALUop1(aludecoder_1_aluop3[2]), .ALUop2(aludecoder_1_aluop3[1]),
    .ALUop3(aludecoder_1_aluop3[0]));
  FunctDecoder functdecoder_1 (
    .Funct0(in_2[5]), .Funct1(in_2[4]), .Funct2(in_2[3]), .Funct3(in_2[2]), .Funct4(in_2[1]),
    .Funct5(in_2[0]), .ALU0(functdecoder_1_alu3[3]), .ALU1(functdecoder_1_alu3[2]),
    .ALU2(functdecoder_1_alu3[1]), .ALU3(functdecoder_1_alu3[0]), .IsJR(functdecoder_1_isjr),
    .IsShamt(functdecoder_1_isshamt));
  not not_1 (not_1_out, isSpecial);
  RegisterRead registerread_1 (
    .op0(in_1[5]), .op1(in_1[4]), .op2(in_1[3]), .op3(in_1[2]), .op4(in_1[1]), .op5(in_1[0]),
    .Funct0(in_2[5]), .Funct1(in_2[4]), .Funct2(in_2[3]), .Funct3(in_2[2]), .Funct4(in_2[1]),
    .Funct5(in_2[0]), .ReadRt(ReadRt), .ReadRs(ReadRs));
  Multiplexer #(.width(4)) multiplexer_1 (
    .in0(functdecoder_1_alu3), .in1(aludecoder_1_aluop3), .out(ALUop), .sel(not_1_out));
  Multiplexer multiplexer_2 (.in0(1'b0), .in1(functdecoder_1_isjr), .out(isJR), .sel(isSpecial));
  Multiplexer multiplexer_3 (.in0(1'b0), .in1(functdecoder_1_isshamt), .out(isShamt), .sel(isSpecial));
  not not_2 (not_2_out, in_1[5]);
  not not_3 (not_3_out, in_1[4]);
  not not_4 (not_4_out, in_1[3]);
  not not_5 (not_5_out, in_1[2]);
  not not_6 (not_6_out, in_1[1]);
  not not_7 (not_7_out, in_1[0]);
  and and_1 (isSpecial, not_2_out, not_3_out, not_4_out, not_5_out, not_6_out, not_7_out);

  // Other names for the same wires on the sheet: Funct[5:0] = in_2; op[5:0] = in_1

  // Notes on the sheet:
  //   Entradas e Saidas
  //   OP Decoding Area
  //   ALU Decoding Area
endmodule

module OpcodeDecoder (
  input  op0,
  input  op1,
  input  op2,
  input  op3,
  input  op4,
  input  op5,
  output MemRead,
  output MemWrite,
  output BneBeq,
  output IsJAL,
  output MemToReg,
  output RegDst,
  output ZeroExtend,
  output Jump,
  output Branch,
  output ALUSrc,
  output RegWrite
);

  wire and_3_out, and_4_out, and_5_out, and_6_out, and_7_out, and_8_out, and_9_out, and_10_out, and_11_out,
       and_12_out, and_14_out, and_15_out, and_17_out, and_18_out, and_19_out, and_20_out, and_21_out,
       and_22_out, and_23_out, and_24_out, and_25_out, and_26_out, and_29_out, and_30_out, not_1_out,
       not_2_out, not_3_out, not_4_out, not_5_out, not_6_out, not_7_out, not_8_out, not_9_out, not_10_out,
       not_11_out, not_12_out, not_13_out, not_14_out, not_15_out, not_16_out, not_17_out, not_18_out,
       not_19_out, not_20_out, not_21_out, not_22_out, not_23_out, not_24_out, not_25_out, not_26_out,
       not_27_out, not_28_out, not_29_out, not_30_out, not_31_out, not_32_out, not_33_out, not_34_out,
       not_35_out, not_36_out, not_37_out, not_38_out, not_39_out, not_40_out, not_41_out, not_42_out,
       not_43_out, not_44_out, not_45_out, not_46_out, not_47_out, not_48_out, not_49_out, not_50_out,
       not_51_out, not_52_out, not_53_out, not_54_out, not_55_out, not_56_out, not_57_out, not_58_out,
       not_59_out, not_60_out, not_61_out, not_62_out, not_63_out, not_64_out, not_65_out, not_66_out,
       not_67_out, not_68_out, not_69_out, not_70_out, not_71_out, not_72_out, not_73_out, not_74_out,
       not_75_out, not_76_out, not_77_out, not_78_out, not_79_out, not_80_out, not_81_out, not_82_out,
       not_83_out, not_84_out, not_85_out, not_86_out, not_87_out, not_88_out, not_89_out, not_90_out,
       not_91_out, not_92_out, not_93_out, not_94_out, not_95_out, not_96_out, not_97_out, not_98_out,
       not_99_out, not_100_out, not_101_out, not_102_out, not_103_out, not_104_out, not_105_out, not_106_out,
       not_107_out, not_108_out, not_109_out, not_110_out, not_111_out, not_112_out, not_113_out,
       not_114_out, not_115_out, not_116_out, not_117_out, not_118_out, not_119_out;

  not not_1 (not_1_out, op1);
  not not_2 (not_2_out, op2);
  not not_3 (not_3_out, op3);
  not not_4 (not_4_out, op1);
  and and_1 (MemRead, op0, not_1_out, not_2_out, not_3_out, op4, op5);
  not not_5 (not_5_out, op3);
  not not_6 (not_6_out, op0);
  and and_2 (MemWrite, op0, not_4_out, op2, not_5_out, op4, op5);
  not not_7 (not_7_out, op1);
  not not_8 (not_8_out, op3);
  not not_9 (not_9_out, op4);
  not not_10 (not_10_out, op5);
  and and_3 (and_3_out, not_6_out, not_7_out, op2, not_8_out, not_9_out, not_10_out);
  not not_11 (not_11_out, op1);
  not not_12 (not_12_out, op2);
  not not_13 (not_13_out, op3);
  and and_4 (and_4_out, op0, not_11_out, not_12_out, not_13_out, op4, op5);
  not not_14 (not_14_out, op1);
  not not_15 (not_15_out, op3);
  and and_5 (and_5_out, op0, not_14_out, op2, not_15_out, op4, op5);
  not not_16 (not_16_out, op0);
  not not_17 (not_17_out, op1);
  not not_18 (not_18_out, op4);
  and and_6 (and_6_out, not_16_out, not_17_out, op2, op3, not_18_out, not_19_out);
  not not_19 (not_19_out, op5);
  not not_20 (not_20_out, op0);
  not not_21 (not_21_out, op1);
  and and_7 (and_7_out, not_20_out, not_21_out, op2, op3, not_22_out, op5);
  or or_1 (ALUSrc, and_3_out, and_4_out, and_5_out, and_6_out, and_7_out, and_8_out, and_9_out, and_10_out);
  not not_22 (not_22_out, op4);
  not not_23 (not_23_out, op0);
  not not_24 (not_24_out, op1);
  and and_8 (and_8_out, not_23_out, not_24_out, op2, not_25_out, op4, not_26_out);
  not not_25 (not_25_out, op3);
  not not_26 (not_26_out, op5);
  not not_27 (not_27_out, op0);
  not not_28 (not_28_out, op1);
  not not_29 (not_29_out, op3);
  not not_30 (not_30_out, op4);
  not not_31 (not_31_out, op0);
  not not_32 (not_32_out, op1);
  and and_9 (and_9_out, not_27_out, not_28_out, op2, not_29_out, not_30_out, op5);
  not not_33 (not_33_out, op5);
  not not_34 (not_34_out, op0);
  not not_35 (not_35_out, op3);
  not not_36 (not_36_out, op4);
  and and_10 (and_10_out, not_31_out, not_32_out, op2, not_35_out, not_36_out, not_33_out);
  not not_37 (not_37_out, op1);
  not not_38 (not_38_out, op2);
  not not_39 (not_39_out, op3);
  not not_40 (not_40_out, op5);
  and and_11 (and_11_out, not_34_out, not_37_out, not_38_out, not_39_out, op4, not_40_out);
  not not_41 (not_41_out, op0);
  not not_42 (not_42_out, op1);
  not not_43 (not_43_out, op2);
  not not_44 (not_44_out, op3);
  and and_12 (and_12_out, not_41_out, not_42_out, not_43_out, not_44_out, op4, op5);
  or or_2 (Jump, and_11_out, and_12_out);
  not not_45 (not_45_out, op1);
  not not_46 (not_46_out, op2);
  not not_47 (not_47_out, op3);
  and and_13 (MemToReg, op0, not_45_out, not_46_out, not_47_out, op4, op5);
  not not_48 (not_48_out, op0);
  not not_49 (not_49_out, op1);
  not not_50 (not_50_out, op2);
  not not_51 (not_51_out, op4);
  and and_14 (and_14_out, not_48_out, not_49_out, not_50_out, op3, not_51_out, op5);
  not not_52 (not_52_out, op0);
  not not_53 (not_53_out, op1);
  not not_54 (not_54_out, op2);
  and and_15 (and_15_out, not_52_out, not_53_out, not_54_out, op3, not_55_out, not_56_out);
  or or_3 (Branch, and_14_out, and_15_out);
  not not_55 (not_55_out, op4);
  not not_56 (not_56_out, op5);
  not not_57 (not_57_out, op0);
  not not_58 (not_58_out, op1);
  not not_59 (not_59_out, op2);
  and and_16 (RegDst, not_57_out, not_58_out, not_59_out, not_60_out, not_61_out, not_62_out);
  not not_60 (not_60_out, op3);
  not not_61 (not_61_out, op4);
  not not_62 (not_62_out, op5);
  not not_63 (not_63_out, op0);
  not not_64 (not_64_out, op1);
  not not_65 (not_65_out, op2);
  not not_66 (not_66_out, op3);
  not not_67 (not_67_out, op4);
  not not_68 (not_68_out, op5);
  not not_69 (not_69_out, op0);
  not not_70 (not_70_out, op1);
  and and_17 (and_17_out, not_63_out, not_64_out, not_65_out, not_66_out, not_67_out, not_68_out);
  not not_71 (not_71_out, op3);
  not not_72 (not_72_out, op4);
  not not_73 (not_73_out, op5);
  and and_18 (and_18_out, not_69_out, not_70_out, op2, not_71_out, not_72_out, not_73_out);
  not not_74 (not_74_out, op1);
  not not_75 (not_75_out, op2);
  not not_76 (not_76_out, op3);
  and and_19 (and_19_out, op0, not_74_out, not_75_out, not_76_out, op4, op5);
  not not_77 (not_77_out, op0);
  not not_78 (not_78_out, op1);
  not not_79 (not_79_out, op4);
  not not_80 (not_80_out, op5);
  and and_20 (and_20_out, not_77_out, not_78_out, op2, op3, not_79_out, not_80_out);
  not not_81 (not_81_out, op0);
  not not_82 (not_82_out, op1);
  not not_83 (not_83_out, op4);
  and and_21 (and_21_out, not_81_out, not_82_out, op2, op3, not_83_out, op5);
  or or_4 (RegWrite, and_17_out, and_18_out, and_19_out, and_20_out, and_21_out, and_22_out, and_23_out, and_24_out, and_25_out, and_26_out);
  not not_84 (not_84_out, op0);
  not not_85 (not_85_out, op1);
  not not_86 (not_86_out, op3);
  and and_22 (and_22_out, not_84_out, not_85_out, op2, not_86_out, op4, not_87_out);
  not not_87 (not_87_out, op5);
  not not_88 (not_88_out, op0);
  not not_89 (not_89_out, op1);
  not not_90 (not_90_out, op3);
  and and_23 (and_23_out, not_88_out, not_89_out, op2, not_90_out, not_91_out, op5);
  not not_91 (not_91_out, op4);
  not not_92 (not_92_out, op0);
  not not_93 (not_93_out, op1);
  and and_24 (and_24_out, not_92_out, not_93_out, op2, not_94_out, not_95_out, not_96_out);
  not not_94 (not_94_out, op3);
  not not_95 (not_95_out, op4);
  not not_96 (not_96_out, op5);
  not not_97 (not_97_out, op0);
  not not_98 (not_98_out, op1);
  not not_99 (not_99_out, op2);
  not not_100 (not_100_out, op3);
  not not_101 (not_101_out, op0);
  and and_25 (and_25_out, not_97_out, not_98_out, not_99_out, not_100_out, op4, op5);
  not not_102 (not_102_out, op2);
  not not_103 (not_103_out, op3);
  not not_104 (not_104_out, op4);
  not not_105 (not_105_out, op5);
  not not_106 (not_106_out, op0);
  and and_26 (and_26_out, not_101_out, op1, not_102_out, not_103_out, not_104_out, not_105_out);
  not not_107 (not_107_out, op1);
  not not_108 (not_108_out, op2);
  not not_109 (not_109_out, op4);
  and and_27 (BneBeq, not_106_out, not_107_out, not_108_out, op3, not_109_out, op5);
  not not_110 (not_110_out, op0);
  not not_111 (not_111_out, op1);
  not not_112 (not_112_out, op2);
  not not_113 (not_113_out, op3);
  and and_28 (IsJAL, not_110_out, not_111_out, not_112_out, not_113_out, op4, op5);
  not not_114 (not_114_out, op0);
  not not_115 (not_115_out, op1);
  not not_116 (not_116_out, op4);
  and and_29 (and_29_out, not_114_out, not_115_out, op2, op3, not_116_out);
  not not_117 (not_117_out, op0);
  not not_118 (not_118_out, op1);
  and and_30 (and_30_out, not_117_out, not_118_out, op2, op3, op4, not_119_out);
  or or_5 (ZeroExtend, and_29_out, and_30_out);
  not not_119 (not_119_out, op5);
endmodule

module RegisterRead (
  input  op0,
  input  op1,
  input  op2,
  input  op3,
  input  op4,
  input  op5,
  input  Funct0,
  input  Funct1,
  input  Funct2,
  input  Funct3,
  input  Funct4,
  input  Funct5,
  output ReadRt,
  output ReadRs
);

  wire and_1_out, and_2_out, and_3_out, and_4_out, and_5_out, and_6_out, and_7_out, and_8_out, and_9_out,
       and_10_out, and_11_out, and_12_out, and_13_out, and_14_out, and_15_out, and_16_out, and_17_out,
       and_18_out, and_19_out, and_20_out, and_21_out, and_22_out, and_23_out, and_24_out, and_25_out,
       and_26_out, and_27_out, and_28_out, and_29_out, and_30_out, and_31_out, and_32_out, and_33_out,
       and_34_out, and_35_out, not_1_out, not_2_out, not_3_out, not_4_out, not_5_out, not_6_out, not_7_out,
       not_8_out, not_9_out, not_10_out, not_11_out, not_12_out, not_13_out, not_14_out, not_15_out,
       not_16_out, not_17_out, not_18_out, not_19_out, not_20_out, not_21_out, not_22_out, not_23_out,
       not_24_out, not_25_out, not_26_out, not_27_out, not_28_out, not_29_out, not_30_out, not_31_out,
       not_32_out, not_33_out, not_34_out, not_35_out, not_36_out, not_37_out, not_38_out, not_39_out,
       not_40_out, not_41_out, not_42_out, not_43_out, not_44_out, not_45_out, not_46_out, not_47_out,
       not_48_out, not_49_out, not_50_out, not_51_out, not_52_out, not_53_out, not_54_out, not_58_out,
       not_59_out, not_60_out, not_61_out, not_62_out, not_63_out, not_64_out, not_65_out, not_66_out,
       not_67_out, not_68_out, not_69_out, not_70_out, not_71_out, not_72_out, not_73_out, not_74_out,
       not_75_out, not_76_out, not_77_out, not_78_out, not_79_out, not_80_out, not_81_out, not_82_out,
       not_83_out, not_84_out, not_85_out, not_86_out, not_87_out, not_88_out, not_89_out, not_90_out,
       not_91_out, not_92_out, not_93_out, not_94_out, not_95_out, not_96_out, not_97_out, not_98_out,
       not_99_out, not_100_out, not_101_out, not_102_out, not_103_out, not_104_out, not_105_out, not_106_out,
       not_107_out, not_108_out, not_109_out, not_110_out, not_111_out, not_112_out, not_113_out,
       not_114_out, not_115_out, not_116_out, not_117_out, not_118_out, not_119_out, not_120_out,
       not_121_out, not_122_out, not_123_out, not_124_out, not_125_out, not_126_out, not_127_out,
       not_128_out, not_129_out, not_130_out, not_131_out, not_132_out, not_133_out, not_134_out,
       not_135_out, not_136_out, not_137_out, not_138_out, not_139_out, not_151_out, not_156_out,
       not_159_out, not_160_out, not_164_out, not_165_out, not_167_out, not_168_out, not_169_out,
       not_170_out, not_172_out, not_180_out, not_181_out, not_182_out, not_183_out, not_190_out,
       not_192_out, not_193_out, not_194_out, not_196_out, not_197_out, not_198_out, not_199_out,
       not_207_out, not_208_out, not_216_out, not_217_out, not_220_out, not_221_out, not_223_out,
       not_233_out, not_246_out, not_261_out, not_262_out, not_270_out, not_271_out, not_272_out,
       not_273_out, not_275_out, not_282_out, not_284_out, not_285_out, not_286_out, not_292_out,
       not_298_out, not_299_out, not_300_out, not_301_out, not_303_out, not_310_out, not_311_out,
       not_312_out, not_314_out, not_315_out, not_316_out, not_323_out, not_324_out, not_326_out,
       not_328_out, not_329_out, not_337_out, not_338_out, not_340_out, not_341_out, not_342_out,
       not_343_out, not_344_out, not_346_out, not_353_out, not_355_out, not_356_out, not_357_out,
       not_359_out, not_360_out, not_361_out, not_369_out, or_1_out, or_3_out;

  not not_1 (not_1_out, op0);
  not not_2 (not_2_out, op1);
  not not_3 (not_3_out, op2);
  not not_4 (not_4_out, op3);
  not not_5 (not_5_out, op4);
  not not_6 (not_6_out, op5);
  and and_1 (and_1_out, not_1_out, not_2_out, not_3_out, not_4_out, not_5_out, not_6_out, or_1_out);
  not not_7 (not_7_out, Funct1);
  not not_8 (not_8_out, Funct2);
  and and_2 (and_2_out, Funct0, not_7_out, not_8_out, not_9_out, not_10_out, not_11_out);
  not not_9 (not_9_out, Funct3);
  not not_10 (not_10_out, Funct4);
  not not_11 (not_11_out, Funct4);
  not not_12 (not_12_out, Funct1);
  not not_13 (not_13_out, Funct2);
  not not_14 (not_14_out, Funct4);
  not not_15 (not_15_out, Funct5);
  and and_3 (and_3_out, Funct0, not_12_out, not_13_out, Funct3, not_14_out, not_15_out);
  not not_16 (not_16_out, Funct1);
  not not_17 (not_17_out, Funct2);
  and and_4 (and_4_out, Funct0, not_16_out, not_17_out, not_18_out, not_19_out, Funct5);
  not not_18 (not_18_out, Funct3);
  not not_19 (not_19_out, Funct4);
  not not_20 (not_20_out, Funct1);
  not not_21 (not_21_out, Funct2);
  not not_22 (not_22_out, Funct3);
  not not_23 (not_23_out, Funct5);
  and and_5 (and_5_out, Funct0, not_20_out, not_21_out, not_22_out, Funct4, not_23_out);
  not not_24 (not_24_out, Funct1);
  not not_25 (not_25_out, Funct2);
  and and_6 (and_6_out, Funct0, not_24_out, not_25_out, Funct3, not_26_out, Funct5);
  or or_1 (or_1_out, and_2_out, and_3_out, and_4_out, and_5_out, and_6_out, and_7_out, and_8_out, and_9_out, and_10_out);
  not not_26 (not_26_out, Funct4);
  not not_27 (not_27_out, Funct1);
  not not_28 (not_28_out, Funct2);
  and and_7 (and_7_out, Funct0, not_27_out, not_28_out, Funct3, Funct4, Funct5);
  not not_29 (not_29_out, Funct1);
  and and_8 (and_8_out, Funct0, not_29_out, Funct2, not_30_out, Funct4, not_31_out);
  not not_30 (not_30_out, Funct3);
  not not_31 (not_31_out, Funct5);
  not not_32 (not_32_out, Funct1);
  not not_33 (not_33_out, Funct3);
  and and_9 (and_9_out, Funct0, not_32_out, Funct2, not_33_out, Funct4, Funct5);
  not not_34 (not_34_out, Funct0);
  not not_35 (not_35_out, Funct1);
  and and_10 (and_10_out, not_34_out, not_35_out, Funct2, not_36_out, not_37_out, not_38_out);
  not not_36 (not_36_out, Funct3);
  not not_37 (not_37_out, Funct4);
  not not_38 (not_38_out, Funct5);
  not not_39 (not_39_out, op0);
  not not_40 (not_40_out, op1);
  not not_41 (not_41_out, op3);
  not not_42 (not_42_out, op4);
  not not_43 (not_43_out, op5);
  and and_11 (and_11_out, not_39_out, not_40_out, op2, not_41_out, not_42_out, not_43_out);
  not not_44 (not_44_out, op0);
  not not_45 (not_45_out, op1);
  and and_12 (and_12_out, not_44_out, not_45_out, op2, not_46_out, not_47_out, op5);
  not not_46 (not_46_out, op3);
  not not_47 (not_47_out, op4);
  not not_48 (not_48_out, op0);
  not not_49 (not_49_out, op1);
  not not_50 (not_50_out, op4);
  not not_51 (not_51_out, op5);
  and and_13 (and_13_out, not_48_out, not_49_out, op2, op3, not_50_out, not_51_out);
  not not_52 (not_52_out, op0);
  not not_53 (not_53_out, op1);
  and and_14 (and_14_out, not_52_out, not_53_out, op2, op3, not_54_out, op5);
  not not_54 (not_54_out, op4);
  // NOT_Gate not_55 is placed but not wired
  // NOT_Gate not_56 is placed but not wired
  // NOT_Gate not_57 is placed but not wired
  not not_58 (not_58_out, op1);
  not not_59 (not_59_out, op2);
  not not_60 (not_60_out, op3);
  and and_15 (and_15_out, op0, not_58_out, not_59_out, not_60_out, op4, op5);
  or or_2 (ReadRs, and_1_out, and_11_out, and_12_out, and_13_out, and_14_out, and_15_out, and_16_out, and_17_out, and_18_out, and_19_out);
  not not_61 (not_61_out, op0);
  not not_62 (not_62_out, op1);
  not not_63 (not_63_out, op2);
  and and_16 (and_16_out, not_61_out, not_62_out, not_63_out, op3, not_64_out, not_65_out);
  not not_64 (not_64_out, op4);
  not not_65 (not_65_out, op5);
  not not_66 (not_66_out, op0);
  not not_67 (not_67_out, op1);
  not not_68 (not_68_out, op2);
  not not_69 (not_69_out, op4);
  and and_17 (and_17_out, not_66_out, not_67_out, not_68_out, op3, not_69_out, op5);
  not not_70 (not_70_out, op0);
  not not_71 (not_71_out, op1);
  and and_18 (and_18_out, not_70_out, not_71_out, op2, not_72_out, op4, not_73_out);
  not not_72 (not_72_out, op3);
  not not_73 (not_73_out, op5);
  not not_74 (not_74_out, op1);
  not not_75 (not_75_out, op3);
  and and_19 (and_19_out, op0, not_74_out, op2, not_75_out, op4, op5);
  not not_76 (not_76_out, op0);
  not not_77 (not_77_out, op1);
  not not_78 (not_78_out, op2);
  not not_79 (not_79_out, op3);
  and and_20 (and_20_out, not_76_out, not_77_out, not_78_out, not_79_out, not_80_out, not_81_out, or_3_out);
  not not_80 (not_80_out, op4);
  not not_81 (not_81_out, op5);
  not not_82 (not_82_out, Funct1);
  not not_83 (not_83_out, Funct2);
  not not_84 (not_84_out, Funct3);
  not not_85 (not_85_out, Funct4);
  not not_86 (not_86_out, Funct5);
  and and_21 (and_21_out, Funct0, not_82_out, not_83_out, not_84_out, not_85_out, not_86_out);
  not not_87 (not_87_out, Funct1);
  not not_88 (not_88_out, Funct2);
  and and_22 (and_22_out, Funct0, not_87_out, not_88_out, not_89_out, not_90_out, Funct5);
  not not_89 (not_89_out, Funct3);
  not not_90 (not_90_out, Funct4);
  not not_91 (not_91_out, Funct1);
  not not_92 (not_92_out, Funct2);
  not not_93 (not_93_out, Funct4);
  not not_94 (not_94_out, Funct5);
  and and_23 (and_23_out, Funct0, not_91_out, not_92_out, Funct3, not_93_out, not_94_out);
  not not_95 (not_95_out, Funct0);
  not not_96 (not_96_out, Funct1);
  not not_97 (not_97_out, Funct2);
  and and_24 (and_24_out, not_95_out, not_96_out, not_97_out, not_98_out, not_99_out, not_100_out);
  or or_3 (or_3_out, and_21_out, and_22_out, and_23_out, and_24_out, and_25_out, and_26_out, and_27_out, and_28_out, and_29_out, and_30_out, and_31_out);
  not not_98 (not_98_out, Funct3);
  not not_99 (not_99_out, Funct4);
  not not_100 (not_100_out, Funct5);
  not not_101 (not_101_out, Funct0);
  not not_102 (not_102_out, Funct1);
  not not_103 (not_103_out, Funct2);
  not not_104 (not_104_out, Funct3);
  and and_25 (and_25_out, not_101_out, not_102_out, not_103_out, not_104_out, Funct4, Funct5);
  not not_105 (not_105_out, Funct0);
  not not_106 (not_106_out, Funct1);
  not not_107 (not_107_out, Funct2);
  and and_26 (and_26_out, not_105_out, not_106_out, not_107_out, not_108_out, Funct4, not_109_out);
  not not_108 (not_108_out, Funct3);
  not not_109 (not_109_out, Funct5);
  not not_110 (not_110_out, Funct1);
  not not_111 (not_111_out, Funct2);
  not not_112 (not_112_out, Funct3);
  not not_113 (not_113_out, Funct5);
  and and_27 (and_27_out, Funct0, not_110_out, not_111_out, not_112_out, Funct4, not_113_out);
  not not_114 (not_114_out, Funct1);
  not not_115 (not_115_out, Funct2);
  and and_28 (and_28_out, Funct0, not_114_out, not_115_out, Funct3, not_116_out, Funct5);
  not not_116 (not_116_out, Funct4);
  not not_117 (not_117_out, Funct1);
  not not_118 (not_118_out, Funct2);
  and and_29 (and_29_out, Funct0, not_117_out, not_118_out, Funct3, Funct4, Funct5);
  not not_119 (not_119_out, Funct1);
  and and_30 (and_30_out, Funct0, not_119_out, Funct2, not_120_out, Funct4, not_121_out);
  not not_120 (not_120_out, Funct3);
  not not_121 (not_121_out, Funct5);
  not not_122 (not_122_out, Funct1);
  not not_123 (not_123_out, Funct3);
  and and_31 (and_31_out, Funct0, not_122_out, Funct2, not_123_out, Funct4, Funct5);
  not not_124 (not_124_out, op0);
  not not_125 (not_125_out, op1);
  not not_126 (not_126_out, op2);
  and and_32 (and_32_out, not_124_out, not_125_out, not_126_out, op3, not_127_out, not_128_out);
  not not_127 (not_127_out, op4);
  not not_128 (not_128_out, op5);
  not not_129 (not_129_out, op0);
  not not_130 (not_130_out, op1);
  not not_131 (not_131_out, op2);
  not not_132 (not_132_out, op4);
  and and_33 (and_33_out, not_129_out, not_130_out, not_131_out, op3, not_132_out, op5);
  or or_4 (ReadRt, and_20_out, and_32_out, and_33_out, and_34_out, and_35_out);
  not not_133 (not_133_out, op0);
  not not_134 (not_134_out, op2);
  and and_34 (and_34_out, not_133_out, op1, not_134_out, not_135_out, not_136_out, not_137_out);
  not not_135 (not_135_out, op3);
  not not_136 (not_136_out, op4);
  not not_137 (not_137_out, op5);
  not not_138 (not_138_out, op1);
  not not_139 (not_139_out, op3);
  and and_35 (and_35_out, op0, not_138_out, op2, not_139_out, op4, op5);
  // NOT_Gate not_140 is placed but not wired
  // NOT_Gate not_141 is placed but not wired
  // NOT_Gate not_142 is placed but not wired
  // NOT_Gate not_143 is placed but not wired
  // NOT_Gate not_144 is placed but not wired
  // NOT_Gate not_145 is placed but not wired
  // NOT_Gate not_146 is placed but not wired
  // AND_Gate and_36 is placed but not wired
  // NOT_Gate not_147 is placed but not wired
  // NOT_Gate not_148 is placed but not wired
  // NOT_Gate not_149 is placed but not wired
  // NOT_Gate not_150 is placed but not wired
  // NOT_Gate not_151 has open pins: in=open, out=not_151_out
  // NOT_Gate not_152 is placed but not wired
  // NOT_Gate not_153 is placed but not wired
  // NOT_Gate not_154 has open pins: in=not_151_out, out=open
  // NOT_Gate not_155 is placed but not wired
  // NOT_Gate not_156 has open pins: in=open, out=not_156_out
  // NOT_Gate not_157 has open pins: in=not_156_out, out=open
  // NOT_Gate not_158 is placed but not wired
  // NOT_Gate not_159 has open pins: in=open, out=not_159_out
  // NOT_Gate not_160 has open pins: in=open, out=not_160_out
  // NOT_Gate not_161 has open pins: in=not_159_out, out=open
  // NOT_Gate not_162 is placed but not wired
  // NOT_Gate not_163 has open pins: in=not_160_out, out=open
  // AND_Gate and_37 is placed but not wired
  // NOT_Gate not_164 has open pins: in=open, out=not_164_out
  // NOT_Gate not_165 has open pins: in=open, out=not_165_out
  // NOT_Gate not_166 is placed but not wired
  // NOT_Gate not_167 has open pins: in=open, out=not_167_out
  not not_168 (not_168_out, not_164_out);
  not not_169 (not_169_out, not_165_out);
  // NOT_Gate not_170 has open pins: in=open, out=not_170_out
  // NOT_Gate not_171 is placed but not wired
  not not_172 (not_172_out, not_167_out);
  // NOT_Gate not_173 has open pins: in=not_168_out, out=open
  // NOT_Gate not_174 has open pins: in=not_169_out, out=open
  // NOT_Gate not_175 has open pins: in=not_170_out, out=open
  // NOT_Gate not_176 is placed but not wired
  // NOT_Gate not_177 has open pins: in=not_172_out, out=open
  // NOT_Gate not_178 is placed but not wired
  // NOT_Gate not_179 is placed but not wired
  // NOT_Gate not_180 has open pins: in=open, out=not_180_out
  // NOT_Gate not_181 has open pins: in=open, out=not_181_out
  // NOT_Gate not_182 has open pins: in=open, out=not_182_out
  // NOT_Gate not_183 has open pins: in=open, out=not_183_out
  // NOT_Gate not_184 is placed but not wired
  // NOT_Gate not_185 has open pins: in=not_180_out, out=open
  // NOT_Gate not_186 has open pins: in=not_181_out, out=open
  // NOT_Gate not_187 has open pins: in=not_182_out, out=open
  // NOT_Gate not_188 has open pins: in=not_183_out, out=open
  // NOT_Gate not_189 is placed but not wired
  // AND_Gate and_38 is placed but not wired
  // NOT_Gate not_190 has open pins: in=open, out=not_190_out
  // NOT_Gate not_191 is placed but not wired
  // NOT_Gate not_192 has open pins: in=open, out=not_192_out
  // NOT_Gate not_193 has open pins: in=open, out=not_193_out
  not not_194 (not_194_out, not_190_out);
  // NOT_Gate not_195 is placed but not wired
  // NOT_Gate not_196 has open pins: in=open, out=not_196_out
  not not_197 (not_197_out, not_192_out);
  not not_198 (not_198_out, not_193_out);
  // NOT_Gate not_199 has open pins: in=open, out=not_199_out
  // NOT_Gate not_200 has open pins: in=not_194_out, out=open
  // NOT_Gate not_201 is placed but not wired
  // NOT_Gate not_202 has open pins: in=not_196_out, out=open
  // NOT_Gate not_203 has open pins: in=not_197_out, out=open
  // NOT_Gate not_204 has open pins: in=not_198_out, out=open
  // NOT_Gate not_205 has open pins: in=not_199_out, out=open
  // NOT_Gate not_206 is placed but not wired
  // NOT_Gate not_207 has open pins: in=open, out=not_207_out
  // NOT_Gate not_208 has open pins: in=open, out=not_208_out
  // NOT_Gate not_209 is placed but not wired
  // NOT_Gate not_210 has open pins: in=not_207_out, out=open
  // NOT_Gate not_211 is placed but not wired
  // NOT_Gate not_212 has open pins: in=not_208_out, out=open
  // NOT_Gate not_213 is placed but not wired
  // NOT_Gate not_214 is placed but not wired
  // NOT_Gate not_215 is placed but not wired
  // NOT_Gate not_216 has open pins: in=open, out=not_216_out
  // NOT_Gate not_217 has open pins: in=open, out=not_217_out
  // NOT_Gate not_218 is placed but not wired
  // NOT_Gate not_219 is placed but not wired
  not not_220 (not_220_out, not_216_out);
  not not_221 (not_221_out, not_217_out);
  // NOT_Gate not_222 is placed but not wired
  // NOT_Gate not_223 has open pins: in=open, out=not_223_out
  // NOT_Gate not_224 is placed but not wired
  // NOT_Gate not_225 has open pins: in=not_220_out, out=open
  // NOT_Gate not_226 is placed but not wired
  // NOT_Gate not_227 has open pins: in=not_221_out, out=open
  // NOT_Gate not_228 is placed but not wired
  // NOT_Gate not_229 has open pins: in=not_223_out, out=open
  // NOT_Gate not_230 is placed but not wired
  // NOT_Gate not_231 is placed but not wired
  // NOT_Gate not_232 is placed but not wired
  // AND_Gate and_39 is placed but not wired
  // NOT_Gate not_233 has open pins: in=open, out=not_233_out
  // NOT_Gate not_234 is placed but not wired
  // NOT_Gate not_235 is placed but not wired
  // NOT_Gate not_236 is placed but not wired
  // NOT_Gate not_237 is placed but not wired
  // NOT_Gate not_238 has open pins: in=not_233_out, out=open
  // NOT_Gate not_239 is placed but not wired
  // NOT_Gate not_240 is placed but not wired
  // AND_Gate and_40 is placed but not wired
  // NOT_Gate not_241 is placed but not wired
  // NOT_Gate not_242 is placed but not wired
  // NOT_Gate not_243 is placed but not wired
  // NOT_Gate not_244 is placed but not wired
  // NOT_Gate not_245 is placed but not wired
  // NOT_Gate not_246 has open pins: in=open, out=not_246_out
  // NOT_Gate not_247 has open pins: in=not_246_out, out=open
  // NOT_Gate not_248 is placed but not wired
  // NOT_Gate not_249 is placed but not wired
  // NOT_Gate not_250 is placed but not wired
  // NOT_Gate not_251 is placed but not wired
  // NOT_Gate not_252 is placed but not wired
  // NOT_Gate not_253 is placed but not wired
  // NOT_Gate not_254 is placed but not wired
  // NOT_Gate not_255 is placed but not wired
  // NOT_Gate not_256 is placed but not wired
  // NOT_Gate not_257 is placed but not wired
  // NOT_Gate not_258 is placed but not wired
  // AND_Gate and_41 is placed but not wired
  // NOT_Gate not_259 is placed but not wired
  // NOT_Gate not_260 is placed but not wired
  // NOT_Gate not_261 has open pins: in=open, out=not_261_out
  // NOT_Gate not_262 has open pins: in=open, out=not_262_out
  // NOT_Gate not_263 is placed but not wired
  // NOT_Gate not_264 is placed but not wired
  // NOT_Gate not_265 is placed but not wired
  // NOT_Gate not_266 has open pins: in=not_261_out, out=open
  // NOT_Gate not_267 is placed but not wired
  // NOT_Gate not_268 has open pins: in=not_262_out, out=open
  // NOT_Gate not_269 is placed but not wired
  // AND_Gate and_42 is placed but not wired
  // NOT_Gate not_270 has open pins: in=open, out=not_270_out
  // NOT_Gate not_271 has open pins: in=open, out=not_271_out
  // NOT_Gate not_272 has open pins: in=open, out=not_272_out
  // NOT_Gate not_273 has open pins: in=open, out=not_273_out
  // NOT_Gate not_274 is placed but not wired
  // NOT_Gate not_275 has open pins: in=open, out=not_275_out
  // NOT_Gate not_276 has open pins: in=not_270_out, out=open
  // NOT_Gate not_277 has open pins: in=not_271_out, out=open
  // NOT_Gate not_278 has open pins: in=not_272_out, out=open
  // NOT_Gate not_279 has open pins: in=not_273_out, out=open
  // NOT_Gate not_280 is placed but not wired
  // NOT_Gate not_281 has open pins: in=not_275_out, out=open
  // NOT_Gate not_282 has open pins: in=open, out=not_282_out
  // NOT_Gate not_283 is placed but not wired
  // NOT_Gate not_284 has open pins: in=open, out=not_284_out
  // NOT_Gate not_285 has open pins: in=open, out=not_285_out
  // NOT_Gate not_286 has open pins: in=open, out=not_286_out
  // NOT_Gate not_287 is placed but not wired
  // NOT_Gate not_288 has open pins: in=not_282_out, out=open
  // NOT_Gate not_289 has open pins: in=not_284_out, out=open
  // NOT_Gate not_290 has open pins: in=not_285_out, out=open
  // NOT_Gate not_291 has open pins: in=not_286_out, out=open
  // AND_Gate and_43 is placed but not wired
  // NOT_Gate not_292 has open pins: in=open, out=not_292_out
  // NOT_Gate not_293 has open pins: in=not_292_out, out=open
  // NOT_Gate not_294 is placed but not wired
  // NOT_Gate not_295 is placed but not wired
  // NOT_Gate not_296 is placed but not wired
  // NOT_Gate not_297 is placed but not wired
  // AND_Gate and_44 is placed but not wired
  // NOT_Gate not_298 has open pins: in=open, out=not_298_out
  // NOT_Gate not_299 has open pins: in=open, out=not_299_out
  // NOT_Gate not_300 has open pins: in=open, out=not_300_out
  // NOT_Gate not_301 has open pins: in=open, out=not_301_out
  // NOT_Gate not_302 is placed but not wired
  // NOT_Gate not_303 has open pins: in=open, out=not_303_out
  // NOT_Gate not_304 has open pins: in=not_298_out, out=open
  // NOT_Gate not_305 has open pins: in=not_299_out, out=open
  // NOT_Gate not_306 has open pins: in=not_300_out, out=open
  // NOT_Gate not_307 has open pins: in=not_301_out, out=open
  // NOT_Gate not_308 is placed but not wired
  // NOT_Gate not_309 has open pins: in=not_303_out, out=open
  // NOT_Gate not_310 has open pins: in=open, out=not_310_out
  // NOT_Gate not_311 has open pins: in=open, out=not_311_out
  // NOT_Gate not_312 has open pins: in=open, out=not_312_out
  // NOT_Gate not_313 is placed but not wired
  // NOT_Gate not_314 has open pins: in=open, out=not_314_out
  not not_315 (not_315_out, not_310_out);
  not not_316 (not_316_out, not_311_out);
  // NOT_Gate not_317 is placed but not wired
  // NOT_Gate not_318 has open pins: in=not_312_out, out=open
  // NOT_Gate not_319 has open pins: in=not_314_out, out=open
  // NOT_Gate not_320 has open pins: in=not_315_out, out=open
  // NOT_Gate not_321 has open pins: in=not_316_out, out=open
  // NOT_Gate not_322 is placed but not wired
  // NOT_Gate not_323 has open pins: in=open, out=not_323_out
  // NOT_Gate not_324 has open pins: in=open, out=not_324_out
  // NOT_Gate not_325 is placed but not wired
  // NOT_Gate not_326 has open pins: in=open, out=not_326_out
  // NOT_Gate not_327 is placed but not wired
  not not_328 (not_328_out, not_323_out);
  not not_329 (not_329_out, not_324_out);
  // NOT_Gate not_330 is placed but not wired
  // NOT_Gate not_331 has open pins: in=not_326_out, out=open
  // NOT_Gate not_332 is placed but not wired
  // NOT_Gate not_333 has open pins: in=not_328_out, out=open
  // NOT_Gate not_334 is placed but not wired
  // NOT_Gate not_335 has open pins: in=not_329_out, out=open
  // NOT_Gate not_336 is placed but not wired
  // NOT_Gate not_337 has open pins: in=open, out=not_337_out
  // NOT_Gate not_338 has open pins: in=open, out=not_338_out
  // NOT_Gate not_339 is placed but not wired
  // NOT_Gate not_340 has open pins: in=open, out=not_340_out
  // NOT_Gate not_341 has open pins: in=open, out=not_341_out
  not not_342 (not_342_out, not_337_out);
  not not_343 (not_343_out, not_338_out);
  // NOT_Gate not_344 has open pins: in=open, out=not_344_out
  // NOT_Gate not_345 is placed but not wired
  not not_346 (not_346_out, not_340_out);
  // NOT_Gate not_347 has open pins: in=not_341_out, out=open
  // NOT_Gate not_348 has open pins: in=not_342_out, out=open
  // NOT_Gate not_349 has open pins: in=not_343_out, out=open
  // NOT_Gate not_350 has open pins: in=not_344_out, out=open
  // NOT_Gate not_351 is placed but not wired
  // NOT_Gate not_352 has open pins: in=not_346_out, out=open
  // NOT_Gate not_353 has open pins: in=open, out=not_353_out
  // NOT_Gate not_354 is placed but not wired
  // NOT_Gate not_355 has open pins: in=open, out=not_355_out
  // NOT_Gate not_356 has open pins: in=open, out=not_356_out
  not not_357 (not_357_out, not_353_out);
  // NOT_Gate not_358 is placed but not wired
  // NOT_Gate not_359 has open pins: in=open, out=not_359_out
  not not_360 (not_360_out, not_355_out);
  not not_361 (not_361_out, not_356_out);
  // NOT_Gate not_362 is placed but not wired
  // NOT_Gate not_363 has open pins: in=not_357_out, out=open
  // NOT_Gate not_364 is placed but not wired
  // NOT_Gate not_365 has open pins: in=not_359_out, out=open
  // NOT_Gate not_366 has open pins: in=not_360_out, out=open
  // NOT_Gate not_367 has open pins: in=not_361_out, out=open
  // NOT_Gate not_368 is placed but not wired
  // NOT_Gate not_369 has open pins: in=open, out=not_369_out
  // NOT_Gate not_370 is placed but not wired
  // NOT_Gate not_371 is placed but not wired
  // NOT_Gate not_372 is placed but not wired
  // NOT_Gate not_373 is placed but not wired
  // NOT_Gate not_374 has open pins: in=not_369_out, out=open
  // NOT_Gate not_375 is placed but not wired
  // NOT_Gate not_376 is placed but not wired
  // NOT_Gate not_377 is placed but not wired
  // NOT_Gate not_378 is placed but not wired
  // NOT_Gate not_379 is placed but not wired
endmodule

module FunctDecoder (
  input  Funct0,
  input  Funct1,
  input  Funct2,
  input  Funct3,
  input  Funct4,
  input  Funct5,
  output ALU0,
  output ALU1,
  output ALU2,
  output ALU3,
  output IsJR,
  output IsShamt
);

  wire and_1_out, and_2_out, and_3_out, and_4_out, and_5_out, and_6_out, and_7_out, and_8_out, and_9_out,
       and_10_out, and_11_out, and_12_out, and_13_out, and_14_out, and_15_out, and_16_out, and_17_out,
       and_19_out, and_20_out, and_21_out, not_1_out, not_2_out, not_3_out, not_4_out, not_5_out, not_6_out,
       not_7_out, not_8_out, not_9_out, not_10_out, not_11_out, not_12_out, not_13_out, not_14_out,
       not_15_out, not_16_out, not_17_out, not_18_out, not_19_out, not_20_out, not_21_out, not_22_out,
       not_23_out, not_24_out, not_25_out, not_26_out, not_27_out, not_28_out, not_29_out, not_30_out,
       not_31_out, not_32_out, not_33_out, not_34_out, not_35_out, not_36_out, not_37_out, not_38_out,
       not_39_out, not_40_out, not_41_out, not_42_out, not_43_out, not_44_out, not_45_out, not_46_out,
       not_47_out, not_48_out, not_49_out, not_50_out, not_51_out, not_52_out, not_53_out, not_54_out,
       not_55_out, not_56_out, not_57_out, not_58_out, not_59_out, not_60_out, not_61_out, not_62_out,
       not_63_out, not_64_out, not_65_out, not_66_out, not_67_out, not_68_out, not_69_out, not_70_out,
       not_71_out, not_72_out, not_73_out, not_74_out, not_75_out, not_76_out, not_77_out;

  not not_1 (not_1_out, Funct1);
  not not_2 (not_2_out, Funct2);
  not not_3 (not_3_out, Funct4);
  and and_1 (and_1_out, Funct0, not_1_out, not_2_out, Funct3, not_3_out, Funct5);
  not not_4 (not_4_out, Funct1);
  not not_5 (not_5_out, Funct2);
  and and_2 (and_2_out, Funct0, not_4_out, not_5_out, Funct3, Funct4, Funct5);
  or or_1 (ALU0, and_1_out, and_2_out, and_3_out, and_4_out);
  not not_6 (not_6_out, Funct1);
  not not_7 (not_7_out, Funct3);
  not not_8 (not_8_out, Funct5);
  and and_3 (and_3_out, Funct0, not_6_out, Funct2, not_7_out, Funct4, not_8_out);
  not not_9 (not_9_out, Funct1);
  and and_4 (and_4_out, Funct0, not_9_out, Funct2, not_10_out, Funct4, Funct5);
  not not_10 (not_10_out, Funct3);
  not not_11 (not_11_out, Funct1);
  not not_12 (not_12_out, Funct2);
  not not_13 (not_13_out, Funct3);
  not not_14 (not_14_out, Funct4);
  and and_5 (and_5_out, Funct0, not_11_out, not_12_out, not_13_out, not_14_out);
  not not_15 (not_15_out, Funct1);
  not not_16 (not_16_out, Funct2);
  and and_6 (and_6_out, Funct0, not_15_out, not_16_out, not_17_out, not_18_out);
  not not_17 (not_17_out, Funct3);
  not not_18 (not_18_out, Funct5);
  or or_2 (ALU1, and_5_out, and_6_out, and_7_out, and_8_out);
  not not_19 (not_19_out, Funct4);
  not not_20 (not_20_out, Funct5);
  not not_21 (not_21_out, Funct1);
  not not_22 (not_22_out, Funct2);
  and and_7 (and_7_out, Funct0, not_21_out, not_22_out, not_19_out, not_20_out);
  not not_23 (not_23_out, Funct1);
  and and_8 (and_8_out, Funct0, not_23_out, Funct2, not_24_out, Funct4, Funct5);
  not not_24 (not_24_out, Funct3);
  not not_25 (not_25_out, Funct1);
  not not_26 (not_26_out, Funct2);
  not not_27 (not_27_out, Funct3);
  not not_28 (not_28_out, Funct5);
  and and_9 (and_9_out, Funct0, not_25_out, not_26_out, not_27_out, Funct4, not_28_out);
  not not_29 (not_29_out, Funct1);
  not not_30 (not_30_out, Funct2);
  and and_10 (and_10_out, Funct0, not_29_out, not_30_out, Funct3, not_31_out, not_32_out);
  not not_31 (not_31_out, Funct4);
  not not_32 (not_32_out, Funct5);
  not not_33 (not_33_out, Funct0);
  not not_34 (not_34_out, Funct1);
  not not_35 (not_35_out, Funct2);
  not not_36 (not_36_out, Funct3);
  not not_37 (not_37_out, Funct5);
  and and_11 (and_11_out, not_33_out, not_34_out, not_35_out, not_36_out, Funct4, not_37_out);
  or or_3 (ALU2, and_9_out, and_10_out, and_11_out, and_12_out, and_13_out);
  not not_38 (not_38_out, Funct1);
  not not_39 (not_39_out, Funct2);
  and and_12 (and_12_out, Funct0, not_38_out, not_39_out, Funct3, Funct4, Funct5);
  not not_40 (not_40_out, Funct1);
  not not_41 (not_41_out, Funct3);
  not not_42 (not_42_out, Funct5);
  and and_13 (and_13_out, Funct0, not_40_out, Funct2, not_41_out, Funct4, not_42_out);
  not not_43 (not_43_out, Funct0);
  not not_44 (not_44_out, Funct1);
  not not_45 (not_45_out, Funct2);
  and and_14 (and_14_out, not_43_out, not_44_out, not_45_out, not_46_out, Funct4, Funct5);
  not not_46 (not_46_out, Funct3);
  not not_47 (not_47_out, Funct1);
  not not_48 (not_48_out, Funct2);
  not not_49 (not_49_out, Funct3);
  not not_50 (not_50_out, Funct4);
  and and_15 (and_15_out, Funct0, not_47_out, not_48_out, not_49_out, not_50_out);
  not not_51 (not_51_out, Funct1);
  not not_52 (not_52_out, Funct2);
  and and_16 (and_16_out, Funct0, not_51_out, not_52_out, not_53_out, not_54_out);
  or or_4 (ALU3, and_14_out, and_15_out, and_16_out, and_17_out);
  not not_53 (not_53_out, Funct4);
  not not_54 (not_54_out, Funct5);
  not not_55 (not_55_out, Funct1);
  not not_56 (not_56_out, Funct3);
  not not_57 (not_57_out, Funct5);
  and and_17 (and_17_out, Funct0, not_55_out, Funct2, not_56_out, Funct4, not_57_out);
  not not_58 (not_58_out, Funct0);
  not not_59 (not_59_out, Funct1);
  and and_18 (IsJR, not_58_out, not_59_out, Funct2, not_60_out, not_61_out, not_62_out);
  not not_60 (not_60_out, Funct3);
  not not_61 (not_61_out, Funct4);
  not not_62 (not_62_out, Funct5);
  not not_63 (not_63_out, Funct0);
  not not_64 (not_64_out, Funct1);
  not not_65 (not_65_out, Funct2);
  not not_66 (not_66_out, Funct3);
  and and_19 (and_19_out, not_63_out, not_64_out, not_65_out, not_66_out, Funct4, Funct5);
  not not_67 (not_67_out, Funct0);
  not not_68 (not_68_out, Funct1);
  not not_69 (not_69_out, Funct2);
  and and_20 (and_20_out, not_67_out, not_68_out, not_69_out, not_70_out, Funct4, not_71_out);
  or or_5 (IsShamt, and_19_out, and_20_out, and_21_out);
  not not_70 (not_70_out, Funct3);
  not not_71 (not_71_out, Funct5);
  not not_72 (not_72_out, Funct0);
  not not_73 (not_73_out, Funct1);
  not not_74 (not_74_out, Funct2);
  not not_75 (not_75_out, Funct3);
  not not_76 (not_76_out, Funct4);
  not not_77 (not_77_out, Funct5);
  and and_21 (and_21_out, not_72_out, not_73_out, not_74_out, not_75_out, not_76_out, not_77_out);
endmodule

module ALUDecoder (
  input  op0,
  input  op1,
  input  op2,
  input  op3,
  input  op4,
  input  op5,
  output ALUop0,
  output ALUop1,
  output ALUop2,
  output ALUop3
);

  wire and_1_out, and_2_out, and_3_out, and_4_out, and_5_out, and_6_out, and_7_out, and_8_out, and_9_out,
       and_10_out, and_11_out, and_12_out, and_13_out, and_14_out, and_15_out, and_16_out, and_17_out,
       and_18_out, and_19_out, and_20_out, and_21_out, and_22_out, and_23_out, and_24_out, and_25_out,
       and_26_out, and_27_out, and_28_out, and_29_out, not_1_out, not_2_out, not_3_out, not_4_out, not_5_out,
       not_6_out, not_7_out, not_8_out, not_9_out, not_10_out, not_11_out, not_12_out, not_13_out,
       not_14_out, not_15_out, not_16_out, not_17_out, not_18_out, not_19_out, not_20_out, not_21_out,
       not_22_out, not_23_out, not_24_out, not_25_out, not_26_out, not_27_out, not_28_out, not_29_out,
       not_30_out, not_31_out, not_32_out, not_33_out, not_34_out, not_35_out, not_36_out, not_37_out,
       not_38_out, not_39_out, not_40_out, not_41_out, not_42_out, not_43_out, not_44_out, not_45_out,
       not_46_out, not_47_out, not_48_out, not_49_out, not_50_out, not_51_out, not_52_out, not_53_out,
       not_54_out, not_55_out, not_56_out, not_57_out, not_58_out, not_59_out, not_60_out, not_61_out,
       not_62_out, not_63_out, not_64_out, not_65_out, not_66_out, not_67_out, not_68_out, not_69_out,
       not_70_out, not_71_out, not_72_out, not_73_out, not_74_out, not_75_out, not_76_out, not_77_out,
       not_78_out, not_79_out, not_80_out, not_81_out, not_82_out, not_83_out, not_84_out, not_85_out,
       not_86_out, not_87_out, not_88_out, not_89_out, not_90_out, not_91_out, not_92_out, not_93_out,
       not_94_out, not_95_out, not_96_out, not_97_out, not_98_out, not_99_out, not_100_out, not_101_out,
       not_102_out, not_103_out, not_104_out, not_105_out, not_106_out, not_107_out, not_108_out,
       not_109_out, not_110_out, not_111_out, not_112_out, not_113_out, not_114_out, not_115_out,
       not_116_out, not_117_out, not_118_out, not_119_out, not_120_out, not_121_out, not_122_out, not_123_out;

  not not_1 (not_1_out, op0);
  not not_2 (not_2_out, op1);
  not not_3 (not_3_out, op4);
  and and_1 (and_1_out, not_1_out, not_2_out, op2, op3, not_3_out, op5);
  or or_1 (ALUop0, and_1_out, and_2_out);
  not not_4 (not_4_out, op0);
  not not_5 (not_5_out, op1);
  not not_6 (not_6_out, op3);
  and and_2 (and_2_out, not_4_out, not_5_out, op2, not_6_out, op4, not_7_out);
  not not_7 (not_7_out, op5);
  not not_8 (not_8_out, op0);
  not not_9 (not_9_out, op1);
  not not_10 (not_10_out, op2);
  not not_11 (not_11_out, op3);
  not not_12 (not_12_out, op4);
  not not_13 (not_13_out, op5);
  and and_3 (and_3_out, not_8_out, not_9_out, not_10_out, not_11_out, not_12_out, not_13_out);
  not not_14 (not_14_out, op0);
  not not_15 (not_15_out, op1);
  not not_16 (not_16_out, op3);
  not not_17 (not_17_out, op4);
  and and_4 (and_4_out, not_14_out, not_15_out, op2, not_16_out, not_17_out, not_19_out);
  not not_18 (not_18_out, op1);
  not not_19 (not_19_out, op5);
  not not_20 (not_20_out, op2);
  not not_21 (not_21_out, op3);
  and and_5 (and_5_out, op0, not_18_out, not_20_out, not_21_out, op4, op5);
  not not_22 (not_22_out, op1);
  not not_23 (not_23_out, op3);
  and and_6 (and_6_out, op0, not_22_out, op2, not_23_out, op4, op5);
  not not_24 (not_24_out, op0);
  not not_25 (not_25_out, op1);
  not not_26 (not_26_out, op2);
  not not_27 (not_27_out, op4);
  and and_7 (and_7_out, not_24_out, not_25_out, not_26_out, op3, not_27_out, op5);
  not not_28 (not_28_out, op0);
  not not_29 (not_29_out, op1);
  not not_30 (not_30_out, op2);
  not not_31 (not_31_out, op4);
  and and_8 (and_8_out, not_28_out, not_29_out, not_30_out, op3, not_31_out, not_32_out);
  or or_2 (ALUop1, and_3_out, and_4_out, and_5_out, and_6_out, and_7_out, and_8_out, and_9_out, and_10_out, and_11_out, and_12_out, and_13_out, and_14_out);
  not not_32 (not_32_out, op5);
  not not_33 (not_33_out, op0);
  not not_34 (not_34_out, op1);
  not not_35 (not_35_out, op4);
  not not_36 (not_36_out, op5);
  and and_9 (and_9_out, not_33_out, not_34_out, op2, op3, not_35_out, not_36_out);
  not not_37 (not_37_out, op0);
  not not_38 (not_38_out, op1);
  not not_39 (not_39_out, op3);
  not not_40 (not_40_out, op4);
  and and_10 (and_10_out, not_37_out, not_38_out, op2, not_39_out, not_40_out, op5);
  not not_41 (not_41_out, op0);
  not not_42 (not_42_out, op1);
  not not_43 (not_43_out, op3);
  not not_44 (not_44_out, op4);
  not not_45 (not_45_out, op5);
  and and_11 (and_11_out, not_41_out, not_42_out, op2, not_43_out, not_44_out, not_45_out);
  not not_46 (not_46_out, op0);
  not not_47 (not_47_out, op1);
  not not_48 (not_48_out, op2);
  not not_49 (not_49_out, op3);
  and and_12 (and_12_out, not_46_out, not_47_out, not_48_out, not_49_out, op4, not_50_out);
  not not_50 (not_50_out, op5);
  not not_51 (not_51_out, op0);
  not not_52 (not_52_out, op1);
  not not_53 (not_53_out, op2);
  not not_54 (not_54_out, op3);
  and and_13 (and_13_out, not_51_out, not_52_out, not_53_out, not_54_out, op4, op5);
  not not_55 (not_55_out, op0);
  not not_56 (not_56_out, op2);
  not not_57 (not_57_out, op3);
  not not_58 (not_58_out, op4);
  and and_14 (and_14_out, not_55_out, op1, not_56_out, not_57_out, not_58_out, not_59_out);
  not not_59 (not_59_out, op5);
  not not_60 (not_60_out, op0);
  not not_61 (not_61_out, op1);
  not not_62 (not_62_out, op4);
  not not_63 (not_63_out, op5);
  and and_15 (and_15_out, not_60_out, not_61_out, op2, op3, not_62_out, not_63_out);
  not not_64 (not_64_out, op0);
  not not_65 (not_65_out, op1);
  not not_66 (not_66_out, op3);
  and and_16 (and_16_out, not_64_out, not_65_out, op2, not_66_out, op4, not_67_out);
  or or_3 (ALUop2, and_15_out, and_16_out);
  not not_67 (not_67_out, op5);
  not not_68 (not_68_out, op0);
  not not_69 (not_69_out, op1);
  not not_70 (not_70_out, op2);
  not not_71 (not_71_out, op3);
  not not_72 (not_72_out, op4);
  not not_73 (not_73_out, op5);
  and and_17 (and_17_out, not_68_out, not_69_out, not_70_out, not_71_out, not_72_out, not_73_out);
  not not_74 (not_74_out, op0);
  not not_75 (not_75_out, op1);
  not not_76 (not_76_out, op3);
  not not_77 (not_77_out, op4);
  and and_18 (and_18_out, not_74_out, not_75_out, op2, not_76_out, not_77_out, not_78_out);
  not not_78 (not_78_out, op5);
  not not_79 (not_79_out, op1);
  not not_80 (not_80_out, op2);
  not not_81 (not_81_out, op3);
  and and_19 (and_19_out, op0, not_79_out, not_80_out, not_81_out, op4, op5);
  not not_82 (not_82_out, op1);
  not not_83 (not_83_out, op3);
  and and_20 (and_20_out, op0, not_82_out, op2, not_83_out, op4, op5);
  not not_84 (not_84_out, op0);
  not not_85 (not_85_out, op1);
  not not_86 (not_86_out, op2);
  not not_87 (not_87_out, op4);
  and and_21 (and_21_out, not_84_out, not_85_out, not_86_out, op3, not_87_out, op5);
  not not_88 (not_88_out, op0);
  not not_89 (not_89_out, op1);
  not not_90 (not_90_out, op2);
  not not_91 (not_91_out, op4);
  and and_22 (and_22_out, not_88_out, not_89_out, not_90_out, op3, not_91_out, not_92_out);
  not not_92 (not_92_out, op5);
  not not_93 (not_93_out, op0);
  not not_94 (not_94_out, op1);
  not not_95 (not_95_out, op4);
  not not_96 (not_96_out, op5);
  and and_23 (and_23_out, not_93_out, not_94_out, op2, op3, not_95_out, not_96_out);
  or or_4 (ALUop3, and_17_out, and_18_out, and_19_out, and_20_out, and_21_out, and_22_out, and_23_out, and_24_out, and_25_out, and_26_out, and_27_out, and_28_out, and_29_out);
  not not_97 (not_97_out, op0);
  not not_98 (not_98_out, op1);
  not not_99 (not_99_out, op3);
  not not_100 (not_100_out, op5);
  and and_24 (and_24_out, not_97_out, not_98_out, op2, not_99_out, op4, not_100_out);
  not not_101 (not_101_out, op0);
  not not_102 (not_102_out, op1);
  not not_103 (not_103_out, op3);
  not not_104 (not_104_out, op4);
  and and_25 (and_25_out, not_101_out, not_102_out, op2, not_103_out, not_104_out, op5);
  not not_105 (not_105_out, op0);
  not not_106 (not_106_out, op1);
  not not_107 (not_107_out, op3);
  not not_108 (not_108_out, op4);
  not not_109 (not_109_out, op5);
  and and_26 (and_26_out, not_105_out, not_106_out, op2, not_107_out, not_108_out, not_109_out);
  not not_110 (not_110_out, op0);
  not not_111 (not_111_out, op1);
  not not_112 (not_112_out, op2);
  not not_113 (not_113_out, op3);
  not not_114 (not_114_out, op5);
  and and_27 (and_27_out, not_110_out, not_111_out, not_112_out, not_113_out, op4, not_114_out);
  not not_115 (not_115_out, op0);
  not not_116 (not_116_out, op1);
  not not_117 (not_117_out, op2);
  not not_118 (not_118_out, op3);
  and and_28 (and_28_out, not_115_out, not_116_out, not_117_out, not_118_out, op4, op5);
  not not_119 (not_119_out, op0);
  not not_120 (not_120_out, op2);
  not not_121 (not_121_out, op3);
  not not_122 (not_122_out, op4);
  not not_123 (not_123_out, op5);
  and and_29 (and_29_out, not_119_out, op1, not_120_out, not_121_out, not_122_out, not_123_out);
endmodule

module pALU (
  input  [31:0] X,
  input  [31:0] Y,
  input  [3:0] ALUOp,
  output SignedOverflow,
  output UnsignedOverflow,
  output [31:0] Result1,
  output [31:0] Result2,
  output isEqual
);

  wire comparator_1_lt, comparator_2_lt;
  wire [1:0] somadorcomoverflowdetection_1_out_4, subtratorcomoverflowdetection_1_out_4;
  wire [31:0] and_1_out, bit_extender_1_out, bit_extender_2_out, divider_1_out, divider_1_rem,
       multiplier_1_cout, multiplier_1_out, not_1_out, or_1_out, or_2_out, shifter_1_out, shifter_2_out,
       shifter_3_out, somadorcomoverflowdetection_1_opresult, subtratorcomoverflowdetection_1_resultado,
       xor_1_out;

  Shifter #(.width(32)) shifter_1 (.in(X), .\dist (Y[4:0]), .out(shifter_1_out));
  Shifter #(.shift("ar"), .width(32)) shifter_2 (.in(X), .\dist (Y[4:0]), .out(shifter_2_out));
  Shifter #(.shift("lr"), .width(32)) shifter_3 (.in(X), .\dist (Y[4:0]), .out(shifter_3_out));
  Multiplier #(.width(32)) multiplier_1 (.a(X), .b(Y), .out(multiplier_1_out), .cout(multiplier_1_cout));  // open: cin
  Divider #(.width(32)) divider_1 (.a(X), .b(Y), .out(divider_1_out), .rem(divider_1_rem));  // open: upper
  assign and_1_out = X & Y;  // AND_Gate and_1, 32 bits wide
  assign or_1_out = X | Y;  // OR_Gate or_1, 32 bits wide
  assign xor_1_out = X ^ Y;  // XOR_Gate xor_1, 32 bits wide
  assign or_2_out = X | Y;  // OR_Gate or_2, 32 bits wide
  Comparator #(.width(32)) comparator_1 (.a(X), .b(Y), .lt(comparator_1_lt));  // open: gt, eq
  Comparator #(.width(32)) comparator_2 (.a(X), .b(Y), .eq(isEqual), .lt(comparator_2_lt));  // open: gt
  assign not_1_out = ~or_2_out;  // NOT_Gate not_1, 32 bits wide
  Multiplexer #(.disabled("Z"), .select(4), .width(2)) multiplexer_1 (
    .in0(2'b00), .in1(2'b00), .in2(2'b00), .in3(2'b00), .in4(2'b00),
    .in5(somadorcomoverflowdetection_1_out_4), .in6(subtratorcomoverflowdetection_1_out_4), .in7(2'b00),
    .in8(2'b00), .in9(2'b00), .in10(2'b00), .in11(2'b00), .in12(2'b00), .in13(2'b00), .in14(2'b00),
    .in15(2'b00), .out({UnsignedOverflow, SignedOverflow}), .sel(ALUOp));
  SomadorComOverflowDetection somadorcomoverflowdetection_1 (
    .X(X), .Y(Y), .opResult(somadorcomoverflowdetection_1_opresult),
    .out_6(somadorcomoverflowdetection_1_out_4[1]), .out_4(somadorcomoverflowdetection_1_out_4[0]));  // open: in_3
  SubtratorComOverflowDetection subtratorcomoverflowdetection_1 (
    .X(X), .Y(Y), .Resultado(subtratorcomoverflowdetection_1_resultado),
    .out_6(subtratorcomoverflowdetection_1_out_4[1]), .out_4(subtratorcomoverflowdetection_1_out_4[0]));  // open: in_3
  Multiplexer #(.disabled("Z"), .select(4), .width(32)) multiplexer_2 (
    .in0({32{1'b0}}), .in1({32{1'b0}}), .in2({32{1'b0}}), .in3(multiplier_1_cout), .in4(divider_1_rem),
    .in5({32{1'b0}}), .in6({32{1'b0}}), .in7({32{1'b0}}), .in8({32{1'b0}}), .in9({32{1'b0}}),
    .in10({32{1'b0}}), .in11({32{1'b0}}), .in12({32{1'b0}}), .in13({32{1'b0}}), .in14({32{1'b0}}),
    .in15({32{1'b0}}), .out(Result2), .sel(ALUOp));
  assign bit_extender_1_out = {{31{1'b0}}, comparator_1_lt};  // Bit_Extender bit_extender_1
  assign bit_extender_2_out = {{31{1'b0}}, comparator_2_lt};  // Bit_Extender bit_extender_2
  Multiplexer #(.select(4), .width(32)) multiplexer_3 (
    .in0(shifter_1_out), .in1(shifter_2_out), .in2(shifter_3_out), .in3(multiplier_1_out),
    .in4(divider_1_out), .in5(somadorcomoverflowdetection_1_opresult),
    .in6(subtratorcomoverflowdetection_1_resultado), .in7(and_1_out), .in8(or_1_out), .in9(xor_1_out),
    .in10(not_1_out), .in11(bit_extender_1_out), .in12(bit_extender_2_out), .in13({32{1'b0}}),
    .in14({32{1'b0}}), .in15({32{1'b0}}), .out(Result1), .sel(ALUOp));

  // Other names for the same wires on the sheet: SigOverFlow = SignedOverflow; UsgOverflow = UnsignedOverflow;
  //   S[3:0] = ALUOp
endmodule

module SomadorComOverflowDetection (
  input  [31:0] X,
  input  [31:0] Y,
  input  in_3,
  output out_4,
  output [31:0] opResult,
  output out_6
);

  wire adder_1_cout;

  Adder #(.width(31)) adder_1 (.a(X[30:0]), .b(Y[30:0]), .out(opResult[30:0]), .cin(in_3), .cout(adder_1_cout));
  Adder #(.width(1)) adder_2 (.a(X[31]), .b(Y[31]), .out(opResult[31]), .cin(adder_1_cout), .cout(out_4));
  xor xor_1 (out_6, adder_1_cout, out_4);

  // Other names for the same wires on the sheet: cin = in_3; SignedOverflowsum = out_4; sumResult[31:0] = opResult;
  //   UnsignedOverflowsum = out_6
endmodule

module SubtratorComOverflowDetection (
  input  [31:0] X,
  input  [31:0] Y,
  input  in_3,
  output out_4,
  output [31:0] Resultado,
  output out_6
);

  wire subtractor_1_bout;

  Subtractor #(.width(31)) subtractor_1 (
    .a(X[30:0]), .b(Y[30:0]), .out(Resultado[30:0]), .bin(in_3), .bout(subtractor_1_bout));
  Subtractor #(.width(1)) subtractor_2 (
    .a(X[31]), .b(Y[31]), .out(Resultado[31]), .bin(subtractor_1_bout), .bout(out_6));
  xor xor_1 (out_4, subtractor_1_bout, out_6);

  // Other names for the same wires on the sheet: cin = in_3; Resultsub[31:0] = Resultado; SignedOverflowsub = out_6;
  //   UnsignedOverflowsub = out_4
endmodule

module HazardControl (
  input  clk_hazard,
  input  isToBranchOrJump_hazard,
  input  readRs_hazard,
  input  readRt_hazard,
  input  RegWriteMEM_hazard,
  input  [4:0] RT_hazard,
  input  [4:0] RS_hazard,
  input  [4:0] WriteRegMEM_hazard,
  input  RegWriteEX_hazard,
  input  [4:0] WirteRegEX_hazard,
  output FlushIF_hazard,
  output FlushID_hazard,
  output StallIF_hazard,
  output StallID_hazard
);

  wire and_1_out, and_2_out, and_3_out, and_4_out, and_5_out, and_6_out, and_7_out, and_8_out,
       comparator_1_eq, comparator_2_eq, comparator_3_eq, comparator_4_eq, comparator_5_eq, comparator_6_eq,
       d_ff_1_q, d_ff_2_q, not_1_out, not_2_out, not_3_out, or_1_out, or_2_out;

  Comparator #(.width(5)) comparator_1 (.a({5{1'b0}}), .b(WriteRegMEM_hazard), .eq(comparator_1_eq));  // open: gt, lt
  Comparator #(.width(5)) comparator_2 (.a(WriteRegMEM_hazard), .b(RT_hazard), .eq(comparator_2_eq));  // open: gt, lt
  Comparator #(.width(5)) comparator_3 (.a(WriteRegMEM_hazard), .b(RS_hazard), .eq(comparator_3_eq));  // open: gt, lt
  Comparator #(.width(5)) comparator_4 (.a({5{1'b0}}), .b(WirteRegEX_hazard), .eq(comparator_4_eq));  // open: gt, lt
  Comparator #(.width(5)) comparator_5 (.a(WirteRegEX_hazard), .b(RT_hazard), .eq(comparator_5_eq));  // open: gt, lt
  Comparator #(.width(5)) comparator_6 (.a(WirteRegEX_hazard), .b(RS_hazard), .eq(comparator_6_eq));  // open: gt, lt
  not not_1 (not_1_out, comparator_1_eq);
  not not_2 (not_2_out, comparator_4_eq);
  and and_1 (and_1_out, comparator_2_eq, readRt_hazard);
  and and_2 (and_2_out, comparator_3_eq, readRs_hazard);
  and and_3 (and_3_out, comparator_5_eq, readRt_hazard);
  and and_4 (and_4_out, comparator_6_eq, readRs_hazard);
  or or_1 (or_1_out, and_1_out, and_2_out);
  or or_2 (or_2_out, and_3_out, and_4_out);
  and and_5 (and_5_out, not_1_out, or_1_out);
  and and_6 (and_6_out, not_2_out, or_2_out);
  and and_7 (and_7_out, RegWriteMEM_hazard, and_5_out);
  and and_8 (and_8_out, RegWriteEX_hazard, and_6_out);
  or or_3 (StallID_hazard, and_7_out, and_8_out);
  D_Flip_Flop #(.trigger("falling")) d_ff_1 (
    .D(isToBranchOrJump_hazard), .clk(clk_hazard), .Q(d_ff_1_q));  // open: Qn, preset, reset
  not not_3 (not_3_out, clk_hazard);
  D_Flip_Flop #(.trigger("falling")) d_ff_2 (
    .D(StallID_hazard), .clk(clk_hazard), .Q(d_ff_2_q));  // open: Qn, preset, reset
  and and_9 (FlushIF_hazard, not_3_out, d_ff_1_q);
  and and_10 (FlushID_hazard, clk_hazard, d_ff_2_q);

  assign StallIF_hazard = StallID_hazard;

  // Other names for the same wires on the sheet: Tclk_hazard = clk_hazard

  // Notes on the sheet:
  //   _______
endmodule

module registerFileP (
  input  [4:0] R1In,
  input  [4:0] R2In,
  input  [4:0] RwIn,
  input  [31:0] inData,
  input  WriteEnable,
  input  clk,
  output [31:0] R1Out,
  output [31:0] a0Out,
  output [31:0] R2Out,
  output [31:0] v0Out
);

  wire demultiplexer_1_out0, demultiplexer_1_out1, demultiplexer_1_out2, demultiplexer_1_out3,
       demultiplexer_2_out0, demultiplexer_2_out1, demultiplexer_2_out2, demultiplexer_2_out3,
       demultiplexer_2_out4, demultiplexer_2_out5, demultiplexer_2_out6, demultiplexer_2_out7,
       demultiplexer_3_out0, demultiplexer_3_out1, demultiplexer_3_out2, demultiplexer_3_out3,
       demultiplexer_3_out4, demultiplexer_3_out5, demultiplexer_3_out6, demultiplexer_3_out7,
       demultiplexer_4_out0, demultiplexer_4_out1, demultiplexer_4_out2, demultiplexer_4_out3,
       demultiplexer_4_out4, demultiplexer_4_out5, demultiplexer_4_out6, demultiplexer_4_out7,
       demultiplexer_5_out0, demultiplexer_5_out1, demultiplexer_5_out2, demultiplexer_5_out3,
       demultiplexer_5_out4, demultiplexer_5_out5, demultiplexer_5_out6, demultiplexer_5_out7;
  wire [31:0] a1_5_q, a2_6_q, a3_7_q, at_1_q, fp_30_q, gp_28_q, k0_26_q, k1_27_q, s3_19_q, s4_20_q, s5_21_q,
       s6_22_q, s7_23_q, sp_29_q, t0_8_q, t1_9_q, t2_10_q, t3_11_q, t4_12_q, t5_15_q, t6_14_q, t7_15_q,
       t8_24_q, t9_25_q, Tra, Ts0, Ts1, Ts2, v1_3_q, zero_0_q;

  Demultiplexer #(.enable("true"), .select(2)) demultiplexer_1 (
    .out0(demultiplexer_1_out0), .out1(demultiplexer_1_out1), .out2(demultiplexer_1_out2),
    .out3(demultiplexer_1_out3), .in(1'b1), .sel(RwIn[4:3]), .en(WriteEnable));
  Demultiplexer #(.enable("true"), .select(3)) demultiplexer_2 (
    .out0(demultiplexer_2_out0), .out1(demultiplexer_2_out1), .out2(demultiplexer_2_out2),
    .out3(demultiplexer_2_out3), .out4(demultiplexer_2_out4), .out5(demultiplexer_2_out5),
    .out6(demultiplexer_2_out6), .out7(demultiplexer_2_out7), .in(1'b1), .sel(RwIn[2:0]),
    .en(demultiplexer_1_out0));
  Demultiplexer #(.enable("true"), .select(3)) demultiplexer_3 (
    .out0(demultiplexer_3_out0), .out1(demultiplexer_3_out1), .out2(demultiplexer_3_out2),
    .out3(demultiplexer_3_out3), .out4(demultiplexer_3_out4), .out5(demultiplexer_3_out5),
    .out6(demultiplexer_3_out6), .out7(demultiplexer_3_out7), .in(1'b1), .sel(RwIn[2:0]),
    .en(demultiplexer_1_out1));
  Demultiplexer #(.enable("true"), .select(3)) demultiplexer_4 (
    .out0(demultiplexer_4_out0), .out1(demultiplexer_4_out1), .out2(demultiplexer_4_out2),
    .out3(demultiplexer_4_out3), .out4(demultiplexer_4_out4), .out5(demultiplexer_4_out5),
    .out6(demultiplexer_4_out6), .out7(demultiplexer_4_out7), .in(1'b1), .sel(RwIn[2:0]),
    .en(demultiplexer_1_out2));
  Demultiplexer #(.enable("true"), .select(3)) demultiplexer_5 (
    .out0(demultiplexer_5_out0), .out1(demultiplexer_5_out1), .out2(demultiplexer_5_out2),
    .out3(demultiplexer_5_out3), .out4(demultiplexer_5_out4), .out5(demultiplexer_5_out5),
    .out6(demultiplexer_5_out6), .out7(demultiplexer_5_out7), .in(1'b1), .sel(RwIn[2:0]),
    .en(demultiplexer_1_out3));
  Register #(.width(32)) zero_0 (.D(inData), .en(demultiplexer_2_out0), .Q(zero_0_q));  // open: clk, clr
  Register #(.width(32)) t0_8 (.D(inData), .en(demultiplexer_3_out0), .clk(clk), .Q(t0_8_q));  // open: clr
  Register #(.width(32)) s0_16 (.D(inData), .en(demultiplexer_4_out0), .clk(clk), .Q(Ts0));  // open: clr
  Register #(.width(32)) t8_24 (.D(inData), .en(demultiplexer_5_out0), .clk(clk), .Q(t8_24_q));  // open: clr
  Register #(.width(32)) at_1 (.D(inData), .en(demultiplexer_2_out1), .clk(clk), .Q(at_1_q));  // open: clr
  Register #(.width(32)) t1_9 (.D(inData), .en(demultiplexer_3_out1), .clk(clk), .Q(t1_9_q));  // open: clr
  Register #(.width(32)) s1_17 (.D(inData), .en(demultiplexer_4_out1), .clk(clk), .Q(Ts1));  // open: clr
  Register #(.width(32)) t9_25 (.D(inData), .en(demultiplexer_5_out1), .clk(clk), .Q(t9_25_q));  // open: clr
  Register #(.width(32)) v0_2 (.D(inData), .en(demultiplexer_2_out2), .clk(clk), .Q(v0Out));  // open: clr
  Register #(.width(32)) t2_10 (.D(inData), .en(demultiplexer_3_out2), .clk(clk), .Q(t2_10_q));  // open: clr
  Register #(.width(32)) s2_18 (.D(inData), .en(demultiplexer_4_out2), .clk(clk), .Q(Ts2));  // open: clr
  Register #(.width(32)) k0_26 (.D(inData), .en(demultiplexer_5_out2), .clk(clk), .Q(k0_26_q));  // open: clr
  Register #(.width(32)) v1_3 (.D(inData), .en(demultiplexer_2_out3), .clk(clk), .Q(v1_3_q));  // open: clr
  Register #(.width(32)) t3_11 (.D(inData), .en(demultiplexer_3_out3), .clk(clk), .Q(t3_11_q));  // open: clr
  Register #(.width(32)) s3_19 (.D(inData), .en(demultiplexer_4_out3), .clk(clk), .Q(s3_19_q));  // open: clr
  Register #(.width(32)) k1_27 (.D(inData), .en(demultiplexer_5_out3), .clk(clk), .Q(k1_27_q));  // open: clr
  Register #(.width(32)) a0_4 (.D(inData), .en(demultiplexer_2_out4), .clk(clk), .Q(v0Out));  // open: clr
  Register #(.width(32)) t4_12 (.D(inData), .en(demultiplexer_3_out4), .clk(clk), .Q(t4_12_q));  // open: clr
  Register #(.width(32)) s4_20 (.D(inData), .en(demultiplexer_4_out4), .clk(clk), .Q(s4_20_q));  // open: clr
  Register #(.width(32)) gp_28 (.D(inData), .en(demultiplexer_5_out4), .clk(clk), .Q(gp_28_q));  // open: clr
  Register #(.width(32)) a1_5 (.D(inData), .en(demultiplexer_2_out5), .clk(clk), .Q(a1_5_q));  // open: clr
  Register #(.width(32)) t5_15 (.D(inData), .en(demultiplexer_3_out5), .clk(clk), .Q(t5_15_q));  // open: clr
  Register #(.width(32)) s5_21 (.D(inData), .en(demultiplexer_4_out5), .clk(clk), .Q(s5_21_q));  // open: clr
  Register #(.width(32)) sp_29 (.D(inData), .en(demultiplexer_5_out5), .clk(clk), .Q(sp_29_q));  // open: clr
  Register #(.width(32)) a2_6 (.D(inData), .en(demultiplexer_2_out6), .clk(clk), .Q(a2_6_q));  // open: clr
  Register #(.width(32)) t6_14 (.D(inData), .en(demultiplexer_3_out6), .clk(clk), .Q(t6_14_q));  // open: clr
  Register #(.width(32)) s6_22 (.D(inData), .en(demultiplexer_4_out6), .clk(clk), .Q(s6_22_q));  // open: clr
  Register #(.width(32)) fp_30 (.D(inData), .en(demultiplexer_5_out6), .clk(clk), .Q(fp_30_q));  // open: clr
  Register #(.width(32)) a3_7 (.D(inData), .en(demultiplexer_2_out7), .clk(clk), .Q(a3_7_q));  // open: clr
  Register #(.width(32)) t7_15 (.D(inData), .en(demultiplexer_3_out7), .clk(clk), .Q(t7_15_q));  // open: clr
  Register #(.width(32)) s7_23 (.D(inData), .en(demultiplexer_4_out7), .clk(clk), .Q(s7_23_q));  // open: clr
  Register #(.width(32)) ra_31 (.D(inData), .en(demultiplexer_5_out7), .clk(clk), .Q(Tra));  // open: clr
  Multiplexer #(.disabled("Z"), .select(5), .width(32)) multiplexer_1 (
    .in0(zero_0_q), .in1(at_1_q), .in2(v0Out), .in3(v1_3_q), .in4(v0Out), .in5(a1_5_q), .in6(a2_6_q),
    .in7(a3_7_q), .in8(t0_8_q), .in9(t1_9_q), .in10(t2_10_q), .in11(t3_11_q), .in12(t4_12_q), .in13(t5_15_q),
    .in14(t6_14_q), .in15(t7_15_q), .in16(Ts0), .in17(Ts1), .in18(Ts2), .in19(s3_19_q), .in20(s4_20_q),
    .in21(s5_21_q), .in22(s6_22_q), .in23(s7_23_q), .in24(t8_24_q), .in25(t9_25_q), .in26(k0_26_q),
    .in27(k1_27_q), .in28(gp_28_q), .in29(sp_29_q), .in30(fp_30_q), .in31(Tra), .out(R1Out), .sel(R1In));
  Multiplexer #(.disabled("Z"), .select(5), .width(32)) multiplexer_2 (
    .in0(zero_0_q), .in1(at_1_q), .in2(v0Out), .in3(v1_3_q), .in4(v0Out), .in5(a1_5_q), .in6(a2_6_q),
    .in7(a3_7_q), .in8(t0_8_q), .in9(t1_9_q), .in10(t2_10_q), .in11(t3_11_q), .in12(t4_12_q), .in13(t5_15_q),
    .in14(t6_14_q), .in15(t7_15_q), .in16(Ts0), .in17(Ts1), .in18(Ts2), .in19(s3_19_q), .in20(s4_20_q),
    .in21(s5_21_q), .in22(s6_22_q), .in23(s7_23_q), .in24(t8_24_q), .in25(t9_25_q), .in26(k0_26_q),
    .in27(k1_27_q), .in28(gp_28_q), .in29(sp_29_q), .in30(fp_30_q), .in31(Tra), .out(R2Out), .sel(R2In));

  // Other names for the same wires on the sheet: Ta0[31:0] = a0Out; Tclk = clk; TinDado[31:0] = inData;
  //   TR1[4:0] = R1In; TR2[4:0] = R2In; Treg1[31:0] = R1Out; Treg2[31:0] = R2Out; TRw[4:0] = RwIn; Tv0[31:0] = v0Out;
  //   TWE = WriteEnable
endmodule

module FHazardUnit (
  input  IsToBranchOrJump,
  input  clk,
  input  ReadRs,
  input  ReadRt,
  input  RegWriteEX,
  input  RegWriteMEM,
  input  [4:0] RS,
  input  [4:0] RT,
  input  IsLW,
  input  [4:0] WriteRegEX,
  input  [4:0] WriteRegMEM,
  output FlushIF,
  output [1:0] RsOutput,
  output FlushID,
  output StallIF,
  output StallID,
  output [1:0] RtOutput
);

  wire d_ff_1_q, d_ff_2_q, detectordehazard_1_hazarddetectado, detectordehazard_2_hazarddetectado,
       detectordehazard_3_hazarddetectado, detectordehazard_4_hazarddetectado, not_1_out, or_1_out;
  wire [1:0] multiplexer_1_out, multiplexer_2_out;

  // Probe on RsOutput
  // Probe on RtOutput
  // Probe on StallID
  // Probe on StallID
  // Probe on FlushIF
  // Probe on FlushID
  DetectorDeHazard detectordehazard_1 (
    .lendoReg(ReadRs), .escrevendoReg(RegWriteMEM), .regEscrito(WriteRegMEM), .regAcessado(RS),
    .HazardDetectado(detectordehazard_1_hazarddetectado));
  DetectorDeHazard detectordehazard_2 (
    .lendoReg(ReadRs), .escrevendoReg(RegWriteEX), .regEscrito(WriteRegEX), .regAcessado(RS),
    .HazardDetectado(detectordehazard_2_hazarddetectado));
  DetectorDeHazard detectordehazard_3 (
    .lendoReg(ReadRt), .escrevendoReg(RegWriteMEM), .regEscrito(WriteRegMEM), .regAcessado(RT),
    .HazardDetectado(detectordehazard_3_hazarddetectado));
  DetectorDeHazard detectordehazard_4 (
    .lendoReg(ReadRt), .escrevendoReg(RegWriteEX), .regEscrito(WriteRegEX), .regAcessado(RT),
    .HazardDetectado(detectordehazard_4_hazarddetectado));
  Multiplexer #(.disabled("Z"), .width(2)) multiplexer_1 (
    .in0(2'b00), .in1(2'b10), .out(multiplexer_1_out), .sel(detectordehazard_1_hazarddetectado));
  Multiplexer #(.disabled("Z"), .width(2)) multiplexer_2 (
    .in0(2'b00), .in1(2'b10), .out(multiplexer_2_out), .sel(detectordehazard_3_hazarddetectado));
  Multiplexer #(.width(2)) multiplexer_3 (
    .in0(multiplexer_1_out), .in1(2'b01), .out(RsOutput), .sel(detectordehazard_2_hazarddetectado));
  Multiplexer #(.width(2)) multiplexer_4 (
    .in0(multiplexer_2_out), .in1(2'b01), .out(RtOutput), .sel(detectordehazard_4_hazarddetectado));
  or or_1 (or_1_out, detectordehazard_2_hazarddetectado, detectordehazard_4_hazarddetectado);
  and and_1 (StallID, IsLW, or_1_out);
  not not_1 (not_1_out, clk);
  D_Flip_Flop #(.trigger("falling")) d_ff_1 (.D(IsToBranchOrJump), .clk(clk), .Q(d_ff_1_q));  // open: Qn, preset, reset
  D_Flip_Flop #(.trigger("falling")) d_ff_2 (.D(StallID), .clk(clk), .Q(d_ff_2_q));  // open: Qn, preset, reset
  and and_2 (FlushIF, not_1_out, d_ff_1_q);
  and and_3 (FlushID, clk, d_ff_2_q);

  assign StallIF = StallID;

  // Other names for the same wires on the sheet: Tclk = clk; TFlushID = FlushID; TFlushIF = FlushIF; TReadRs = ReadRs;
  //   TReadRt = ReadRt; TReadWriteEX = RegWriteEX; TReadWriteMEM = RegWriteMEM; TRS[4:0] = RS;
  //   TRsOutput[1:0] = RsOutput; TRT[4:0] = RT; TRtOutput[1:0] = RtOutput; TStallID = StallID; TStallIF = StallID;
  //   TWriteRegEX[4:0] = WriteRegEX; TWriteRegMEM[4:0] = WriteRegMEM

  // Notes on the sheet:
  //   Rs Hazard in MEM
  //   Rs Hazard in EX
  //   Rt Hazard in MEM
  //   Rt Hazard in EX
  //   hasHazard
  //   aaaaaaaaaaaaaaaaaaaaaaaaaaaaaaaaaaaaaaaaaaaaaaaaaa
endmodule

module DetectorDeHazard (
  input  lendoReg,
  input  escrevendoReg,
  input  [4:0] regEscrito,
  input  [4:0] regAcessado,
  output HazardDetectado
);

  wire comparator_1_eq, comparator_2_eq, not_1_out;

  Comparator #(.width(5)) comparator_1 (.a({5{1'b0}}), .b(regEscrito), .eq(comparator_1_eq));  // open: gt, lt
  Comparator #(.width(5)) comparator_2 (.a(regEscrito), .b(regAcessado), .eq(comparator_2_eq));  // open: gt, lt
  not not_1 (not_1_out, comparator_1_eq);
  and and_1 (HazardDetectado, lendoReg, escrevendoReg, not_1_out, comparator_2_eq);
endmodule

module Contador (
  input  clkSignal,
  input  zerarContador,
  output [31:0] NumeroCiclos
);

  wire [31:0] adder_1_out;

  Register #(.width(32)) register_1 (
    .D(adder_1_out), .en(clkSignal), .clk(clkSignal), .Q(NumeroCiclos), .clr(zerarContador));
  Adder #(.width(32)) adder_1 (.a(NumeroCiclos), .b(32'h1), .out(adder_1_out));  // open: cin, cout
endmodule
module registerFilePMostradores (
  input  [4:0] R1in,
  input  [4:0] R2in,
  input  [4:0] Rw,
  input  [31:0] inDado,
  input  WE,
  input  clk,
  input  rst,
  output [31:0] R1out,
  output [31:0] a0out,
  output [31:0] R2out,
  output [31:0] v0out,
  output [31:0] SR0,
  output [31:0] SR8,
  output [31:0] SR16,
  output [31:0] SR24,
  output [31:0] SR1,
  output [31:0] SR9,
  output [31:0] SR17,
  output [31:0] SR25,
  output [31:0] SR2,
  output [31:0] SR10,
  output [31:0] SR18,
  output [31:0] SR26,
  output [31:0] SR3,
  output [31:0] SR11,
  output [31:0] SR19,
  output [31:0] SR27,
  output [31:0] SR4,
  output [31:0] SR12,
  output [31:0] SR20,
  output [31:0] SR28,
  output [31:0] SR5,
  output [31:0] SR13,
  output [31:0] SR21,
  output [31:0] SR29,
  output [31:0] SR6,
  output [31:0] SR14,
  output [31:0] SR22,
  output [31:0] SR30,
  output [31:0] SR7,
  output [31:0] SR15,
  output [31:0] SR23,
  output [31:0] SR31
);

  wire demultiplexer_1_out0, demultiplexer_1_out1, demultiplexer_1_out2, demultiplexer_1_out3,
       demultiplexer_2_out0, demultiplexer_2_out1, demultiplexer_2_out2, demultiplexer_2_out3,
       demultiplexer_2_out4, demultiplexer_2_out5, demultiplexer_2_out6, demultiplexer_2_out7,
       demultiplexer_3_out0, demultiplexer_3_out1, demultiplexer_3_out2, demultiplexer_3_out3,
       demultiplexer_3_out4, demultiplexer_3_out5, demultiplexer_3_out6, demultiplexer_3_out7,
       demultiplexer_4_out0, demultiplexer_4_out1, demultiplexer_4_out2, demultiplexer_4_out3,
       demultiplexer_4_out4, demultiplexer_4_out5, demultiplexer_4_out6, demultiplexer_4_out7,
       demultiplexer_5_out0, demultiplexer_5_out1, demultiplexer_5_out2, demultiplexer_5_out3,
       demultiplexer_5_out4, demultiplexer_5_out5, demultiplexer_5_out6, demultiplexer_5_out7;

  Demultiplexer #(.enable("true"), .select(2)) demultiplexer_1 (
    .out0(demultiplexer_1_out0), .out1(demultiplexer_1_out1), .out2(demultiplexer_1_out2),
    .out3(demultiplexer_1_out3), .in(1'b1), .sel(Rw[4:3]), .en(WE));
  Demultiplexer #(.enable("true"), .select(3)) demultiplexer_2 (
    .out0(demultiplexer_2_out0), .out1(demultiplexer_2_out1), .out2(demultiplexer_2_out2),
    .out3(demultiplexer_2_out3), .out4(demultiplexer_2_out4), .out5(demultiplexer_2_out5),
    .out6(demultiplexer_2_out6), .out7(demultiplexer_2_out7), .in(1'b1), .sel(Rw[2:0]),
    .en(demultiplexer_1_out0));
  Demultiplexer #(.enable("true"), .select(3)) demultiplexer_3 (
    .out0(demultiplexer_3_out0), .out1(demultiplexer_3_out1), .out2(demultiplexer_3_out2),
    .out3(demultiplexer_3_out3), .out4(demultiplexer_3_out4), .out5(demultiplexer_3_out5),
    .out6(demultiplexer_3_out6), .out7(demultiplexer_3_out7), .in(1'b1), .sel(Rw[2:0]),
    .en(demultiplexer_1_out1));
  Demultiplexer #(.enable("true"), .select(3)) demultiplexer_4 (
    .out0(demultiplexer_4_out0), .out1(demultiplexer_4_out1), .out2(demultiplexer_4_out2),
    .out3(demultiplexer_4_out3), .out4(demultiplexer_4_out4), .out5(demultiplexer_4_out5),
    .out6(demultiplexer_4_out6), .out7(demultiplexer_4_out7), .in(1'b1), .sel(Rw[2:0]),
    .en(demultiplexer_1_out2));
  Demultiplexer #(.enable("true"), .select(3)) demultiplexer_5 (
    .out0(demultiplexer_5_out0), .out1(demultiplexer_5_out1), .out2(demultiplexer_5_out2),
    .out3(demultiplexer_5_out3), .out4(demultiplexer_5_out4), .out5(demultiplexer_5_out5),
    .out6(demultiplexer_5_out6), .out7(demultiplexer_5_out7), .in(1'b1), .sel(Rw[2:0]),
    .en(demultiplexer_1_out3));
  Register #(.width(32)) zero_0 (.D(inDado), .en(demultiplexer_2_out0), .Q(SR0));  // open: clk, clr
  Register #(.width(32)) t0_8 (.D(inDado), .en(demultiplexer_3_out0), .clk(clk), .Q(SR8), .clr(rst));
  Register #(.width(32)) s0_16 (.D(inDado), .en(demultiplexer_4_out0), .clk(clk), .Q(SR16), .clr(rst));
  Register #(.width(32)) t8_24 (.D(inDado), .en(demultiplexer_5_out0), .clk(clk), .Q(SR24), .clr(rst));
  Register #(.width(32)) at_1 (.D(inDado), .en(demultiplexer_2_out1), .clk(clk), .Q(SR1), .clr(rst));
  Register #(.width(32)) t1_9 (.D(inDado), .en(demultiplexer_3_out1), .clk(clk), .Q(SR9), .clr(rst));
  Register #(.width(32)) s1_17 (.D(inDado), .en(demultiplexer_4_out1), .clk(clk), .Q(SR17), .clr(rst));
  Register #(.width(32)) t9_25 (.D(inDado), .en(demultiplexer_5_out1), .clk(clk), .Q(SR25), .clr(rst));
  Register #(.width(32)) v0_2 (.D(inDado), .en(demultiplexer_2_out2), .clk(clk), .Q(SR2), .clr(rst));
  Register #(.width(32)) t2_10 (.D(inDado), .en(demultiplexer_3_out2), .clk(clk), .Q(SR10), .clr(rst));
  Register #(.width(32)) s2_18 (.D(inDado), .en(demultiplexer_4_out2), .clk(clk), .Q(SR18), .clr(rst));
  Register #(.width(32)) k0_26 (.D(inDado), .en(demultiplexer_5_out2), .clk(clk), .Q(SR26), .clr(rst));
  Register #(.width(32)) v1_3 (.D(inDado), .en(demultiplexer_2_out3), .clk(clk), .Q(SR3), .clr(rst));
  Register #(.width(32)) t3_11 (.D(inDado), .en(demultiplexer_3_out3), .clk(clk), .Q(SR11), .clr(rst));
  Register #(.width(32)) s3_19 (.D(inDado), .en(demultiplexer_4_out3), .clk(clk), .Q(SR19), .clr(rst));
  Register #(.width(32)) k1_27 (.D(inDado), .en(demultiplexer_5_out3), .clk(clk), .Q(SR27), .clr(rst));
  Register #(.width(32)) a0_4 (.D(inDado), .en(demultiplexer_2_out4), .clk(clk), .Q(a0out), .clr(rst));
  Register #(.width(32)) t4_12 (.D(inDado), .en(demultiplexer_3_out4), .clk(clk), .Q(SR12), .clr(rst));
  Register #(.width(32)) s4_20 (.D(inDado), .en(demultiplexer_4_out4), .clk(clk), .Q(SR20), .clr(rst));
  Register #(.width(32)) gp_28 (.D(inDado), .en(demultiplexer_5_out4), .clk(clk), .Q(SR28), .clr(rst));
  Register #(.width(32)) a1_5 (.D(inDado), .en(demultiplexer_2_out5), .clk(clk), .Q(SR5), .clr(rst));
  Register #(.width(32)) t5_15 (.D(inDado), .en(demultiplexer_3_out5), .clk(clk), .Q(SR13), .clr(rst));
  Register #(.width(32)) s5_21 (.D(inDado), .en(demultiplexer_4_out5), .clk(clk), .Q(SR21), .clr(rst));
  Register #(.width(32)) sp_29 (.D(inDado), .en(demultiplexer_5_out5), .clk(clk), .Q(SR29), .clr(rst));
  Register #(.width(32)) a2_6 (.D(inDado), .en(demultiplexer_2_out6), .clk(clk), .Q(SR6), .clr(rst));
  Register #(.width(32)) t6_14 (.D(inDado), .en(demultiplexer_3_out6), .clk(clk), .Q(SR14), .clr(rst));
  Register #(.width(32)) s6_22 (.D(inDado), .en(demultiplexer_4_out6), .clk(clk), .Q(SR22), .clr(rst));
  Register #(.width(32)) fp_30 (.D(inDado), .en(demultiplexer_5_out6), .clk(clk), .Q(SR30), .clr(rst));
  Register #(.width(32)) a3_7 (.D(inDado), .en(demultiplexer_2_out7), .clk(clk), .Q(SR7), .clr(rst));
  Register #(.width(32)) t7_15 (.D(inDado), .en(demultiplexer_3_out7), .clk(clk), .Q(SR15), .clr(rst));
  Register #(.width(32)) s7_23 (.D(inDado), .en(demultiplexer_4_out7), .clk(clk), .Q(SR23), .clr(rst));
  Register #(.width(32)) ra_31 (.D(inDado), .en(demultiplexer_5_out7), .clk(clk), .Q(SR31), .clr(rst));
  Multiplexer #(.disabled("Z"), .select(5), .width(32)) multiplexer_1 (
    .in0(SR0), .in1(SR1), .in2(SR2), .in3(SR3), .in4(a0out), .in5(SR5), .in6(SR6), .in7(SR7), .in8(SR8),
    .in9(SR9), .in10(SR10), .in11(SR11), .in12(SR12), .in13(SR13), .in14(SR14), .in15(SR15), .in16(SR16),
    .in17(SR17), .in18(SR18), .in19(SR19), .in20(SR20), .in21(SR21), .in22(SR22), .in23(SR23), .in24(SR24),
    .in25(SR25), .in26(SR26), .in27(SR27), .in28(SR28), .in29(SR29), .in30(SR30), .in31(SR31), .out(R1out),
    .sel(R1in));
  Multiplexer #(.disabled("Z"), .select(5), .width(32)) multiplexer_2 (
    .in0(SR0), .in1(SR1), .in2(SR2), .in3(SR3), .in4(a0out), .in5(SR5), .in6(SR6), .in7(SR7), .in8(SR8),
    .in9(SR9), .in10(SR10), .in11(SR11), .in12(SR12), .in13(SR13), .in14(SR14), .in15(SR15), .in16(SR16),
    .in17(SR17), .in18(SR18), .in19(SR19), .in20(SR20), .in21(SR21), .in22(SR22), .in23(SR23), .in24(SR24),
    .in25(SR25), .in26(SR26), .in27(SR27), .in28(SR28), .in29(SR29), .in30(SR30), .in31(SR31), .out(R2out),
    .sel(R2in));

  assign SR4 = a0out;
  assign v0out = SR2;

  // Other names for the same wires on the sheet: T0[31:0] = SR0; T1[31:0] = SR1; T3[31:0] = SR3; T5[31:0] = SR5;
  //   T6[31:0] = SR6; T7[31:0] = SR7; T8[31:0] = SR8; T9[31:0] = SR9; T10[31:0] = SR10; T11[31:0] = SR11;
  //   T12[31:0] = SR12; T13[31:0] = SR13; T14[31:0] = SR14; T15[31:0] = SR15; T16[31:0] = SR16; T17[31:0] = SR17;
  //   T18[31:0] = SR18; T19[31:0] = SR19; T20[31:0] = SR20; T21[31:0] = SR21; T22[31:0] = SR22; T23[31:0] = SR23;
  //   T24[31:0] = SR24; T25[31:0] = SR25; T26[31:0] = SR26; T27[31:0] = SR27; T28[31:0] = SR28; T29[31:0] = SR29;
  //   T30[31:0] = SR30; T4[31:0] = a0out; Ta0[31:0] = a0out; Tclk = clk; TinDado[31:0] = inDado; TR1[4:0] = R1in;
  //   TR2[4:0] = R2in; T31[31:0] = SR31; Tra[31:0] = SR31; Treg1[31:0] = R1out; Treg2[31:0] = R2out; Trst = rst;
  //   TRw[4:0] = Rw; T2[31:0] = SR2; Tv0[31:0] = SR2; TWE = WE

  // Notes on the sheet:
  //   aaaaaaaaaaaaaaaaaaa
endmodule

module JTB (
  input  update,
  input  clear,
  input  clk,
  input  [31:0] pcIn,
  input  [31:0] instruction,
  input  [31:0] newpc,
  input  [31:0] targuet,
  output [31:0] instructionOut,
  output hit,
  output needUpdate
);

  wire and_1_out, and_3_out, comparator_1_eq, comparator_2_eq, d_ff_1_q, demultiplexer_1_out0,
       demultiplexer_1_out1, demultiplexer_1_out2, demultiplexer_1_out3, demultiplexer_1_out4,
       demultiplexer_1_out5, demultiplexer_1_out6, demultiplexer_1_out7, demultiplexer_2_out0,
       demultiplexer_2_out1, demultiplexer_2_out2, demultiplexer_2_out3, demultiplexer_2_out4,
       demultiplexer_2_out5, demultiplexer_2_out6, demultiplexer_2_out7, not_1_out, not_2_out, not_3_out,
       not_4_out, not_5_out, not_6_out, not_7_out;
  wire [31:0] multiplexer_1_out, register_1_q, register_2_q, register_3_q, register_4_q, register_5_q,
       register_6_q, register_7_q, register_8_q, register_9_q, register_10_q, register_11_q, register_12_q,
       register_13_q, register_14_q, register_15_q, register_16_q;

  Register #(.width(32)) register_1 (.D(newpc), .en(demultiplexer_1_out0), .clk(clk), .Q(register_1_q), .clr(clear));
  Register #(.width(32)) register_2 (.D(targuet), .en(demultiplexer_2_out0), .clk(clk), .Q(register_2_q), .clr(clear));
  Register #(.width(32)) register_3 (.D(newpc), .en(demultiplexer_1_out1), .clk(clk), .Q(register_3_q), .clr(clear));
  Register #(.width(32)) register_4 (.D(targuet), .en(demultiplexer_2_out1), .clk(clk), .Q(register_4_q), .clr(clear));
  Register #(.width(32)) register_5 (.D(newpc), .en(demultiplexer_1_out2), .clk(clk), .Q(register_5_q), .clr(clear));
  Register #(.width(32)) register_6 (.D(targuet), .en(demultiplexer_2_out2), .clk(clk), .Q(register_6_q), .clr(clear));
  not not_1 (not_1_out, instruction[26]);
  not not_2 (not_2_out, instruction[28]);
  and and_1 (and_1_out, not_1_out, instruction[27], not_2_out, not_3_out, not_4_out, not_5_out);
  not not_3 (not_3_out, instruction[29]);
  not not_4 (not_4_out, instruction[30]);
  not not_5 (not_5_out, instruction[31]);
  Register #(.width(32)) register_7 (.D(newpc), .en(demultiplexer_1_out3), .clk(clk), .Q(register_7_q), .clr(clear));
  Multiplexer #(.select(3), .width(32)) multiplexer_1 (
    .in0(register_1_q), .in1(register_3_q), .in2(register_5_q), .in3(register_7_q), .in4(register_9_q),
    .in5(register_11_q), .in6(register_13_q), .in7(register_15_q), .out(multiplexer_1_out), .sel(pcIn[4:2]));
  Register #(.width(32)) register_8 (.D(targuet), .en(demultiplexer_2_out3), .clk(clk), .Q(register_8_q), .clr(clear));
  Multiplexer #(.select(3), .width(32)) multiplexer_2 (
    .in0(register_2_q), .in1(register_4_q), .in2(register_6_q), .in3(register_8_q), .in4(register_10_q),
    .in5(register_12_q), .in6(register_14_q), .in7(register_16_q), .out(instructionOut), .sel(pcIn[4:2]));
  Register #(.width(32)) register_9 (.D(newpc), .en(demultiplexer_1_out4), .clk(clk), .Q(register_9_q), .clr(clear));
  Comparator #(.width(32)) comparator_1 (.a({32{1'b0}}), .b(multiplexer_1_out), .eq(comparator_1_eq));  // open: gt, lt
  Comparator #(.width(32)) comparator_2 (.a(multiplexer_1_out), .b(pcIn), .eq(comparator_2_eq));  // open: gt, lt
  Register #(.width(32)) register_10 (
    .D(targuet), .en(demultiplexer_2_out4), .clk(clk), .Q(register_10_q), .clr(clear));
  Register #(.width(32)) register_11 (.D(newpc), .en(demultiplexer_1_out5), .clk(clk), .Q(register_11_q), .clr(clear));
  not not_6 (not_6_out, comparator_1_eq);
  Register #(.width(32)) register_12 (
    .D(targuet), .en(demultiplexer_2_out5), .clk(clk), .Q(register_12_q), .clr(clear));
  and and_2 (hit, not_6_out, comparator_2_eq);
  Register #(.width(32)) register_13 (.D(newpc), .en(demultiplexer_1_out6), .clk(clk), .Q(register_13_q), .clr(clear));
  Register #(.width(32)) register_14 (
    .D(targuet), .en(demultiplexer_2_out6), .clk(clk), .Q(register_14_q), .clr(clear));
  Register #(.width(32)) register_15 (.D(newpc), .en(demultiplexer_1_out7), .clk(clk), .Q(register_15_q), .clr(clear));
  Register #(.width(32)) register_16 (
    .D(targuet), .en(demultiplexer_2_out7), .clk(clk), .Q(register_16_q), .clr(clear));
  Demultiplexer #(.enable("true"), .select(3)) demultiplexer_1 (
    .out0(demultiplexer_1_out0), .out1(demultiplexer_1_out1), .out2(demultiplexer_1_out2),
    .out3(demultiplexer_1_out3), .out4(demultiplexer_1_out4), .out5(demultiplexer_1_out5),
    .out6(demultiplexer_1_out6), .out7(demultiplexer_1_out7), .in(1'b1), .sel(newpc[4:2]), .en(update));
  Demultiplexer #(.enable("true"), .select(3)) demultiplexer_2 (
    .out0(demultiplexer_2_out0), .out1(demultiplexer_2_out1), .out2(demultiplexer_2_out2),
    .out3(demultiplexer_2_out3), .out4(demultiplexer_2_out4), .out5(demultiplexer_2_out5),
    .out6(demultiplexer_2_out6), .out7(demultiplexer_2_out7), .in(1'b1), .sel(newpc[4:2]), .en(update));
  // Probe on instructionOut
  not not_7 (not_7_out, hit);
  and and_3 (and_3_out, not_7_out, and_1_out);
  D_Flip_Flop d_ff_1 (.D(and_3_out), .clk(clk), .Q(d_ff_1_q));  // open: Qn, preset, reset
  and and_4 (needUpdate, and_3_out, ~d_ff_1_q);  // AND_Gate
endmodule
