// Logisim project pipeline_forwarding_4.circ as structural Verilog: 1 circuit, main circuit main
module main (
  input  ClearPC,
  input  in_2,
  input  in_3
);

  wire disablePC, not_1_out, not_2_out, not_3_out, palu_1_isequal, TALUSrc, TALUSrcEX, TBneOrBeq,
       TBneOrBeqEX, TBranch, TBranch_3, TBranchEX, Tclk, TFlushIdHazard, TFlushIF, TisJAL, TisJAL_MEM,
       TisJAL_WB, TisJALEX, TisJR, TisJREX, TisJump, TisJumpEX, TisShamt, TisShamtEX, TIsToBranchOrJump,
       TMemRead, TMemReadEX, TMemReadMEM, TMemToReg, TMemToRegEX, TMemToRegMEM, TMemToRegWB, TMemWrite,
       TMemWriteEx, TMemWriteMEM, TReadRsHazard, TReadRtHazard, TRegDst, TRegWrite, TRegWriteEX,
       TRegWriteMEM, TStallID, TWriteEnable, TZeroExtd, xor_1_out;
  wire [1:0] TRsOutput, TRtOutput;
  wire [3:0] TALUOp, TALUOp_ID;
  wire [4:0] multiplexer_4_out, Trd, Trs, Trt, Tshamt, TWriteReg_5, TWriteReg_ID, TWriteRegEX, TWriteRegMEM;
  wire [5:0] instructiondecoder_1_funct, instructiondecoder_1_op;
  wire [15:0] Timmediate;
  wire [25:0] TAddress;
  wire [31:0] bit_extender_1_out, contador_1_numerodeciclos, multiplexer_1_out, multiplexer_2_out,
       multiplexer_3_out, multiplexer_8_out, multiplexer_9_out, multiplexer_10_out, multiplexer_12_out,
       PCPLUS4_1, regfiledisplay_1_sr0, regfiledisplay_1_sr1, regfiledisplay_1_sr2, regfiledisplay_1_sr3,
       regfiledisplay_1_sr4, regfiledisplay_1_sr5, regfiledisplay_1_sr6, regfiledisplay_1_sr7,
       regfiledisplay_1_sr8, regfiledisplay_1_sr9, regfiledisplay_1_sr10, regfiledisplay_1_sr11,
       regfiledisplay_1_sr12, regfiledisplay_1_sr13, regfiledisplay_1_sr14, regfiledisplay_1_sr15,
       regfiledisplay_1_sr16, regfiledisplay_1_sr17, regfiledisplay_1_sr18, regfiledisplay_1_sr19,
       regfiledisplay_1_sr20, regfiledisplay_1_sr21, regfiledisplay_1_sr22, regfiledisplay_1_sr23,
       regfiledisplay_1_sr24, regfiledisplay_1_sr25, regfiledisplay_1_sr26, regfiledisplay_1_sr27,
       regfiledisplay_1_sr28, regfiledisplay_1_sr29, regfiledisplay_1_sr30, regfiledisplay_1_sr31,
       register_1_q, shifter_1_out, T_WB_DATA_5, TALUResultEX, TALUResultMEM, TALUResultWB, TDataFromMEM,
       TImmediate_ID, TImmEX, Tinstruction, TinstructionIF, TJumpAddr_3, TJumpAddr_ID, TJumpAddrEX,
       TJumpAddrMEM, TJumpADDRWB, TOutputFromMEM, TPCPlus4EX, Tpcplus4IF, TR1_ID, TR1EX, TR1FromReg, TR2_ID,
       TR2FromReg, TReadDataWB, TShamtEX, TWriteDataEx, TWriteDataMEM;

  Multiplexer #(.disabled("Z"), .width(32)) multiplexer_1 (
    .in0(PCPLUS4_1), .in1(TJumpAddr_3), .out(multiplexer_1_out), .sel(TBranch_3));
  Multiplexer #(.disabled("Z"), .width(32)) multiplexer_2 (
    .in0(multiplexer_1_out), .in1(TJumpAddrEX), .out(multiplexer_2_out), .sel(TisJumpEX));
  Multiplexer #(.disabled("Z"), .width(32)) multiplexer_3 (
    .in0(multiplexer_2_out), .in1(TR1EX), .out(multiplexer_3_out), .sel(TisJREX));
  not not_1 (not_1_out, disablePC);
  Register #(.width(32)) register_1 (
    .D(multiplexer_3_out), .en(not_1_out), .clk(Tclk), .Q(register_1_q), .clr(ClearPC));
  Clock clock_1 (.out(Tclk));
  Contador contador_1 (.clkSignal(Tclk), .reset(in_2), .NumeroDeCiclos(contador_1_numerodeciclos));
  // Probe on contador_1_numerodeciclos
  Adder #(.width(32)) adder_1 (.a(register_1_q), .b(32'h4), .out(PCPLUS4_1));  // open: cin, cout
  ROM #(.addrWidth(10), .dataWidth(32)) rom_1 (.addr(register_1_q[11:2]), .data(Tinstruction));
  IF_ID if_id_1 (
    .clk_if_id(Tclk), .Instruction_IF(Tinstruction), .PCPlus4_IF(PCPLUS4_1), .Enable_if_id(not_2_out),
    .clr_if_id(TFlushIF), .Instruction_ID(TinstructionIF), .PCPus4_ID(Tpcplus4IF));
  not not_2 (not_2_out, TStallID);
  InstructionDecoder instructiondecoder_1 (
    .Instruction(TinstructionIF), .op(instructiondecoder_1_op), .rs(Trs), .rt(Trt), .rd(Trd), .shamt(Tshamt),
    .funct(instructiondecoder_1_funct), .immediate(Timmediate), .adderess(TAddress));
  ComplementadorSinal complementadorsinal_1 (
    .ZeroExtend(TZeroExtd), .address16(Timmediate), .address32ext(TImmediate_ID));
  JumpAddess jumpaddess_1 (.Address(TAddress), .PC4(Tpcplus4IF), .JumpAddress(TJumpAddr_ID));
  ControlUnit controlunit_1 (
    .op(instructiondecoder_1_op), .funct(instructiondecoder_1_funct), .isShamt(TisShamt), .MemRead(TMemRead),
    .MemToReg(TMemToReg), .MemWrite(TMemWrite), .RegWrite(TRegWrite), .Jump(TisJump), .BneOrBeq(TBneOrBeq),
    .Branch(TBranch), .ALUSrc(TALUSrc), .RegDst(TRegDst), .ZeroExtend(TZeroExtd), .isJR(TisJR),
    .ALUop(TALUOp_ID), .ReadRs(TReadRsHazard), .isJAL(TisJAL), .ReadRt(TReadRtHazard));
  not not_3 (not_3_out, Tclk);
  // Probe on regfiledisplay_1_sr0
  // Probe on regfiledisplay_1_sr1
  // Probe on regfiledisplay_1_sr2
  // Probe on regfiledisplay_1_sr3
  // Probe on regfiledisplay_1_sr4
  // Probe on regfiledisplay_1_sr5
  // Probe on regfiledisplay_1_sr6
  // Probe on regfiledisplay_1_sr7
  // Probe on regfiledisplay_1_sr8
  // Probe on regfiledisplay_1_sr9
  // Probe on regfiledisplay_1_sr10
  // Probe on regfiledisplay_1_sr11
  // Probe on regfiledisplay_1_sr12
  // Probe on regfiledisplay_1_sr13
  // Probe on regfiledisplay_1_sr14
  // Probe on regfiledisplay_1_sr15
  Multiplexer #(.disabled("Z"), .width(5)) multiplexer_4 (.in0(Trt), .in1(Trd), .out(multiplexer_4_out), .sel(TRegDst));
  // Probe on regfiledisplay_1_sr16
  // Probe on regfiledisplay_1_sr17
  // Probe on regfiledisplay_1_sr18
  // Probe on regfiledisplay_1_sr19
  // Probe on regfiledisplay_1_sr20
  // Probe on regfiledisplay_1_sr21
  // Probe on regfiledisplay_1_sr22
  // Probe on regfiledisplay_1_sr23
  // Probe on regfiledisplay_1_sr24
  // Probe on regfiledisplay_1_sr25
  // Probe on regfiledisplay_1_sr26
  // Probe on regfiledisplay_1_sr27
  // Probe on regfiledisplay_1_sr28
  // Probe on regfiledisplay_1_sr29
  // Probe on regfiledisplay_1_sr30
  // Probe on regfiledisplay_1_sr31
  Multiplexer #(.disabled("Z"), .width(5)) multiplexer_5 (
    .in0(multiplexer_4_out), .in1({5{1'b1}}), .out(TWriteReg_ID), .sel(TisJAL));
  regFileDisplay regfiledisplay_1 (
    .Rw(TWriteReg_5), .inDado(T_WB_DATA_5), .WE(TWriteEnable), .clk(not_3_out), .rst(in_3), .R1in(Trs),
    .R2in(Trt), .SR15(regfiledisplay_1_sr15), .SR8(regfiledisplay_1_sr8), .SR9(regfiledisplay_1_sr9),
    .SR10(regfiledisplay_1_sr10), .SR11(regfiledisplay_1_sr11), .SR12(regfiledisplay_1_sr12),
    .SR13(regfiledisplay_1_sr13), .SR14(regfiledisplay_1_sr14), .R1out(TR1FromReg),
    .SR23(regfiledisplay_1_sr23), .R2out(TR2FromReg), .SR16(regfiledisplay_1_sr16),
    .SR17(regfiledisplay_1_sr17), .SR18(regfiledisplay_1_sr18), .SR19(regfiledisplay_1_sr19),
    .SR20(regfiledisplay_1_sr20), .SR21(regfiledisplay_1_sr21), .SR22(regfiledisplay_1_sr22),
    .SR31(regfiledisplay_1_sr31), .SR24(regfiledisplay_1_sr24), .SR25(regfiledisplay_1_sr25),
    .SR26(regfiledisplay_1_sr26), .SR27(regfiledisplay_1_sr27), .SR28(regfiledisplay_1_sr28),
    .SR29(regfiledisplay_1_sr29), .SR30(regfiledisplay_1_sr30), .SR7(regfiledisplay_1_sr7),
    .SR0(regfiledisplay_1_sr0), .SR1(regfiledisplay_1_sr1), .SR2(regfiledisplay_1_sr2),
    .SR3(regfiledisplay_1_sr3), .SR4(regfiledisplay_1_sr4), .SR5(regfiledisplay_1_sr5),
    .SR6(regfiledisplay_1_sr6));  // open: a0out, v0out
  HazardForwardingUnit hazardforwardingunit_1 (
    .IsToBranchOrJump(TIsToBranchOrJump), .clk(Tclk), .ReadRs(TReadRsHazard), .ReadRt(TReadRtHazard),
    .isRegWriteEX(TRegWriteEX), .isRegWriteMEM(TRegWriteMEM), .RS(Trs), .RT(Trt), .IsLW(TMemReadEX),
    .WriteRegEX(TWriteRegEX), .WriteRegMEM(TWriteRegMEM), .FlushIF(TFlushIF), .RsOutput(TRsOutput),
    .FlushID(TFlushIdHazard), .StallIF(disablePC), .StallID(TStallID), .RtOutput(TRtOutput));
  assign bit_extender_1_out = {{27{1'b0}}, Tshamt};  // Bit_Extender bit_extender_1
  Multiplexer #(.disabled("Z"), .select(2), .width(32)) multiplexer_6 (
    .in0(TR1FromReg), .in1(TALUResultEX), .in2(TDataFromMEM), .out(TR1_ID), .sel(TRsOutput));  // open: in3
  Multiplexer #(.disabled("Z"), .select(2), .width(32)) multiplexer_7 (
    .in0(TR2FromReg), .in1(TALUResultEX), .in2(TDataFromMEM), .out(TR2_ID), .sel(TRtOutput));  // open: in3
  ID_EX id_ex_1 (
    .isSham_ID(TisShamt), .MemToReg_ID(TMemToReg), .RegWrite_ID(TRegWrite), .BneOrBeq_ID(TBneOrBeq),
    .clr_ID_EX(TFlushIdHazard), .ALUSrc_ID(TALUSrc), .MemRead_ID(TMemRead), .MemWrite_ID(TMemWrite),
    .isJump_ID(TisJump), .Branch_ID(TBranch), .is_JR_ID(TisJR), .ALUOp_ID(TALUOp_ID),
    .WriteReg_ID(TWriteReg_ID), .isJAL_ID(TisJAL), .Imm_ID(TImmediate_ID), .R1_ID(TR1_ID), .R2_ID(TR2_ID),
    .enable_id_ex(1'b1), .Sham_ID(bit_extender_1_out), .JumpAddr_ID(TJumpAddr_ID), .PCPlus4_ID(Tpcplus4IF),
    .clk_ID_EX(Tclk), .isSham_EX(TisShamtEX), .MemToReg_EX(TMemToRegEX), .RegWrite_EX(TRegWriteEX),
    .BneOrBeq_EX(TBneOrBeqEX), .ALUSrc_EX(TALUSrcEX), .MemRead_EX(TMemReadEX), .MemWrite_EX(TMemWriteEx),
    .isJump_EX(TisJumpEX), .Branch_EX(TBranchEX), .isJR_EX(TisJREX), .ALUOp_EX(TALUOp),
    .WriteReg_EX(TWriteRegEX), .isJAL_EX(TisJALEX), .Imm_EX(TImmEX), .R1_EX(TR1EX), .R2_EX(TWriteDataEx),
    .Sham_EX(TShamtEX), .JumpAddr_EX(TJumpAddrEX), .PCPus4_EX(TPCPlus4EX));
  Multiplexer #(.disabled("Z"), .width(32)) multiplexer_8 (
    .in0(TR1EX), .in1(TWriteDataEx), .out(multiplexer_8_out), .sel(TisShamtEX));
  Multiplexer #(.disabled("Z"), .width(32)) multiplexer_9 (
    .in0(TWriteDataEx), .in1(TShamtEX), .out(multiplexer_9_out), .sel(TisShamtEX));
  Shifter #(.width(32)) shifter_1 (.in(TImmEX), .\dist (5'b00010), .out(shifter_1_out));
  Multiplexer #(.disabled("Z"), .width(32)) multiplexer_10 (
    .in0(multiplexer_9_out), .in1(TImmEX), .out(multiplexer_10_out), .sel(TALUSrcEX));
  Adder #(.width(32)) adder_2 (.a(TPCPlus4EX), .b(shifter_1_out), .out(TJumpAddr_3));  // open: cin, cout
  or or_1 (TIsToBranchOrJump, TisJALEX, TisJREX, TBranch_3, TisJumpEX);
  pALU palu_1 (
    .X(multiplexer_8_out), .Y(multiplexer_10_out), .ALUOp(TALUOp), .Result1(TALUResultEX),
    .isEqual(palu_1_isequal));  // open: SignedOverflow, UnsignedOverflow, Result2
  xor xor_1 (xor_1_out, palu_1_isequal, TBneOrBeqEX);
  and and_1 (TBranch_3, xor_1_out, TBranchEX);
  EX_MEM ex_mem_1 (
    .clk_EX_MEM(Tclk), .clr_EX_MEM(1'b0), .MemToReg_Ex(TMemToRegEX), .RegWrite_Ex(TRegWriteEX),
    .MemRead_Ex(TMemReadEX), .MemWrite_EX(TMemWriteEx), .WriteReg_EX(TWriteRegEX), .Enable_EX_MEM(1'b1),
    .ALU_Result_EX(TALUResultEX), .WriteData_EX(TWriteDataEx), .JumpAddr_EX(TPCPlus4EX), .isJAL_EX(TisJALEX),
    .ALUResult_MEM(TALUResultMEM), .WriteData_MEM(TWriteDataMEM), .JumpAddr_MEM(TJumpAddrMEM),
    .isJAL_MEM(TisJAL_MEM), .MemToReg_MEM(TMemToRegMEM), .RegWrite_MEM(TRegWriteMEM),
    .MemRead_MEM(TMemReadMEM), .MemWrite_MEM(TMemWriteMEM), .WriteReg_MEM(TWriteRegMEM));
  Multiplexer #(.width(32)) multiplexer_11 (
    .in0(TALUResultMEM), .in1(TOutputFromMEM), .out(TDataFromMEM), .sel(TMemToRegMEM));
  RAM #(.addrWidth(10), .dataWidth(32), .trigger("falling")) ram_1 (
    .addr(TALUResultMEM[11:2]), .we(TMemWriteMEM), .oe(TMemReadMEM), .clk(Tclk), .din(TWriteDataMEM),
    .dout(TOutputFromMEM));
  MEM_WB mem_wb_1 (
    .clk_mem_wb(Tclk), .memToReg_mem(TMemToRegMEM), .regWrite_mem(TRegWriteMEM), .writeReg_mem(TWriteRegMEM),
    .isJALMEM(TisJAL_MEM), .enable_mem_wb(1'b1), .clr_mem_wb(1'b0), .ALUResult_mem(TALUResultMEM),
    .ReadData_mem(TJumpAddrMEM), .JumpAddr_MEM(TOutputFromMEM), .ALUResult_wb(TALUResultWB),
    .ReadData_wb(TReadDataWB), .JumpAddr_wb(TJumpADDRWB), .memToReg_wb(TMemToRegWB),
    .regWrite_wb(TWriteEnable), .writeReg_wb(TWriteReg_5), .isJALWB(TisJAL_WB));
  Multiplexer #(.width(32)) multiplexer_12 (
    .in0(TALUResultWB), .in1(TJumpADDRWB), .out(multiplexer_12_out), .sel(TMemToRegWB));
  Multiplexer #(.width(32)) multiplexer_13 (
    .in0(multiplexer_12_out), .in1(TReadDataWB), .out(T_WB_DATA_5), .sel(TisJAL_WB));

  // Notes on the sheet:
  //   aaaaaaaaaaaaaaaaaaaaaaaaaaaaaaaaa
endmodule
