// Logisim project monociclo.circ as structural Verilog: 1 circuit, main circuit main
module main (
  input  in_1,
  input  ClearPC,
  input  in_3
);

  wire and_1_out, TALUSrc, TBne, TBranch, Tclk, TisEqual, TisJAL, TisJR, TisJump, TisShamt, TMemRead,
       TMemToReg, TMemWrite, TRegDst, TRegWrite, TZeroExtd, xor_1_out;
  wire [3:0] TALUOp;
  wire [4:0] multiplexer_1_out, multiplexer_2_out, Trd, Trs, Trt, Tshamt;
  wire [5:0] instructiondecoder_1_funct, instructiondecoder_1_op;
  wire [15:0] Timmediate_t;
  wire [25:0] TAddress;
  wire [31:0] adder_2_out, adder_3_out, contador_1_numerodeciclos, multiplexer_3_out, multiplexer_4_out,
       multiplexer_5_out, multiplexer_6_out, multiplexer_7_out, multiplexer_8_out, multiplexer_9_out,
       palu_1_result1, PCPLUS4_1, ram_1_dout, regfiledisplay_1_r1out, regfiledisplay_1_r2out,
       regfiledisplay_1_sr0, regfiledisplay_1_sr1, regfiledisplay_1_sr2, regfiledisplay_1_sr3,
       regfiledisplay_1_sr4, regfiledisplay_1_sr5, regfiledisplay_1_sr6, regfiledisplay_1_sr7,
       regfiledisplay_1_sr8, regfiledisplay_1_sr9, regfiledisplay_1_sr10, regfiledisplay_1_sr11,
       regfiledisplay_1_sr12, regfiledisplay_1_sr13, regfiledisplay_1_sr14, regfiledisplay_1_sr15,
       regfiledisplay_1_sr16, regfiledisplay_1_sr17, regfiledisplay_1_sr18, regfiledisplay_1_sr19,
       regfiledisplay_1_sr20, regfiledisplay_1_sr21, regfiledisplay_1_sr22, regfiledisplay_1_sr23,
       regfiledisplay_1_sr24, regfiledisplay_1_sr25, regfiledisplay_1_sr26, regfiledisplay_1_sr27,
       regfiledisplay_1_sr28, regfiledisplay_1_sr29, regfiledisplay_1_sr30, regfiledisplay_1_sr31,
       register_1_q, rom_1_data, shifter_1_out, TImmediate, TImmEX, TJumpAddr, Tpcplus4, TshamtEXT;

  Register #(.width(32)) register_1 (.D(multiplexer_8_out), .en(1'b1), .clk(Tclk), .Q(register_1_q), .clr(ClearPC));
  Adder #(.width(32)) adder_1 (.a(register_1_q), .b(32'h4), .out(PCPLUS4_1));  // open: cin, cout
  ROM #(.addrWidth(10), .dataWidth(32)) rom_1 (.addr(register_1_q[11:2]), .data(rom_1_data));
  // Probe on contador_1_numerodeciclos
  Contador contador_1 (.clkSignal(Tclk), .reset(in_1), .NumeroDeCiclos(contador_1_numerodeciclos));
  assign TshamtEXT = {{27{1'b0}}, Tshamt};  // Bit_Extender bit_extender_1
  Clock clock_1 (.out(Tclk));
  InstructionDecoder instructiondecoder_1 (
    .Instruction(rom_1_data), .op(instructiondecoder_1_op), .rs(Trs), .rt(Trt), .rd(Trd), .shamt(Tshamt),
    .funct(instructiondecoder_1_funct), .immediate(Timmediate_t), .adderess(TAddress));
  ComplementadorSinal complementadorsinal_1 (
    .ZeroExtend(TZeroExtd), .address16(Timmediate_t), .address32ext(TImmediate));
  JumpAddess jumpaddess_1 (.Address(TAddress), .PC4(Tpcplus4), .JumpAddress(TJumpAddr));
  ControlUnit controlunit_1 (
    .op(instructiondecoder_1_op), .funct(instructiondecoder_1_funct), .isShamt(TisShamt), .MemRead(TMemRead),
    .MemToReg(TMemToReg), .MemWrite(TMemWrite), .RegWrite(TRegWrite), .Jump(TisJump), .BneOrBeq(TBne),
    .Branch(TBranch), .ALUSrc(TALUSrc), .RegDst(TRegDst), .ZeroExtend(TZeroExtd), .isJR(TisJR),
    .ALUop(TALUOp), .isJAL(TisJAL));  // open: ReadRs, ReadRt
  Multiplexer #(.width(5)) multiplexer_1 (.in0(Trt), .in1(Trd), .out(multiplexer_1_out), .sel(TRegDst));
  Multiplexer #(.width(5)) multiplexer_2 (
    .in0(multiplexer_1_out), .in1({5{1'b1}}), .out(multiplexer_2_out), .sel(TisJAL));
  // Probe on regfiledisplay_1_sr0
  // Probe on regfiledisplay_1_sr1
  // Probe on regfiledisplay_1_sr2
  // Probe on regfiledisplay_1_sr3
  // Probe on regfiledisplay_1_sr4
  // Probe on regfiledisplay_1_sr5
  // Probe on regfiledisplay_1_sr6
  // Probe on regfiledisplay_1_sr7
  // Probe on regfiledisplay_1_sr8
  // Probe on regfiledisplay_1_sr9
  // Probe on regfiledisplay_1_sr10
  // Probe on regfiledisplay_1_sr11
  // Probe on regfiledisplay_1_sr12
  // Probe on regfiledisplay_1_sr13
  // Probe on regfiledisplay_1_sr14
  // Probe on regfiledisplay_1_sr15
  // Probe on regfiledisplay_1_sr16
  // Probe on regfiledisplay_1_sr17
  // Probe on regfiledisplay_1_sr18
  // Probe on regfiledisplay_1_sr19
  // Probe on regfiledisplay_1_sr20
  // Probe on regfiledisplay_1_sr21
  // Probe on regfiledisplay_1_sr22
  // Probe on regfiledisplay_1_sr23
  // Probe on regfiledisplay_1_sr24
  // Probe on regfiledisplay_1_sr25
  // Probe on regfiledisplay_1_sr26
  // Probe on regfiledisplay_1_sr27
  // Probe on regfiledisplay_1_sr28
  // Probe on regfiledisplay_1_sr29
  // Probe on regfiledisplay_1_sr30
  // Probe on regfiledisplay_1_sr31
  regFileDisplay regfiledisplay_1 (
    .Rw(multiplexer_2_out), .inDado(multiplexer_9_out), .WE(TRegWrite), .clk(Tclk), .rst(in_3), .R1in(Trs),
    .R2in(Trt), .SR15(regfiledisplay_1_sr15), .SR8(regfiledisplay_1_sr8), .SR9(regfiledisplay_1_sr9),
    .SR10(regfiledisplay_1_sr10), .SR11(regfiledisplay_1_sr11), .SR12(regfiledisplay_1_sr12),
    .SR13(regfiledisplay_1_sr13), .SR14(regfiledisplay_1_sr14), .R1out(regfiledisplay_1_r1out),
    .SR23(regfiledisplay_1_sr23), .R2out(regfiledisplay_1_r2out), .SR16(regfiledisplay_1_sr16),
    .SR17(regfiledisplay_1_sr17), .SR18(regfiledisplay_1_sr18), .SR19(regfiledisplay_1_sr19),
    .SR20(regfiledisplay_1_sr20), .SR21(regfiledisplay_1_sr21), .SR22(regfiledisplay_1_sr22),
    .SR31(regfiledisplay_1_sr31), .SR24(regfiledisplay_1_sr24), .SR25(regfiledisplay_1_sr25),
    .SR26(regfiledisplay_1_sr26), .SR27(regfiledisplay_1_sr27), .SR28(regfiledisplay_1_sr28),
    .SR29(regfiledisplay_1_sr29), .SR30(regfiledisplay_1_sr30), .SR7(regfiledisplay_1_sr7),
    .SR0(regfiledisplay_1_sr0), .SR1(regfiledisplay_1_sr1), .SR2(regfiledisplay_1_sr2),
    .SR3(regfiledisplay_1_sr3), .SR4(regfiledisplay_1_sr4), .SR5(regfiledisplay_1_sr5),
    .SR6(regfiledisplay_1_sr6));  // open: a0out, v0out
  Multiplexer #(.width(32)) multiplexer_3 (
    .in0(regfiledisplay_1_r2out), .in1(TImmediate), .out(multiplexer_3_out), .sel(TALUSrc));
  Multiplexer #(.width(32)) multiplexer_4 (
    .in0(regfiledisplay_1_r1out), .in1(regfiledisplay_1_r2out), .out(multiplexer_4_out), .sel(TisShamt));
  Multiplexer #(.width(32)) multiplexer_5 (
    .in0(multiplexer_3_out), .in1(TshamtEXT), .out(multiplexer_5_out), .sel(TisShamt));
  Shifter #(.width(32)) shifter_1 (.in(TImmEX), .\dist (5'b00010), .out(shifter_1_out));
  Adder #(.width(32)) adder_2 (.a(register_1_q), .b(32'h4), .out(adder_2_out));  // open: cin, cout
  Adder #(.width(32)) adder_3 (.a(adder_2_out), .b(shifter_1_out), .out(adder_3_out));  // open: cin, cout
  xor xor_1 (xor_1_out, TisEqual, TBne);
  pALU palu_1 (
    .X(multiplexer_4_out), .Y(multiplexer_5_out), .ALUOp(TALUOp), .Result1(palu_1_result1), .isEqual(TisEqual));  // open: SignedOverflow, UnsignedOverflow, Result2
  and and_1 (and_1_out, TisJump, xor_1_out);
  Multiplexer #(.width(32)) multiplexer_6 (
    .in0(adder_2_out), .in1(adder_3_out), .out(multiplexer_6_out), .sel(and_1_out));
  Multiplexer #(.width(32)) multiplexer_7 (
    .in0(multiplexer_6_out), .in1(TJumpAddr), .out(multiplexer_7_out), .sel(TisJump));
  RAM #(.addrWidth(10), .dataWidth(32)) ram_1 (
    .addr(palu_1_result1[11:2]), .we(TMemWrite), .oe(TMemRead), .clk(Tclk), .din(regfiledisplay_1_r2out),
    .dout(ram_1_dout));
  Multiplexer #(.width(32)) multiplexer_8 (
    .in0(multiplexer_7_out), .in1(regfiledisplay_1_r1out), .out(multiplexer_8_out), .sel(TisJR));
  Multiplexer #(.width(32)) multiplexer_9 (
    .in0(palu_1_result1), .in1(ram_1_dout), .out(multiplexer_9_out), .sel(TMemToReg));
endmodule
